// Logisim project 6502.circ as structural Verilog: 18 circuits, main circuit 6502
module _6502 (
  input  nNMI,
  input  nIRQ,
  input  RDY,
  input  nRES,
  input  SO,
  output PHI1,
  output PHI2,
  output R_W,
  output SYNC
);

  wire d_ff_1_q, d_latch_1_not_q, d_latch_2_not_q, d_latch_3_q, DECODER__0, DECODER__1, DECODER__2,
       DECODER__3, DECODER__4, DECODER__5, DECODER__6, DECODER__7, DECODER__8, DECODER__9, DECODER__10,
       DECODER__11, DECODER__12, DECODER__13, DECODER__14, DECODER__15, DECODER__16, DECODER__17,
       DECODER__18, DECODER__19, DECODER__20, DECODER__21, DECODER__22, DECODER__23, DECODER__24,
       DECODER__25, DECODER__26, DECODER__27, DECODER__28, DECODER__29, DECODER__30, DECODER__31,
       DECODER__32, DECODER__33, DECODER__34, DECODER__35, DECODER__36, DECODER__37, DECODER__38,
       DECODER__39, DECODER__40, DECODER__41, DECODER__42, DECODER__43, DECODER__44, DECODER__45,
       DECODER__46, DECODER__47, DECODER__48, DECODER__49, DECODER__50, DECODER__51, DECODER__52,
       DECODER__53, DECODER__54, DECODER__55, DECODER__56, DECODER__57, DECODER__58, DECODER__59,
       DECODER__60, DECODER__61, DECODER__62, DECODER__63, DECODER__64, DECODER__65, DECODER__66,
       DECODER__67, DECODER__68, DECODER__69, DECODER__70, DECODER__71, DECODER__72, DECODER__73,
       DECODER__74, DECODER__75, DECODER__76, DECODER__77, DECODER__78, DECODER__79, DECODER__80,
       DECODER__81, DECODER__82, DECODER__83, DECODER__84, DECODER__85, DECODER__86, DECODER__87,
       DECODER__88, DECODER__89, DECODER__90, DECODER__91, DECODER__92, DECODER__93, DECODER__94,
       DECODER__95, DECODER__96, DECODER__97, DECODER__98, DECODER__99, DECODER__100, DECODER__101,
       DECODER__102, DECODER__103, DECODER__104, DECODER__105, DECODER__106, DECODER__107, DECODER__108,
       DECODER__109, DECODER__110, DECODER__111, DECODER__112, DECODER__113, DECODER__114, DECODER__115,
       DECODER__116, DECODER__117, DECODER__118, DECODER__119, DECODER__120, DECODER__121, DECODER__122,
       DECODER__123, DECODER__124, DECODER__125, DECODER__126, DECODER__127, DECODER__128, DECODER__129,
       IR_ir0, IR_ir1, IR_ir2, IR_ir3, IR_ir4, IR_ir5, IR_ir6, IR_ir7, nor_1_out, not_1_out, PHI0_out,
       PREDECODE_nimplied, PREDECODE_npd0, PREDECODE_npd1, PREDECODE_npd2, PREDECODE_npd3, PREDECODE_npd4,
       PREDECODE_npd5, PREDECODE_npd6, PREDECODE_npd7, PREDECODE_ntwocycle, RANDOM_LOGIC__0_ir,
       RANDOM_LOGIC_fetch, RANDOM_LOGIC_nt0, RANDOM_LOGIC_nt1x, RANDOM_LOGIC_nt2, RANDOM_LOGIC_nt3,
       RANDOM_LOGIC_nt4, RANDOM_LOGIC_nt5, RANDOM_LOGIC_t1, RANDOM_LOGIC_wr, undriven, undriven_2;

  buf buffer_1 (SYNC, RANDOM_LOGIC_t1);
  ABH abh_1 ();  // open: PHI1, ADH_ABH, FROM_ADH0, FROM_ADH1, FROM_ADH2, FROM_ADH3, FROM_ADH4, FROM_ADH5, FROM_ADH6, FROM_ADH7, A8, A9, A10, A11, A12, A13, A14, A15
  D_Flip_Flop #(.trigger("high")) d_ff_1 (.clk(PHI2), .D(nNMI), .Q(d_ff_1_q));  // open: Qn, preset, en, reset
  DECODER_TRANS DECODER (
    .nT5(RANDOM_LOGIC_nt5), .nT4(RANDOM_LOGIC_nt4), .nT3(RANDOM_LOGIC_nt3), .nT2(RANDOM_LOGIC_nt2),
    .IR0(IR_ir7), .IR1(IR_ir6), .IR7(IR_ir5), .IR4(IR_ir4), .IR3(IR_ir3), .IR2(IR_ir2), .IR6(IR_ir1),
    .IR5(IR_ir0), .nT0(RANDOM_LOGIC_nt0), .nT1X(RANDOM_LOGIC_nt1x), ._0(DECODER__0), ._1(DECODER__1),
    ._2(DECODER__2), ._3(DECODER__3), ._4(DECODER__4), ._5(DECODER__5), ._6(DECODER__6), ._7(DECODER__7),
    ._8(DECODER__8), ._9(DECODER__9), ._10(DECODER__10), ._11(DECODER__11), ._12(DECODER__12),
    ._13(DECODER__13), ._14(DECODER__14), ._15(DECODER__15), ._16(DECODER__16), ._17(DECODER__17),
    ._18(DECODER__18), ._19(DECODER__19), ._20(DECODER__20), ._21(DECODER__21), ._22(DECODER__22),
    ._23(DECODER__23), ._24(DECODER__24), ._25(DECODER__25), ._26(DECODER__26), ._27(DECODER__27),
    ._28(DECODER__28), ._29(DECODER__29), ._30(DECODER__30), ._31(DECODER__31), ._32(DECODER__32),
    ._33(DECODER__33), ._34(DECODER__34), ._35(DECODER__35), ._36(DECODER__36), ._37(DECODER__37),
    ._38(DECODER__38), ._39(DECODER__39), ._40(DECODER__40), ._41(DECODER__41), ._42(DECODER__42),
    ._43(DECODER__43), ._44(DECODER__44), ._45(DECODER__45), ._46(DECODER__46), ._47(DECODER__47),
    ._48(DECODER__48), ._49(DECODER__49), ._50(DECODER__50), ._51(DECODER__51), ._52(DECODER__52),
    ._53(DECODER__53), ._54(DECODER__54), ._55(DECODER__55), ._56(DECODER__56), ._57(DECODER__57),
    ._58(DECODER__58), ._59(DECODER__59), ._60(DECODER__60), ._61(DECODER__61), ._62(DECODER__62),
    ._63(DECODER__63), ._64(DECODER__64), ._65(DECODER__65), ._66(DECODER__66), ._67(DECODER__67),
    ._68(DECODER__68), ._69(DECODER__69), ._70(DECODER__70), ._71(DECODER__71), ._72(DECODER__72),
    ._73(DECODER__73), ._74(DECODER__74), ._75(DECODER__75), ._76(DECODER__76), ._77(DECODER__77),
    ._78(DECODER__78), ._79(DECODER__79), ._80(DECODER__80), ._81(DECODER__81), ._82(DECODER__82),
    ._83(DECODER__83), ._84(DECODER__84), ._85(DECODER__85), ._86(DECODER__86), ._87(DECODER__87),
    ._88(DECODER__88), ._89(DECODER__89), ._90(DECODER__90), ._91(DECODER__91), ._92(DECODER__92),
    ._93(DECODER__93), ._94(DECODER__94), ._95(DECODER__95), ._96(DECODER__96), ._97(DECODER__97),
    ._98(DECODER__98), ._99(DECODER__99), ._100(DECODER__100), ._101(DECODER__101), ._102(DECODER__102),
    ._103(DECODER__103), ._104(DECODER__104), ._105(DECODER__105), ._106(DECODER__106), ._107(DECODER__107),
    ._108(DECODER__108), ._109(DECODER__109), ._110(DECODER__110), ._111(DECODER__111), ._112(DECODER__112),
    ._113(DECODER__113), ._114(DECODER__114), ._115(DECODER__115), ._116(DECODER__116), ._117(DECODER__117),
    ._118(DECODER__118), ._119(DECODER__119), ._120(DECODER__120), ._121(DECODER__121), ._122(DECODER__122),
    ._123(DECODER__123), ._124(DECODER__124), ._125(DECODER__125), ._126(DECODER__126), ._127(DECODER__127),
    ._128(DECODER__128), ._129(DECODER__129));
  RANDOM_LOGIC RANDOM_LOGIC (
    .X0(DECODER__0), .X1(DECODER__1), .X2(DECODER__2), .X3(DECODER__3), .X4(DECODER__4), .X5(DECODER__5),
    .X6(DECODER__6), .X7(DECODER__7), .X8(DECODER__8), .X9(DECODER__9), .X10(DECODER__10), .X11(DECODER__11),
    .X12(DECODER__12), .X13(DECODER__13), .X14(DECODER__14), .X15(DECODER__15), .X16(DECODER__16),
    .X17(DECODER__17), .X18(DECODER__18), .X19(DECODER__19), .X20(DECODER__20), .X21(DECODER__21),
    .X22(DECODER__22), .X23(DECODER__23), .X24(DECODER__24), .X25(DECODER__25), .X26(DECODER__26),
    .X27(DECODER__27), .X28(DECODER__28), .X29(DECODER__29), .X30(DECODER__30), .X31(DECODER__31),
    .X32(DECODER__32), .X33(DECODER__33), .X34(DECODER__34), .X35(DECODER__35), .X36(DECODER__36),
    .X37(DECODER__37), .X38(DECODER__38), .X39(DECODER__39), .X40(DECODER__40), .X41(DECODER__41),
    .X42(DECODER__42), .X43(DECODER__43), .X44(DECODER__44), .X45(DECODER__45), .X46(DECODER__46),
    .X47(DECODER__47), .X48(DECODER__48), .X49(DECODER__49), .X50(DECODER__50), .X51(DECODER__51),
    .X52(DECODER__52), .X53(DECODER__53), .X54(DECODER__54), .X55(DECODER__55), .X56(DECODER__56),
    .X57(DECODER__57), .X58(DECODER__58), .X59(DECODER__59), .X60(DECODER__60), .X61(DECODER__61),
    .X62(DECODER__62), .X63(DECODER__63), .X64(DECODER__64), .X65(DECODER__65), .X66(DECODER__66),
    .X67(DECODER__67), .X68(DECODER__68), .X69(DECODER__69), .X70(DECODER__70), .X71(DECODER__71),
    .X72(DECODER__72), .X73(DECODER__73), .X74(DECODER__74), .X75(DECODER__75), .X76(DECODER__76),
    .X77(DECODER__77), .X78(DECODER__78), .X79(DECODER__79), .X80(DECODER__80), .X81(DECODER__81),
    .X82(DECODER__82), .X83(DECODER__83), .X84(DECODER__84), .X85(DECODER__85), .X86(DECODER__86),
    .X87(DECODER__87), .X88(DECODER__88), .X89(DECODER__89), .X90(DECODER__90), .X91(DECODER__91),
    .X92(DECODER__92), .X93(DECODER__93), .X94(DECODER__94), .X95(DECODER__95), .X96(DECODER__96),
    .X97(DECODER__97), .X98(DECODER__98), .X99(DECODER__99), .X100(DECODER__100), .X101(DECODER__101),
    .X102(DECODER__102), .X103(DECODER__103), .X104(DECODER__104), .X105(DECODER__105), .X106(DECODER__106),
    .X107(DECODER__107), .X108(DECODER__108), .X109(DECODER__109), .X110(DECODER__110), .X111(DECODER__111),
    .X112(DECODER__112), .X113(DECODER__113), .X114(DECODER__114), .X115(DECODER__115), .X116(DECODER__116),
    .X117(DECODER__117), .X118(DECODER__118), .X119(DECODER__119), .X120(DECODER__120), .X121(DECODER__121),
    .X122(DECODER__122), .X123(DECODER__123), .X124(DECODER__124), .X125(DECODER__125), .X126(DECODER__126),
    .X127(DECODER__127), .X128(DECODER__128), .X129(DECODER__129), .nNMIP(d_ff_1_q), .nIRQP(undriven),
    .RESP(undriven_2), .RDY(RDY), .SV(nor_1_out), .nT0(RANDOM_LOGIC_nt0), .nT1X(RANDOM_LOGIC_nt1x),
    .nT2(RANDOM_LOGIC_nt2), .nT3(RANDOM_LOGIC_nt3), .nT4(RANDOM_LOGIC_nt4), .nT5(RANDOM_LOGIC_nt5),
    .PHI1(PHI1), .PHI2(PHI2), .nTWOCYCLE(PREDECODE_ntwocycle), .nIMPLIED(PREDECODE_nimplied),
    .FETCH(RANDOM_LOGIC_fetch), .WR(RANDOM_LOGIC_wr), ._0_IR(RANDOM_LOGIC__0_ir), .T1(RANDOM_LOGIC_t1));  // open: DB0, DB1, DB2, DB3, DB4, DB5, DB6, DB7, AVR, ACR, ADH_ABH, ADL_ABL, Y_SB, X_SB, _0_ADL0, _0_ADL1, _0_ADL2, SB_Y, SB_X, S_SB, S_ADL, SB_S, S_S, SBXY, NDB_ADD, DB_ADD, _0_ADD, SB_ADD, ADL_ADD, ANDS, EORS, ORS, nACIN, SUMS, SRS, nDAA, ADD_SB7, ADD_SB06, ADD_ADL, nDSA
  not not_1 (not_1_out, SO);
  D_latch d_latch_1 (.EN(PHI1), .D(not_1_out), .NOT_Q(d_latch_1_not_q));  // open: Q
  D_latch d_latch_2 (.EN(PHI2), .D(d_latch_1_not_q), .NOT_Q(d_latch_2_not_q));  // open: Q
  D_latch d_latch_3 (.EN(PHI1), .D(d_latch_2_not_q), .Q(d_latch_3_q));  // open: NOT_Q
  nor nor_1 (nor_1_out, d_latch_3_q, d_latch_1_not_q);
  Clock PHI0 (.out(PHI0_out));
  CLOCKGEN clockgen_1 (.PHI0(PHI0_out), .PHI2(PHI2), .PHI1(PHI1));
  D_latch RWLatch (.EN(PHI1), .D(RANDOM_LOGIC_wr), .NOT_Q(R_W));  // open: Q
  IR IR (
    .FETCH(RANDOM_LOGIC_fetch), .PHI1(PHI1), .nin0(PREDECODE_npd7), .nin1(PREDECODE_npd6),
    .nin2(PREDECODE_npd5), .nin3(PREDECODE_npd4), .nin4(PREDECODE_npd3), .nin5(PREDECODE_npd2),
    .nin6(PREDECODE_npd1), .nin7(PREDECODE_npd0), .IR0(IR_ir0), .IR2(IR_ir2), .IR3(IR_ir3), .IR4(IR_ir4),
    .IR5(IR_ir5), .IR6(IR_ir6), .IR7(IR_ir7), .IR1(IR_ir1));
  PREDECODE PREDECODE (
    .PHI2(PHI2), ._0_IR(RANDOM_LOGIC__0_ir), .nPD0(PREDECODE_npd0), .nPD1(PREDECODE_npd1),
    .nPD2(PREDECODE_npd2), .nPD3(PREDECODE_npd3), .nPD4(PREDECODE_npd4), .nPD5(PREDECODE_npd5),
    .nPD6(PREDECODE_npd6), .nPD7(PREDECODE_npd7), .nIMPLIED(PREDECODE_nimplied),
    .nTWOCYCLE(PREDECODE_ntwocycle));  // open: D0, D1, D2, D3, D4, D5, D6, D7

  // Notes on the sheet:
  //   PHI2
  //   PHI1
  //   T1
  //   /NMIP
  //   SV
  //   PHI2
  //   PHI1
  //   FETCH
  //   WR
  //   PHI1
  //   PHI2
endmodule

module CLOCKGEN (
  input  PHI0,
  output PHI2,
  output PHI1
);

  wire not_1_out;

  not not_1 (not_1_out, PHI0);
  not not_2 (PHI1, PHI0);
  not not_3 (PHI2, not_1_out);
endmodule

module IR (
  input  FETCH,
  input  PHI1,
  input  nin0,
  input  nin1,
  input  nin2,
  input  nin3,
  input  nin4,
  input  nin5,
  input  nin6,
  input  nin7,
  output IR0,
  output IR1,
  output IR2,
  output IR3,
  output IR4,
  output IR5,
  output IR6,
  output IR7
);

  wire and1_out;

  and and1 (and1_out, FETCH, PHI1);
  D_latch d_latch_1 (.EN(and1_out), .D(nin0), .NOT_Q(IR0));  // open: Q
  D_latch d_latch_2 (.EN(and1_out), .D(nin1), .NOT_Q(IR1));  // open: Q
  D_latch d_latch_3 (.EN(and1_out), .D(nin2), .NOT_Q(IR2));  // open: Q
  D_latch d_latch_4 (.EN(and1_out), .D(nin3), .NOT_Q(IR3));  // open: Q
  D_latch d_latch_5 (.EN(and1_out), .D(nin4), .NOT_Q(IR4));  // open: Q
  D_latch d_latch_6 (.EN(and1_out), .D(nin5), .NOT_Q(IR5));  // open: Q
  D_latch d_latch_7 (.EN(and1_out), .D(nin6), .NOT_Q(IR6));  // open: Q
  D_latch d_latch_8 (.EN(and1_out), .D(nin7), .NOT_Q(IR7));  // open: Q
endmodule

module DECODER_TRANS (
  input  nT5,
  input  nT4,
  input  nT3,
  input  nT2,
  input  IR0,
  input  IR1,
  input  IR7,
  input  IR4,
  input  IR3,
  input  IR2,
  input  IR6,
  input  IR5,
  input  nT0,
  input  nT1X,
  output _0,
  output _1,
  output _2,
  output _3,
  output _4,
  output _5,
  output _6,
  output _7,
  output _8,
  output _9,
  output _10,
  output _11,
  output _12,
  output _13,
  output _14,
  output _15,
  output _16,
  output _17,
  output _18,
  output _19,
  output _20,
  output _21,
  output _22,
  output _23,
  output _24,
  output _25,
  output _26,
  output _27,
  output _28,
  output _29,
  output _30,
  output _31,
  output _32,
  output _33,
  output _34,
  output _35,
  output _36,
  output _37,
  output _38,
  output _39,
  output _40,
  output _41,
  output _42,
  output _43,
  output _44,
  output _45,
  output _46,
  output _47,
  output _48,
  output _49,
  output _50,
  output _51,
  output _52,
  output _53,
  output _54,
  output _55,
  output _56,
  output _57,
  output _58,
  output _59,
  output _60,
  output _61,
  output _62,
  output _63,
  output _64,
  output _65,
  output _66,
  output _67,
  output _68,
  output _69,
  output _70,
  output _71,
  output _72,
  output _73,
  output _74,
  output _75,
  output _76,
  output _77,
  output _78,
  output _79,
  output _80,
  output _81,
  output _82,
  output _83,
  output _84,
  output _85,
  output _86,
  output _87,
  output _88,
  output _89,
  output _90,
  output _91,
  output _92,
  output _93,
  output _94,
  output _95,
  output _96,
  output _97,
  output _98,
  output _99,
  output _100,
  output _101,
  output _102,
  output _103,
  output _104,
  output _105,
  output _106,
  output _107,
  output _108,
  output _109,
  output _110,
  output _111,
  output _112,
  output _113,
  output _114,
  output _115,
  output _116,
  output _117,
  output _118,
  output _119,
  output _120,
  output _121,
  output _122,
  output _123,
  output _124,
  output _125,
  output _126,
  output _127,
  output _128,
  output _129
);

  wire not_1_out, not_2_out, not_3_out, not_4_out, not_5_out, not_6_out, not_7_out, not_8_out, or_1_out;

  not not_1 (not_1_out, IR1);
  or or_1 (or_1_out, IR0, IR1);
  not not_2 (not_2_out, IR0);
  not not_3 (not_3_out, IR7);
  not not_4 (not_4_out, IR4);
  not not_5 (not_5_out, IR3);
  not not_6 (not_6_out, IR2);
  not not_7 (not_7_out, IR6);
  not not_8 (not_8_out, IR5);
  Pull_Resistor #(.pull(1)) pull_resistor_1 (.node(_0));
  Pull_Resistor #(.pull(1)) pull_resistor_2 (.node(_1));
  Transistor #(.\type ("n")) transistor_1 (.in(1'b0), .out(_1), .gate(nT3));
  Transistor #(.\type ("n")) transistor_2 (.in(1'b0), .out(_0), .gate(or_1_out));
  Transistor #(.\type ("n")) transistor_3 (.in(1'b0), .out(_1), .gate(not_2_out));
  Transistor #(.\type ("n")) transistor_4 (.in(1'b0), .out(_0), .gate(not_3_out));
  Transistor #(.\type ("n")) transistor_5 (.in(1'b0), .out(_0), .gate(not_4_out));
  Transistor #(.\type ("n")) transistor_6 (.in(1'b0), .out(_1), .gate(not_4_out));
  Transistor #(.\type ("n")) transistor_7 (.in(1'b0), .out(_1), .gate(IR3));
  Transistor #(.\type ("n")) transistor_8 (.in(1'b0), .out(_1), .gate(IR2));
  Transistor #(.\type ("n")) transistor_9 (.in(1'b0), .out(_0), .gate(not_6_out));
  Transistor #(.\type ("n")) transistor_10 (.in(1'b0), .out(_0), .gate(IR6));
  Transistor #(.\type ("n")) transistor_11 (.in(1'b0), .out(_0), .gate(IR5));
  Pull_Resistor #(.pull(1)) pull_resistor_3 (.node(_2));
  Transistor #(.\type ("n")) transistor_12 (.in(1'b0), .out(_2), .gate(nT2));
  Transistor #(.\type ("n")) transistor_13 (.in(1'b0), .out(_2), .gate(not_2_out));
  Transistor #(.\type ("n")) transistor_14 (.in(1'b0), .out(_2), .gate(not_4_out));
  Transistor #(.\type ("n")) transistor_15 (.in(1'b0), .out(_2), .gate(not_5_out));
  Transistor #(.\type ("n")) transistor_16 (.in(1'b0), .out(_2), .gate(IR2));
  Pull_Resistor #(.pull(1)) pull_resistor_4 (.node(_3));
  Transistor #(.\type ("n")) transistor_17 (.in(1'b0), .out(_3), .gate(or_1_out));
  Transistor #(.\type ("n")) transistor_18 (.in(1'b0), .out(_3), .gate(not_3_out));
  Transistor #(.\type ("n")) transistor_19 (.in(1'b0), .out(_3), .gate(IR4));
  Transistor #(.\type ("n")) transistor_20 (.in(1'b0), .out(_3), .gate(not_5_out));
  Transistor #(.\type ("n")) transistor_21 (.in(1'b0), .out(_3), .gate(IR2));
  Transistor #(.\type ("n")) transistor_22 (.in(1'b0), .out(_3), .gate(IR5));
  Transistor #(.\type ("n")) transistor_23 (.in(1'b0), .out(_3), .gate(nT0));
  Pull_Resistor #(.pull(1)) pull_resistor_5 (.node(_5));
  Pull_Resistor #(.pull(1)) pull_resistor_6 (.node(_4));
  Transistor #(.\type ("n")) transistor_24 (.in(1'b0), .out(_4), .gate(or_1_out));
  Transistor #(.\type ("n")) transistor_25 (.in(1'b0), .out(_5), .gate(or_1_out));
  Transistor #(.\type ("n")) transistor_26 (.in(1'b0), .out(_5), .gate(not_3_out));
  Transistor #(.\type ("n")) transistor_27 (.in(1'b0), .out(_4), .gate(not_3_out));
  Transistor #(.\type ("n")) transistor_28 (.in(1'b0), .out(_5), .gate(IR4));
  Transistor #(.\type ("n")) transistor_29 (.in(1'b0), .out(_4), .gate(not_4_out));
  Transistor #(.\type ("n")) transistor_30 (.in(1'b0), .out(_4), .gate(not_5_out));
  Transistor #(.\type ("n")) transistor_31 (.in(1'b0), .out(_4), .gate(IR2));
  Transistor #(.\type ("n")) transistor_32 (.in(1'b0), .out(_4), .gate(IR6));
  Transistor #(.\type ("n")) transistor_33 (.in(1'b0), .out(_5), .gate(not_7_out));
  Transistor #(.\type ("n")) transistor_34 (.in(1'b0), .out(_4), .gate(IR5));
  Transistor #(.\type ("n")) transistor_35 (.in(1'b0), .out(_5), .gate(IR5));
  Transistor #(.\type ("n")) transistor_36 (.in(1'b0), .out(_4), .gate(nT0));
  Transistor #(.\type ("n")) transistor_37 (.in(1'b0), .out(_5), .gate(nT0));
  Pull_Resistor #(.pull(1)) pull_resistor_7 (.node(_6));
  Transistor #(.\type ("n")) transistor_38 (.in(1'b0), .out(_6), .gate(nT2));
  Transistor #(.\type ("n")) transistor_39 (.in(1'b0), .out(_6), .gate(not_4_out));
  Transistor #(.\type ("n")) transistor_40 (.in(1'b0), .out(_6), .gate(not_6_out));
  Pull_Resistor #(.pull(1)) pull_resistor_8 (.node(_7));
  Transistor #(.\type ("n")) transistor_41 (.in(1'b0), .out(_7), .gate(not_1_out));
  Transistor #(.\type ("n")) transistor_42 (.in(1'b0), .out(_7), .gate(not_3_out));
  Transistor #(.\type ("n")) transistor_43 (.in(1'b0), .out(_7), .gate(IR6));
  Pull_Resistor #(.pull(1)) pull_resistor_9 (.node(_8));
  Pull_Resistor #(.pull(1)) pull_resistor_10 (.node(_9));
  Transistor #(.\type ("n")) transistor_44 (.in(1'b0), .out(_8), .gate(nT2));
  Transistor #(.\type ("n")) transistor_45 (.in(1'b0), .out(_9), .gate(not_1_out));
  Transistor #(.\type ("n")) transistor_46 (.in(1'b0), .out(_8), .gate(not_2_out));
  Transistor #(.\type ("n")) transistor_47 (.in(1'b0), .out(_9), .gate(not_3_out));
  Transistor #(.\type ("n")) transistor_48 (.in(1'b0), .out(_9), .gate(IR4));
  Transistor #(.\type ("n")) transistor_49 (.in(1'b0), .out(_8), .gate(IR4));
  Transistor #(.\type ("n")) transistor_50 (.in(1'b0), .out(_8), .gate(IR3));
  Transistor #(.\type ("n")) transistor_51 (.in(1'b0), .out(_9), .gate(not_5_out));
  Transistor #(.\type ("n")) transistor_52 (.in(1'b0), .out(_9), .gate(IR2));
  Transistor #(.\type ("n")) transistor_53 (.in(1'b0), .out(_8), .gate(IR2));
  Transistor #(.\type ("n")) transistor_54 (.in(1'b0), .out(_9), .gate(IR6));
  Transistor #(.\type ("n")) transistor_55 (.in(1'b0), .out(_9), .gate(IR5));
  Transistor #(.\type ("n")) transistor_56 (.in(1'b0), .out(_9), .gate(nT0));
  Pull_Resistor #(.pull(1)) pull_resistor_11 (.node(_10));
  Transistor #(.\type ("n")) transistor_57 (.in(1'b0), .out(_10), .gate(not_1_out));
  Transistor #(.\type ("n")) transistor_58 (.in(1'b0), .out(_10), .gate(not_3_out));
  Transistor #(.\type ("n")) transistor_59 (.in(1'b0), .out(_10), .gate(IR4));
  Transistor #(.\type ("n")) transistor_60 (.in(1'b0), .out(_10), .gate(not_5_out));
  Transistor #(.\type ("n")) transistor_61 (.in(1'b0), .out(_10), .gate(IR2));
  Transistor #(.\type ("n")) transistor_62 (.in(1'b0), .out(_10), .gate(not_7_out));
  Transistor #(.\type ("n")) transistor_63 (.in(1'b0), .out(_10), .gate(IR5));
  Transistor #(.\type ("n")) transistor_64 (.in(1'b0), .out(_10), .gate(nT0));
  Pull_Resistor #(.pull(1)) pull_resistor_12 (.node(_11));
  Transistor #(.\type ("n")) transistor_65 (.in(1'b0), .out(_11), .gate(or_1_out));
  Transistor #(.\type ("n")) transistor_66 (.in(1'b0), .out(_11), .gate(not_3_out));
  Transistor #(.\type ("n")) transistor_67 (.in(1'b0), .out(_11), .gate(IR4));
  Transistor #(.\type ("n")) transistor_68 (.in(1'b0), .out(_11), .gate(not_7_out));
  Transistor #(.\type ("n")) transistor_69 (.in(1'b0), .out(_11), .gate(not_8_out));
  Transistor #(.\type ("n")) transistor_70 (.in(1'b0), .out(_11), .gate(nT0));
  Pull_Resistor #(.pull(1)) pull_resistor_13 (.node(_12));
  Pull_Resistor #(.pull(1)) pull_resistor_14 (.node(_13));
  Transistor #(.\type ("n")) transistor_71 (.in(1'b0), .out(_13), .gate(not_1_out));
  Transistor #(.\type ("n")) transistor_72 (.in(1'b0), .out(_12), .gate(not_1_out));
  Transistor #(.\type ("n")) transistor_73 (.in(1'b0), .out(_13), .gate(not_3_out));
  Transistor #(.\type ("n")) transistor_74 (.in(1'b0), .out(_12), .gate(not_3_out));
  Transistor #(.\type ("n")) transistor_75 (.in(1'b0), .out(_13), .gate(not_4_out));
  Transistor #(.\type ("n")) transistor_76 (.in(1'b0), .out(_13), .gate(not_5_out));
  Transistor #(.\type ("n")) transistor_77 (.in(1'b0), .out(_13), .gate(IR2));
  Transistor #(.\type ("n")) transistor_78 (.in(1'b0), .out(_12), .gate(IR6));
  Transistor #(.\type ("n")) transistor_79 (.in(1'b0), .out(_13), .gate(IR6));
  Transistor #(.\type ("n")) transistor_80 (.in(1'b0), .out(_13), .gate(IR5));
  Transistor #(.\type ("n")) transistor_81 (.in(1'b0), .out(_12), .gate(IR5));
  Transistor #(.\type ("n")) transistor_82 (.in(1'b0), .out(_13), .gate(nT0));
  Pull_Resistor #(.pull(1)) pull_resistor_15 (.node(_14));
  Transistor #(.\type ("n")) transistor_83 (.in(1'b0), .out(_14), .gate(not_1_out));
  Transistor #(.\type ("n")) transistor_84 (.in(1'b0), .out(_14), .gate(not_3_out));
  Transistor #(.\type ("n")) transistor_85 (.in(1'b0), .out(_14), .gate(IR6));
  Transistor #(.\type ("n")) transistor_86 (.in(1'b0), .out(_14), .gate(not_8_out));
  Transistor #(.\type ("n")) transistor_87 (.in(1'b0), .out(_14), .gate(nT0));
  Pull_Resistor #(.pull(1)) pull_resistor_16 (.node(_15));
  Transistor #(.\type ("n")) transistor_88 (.in(1'b0), .out(_15), .gate(not_1_out));
  Transistor #(.\type ("n")) transistor_89 (.in(1'b0), .out(_15), .gate(not_3_out));
  Transistor #(.\type ("n")) transistor_90 (.in(1'b0), .out(_15), .gate(IR4));
  Transistor #(.\type ("n")) transistor_91 (.in(1'b0), .out(_15), .gate(not_5_out));
  Transistor #(.\type ("n")) transistor_92 (.in(1'b0), .out(_15), .gate(IR2));
  Transistor #(.\type ("n")) transistor_93 (.in(1'b0), .out(_15), .gate(not_7_out));
  Transistor #(.\type ("n")) transistor_94 (.in(1'b0), .out(_15), .gate(IR5));
  Transistor #(.\type ("n")) transistor_95 (.in(1'b0), .out(_15), .gate(nT1X));
  Pull_Resistor #(.pull(1)) pull_resistor_17 (.node(_16));
  Pull_Resistor #(.pull(1)) pull_resistor_18 (.node(_17));
  Transistor #(.\type ("n")) transistor_96 (.in(1'b0), .out(_17), .gate(not_1_out));
  Transistor #(.\type ("n")) transistor_97 (.in(1'b0), .out(_16), .gate(or_1_out));
  Transistor #(.\type ("n")) transistor_98 (.in(1'b0), .out(_17), .gate(not_3_out));
  Transistor #(.\type ("n")) transistor_99 (.in(1'b0), .out(_16), .gate(not_3_out));
  Transistor #(.\type ("n")) transistor_100 (.in(1'b0), .out(_16), .gate(IR4));
  Transistor #(.\type ("n")) transistor_101 (.in(1'b0), .out(_17), .gate(not_4_out));
  Transistor #(.\type ("n")) transistor_102 (.in(1'b0), .out(_17), .gate(not_5_out));
  Transistor #(.\type ("n")) transistor_103 (.in(1'b0), .out(_16), .gate(not_5_out));
  Transistor #(.\type ("n")) transistor_104 (.in(1'b0), .out(_16), .gate(IR2));
  Transistor #(.\type ("n")) transistor_105 (.in(1'b0), .out(_17), .gate(IR2));
  Transistor #(.\type ("n")) transistor_106 (.in(1'b0), .out(_17), .gate(IR6));
  Transistor #(.\type ("n")) transistor_107 (.in(1'b0), .out(_16), .gate(not_7_out));
  Transistor #(.\type ("n")) transistor_108 (.in(1'b0), .out(_16), .gate(not_8_out));
  Transistor #(.\type ("n")) transistor_109 (.in(1'b0), .out(_17), .gate(not_8_out));
  Transistor #(.\type ("n")) transistor_110 (.in(1'b0), .out(_17), .gate(nT0));
  Transistor #(.\type ("n")) transistor_111 (.in(1'b0), .out(_16), .gate(nT1X));
  Pull_Resistor #(.pull(1)) pull_resistor_19 (.node(_18));
  Transistor #(.\type ("n")) transistor_112 (.in(1'b0), .out(_18), .gate(or_1_out));
  Transistor #(.\type ("n")) transistor_113 (.in(1'b0), .out(_18), .gate(not_3_out));
  Transistor #(.\type ("n")) transistor_114 (.in(1'b0), .out(_18), .gate(IR4));
  Transistor #(.\type ("n")) transistor_115 (.in(1'b0), .out(_18), .gate(not_5_out));
  Transistor #(.\type ("n")) transistor_116 (.in(1'b0), .out(_18), .gate(IR2));
  Transistor #(.\type ("n")) transistor_117 (.in(1'b0), .out(_18), .gate(IR5));
  Transistor #(.\type ("n")) transistor_118 (.in(1'b0), .out(_18), .gate(nT1X));
  Pull_Resistor #(.pull(1)) pull_resistor_20 (.node(_19));
  Transistor #(.\type ("n")) transistor_119 (.in(1'b0), .out(_19), .gate(or_1_out));
  Transistor #(.\type ("n")) transistor_120 (.in(1'b0), .out(_19), .gate(not_3_out));
  Transistor #(.\type ("n")) transistor_121 (.in(1'b0), .out(_19), .gate(not_6_out));
  Transistor #(.\type ("n")) transistor_122 (.in(1'b0), .out(_19), .gate(IR6));
  Transistor #(.\type ("n")) transistor_123 (.in(1'b0), .out(_19), .gate(not_8_out));
  Transistor #(.\type ("n")) transistor_124 (.in(1'b0), .out(_19), .gate(nT0));
  Pull_Resistor #(.pull(1)) pull_resistor_21 (.node(_20));
  Transistor #(.\type ("n")) transistor_125 (.in(1'b0), .out(_20), .gate(or_1_out));
  Transistor #(.\type ("n")) transistor_126 (.in(1'b0), .out(_20), .gate(not_3_out));
  Transistor #(.\type ("n")) transistor_127 (.in(1'b0), .out(_20), .gate(IR4));
  Transistor #(.\type ("n")) transistor_128 (.in(1'b0), .out(_20), .gate(IR6));
  Transistor #(.\type ("n")) transistor_129 (.in(1'b0), .out(_20), .gate(not_8_out));
  Transistor #(.\type ("n")) transistor_130 (.in(1'b0), .out(_20), .gate(nT0));
  Pull_Resistor #(.pull(1)) pull_resistor_22 (.node(_21));
  Transistor #(.\type ("n")) transistor_131 (.in(1'b0), .out(_21), .gate(or_1_out));
  Transistor #(.\type ("n")) transistor_132 (.in(1'b0), .out(_21), .gate(IR7));
  Transistor #(.\type ("n")) transistor_133 (.in(1'b0), .out(_21), .gate(IR4));
  Transistor #(.\type ("n")) transistor_134 (.in(1'b0), .out(_21), .gate(IR3));
  Transistor #(.\type ("n")) transistor_135 (.in(1'b0), .out(_21), .gate(IR2));
  Transistor #(.\type ("n")) transistor_136 (.in(1'b0), .out(_21), .gate(IR6));
  Transistor #(.\type ("n")) transistor_137 (.in(1'b0), .out(_21), .gate(not_8_out));
  Transistor #(.\type ("n")) transistor_138 (.in(1'b0), .out(_21), .gate(nT0));
  Pull_Resistor #(.pull(1)) pull_resistor_23 (.node(_22));
  Transistor #(.\type ("n")) transistor_139 (.in(1'b0), .out(_22), .gate(nT5));
  Transistor #(.\type ("n")) transistor_140 (.in(1'b0), .out(_22), .gate(or_1_out));
  Transistor #(.\type ("n")) transistor_141 (.in(1'b0), .out(_22), .gate(IR7));
  Transistor #(.\type ("n")) transistor_142 (.in(1'b0), .out(_22), .gate(IR4));
  Transistor #(.\type ("n")) transistor_143 (.in(1'b0), .out(_22), .gate(IR3));
  Transistor #(.\type ("n")) transistor_144 (.in(1'b0), .out(_22), .gate(IR2));
  Transistor #(.\type ("n")) transistor_145 (.in(1'b0), .out(_22), .gate(IR6));
  Transistor #(.\type ("n")) transistor_146 (.in(1'b0), .out(_22), .gate(IR5));
  Pull_Resistor #(.pull(1)) pull_resistor_24 (.node(_23));
  Transistor #(.\type ("n")) transistor_147 (.in(1'b0), .out(_23), .gate(or_1_out));
  Transistor #(.\type ("n")) transistor_148 (.in(1'b0), .out(_23), .gate(IR7));
  Transistor #(.\type ("n")) transistor_149 (.in(1'b0), .out(_23), .gate(IR4));
  Transistor #(.\type ("n")) transistor_150 (.in(1'b0), .out(_23), .gate(not_5_out));
  Transistor #(.\type ("n")) transistor_151 (.in(1'b0), .out(_23), .gate(IR2));
  Transistor #(.\type ("n")) transistor_152 (.in(1'b0), .out(_23), .gate(IR5));
  Transistor #(.\type ("n")) transistor_153 (.in(1'b0), .out(_23), .gate(nT0));
  Pull_Resistor #(.pull(1)) pull_resistor_25 (.node(_25));
  Pull_Resistor #(.pull(1)) pull_resistor_26 (.node(_24));
  Transistor #(.\type ("n")) transistor_154 (.in(1'b0), .out(_24), .gate(nT4));
  Transistor #(.\type ("n")) transistor_155 (.in(1'b0), .out(_25), .gate(nT3));
  Transistor #(.\type ("n")) transistor_156 (.in(1'b0), .out(_24), .gate(or_1_out));
  Transistor #(.\type ("n")) transistor_157 (.in(1'b0), .out(_25), .gate(or_1_out));
  Transistor #(.\type ("n")) transistor_158 (.in(1'b0), .out(_24), .gate(IR7));
  Transistor #(.\type ("n")) transistor_159 (.in(1'b0), .out(_25), .gate(IR7));
  Transistor #(.\type ("n")) transistor_160 (.in(1'b0), .out(_24), .gate(IR4));
  Transistor #(.\type ("n")) transistor_161 (.in(1'b0), .out(_25), .gate(IR4));
  Transistor #(.\type ("n")) transistor_162 (.in(1'b0), .out(_24), .gate(IR3));
  Transistor #(.\type ("n")) transistor_163 (.in(1'b0), .out(_25), .gate(not_5_out));
  Transistor #(.\type ("n")) transistor_164 (.in(1'b0), .out(_25), .gate(IR2));
  Transistor #(.\type ("n")) transistor_165 (.in(1'b0), .out(_24), .gate(IR2));
  Transistor #(.\type ("n")) transistor_166 (.in(1'b0), .out(_24), .gate(not_7_out));
  Transistor #(.\type ("n")) transistor_167 (.in(1'b0), .out(_25), .gate(not_8_out));
  Transistor #(.\type ("n")) transistor_168 (.in(1'b0), .out(_24), .gate(not_8_out));
  Pull_Resistor #(.pull(1)) pull_resistor_27 (.node(_26));
  Transistor #(.\type ("n")) transistor_169 (.in(1'b0), .out(_26), .gate(nT5));
  Transistor #(.\type ("n")) transistor_170 (.in(1'b0), .out(_26), .gate(or_1_out));
  Transistor #(.\type ("n")) transistor_171 (.in(1'b0), .out(_26), .gate(IR7));
  Transistor #(.\type ("n")) transistor_172 (.in(1'b0), .out(_26), .gate(IR4));
  Transistor #(.\type ("n")) transistor_173 (.in(1'b0), .out(_26), .gate(IR3));
  Transistor #(.\type ("n")) transistor_174 (.in(1'b0), .out(_26), .gate(IR2));
  Transistor #(.\type ("n")) transistor_175 (.in(1'b0), .out(_26), .gate(not_7_out));
  Transistor #(.\type ("n")) transistor_176 (.in(1'b0), .out(_26), .gate(IR5));
  Pull_Resistor #(.pull(1)) pull_resistor_28 (.node(_27));
  Transistor #(.\type ("n")) transistor_177 (.in(1'b0), .out(_27), .gate(not_1_out));
  Transistor #(.\type ("n")) transistor_178 (.in(1'b0), .out(_27), .gate(IR7));
  Transistor #(.\type ("n")) transistor_179 (.in(1'b0), .out(_27), .gate(not_7_out));
  Transistor #(.\type ("n")) transistor_180 (.in(1'b0), .out(_27), .gate(not_8_out));
  Pull_Resistor #(.pull(1)) pull_resistor_29 (.node(_28));
  Pull_Resistor #(.pull(1)) pull_resistor_30 (.node(_29));
  Transistor #(.\type ("n")) transistor_181 (.in(1'b0), .out(_28), .gate(nT2));
  Transistor #(.\type ("n")) transistor_182 (.in(1'b0), .out(_29), .gate(not_2_out));
  Transistor #(.\type ("n")) transistor_183 (.in(1'b0), .out(_29), .gate(IR7));
  Transistor #(.\type ("n")) transistor_184 (.in(1'b0), .out(_29), .gate(not_7_out));
  Transistor #(.\type ("n")) transistor_185 (.in(1'b0), .out(_29), .gate(IR5));
  Transistor #(.\type ("n")) transistor_186 (.in(1'b0), .out(_29), .gate(nT0));
  Pull_Resistor #(.pull(1)) pull_resistor_31 (.node(_30));
  Transistor #(.\type ("n")) transistor_187 (.in(1'b0), .out(_30), .gate(or_1_out));
  Transistor #(.\type ("n")) transistor_188 (.in(1'b0), .out(_30), .gate(IR7));
  Transistor #(.\type ("n")) transistor_189 (.in(1'b0), .out(_30), .gate(IR4));
  Transistor #(.\type ("n")) transistor_190 (.in(1'b0), .out(_30), .gate(not_5_out));
  Transistor #(.\type ("n")) transistor_191 (.in(1'b0), .out(_30), .gate(not_6_out));
  Transistor #(.\type ("n")) transistor_192 (.in(1'b0), .out(_30), .gate(not_7_out));
  Pull_Resistor #(.pull(1)) pull_resistor_32 (.node(_31));
  Transistor #(.\type ("n")) transistor_193 (.in(1'b0), .out(_31), .gate(nT2));
  Transistor #(.\type ("n")) transistor_194 (.in(1'b0), .out(_31), .gate(IR4));
  Transistor #(.\type ("n")) transistor_195 (.in(1'b0), .out(_31), .gate(not_5_out));
  Transistor #(.\type ("n")) transistor_196 (.in(1'b0), .out(_31), .gate(not_6_out));
  Pull_Resistor #(.pull(1)) pull_resistor_33 (.node(_32));
  Pull_Resistor #(.pull(1)) pull_resistor_34 (.node(_33));
  Transistor #(.\type ("n")) transistor_197 (.in(1'b0), .out(_33), .gate(nT2));
  Transistor #(.\type ("n")) transistor_198 (.in(1'b0), .out(_32), .gate(not_2_out));
  Transistor #(.\type ("n")) transistor_199 (.in(1'b0), .out(_32), .gate(IR7));
  Transistor #(.\type ("n")) transistor_200 (.in(1'b0), .out(_33), .gate(IR3));
  Transistor #(.\type ("n")) transistor_201 (.in(1'b0), .out(_32), .gate(IR6));
  Transistor #(.\type ("n")) transistor_202 (.in(1'b0), .out(_32), .gate(IR5));
  Transistor #(.\type ("n")) transistor_203 (.in(1'b0), .out(_32), .gate(nT0));
  Pull_Resistor #(.pull(1)) pull_resistor_35 (.node(_34));
  Transistor #(.\type ("n")) transistor_204 (.in(1'b0), .out(_34), .gate(nT0));
  Pull_Resistor #(.pull(1)) pull_resistor_36 (.node(_35));
  Transistor #(.\type ("n")) transistor_205 (.in(1'b0), .out(_35), .gate(nT2));
  Transistor #(.\type ("n")) transistor_206 (.in(1'b0), .out(_35), .gate(or_1_out));
  Transistor #(.\type ("n")) transistor_207 (.in(1'b0), .out(_35), .gate(IR7));
  Transistor #(.\type ("n")) transistor_208 (.in(1'b0), .out(_35), .gate(IR4));
  Transistor #(.\type ("n")) transistor_209 (.in(1'b0), .out(_35), .gate(IR2));
  Pull_Resistor #(.pull(1)) pull_resistor_37 (.node(_36));
  Transistor #(.\type ("n")) transistor_210 (.in(1'b0), .out(_36), .gate(nT3));
  Transistor #(.\type ("n")) transistor_211 (.in(1'b0), .out(_36), .gate(or_1_out));
  Transistor #(.\type ("n")) transistor_212 (.in(1'b0), .out(_36), .gate(IR7));
  Transistor #(.\type ("n")) transistor_213 (.in(1'b0), .out(_36), .gate(IR4));
  Pull_Resistor #(.pull(1)) pull_resistor_38 (.node(_37));
  Transistor #(.\type ("n")) transistor_214 (.in(1'b0), .out(_37), .gate(nT4));
  Transistor #(.\type ("n")) transistor_215 (.in(1'b0), .out(_37), .gate(or_1_out));
  Transistor #(.\type ("n")) transistor_216 (.in(1'b0), .out(_37), .gate(IR7));
  Transistor #(.\type ("n")) transistor_217 (.in(1'b0), .out(_37), .gate(IR4));
  Transistor #(.\type ("n")) transistor_218 (.in(1'b0), .out(_37), .gate(IR3));
  Transistor #(.\type ("n")) transistor_219 (.in(1'b0), .out(_37), .gate(IR2));
  Transistor #(.\type ("n")) transistor_220 (.in(1'b0), .out(_37), .gate(IR6));
  Pull_Resistor #(.pull(1)) pull_resistor_39 (.node(_38));
  Transistor #(.\type ("n")) transistor_221 (.in(1'b0), .out(_38), .gate(nT4));
  Transistor #(.\type ("n")) transistor_222 (.in(1'b0), .out(_38), .gate(or_1_out));
  Transistor #(.\type ("n")) transistor_223 (.in(1'b0), .out(_38), .gate(IR7));
  Transistor #(.\type ("n")) transistor_224 (.in(1'b0), .out(_38), .gate(IR4));
  Transistor #(.\type ("n")) transistor_225 (.in(1'b0), .out(_38), .gate(IR3));
  Transistor #(.\type ("n")) transistor_226 (.in(1'b0), .out(_38), .gate(IR2));
  Transistor #(.\type ("n")) transistor_227 (.in(1'b0), .out(_38), .gate(not_7_out));
  Transistor #(.\type ("n")) transistor_228 (.in(1'b0), .out(_38), .gate(IR5));
  Pull_Resistor #(.pull(1)) pull_resistor_40 (.node(_39));
  Pull_Resistor #(.pull(1)) pull_resistor_41 (.node(_40));
  Transistor #(.\type ("n")) transistor_229 (.in(1'b0), .out(_40), .gate(nT4));
  Transistor #(.\type ("n")) transistor_230 (.in(1'b0), .out(_39), .gate(nT3));
  Transistor #(.\type ("n")) transistor_231 (.in(1'b0), .out(_39), .gate(not_2_out));
  Transistor #(.\type ("n")) transistor_232 (.in(1'b0), .out(_40), .gate(not_2_out));
  Transistor #(.\type ("n")) transistor_233 (.in(1'b0), .out(_39), .gate(IR4));
  Transistor #(.\type ("n")) transistor_234 (.in(1'b0), .out(_40), .gate(not_4_out));
  Transistor #(.\type ("n")) transistor_235 (.in(1'b0), .out(_40), .gate(IR3));
  Transistor #(.\type ("n")) transistor_236 (.in(1'b0), .out(_39), .gate(IR3));
  Transistor #(.\type ("n")) transistor_237 (.in(1'b0), .out(_40), .gate(IR2));
  Transistor #(.\type ("n")) transistor_238 (.in(1'b0), .out(_39), .gate(IR2));
  Pull_Resistor #(.pull(1)) pull_resistor_42 (.node(_41));
  Transistor #(.\type ("n")) transistor_239 (.in(1'b0), .out(_41), .gate(nT2));
  Transistor #(.\type ("n")) transistor_240 (.in(1'b0), .out(_41), .gate(not_2_out));
  Transistor #(.\type ("n")) transistor_241 (.in(1'b0), .out(_41), .gate(not_4_out));
  Transistor #(.\type ("n")) transistor_242 (.in(1'b0), .out(_41), .gate(IR3));
  Transistor #(.\type ("n")) transistor_243 (.in(1'b0), .out(_41), .gate(IR2));
  Pull_Resistor #(.pull(1)) pull_resistor_43 (.node(_42));
  Transistor #(.\type ("n")) transistor_244 (.in(1'b0), .out(_42), .gate(nT3));
  Transistor #(.\type ("n")) transistor_245 (.in(1'b0), .out(_42), .gate(not_4_out));
  Transistor #(.\type ("n")) transistor_246 (.in(1'b0), .out(_42), .gate(not_5_out));
  Pull_Resistor #(.pull(1)) pull_resistor_44 (.node(_44));
  Pull_Resistor #(.pull(1)) pull_resistor_45 (.node(_43));
  Transistor #(.\type ("n")) transistor_247 (.in(1'b0), .out(_44), .gate(not_1_out));
  Transistor #(.\type ("n")) transistor_248 (.in(1'b0), .out(_43), .gate(or_1_out));
  Transistor #(.\type ("n")) transistor_249 (.in(1'b0), .out(_43), .gate(IR7));
  Transistor #(.\type ("n")) transistor_250 (.in(1'b0), .out(_44), .gate(not_3_out));
  Transistor #(.\type ("n")) transistor_251 (.in(1'b0), .out(_43), .gate(IR4));
  Transistor #(.\type ("n")) transistor_252 (.in(1'b0), .out(_43), .gate(not_5_out));
  Transistor #(.\type ("n")) transistor_253 (.in(1'b0), .out(_43), .gate(IR2));
  Transistor #(.\type ("n")) transistor_254 (.in(1'b0), .out(_44), .gate(not_7_out));
  Transistor #(.\type ("n")) transistor_255 (.in(1'b0), .out(_44), .gate(not_8_out));
  Transistor #(.\type ("n")) transistor_256 (.in(1'b0), .out(_43), .gate(not_8_out));
  Pull_Resistor #(.pull(1)) pull_resistor_46 (.node(_45));
  Transistor #(.\type ("n")) transistor_257 (.in(1'b0), .out(_45), .gate(nT4));
  Transistor #(.\type ("n")) transistor_258 (.in(1'b0), .out(_45), .gate(not_2_out));
  Transistor #(.\type ("n")) transistor_259 (.in(1'b0), .out(_45), .gate(IR4));
  Transistor #(.\type ("n")) transistor_260 (.in(1'b0), .out(_45), .gate(IR3));
  Transistor #(.\type ("n")) transistor_261 (.in(1'b0), .out(_45), .gate(IR2));
  Pull_Resistor #(.pull(1)) pull_resistor_47 (.node(_46));
  Transistor #(.\type ("n")) transistor_262 (.in(1'b0), .out(_46), .gate(nT3));
  Transistor #(.\type ("n")) transistor_263 (.in(1'b0), .out(_46), .gate(not_2_out));
  Transistor #(.\type ("n")) transistor_264 (.in(1'b0), .out(_46), .gate(not_4_out));
  Transistor #(.\type ("n")) transistor_265 (.in(1'b0), .out(_46), .gate(IR3));
  Transistor #(.\type ("n")) transistor_266 (.in(1'b0), .out(_46), .gate(IR2));
  Pull_Resistor #(.pull(1)) pull_resistor_48 (.node(_48));
  Pull_Resistor #(.pull(1)) pull_resistor_49 (.node(_47));
  Transistor #(.\type ("n")) transistor_267 (.in(1'b0), .out(_48), .gate(nT2));
  Transistor #(.\type ("n")) transistor_268 (.in(1'b0), .out(_48), .gate(or_1_out));
  Transistor #(.\type ("n")) transistor_269 (.in(1'b0), .out(_47), .gate(or_1_out));
  Transistor #(.\type ("n")) transistor_270 (.in(1'b0), .out(_48), .gate(IR7));
  Transistor #(.\type ("n")) transistor_271 (.in(1'b0), .out(_47), .gate(IR7));
  Transistor #(.\type ("n")) transistor_272 (.in(1'b0), .out(_47), .gate(IR4));
  Transistor #(.\type ("n")) transistor_273 (.in(1'b0), .out(_48), .gate(IR4));
  Transistor #(.\type ("n")) transistor_274 (.in(1'b0), .out(_47), .gate(IR3));
  Transistor #(.\type ("n")) transistor_275 (.in(1'b0), .out(_48), .gate(IR3));
  Transistor #(.\type ("n")) transistor_276 (.in(1'b0), .out(_48), .gate(IR2));
  Transistor #(.\type ("n")) transistor_277 (.in(1'b0), .out(_47), .gate(IR2));
  Transistor #(.\type ("n")) transistor_278 (.in(1'b0), .out(_48), .gate(IR6));
  Transistor #(.\type ("n")) transistor_279 (.in(1'b0), .out(_47), .gate(not_7_out));
  Transistor #(.\type ("n")) transistor_280 (.in(1'b0), .out(_48), .gate(not_8_out));
  Pull_Resistor #(.pull(1)) pull_resistor_50 (.node(_49));
  Transistor #(.\type ("n")) transistor_281 (.in(1'b0), .out(_49), .gate(or_1_out));
  Transistor #(.\type ("n")) transistor_282 (.in(1'b0), .out(_49), .gate(not_3_out));
  Transistor #(.\type ("n")) transistor_283 (.in(1'b0), .out(_49), .gate(IR4));
  Transistor #(.\type ("n")) transistor_284 (.in(1'b0), .out(_49), .gate(not_7_out));
  Transistor #(.\type ("n")) transistor_285 (.in(1'b0), .out(_49), .gate(nT0));
  Pull_Resistor #(.pull(1)) pull_resistor_51 (.node(_50));
  Transistor #(.\type ("n")) transistor_286 (.in(1'b0), .out(_50), .gate(not_2_out));
  Transistor #(.\type ("n")) transistor_287 (.in(1'b0), .out(_50), .gate(not_3_out));
  Transistor #(.\type ("n")) transistor_288 (.in(1'b0), .out(_50), .gate(not_7_out));
  Transistor #(.\type ("n")) transistor_289 (.in(1'b0), .out(_50), .gate(IR5));
  Transistor #(.\type ("n")) transistor_290 (.in(1'b0), .out(_50), .gate(nT0));
  Pull_Resistor #(.pull(1)) pull_resistor_52 (.node(_52));
  Pull_Resistor #(.pull(1)) pull_resistor_53 (.node(_51));
  Transistor #(.\type ("n")) transistor_291 (.in(1'b0), .out(_52), .gate(not_2_out));
  Transistor #(.\type ("n")) transistor_292 (.in(1'b0), .out(_51), .gate(not_2_out));
  Transistor #(.\type ("n")) transistor_293 (.in(1'b0), .out(_51), .gate(not_3_out));
  Transistor #(.\type ("n")) transistor_294 (.in(1'b0), .out(_52), .gate(not_7_out));
  Transistor #(.\type ("n")) transistor_295 (.in(1'b0), .out(_51), .gate(not_7_out));
  Transistor #(.\type ("n")) transistor_296 (.in(1'b0), .out(_52), .gate(not_8_out));
  Transistor #(.\type ("n")) transistor_297 (.in(1'b0), .out(_51), .gate(not_8_out));
  Transistor #(.\type ("n")) transistor_298 (.in(1'b0), .out(_52), .gate(nT0));
  Transistor #(.\type ("n")) transistor_299 (.in(1'b0), .out(_51), .gate(nT0));
  Pull_Resistor #(.pull(1)) pull_resistor_54 (.node(_53));
  Transistor #(.\type ("n")) transistor_300 (.in(1'b0), .out(_53), .gate(not_1_out));
  Transistor #(.\type ("n")) transistor_301 (.in(1'b0), .out(_53), .gate(IR7));
  Transistor #(.\type ("n")) transistor_302 (.in(1'b0), .out(_53), .gate(IR6));
  Transistor #(.\type ("n")) transistor_303 (.in(1'b0), .out(_53), .gate(not_8_out));
  Pull_Resistor #(.pull(1)) pull_resistor_55 (.node(_54));
  Transistor #(.\type ("n")) transistor_304 (.in(1'b0), .out(_54), .gate(nT3));
  Transistor #(.\type ("n")) transistor_305 (.in(1'b0), .out(_54), .gate(or_1_out));
  Transistor #(.\type ("n")) transistor_306 (.in(1'b0), .out(_54), .gate(IR7));
  Transistor #(.\type ("n")) transistor_307 (.in(1'b0), .out(_54), .gate(IR4));
  Transistor #(.\type ("n")) transistor_308 (.in(1'b0), .out(_54), .gate(not_5_out));
  Transistor #(.\type ("n")) transistor_309 (.in(1'b0), .out(_54), .gate(not_6_out));
  Transistor #(.\type ("n")) transistor_310 (.in(1'b0), .out(_54), .gate(not_7_out));
  Pull_Resistor #(.pull(1)) pull_resistor_56 (.node(_55));
  Pull_Resistor #(.pull(1)) pull_resistor_57 (.node(_56));
  Transistor #(.\type ("n")) transistor_311 (.in(1'b0), .out(_56), .gate(nT5));
  Transistor #(.\type ("n")) transistor_312 (.in(1'b0), .out(_55), .gate(not_1_out));
  Transistor #(.\type ("n")) transistor_313 (.in(1'b0), .out(_56), .gate(or_1_out));
  Transistor #(.\type ("n")) transistor_314 (.in(1'b0), .out(_55), .gate(IR7));
  Transistor #(.\type ("n")) transistor_315 (.in(1'b0), .out(_56), .gate(IR7));
  Transistor #(.\type ("n")) transistor_316 (.in(1'b0), .out(_56), .gate(IR4));
  Transistor #(.\type ("n")) transistor_317 (.in(1'b0), .out(_56), .gate(IR3));
  Transistor #(.\type ("n")) transistor_318 (.in(1'b0), .out(_56), .gate(IR2));
  Transistor #(.\type ("n")) transistor_319 (.in(1'b0), .out(_55), .gate(IR6));
  Transistor #(.\type ("n")) transistor_320 (.in(1'b0), .out(_56), .gate(IR6));
  Transistor #(.\type ("n")) transistor_321 (.in(1'b0), .out(_56), .gate(not_8_out));
  Pull_Resistor #(.pull(1)) pull_resistor_58 (.node(_57));
  Transistor #(.\type ("n")) transistor_322 (.in(1'b0), .out(_57), .gate(nT2));
  Transistor #(.\type ("n")) transistor_323 (.in(1'b0), .out(_57), .gate(or_1_out));
  Transistor #(.\type ("n")) transistor_324 (.in(1'b0), .out(_57), .gate(IR7));
  Transistor #(.\type ("n")) transistor_325 (.in(1'b0), .out(_57), .gate(IR4));
  Transistor #(.\type ("n")) transistor_326 (.in(1'b0), .out(_57), .gate(IR2));
  Pull_Resistor #(.pull(1)) pull_resistor_59 (.node(_58));
  Transistor #(.\type ("n")) transistor_327 (.in(1'b0), .out(_58), .gate(or_1_out));
  Transistor #(.\type ("n")) transistor_328 (.in(1'b0), .out(_58), .gate(not_3_out));
  Transistor #(.\type ("n")) transistor_329 (.in(1'b0), .out(_58), .gate(not_4_out));
  Transistor #(.\type ("n")) transistor_330 (.in(1'b0), .out(_58), .gate(not_5_out));
  Transistor #(.\type ("n")) transistor_331 (.in(1'b0), .out(_58), .gate(IR2));
  Transistor #(.\type ("n")) transistor_332 (.in(1'b0), .out(_58), .gate(IR6));
  Transistor #(.\type ("n")) transistor_333 (.in(1'b0), .out(_58), .gate(IR5));
  Transistor #(.\type ("n")) transistor_334 (.in(1'b0), .out(_58), .gate(nT0));
  Pull_Resistor #(.pull(1)) pull_resistor_60 (.node(_60));
  Pull_Resistor #(.pull(1)) pull_resistor_61 (.node(_59));
  Transistor #(.\type ("n")) transistor_335 (.in(1'b0), .out(_60), .gate(not_2_out));
  Transistor #(.\type ("n")) transistor_336 (.in(1'b0), .out(_59), .gate(not_2_out));
  Transistor #(.\type ("n")) transistor_337 (.in(1'b0), .out(_59), .gate(IR7));
  Transistor #(.\type ("n")) transistor_338 (.in(1'b0), .out(_60), .gate(not_7_out));
  Transistor #(.\type ("n")) transistor_339 (.in(1'b0), .out(_60), .gate(not_8_out));
  Transistor #(.\type ("n")) transistor_340 (.in(1'b0), .out(_59), .gate(nT1X));
  Transistor #(.\type ("n")) transistor_341 (.in(1'b0), .out(_60), .gate(nT1X));
  Pull_Resistor #(.pull(1)) pull_resistor_62 (.node(_61));
  Transistor #(.\type ("n")) transistor_342 (.in(1'b0), .out(_61), .gate(not_1_out));
  Transistor #(.\type ("n")) transistor_343 (.in(1'b0), .out(_61), .gate(IR7));
  Transistor #(.\type ("n")) transistor_344 (.in(1'b0), .out(_61), .gate(IR4));
  Transistor #(.\type ("n")) transistor_345 (.in(1'b0), .out(_61), .gate(IR2));
  Transistor #(.\type ("n")) transistor_346 (.in(1'b0), .out(_61), .gate(nT1X));
  Pull_Resistor #(.pull(1)) pull_resistor_63 (.node(_62));
  Transistor #(.\type ("n")) transistor_347 (.in(1'b0), .out(_62), .gate(not_1_out));
  Transistor #(.\type ("n")) transistor_348 (.in(1'b0), .out(_62), .gate(not_3_out));
  Transistor #(.\type ("n")) transistor_349 (.in(1'b0), .out(_62), .gate(IR4));
  Transistor #(.\type ("n")) transistor_350 (.in(1'b0), .out(_62), .gate(not_5_out));
  Transistor #(.\type ("n")) transistor_351 (.in(1'b0), .out(_62), .gate(IR2));
  Transistor #(.\type ("n")) transistor_352 (.in(1'b0), .out(_62), .gate(IR6));
  Transistor #(.\type ("n")) transistor_353 (.in(1'b0), .out(_62), .gate(IR5));
  Transistor #(.\type ("n")) transistor_354 (.in(1'b0), .out(_62), .gate(nT0));
  Pull_Resistor #(.pull(1)) pull_resistor_64 (.node(_63));
  Pull_Resistor #(.pull(1)) pull_resistor_65 (.node(_64));
  Transistor #(.\type ("n")) transistor_355 (.in(1'b0), .out(_63), .gate(or_1_out));
  Transistor #(.\type ("n")) transistor_356 (.in(1'b0), .out(_64), .gate(not_2_out));
  Transistor #(.\type ("n")) transistor_357 (.in(1'b0), .out(_63), .gate(IR7));
  Transistor #(.\type ("n")) transistor_358 (.in(1'b0), .out(_64), .gate(not_3_out));
  Transistor #(.\type ("n")) transistor_359 (.in(1'b0), .out(_63), .gate(IR4));
  Transistor #(.\type ("n")) transistor_360 (.in(1'b0), .out(_63), .gate(not_5_out));
  Transistor #(.\type ("n")) transistor_361 (.in(1'b0), .out(_63), .gate(IR2));
  Transistor #(.\type ("n")) transistor_362 (.in(1'b0), .out(_64), .gate(IR6));
  Transistor #(.\type ("n")) transistor_363 (.in(1'b0), .out(_63), .gate(not_7_out));
  Transistor #(.\type ("n")) transistor_364 (.in(1'b0), .out(_63), .gate(not_8_out));
  Transistor #(.\type ("n")) transistor_365 (.in(1'b0), .out(_64), .gate(not_8_out));
  Transistor #(.\type ("n")) transistor_366 (.in(1'b0), .out(_64), .gate(nT0));
  Transistor #(.\type ("n")) transistor_367 (.in(1'b0), .out(_63), .gate(nT0));
  Pull_Resistor #(.pull(1)) pull_resistor_66 (.node(_65));
  Transistor #(.\type ("n")) transistor_368 (.in(1'b0), .out(_65), .gate(not_2_out));
  Transistor #(.\type ("n")) transistor_369 (.in(1'b0), .out(_65), .gate(nT0));
  Pull_Resistor #(.pull(1)) pull_resistor_67 (.node(_66));
  Transistor #(.\type ("n")) transistor_370 (.in(1'b0), .out(_66), .gate(or_1_out));
  Transistor #(.\type ("n")) transistor_371 (.in(1'b0), .out(_66), .gate(not_3_out));
  Transistor #(.\type ("n")) transistor_372 (.in(1'b0), .out(_66), .gate(IR4));
  Transistor #(.\type ("n")) transistor_373 (.in(1'b0), .out(_66), .gate(not_5_out));
  Transistor #(.\type ("n")) transistor_374 (.in(1'b0), .out(_66), .gate(IR2));
  Transistor #(.\type ("n")) transistor_375 (.in(1'b0), .out(_66), .gate(IR6));
  Transistor #(.\type ("n")) transistor_376 (.in(1'b0), .out(_66), .gate(not_8_out));
  Transistor #(.\type ("n")) transistor_377 (.in(1'b0), .out(_66), .gate(nT0));
  Pull_Resistor #(.pull(1)) pull_resistor_68 (.node(_67));
  Pull_Resistor #(.pull(1)) pull_resistor_69 (.node(_68));
  Transistor #(.\type ("n")) transistor_378 (.in(1'b0), .out(_67), .gate(not_1_out));
  Transistor #(.\type ("n")) transistor_379 (.in(1'b0), .out(_68), .gate(not_1_out));
  Transistor #(.\type ("n")) transistor_380 (.in(1'b0), .out(_67), .gate(IR7));
  Transistor #(.\type ("n")) transistor_381 (.in(1'b0), .out(_68), .gate(not_3_out));
  Transistor #(.\type ("n")) transistor_382 (.in(1'b0), .out(_67), .gate(IR4));
  Transistor #(.\type ("n")) transistor_383 (.in(1'b0), .out(_68), .gate(IR4));
  Transistor #(.\type ("n")) transistor_384 (.in(1'b0), .out(_68), .gate(not_5_out));
  Transistor #(.\type ("n")) transistor_385 (.in(1'b0), .out(_67), .gate(not_5_out));
  Transistor #(.\type ("n")) transistor_386 (.in(1'b0), .out(_68), .gate(IR2));
  Transistor #(.\type ("n")) transistor_387 (.in(1'b0), .out(_67), .gate(IR2));
  Transistor #(.\type ("n")) transistor_388 (.in(1'b0), .out(_68), .gate(IR6));
  Transistor #(.\type ("n")) transistor_389 (.in(1'b0), .out(_68), .gate(not_8_out));
  Transistor #(.\type ("n")) transistor_390 (.in(1'b0), .out(_67), .gate(nT0));
  Transistor #(.\type ("n")) transistor_391 (.in(1'b0), .out(_68), .gate(nT0));
  Pull_Resistor #(.pull(1)) pull_resistor_70 (.node(_69));
  Transistor #(.\type ("n")) transistor_392 (.in(1'b0), .out(_69), .gate(or_1_out));
  Transistor #(.\type ("n")) transistor_393 (.in(1'b0), .out(_69), .gate(IR7));
  Transistor #(.\type ("n")) transistor_394 (.in(1'b0), .out(_69), .gate(IR4));
  Transistor #(.\type ("n")) transistor_395 (.in(1'b0), .out(_69), .gate(not_6_out));
  Transistor #(.\type ("n")) transistor_396 (.in(1'b0), .out(_69), .gate(IR6));
  Transistor #(.\type ("n")) transistor_397 (.in(1'b0), .out(_69), .gate(not_8_out));
  Transistor #(.\type ("n")) transistor_398 (.in(1'b0), .out(_69), .gate(nT0));
  Pull_Resistor #(.pull(1)) pull_resistor_71 (.node(_70));
  Transistor #(.\type ("n")) transistor_399 (.in(1'b0), .out(_70), .gate(not_2_out));
  Transistor #(.\type ("n")) transistor_400 (.in(1'b0), .out(_70), .gate(IR7));
  Transistor #(.\type ("n")) transistor_401 (.in(1'b0), .out(_70), .gate(IR6));
  Transistor #(.\type ("n")) transistor_402 (.in(1'b0), .out(_70), .gate(not_8_out));
  Transistor #(.\type ("n")) transistor_403 (.in(1'b0), .out(_70), .gate(nT0));
  Pull_Resistor #(.pull(1)) pull_resistor_72 (.node(_71));
  Pull_Resistor #(.pull(1)) pull_resistor_73 (.node(_72));
  Transistor #(.\type ("n")) transistor_404 (.in(1'b0), .out(_72), .gate(nT5));
  Transistor #(.\type ("n")) transistor_405 (.in(1'b0), .out(_71), .gate(nT4));
  Transistor #(.\type ("n")) transistor_406 (.in(1'b0), .out(_72), .gate(not_2_out));
  Transistor #(.\type ("n")) transistor_407 (.in(1'b0), .out(_72), .gate(not_4_out));
  Transistor #(.\type ("n")) transistor_408 (.in(1'b0), .out(_71), .gate(not_4_out));
  Transistor #(.\type ("n")) transistor_409 (.in(1'b0), .out(_72), .gate(IR3));
  Transistor #(.\type ("n")) transistor_410 (.in(1'b0), .out(_71), .gate(not_5_out));
  Transistor #(.\type ("n")) transistor_411 (.in(1'b0), .out(_72), .gate(IR2));
  Pull_Resistor #(.pull(1)) pull_resistor_74 (.node(_73));
  Transistor #(.\type ("n")) transistor_412 (.in(1'b0), .out(_73), .gate(or_1_out));
  Transistor #(.\type ("n")) transistor_413 (.in(1'b0), .out(_73), .gate(not_4_out));
  Transistor #(.\type ("n")) transistor_414 (.in(1'b0), .out(_73), .gate(IR3));
  Transistor #(.\type ("n")) transistor_415 (.in(1'b0), .out(_73), .gate(IR2));
  Transistor #(.\type ("n")) transistor_416 (.in(1'b0), .out(_73), .gate(nT0));
  Pull_Resistor #(.pull(1)) pull_resistor_75 (.node(_75));
  Pull_Resistor #(.pull(1)) pull_resistor_76 (.node(_74));
  Transistor #(.\type ("n")) transistor_417 (.in(1'b0), .out(_74), .gate(nT2));
  Transistor #(.\type ("n")) transistor_418 (.in(1'b0), .out(_75), .gate(not_1_out));
  Transistor #(.\type ("n")) transistor_419 (.in(1'b0), .out(_74), .gate(or_1_out));
  Transistor #(.\type ("n")) transistor_420 (.in(1'b0), .out(_75), .gate(IR7));
  Transistor #(.\type ("n")) transistor_421 (.in(1'b0), .out(_74), .gate(IR7));
  Transistor #(.\type ("n")) transistor_422 (.in(1'b0), .out(_74), .gate(IR4));
  Transistor #(.\type ("n")) transistor_423 (.in(1'b0), .out(_75), .gate(IR4));
  Transistor #(.\type ("n")) transistor_424 (.in(1'b0), .out(_74), .gate(not_5_out));
  Transistor #(.\type ("n")) transistor_425 (.in(1'b0), .out(_75), .gate(not_5_out));
  Transistor #(.\type ("n")) transistor_426 (.in(1'b0), .out(_74), .gate(IR2));
  Transistor #(.\type ("n")) transistor_427 (.in(1'b0), .out(_75), .gate(IR2));
  Transistor #(.\type ("n")) transistor_428 (.in(1'b0), .out(_74), .gate(not_7_out));
  Transistor #(.\type ("n")) transistor_429 (.in(1'b0), .out(_75), .gate(not_7_out));
  Transistor #(.\type ("n")) transistor_430 (.in(1'b0), .out(_74), .gate(IR5));
  Transistor #(.\type ("n")) transistor_431 (.in(1'b0), .out(_75), .gate(nT0));
  Pull_Resistor #(.pull(1)) pull_resistor_77 (.node(_76));
  Transistor #(.\type ("n")) transistor_432 (.in(1'b0), .out(_76), .gate(not_1_out));
  Transistor #(.\type ("n")) transistor_433 (.in(1'b0), .out(_76), .gate(IR7));
  Transistor #(.\type ("n")) transistor_434 (.in(1'b0), .out(_76), .gate(not_7_out));
  Pull_Resistor #(.pull(1)) pull_resistor_78 (.node(_77));
  Transistor #(.\type ("n")) transistor_435 (.in(1'b0), .out(_77), .gate(nT2));
  Transistor #(.\type ("n")) transistor_436 (.in(1'b0), .out(_77), .gate(or_1_out));
  Transistor #(.\type ("n")) transistor_437 (.in(1'b0), .out(_77), .gate(IR7));
  Transistor #(.\type ("n")) transistor_438 (.in(1'b0), .out(_77), .gate(IR4));
  Transistor #(.\type ("n")) transistor_439 (.in(1'b0), .out(_77), .gate(IR3));
  Transistor #(.\type ("n")) transistor_440 (.in(1'b0), .out(_77), .gate(IR2));
  Transistor #(.\type ("n")) transistor_441 (.in(1'b0), .out(_77), .gate(IR6));
  Transistor #(.\type ("n")) transistor_442 (.in(1'b0), .out(_77), .gate(IR5));
  Pull_Resistor #(.pull(1)) pull_resistor_79 (.node(_78));
  Pull_Resistor #(.pull(1)) pull_resistor_80 (.node(_79));
  Transistor #(.\type ("n")) transistor_443 (.in(1'b0), .out(_78), .gate(nT3));
  Transistor #(.\type ("n")) transistor_444 (.in(1'b0), .out(_78), .gate(or_1_out));
  Transistor #(.\type ("n")) transistor_445 (.in(1'b0), .out(_79), .gate(not_2_out));
  Transistor #(.\type ("n")) transistor_446 (.in(1'b0), .out(_78), .gate(IR7));
  Transistor #(.\type ("n")) transistor_447 (.in(1'b0), .out(_79), .gate(not_3_out));
  Transistor #(.\type ("n")) transistor_448 (.in(1'b0), .out(_78), .gate(IR4));
  Transistor #(.\type ("n")) transistor_449 (.in(1'b0), .out(_78), .gate(IR3));
  Transistor #(.\type ("n")) transistor_450 (.in(1'b0), .out(_78), .gate(IR2));
  Transistor #(.\type ("n")) transistor_451 (.in(1'b0), .out(_78), .gate(IR6));
  Transistor #(.\type ("n")) transistor_452 (.in(1'b0), .out(_79), .gate(IR6));
  Transistor #(.\type ("n")) transistor_453 (.in(1'b0), .out(_79), .gate(IR5));
  Transistor #(.\type ("n")) transistor_454 (.in(1'b0), .out(_78), .gate(not_8_out));
  Pull_Resistor #(.pull(1)) pull_resistor_81 (.node(_80));
  Transistor #(.\type ("n")) transistor_455 (.in(1'b0), .out(_80), .gate(nT2));
  Transistor #(.\type ("n")) transistor_456 (.in(1'b0), .out(_80), .gate(or_1_out));
  Transistor #(.\type ("n")) transistor_457 (.in(1'b0), .out(_80), .gate(not_4_out));
  Transistor #(.\type ("n")) transistor_458 (.in(1'b0), .out(_80), .gate(IR3));
  Transistor #(.\type ("n")) transistor_459 (.in(1'b0), .out(_80), .gate(IR2));
  Pull_Resistor #(.pull(1)) pull_resistor_82 (.node(_81));
  Transistor #(.\type ("n")) transistor_460 (.in(1'b0), .out(_81), .gate(nT2));
  Transistor #(.\type ("n")) transistor_461 (.in(1'b0), .out(_81), .gate(IR3));
  Transistor #(.\type ("n")) transistor_462 (.in(1'b0), .out(_81), .gate(not_6_out));
  Pull_Resistor #(.pull(1)) pull_resistor_83 (.node(_83));
  Pull_Resistor #(.pull(1)) pull_resistor_84 (.node(_82));
  Transistor #(.\type ("n")) transistor_463 (.in(1'b0), .out(_83), .gate(nT2));
  Transistor #(.\type ("n")) transistor_464 (.in(1'b0), .out(_82), .gate(nT2));
  Transistor #(.\type ("n")) transistor_465 (.in(1'b0), .out(_82), .gate(not_2_out));
  Transistor #(.\type ("n")) transistor_466 (.in(1'b0), .out(_82), .gate(IR3));
  Transistor #(.\type ("n")) transistor_467 (.in(1'b0), .out(_83), .gate(not_5_out));
  Transistor #(.\type ("n")) transistor_468 (.in(1'b0), .out(_82), .gate(IR2));
  Pull_Resistor #(.pull(1)) pull_resistor_85 (.node(_84));
  Transistor #(.\type ("n")) transistor_469 (.in(1'b0), .out(_84), .gate(nT5));
  Transistor #(.\type ("n")) transistor_470 (.in(1'b0), .out(_84), .gate(or_1_out));
  Transistor #(.\type ("n")) transistor_471 (.in(1'b0), .out(_84), .gate(IR7));
  Transistor #(.\type ("n")) transistor_472 (.in(1'b0), .out(_84), .gate(IR4));
  Transistor #(.\type ("n")) transistor_473 (.in(1'b0), .out(_84), .gate(IR3));
  Transistor #(.\type ("n")) transistor_474 (.in(1'b0), .out(_84), .gate(IR2));
  Transistor #(.\type ("n")) transistor_475 (.in(1'b0), .out(_84), .gate(not_7_out));
  Transistor #(.\type ("n")) transistor_476 (.in(1'b0), .out(_84), .gate(not_8_out));
  Pull_Resistor #(.pull(1)) pull_resistor_86 (.node(_85));
  Transistor #(.\type ("n")) transistor_477 (.in(1'b0), .out(_85), .gate(nT4));
  Pull_Resistor #(.pull(1)) pull_resistor_87 (.node(_87));
  Pull_Resistor #(.pull(1)) pull_resistor_88 (.node(_86));
  Transistor #(.\type ("n")) transistor_478 (.in(1'b0), .out(_86), .gate(nT3));
  Transistor #(.\type ("n")) transistor_479 (.in(1'b0), .out(_87), .gate(or_1_out));
  Transistor #(.\type ("n")) transistor_480 (.in(1'b0), .out(_87), .gate(IR7));
  Transistor #(.\type ("n")) transistor_481 (.in(1'b0), .out(_87), .gate(IR4));
  Transistor #(.\type ("n")) transistor_482 (.in(1'b0), .out(_87), .gate(IR3));
  Transistor #(.\type ("n")) transistor_483 (.in(1'b0), .out(_87), .gate(IR2));
  Transistor #(.\type ("n")) transistor_484 (.in(1'b0), .out(_87), .gate(IR5));
  Transistor #(.\type ("n")) transistor_485 (.in(1'b0), .out(_87), .gate(nT0));
  Pull_Resistor #(.pull(1)) pull_resistor_89 (.node(_88));
  Transistor #(.\type ("n")) transistor_486 (.in(1'b0), .out(_88), .gate(or_1_out));
  Transistor #(.\type ("n")) transistor_487 (.in(1'b0), .out(_88), .gate(IR7));
  Transistor #(.\type ("n")) transistor_488 (.in(1'b0), .out(_88), .gate(IR4));
  Transistor #(.\type ("n")) transistor_489 (.in(1'b0), .out(_88), .gate(not_5_out));
  Transistor #(.\type ("n")) transistor_490 (.in(1'b0), .out(_88), .gate(not_6_out));
  Transistor #(.\type ("n")) transistor_491 (.in(1'b0), .out(_88), .gate(not_7_out));
  Transistor #(.\type ("n")) transistor_492 (.in(1'b0), .out(_88), .gate(nT0));
  Pull_Resistor #(.pull(1)) pull_resistor_90 (.node(_89));
  Transistor #(.\type ("n")) transistor_493 (.in(1'b0), .out(_89), .gate(nT5));
  Transistor #(.\type ("n")) transistor_494 (.in(1'b0), .out(_89), .gate(not_2_out));
  Transistor #(.\type ("n")) transistor_495 (.in(1'b0), .out(_89), .gate(IR4));
  Transistor #(.\type ("n")) transistor_496 (.in(1'b0), .out(_89), .gate(IR3));
  Transistor #(.\type ("n")) transistor_497 (.in(1'b0), .out(_89), .gate(IR2));
  Pull_Resistor #(.pull(1)) pull_resistor_91 (.node(_90));
  Transistor #(.\type ("n")) transistor_498 (.in(1'b0), .out(_90), .gate(nT3));
  Transistor #(.\type ("n")) transistor_499 (.in(1'b0), .out(_90), .gate(not_5_out));
  Pull_Resistor #(.pull(1)) pull_resistor_92 (.node(_91));
  Transistor #(.\type ("n")) transistor_500 (.in(1'b0), .out(_91), .gate(nT4));
  Transistor #(.\type ("n")) transistor_501 (.in(1'b0), .out(_91), .gate(not_2_out));
  Transistor #(.\type ("n")) transistor_502 (.in(1'b0), .out(_91), .gate(not_4_out));
  Transistor #(.\type ("n")) transistor_503 (.in(1'b0), .out(_91), .gate(IR3));
  Transistor #(.\type ("n")) transistor_504 (.in(1'b0), .out(_91), .gate(IR2));
  Pull_Resistor #(.pull(1)) pull_resistor_93 (.node(_92));
  Transistor #(.\type ("n")) transistor_505 (.in(1'b0), .out(_92), .gate(nT3));
  Transistor #(.\type ("n")) transistor_506 (.in(1'b0), .out(_92), .gate(not_4_out));
  Transistor #(.\type ("n")) transistor_507 (.in(1'b0), .out(_92), .gate(not_5_out));
  Pull_Resistor #(.pull(1)) pull_resistor_94 (.node(_94));
  Pull_Resistor #(.pull(1)) pull_resistor_95 (.node(_93));
  Transistor #(.\type ("n")) transistor_508 (.in(1'b0), .out(_93), .gate(nT3));
  Transistor #(.\type ("n")) transistor_509 (.in(1'b0), .out(_93), .gate(or_1_out));
  Transistor #(.\type ("n")) transistor_510 (.in(1'b0), .out(_94), .gate(or_1_out));
  Transistor #(.\type ("n")) transistor_511 (.in(1'b0), .out(_94), .gate(IR7));
  Transistor #(.\type ("n")) transistor_512 (.in(1'b0), .out(_94), .gate(IR4));
  Transistor #(.\type ("n")) transistor_513 (.in(1'b0), .out(_93), .gate(not_4_out));
  Transistor #(.\type ("n")) transistor_514 (.in(1'b0), .out(_93), .gate(IR3));
  Transistor #(.\type ("n")) transistor_515 (.in(1'b0), .out(_94), .gate(IR3));
  Transistor #(.\type ("n")) transistor_516 (.in(1'b0), .out(_94), .gate(IR2));
  Transistor #(.\type ("n")) transistor_517 (.in(1'b0), .out(_93), .gate(IR2));
  Transistor #(.\type ("n")) transistor_518 (.in(1'b0), .out(_94), .gate(IR5));
  Pull_Resistor #(.pull(1)) pull_resistor_96 (.node(_95));
  Transistor #(.\type ("n")) transistor_519 (.in(1'b0), .out(_95), .gate(or_1_out));
  Transistor #(.\type ("n")) transistor_520 (.in(1'b0), .out(_95), .gate(IR7));
  Transistor #(.\type ("n")) transistor_521 (.in(1'b0), .out(_95), .gate(IR4));
  Transistor #(.\type ("n")) transistor_522 (.in(1'b0), .out(_95), .gate(IR3));
  Transistor #(.\type ("n")) transistor_523 (.in(1'b0), .out(_95), .gate(IR2));
  Transistor #(.\type ("n")) transistor_524 (.in(1'b0), .out(_95), .gate(IR6));
  Transistor #(.\type ("n")) transistor_525 (.in(1'b0), .out(_95), .gate(not_8_out));
  Pull_Resistor #(.pull(1)) pull_resistor_97 (.node(_96));
  Transistor #(.\type ("n")) transistor_526 (.in(1'b0), .out(_96), .gate(or_1_out));
  Transistor #(.\type ("n")) transistor_527 (.in(1'b0), .out(_96), .gate(IR7));
  Transistor #(.\type ("n")) transistor_528 (.in(1'b0), .out(_96), .gate(IR4));
  Transistor #(.\type ("n")) transistor_529 (.in(1'b0), .out(_96), .gate(not_5_out));
  Transistor #(.\type ("n")) transistor_530 (.in(1'b0), .out(_96), .gate(not_6_out));
  Transistor #(.\type ("n")) transistor_531 (.in(1'b0), .out(_96), .gate(not_7_out));
  Pull_Resistor #(.pull(1)) pull_resistor_98 (.node(_97));
  Transistor #(.\type ("n")) transistor_532 (.in(1'b0), .out(_97), .gate(not_3_out));
  Transistor #(.\type ("n")) transistor_533 (.in(1'b0), .out(_97), .gate(IR6));
  Transistor #(.\type ("n")) transistor_534 (.in(1'b0), .out(_97), .gate(IR5));
  Pull_Resistor #(.pull(1)) pull_resistor_99 (.node(_98));
  Transistor #(.\type ("n")) transistor_535 (.in(1'b0), .out(_98), .gate(nT4));
  Transistor #(.\type ("n")) transistor_536 (.in(1'b0), .out(_98), .gate(or_1_out));
  Transistor #(.\type ("n")) transistor_537 (.in(1'b0), .out(_98), .gate(IR7));
  Transistor #(.\type ("n")) transistor_538 (.in(1'b0), .out(_98), .gate(IR4));
  Transistor #(.\type ("n")) transistor_539 (.in(1'b0), .out(_98), .gate(IR3));
  Transistor #(.\type ("n")) transistor_540 (.in(1'b0), .out(_98), .gate(IR2));
  Transistor #(.\type ("n")) transistor_541 (.in(1'b0), .out(_98), .gate(IR6));
  Transistor #(.\type ("n")) transistor_542 (.in(1'b0), .out(_98), .gate(IR5));
  Pull_Resistor #(.pull(1)) pull_resistor_100 (.node(_99));
  Pull_Resistor #(.pull(1)) pull_resistor_101 (.node(_100));
  Transistor #(.\type ("n")) transistor_543 (.in(1'b0), .out(_100), .gate(nT2));
  Transistor #(.\type ("n")) transistor_544 (.in(1'b0), .out(_99), .gate(nT2));
  Transistor #(.\type ("n")) transistor_545 (.in(1'b0), .out(_100), .gate(or_1_out));
  Transistor #(.\type ("n")) transistor_546 (.in(1'b0), .out(_99), .gate(or_1_out));
  Transistor #(.\type ("n")) transistor_547 (.in(1'b0), .out(_99), .gate(IR7));
  Transistor #(.\type ("n")) transistor_548 (.in(1'b0), .out(_100), .gate(IR7));
  Transistor #(.\type ("n")) transistor_549 (.in(1'b0), .out(_100), .gate(IR4));
  Transistor #(.\type ("n")) transistor_550 (.in(1'b0), .out(_99), .gate(IR4));
  Transistor #(.\type ("n")) transistor_551 (.in(1'b0), .out(_99), .gate(not_5_out));
  Transistor #(.\type ("n")) transistor_552 (.in(1'b0), .out(_100), .gate(not_5_out));
  Transistor #(.\type ("n")) transistor_553 (.in(1'b0), .out(_100), .gate(IR2));
  Transistor #(.\type ("n")) transistor_554 (.in(1'b0), .out(_99), .gate(IR2));
  Transistor #(.\type ("n")) transistor_555 (.in(1'b0), .out(_99), .gate(IR6));
  Transistor #(.\type ("n")) transistor_556 (.in(1'b0), .out(_99), .gate(IR5));
  Transistor #(.\type ("n")) transistor_557 (.in(1'b0), .out(_100), .gate(IR5));
  Pull_Resistor #(.pull(1)) pull_resistor_102 (.node(_101));
  Transistor #(.\type ("n")) transistor_558 (.in(1'b0), .out(_101), .gate(nT4));
  Transistor #(.\type ("n")) transistor_559 (.in(1'b0), .out(_101), .gate(or_1_out));
  Transistor #(.\type ("n")) transistor_560 (.in(1'b0), .out(_101), .gate(IR7));
  Transistor #(.\type ("n")) transistor_561 (.in(1'b0), .out(_101), .gate(IR4));
  Transistor #(.\type ("n")) transistor_562 (.in(1'b0), .out(_101), .gate(not_5_out));
  Transistor #(.\type ("n")) transistor_563 (.in(1'b0), .out(_101), .gate(not_6_out));
  Transistor #(.\type ("n")) transistor_564 (.in(1'b0), .out(_101), .gate(not_7_out));
  Pull_Resistor #(.pull(1)) pull_resistor_103 (.node(_102));
  Transistor #(.\type ("n")) transistor_565 (.in(1'b0), .out(_102), .gate(nT5));
  Transistor #(.\type ("n")) transistor_566 (.in(1'b0), .out(_102), .gate(or_1_out));
  Transistor #(.\type ("n")) transistor_567 (.in(1'b0), .out(_102), .gate(IR7));
  Transistor #(.\type ("n")) transistor_568 (.in(1'b0), .out(_102), .gate(IR4));
  Transistor #(.\type ("n")) transistor_569 (.in(1'b0), .out(_102), .gate(IR3));
  Transistor #(.\type ("n")) transistor_570 (.in(1'b0), .out(_102), .gate(IR2));
  Transistor #(.\type ("n")) transistor_571 (.in(1'b0), .out(_102), .gate(not_7_out));
  Pull_Resistor #(.pull(1)) pull_resistor_104 (.node(_103));
  Transistor #(.\type ("n")) transistor_572 (.in(1'b0), .out(_103), .gate(nT5));
  Transistor #(.\type ("n")) transistor_573 (.in(1'b0), .out(_103), .gate(or_1_out));
  Transistor #(.\type ("n")) transistor_574 (.in(1'b0), .out(_103), .gate(IR7));
  Transistor #(.\type ("n")) transistor_575 (.in(1'b0), .out(_103), .gate(IR4));
  Transistor #(.\type ("n")) transistor_576 (.in(1'b0), .out(_103), .gate(IR3));
  Transistor #(.\type ("n")) transistor_577 (.in(1'b0), .out(_103), .gate(IR2));
  Transistor #(.\type ("n")) transistor_578 (.in(1'b0), .out(_103), .gate(IR6));
  Transistor #(.\type ("n")) transistor_579 (.in(1'b0), .out(_103), .gate(not_8_out));
  Pull_Resistor #(.pull(1)) pull_resistor_105 (.node(_105));
  Pull_Resistor #(.pull(1)) pull_resistor_106 (.node(_104));
  Transistor #(.\type ("n")) transistor_580 (.in(1'b0), .out(_105), .gate(nT3));
  Transistor #(.\type ("n")) transistor_581 (.in(1'b0), .out(_104), .gate(nT2));
  Transistor #(.\type ("n")) transistor_582 (.in(1'b0), .out(_105), .gate(or_1_out));
  Transistor #(.\type ("n")) transistor_583 (.in(1'b0), .out(_104), .gate(or_1_out));
  Transistor #(.\type ("n")) transistor_584 (.in(1'b0), .out(_105), .gate(IR7));
  Transistor #(.\type ("n")) transistor_585 (.in(1'b0), .out(_104), .gate(IR7));
  Transistor #(.\type ("n")) transistor_586 (.in(1'b0), .out(_104), .gate(IR4));
  Transistor #(.\type ("n")) transistor_587 (.in(1'b0), .out(_105), .gate(IR4));
  Transistor #(.\type ("n")) transistor_588 (.in(1'b0), .out(_105), .gate(not_5_out));
  Transistor #(.\type ("n")) transistor_589 (.in(1'b0), .out(_104), .gate(not_5_out));
  Transistor #(.\type ("n")) transistor_590 (.in(1'b0), .out(_105), .gate(IR2));
  Transistor #(.\type ("n")) transistor_591 (.in(1'b0), .out(_104), .gate(not_6_out));
  Transistor #(.\type ("n")) transistor_592 (.in(1'b0), .out(_104), .gate(not_7_out));
  Transistor #(.\type ("n")) transistor_593 (.in(1'b0), .out(_104), .gate(IR5));
  Transistor #(.\type ("n")) transistor_594 (.in(1'b0), .out(_105), .gate(not_8_out));
  Pull_Resistor #(.pull(1)) pull_resistor_107 (.node(_106));
  Transistor #(.\type ("n")) transistor_595 (.in(1'b0), .out(_106), .gate(not_1_out));
  Transistor #(.\type ("n")) transistor_596 (.in(1'b0), .out(_106), .gate(not_7_out));
  Pull_Resistor #(.pull(1)) pull_resistor_108 (.node(_107));
  Transistor #(.\type ("n")) transistor_597 (.in(1'b0), .out(_107), .gate(not_1_out));
  Transistor #(.\type ("n")) transistor_598 (.in(1'b0), .out(_107), .gate(IR7));
  Transistor #(.\type ("n")) transistor_599 (.in(1'b0), .out(_107), .gate(IR6));
  Pull_Resistor #(.pull(1)) pull_resistor_109 (.node(_108));
  Transistor #(.\type ("n")) transistor_600 (.in(1'b0), .out(_108), .gate(or_1_out));
  Transistor #(.\type ("n")) transistor_601 (.in(1'b0), .out(_108), .gate(IR7));
  Transistor #(.\type ("n")) transistor_602 (.in(1'b0), .out(_108), .gate(not_4_out));
  Transistor #(.\type ("n")) transistor_603 (.in(1'b0), .out(_108), .gate(IR2));
  Transistor #(.\type ("n")) transistor_604 (.in(1'b0), .out(_108), .gate(not_7_out));
  Transistor #(.\type ("n")) transistor_605 (.in(1'b0), .out(_108), .gate(nT0));
  Pull_Resistor #(.pull(1)) pull_resistor_110 (.node(_109));
  Transistor #(.\type ("n")) transistor_606 (.in(1'b0), .out(_109), .gate(or_1_out));
  Transistor #(.\type ("n")) transistor_607 (.in(1'b0), .out(_109), .gate(IR7));
  Transistor #(.\type ("n")) transistor_608 (.in(1'b0), .out(_109), .gate(IR4));
  Transistor #(.\type ("n")) transistor_609 (.in(1'b0), .out(_109), .gate(not_6_out));
  Transistor #(.\type ("n")) transistor_610 (.in(1'b0), .out(_109), .gate(IR6));
  Transistor #(.\type ("n")) transistor_611 (.in(1'b0), .out(_109), .gate(not_8_out));
  Transistor #(.\type ("n")) transistor_612 (.in(1'b0), .out(_109), .gate(nT1X));
  Pull_Resistor #(.pull(1)) pull_resistor_111 (.node(_110));
  Pull_Resistor #(.pull(1)) pull_resistor_112 (.node(_111));
  Transistor #(.\type ("n")) transistor_613 (.in(1'b0), .out(_111), .gate(nT3));
  Transistor #(.\type ("n")) transistor_614 (.in(1'b0), .out(_110), .gate(or_1_out));
  Transistor #(.\type ("n")) transistor_615 (.in(1'b0), .out(_110), .gate(IR7));
  Transistor #(.\type ("n")) transistor_616 (.in(1'b0), .out(_111), .gate(not_4_out));
  Transistor #(.\type ("n")) transistor_617 (.in(1'b0), .out(_110), .gate(not_4_out));
  Transistor #(.\type ("n")) transistor_618 (.in(1'b0), .out(_111), .gate(IR3));
  Transistor #(.\type ("n")) transistor_619 (.in(1'b0), .out(_110), .gate(not_5_out));
  Transistor #(.\type ("n")) transistor_620 (.in(1'b0), .out(_110), .gate(IR2));
  Transistor #(.\type ("n")) transistor_621 (.in(1'b0), .out(_111), .gate(not_6_out));
  Transistor #(.\type ("n")) transistor_622 (.in(1'b0), .out(_110), .gate(IR6));
  Transistor #(.\type ("n")) transistor_623 (.in(1'b0), .out(_110), .gate(nT0));
  Pull_Resistor #(.pull(1)) pull_resistor_113 (.node(_112));
  Transistor #(.\type ("n")) transistor_624 (.in(1'b0), .out(_112), .gate(not_2_out));
  Transistor #(.\type ("n")) transistor_625 (.in(1'b0), .out(_112), .gate(not_7_out));
  Transistor #(.\type ("n")) transistor_626 (.in(1'b0), .out(_112), .gate(not_8_out));
  Transistor #(.\type ("n")) transistor_627 (.in(1'b0), .out(_112), .gate(nT1X));
  Pull_Resistor #(.pull(1)) pull_resistor_114 (.node(_113));
  Transistor #(.\type ("n")) transistor_628 (.in(1'b0), .out(_113), .gate(or_1_out));
  Transistor #(.\type ("n")) transistor_629 (.in(1'b0), .out(_113), .gate(IR7));
  Transistor #(.\type ("n")) transistor_630 (.in(1'b0), .out(_113), .gate(IR4));
  Transistor #(.\type ("n")) transistor_631 (.in(1'b0), .out(_113), .gate(not_6_out));
  Transistor #(.\type ("n")) transistor_632 (.in(1'b0), .out(_113), .gate(IR6));
  Transistor #(.\type ("n")) transistor_633 (.in(1'b0), .out(_113), .gate(not_8_out));
  Transistor #(.\type ("n")) transistor_634 (.in(1'b0), .out(_113), .gate(nT0));
  Pull_Resistor #(.pull(1)) pull_resistor_115 (.node(_114));
  Pull_Resistor #(.pull(1)) pull_resistor_116 (.node(_115));
  Transistor #(.\type ("n")) transistor_635 (.in(1'b0), .out(_115), .gate(nT4));
  Transistor #(.\type ("n")) transistor_636 (.in(1'b0), .out(_115), .gate(or_1_out));
  Transistor #(.\type ("n")) transistor_637 (.in(1'b0), .out(_114), .gate(or_1_out));
  Transistor #(.\type ("n")) transistor_638 (.in(1'b0), .out(_114), .gate(IR7));
  Transistor #(.\type ("n")) transistor_639 (.in(1'b0), .out(_115), .gate(IR7));
  Transistor #(.\type ("n")) transistor_640 (.in(1'b0), .out(_114), .gate(IR4));
  Transistor #(.\type ("n")) transistor_641 (.in(1'b0), .out(_115), .gate(IR4));
  Transistor #(.\type ("n")) transistor_642 (.in(1'b0), .out(_115), .gate(IR3));
  Transistor #(.\type ("n")) transistor_643 (.in(1'b0), .out(_114), .gate(not_5_out));
  Transistor #(.\type ("n")) transistor_644 (.in(1'b0), .out(_114), .gate(IR2));
  Transistor #(.\type ("n")) transistor_645 (.in(1'b0), .out(_115), .gate(IR2));
  Transistor #(.\type ("n")) transistor_646 (.in(1'b0), .out(_114), .gate(IR6));
  Transistor #(.\type ("n")) transistor_647 (.in(1'b0), .out(_115), .gate(not_7_out));
  Transistor #(.\type ("n")) transistor_648 (.in(1'b0), .out(_115), .gate(IR5));
  Transistor #(.\type ("n")) transistor_649 (.in(1'b0), .out(_114), .gate(not_8_out));
  Transistor #(.\type ("n")) transistor_650 (.in(1'b0), .out(_114), .gate(nT0));
  Pull_Resistor #(.pull(1)) pull_resistor_117 (.node(_116));
  Transistor #(.\type ("n")) transistor_651 (.in(1'b0), .out(_116), .gate(not_2_out));
  Transistor #(.\type ("n")) transistor_652 (.in(1'b0), .out(_116), .gate(not_3_out));
  Transistor #(.\type ("n")) transistor_653 (.in(1'b0), .out(_116), .gate(not_7_out));
  Transistor #(.\type ("n")) transistor_654 (.in(1'b0), .out(_116), .gate(IR5));
  Transistor #(.\type ("n")) transistor_655 (.in(1'b0), .out(_116), .gate(nT1X));
  Pull_Resistor #(.pull(1)) pull_resistor_118 (.node(_117));
  Transistor #(.\type ("n")) transistor_656 (.in(1'b0), .out(_117), .gate(or_1_out));
  Transistor #(.\type ("n")) transistor_657 (.in(1'b0), .out(_117), .gate(not_3_out));
  Transistor #(.\type ("n")) transistor_658 (.in(1'b0), .out(_117), .gate(IR4));
  Transistor #(.\type ("n")) transistor_659 (.in(1'b0), .out(_117), .gate(not_5_out));
  Transistor #(.\type ("n")) transistor_660 (.in(1'b0), .out(_117), .gate(not_6_out));
  Transistor #(.\type ("n")) transistor_661 (.in(1'b0), .out(_117), .gate(not_7_out));
  Transistor #(.\type ("n")) transistor_662 (.in(1'b0), .out(_117), .gate(nT1X));
  Pull_Resistor #(.pull(1)) pull_resistor_119 (.node(_119));
  Pull_Resistor #(.pull(1)) pull_resistor_120 (.node(_118));
  Transistor #(.\type ("n")) transistor_663 (.in(1'b0), .out(_118), .gate(not_1_out));
  Transistor #(.\type ("n")) transistor_664 (.in(1'b0), .out(_119), .gate(or_1_out));
  Transistor #(.\type ("n")) transistor_665 (.in(1'b0), .out(_118), .gate(IR7));
  Transistor #(.\type ("n")) transistor_666 (.in(1'b0), .out(_119), .gate(not_3_out));
  Transistor #(.\type ("n")) transistor_667 (.in(1'b0), .out(_118), .gate(IR4));
  Transistor #(.\type ("n")) transistor_668 (.in(1'b0), .out(_119), .gate(IR4));
  Transistor #(.\type ("n")) transistor_669 (.in(1'b0), .out(_119), .gate(IR3));
  Transistor #(.\type ("n")) transistor_670 (.in(1'b0), .out(_118), .gate(not_5_out));
  Transistor #(.\type ("n")) transistor_671 (.in(1'b0), .out(_118), .gate(IR2));
  Transistor #(.\type ("n")) transistor_672 (.in(1'b0), .out(_118), .gate(IR6));
  Transistor #(.\type ("n")) transistor_673 (.in(1'b0), .out(_119), .gate(not_7_out));
  Transistor #(.\type ("n")) transistor_674 (.in(1'b0), .out(_118), .gate(nT1X));
  Transistor #(.\type ("n")) transistor_675 (.in(1'b0), .out(_119), .gate(nT1X));
  Pull_Resistor #(.pull(1)) pull_resistor_121 (.node(_121));
  Pull_Resistor #(.pull(1)) pull_resistor_122 (.node(_120));
  Transistor #(.\type ("n")) transistor_676 (.in(1'b0), .out(_120), .gate(or_1_out));
  Transistor #(.\type ("n")) transistor_677 (.in(1'b0), .out(_120), .gate(not_3_out));
  Transistor #(.\type ("n")) transistor_678 (.in(1'b0), .out(_120), .gate(not_4_out));
  Transistor #(.\type ("n")) transistor_679 (.in(1'b0), .out(_120), .gate(not_5_out));
  Transistor #(.\type ("n")) transistor_680 (.in(1'b0), .out(_120), .gate(IR2));
  Transistor #(.\type ("n")) transistor_681 (.in(1'b0), .out(_121), .gate(IR6));
  Transistor #(.\type ("n")) transistor_682 (.in(1'b0), .out(_120), .gate(not_7_out));
  Transistor #(.\type ("n")) transistor_683 (.in(1'b0), .out(_120), .gate(nT0));
  Pull_Resistor #(.pull(1)) pull_resistor_123 (.node(_122));
  Transistor #(.\type ("n")) transistor_684 (.in(1'b0), .out(_122), .gate(nT3));
  Transistor #(.\type ("n")) transistor_685 (.in(1'b0), .out(_122), .gate(IR4));
  Transistor #(.\type ("n")) transistor_686 (.in(1'b0), .out(_122), .gate(not_5_out));
  Transistor #(.\type ("n")) transistor_687 (.in(1'b0), .out(_122), .gate(not_6_out));
  Pull_Resistor #(.pull(1)) pull_resistor_124 (.node(_123));
  Transistor #(.\type ("n")) transistor_688 (.in(1'b0), .out(_123), .gate(nT2));
  Transistor #(.\type ("n")) transistor_689 (.in(1'b0), .out(_123), .gate(IR4));
  Transistor #(.\type ("n")) transistor_690 (.in(1'b0), .out(_123), .gate(IR3));
  Transistor #(.\type ("n")) transistor_691 (.in(1'b0), .out(_123), .gate(not_6_out));
  Pull_Resistor #(.pull(1)) pull_resistor_125 (.node(_124));
  Pull_Resistor #(.pull(1)) pull_resistor_126 (.node(_125));
  Transistor #(.\type ("n")) transistor_692 (.in(1'b0), .out(_124), .gate(nT5));
  Transistor #(.\type ("n")) transistor_693 (.in(1'b0), .out(_125), .gate(nT4));
  Transistor #(.\type ("n")) transistor_694 (.in(1'b0), .out(_124), .gate(not_2_out));
  Transistor #(.\type ("n")) transistor_695 (.in(1'b0), .out(_125), .gate(not_4_out));
  Transistor #(.\type ("n")) transistor_696 (.in(1'b0), .out(_124), .gate(IR3));
  Transistor #(.\type ("n")) transistor_697 (.in(1'b0), .out(_125), .gate(not_5_out));
  Transistor #(.\type ("n")) transistor_698 (.in(1'b0), .out(_124), .gate(IR2));
  Pull_Resistor #(.pull(1)) pull_resistor_127 (.node(_126));
  Transistor #(.\type ("n")) transistor_699 (.in(1'b0), .out(_126), .gate(IR7));
  Pull_Resistor #(.pull(1)) pull_resistor_128 (.node(_127));
  Transistor #(.\type ("n")) transistor_700 (.in(1'b0), .out(_127), .gate(or_1_out));
  Transistor #(.\type ("n")) transistor_701 (.in(1'b0), .out(_127), .gate(not_3_out));
  Transistor #(.\type ("n")) transistor_702 (.in(1'b0), .out(_127), .gate(not_4_out));
  Transistor #(.\type ("n")) transistor_703 (.in(1'b0), .out(_127), .gate(not_5_out));
  Transistor #(.\type ("n")) transistor_704 (.in(1'b0), .out(_127), .gate(IR2));
  Transistor #(.\type ("n")) transistor_705 (.in(1'b0), .out(_127), .gate(IR6));
  Transistor #(.\type ("n")) transistor_706 (.in(1'b0), .out(_127), .gate(not_8_out));
  Pull_Resistor #(.pull(1)) pull_resistor_129 (.node(_128));
  Pull_Resistor #(.pull(1)) pull_resistor_130 (.node(_129));
  Transistor #(.\type ("n")) transistor_707 (.in(1'b0), .out(_128), .gate(IR0));
  Transistor #(.\type ("n")) transistor_708 (.in(1'b0), .out(_129), .gate(or_1_out));
  Transistor #(.\type ("n")) transistor_709 (.in(1'b0), .out(_129), .gate(IR7));
  Transistor #(.\type ("n")) transistor_710 (.in(1'b0), .out(_129), .gate(IR4));
  Transistor #(.\type ("n")) transistor_711 (.in(1'b0), .out(_128), .gate(not_5_out));
  Transistor #(.\type ("n")) transistor_712 (.in(1'b0), .out(_129), .gate(not_5_out));
  Transistor #(.\type ("n")) transistor_713 (.in(1'b0), .out(_129), .gate(IR2));
  Transistor #(.\type ("n")) transistor_714 (.in(1'b0), .out(_128), .gate(IR2));

  // Notes on the sheet:
  //   TODO: Move IR0 to random logic
endmodule

module PREDECODE (
  input  PHI2,
  input  _0_IR,
  input  D0,
  input  D1,
  input  D2,
  input  D3,
  input  D4,
  input  D5,
  input  D6,
  input  D7,
  output nIMPLIED,
  output nTWOCYCLE,
  output nPD0,
  output nPD1,
  output nPD2,
  output nPD3,
  output nPD4,
  output nPD5,
  output nPD6,
  output nPD7
);

  wire and1_out, and2_out, and3_out, and4_out, and5_out, and6_out, and7_out, and8_out, d_latch_1_not_q,
       d_latch_2_not_q, d_latch_3_not_q, d_latch_4_not_q, d_latch_5_not_q, d_latch_6_not_q, d_latch_7_not_q,
       d_latch_8_not_q, nand1_out, nor1_out, nor2_out, nor3_out, nor4_out, nor5_out, not_1_out, not_2_out,
       not_3_out, not_4_out, not_5_out, not_6_out, not_7_out, not_8_out, not_9_out, not_10_out, not_11_out,
       not_12_out, not_13_out, not_22_out;

  not not_1 (not_1_out, D0);
  not not_2 (not_2_out, D1);
  not not_3 (not_3_out, D2);
  not not_4 (not_4_out, D3);
  not not_5 (not_5_out, D4);
  not not_6 (not_6_out, D5);
  not not_7 (not_7_out, D6);
  not not_8 (not_8_out, D7);
  not not_9 (not_9_out, _0_IR);
  D_latch d_latch_1 (.EN(PHI2), .D(not_1_out), .NOT_Q(d_latch_1_not_q));  // open: Q
  D_latch d_latch_2 (.EN(PHI2), .D(not_2_out), .NOT_Q(d_latch_2_not_q));  // open: Q
  D_latch d_latch_3 (.EN(PHI2), .D(not_3_out), .NOT_Q(d_latch_3_not_q));  // open: Q
  D_latch d_latch_4 (.EN(PHI2), .D(not_4_out), .NOT_Q(d_latch_4_not_q));  // open: Q
  D_latch d_latch_5 (.EN(PHI2), .D(not_5_out), .NOT_Q(d_latch_5_not_q));  // open: Q
  D_latch d_latch_6 (.EN(PHI2), .D(not_6_out), .NOT_Q(d_latch_6_not_q));  // open: Q
  D_latch d_latch_7 (.EN(PHI2), .D(not_7_out), .NOT_Q(d_latch_7_not_q));  // open: Q
  D_latch d_latch_8 (.EN(PHI2), .D(not_8_out), .NOT_Q(d_latch_8_not_q));  // open: Q
  and and1 (and1_out, d_latch_1_not_q, not_9_out);
  and and2 (and2_out, d_latch_2_not_q, not_9_out);
  and and3 (and3_out, d_latch_3_not_q, not_9_out);
  and and4 (and4_out, d_latch_4_not_q, not_9_out);
  and and5 (and5_out, d_latch_5_not_q, not_9_out);
  and and6 (and6_out, d_latch_6_not_q, not_9_out);
  and and7 (and7_out, d_latch_7_not_q, not_9_out);
  and and8 (and8_out, d_latch_8_not_q, not_9_out);
  not not_10 (not_10_out, and4_out);
  nor nor1 (nor1_out, and1_out, and3_out, not_10_out);
  nor nor2 (nor2_out, and2_out, and5_out, and8_out);
  not not_11 (not_11_out, and1_out);
  not not_12 (not_12_out, and4_out);
  nor nor3 (nor3_out, not_11_out, and3_out, not_12_out, and5_out);
  not not_13 (not_13_out, and8_out);
  nor nor4 (nor4_out, and1_out, and3_out, and4_out, and5_out, not_13_out);
  not not_14 (nPD0, and1_out);
  not not_15 (nPD1, and2_out);
  not not_16 (nPD2, and3_out);
  not not_17 (nPD3, and4_out);
  not not_18 (nPD4, and5_out);
  not not_19 (nPD5, and6_out);
  not not_20 (nPD6, and7_out);
  not not_21 (nPD7, and8_out);
  nand nand1 (nand1_out, nor1_out, not_22_out);
  not not_22 (not_22_out, nor2_out);
  nor nor5 (nor5_out, nor3_out, nor4_out);
  not not_23 (nIMPLIED, nor1_out);
  and and9 (nTWOCYCLE, nand1_out, nor5_out);
endmodule

// BUS CONTROL
module RANDOM_LOGIC (
  input  X0,
  input  X1,
  input  X2,
  input  X3,
  input  X4,
  input  X5,
  input  X6,
  input  X7,
  input  X8,
  input  X9,
  input  X10,
  input  X11,
  input  X12,
  input  X13,
  input  X14,
  input  X15,
  input  X16,
  input  X17,
  input  X18,
  input  X19,
  input  X20,
  input  X21,
  input  X22,
  input  X23,
  input  X24,
  input  X25,
  input  X26,
  input  X27,
  input  X28,
  input  X29,
  input  X30,
  input  X31,
  input  X32,
  input  X33,
  input  X34,
  input  X35,
  input  X36,
  input  X37,
  input  X38,
  input  X39,
  input  X40,
  input  X41,
  input  X42,
  input  X43,
  input  X44,
  input  X45,
  input  X46,
  input  X47,
  input  X48,
  input  X49,
  input  X50,
  input  X51,
  input  X52,
  input  X53,
  input  X54,
  input  X55,
  input  X56,
  input  X57,
  input  X58,
  input  X59,
  input  X60,
  input  X61,
  input  X62,
  input  X63,
  input  X64,
  input  X65,
  input  X66,
  input  X67,
  input  X68,
  input  X69,
  input  X70,
  input  X71,
  input  X72,
  input  X73,
  input  X74,
  input  X75,
  input  X76,
  input  X77,
  input  X78,
  input  X79,
  input  X80,
  input  X81,
  input  X82,
  input  X83,
  input  X84,
  input  X85,
  input  X86,
  input  X87,
  input  X88,
  input  X89,
  input  X90,
  input  X91,
  input  X92,
  input  X93,
  input  X94,
  input  X95,
  input  X96,
  input  X97,
  input  X98,
  input  X99,
  input  X100,
  input  X101,
  input  X102,
  input  X103,
  input  X104,
  input  X105,
  input  X106,
  input  X107,
  input  X108,
  input  X109,
  input  X110,
  input  X111,
  input  X112,
  input  X113,
  input  X114,
  input  X115,
  input  X116,
  input  X117,
  input  X118,
  input  X119,
  input  X120,
  input  X121,
  input  X122,
  input  X123,
  input  X124,
  input  X125,
  input  X126,
  input  X127,
  input  X128,
  input  X129,
  input  PHI1,
  input  PHI2,
  input  nNMIP,
  input  nTWOCYCLE,
  input  RESP,
  input  nIMPLIED,
  input  nIRQP,
  input  SV,
  input  RDY,
  input  ACR,
  input  AVR,
  input  DB7,
  input  DB6,
  input  DB5,
  input  DB4,
  input  DB3,
  input  DB2,
  input  DB1,
  input  DB0,
  output WR,
  output T1,
  output nT1X,
  output FETCH,
  output nT2,
  output _0_IR,
  output nT3,
  output nT0,
  output nT4,
  output nT5,
  output ADH_ABH,
  output ADL_ABL,
  output Y_SB,
  output X_SB,
  output _0_ADL0,
  output _0_ADL1,
  output _0_ADL2,
  output SB_Y,
  output SB_X,
  output S_SB,
  output S_ADL,
  output SB_S,
  output S_S,
  output SBXY,
  output NDB_ADD,
  output DB_ADD,
  output _0_ADD,
  output SB_ADD,
  output ADL_ADD,
  output ANDS,
  output EORS,
  output ORS,
  output nACIN,
  output SRS,
  output SUMS,
  output nDAA,
  output ADD_SB7,
  output ADD_SB06,
  output ADD_ADL,
  output nDSA
);

  wire alu_setup_1_p3, alu_setup_1_p4, alu_setup_1_p5, alu_setup_1_p6, alu_setup_1_p8, alu_setup_1_p9,
       alu_setup_1_p10, alu_setup_1_p11, dispath_1_stor, INTERRUPT_RESET_CONTROL_brk7,
       INTERRUPT_RESET_CONTROL_dores, INTERRUPT_RESET_CONTROL_ndonmi, pc_setup_1_adl_pcl, pc_setup_1_dl_adh,
       pc_setup_1_pc_db, pc_setup_1_pch_adh, pc_setup_1_pch_db, pc_setup_1_pcl_adl, pc_setup_1_pcl_db,
       pc_setup_1_pcl_pcl, undriven, undriven_2, undriven_3, xys_control_1_stkop, xys_control_1_stxy;

  INT_RESET_CONTROL INTERRUPT_RESET_CONTROL (
    .PHI1(PHI1), .PHI2(PHI2), .BRK5(X22), .NMIP(nNMIP), .RESP(RESP), .BRK7(INTERRUPT_RESET_CONTROL_brk7),
    .nDONMI(INTERRUPT_RESET_CONTROL_ndonmi), .DORES(INTERRUPT_RESET_CONTROL_dores));  // open: nready, BRK6E
  EXTENDED_CYCLE_COUNTER extended_cycle_counter_1 (
    .T1(undriven), .nT2(nT2), .nT3(nT3), .nT4(nT4), .PHI1(PHI1), .nREADY(alu_setup_1_p3), .nT5(nT5),
    .PHI2(PHI2));  // open: TRES2
  INT_VECTOR INTERRUPT_VECTOR (
    .PHI2(PHI2), .BRK5(X22), .BRK7(INTERRUPT_RESET_CONTROL_brk7), .DORES(INTERRUPT_RESET_CONTROL_dores),
    .nDONMI(INTERRUPT_RESET_CONTROL_ndonmi), ._0_ADL0(_0_ADL0), ._0_ADL1(_0_ADL1), ._0_ADL2(_0_ADL2));
  XYS_CONTROL xys_control_1 (
    .nready(alu_setup_1_p3), .PHI1(PHI1), .STOR(dispath_1_stor), .Y_SB(Y_SB), .X_SB(X_SB), .S_ADL(S_ADL),
    .SB_S(SB_S), .S_S(S_S), .STXY(xys_control_1_stxy), .SBXY(SBXY), .STKOP(xys_control_1_stkop), ._0(X0),
    ._1(X1), ._2(X2), ._3(X3), ._4(X4), ._5(X5), ._6(X6), ._7(X7), ._8(X8), ._9(X9), ._10(X10), ._11(X11),
    ._12(X12), ._13(X13), ._14(X14), ._15(X15), ._16(X16), ._17(X17), ._18(X18), ._19(X19), ._20(X20),
    ._21(X21), ._22(X22), ._23(X23), ._24(X24), ._25(X25), ._26(X26), ._48(X48), .SB_X(SB_X), .SB_Y(SB_Y),
    .S_SB(S_SB), .PHI2(PHI2));  // open: STK2
  // ALU_SETUP alu_setup_1: pin names not known; wires that end beside it: PHI1, PHI2, alu_setup_1_p3, alu_setup_1_p4, alu_setup_1_p5, alu_setup_1_p6, xys_control_1_stkop, alu_setup_1_p8, alu_setup_1_p9, alu_setup_1_p10, alu_setup_1_p11, X93, X27, X28, X29, NDB_ADD, X30, X31, DB_ADD, X32, X33, _0_ADD, X34, X35, SB_ADD, X36, X37, ADL_ADD, X38, X39, ANDS, X40, X41, EORS, X42, X43, ORS, X44, X45, nACIN, X46, X47, SRS, X48, X49, SUMS, X50, X51, nDAA, X52, X53, ADD_SB7, X54, ADD_SB06, X56, ADD_ADL, X58, X59, nDSA, X60, X61, X62, X63, X64
  BUS_CONTROL bus_control_1 (
    .D58(X58), .D59(X59), .D60(X60), .D61(X61), .D62(X62), .D63(X63), .D64(X64), .D65(X65), .D66(X66),
    .D67(X67), .D68(X68), .D69(X69), .D70(X70), .D71(X71), .D72(X72), .D73(X73), .D74(X74), .D79(X79),
    .D81(X81), .D82(X82), .D89(X89), .D90(X90), .D91(X91), .SB_AC(alu_setup_1_p11), ._0_ADH17(alu_setup_1_p10));  // open: PHI1, PHI2, DL_ADH, DL_DB, DL_ADL, BR2, SB_ADH, ADH_ABH, ADL_ABL, AC_SB, D57, AC_DB, SB_DB, RDY, BR3, nREADY, T2
  PC_SETUP pc_setup_1 (
    .BR0(undriven_2), .PHI1(PHI1), .PHI2(PHI2), .D56(X56), .D77(X77), .D78(X78), .D83(X83), .D84(X84),
    .D94(X94), .D95(X95), .D96(X96), .nREADY(alu_setup_1_p3), .BR3(X93), .BR2(X80),
    .PCL_DB(pc_setup_1_pcl_db), .PCH_DB(pc_setup_1_pch_db), .PC_DB(pc_setup_1_pc_db),
    .PCL_ADL(pc_setup_1_pcl_adl), .PCH_ADH(pc_setup_1_pch_adh), .PCL_PCL(pc_setup_1_pcl_pcl),
    .ADL_PCL(pc_setup_1_adl_pcl), .DL_ADH(pc_setup_1_dl_adh));  // open: Push_pull, T0, T1, IND
  DISPATH dispath_1 (
    .PHI1(PHI1), .PHI2(PHI2), .BR2(X80), .D91(X91), .D92(X92), .D106(X106), .D107(X107), .D111(X111),
    .D122(X122), .D123(X123), .D124(X124), .D125(X125), .nTWOCYCLE(nTWOCYCLE), .RDY(RDY),
    .T5(alu_setup_1_p10), .T6(alu_setup_1_p11), ._0_IR(_0_IR), .FETCH(FETCH), .nT0(nT0),
    .nREADY(alu_setup_1_p3), .D97(X97), .D98(X98), .D100(X100), .BR3(X93), .D96(X96), .STOR(dispath_1_stor),
    .D101(X101), .D102(X102), .D103(X103), .D104(X104), .D105(X105), .nIMPLED(nIMPLIED));  // open: BRK6E, RESP, ACR, B_OUT, nBRTAKEN, TRESX, ENDS, ENDX, SYNC, TRES1, nT0X, nT1X, RD, R_W, _1_PC, DORES, PC_DB, BRFW, nADL_PCL
  BRANCH_LOGIC BRANCH_LOGIC (
    .nIR5(undriven_3), .D126(X126), .PHI1(PHI1), .PHI2(PHI2), .BR2(X80), .D121(X121));  // open: nC_OUT, nV_OUT, nN_OUT, nZ_OUT, ACR, nBRTAKEN, BRFW

  // Other names for the same wires on the sheet: BR2 = X80; BR3 = X93

  // Notes on the sheet:
  //   PHI1
  //   PHI2
  //   TODO (T1 != /T1X)
  //   BRK5
  //   BRK5
  //   PHI1
  //   BRK5
  //   PHI1
  //   PHI2
endmodule

module D_latch (
  input  EN,
  input  D,
  output Q,
  output NOT_Q
);

  D_Flip_Flop #(.trigger("high")) d_ff_1 (.clk(EN), .D(D), .Q(Q), .Qn(NOT_Q));  // open: preset, en, reset
endmodule

module NMI_FF (
  input  nNMI,
  input  PHI2,
  output NMIP
);

  wire and_1_out, and_2_out, nor_1_out, nor_2_out, not_1_out;

  not not_1 (not_1_out, nNMI);
  and and_1 (and_1_out, not_1_out, PHI2);
  nor nor_1 (nor_1_out, and_2_out, nor_2_out);
  and and_2 (and_2_out, nNMI, PHI2);
  nor nor_2 (nor_2_out, nor_1_out, and_1_out);
  not not_2 (NMIP, nor_2_out);
endmodule

module INT_RESET_CONTROL (
  input  PHI1,
  input  PHI2,
  input  nready,
  input  BRK5,
  input  NMIP,
  input  RESP,
  output BRK6E,
  output BRK7,
  output nDONMI,
  output DORES
);
endmodule

module INT_VECTOR (
  input  PHI2,
  input  BRK5,
  input  BRK7,
  input  DORES,
  input  nDONMI,
  output _0_ADL0,
  output _0_ADL1,
  output _0_ADL2
);

  wire nor_1_out, nor_2_out, not_1_out, not_2_out, not_3_out;

  not not_1 (not_1_out, DORES);
  not not_2 (not_2_out, BRK5);
  nor nor_1 (nor_1_out, BRK7, not_1_out);
  not not_3 (not_3_out, nor_1_out);
  nor nor_2 (nor_2_out, BRK7, nDONMI, DORES);
  D_latch d_latch_1 (.EN(PHI2), .D(not_2_out), .NOT_Q(_0_ADL0));  // open: Q
  D_latch d_latch_2 (.EN(PHI2), .D(not_3_out), .NOT_Q(_0_ADL1));  // open: Q
  D_latch d_latch_3 (.EN(PHI2), .D(nor_2_out), .Q(_0_ADL2));  // open: NOT_Q

  // Notes on the sheet:
  //   FFFA:NMI, 1010
  //   FFFC:RESET, 1100
  //   FFFE:IRQ/BRK, 1110
endmodule

module XYS_CONTROL (
  input  PHI1,
  input  PHI2,
  input  STOR,
  input  _0,
  input  _1,
  input  _2,
  input  _3,
  input  _4,
  input  _5,
  input  _6,
  input  _7,
  input  _8,
  input  _9,
  input  _10,
  input  _11,
  input  _12,
  input  _13,
  input  _14,
  input  _15,
  input  _16,
  input  _17,
  input  _18,
  input  _19,
  input  _20,
  input  _21,
  input  _22,
  input  _23,
  input  _24,
  input  _25,
  input  _26,
  input  _48,
  input  nready,
  input  STK2,
  output Y_SB,
  output STXY,
  output X_SB,
  output S_SB,
  output SB_X,
  output SBXY,
  output SB_Y,
  output SB_S,
  output S_S,
  output STKOP,
  output S_ADL
);

  wire and_1_out, and_2_out, and_4_out, buffer_1_out, buffer_2_out, buffer_3_out, buffer_4_out, buffer_5_out,
       buffer_6_out, buffer_7_out, buffer_8_out, d_latch_1_q, d_latch_2_not_q, d_latch_3_not_q,
       d_latch_4_not_q, d_latch_5_not_q, d_latch_6_not_q, d_latch_7_not_q, d_latch_8_not_q, d_latch_9_not_q,
       nand_1_out, nand_2_out, nand_3_out, nand_4_out, nand_5_out, nand_6_out, nand_7_out, nor_1_out,
       nor_2_out, nor_3_out, nor_4_out, nor_5_out, nor_6_out, nor_8_out, not_1_out, not_2_out, not_3_out,
       not_4_out, not_5_out, not_6_out;

  nor nor_1 (nor_1_out, _14, _15, _16);
  not not_1 (not_1_out, _17);
  nor nor_2 (nor_2_out, _18, _19, _20);
  nor nor_3 (nor_3_out, _21, _22, _23, _24, _25, _26);
  nor nor_4 (nor_4_out, _1, _2, _3, _4, _5);
  nor nor_5 (nor_5_out, _8, _9, _10, _11, _13);
  nand nand_1 (nand_1_out, _0, STOR);
  nand nand_2 (nand_2_out, _6, _7);
  nand nand_3 (nand_3_out, _6, not_2_out);
  not not_2 (not_2_out, _7);
  nand nand_4 (nand_4_out, STOR, _12);
  D_latch d_latch_1 (.EN(PHI2), .D(nready), .Q(d_latch_1_q));  // open: NOT_Q
  not not_3 (not_3_out, _48);
  nor nor_6 (nor_6_out, not_3_out, nready);
  and and_1 (and_1_out, nand_1_out, nor_4_out, nand_2_out);
  and and_2 (and_2_out, nand_3_out, nor_5_out, nand_4_out);
  nor nor_7 (STKOP, nor_3_out, d_latch_1_q);
  not not_4 (not_4_out, d_latch_1_q);
  nand nand_5 (nand_5_out, _0, STOR);
  nand nand_6 (nand_6_out, STOR, _12);
  nand nand_7 (nand_7_out, not_4_out, _21);
  and and_3 (STXY, nand_5_out, nand_6_out);
  nor nor_8 (nor_8_out, _13, STKOP, nor_6_out);
  and and_4 (and_4_out, nand_7_out, not_5_out);
  not not_5 (not_5_out, STK2);
  nand nand_8 (SBXY, nor_1_out, nor_2_out);
  not not_6 (not_6_out, nor_8_out);
  D_latch d_latch_2 (.EN(PHI1), .D(and_1_out), .NOT_Q(d_latch_2_not_q));  // open: Q
  buf buffer_1 (buffer_1_out, d_latch_2_not_q);
  D_latch d_latch_3 (.EN(PHI1), .D(and_2_out), .NOT_Q(d_latch_3_not_q));  // open: Q
  buf buffer_2 (buffer_2_out, d_latch_3_not_q);
  D_latch d_latch_4 (.EN(PHI1), .D(not_1_out), .NOT_Q(d_latch_4_not_q));  // open: Q
  buf buffer_3 (buffer_3_out, d_latch_4_not_q);
  D_latch d_latch_5 (.EN(PHI1), .D(nor_1_out), .NOT_Q(d_latch_5_not_q));  // open: Q
  buf buffer_4 (buffer_4_out, d_latch_5_not_q);
  D_latch d_latch_6 (.EN(PHI1), .D(nor_2_out), .NOT_Q(d_latch_6_not_q));  // open: Q
  buf buffer_5 (buffer_5_out, d_latch_6_not_q);
  D_latch d_latch_7 (.EN(PHI1), .D(nor_8_out), .NOT_Q(d_latch_7_not_q));  // open: Q
  buf buffer_6 (buffer_6_out, d_latch_7_not_q);
  D_latch d_latch_8 (.EN(PHI1), .D(not_6_out), .NOT_Q(d_latch_8_not_q));  // open: Q
  buf buffer_7 (buffer_7_out, d_latch_8_not_q);
  D_latch d_latch_9 (.EN(PHI1), .D(and_4_out), .NOT_Q(d_latch_9_not_q));  // open: Q
  buf buffer_8 (buffer_8_out, d_latch_9_not_q);
  and and_5 (Y_SB, PHI2, buffer_1_out);
  and and_6 (X_SB, PHI2, buffer_2_out);
  and and_7 (S_SB, PHI2, buffer_3_out);
  and and_8 (SB_X, PHI2, buffer_4_out);
  and and_9 (SB_Y, PHI2, buffer_5_out);
  and and_10 (SB_S, PHI2, buffer_6_out);
  and and_11 (S_S, PHI2, buffer_7_out);
  and and_12 (S_ADL, PHI2, buffer_8_out);

  // Notes on the sheet:
  //   JRS2
  //   TXS
  //   #SB/X
  //   #S/SB
  //   #SB/Y
  //   STORE
  //   STORE
  //   #Y/SB
  //   STORE
  //   #X/SB
  //   STKOP
  //   #SB/S
  //   SBXY
endmodule

module ABH (
  input  PHI1,
  input  ADH_ABH,
  input  FROM_ADH0,
  input  FROM_ADH1,
  input  FROM_ADH2,
  input  FROM_ADH3,
  input  FROM_ADH4,
  input  FROM_ADH5,
  input  FROM_ADH6,
  input  FROM_ADH7,
  output A8,
  output A9,
  output A10,
  output A11,
  output A12,
  output A13,
  output A14,
  output A15
);

  wire and_1_out;

  and and_1 (and_1_out, PHI1, ADH_ABH);
  D_Flip_Flop #(.trigger("high")) d_ff_1 (.clk(and_1_out), .D(FROM_ADH0), .Q(A8));  // open: Qn, preset, en, reset
  D_Flip_Flop #(.trigger("high")) d_ff_2 (.clk(and_1_out), .D(FROM_ADH1), .Q(A9));  // open: Qn, preset, en, reset
  D_Flip_Flop #(.trigger("high")) d_ff_3 (.clk(and_1_out), .D(FROM_ADH2), .Q(A10));  // open: Qn, preset, en, reset
  D_Flip_Flop #(.trigger("high")) d_ff_4 (.clk(and_1_out), .D(FROM_ADH3), .Q(A11));  // open: Qn, preset, en, reset
  D_Flip_Flop #(.trigger("high")) d_ff_5 (.clk(and_1_out), .D(FROM_ADH4), .Q(A12));  // open: Qn, preset, en, reset
  D_Flip_Flop #(.trigger("high")) d_ff_6 (.clk(and_1_out), .D(FROM_ADH5), .Q(A13));  // open: Qn, preset, en, reset
  D_Flip_Flop #(.trigger("high")) d_ff_7 (.clk(and_1_out), .D(FROM_ADH6), .Q(A14));  // open: Qn, preset, en, reset
  D_Flip_Flop #(.trigger("high")) d_ff_8 (.clk(and_1_out), .D(FROM_ADH7), .Q(A15));  // open: Qn, preset, en, reset
endmodule
module EXTENDED_CYCLE_COUNTER (
  input  PHI1,
  input  PHI2,
  input  TRES2,
  input  nREADY,
  input  T1,
  output nT2,
  output nT3,
  output nT4,
  output nT5
);

  wire d_latch_1_not_q, d_latch_2_not_q, d_latch_3_q, d_latch_4_not_q, d_latch_5_q, d_latch_6_not_q,
       d_latch_7_q, d_latch_8_not_q, d_latch_9_q, multiplexer_1_out, multiplexer_2_out, multiplexer_3_out,
       multiplexer_4_out, nor_1_out, nor_2_out, nor_3_out, nor_4_out, not_5_out, undriven;

  D_latch d_latch_1 (.EN(PHI2), .D(T1), .NOT_Q(d_latch_1_not_q));  // open: Q
  Multiplexer #(.enable("false")) multiplexer_1 (
    .in0(d_latch_1_not_q), .in1(d_latch_2_not_q), .out(multiplexer_1_out), .sel(nREADY));
  Multiplexer #(.enable("false")) multiplexer_2 (
    .in0(d_latch_2_not_q), .in1(d_latch_4_not_q), .out(multiplexer_2_out), .sel(nREADY));
  Multiplexer #(.enable("false")) multiplexer_3 (
    .in0(d_latch_4_not_q), .in1(d_latch_6_not_q), .out(multiplexer_3_out), .sel(nREADY));
  Multiplexer #(.enable("false")) multiplexer_4 (
    .in0(d_latch_6_not_q), .in1(d_latch_8_not_q), .out(multiplexer_4_out), .sel(nREADY));
  nor nor_1 (nor_1_out, TRES2, d_latch_3_q);
  nor nor_2 (nor_2_out, TRES2, d_latch_5_q);
  nor nor_3 (nor_3_out, TRES2, d_latch_7_q);
  nor nor_4 (nor_4_out, TRES2, d_latch_9_q);
  D_latch d_latch_2 (.EN(PHI2), .D(nor_1_out), .NOT_Q(d_latch_2_not_q));  // open: Q
  D_latch d_latch_3 (.EN(PHI1), .D(multiplexer_1_out), .Q(d_latch_3_q));  // open: NOT_Q
  D_latch d_latch_4 (.EN(PHI2), .D(nor_2_out), .NOT_Q(d_latch_4_not_q));  // open: Q
  D_latch d_latch_5 (.EN(PHI1), .D(multiplexer_2_out), .Q(d_latch_5_q));  // open: NOT_Q
  D_latch d_latch_6 (.EN(PHI2), .D(nor_3_out), .NOT_Q(d_latch_6_not_q));  // open: Q
  D_latch d_latch_7 (.EN(PHI1), .D(multiplexer_3_out), .Q(d_latch_7_q));  // open: NOT_Q
  D_latch d_latch_8 (.EN(PHI2), .D(nor_4_out), .NOT_Q(d_latch_8_not_q));  // open: Q
  D_latch d_latch_9 (.EN(PHI1), .D(multiplexer_4_out), .Q(d_latch_9_q));  // open: NOT_Q
  not not_1 (nT2, nor_1_out);
  not not_2 (nT3, nor_2_out);
  not not_3 (nT4, nor_3_out);
  not not_4 (nT5, nor_4_out);
  not not_5 (not_5_out, undriven);

  // Notes on the sheet:
  //   To test the shift register you must disconnect PHI1 and instead connect PHI2 via an inverter:
  //   PHI2
  //   PHI2
  //   PHI1
endmodule

module ALU_SETUP (
  input  PHI1,
  input  PHI2,
  input  nREADY,
  input  BRK6E,
  input  STKOP,
  input  D27,
  input  D28,
  input  D29,
  input  D30,
  input  D31,
  input  D32,
  input  D33,
  input  D34,
  input  D35,
  input  D36,
  input  D37,
  input  D38,
  input  D39,
  input  D40,
  input  D41,
  input  D42,
  input  D43,
  input  D44,
  input  D45,
  input  D46,
  input  D47,
  input  D48,
  input  D49,
  input  D50,
  input  D51,
  input  D52,
  input  D53,
  input  D54,
  input  D56,
  input  D58,
  input  D59,
  input  D60,
  input  D61,
  input  D62,
  input  D63,
  input  D64,
  input  SRS,
  input  T0,
  input  T1,
  input  T5,
  input  T6,
  input  AND,
  input  PGX,
  input  BR3,
  input  nD_OUT,
  input  nC_OUT,
  input  NOADL,
  output NDB_ADD,
  output DB_ADD,
  output _0_ADD,
  output SB_ADD,
  output ADL_ADD,
  output ANDS,
  output EORS,
  output ORS,
  output nACIN,
  output SRS_2,
  output SUMS,
  output nDAA,
  output ADD_SB7,
  output ADD_SB06,
  output ADD_ADL,
  output nDSA,
  output nSB_AC,
  output DL_DB
);

  wire and_1_out, and_2_out, and_3_out, BRFW, buffer_1_out, buffer_2_out, buffer_3_out, buffer_4_out,
       buffer_5_out, d_latch_1_q, d_latch_2_q, d_latch_3_q, d_latch_4_q, d_latch_5_q, d_latch_6_not_q,
       d_latch_7_q, d_latch_8_q, d_latch_9_not_q, d_latch_10_q, d_latch_11_not_q, d_latch_12_not_q,
       d_latch_13_not_q, d_latch_14_not_q, d_latch_15_not_q, d_latch_16_not_q, d_latch_17_not_q,
       d_latch_18_not_q, d_latch_19_not_q, d_latch_20_not_q, d_latch_21_not_q, d_latch_22_not_q,
       d_latch_23_not_q, d_latch_24_not_q, d_latch_25_not_q, d_latch_26_not_q, d_latch_27_not_q,
       d_latch_28_not_q, d_latch_29_not_q, d_latch_30_not_q, d_latch_31_not_q, d_latch_32_not_q,
       d_latch_33_not_q, nand_1_out, nand_2_out, nand_3_out, nand_4_out, nand_5_out, nand_6_out, nand_7_out,
       nand_8_out, nor_1_out, nor_2_out, nor_4_out, nor_5_out, nor_6_out, nor_7_out, nor_8_out, nor_9_out,
       nor_10_out, nor_11_out, nor_12_out, nor_13_out, nor_14_out, nor_15_out, nor_16_out, nor_17_out,
       nor_18_out, nor_19_out, nor_20_out, nor_21_out, not_1_out, not_2_out, not_3_out, not_4_out, not_5_out,
       not_6_out, not_8_out, not_9_out, not_10_out, not_11_out, not_12_out, not_13_out, not_14_out,
       not_15_out, not_16_out, not_17_out, not_18_out, or_1_out, or_2_out, PHI0;

  nor nor_1 (nor_1_out, D52, D53);
  nor nor_2 (nor_2_out, D39, D40, D41, D42, D43);
  nor nor_3 (nSB_AC, D58, D59, D60, D61, D62, D63, D64);
  not not_1 (not_1_out, D34);
  nor nor_4 (nor_4_out, D35, D36, D37, D38, D39, nREADY);
  not not_2 (not_2_out, BR3);
  nor nor_5 (nor_5_out, not_2_out, BRFW);
  nand nand_1 (nand_1_out, D33, not_1_out);
  and and_1 (and_1_out, nand_1_out, nor_4_out);
  nand nand_2 (nand_2_out, T5, D44);
  not not_3 (not_3_out, nor_6_out);
  nor nor_6 (nor_6_out, D49, D50, nor_5_out);
  nor nor_7 (nor_7_out, T0, T5);
  and and_2 (and_2_out, nor_2_out, nand_2_out);
  not not_4 (not_4_out, and_2_out);
  nor nor_8 (nor_8_out, nor_7_out, nC_OUT);
  not not_5 (not_5_out, nor_8_out);
  or or_1 (or_1_out, not_5_out, nor_1_out);
  not not_6 (not_6_out, D54);
  nor nor_9 (nor_9_out, STKOP, D30, D31, D45, D48, not_4_out, D47, BRK6E, nREADY);
  not not_7 (DL_DB, nor_10_out);
  nor nor_10 (nor_10_out, not_4_out, D45, BRK6E, D46, D47, D48);
  nand nand_3 (nand_3_out, or_1_out, not_6_out);
  nor nor_11 (nor_11_out, and_1_out, not_8_out);
  not not_8 (not_8_out, D47);
  D_latch d_latch_1 (.EN(PHI1), .D(nor_11_out), .Q(d_latch_1_q));  // open: NOT_Q
  D_latch d_latch_2 (.EN(PHI1), .D(not_4_out), .Q(d_latch_2_q));  // open: NOT_Q
  D_latch d_latch_3 (.EN(PHI1), .D(not_3_out), .Q(d_latch_3_q));  // open: NOT_Q
  D_latch d_latch_4 (.EN(PHI1), .D(nand_3_out), .Q(d_latch_4_q));  // open: NOT_Q
  not not_9 (not_9_out, SRS);
  D_latch d_latch_5 (.EN(PHI2), .D(nREADY), .Q(d_latch_5_q));  // open: NOT_Q
  nor nor_12 (nor_12_out, NOADL, PGX);
  nor nor_13 (nor_13_out, D32, nREADY);
  not not_10 (not_10_out, nor_13_out);
  not not_11 (not_11_out, nC_OUT);
  nor nor_14 (nor_14_out, not_9_out, d_latch_5_q);
  nor nor_15 (nor_15_out, d_latch_1_q, d_latch_2_q, d_latch_3_q, d_latch_4_q);
  D_latch d_latch_6 (.EN(PHI1), .D(not_11_out), .NOT_Q(d_latch_6_not_q));  // open: Q
  D_latch d_latch_7 (.EN(PHI1), .D(nor_14_out), .Q(d_latch_7_q));  // open: NOT_Q
  not not_12 (not_12_out, d_latch_7_q);
  D_latch d_latch_8 (.EN(PHI1), .D(d_latch_11_not_q), .Q(d_latch_8_q));  // open: NOT_Q
  not not_13 (not_13_out, nD_OUT);
  not not_14 (not_14_out, nD_OUT);
  nand nand_4 (nand_4_out, d_latch_6_not_q, d_latch_7_q);
  nand nand_5 (nand_5_out, not_12_out, d_latch_8_q);
  nand nand_6 (nand_6_out, not_14_out, D52);
  nor nor_16 (nor_16_out, not_3_out, D56, D51);
  D_latch d_latch_9 (.EN(PHI1), .D(SRS), .NOT_Q(d_latch_9_not_q));  // open: Q
  and and_3 (and_3_out, nand_4_out, nand_5_out);
  nand nand_7 (nand_7_out, D51, not_13_out);
  not not_15 (not_15_out, nor_17_out);
  nor nor_17 (nor_17_out, D51, nand_6_out);
  or or_2 (or_2_out, nor_16_out, nREADY);
  nor nor_18 (nor_18_out, T6, STKOP, PGX, T1, D56);
  D_latch d_latch_10 (.EN(PHI2), .D(d_latch_9_not_q), .Q(d_latch_10_q));  // open: NOT_Q
  not not_16 (not_16_out, D27);
  D_latch d_latch_11 (.EN(PHI2), .D(and_3_out), .NOT_Q(d_latch_11_not_q));  // open: Q
  D_latch d_latch_12 (.EN(PHI0), .D(nand_7_out), .NOT_Q(d_latch_12_not_q));  // open: Q
  D_latch d_latch_13 (.EN(PHI0), .D(not_15_out), .NOT_Q(d_latch_13_not_q));  // open: Q
  nand nand_8 (nand_8_out, or_2_out, and_1_out);
  nor nor_19 (nor_19_out, AND, D29, not_10_out, SRS);
  nor nor_20 (nor_20_out, d_latch_10_q, not_16_out, d_latch_11_not_q);
  nor nor_21 (nor_21_out, nor_20_out, nor_18_out);
  not not_17 (not_17_out, nor_9_out);
  D_latch d_latch_14 (.EN(PHI1), .D(AND), .NOT_Q(d_latch_14_not_q));  // open: Q
  D_latch d_latch_15 (.EN(PHI1), .D(D29), .NOT_Q(d_latch_15_not_q));  // open: Q
  D_latch d_latch_16 (.EN(PHI1), .D(not_10_out), .NOT_Q(d_latch_16_not_q));  // open: Q
  D_latch d_latch_17 (.EN(PHI1), .D(SRS), .NOT_Q(d_latch_17_not_q));  // open: Q
  D_latch d_latch_18 (.EN(PHI1), .D(nor_19_out), .NOT_Q(d_latch_18_not_q));  // open: Q
  not not_18 (not_18_out, nor_12_out);
  D_latch d_latch_19 (.EN(PHI1), .D(or_2_out), .NOT_Q(d_latch_19_not_q));  // open: Q
  D_latch d_latch_20 (.EN(PHI1), .D(nand_8_out), .NOT_Q(d_latch_20_not_q));  // open: Q
  D_latch d_latch_21 (.EN(PHI1), .D(nor_9_out), .NOT_Q(d_latch_21_not_q));  // open: Q
  D_latch d_latch_22 (.EN(PHI1), .D(not_17_out), .NOT_Q(d_latch_22_not_q));  // open: Q
  D_latch d_latch_23 (.EN(PHI1), .D(and_1_out), .NOT_Q(d_latch_23_not_q));  // open: Q
  D_latch d_latch_24 (.EN(PHI2), .D(d_latch_14_not_q), .NOT_Q(d_latch_24_not_q));  // open: Q
  D_latch d_latch_25 (.EN(PHI2), .D(d_latch_15_not_q), .NOT_Q(d_latch_25_not_q));  // open: Q
  D_latch d_latch_26 (.EN(PHI2), .D(d_latch_16_not_q), .NOT_Q(d_latch_26_not_q));  // open: Q
  D_latch d_latch_27 (.EN(PHI2), .D(nor_15_out), .NOT_Q(d_latch_27_not_q));  // open: Q
  D_latch d_latch_28 (.EN(PHI2), .D(d_latch_17_not_q), .NOT_Q(d_latch_28_not_q));  // open: Q
  D_latch d_latch_29 (.EN(PHI2), .D(d_latch_18_not_q), .NOT_Q(d_latch_29_not_q));  // open: Q
  D_latch d_latch_30 (.EN(PHI2), .D(d_latch_12_not_q), .NOT_Q(d_latch_30_not_q));  // open: Q
  D_latch d_latch_31 (.EN(PHI1), .D(nor_21_out), .NOT_Q(d_latch_31_not_q));  // open: Q
  D_latch d_latch_32 (.EN(PHI1), .D(nor_18_out), .NOT_Q(d_latch_32_not_q));  // open: Q
  D_latch d_latch_33 (.EN(PHI1), .D(not_18_out), .NOT_Q(d_latch_33_not_q));  // open: Q
  D_latch d_latch_34 (.EN(PHI2), .D(d_latch_13_not_q), .NOT_Q(nDSA));  // open: Q
  buf buffer_1 (buffer_1_out, d_latch_19_not_q);
  buf buffer_2 (buffer_2_out, d_latch_20_not_q);
  buf buffer_3 (buffer_3_out, d_latch_21_not_q);
  buf buffer_4 (buffer_4_out, d_latch_22_not_q);
  buf buffer_5 (buffer_5_out, d_latch_23_not_q);
  buf buffer_6 (ANDS, d_latch_24_not_q);
  buf buffer_7 (EORS, d_latch_25_not_q);
  buf buffer_8 (ORS, d_latch_26_not_q);
  not not_19 (nACIN, d_latch_27_not_q);
  buf buffer_9 (SRS_2, d_latch_28_not_q);
  buf buffer_10 (SUMS, d_latch_29_not_q);
  buf buffer_11 (nDAA, d_latch_30_not_q);
  buf buffer_12 (ADD_SB7, d_latch_31_not_q);
  buf buffer_13 (ADD_SB06, d_latch_32_not_q);
  buf buffer_14 (ADD_ADL, d_latch_33_not_q);
  and and_4 (NDB_ADD, PHI2, buffer_1_out);
  and and_5 (DB_ADD, PHI2, buffer_2_out);
  and and_6 (_0_ADD, PHI2, buffer_3_out);
  and and_7 (SB_ADD, PHI2, buffer_4_out);
  and and_8 (ADL_ADD, PHI2, buffer_5_out);

  // Other names for the same wires on the sheet: JSR_5 = D56; SBC0 = D51

  // Notes on the sheet:
  //   ROR
  //   T2
  //   EOR
  //   STK2
  //   RET
  //   JSR2
  //   #SB/AC
  //   #ADL/ADD
  //   JSR2
  //   JSR2
  //   INC_SB
  //   BRX
  //   RET
  //   to DL/DB
  //   CSET
  //   CSET
  //   NOADL
  //   PGX
  //   SB/ADD
  //   /ACIN
  //   ROR
  //   #ADL/ABL
  //   ORS
  //   #NDB/ADD
  //   #ADL/ADD
  //   #ADD/SB7
  //   #ADD/SB06
  //   /ACIN
endmodule

module BRANCH_LOGIC (
  input  nIR5,
  input  D121,
  input  D126,
  input  nC_OUT,
  input  nV_OUT,
  input  nN_OUT,
  input  nZ_OUT,
  input  PHI1,
  input  PHI2,
  input  ACR,
  input  BR2,
  output nBRTAKEN,
  output BRFW
);

  wire and_1_out, d_latch_1_q, d_latch_2_q, d_latch_3_not_q, nand_1_out, nand_2_out, nand_3_out, nor_1_out,
       nor_2_out, nor_3_out, nor_4_out, nor_5_out, nor_6_out, not_1_out, not_2_out, not_3_out, not_4_out,
       not_5_out, not_6_out, not_7_out;

  not not_1 (not_1_out, D121);
  not not_2 (not_2_out, D126);
  not not_3 (not_3_out, D126);
  not not_4 (not_4_out, D121);
  D_latch d_latch_1 (.EN(PHI1), .D(BR2), .Q(d_latch_1_q));  // open: NOT_Q
  D_latch d_latch_2 (.EN(PHI1), .D(d_latch_3_not_q), .Q(d_latch_2_q));  // open: NOT_Q
  nor nor_1 (nor_1_out, nC_OUT, D126, not_1_out);
  nor nor_2 (nor_2_out, nV_OUT, D121, not_2_out);
  nor nor_3 (nor_3_out, nN_OUT, not_3_out, not_4_out);
  nor nor_4 (nor_4_out, D126, D121, nZ_OUT);
  not not_5 (not_5_out, ACR);
  not not_6 (not_6_out, d_latch_1_q);
  nor nor_5 (nor_5_out, nor_1_out, nor_2_out, nor_3_out, nor_4_out);
  nand nand_1 (nand_1_out, not_5_out, d_latch_1_q);
  and and_1 (and_1_out, nand_1_out, nand_2_out);
  nand nand_2 (nand_2_out, not_6_out, d_latch_2_q);
  nand nand_3 (nand_3_out, nIR5, nor_5_out);
  nor nor_6 (nor_6_out, nIR5, nor_5_out);
  not not_7 (not_7_out, nor_6_out);
  D_latch d_latch_3 (.EN(PHI2), .D(and_1_out), .NOT_Q(d_latch_3_not_q));  // open: Q
  and and_2 (nBRTAKEN, nand_3_out, not_7_out);
  not not_8 (BRFW, d_latch_3_not_q);

  // Notes on the sheet:
  //   /IR7
endmodule

// PROGRAM COUNTER SETUP
module PC_SETUP (
  input  BR0,
  input  PHI1,
  input  PHI2,
  input  D56,
  input  D77,
  input  D78,
  input  D83,
  input  D84,
  input  D94,
  input  D95,
  input  D96,
  input  Push_pull,
  input  nREADY,
  input  BR3,
  input  BR2,
  input  T0,
  input  T1,
  input  IND,
  output PCL_DB,
  output PCH_DB,
  output PC_DB,
  output PCL_ADL,
  output PCH_ADH,
  output PCL_PCL,
  output ADL_PCL,
  output DL_ADH
);

  wire and_1_out, and_2_out, and_3_out, d_latch_1_q, d_latch_2_q, d_latch_3_not_q, d_latch_4_not_q,
       d_latch_5_not_q, d_latch_6_not_q, d_latch_7_not_q, d_latch_8_not_q, d_latch_9_not_q, d_latch_10_not_q,
       nand_1_out, nor_1_out, nor_2_out, nor_3_out, nor_4_out, nor_5_out, nor_6_out, nor_7_out, nor_8_out,
       nor_9_out, nor_10_out, nor_11_out, nor_12_out, not_1_out, not_2_out, not_3_out, not_4_out;

  nor nor_1 (nor_1_out, D94, D95, D96);
  nor nor_2 (nor_2_out, D77, D78);
  nor nor_3 (nor_3_out, D83, Push_pull);
  D_latch d_latch_1 (.EN(PHI2), .D(nREADY), .Q(d_latch_1_q));  // open: NOT_Q
  D_latch d_latch_2 (.EN(PHI1), .D(nor_2_out), .Q(d_latch_2_q));  // open: NOT_Q
  nor nor_4 (nor_4_out, nor_1_out, d_latch_1_q);
  not not_1 (not_1_out, T0);
  nor nor_5 (nor_5_out, d_latch_2_q, nREADY);
  nor nor_6 (nor_6_out, nor_4_out, not_1_out);
  D_latch d_latch_3 (.EN(PHI2), .D(nor_5_out), .NOT_Q(d_latch_3_not_q));  // open: Q
  not not_2 (not_2_out, nor_9_out);
  not not_3 (not_3_out, d_latch_1_q);
  nor nor_7 (nor_7_out, not_1_out, nor_1_out);
  nor nor_8 (nor_8_out, not_2_out, D84, T0);
  nand nand_1 (nand_1_out, not_3_out, BR3);
  nand nand_2 (PC_DB, d_latch_3_not_q, nor_2_out);
  nor nor_9 (nor_9_out, T1, D56, nor_3_out, nor_6_out, BR2);
  and and_1 (and_1_out, nor_8_out, nand_1_out);
  nor nor_10 (nor_10_out, BR0, nor_9_out, nor_7_out);
  nor nor_11 (nor_11_out, nor_10_out, BR3);
  not not_4 (not_4_out, and_1_out);
  nor nor_12 (nor_12_out, nor_7_out, IND);
  D_latch d_latch_4 (.EN(PHI1), .D(d_latch_3_not_q), .NOT_Q(d_latch_4_not_q));  // open: Q
  D_latch d_latch_5 (.EN(PHI1), .D(nor_2_out), .NOT_Q(d_latch_5_not_q));  // open: Q
  D_latch d_latch_6 (.EN(PHI1), .D(nor_9_out), .NOT_Q(d_latch_6_not_q));  // open: Q
  D_latch d_latch_7 (.EN(PHI1), .D(nor_11_out), .NOT_Q(d_latch_7_not_q));  // open: Q
  D_latch d_latch_8 (.EN(PHI1), .D(not_4_out), .NOT_Q(d_latch_8_not_q));  // open: Q
  D_latch d_latch_9 (.EN(PHI1), .D(and_1_out), .NOT_Q(d_latch_9_not_q));  // open: Q
  D_latch d_latch_10 (.EN(PHI1), .D(nor_12_out), .NOT_Q(d_latch_10_not_q));  // open: Q
  buf buffer_1 (PCL_DB, d_latch_4_not_q);
  buf buffer_2 (PCH_DB, d_latch_5_not_q);
  buf buffer_3 (PCL_ADL, d_latch_6_not_q);
  buf buffer_4 (PCH_ADH, d_latch_7_not_q);
  buf buffer_5 (PCL_PCL, and_2_out);
  and and_2 (and_2_out, d_latch_8_not_q, PHI2);
  buf buffer_6 (ADL_PCL, and_3_out);
  and and_3 (and_3_out, d_latch_9_not_q, PHI2);
  buf buffer_7 (DL_ADH, d_latch_10_not_q);

  // Notes on the sheet:
  //   JRS5
  //   JB
  //   #PCH/DB
  //   ABS/2
  //   DL/PCH
  //   #PCL/DB
  //   PC/DB
  //   #PCL/ADL
  //   #ADL/PCL
  //   DL/PCH
endmodule

module DISPATH (
  input  PHI1,
  input  PHI2,
  input  BRK6E,
  input  BR2,
  input  DORES,
  input  RESP,
  input  ACR,
  input  PC_DB,
  input  D91,
  input  D92,
  input  BR3,
  input  D96,
  input  D97,
  input  D98,
  input  D100,
  input  D101,
  input  D102,
  input  D103,
  input  D104,
  input  D105,
  input  D106,
  input  D107,
  input  D111,
  input  D122,
  input  D123,
  input  D124,
  input  D125,
  input  B_OUT,
  input  BRFW,
  input  RDY,
  input  nBRTAKEN,
  input  nTWOCYCLE,
  input  nADL_PCL,
  input  nIMPLED,
  output T5,
  output T6,
  output TRESX,
  output ENDX,
  output STOR,
  output _0_IR,
  output FETCH,
  output ENDS,
  output nREADY,
  output R_W,
  output RD,
  output SYNC,
  output TRES1,
  output nT0X,
  output nT0,
  output nT1X,
  output _1_PC
);

  wire ACRL1, ACRL2, and_2_out, and_3_out, and_4_out, and_6_out, and_7_out, and_8_out, d_latch_1_not_q,
       d_latch_2_not_q, d_latch_4_q, d_latch_5_q, d_latch_6_q, d_latch_7_q, d_latch_8_q, d_latch_9_q,
       d_latch_10_not_q, d_latch_11_q, d_latch_12_q, d_latch_13_q, d_latch_14_q, d_latch_15_q,
       d_latch_16_not_q, d_latch_17_not_q, d_latch_18_not_q, d_latch_20_q, d_latch_21_q, d_latch_22_q,
       d_latch_24_q, d_latch_25_q, d_latch_26_q, d_latch_27_q, d_latch_28_q, d_latch_29_q, d_latch_31_not_q,
       d_latch_32_not_q, multiplexer_1_out, nand_1_out, nand_2_out, nand_3_out, nand_4_out, nand_5_out,
       nand_6_out, nand_7_out, nMemOP, nor_1_out, nor_3_out, nor_4_out, nor_6_out, nor_7_out, nor_8_out,
       nor_9_out, nor_11_out, nor_12_out, nor_13_out, nor_14_out, nor_15_out, nor_16_out, nor_17_out,
       nor_18_out, nor_19_out, nor_20_out, nor_21_out, nor_23_out, nor_24_out, nor_25_out, nor_27_out,
       nor_29_out, not_1_out, not_2_out, not_3_out, not_4_out, not_5_out, not_6_out, not_7_out, not_8_out,
       not_9_out, not_10_out, not_11_out, not_13_out, not_14_out, not_15_out, not_18_out, NotReadyPhi1,
       nready_t, nSHIFT, or_1_out, PHI0, REST, STOR_t, xnor_1_out;

  nor nor_1 (nor_1_out, D91, D92);
  not not_1 (not_1_out, D97);
  nor nor_2 (nSHIFT, D106, D107);
  nor nor_3 (nor_3_out, BR2, BR3);
  nor nor_4 (nor_4_out, D100, D101, D102, D103, D104, D105);
  nor nor_5 (nMemOP, D111, D122, D123, D124, D125);
  not not_2 (not_2_out, nor_3_out);
  not not_3 (not_3_out, ACR);
  nand nand_1 (nand_1_out, not_3_out, NotReadyPhi1);
  not not_4 (not_4_out, nor_6_out);
  nor nor_6 (nor_6_out, NotReadyPhi1, ACRL1);
  not not_5 (not_5_out, nT0);
  nand nand_2 (nand_2_out, nBRTAKEN, BR2);
  nand nand_3 (nand_3_out, nBRTAKEN, BR2);
  nor nor_7 (nor_7_out, nADL_PCL, not_2_out);
  not not_6 (not_6_out, nor_7_out);
  and and_1 (ACRL2, nand_1_out, not_4_out);
  nor nor_8 (nor_8_out, PC_DB, D98, D100, T5, T6, STOR_t);
  not not_7 (not_7_out, nor_4_out);
  and and_2 (and_2_out, not_5_out, nand_2_out);
  Multiplexer #(.enable("false")) multiplexer_1 (
    .in0(and_2_out), .in1(not_8_out), .out(multiplexer_1_out), .sel(nready_t));
  not not_8 (not_8_out, SYNC);
  not not_9 (not_9_out, BR3);
  D_latch d_latch_1 (.EN(PHI2), .D(nready_t), .NOT_Q(d_latch_1_not_q));  // open: Q
  and and_3 (and_3_out, nand_3_out, not_6_out);
  D_latch d_latch_2 (.EN(PHI2), .D(ACRL2), .NOT_Q(d_latch_2_not_q));  // open: Q
  D_latch d_latch_3 (.EN(PHI1), .D(d_latch_2_not_q), .NOT_Q(ACRL1));  // open: Q
  D_latch d_latch_4 (.EN(PHI1), .D(nor_1_out), .Q(d_latch_4_q));  // open: NOT_Q
  D_latch d_latch_5 (.EN(PHI1), .D(nor_8_out), .Q(d_latch_5_q));  // open: NOT_Q
  D_latch d_latch_6 (.EN(PHI1), .D(multiplexer_1_out), .Q(d_latch_6_q));  // open: NOT_Q
  D_latch d_latch_7 (.EN(PHI1), .D(RESP), .Q(d_latch_7_q));  // open: NOT_Q
  D_latch d_latch_8 (.EN(PHI2), .D(not_10_out), .Q(d_latch_8_q));  // open: NOT_Q
  not not_10 (not_10_out, nready_t);
  D_latch d_latch_9 (.EN(PHI1), .D(nor_9_out), .Q(d_latch_9_q));  // open: NOT_Q
  nor nor_9 (nor_9_out, not_9_out, NotReadyPhi1);
  D_latch d_latch_10 (.EN(PHI1), .D(d_latch_1_not_q), .NOT_Q(d_latch_10_not_q));  // open: Q
  D_latch d_latch_11 (.EN(PHI2), .D(TRES1), .Q(d_latch_11_q));  // open: NOT_Q
  D_latch d_latch_12 (.EN(PHI2), .D(nTWOCYCLE), .Q(d_latch_12_q));  // open: NOT_Q
  D_latch d_latch_13 (.EN(PHI2), .D(TRESX), .Q(d_latch_13_q));  // open: NOT_Q
  D_latch d_latch_14 (.EN(PHI1), .D(and_3_out), .Q(d_latch_14_q));  // open: NOT_Q
  not not_11 (not_11_out, nIMPLED);
  nand nand_4 (nand_4_out, nSHIFT, not_1_out);
  and and_4 (and_4_out, d_latch_9_q, xnor_1_out);
  xnor xnor_1 (xnor_1_out, BRFW, ACR);
  not not_12 (NotReadyPhi1, d_latch_10_not_q);
  not not_13 (not_13_out, d_latch_11_q);
  nand nand_5 (nand_5_out, d_latch_12_q, d_latch_13_q);
  and and_5 (REST, DORES, nand_4_out);
  nor nor_10 (ENDS, d_latch_6_q, d_latch_7_q);
  and and_6 (and_6_out, not_13_out, nand_5_out);
  nor nor_11 (nor_11_out, nready_t, d_latch_14_q, not_11_out);
  nor nor_12 (nor_12_out, nSHIFT, nMemOP, nready_t);
  not not_14 (not_14_out, nready_t);
  nor nor_13 (nor_13_out, nready_t, d_latch_4_q, ACRL1, REST);
  nor nor_14 (nor_14_out, nor_25_out, RESP, ENDS);
  nor nor_15 (nor_15_out, nor_20_out, nready_t);
  nor nor_16 (nor_16_out, d_latch_24_q, d_latch_25_q);
  D_latch d_latch_15 (.EN(PHI1), .D(nor_12_out), .Q(d_latch_15_q));  // open: NOT_Q
  nand nand_6 (nand_6_out, T5, not_14_out);
  nor nor_17 (nor_17_out, RDY, d_latch_20_q);
  nor nor_18 (nor_18_out, nready_t, d_latch_5_q, REST);
  nor nor_19 (nor_19_out, d_latch_8_q, RESP, d_latch_22_q);
  nor nor_20 (nor_20_out, d_latch_21_q, and_4_out);
  nor nor_21 (nor_21_out, nor_15_out, ENDS);
  nor nor_22 (nT0X, and_6_out, nor_16_out);
  nor nor_23 (nor_23_out, and_6_out, nor_16_out);
  nor nor_24 (nor_24_out, d_latch_24_q, nready_t);
  nand nand_7 (nand_7_out, d_latch_29_q, nready_t);
  and and_7 (and_7_out, nand_7_out, not_15_out);
  not not_15 (not_15_out, d_latch_15_q);
  D_latch d_latch_16 (.EN(PHI1), .D(nand_6_out), .NOT_Q(d_latch_16_not_q));  // open: Q
  D_latch d_latch_17 (.EN(PHI1), .D(nor_14_out), .NOT_Q(d_latch_17_not_q));  // open: Q
  nor nor_25 (nor_25_out, nready_t, ENDX);
  D_latch d_latch_18 (.EN(PHI0), .D(SYNC), .NOT_Q(d_latch_18_not_q));  // open: Q
  D_latch d_latch_19 (.EN(PHI1), .D(nor_17_out), .Q(nready_t));  // open: NOT_Q
  D_latch d_latch_20 (.EN(PHI2), .D(nor_18_out), .Q(d_latch_20_q));  // open: NOT_Q
  D_latch d_latch_21 (.EN(PHI1), .D(nor_19_out), .Q(d_latch_21_q));  // open: NOT_Q
  D_latch d_latch_22 (.EN(PHI2), .D(nor_20_out), .Q(d_latch_22_q));  // open: NOT_Q
  D_latch d_latch_23 (.EN(PHI2), .D(nor_21_out), .NOT_Q(SYNC));  // open: Q
  not not_16 (TRES1, nor_21_out);
  D_latch d_latch_24 (.EN(PHI1), .D(nor_23_out), .Q(d_latch_24_q));  // open: NOT_Q
  not not_17 (nT0, nor_23_out);
  D_latch d_latch_25 (.EN(PHI2), .D(nor_24_out), .Q(d_latch_25_q), .NOT_Q(nT1X));
  D_latch d_latch_26 (.EN(PHI2), .D(B_OUT), .Q(d_latch_26_q));  // open: NOT_Q
  D_latch d_latch_27 (.EN(PHI2), .D(and_4_out), .Q(d_latch_27_q));  // open: NOT_Q
  D_latch d_latch_28 (.EN(PHI2), .D(nor_11_out), .Q(d_latch_28_q));  // open: NOT_Q
  D_latch d_latch_29 (.EN(PHI1), .D(T5), .Q(d_latch_29_q));  // open: NOT_Q
  D_latch d_latch_30 (.EN(PHI2), .D(and_7_out), .NOT_Q(T5));  // open: Q
  D_latch d_latch_31 (.EN(PHI2), .D(d_latch_16_not_q), .NOT_Q(d_latch_31_not_q));  // open: Q
  nor nor_26 (TRESX, nor_13_out, BRK6E, d_latch_17_not_q);
  nor nor_27 (nor_27_out, D96, nMemOP, not_18_out);
  not not_18 (not_18_out, nSHIFT);
  nor nor_28 (FETCH, d_latch_18_not_q, nready_t);
  or or_1 (or_1_out, d_latch_27_q, d_latch_28_q);
  not not_19 (T6, d_latch_31_not_q);
  nand nand_8 (_0_IR, B_OUT, FETCH);
  D_latch d_latch_32 (.EN(PHI2), .D(nor_18_out), .NOT_Q(d_latch_32_not_q));  // open: Q
  nor nor_29 (nor_29_out, d_latch_32_not_q, PHI2);
  and and_8 (and_8_out, d_latch_26_q, or_1_out);
  nor nor_30 (ENDX, T6, BR3, nor_27_out, not_7_out);
  nor nor_31 (STOR, not_1_out, nMemOP);
  buf buffer_1 (nREADY, nready_t);
  buf buffer_2 (R_W, d_latch_32_not_q);
  not not_20 (RD, nor_29_out);
  not not_21 (_1_PC, and_8_out);

  // Other names for the same wires on the sheet: T0 = nT0; T1 = SYNC

  // Notes on the sheet:
  //   /STORE
  //   ReadyDelay
  //   TRES1
  //   /IMPLIED
  //   ENDS
  //   ENDS
  //   RDY
  //   ENDS
  //   WR
  //   /T0X
  //   TRES1
  //   a
  //   b
  //   c
  //   /T1X
  //   0/IR
  //   FETCH
  //   1/PC
endmodule

// BUS CONTROL
module BUS_CONTROL (
  input  PHI1,
  input  PHI2,
  input  D57,
  input  D58,
  input  D59,
  input  D60,
  input  D61,
  input  D62,
  input  D63,
  input  D64,
  input  D65,
  input  D66,
  input  D67,
  input  D68,
  input  D69,
  input  D70,
  input  D71,
  input  D72,
  input  D73,
  input  D74,
  input  D79,
  input  BR2,
  input  D81,
  input  D82,
  input  D89,
  input  D90,
  input  D91,
  input  RDY,
  input  BR3,
  input  nREADY,
  input  T2,
  output _0_ADH17,
  output SB_AC,
  output ADL_ABL,
  output AC_SB,
  output SB_DB,
  output AC_DB,
  output SB_ADH,
  output DL_ADH,
  output DL_DB,
  output DL_ADL,
  output ADH_ABH
);

  wire ACRL2, AND, and_1_out, and_2_out, and_3_out, buffer_2_out, buffer_4_out, buffer_6_out,
       d_latch_2_not_q, d_latch_3_not_q, d_latch_4_not_q, d_latch_5_not_q, d_latch_6_not_q, d_latch_7_not_q,
       d_latch_8_not_q, d_latch_9_not_q, d_latch_10_not_q, d_latch_11_not_q, d_latch_12_not_q,
       d_latch_13_not_q, d_latch_14_not_q, IND, JSR_5, nand_1_out, nand_2_out, nand_3_out, nand_4_out,
       nand_5_out, nand_6_out, nor_1_out, nor_2_out, nor_3_out, nor_4_out, nor_5_out, nor_6_out, nor_7_out,
       nor_8_out, nor_9_out, nor_10_out, nor_11_out, nor_12_out, nor_13_out, nor_14_out, nor_15_out,
       nor_16_out, nor_17_out, nor_18_out, nor_19_out, nor_20_out, not_1_out, not_2_out, not_4_out,
       not_6_out, not_7_out, not_8_out, not_10_out, not_11_out, not_12_out, NotReadyPhi1, nPCH_PCH, nready_t,
       or_1_out, PHI1_t, PHI2_t, RTS_5, STOR, T1, T5, T6, undriven, undriven_2, undriven_3, undriven_4,
       undriven_5, undriven_6, undriven_7, undriven_8;

  not not_1 (not_1_out, RDY);
  not not_2 (not_2_out, D64);
  nor nor_1 (nor_1_out, D69, D70);
  not not_3 (AND, nor_1_out);
  nor nor_2 (nor_2_out, D71, D72);
  nor nor_3 (nor_3_out, D81, D82);
  nor nor_4 (nor_4_out, undriven, D90);
  D_latch d_latch_1 (.EN(PHI1_t), .D(nready_t), .Q(NotReadyPhi1));  // open: NOT_Q
  nor nor_5 (nor_5_out, D58, D59, D60, D61, D62, D63, D64);
  nand nand_1 (nand_1_out, not_2_out, D65);
  nor nor_6 (nor_6_out, D89, nor_4_out, D91, RTS_5);
  not not_4 (not_4_out, NotReadyPhi1);
  nor nor_7 (nor_7_out, D66, D67, D68, AND);
  D_latch d_latch_2 (.EN(PHI1_t), .D(not_1_out), .NOT_Q(d_latch_2_not_q));  // open: Q
  not not_5 (IND, nor_6_out);
  nand nand_2 (nand_2_out, ACRL2, not_4_out);
  and and_1 (and_1_out, nand_1_out, nor_7_out);
  D_latch d_latch_3 (.EN(PHI2_t), .D(d_latch_2_not_q), .NOT_Q(d_latch_3_not_q));  // open: Q
  nor nor_8 (nor_8_out, nand_2_out, undriven_2);
  nor nor_9 (nor_9_out, D73, d_latch_3_not_q);
  nor nor_10 (nor_10_out, IND, T2, JSR_5, nPCH_PCH);
  not not_6 (not_6_out, nor_2_out);
  nand nand_3 (nand_3_out, undriven_5, T5);
  not not_7 (not_7_out, nor_9_out);
  nor nor_11 (nor_11_out, D57, not_8_out);
  not not_8 (not_8_out, nor_3_out);
  nor nor_12 (nor_12_out, not_6_out, nready_t);
  nor nor_13 (nor_13_out, T6, T5);
  // NOT_Gate not_9 has open pins: in=undriven_6, out=open
  nor nor_14 (nor_14_out, undriven_6, AND);
  not not_10 (not_10_out, nand_3_out);
  nand nand_4 (nand_4_out, nor_2_out, not_7_out);
  nor nor_15 (nor_15_out, nor_8_out, nor_16_out);
  nor nor_16 (nor_16_out, nor_10_out, nready_t);
  nand nand_5 (nand_5_out, nor_12_out, nor_13_out);
  not not_11 (not_11_out, D74);
  nand nand_6 (nand_6_out, D79, STOR);
  nor nor_17 (nor_17_out, BR3, nand_4_out);
  nor nor_18 (nor_18_out, undriven_8, IND);
  nor nor_19 (nor_19_out, BR2, undriven_4, undriven_7, T5);
  // NOT_Gate not_12 has open pins: in=open, out=not_12_out
  or or_1 (or_1_out, nor_15_out, BR3);
  nor nor_20 (nor_20_out, T1, nor_14_out, D67, not_10_out, BR2, undriven_3);
  and and_2 (and_2_out, not_11_out, nand_6_out);
  and and_3 (and_3_out, not_12_out, or_1_out);
  D_latch d_latch_4 (.EN(PHI1), .D(nor_11_out), .NOT_Q(d_latch_4_not_q));  // open: Q
  D_latch d_latch_5 (.EN(PHI1), .D(nor_5_out), .NOT_Q(d_latch_5_not_q));  // open: Q
  D_latch d_latch_6 (.EN(PHI1), .D(nand_5_out), .NOT_Q(d_latch_6_not_q));  // open: Q
  D_latch d_latch_7 (.EN(PHI1), .D(and_1_out), .NOT_Q(d_latch_7_not_q));  // open: Q
  D_latch d_latch_8 (.EN(PHI1), .D(nor_20_out), .NOT_Q(d_latch_8_not_q));  // open: Q
  D_latch d_latch_9 (.EN(PHI1), .D(and_2_out), .NOT_Q(d_latch_9_not_q));  // open: Q
  D_latch d_latch_10 (.EN(PHI1), .D(nor_17_out), .NOT_Q(d_latch_10_not_q));  // open: Q
  D_latch d_latch_11 (.EN(PHI1), .D(nor_18_out), .NOT_Q(d_latch_11_not_q));  // open: Q
  D_latch d_latch_12 (.EN(PHI1), .D(nor_19_out), .NOT_Q(d_latch_12_not_q));  // open: Q
  D_latch d_latch_13 (.EN(PHI1), .D(nor_3_out), .NOT_Q(d_latch_13_not_q));  // open: Q
  D_latch d_latch_14 (.EN(PHI1), .D(and_3_out), .NOT_Q(d_latch_14_not_q));  // open: Q
  buf buffer_1 (_0_ADH17, d_latch_4_not_q);
  buf buffer_2 (buffer_2_out, d_latch_5_not_q);
  buf buffer_3 (ADL_ABL, d_latch_6_not_q);
  buf buffer_4 (buffer_4_out, d_latch_7_not_q);
  buf buffer_5 (SB_DB, d_latch_8_not_q);
  buf buffer_6 (buffer_6_out, d_latch_9_not_q);
  buf buffer_7 (SB_ADH, d_latch_10_not_q);
  buf buffer_8 (DL_ADH, d_latch_11_not_q);
  buf buffer_9 (DL_DB, d_latch_12_not_q);
  buf buffer_10 (DL_ADL, d_latch_13_not_q);
  buf buffer_11 (ADH_ABH, d_latch_14_not_q);
  and and_4 (SB_AC, PHI2, buffer_2_out);
  and and_5 (AC_SB, PHI2, buffer_4_out);
  and and_6 (AC_DB, PHI2, buffer_6_out);

  // Notes on the sheet:
  //   STA
  //   #DL/ADL
  //   /RDY
  //   push pull
  //   NotReadyPhi1
  //   #SB/AC
  //   Rdy delay
  //   #SB/ADH
  //   T2
  //   #AC/SB
  //   #ADL/ABL
  //   BR0
  //   JMP/4
  //   #DL/ADL
  //   STA
  //   JSXY
  //   PGX
  //   DL/PCH
  //   0/ADL0
  //   #SB/DB
  //   #DL/DB
endmodule
