// Logisim project 6502_Evo.circ as structural Verilog
module MOS_6502 (
  input  n_NMI,
  input  n_IRQ,
  input  RDY,
  input  n_RES,
  input  SO,
  input  D0_IN,
  input  D1_IN,
  input  D2_IN,
  input  D3_IN,
  input  D4_IN,
  input  D5_IN,
  input  D6_IN,
  input  D7_IN,
  output PHI1,
  output PHI2,
  output R_W,
  output SYNC,
  output A0,
  output A1,
  output A2,
  output A3,
  output A4,
  output A5,
  output A6,
  output A7,
  output D0_OUT,
  output D1_OUT,
  output D2_OUT,
  output D3_OUT,
  output D4_OUT,
  output D5_OUT,
  output A8,
  output A9,
  output A10,
  output A11,
  output A12,
  output A13,
  output A14,
  output A15,
  output D6_OUT,
  output D7_OUT
);

  wire ALU_inst_acr, ALU_inst_avr, Decoder_inst_l_0_090b2452, Decoder_inst_l_1_28cbbb7d,
       Decoder_inst_l_2_143403ae, Decoder_inst_l_3_39a566ac, Decoder_inst_l_4_558283f2,
       Decoder_inst_l_5_9518e519, Decoder_inst_l_6_5b7e39b9, Decoder_inst_l_7_14ab2533,
       Decoder_inst_l_8_05eb4f56, Decoder_inst_l_9_0082242d, Decoder_inst_l_10_57b0d741,
       Decoder_inst_l_11_aa2e7fa3, Decoder_inst_l_12_85a3418f, Decoder_inst_l_13_587da886,
       Decoder_inst_l_14_4f483598, Decoder_inst_l_15_5dad5732, Decoder_inst_l_16_c7396848,
       Decoder_inst_l_17_0f5278c7, Decoder_inst_l_18_4ab117a9, Decoder_inst_l_19_e094c090,
       Decoder_inst_l_20_adeacd1b, Decoder_inst_l_21_ada5c31c, Decoder_inst_l_22_f545d19e,
       Decoder_inst_l_23_d0835dd9, Decoder_inst_l_24_b6efc2f4, Decoder_inst_l_25_f5ad6aee,
       Decoder_inst_l_26_ffeee2da, Decoder_inst_l_27_6492a6f4, Decoder_inst_l_28_647e552a,
       Decoder_inst_l_29_1d3a3eb3, Decoder_inst_l_30_3bf8f3d0, Decoder_inst_l_31_e958c8e2,
       Decoder_inst_l_32_7de83e69, Decoder_inst_l_33_cae225fb, Decoder_inst_l_34_97db28cb,
       Decoder_inst_l_35_8b2262aa, Decoder_inst_l_36_34609549, Decoder_inst_l_37_acfb42d2,
       Decoder_inst_l_38_43aa51c3, Decoder_inst_l_39_c97a3f22, Decoder_inst_l_40_1e6b68e0,
       Decoder_inst_l_41_b24af141, Decoder_inst_l_42_ae8bf3e0, Decoder_inst_l_43_fdaf143b,
       Decoder_inst_l_44_bb416d4b, Decoder_inst_l_45_e516ed8c, Decoder_inst_l_46_6c10990a,
       Decoder_inst_l_47_7c60183d, Decoder_inst_l_48_330a6f3f, Decoder_inst_l_49_f70f8148,
       Decoder_inst_l_50_6b408103, Decoder_inst_l_51_79fb832a, Decoder_inst_l_52_253f2da2,
       Decoder_inst_l_53_d08b6e35, Decoder_inst_l_54_01afe50f, Decoder_inst_l_55_73ecc214,
       Decoder_inst_l_56_35bf93dd, Decoder_inst_l_57_0f0af090, Decoder_inst_l_58_4e7562c2,
       Decoder_inst_l_59_d4e3d539, Decoder_inst_l_60_8c46ae22, Decoder_inst_l_61_ef440803,
       Decoder_inst_l_62_1470bf03, Decoder_inst_l_63_0a5e7e38, Decoder_inst_l_64_e6cb4ce5,
       Decoder_inst_l_65_6a42b4dc, Decoder_inst_l_66_3306dbdf, Decoder_inst_l_67_7ef59d0e,
       Decoder_inst_l_68_820561b0, Decoder_inst_l_69_cbdecb8a, Decoder_inst_l_70_099188dc,
       Decoder_inst_l_71_facae7ec, Decoder_inst_l_72_92460769, Decoder_inst_l_73_3c19a6e4,
       Decoder_inst_l_74_b252c222, Decoder_inst_l_75_7b13a6b0, Decoder_inst_l_76_ea80c3c2,
       Decoder_inst_l_77_f96dcb28, Decoder_inst_l_78_8a0d457e, Decoder_inst_l_79_7d8df45e,
       Decoder_inst_l_80_053c0a7a, Decoder_inst_l_81_2726249e, Decoder_inst_l_82_298ac22b,
       Decoder_inst_l_83_79a418b7, Decoder_inst_l_84_e79a1766, Decoder_inst_l_85_b2daf010,
       Decoder_inst_l_86_b98cc819, Decoder_inst_l_87_c637b311, Decoder_inst_l_88_055bb603,
       Decoder_inst_l_89_5d5fe4c7, Decoder_inst_l_90_55afaa76, Decoder_inst_l_91_d03b9369,
       Decoder_inst_l_92_0cc1d36a, Decoder_inst_l_93_eaf60893, Decoder_inst_l_94_95326b03,
       Decoder_inst_l_95_f060a0fd, Decoder_inst_l_96_3d015798, Decoder_inst_l_97_f3e813cd,
       Decoder_inst_l_98_f4cee2ae, Decoder_inst_l_99_bb939962, Decoder_inst_l_100_16b00339,
       Decoder_inst_l_101_c09bb9ac, Decoder_inst_l_102_614a85bf, Decoder_inst_l_103_52940b9a,
       Decoder_inst_l_104_443c5ff0, Decoder_inst_l_105_5ce959fd, Decoder_inst_l_106_2a9581c6,
       Decoder_inst_l_107_a96ffaba, Decoder_inst_l_108_c205b5ff, Decoder_inst_l_109_2fe88a94,
       Decoder_inst_l_110_4cc555bd, Decoder_inst_l_111_2b81c3c9, Decoder_inst_l_112_708a0f10,
       Decoder_inst_l_113_fbaa75ad, Decoder_inst_l_114_f9625e87, Decoder_inst_l_115_b1986fe2,
       Decoder_inst_l_116_0ba24dc4, Decoder_inst_l_117_10a3c8b1, Decoder_inst_l_118_e0e8abfe,
       Decoder_inst_l_119_86db347d, Decoder_inst_l_120_c53a083f, Decoder_inst_l_121_da158f44,
       Decoder_inst_l_122_0e8f1988, Decoder_inst_l_123_a8638cda, Decoder_inst_l_124_8d81fffd,
       Decoder_inst_l_125_8f968e43, Decoder_inst_l_126_7e3003c6, Decoder_inst_l_127_28942974,
       Decoder_inst_l_128_23d7200b, Decoder_inst_l_129_7b5e5edf, IR_inst_ir0, IR_inst_ir1, IR_inst_ir2,
       IR_inst_ir3, IR_inst_ir4, IR_inst_ir5, IR_inst_ir6, IR_inst_ir7, IRQ_FF_qn, IRQ_Latch_not_q,
       NMI_FF_qn, not_1_out, not_2_out, not_3_out, PD_inst_n_implied, PD_inst_n_pd0, PD_inst_n_pd1,
       PD_inst_n_pd2, PD_inst_n_pd3, PD_inst_n_pd4, PD_inst_n_pd5, PD_inst_n_pd6, PD_inst_n_pd7,
       PD_inst_n_twocycle, PHI0_out, Random_inst_acr_c_5cb02b46, Random_inst_db_c_01ed158e,
       Random_inst_db_n_68ba26fc, Random_inst_db_p_37e5c1ba, Random_inst_db_v_92adf01b,
       Random_inst_dbz_z_a7859eb1, Random_inst_ends, Random_inst_endx, Random_inst_fetch,
       Random_inst_ir5_c_8cbf3e52, Random_inst_ir5_d_ec89b364, Random_inst_ir5_i_e7eeeda5,
       Random_inst_l_0_ir_c32b8001, Random_inst_l_0_v_f0a8dd83, Random_inst_l_c_out_f91ece9c,
       Random_inst_l_d_out_7d61c6e7, Random_inst_l_i_out_6792f219, Random_inst_l_n_out_10df9d15,
       Random_inst_l_t0_5a901129, Random_inst_l_t1x_624de7e6, Random_inst_l_t2_37fe4d42,
       Random_inst_l_t3_3fe619b3, Random_inst_l_t4_d9b6e407, Random_inst_l_t5_89b31bc6,
       Random_inst_l_v_out_959779aa, Random_inst_l_z_out_2813b2ba, Random_inst_p_db_42279b60,
       Random_inst_r_w_47630a0a, Random_inst_rd, Random_inst_t1, Random_inst_tres1, Random_inst_tresx,
       Random_inst_wr, RDY_Latch1_not_q, RDY_Latch2_not_q, RES_FF_q, RES_Latch_not_q;
  wire [2:0] Random_inst_dl_adl_6c5e0116, Random_inst_l_acin_e173f520;
  wire [4:0] Random_inst_adl_abl_5bea59e2;
  wire [6:0] Random_inst_sb_ac_b159eec5;
  wire [7:0] ALU_inst_ac_debug, ALU_inst_add_debug, ALU_inst_adh0, ALU_inst_ai_debug, ALU_inst_bi_debug,
       DL_inst_dl_debug, DL_inst_dor_debug, Random_inst_db0, Random_inst_y_sb_d628d28f, REGS_inst_adl0,
       REGS_inst_s_debug, REGS_inst_sb0_out, REGS_inst_x_debug, REGS_inst_y_debug;
  wire [8:0] Random_inst_adh_pch_61520abf;
  wire [12:0] Random_inst_ndb_add_ee0a1870;
  wire [15:0] PC_inst_pc_debug, PC_inst_pcs_debug;

  buf buffer_1 (SYNC, Random_inst_t1);
  D_Flip_Flop #(.trigger("high")) NMI_FF (.D(n_NMI), .clk(PHI2), .Qn(NMI_FF_qn));  // open: Q, preset, reset
  DECODER_TRANS Decoder_inst (
    .L_10_57b0d741(Decoder_inst_l_10_57b0d741), .L_11_aa2e7fa3(Decoder_inst_l_11_aa2e7fa3),
    .L_12_85a3418f(Decoder_inst_l_12_85a3418f), .L_13_587da886(Decoder_inst_l_13_587da886),
    .L_14_4f483598(Decoder_inst_l_14_4f483598), .L_15_5dad5732(Decoder_inst_l_15_5dad5732),
    .L_16_c7396848(Decoder_inst_l_16_c7396848), .L_17_0f5278c7(Decoder_inst_l_17_0f5278c7),
    .L_18_4ab117a9(Decoder_inst_l_18_4ab117a9), .L_19_e094c090(Decoder_inst_l_19_e094c090),
    .L_20_adeacd1b(Decoder_inst_l_20_adeacd1b), .L_21_ada5c31c(Decoder_inst_l_21_ada5c31c),
    .L_22_f545d19e(Decoder_inst_l_22_f545d19e), .L_23_d0835dd9(Decoder_inst_l_23_d0835dd9),
    .L_24_b6efc2f4(Decoder_inst_l_24_b6efc2f4), .L_25_f5ad6aee(Decoder_inst_l_25_f5ad6aee),
    .L_26_ffeee2da(Decoder_inst_l_26_ffeee2da), .L_27_6492a6f4(Decoder_inst_l_27_6492a6f4),
    .L_28_647e552a(Decoder_inst_l_28_647e552a), .L_29_1d3a3eb3(Decoder_inst_l_29_1d3a3eb3),
    .L_30_3bf8f3d0(Decoder_inst_l_30_3bf8f3d0), .L_31_e958c8e2(Decoder_inst_l_31_e958c8e2),
    .L_32_7de83e69(Decoder_inst_l_32_7de83e69), .L_33_cae225fb(Decoder_inst_l_33_cae225fb),
    .L_34_97db28cb(Decoder_inst_l_34_97db28cb), .L_35_8b2262aa(Decoder_inst_l_35_8b2262aa),
    .L_36_34609549(Decoder_inst_l_36_34609549), .L_37_acfb42d2(Decoder_inst_l_37_acfb42d2),
    .L_38_43aa51c3(Decoder_inst_l_38_43aa51c3), .L_39_c97a3f22(Decoder_inst_l_39_c97a3f22),
    .L_40_1e6b68e0(Decoder_inst_l_40_1e6b68e0), .L_41_b24af141(Decoder_inst_l_41_b24af141),
    .L_42_ae8bf3e0(Decoder_inst_l_42_ae8bf3e0), .L_43_fdaf143b(Decoder_inst_l_43_fdaf143b),
    .L_44_bb416d4b(Decoder_inst_l_44_bb416d4b), .L_0_090b2452(Decoder_inst_l_0_090b2452),
    .L_45_e516ed8c(Decoder_inst_l_45_e516ed8c), .L_46_6c10990a(Decoder_inst_l_46_6c10990a),
    .L_47_7c60183d(Decoder_inst_l_47_7c60183d), .L_48_330a6f3f(Decoder_inst_l_48_330a6f3f),
    .L_49_f70f8148(Decoder_inst_l_49_f70f8148), .L_50_6b408103(Decoder_inst_l_50_6b408103),
    .L_51_79fb832a(Decoder_inst_l_51_79fb832a), .L_52_253f2da2(Decoder_inst_l_52_253f2da2),
    .L_53_d08b6e35(Decoder_inst_l_53_d08b6e35), .L_1_28cbbb7d(Decoder_inst_l_1_28cbbb7d),
    .L_54_01afe50f(Decoder_inst_l_54_01afe50f), .L_55_73ecc214(Decoder_inst_l_55_73ecc214),
    .L_56_35bf93dd(Decoder_inst_l_56_35bf93dd), .L_57_0f0af090(Decoder_inst_l_57_0f0af090),
    .L_58_4e7562c2(Decoder_inst_l_58_4e7562c2), .L_59_d4e3d539(Decoder_inst_l_59_d4e3d539),
    .L_60_8c46ae22(Decoder_inst_l_60_8c46ae22), .L_61_ef440803(Decoder_inst_l_61_ef440803),
    .L_62_1470bf03(Decoder_inst_l_62_1470bf03), .L_2_143403ae(Decoder_inst_l_2_143403ae),
    .L_63_0a5e7e38(Decoder_inst_l_63_0a5e7e38), .L_64_e6cb4ce5(Decoder_inst_l_64_e6cb4ce5),
    .L_65_6a42b4dc(Decoder_inst_l_65_6a42b4dc), .L_66_3306dbdf(Decoder_inst_l_66_3306dbdf),
    .L_67_7ef59d0e(Decoder_inst_l_67_7ef59d0e), .L_68_820561b0(Decoder_inst_l_68_820561b0),
    .L_69_cbdecb8a(Decoder_inst_l_69_cbdecb8a), .L_70_099188dc(Decoder_inst_l_70_099188dc),
    .L_71_facae7ec(Decoder_inst_l_71_facae7ec), .L_72_92460769(Decoder_inst_l_72_92460769),
    .L_3_39a566ac(Decoder_inst_l_3_39a566ac), .L_73_3c19a6e4(Decoder_inst_l_73_3c19a6e4),
    .L_74_b252c222(Decoder_inst_l_74_b252c222), .L_75_7b13a6b0(Decoder_inst_l_75_7b13a6b0),
    .L_76_ea80c3c2(Decoder_inst_l_76_ea80c3c2), .L_77_f96dcb28(Decoder_inst_l_77_f96dcb28),
    .L_78_8a0d457e(Decoder_inst_l_78_8a0d457e), .L_79_7d8df45e(Decoder_inst_l_79_7d8df45e),
    .L_80_053c0a7a(Decoder_inst_l_80_053c0a7a), .L_81_2726249e(Decoder_inst_l_81_2726249e),
    .L_4_558283f2(Decoder_inst_l_4_558283f2), .L_82_298ac22b(Decoder_inst_l_82_298ac22b),
    .L_83_79a418b7(Decoder_inst_l_83_79a418b7), .L_84_e79a1766(Decoder_inst_l_84_e79a1766),
    .L_85_b2daf010(Decoder_inst_l_85_b2daf010), .L_86_b98cc819(Decoder_inst_l_86_b98cc819),
    .L_87_c637b311(Decoder_inst_l_87_c637b311), .L_88_055bb603(Decoder_inst_l_88_055bb603),
    .L_89_5d5fe4c7(Decoder_inst_l_89_5d5fe4c7), .L_90_55afaa76(Decoder_inst_l_90_55afaa76),
    .L_5_9518e519(Decoder_inst_l_5_9518e519), .L_91_d03b9369(Decoder_inst_l_91_d03b9369),
    .L_92_0cc1d36a(Decoder_inst_l_92_0cc1d36a), .L_93_eaf60893(Decoder_inst_l_93_eaf60893),
    .L_94_95326b03(Decoder_inst_l_94_95326b03), .L_95_f060a0fd(Decoder_inst_l_95_f060a0fd),
    .L_96_3d015798(Decoder_inst_l_96_3d015798), .L_97_f3e813cd(Decoder_inst_l_97_f3e813cd),
    .L_98_f4cee2ae(Decoder_inst_l_98_f4cee2ae), .L_99_bb939962(Decoder_inst_l_99_bb939962),
    .L_100_16b00339(Decoder_inst_l_100_16b00339), .L_101_c09bb9ac(Decoder_inst_l_101_c09bb9ac),
    .L_102_614a85bf(Decoder_inst_l_102_614a85bf), .L_103_52940b9a(Decoder_inst_l_103_52940b9a),
    .L_104_443c5ff0(Decoder_inst_l_104_443c5ff0), .L_105_5ce959fd(Decoder_inst_l_105_5ce959fd),
    .L_106_2a9581c6(Decoder_inst_l_106_2a9581c6), .L_107_a96ffaba(Decoder_inst_l_107_a96ffaba),
    .L_108_c205b5ff(Decoder_inst_l_108_c205b5ff), .L_109_2fe88a94(Decoder_inst_l_109_2fe88a94),
    .L_6_5b7e39b9(Decoder_inst_l_6_5b7e39b9), .L_110_4cc555bd(Decoder_inst_l_110_4cc555bd),
    .L_111_2b81c3c9(Decoder_inst_l_111_2b81c3c9), .L_112_708a0f10(Decoder_inst_l_112_708a0f10),
    .L_113_fbaa75ad(Decoder_inst_l_113_fbaa75ad), .L_114_f9625e87(Decoder_inst_l_114_f9625e87),
    .L_115_b1986fe2(Decoder_inst_l_115_b1986fe2), .L_116_0ba24dc4(Decoder_inst_l_116_0ba24dc4),
    .L_117_10a3c8b1(Decoder_inst_l_117_10a3c8b1), .L_118_e0e8abfe(Decoder_inst_l_118_e0e8abfe),
    .L_119_86db347d(Decoder_inst_l_119_86db347d), .L_7_14ab2533(Decoder_inst_l_7_14ab2533),
    .L_120_c53a083f(Decoder_inst_l_120_c53a083f), .L_121_da158f44(Decoder_inst_l_121_da158f44),
    .L_122_0e8f1988(Decoder_inst_l_122_0e8f1988), .L_123_a8638cda(Decoder_inst_l_123_a8638cda),
    .L_124_8d81fffd(Decoder_inst_l_124_8d81fffd), .L_125_8f968e43(Decoder_inst_l_125_8f968e43),
    .L_126_7e3003c6(Decoder_inst_l_126_7e3003c6), .L_127_28942974(Decoder_inst_l_127_28942974),
    .L_128_23d7200b(Decoder_inst_l_128_23d7200b), .L_129_7b5e5edf(Decoder_inst_l_129_7b5e5edf),
    .L_8_05eb4f56(Decoder_inst_l_8_05eb4f56), .L_9_0082242d(Decoder_inst_l_9_0082242d),
    .L_T5_89b31bc6(Random_inst_l_t5_89b31bc6), .L_T4_d9b6e407(Random_inst_l_t4_d9b6e407),
    .L_T3_3fe619b3(Random_inst_l_t3_3fe619b3), .L_T2_37fe4d42(Random_inst_l_t2_37fe4d42), .IR6(IR_inst_ir6),
    .IR5(IR_inst_ir5), .L_T0_5a901129(Random_inst_l_t0_5a901129),
    .L_T1X_624de7e6(Random_inst_l_t1x_624de7e6), .IR0(IR_inst_ir0), .IR1(IR_inst_ir1), .IR7(IR_inst_ir7),
    .IR4(IR_inst_ir4), .IR3(IR_inst_ir3), .IR2(IR_inst_ir2));
  RANDOM_LOGIC Random_inst (
    .L_D_OUT_7d61c6e7(Random_inst_l_d_out_7d61c6e7), .L_C_OUT_f91ece9c(Random_inst_l_c_out_f91ece9c),
    .L_N_OUT_10df9d15(Random_inst_l_n_out_10df9d15), .L_Z_OUT_2813b2ba(Random_inst_l_z_out_2813b2ba),
    .NDB_ADD_ee0a1870(Random_inst_ndb_add_ee0a1870[0]), .DB_ADD_48d85b7e(Random_inst_ndb_add_ee0a1870[1]),
    .L_0_ADD_81d17e61(Random_inst_ndb_add_ee0a1870[2]), .SB_ADD_0eab26ac(Random_inst_ndb_add_ee0a1870[3]),
    .ADL_ADD_e28b8a30(Random_inst_ndb_add_ee0a1870[4]), .ANDS(Random_inst_ndb_add_ee0a1870[8]),
    .EORS(Random_inst_ndb_add_ee0a1870[9]), .ORS(Random_inst_ndb_add_ee0a1870[10]),
    .L_ACIN_e173f520(Random_inst_l_acin_e173f520[0]), .SUMS(Random_inst_ndb_add_ee0a1870[12]),
    .L_DAA_82b80d94(Random_inst_l_acin_e173f520[1]), .ADD_SB7_a8f4b77a(Random_inst_ndb_add_ee0a1870[6]),
    .ADD_SB06_a3738230(Random_inst_ndb_add_ee0a1870[5]), .ADD_ADL_3fac4345(Random_inst_ndb_add_ee0a1870[7]),
    .L_DSA_ea96e89b(Random_inst_l_acin_e173f520[2]), .SRS(Random_inst_ndb_add_ee0a1870[11]),
    .DL_ADL_6c5e0116(Random_inst_dl_adl_6c5e0116[0]), .DL_DB_69522204(Random_inst_dl_adl_6c5e0116[1]),
    .DL_ADH_3839a3d0(Random_inst_dl_adl_6c5e0116[2]), .ADH_ABH_8f72aca9(Random_inst_adl_abl_5bea59e2[1]),
    .ADL_ABL_5bea59e2(Random_inst_adl_abl_5bea59e2[0]), .SB_AC_b159eec5(Random_inst_sb_ac_b159eec5[0]),
    .AC_SB_c49f602a(Random_inst_sb_ac_b159eec5[1]), .L_0_ADH0_e340c71e(Random_inst_sb_ac_b159eec5[5]),
    .L_0_ADH17_f181a8fa(Random_inst_sb_ac_b159eec5[6]), .AC_DB_519ce409(Random_inst_sb_ac_b159eec5[2]),
    .SB_DB_641efa5a(Random_inst_sb_ac_b159eec5[3]), .SB_ADH_4f1456ff(Random_inst_sb_ac_b159eec5[4]),
    .ADL_PCL_9a95c372(Random_inst_adh_pch_61520abf[4]), .PCL_PCL_4f350f4d(Random_inst_adh_pch_61520abf[5]),
    .PCH_ADH_ead93594(Random_inst_adh_pch_61520abf[2]), .PCL_ADL_ee043dbc(Random_inst_adh_pch_61520abf[6]),
    .PCH_DB_a81fefa0(Random_inst_adh_pch_61520abf[3]), .L_0_ADL0_f8fabdab(Random_inst_adl_abl_5bea59e2[2]),
    .PCL_DB_4172714e(Random_inst_adh_pch_61520abf[7]), .ADH_PCH_61520abf(Random_inst_adh_pch_61520abf[0]),
    .PCH_PCH_807b9fbd(Random_inst_adh_pch_61520abf[1]), .TRESX(Random_inst_tresx),
    .L_0_IR_c32b8001(Random_inst_l_0_ir_c32b8001), .ENDS(Random_inst_ends), .ENDX(Random_inst_endx),
    .TRES1(Random_inst_tres1), .T1(Random_inst_t1), .L_0_ADL1_4e9a6ca8(Random_inst_adl_abl_5bea59e2[3]),
    .L_T1X_624de7e6(Random_inst_l_t1x_624de7e6), .RD(Random_inst_rd),
    .R_W_47630a0a(Random_inst_r_w_47630a0a), .L_1_PC_f2b91046(Random_inst_adh_pch_61520abf[8]),
    .P_DB_42279b60(Random_inst_p_db_42279b60), .IR5_I_e7eeeda5(Random_inst_ir5_i_e7eeeda5),
    .IR5_C_8cbf3e52(Random_inst_ir5_c_8cbf3e52), .IR5_D_ec89b364(Random_inst_ir5_d_ec89b364),
    .L_0_V_f0a8dd83(Random_inst_l_0_v_f0a8dd83), .DB7(Random_inst_db0[7]),
    .ACR_C_5cb02b46(Random_inst_acr_c_5cb02b46), .out_233(Random_inst_db0[6]),
    .DBZ_Z_a7859eb1(Random_inst_dbz_z_a7859eb1), .L_0_ADL2_2c4a79f4(Random_inst_adl_abl_5bea59e2[4]),
    .out_234(Random_inst_db0[5]), .DB_N_68ba26fc(Random_inst_db_n_68ba26fc), .DB4(Random_inst_db0[4]),
    .DB_P_37e5c1ba(Random_inst_db_p_37e5c1ba), .out_236(Random_inst_db0[3]),
    .DB_C_01ed158e(Random_inst_db_c_01ed158e), .DB2(Random_inst_db0[2]),
    .DB_V_92adf01b(Random_inst_db_v_92adf01b), .out_238(Random_inst_db0[1]), .DB0(Random_inst_db0[0]),
    .Y_SB_d628d28f(Random_inst_y_sb_d628d28f[0]), .L_T3_3fe619b3(Random_inst_l_t3_3fe619b3),
    .L_T4_d9b6e407(Random_inst_l_t4_d9b6e407), .L_T5_89b31bc6(Random_inst_l_t5_89b31bc6),
    .WR(Random_inst_wr), .FETCH(Random_inst_fetch), .L_T0_5a901129(Random_inst_l_t0_5a901129),
    .L_T2_37fe4d42(Random_inst_l_t2_37fe4d42), .X_SB_222038db(Random_inst_y_sb_d628d28f[2]),
    .SB_Y_9a33ae5e(Random_inst_y_sb_d628d28f[1]), .SB_X_cf392641(Random_inst_y_sb_d628d28f[3]),
    .S_SB_e37affed(Random_inst_y_sb_d628d28f[7]), .S_ADL_07acd992(Random_inst_y_sb_d628d28f[4]),
    .SB_S_4c94ee46(Random_inst_y_sb_d628d28f[6]), .S_S_09f08a69(Random_inst_y_sb_d628d28f[5]),
    .L_V_OUT_959779aa(Random_inst_l_v_out_959779aa), .L_I_OUT_6792f219(Random_inst_l_i_out_6792f219),
    .X25(Decoder_inst_l_25_f5ad6aee), .X26(Decoder_inst_l_26_ffeee2da), .X27(Decoder_inst_l_27_6492a6f4),
    .X28(Decoder_inst_l_28_647e552a), .X29(Decoder_inst_l_29_1d3a3eb3), .X30(Decoder_inst_l_30_3bf8f3d0),
    .X31(Decoder_inst_l_31_e958c8e2), .X32(Decoder_inst_l_32_7de83e69), .X33(Decoder_inst_l_33_cae225fb),
    .X34(Decoder_inst_l_34_97db28cb), .X35(Decoder_inst_l_35_8b2262aa), .X36(Decoder_inst_l_36_34609549),
    .X37(Decoder_inst_l_37_acfb42d2), .X38(Decoder_inst_l_38_43aa51c3), .X39(Decoder_inst_l_39_c97a3f22),
    .X40(Decoder_inst_l_40_1e6b68e0), .X41(Decoder_inst_l_41_b24af141), .X42(Decoder_inst_l_42_ae8bf3e0),
    .L_NMIP_021a4ca5(not_1_out), .RESP(RES_Latch_not_q), .L_IRQP_c24e1171(IRQ_Latch_not_q),
    .AVR(ALU_inst_avr), .ACR(ALU_inst_acr), .SO(SO), .X43(Decoder_inst_l_43_fdaf143b),
    .X44(Decoder_inst_l_44_bb416d4b), .X45(Decoder_inst_l_45_e516ed8c), .X46(Decoder_inst_l_46_6c10990a),
    .X47(Decoder_inst_l_47_7c60183d), .X48(Decoder_inst_l_48_330a6f3f), .X49(Decoder_inst_l_49_f70f8148),
    .X50(Decoder_inst_l_50_6b408103), .X51(Decoder_inst_l_51_79fb832a), .X52(Decoder_inst_l_52_253f2da2),
    .X53(Decoder_inst_l_53_d08b6e35), .X54(Decoder_inst_l_54_01afe50f), .X55(Decoder_inst_l_55_73ecc214),
    .X56(Decoder_inst_l_56_35bf93dd), .X57(Decoder_inst_l_57_0f0af090), .X0(Decoder_inst_l_0_090b2452),
    .X58(Decoder_inst_l_58_4e7562c2), .X59(Decoder_inst_l_59_d4e3d539), .X60(Decoder_inst_l_60_8c46ae22),
    .X61(Decoder_inst_l_61_ef440803), .X62(Decoder_inst_l_62_1470bf03), .X63(Decoder_inst_l_63_0a5e7e38),
    .X64(Decoder_inst_l_64_e6cb4ce5), .X65(Decoder_inst_l_65_6a42b4dc), .X66(Decoder_inst_l_66_3306dbdf),
    .X1(Decoder_inst_l_1_28cbbb7d), .X67(Decoder_inst_l_67_7ef59d0e), .X68(Decoder_inst_l_68_820561b0),
    .X69(Decoder_inst_l_69_cbdecb8a), .X70(Decoder_inst_l_70_099188dc), .X71(Decoder_inst_l_71_facae7ec),
    .X72(Decoder_inst_l_72_92460769), .X73(Decoder_inst_l_73_3c19a6e4), .X74(Decoder_inst_l_74_b252c222),
    .X75(Decoder_inst_l_75_7b13a6b0), .X2(Decoder_inst_l_2_143403ae), .X76(Decoder_inst_l_76_ea80c3c2),
    .X77(Decoder_inst_l_77_f96dcb28), .X78(Decoder_inst_l_78_8a0d457e), .X79(Decoder_inst_l_79_7d8df45e),
    .X80(Decoder_inst_l_80_053c0a7a), .X81(Decoder_inst_l_81_2726249e), .X82(Decoder_inst_l_82_298ac22b),
    .X83(Decoder_inst_l_83_79a418b7), .X84(Decoder_inst_l_84_e79a1766), .X3(Decoder_inst_l_3_39a566ac),
    .X85(Decoder_inst_l_85_b2daf010), .X86(Decoder_inst_l_86_b98cc819), .X87(Decoder_inst_l_87_c637b311),
    .X88(Decoder_inst_l_88_055bb603), .X89(Decoder_inst_l_89_5d5fe4c7), .X90(Decoder_inst_l_90_55afaa76),
    .X91(Decoder_inst_l_91_d03b9369), .X92(Decoder_inst_l_92_0cc1d36a), .X93(Decoder_inst_l_93_eaf60893),
    .X4(Decoder_inst_l_4_558283f2), .X94(Decoder_inst_l_94_95326b03), .X95(Decoder_inst_l_95_f060a0fd),
    .X96(Decoder_inst_l_96_3d015798), .X97(Decoder_inst_l_97_f3e813cd), .X98(Decoder_inst_l_98_f4cee2ae),
    .X99(Decoder_inst_l_99_bb939962), .X100(Decoder_inst_l_100_16b00339), .X101(Decoder_inst_l_101_c09bb9ac),
    .X102(Decoder_inst_l_102_614a85bf), .X5(Decoder_inst_l_5_9518e519), .X103(Decoder_inst_l_103_52940b9a),
    .X104(Decoder_inst_l_104_443c5ff0), .X105(Decoder_inst_l_105_5ce959fd),
    .X106(Decoder_inst_l_106_2a9581c6), .X107(Decoder_inst_l_107_a96ffaba),
    .X108(Decoder_inst_l_108_c205b5ff), .X109(Decoder_inst_l_109_2fe88a94),
    .X110(Decoder_inst_l_110_4cc555bd), .X111(Decoder_inst_l_111_2b81c3c9), .X6(Decoder_inst_l_6_5b7e39b9),
    .X112(Decoder_inst_l_112_708a0f10), .X113(Decoder_inst_l_113_fbaa75ad),
    .X114(Decoder_inst_l_114_f9625e87), .X115(Decoder_inst_l_115_b1986fe2),
    .X116(Decoder_inst_l_116_0ba24dc4), .X117(Decoder_inst_l_117_10a3c8b1),
    .X118(Decoder_inst_l_118_e0e8abfe), .X119(Decoder_inst_l_119_86db347d),
    .X120(Decoder_inst_l_120_c53a083f), .X7(Decoder_inst_l_7_14ab2533), .X121(Decoder_inst_l_121_da158f44),
    .X122(Decoder_inst_l_122_0e8f1988), .X123(Decoder_inst_l_123_a8638cda),
    .X124(Decoder_inst_l_124_8d81fffd), .X125(Decoder_inst_l_125_8f968e43),
    .X126(Decoder_inst_l_126_7e3003c6), .X127(Decoder_inst_l_127_28942974),
    .X128(Decoder_inst_l_128_23d7200b), .X129(Decoder_inst_l_129_7b5e5edf), .X8(Decoder_inst_l_8_05eb4f56),
    .in_143(Random_inst_db0[7]), .DB6(Random_inst_db0[6]), .DB5(Random_inst_db0[5]),
    .in_146(Random_inst_db0[4]), .DB3(Random_inst_db0[3]), .X9(Decoder_inst_l_9_0082242d),
    .in_148(Random_inst_db0[2]), .PHI2(PHI2), .L_IR5_9e15d54c(not_3_out), .PHI1(PHI1),
    .L_TWOCYCLE_54b4f369(PD_inst_n_twocycle), .L_IMPLIED_b029c4af(PD_inst_n_implied), .RDY(RDY_Latch2_not_q),
    .DB1(Random_inst_db0[1]), .in_150(Random_inst_db0[0]), .X10(Decoder_inst_l_10_57b0d741),
    .X11(Decoder_inst_l_11_aa2e7fa3), .X12(Decoder_inst_l_12_85a3418f), .X13(Decoder_inst_l_13_587da886),
    .X14(Decoder_inst_l_14_4f483598), .X15(Decoder_inst_l_15_5dad5732), .X16(Decoder_inst_l_16_c7396848),
    .X17(Decoder_inst_l_17_0f5278c7), .X18(Decoder_inst_l_18_4ab117a9), .X19(Decoder_inst_l_19_e094c090),
    .X20(Decoder_inst_l_20_adeacd1b), .X21(Decoder_inst_l_21_ada5c31c), .X22(Decoder_inst_l_22_f545d19e),
    .X23(Decoder_inst_l_23_d0835dd9), .X24(Decoder_inst_l_24_b6efc2f4));
  not not_1 (not_1_out, NMI_FF_qn);
  ABL ABL_inst (
    .A0(A0), .A1(A1), .A2(A2), .A3(A3), .A4(A4), .A5(A5), .A6(A6), .A7(A7),
    .ADL_ABL(Random_inst_adl_abl_5bea59e2[0]), .L_0_ADL0(Random_inst_adl_abl_5bea59e2[2]),
    .L_0_ADL1(Random_inst_adl_abl_5bea59e2[3]), .L_0_ADL2(Random_inst_adl_abl_5bea59e2[4]),
    .ADL0(REGS_inst_adl0[0]), .PHI1(PHI1), .ADL1(REGS_inst_adl0[1]), .ADL2(REGS_inst_adl0[2]),
    .ADL3(REGS_inst_adl0[3]), .ADL4(REGS_inst_adl0[4]), .ADL5(REGS_inst_adl0[5]), .ADL6(REGS_inst_adl0[6]),
    .ADL7(REGS_inst_adl0[7]), .PHI2(PHI2));
  ABH ABH_inst (
    .A8(A8), .A9(A9), .A10(A10), .A11(A11), .A12(A12), .A13(A13), .A14(A14), .A15(A15),
    .ADH0(ALU_inst_adh0[0]), .ADH1(ALU_inst_adh0[1]), .ADH2(ALU_inst_adh0[2]), .PHI1(PHI1),
    .ADH3(ALU_inst_adh0[3]), .ADH4(ALU_inst_adh0[4]), .ADH5(ALU_inst_adh0[5]), .ADH6(ALU_inst_adh0[6]),
    .ADH7(ALU_inst_adh0[7]), .PHI2(PHI2), .ADH_ABH(Random_inst_adl_abl_5bea59e2[1]));
  D_Flip_Flop #(.trigger("high")) IRQ_FF (.D(n_IRQ), .clk(PHI2), .Qn(IRQ_FF_qn));  // open: Q, preset, reset
  D_Latch IRQ_Latch (.NOT_Q(IRQ_Latch_not_q), .D(IRQ_FF_qn), .EN(PHI1));  // open: Q
  Register #(.trigger("high")) X_Dbg (.D(REGS_inst_x_debug), .en(1'b1), .clk(1'b1));  // open: Q, clr
  REGS REGS_inst (
    .S_Debug(REGS_inst_s_debug), .SB1_Out(REGS_inst_sb0_out[1]), .SB2_Out(REGS_inst_sb0_out[2]),
    .SB3_Out(REGS_inst_sb0_out[3]), .SB4_Out(REGS_inst_sb0_out[4]), .SB5_Out(REGS_inst_sb0_out[5]),
    .SB6_Out(REGS_inst_sb0_out[6]), .SB7_Out(REGS_inst_sb0_out[7]), .ADL0(REGS_inst_adl0[0]),
    .ADL1(REGS_inst_adl0[1]), .ADL2(REGS_inst_adl0[2]), .ADL3(REGS_inst_adl0[3]), .ADL4(REGS_inst_adl0[4]),
    .ADL5(REGS_inst_adl0[5]), .ADL6(REGS_inst_adl0[6]), .ADL7(REGS_inst_adl0[7]),
    .SB0_Out(REGS_inst_sb0_out[0]), .Y_Debug(REGS_inst_y_debug), .X_Debug(REGS_inst_x_debug),
    .Y_SB(Random_inst_y_sb_d628d28f[0]), .SB_Y(Random_inst_y_sb_d628d28f[1]),
    .X_SB(Random_inst_y_sb_d628d28f[2]), .SB_X(Random_inst_y_sb_d628d28f[3]),
    .S_ADL(Random_inst_y_sb_d628d28f[4]), .S_S(Random_inst_y_sb_d628d28f[5]),
    .SB_S(Random_inst_y_sb_d628d28f[6]), .S_SB(Random_inst_y_sb_d628d28f[7]), .SB0_In(REGS_inst_sb0_out[0]),
    .SB1_In(REGS_inst_sb0_out[1]), .SB2_In(REGS_inst_sb0_out[2]), .SB3_In(REGS_inst_sb0_out[3]),
    .SB4_In(REGS_inst_sb0_out[4]), .SB5_In(REGS_inst_sb0_out[5]), .SB6_In(REGS_inst_sb0_out[6]), .PHI2(PHI2),
    .SB7_In(REGS_inst_sb0_out[7]));
  Register #(.trigger("high")) Y_Dbg (.D(REGS_inst_y_debug), .en(1'b1), .clk(1'b1));  // open: Q, clr
  Register #(.trigger("high")) S_Dbg (.D(REGS_inst_s_debug), .en(1'b1), .clk(1'b1));  // open: Q, clr
  not not_2 (not_2_out, RDY);
  Register #(.trigger("high")) AI_Dbg (.D(ALU_inst_ai_debug), .en(1'b1), .clk(1'b1));  // open: Q, clr
  D_Latch RDY_Latch1 (.NOT_Q(RDY_Latch1_not_q), .D(not_2_out), .EN(PHI2));  // open: Q
  ALU ALU_inst (
    .SB4(REGS_inst_sb0_out[4]), .out_75(REGS_inst_sb0_out[5]), .out_79(REGS_inst_sb0_out[6]),
    .SB7(REGS_inst_sb0_out[7]), .out_55(REGS_inst_sb0_out[0]), .SB1(REGS_inst_sb0_out[1]),
    .out_63(REGS_inst_sb0_out[2]), .out_67(REGS_inst_sb0_out[3]), .DB4(Random_inst_db0[4]),
    .out_76(Random_inst_db0[5]), .out_80(Random_inst_db0[6]), .DB7(Random_inst_db0[7]),
    .DB0(Random_inst_db0[0]), .out_60(Random_inst_db0[1]), .DB2(Random_inst_db0[2]),
    .DB3(Random_inst_db0[3]), .ADL4(REGS_inst_adl0[4]), .out_77(REGS_inst_adl0[5]), .ADL6(REGS_inst_adl0[6]),
    .out_85(REGS_inst_adl0[7]), .out_57(REGS_inst_adl0[0]), .out_61(REGS_inst_adl0[1]),
    .ADL2(REGS_inst_adl0[2]), .out_69(REGS_inst_adl0[3]), .AC_Debug(ALU_inst_ac_debug),
    .ADH4(ALU_inst_adh0[4]), .ADH5(ALU_inst_adh0[5]), .ADH6(ALU_inst_adh0[6]), .ADH7(ALU_inst_adh0[7]),
    .ADH0(ALU_inst_adh0[0]), .ADH1(ALU_inst_adh0[1]), .ADH2(ALU_inst_adh0[2]), .ADH3(ALU_inst_adh0[3]),
    .AVR(ALU_inst_avr), .ACR(ALU_inst_acr), .AI_Debug(ALU_inst_ai_debug), .BI_Debug(ALU_inst_bi_debug),
    .ADD_Debug(ALU_inst_add_debug), .in_37(REGS_inst_sb0_out[4]), .SB5(REGS_inst_sb0_out[5]),
    .SB6(REGS_inst_sb0_out[6]), .NDB_ADD_ee0a1870(Random_inst_ndb_add_ee0a1870[0]),
    .in_46(REGS_inst_sb0_out[7]), .DB_ADD_48d85b7e(Random_inst_ndb_add_ee0a1870[1]),
    .L_0_ADD_81d17e61(Random_inst_ndb_add_ee0a1870[2]), .PHI2(PHI2),
    .SB_ADD_0eab26ac(Random_inst_ndb_add_ee0a1870[3]), .ADL_ADD_e28b8a30(Random_inst_ndb_add_ee0a1870[4]),
    .ADD_SB06_a3738230(Random_inst_ndb_add_ee0a1870[5]), .ADD_SB7_a8f4b77a(Random_inst_ndb_add_ee0a1870[6]),
    .ADD_ADL_3fac4345(Random_inst_ndb_add_ee0a1870[7]), .ANDS(Random_inst_ndb_add_ee0a1870[8]),
    .EORS(Random_inst_ndb_add_ee0a1870[9]), .ORS(Random_inst_ndb_add_ee0a1870[10]),
    .SRS(Random_inst_ndb_add_ee0a1870[11]), .SUMS(Random_inst_ndb_add_ee0a1870[12]),
    .SB_AC_b159eec5(Random_inst_sb_ac_b159eec5[0]), .AC_SB_c49f602a(Random_inst_sb_ac_b159eec5[1]),
    .AC_DB_519ce409(Random_inst_sb_ac_b159eec5[2]), .SB_DB_641efa5a(Random_inst_sb_ac_b159eec5[3]),
    .SB_ADH_4f1456ff(Random_inst_sb_ac_b159eec5[4]), .L_0_ADH0_e340c71e(Random_inst_sb_ac_b159eec5[5]),
    .L_0_ADH17_f181a8fa(Random_inst_sb_ac_b159eec5[6]), .n_ACIN(Random_inst_l_acin_e173f520[0]),
    .n_DAA(Random_inst_l_acin_e173f520[1]), .n_DSA(Random_inst_l_acin_e173f520[2]),
    .SB0(REGS_inst_sb0_out[0]), .in_28(REGS_inst_sb0_out[1]), .SB2(REGS_inst_sb0_out[2]),
    .SB3(REGS_inst_sb0_out[3]), .in_38(Random_inst_db0[4]), .DB5(Random_inst_db0[5]),
    .DB6(Random_inst_db0[6]), .in_47(Random_inst_db0[7]), .in_26(Random_inst_db0[0]),
    .DB1(Random_inst_db0[1]), .in_32(Random_inst_db0[2]), .in_35(Random_inst_db0[3]),
    .in_39(REGS_inst_adl0[4]), .ADL5(REGS_inst_adl0[5]), .in_45(REGS_inst_adl0[6]), .ADL7(REGS_inst_adl0[7]),
    .ADL0(REGS_inst_adl0[0]), .ADL1(REGS_inst_adl0[1]), .in_33(REGS_inst_adl0[2]), .ADL3(REGS_inst_adl0[3]));
  Register #(.trigger("high")) BI_Dbg (.D(ALU_inst_bi_debug), .en(1'b1), .clk(1'b1));  // open: Q, clr
  D_Flip_Flop #(.trigger("high")) RES_FF (.D(n_RES), .clk(PHI2), .Q(RES_FF_q));  // open: Qn, preset, reset
  D_Latch RDY_Latch2 (.NOT_Q(RDY_Latch2_not_q), .D(RDY_Latch1_not_q), .EN(PHI1));  // open: Q
  Register #(.trigger("high")) ADD_Dbg (.D(ALU_inst_add_debug), .en(1'b1), .clk(1'b1));  // open: Q, clr
  Register #(.trigger("high")) AC_Dbg (.D(ALU_inst_ac_debug), .en(1'b1), .clk(1'b1));  // open: Q, clr
  D_Latch RES_Latch (.NOT_Q(RES_Latch_not_q), .D(RES_FF_q), .EN(PHI1));  // open: Q
  PC PC_inst (
    .DB2(Random_inst_db0[2]), .DB3(Random_inst_db0[3]), .DB4(Random_inst_db0[4]), .DB5(Random_inst_db0[5]),
    .DB6(Random_inst_db0[6]), .DB7(Random_inst_db0[7]), .ADL0_Out(REGS_inst_adl0[0]),
    .ADL1_Out(REGS_inst_adl0[1]), .ADL2_Out(REGS_inst_adl0[2]), .ADL3_Out(REGS_inst_adl0[3]),
    .ADL4_Out(REGS_inst_adl0[4]), .ADL5_Out(REGS_inst_adl0[5]), .ADL6_Out(REGS_inst_adl0[6]),
    .DB0(Random_inst_db0[0]), .ADL7_Out(REGS_inst_adl0[7]), .ADH0_Out(ALU_inst_adh0[0]),
    .ADH1_Out(ALU_inst_adh0[1]), .ADH2_Out(ALU_inst_adh0[2]), .ADH3_Out(ALU_inst_adh0[3]),
    .ADH4_Out(ALU_inst_adh0[4]), .ADH5_Out(ALU_inst_adh0[5]), .ADH6_Out(ALU_inst_adh0[6]),
    .ADH7_Out(ALU_inst_adh0[7]), .DB1(Random_inst_db0[1]), .PC_Debug(PC_inst_pc_debug),
    .PCS_Debug(PC_inst_pcs_debug), .ADL_PCL_9a95c372(Random_inst_adh_pch_61520abf[4]),
    .PCL_PCL_4f350f4d(Random_inst_adh_pch_61520abf[5]), .PCL_ADL_ee043dbc(Random_inst_adh_pch_61520abf[6]),
    .PCL_DB_4172714e(Random_inst_adh_pch_61520abf[7]), .ADH_PCH_61520abf(Random_inst_adh_pch_61520abf[0]),
    .PCH_PCH_807b9fbd(Random_inst_adh_pch_61520abf[1]), .PCH_ADH_ead93594(Random_inst_adh_pch_61520abf[2]),
    .PCH_DB_a81fefa0(Random_inst_adh_pch_61520abf[3]), .n_1_PC(Random_inst_adh_pch_61520abf[8]), .PHI2(PHI2),
    .ADL0_In(REGS_inst_adl0[0]), .ADL1_In(REGS_inst_adl0[1]), .ADL2_In(REGS_inst_adl0[2]),
    .ADL3_In(REGS_inst_adl0[3]), .ADL4_In(REGS_inst_adl0[4]), .ADL5_In(REGS_inst_adl0[5]),
    .ADL6_In(REGS_inst_adl0[6]), .ADL7_In(REGS_inst_adl0[7]), .ADH0_In(ALU_inst_adh0[0]),
    .ADH1_In(ALU_inst_adh0[1]), .ADH2_In(ALU_inst_adh0[2]), .ADH3_In(ALU_inst_adh0[3]),
    .ADH4_In(ALU_inst_adh0[4]), .ADH5_In(ALU_inst_adh0[5]), .ADH6_In(ALU_inst_adh0[6]),
    .ADH7_In(ALU_inst_adh0[7]));
  Register #(.trigger("high"), .width(16)) PC_Dbg (.D(PC_inst_pc_debug), .en(1'b1), .clk(1'b1));  // open: Q, clr
  Register #(.trigger("high"), .width(16)) PCS_Dbg (.D(PC_inst_pcs_debug), .en(1'b1), .clk(1'b1));  // open: Q, clr
  CLOCKGEN CLK_Gen (.PHI2(PHI2), .PHI1(PHI1), .PHI0(PHI0_out));
  Clock PHI0 (.out(PHI0_out));
  not not_3 (not_3_out, IR_inst_ir5);
  DL DL_inst (
    .D6_Out(D6_OUT), .D7_Out(D7_OUT), .DB2_Out(Random_inst_db0[2]), .DB3_Out(Random_inst_db0[3]),
    .DB4_Out(Random_inst_db0[4]), .DB5_Out(Random_inst_db0[5]), .DB6_Out(Random_inst_db0[6]),
    .DB7_Out(Random_inst_db0[7]), .ADL0(REGS_inst_adl0[0]), .ADL1(REGS_inst_adl0[1]),
    .ADL2(REGS_inst_adl0[2]), .ADL3(REGS_inst_adl0[3]), .ADL4(REGS_inst_adl0[4]), .ADL5(REGS_inst_adl0[5]),
    .ADL6(REGS_inst_adl0[6]), .ADL7(REGS_inst_adl0[7]), .ADH0(ALU_inst_adh0[0]),
    .DB0_Out(Random_inst_db0[0]), .ADH1(ALU_inst_adh0[1]), .ADH2(ALU_inst_adh0[2]), .ADH3(ALU_inst_adh0[3]),
    .ADH4(ALU_inst_adh0[4]), .ADH5(ALU_inst_adh0[5]), .ADH6(ALU_inst_adh0[6]), .ADH7(ALU_inst_adh0[7]),
    .D0_Out(D0_OUT), .D1_Out(D1_OUT), .D2_Out(D2_OUT), .DB1_Out(Random_inst_db0[1]), .D3_Out(D3_OUT),
    .D4_Out(D4_OUT), .D5_Out(D5_OUT), .DL_Debug(DL_inst_dl_debug), .DOR_Debug(DL_inst_dor_debug),
    .WR(Random_inst_wr), .DL_ADL_6c5e0116(Random_inst_dl_adl_6c5e0116[0]),
    .DL_ADH_3839a3d0(Random_inst_dl_adl_6c5e0116[2]), .DL_DB_69522204(Random_inst_dl_adl_6c5e0116[1]),
    .DB0_In(Random_inst_db0[0]), .DB1_In(Random_inst_db0[1]), .DB2_In(Random_inst_db0[2]),
    .DB3_In(Random_inst_db0[3]), .DB4_In(Random_inst_db0[4]), .DB5_In(Random_inst_db0[5]), .PHI1(PHI1),
    .DB6_In(Random_inst_db0[6]), .DB7_In(Random_inst_db0[7]), .D0_In(D0_IN), .D1_In(D1_IN), .D2_In(D2_IN),
    .D3_In(D3_IN), .D4_In(D4_IN), .PHI2(PHI2), .D5_In(D5_IN), .D6_In(D6_IN), .D7_In(D7_IN));
  Register #(.trigger("high")) DL_Dbg (.D(DL_inst_dl_debug), .en(1'b1), .clk(1'b1));  // open: Q, clr
  D_Latch RWLatch (.NOT_Q(R_W), .D(Random_inst_wr), .EN(PHI1));  // open: Q
  IR IR_inst (
    .IR0(IR_inst_ir0), .IR1(IR_inst_ir1), .IR2(IR_inst_ir2), .IR3(IR_inst_ir3), .IR4(IR_inst_ir4),
    .IR5(IR_inst_ir5), .IR6(IR_inst_ir6), .IR7(IR_inst_ir7), .L_in0_dea3fa9c(PD_inst_n_pd0),
    .L_in1_3405e045(PD_inst_n_pd1), .L_in2_d55e1188(PD_inst_n_pd2), .L_in3_e63baf83(PD_inst_n_pd3),
    .L_in4_b1b51af8(PD_inst_n_pd4), .L_in5_af1dd408(PD_inst_n_pd5), .L_in6_328834da(PD_inst_n_pd6),
    .L_in7_b8770e13(PD_inst_n_pd7), .FETCH(Random_inst_fetch), .PHI1(PHI1));
  Register #(.trigger("high")) DOR_Dbg (.D(DL_inst_dor_debug), .en(1'b1), .clk(1'b1));  // open: Q, clr
  PREDECODE PD_inst (
    .n_TWOCYCLE(PD_inst_n_twocycle), .n_IMPLIED(PD_inst_n_implied), .n_PD0(PD_inst_n_pd0),
    .n_PD1(PD_inst_n_pd1), .n_PD2(PD_inst_n_pd2), .n_PD3(PD_inst_n_pd3), .n_PD4(PD_inst_n_pd4),
    .n_PD5(PD_inst_n_pd5), .n_PD6(PD_inst_n_pd6), .n_PD7(PD_inst_n_pd7), .D0(D0_IN), .PHI2(PHI2), .D1(D1_IN),
    .D2(D2_IN), .D3(D3_IN), .D4(D4_IN), .D5(D5_IN), .ZERO_IR(Random_inst_l_0_ir_c32b8001), .D6(D6_IN),
    .D7(D7_IN));

  // Notes on the sheet:
  //   PHI2
  //   PHI1
  //   PHI1
  //   PHI2
  //   T1
  //   The pin layout corresponds to the real chip
  //   /NMIP
  //   ADH
  //   ADL
  //   /IRQP
  //   DB
  //   SB
  //   DEBUG
  //   /RDY
  //   DEBUG
  //   RESP
  //   DEBUG
  //   PHI2
  //   PHI1
  //   WR
  //   DEBUG
  //   PHI1
  //   PHI2
endmodule

module CLOCKGEN (
  input  PHI0,
  output PHI2,
  output PHI1
);

  wire not_1_out;

  not not_1 (not_1_out, PHI0);
  not not_2 (PHI2, not_1_out);
  not not_3 (PHI1, PHI0);
endmodule

module IR (
  input  FETCH,
  input  PHI1,
  input  L_in0_dea3fa9c,
  input  L_in1_3405e045,
  input  L_in2_d55e1188,
  input  L_in3_e63baf83,
  input  L_in4_b1b51af8,
  input  L_in5_af1dd408,
  input  L_in6_328834da,
  input  L_in7_b8770e13,
  output IR0,
  output IR1,
  output IR2,
  output IR3,
  output IR4,
  output IR5,
  output IR6,
  output IR7
);

  wire and1_out;

  and and1 (and1_out, FETCH, PHI1);
  D_Latch d_latch_1 (.NOT_Q(IR0), .D(L_in0_dea3fa9c), .EN(and1_out));  // open: Q
  D_Latch d_latch_2 (.NOT_Q(IR1), .D(L_in1_3405e045), .EN(and1_out));  // open: Q
  D_Latch d_latch_3 (.NOT_Q(IR2), .D(L_in2_d55e1188), .EN(and1_out));  // open: Q
  D_Latch d_latch_4 (.NOT_Q(IR3), .D(L_in3_e63baf83), .EN(and1_out));  // open: Q
  D_Latch d_latch_5 (.NOT_Q(IR4), .D(L_in4_b1b51af8), .EN(and1_out));  // open: Q
  D_Latch d_latch_6 (.NOT_Q(IR5), .D(L_in5_af1dd408), .EN(and1_out));  // open: Q
  D_Latch d_latch_7 (.NOT_Q(IR6), .D(L_in6_328834da), .EN(and1_out));  // open: Q
  D_Latch d_latch_8 (.NOT_Q(IR7), .D(L_in7_b8770e13), .EN(and1_out));  // open: Q
endmodule
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module INT_RESET_CONTROL (
  input  PHI1,
  input  PHI2,
  input  BRK5,
  input  n_READY,
  input  RESP,
  input  n_NMIP,
  input  BR2,
  input  T0,
  input  n_IRQP,
  input  n_I_OUT,
  output BRK6E,
  output BRK7,
  output DORES,
  output n_DONMI,
  output B_OUT
);

  wire and_1_out, and_2_out, and_3_out, and_4_out, and_5_out, d_latch_1_q, d_latch_2_q, d_latch_3_q,
       d_latch_4_not_q, d_latch_5_q, d_latch_6_not_q, d_latch_7_q, d_latch_8_q, d_latch_9_q, d_latch_10_q,
       d_latch_11_q, d_latch_12_not_q, d_latch_13_q, d_latch_14_not_q, d_latch_15_q, nand_1_out, nor_1_out,
       nor_2_out, nor_3_out, nor_4_out, nor_5_out, nor_6_out, nor_7_out, nor_9_out, nor_10_out, not_1_out,
       not_2_out, not_3_out, not_4_out, not_5_out, not_6_out, not_7_out, not_8_out, or_1_out, or_2_out;

  and and_1 (and_1_out, BRK5, not_1_out);
  not not_1 (not_1_out, n_READY);
  not not_2 (not_2_out, n_READY);
  and and_2 (and_2_out, not_2_out, BRK6E);
  and and_3 (and_3_out, n_I_OUT, not_3_out);
  not not_3 (not_3_out, BRK6E);
  D_Latch d_latch_1 (.Q(d_latch_1_q), .D(and_1_out), .EN(PHI2));  // open: NOT_Q
  D_Latch d_latch_2 (.Q(d_latch_2_q), .D(RESP), .EN(PHI2));  // open: NOT_Q
  D_Latch d_latch_3 (.Q(d_latch_3_q), .D(nor_5_out), .EN(PHI1));  // open: NOT_Q
  D_Latch d_latch_4 (.NOT_Q(d_latch_4_not_q), .D(BRK7), .EN(PHI2));  // open: Q
  D_Latch d_latch_5 (.Q(d_latch_5_q), .D(n_NMIP), .EN(PHI1));  // open: NOT_Q
  D_Latch d_latch_6 (.NOT_Q(d_latch_6_not_q), .D(n_DONMI), .EN(PHI2));  // open: Q
  D_Latch d_latch_7 (.Q(d_latch_7_q), .D(n_DONMI), .EN(PHI2));  // open: NOT_Q
  D_Latch d_latch_8 (.Q(d_latch_8_q), .D(and_2_out), .EN(PHI1));  // open: NOT_Q
  not not_4 (not_4_out, and_3_out);
  D_Latch d_latch_9 (.Q(d_latch_9_q), .D(nor_10_out), .EN(PHI1));  // open: NOT_Q
  not not_5 (not_5_out, d_latch_9_q);
  not not_6 (not_6_out, d_latch_1_q);
  and and_4 (and_4_out, not_6_out, nand_1_out);
  nand nand_1 (nand_1_out, n_READY, d_latch_12_not_q);
  nor nor_1 (nor_1_out, d_latch_2_q, d_latch_3_q);
  nor nor_2 (nor_2_out, d_latch_5_q, nor_7_out);
  D_Latch d_latch_10 (.Q(d_latch_10_q), .D(nor_2_out), .EN(PHI1));  // open: NOT_Q
  D_Latch d_latch_11 (.Q(d_latch_11_q), .D(d_latch_6_not_q), .EN(PHI1));  // open: NOT_Q
  nor nor_3 (nor_3_out, d_latch_7_q, d_latch_8_q);
  nor nor_4 (nor_4_out, n_IRQP, not_4_out);
  not not_7 (not_7_out, n_DONMI);
  and and_5 (and_5_out, or_2_out, not_5_out);
  D_Latch d_latch_12 (.NOT_Q(d_latch_12_not_q), .D(and_4_out), .EN(PHI1));  // open: Q
  nor nor_5 (nor_5_out, nor_1_out, BRK6E);
  nor nor_6 (nor_6_out, d_latch_4_not_q, n_NMIP, nor_2_out);
  nor nor_7 (nor_7_out, d_latch_10_q, d_latch_11_q);
  nor nor_8 (n_DONMI, d_latch_15_q, nor_3_out);
  nor nor_9 (nor_9_out, BR2, T0);
  or or_1 (or_1_out, nor_4_out, not_7_out);
  not not_8 (not_8_out, or_1_out);
  D_Latch d_latch_13 (.Q(d_latch_13_q), .D(and_5_out), .EN(PHI2));  // open: NOT_Q
  not not_9 (DORES, nor_1_out);
  or or_2 (or_2_out, nor_9_out, not_8_out);
  nor nor_10 (nor_10_out, d_latch_13_q, BRK6E);
  D_Latch d_latch_14 (.NOT_Q(d_latch_14_not_q), .D(d_latch_12_not_q), .EN(PHI2));  // open: Q
  not not_10 (BRK6E, d_latch_14_not_q);
  nor nor_11 (BRK7, d_latch_12_not_q, and_1_out);
  D_Latch d_latch_15 (.Q(d_latch_15_q), .D(nor_6_out), .EN(PHI1));  // open: NOT_Q
  nor nor_12 (B_OUT, DORES, nor_10_out);

  // Other names for the same wires on the sheet: L_ready_9a3f8f92 = n_READY

  // Notes on the sheet:
  //   /NMIP
  //   /I_OUT
  //   /IRQP
  //   INTERRUPT CYCLE 6-7
  //   RESET FLIP/FLOP
  //   NMI EDGE DETECT
  //   INTERRUPT CHECK
  //   BR2
  //   T0
  //   B FLAG
  //   /DONMI
  //   /DONMI
endmodule

module INT_VECTOR (
  input  PHI2,
  input  BRK5,
  input  BRK7,
  input  DORES,
  input  L_DONMI_29470de9,
  output L_0_ADL0_f8fabdab,
  output L_0_ADL1_4e9a6ca8,
  output L_0_ADL2_2c4a79f4
);

  wire nor_1_out, nor_2_out, not_1_out, not_2_out, not_3_out;

  not not_1 (not_1_out, DORES);
  not not_2 (not_2_out, BRK5);
  nor nor_1 (nor_1_out, BRK7, not_1_out);
  not not_3 (not_3_out, nor_1_out);
  nor nor_2 (nor_2_out, BRK7, DORES, L_DONMI_29470de9);
  D_Latch d_latch_1 (.NOT_Q(L_0_ADL0_f8fabdab), .D(not_2_out), .EN(PHI2));  // open: Q
  D_Latch d_latch_2 (.NOT_Q(L_0_ADL1_4e9a6ca8), .D(not_3_out), .EN(PHI2));  // open: Q
  D_Latch d_latch_3 (.Q(L_0_ADL2_2c4a79f4), .D(nor_2_out), .EN(PHI2));  // open: NOT_Q

  // Notes on the sheet:
  //   FFFA:NMI, 1010
  //   FFFC:RESET, 1100
  //   FFFE:IRQ/BRK, 1110
endmodule

module REGS_CONTROL (
  input  PHI1,
  input  PHI2,
  input  STOR,
  input  L_0_090b2452,
  input  L_1_28cbbb7d,
  input  in_6,
  input  L_3_39a566ac,
  input  in_8,
  input  L_5_9518e519,
  input  L_6_5b7e39b9,
  input  L_7_14ab2533,
  input  L_8_05eb4f56,
  input  L_9_0082242d,
  input  L_10_57b0d741,
  input  in_15,
  input  L_12_85a3418f,
  input  in_17,
  input  in_18,
  input  L_15_5dad5732,
  input  L_16_c7396848,
  input  _12,
  input  L_18_4ab117a9,
  input  L_19_e094c090,
  input  L_20_adeacd1b,
  input  L_21_ada5c31c,
  input  L_22_f545d19e,
  input  L_23_d0835dd9,
  input  L_24_b6efc2f4,
  input  L_25_f5ad6aee,
  input  L_26_ffeee2da,
  input  L_48_330a6f3f,
  input  L_READY_a37d69a3,
  input  D35,
  output Y_SB_d628d28f,
  output STXY,
  output X_SB_222038db,
  output S_SB_e37affed,
  output SB_X_cf392641,
  output SBXY,
  output SB_Y_9a33ae5e,
  output SB_S_4c94ee46,
  output S_S_09f08a69,
  output STKOP,
  output S_ADL_07acd992
);

  wire and_1_out, and_2_out, and_3_out, and_4_out, and_5_out, and_6_out, buffer_1_out, buffer_2_out,
       buffer_4_out, buffer_5_out, buffer_6_out, buffer_7_out, d_latch_1_q, d_latch_2_not_q, d_latch_3_not_q,
       d_latch_4_not_q, d_latch_5_not_q, d_latch_6_not_q, d_latch_7_not_q, d_latch_8_not_q, d_latch_9_not_q,
       L_2_143403ae_out, L_4_558283f2_out, L_13_587da886_out, L_14_4f483598_out, L_17_0f5278c7_out,
       nor_1_out, nor_2_out, nor_3_out, nor_6_out, nor_7_out, nor_8_out, nor_9_out, nor_10_out, nor_11_out,
       nor_12_out, not_1_out, not_2_out, not_3_out, not_4_out;

  not not_1 (not_1_out, L_7_14ab2533);
  nor nor_1 (nor_1_out, in_18, L_15_5dad5732, L_16_c7396848);
  not not_2 (not_2_out, _12);
  nor nor_2 (nor_2_out, L_18_4ab117a9, L_19_e094c090, L_20_adeacd1b);
  not not_3 (not_3_out, L_48_330a6f3f);
  and and_1 (and_1_out, L_6_5b7e39b9, L_7_14ab2533);
  and and_2 (and_2_out, L_6_5b7e39b9, not_1_out);
  nor L_13_587da886 (L_13_587da886_out, L_21_ada5c31c, L_22_f545d19e, L_23_d0835dd9, L_24_b6efc2f4, L_25_f5ad6aee, L_26_ffeee2da);
  D_Latch d_latch_1 (.Q(d_latch_1_q), .D(L_READY_a37d69a3), .EN(PHI1));  // open: NOT_Q
  nor L_17_0f5278c7 (L_17_0f5278c7_out, not_3_out, L_READY_a37d69a3);
  nor nor_3 (nor_3_out, L_1_28cbbb7d, in_6, L_3_39a566ac, in_8, L_5_9518e519, and_1_out, and_3_out);
  and and_3 (and_3_out, L_0_090b2452, STOR);
  and and_4 (and_4_out, STOR, L_12_85a3418f);
  nor L_2_143403ae (L_2_143403ae_out, and_4_out, and_2_out, L_8_05eb4f56, L_9_0082242d, L_10_57b0d741, in_15, in_17);
  and and_5 (and_5_out, L_21_ada5c31c, d_latch_1_q);
  nor nor_4 (STKOP, L_13_587da886_out, d_latch_1_q);
  and L_4_558283f2 (L_4_558283f2_out, L_0_090b2452, STOR);
  and and_6 (and_6_out, STOR, L_12_85a3418f);
  nor nor_5 (STXY, L_4_558283f2_out, and_6_out);
  nand L_11_aa2e7fa3 (SBXY, nor_1_out, nor_2_out);
  nor nor_6 (nor_6_out, in_17, STKOP, L_17_0f5278c7_out);
  nor L_14_4f483598 (L_14_4f483598_out, and_5_out, D35);
  not not_4 (not_4_out, nor_6_out);
  D_Latch d_latch_2 (.NOT_Q(d_latch_2_not_q), .D(nor_3_out), .EN(PHI2));  // open: Q
  D_Latch d_latch_3 (.NOT_Q(d_latch_3_not_q), .D(L_2_143403ae_out), .EN(PHI2));  // open: Q
  D_Latch d_latch_4 (.NOT_Q(d_latch_4_not_q), .D(not_2_out), .EN(PHI2));  // open: Q
  D_Latch d_latch_5 (.NOT_Q(d_latch_5_not_q), .D(nor_1_out), .EN(PHI2));  // open: Q
  D_Latch d_latch_6 (.NOT_Q(d_latch_6_not_q), .D(nor_2_out), .EN(PHI2));  // open: Q
  D_Latch d_latch_7 (.NOT_Q(d_latch_7_not_q), .D(nor_6_out), .EN(PHI2));  // open: Q
  D_Latch d_latch_8 (.NOT_Q(d_latch_8_not_q), .D(not_4_out), .EN(PHI2));  // open: Q
  D_Latch d_latch_9 (.NOT_Q(d_latch_9_not_q), .D(L_14_4f483598_out), .EN(PHI2));  // open: Q
  nor nor_7 (nor_7_out, PHI2, d_latch_2_not_q);
  buf buffer_1 (buffer_1_out, nor_7_out);
  nor nor_8 (nor_8_out, PHI2, d_latch_3_not_q);
  buf buffer_2 (buffer_2_out, nor_8_out);
  buf buffer_3 (S_SB_e37affed, d_latch_4_not_q);
  nor nor_9 (nor_9_out, PHI2, d_latch_5_not_q);
  buf buffer_4 (buffer_4_out, nor_9_out);
  nor nor_10 (nor_10_out, PHI2, d_latch_6_not_q);
  buf buffer_5 (buffer_5_out, nor_10_out);
  nor nor_11 (nor_11_out, PHI2, d_latch_7_not_q);
  buf buffer_6 (buffer_6_out, nor_11_out);
  nor nor_12 (nor_12_out, PHI2, d_latch_8_not_q);
  buf buffer_7 (buffer_7_out, nor_12_out);
  buf buffer_8 (S_ADL_07acd992, d_latch_9_not_q);
  nor nor_13 (Y_SB_d628d28f, PHI2, buffer_1_out);
  nor nor_14 (X_SB_222038db, PHI2, buffer_2_out);
  nor nor_15 (SB_X_cf392641, PHI2, buffer_4_out);
  nor nor_16 (SB_Y_9a33ae5e, PHI2, buffer_5_out);
  nor nor_17 (SB_S_4c94ee46, PHI2, buffer_6_out);
  nor nor_18 (S_S_09f08a69, PHI2, buffer_7_out);

  // Notes on the sheet:
  //   JRS2
  //   3
  //   TXS
  //   #SB/X
  //   #S/SB
  //   #SB/Y
  //   15.2
  //   18
  //   STOR
  //   STOR
  //   #SB/S
  //   STKOP
  //   #S/ADL
  //   #Y/SB
  //   #X/SB
  //   #S/SB
  //   SBXY
endmodule

module ABH (
  input  PHI1,
  input  PHI2,
  input  ADH_ABH,
  input  ADH0,
  input  ADH1,
  input  ADH2,
  input  ADH3,
  input  ADH4,
  input  ADH5,
  input  ADH6,
  input  ADH7,
  output A8,
  output A9,
  output A10,
  output A11,
  output A12,
  output A13,
  output A14,
  output A15
);

  ABH_BIT _0 (.Ax(A8), .ADH_ABH(ADH_ABH), .ADHx(ADH0), .PHI1(PHI1), .PHI2(PHI2));
  ABH_BIT _1 (.Ax(A9), .ADH_ABH(ADH_ABH), .ADHx(ADH1), .PHI1(PHI1), .PHI2(PHI2));
  ABH_BIT _2 (.Ax(A10), .ADH_ABH(ADH_ABH), .ADHx(ADH2), .PHI1(PHI1), .PHI2(PHI2));
  ABH_BIT _3 (.Ax(A11), .ADH_ABH(ADH_ABH), .ADHx(ADH3), .PHI1(PHI1), .PHI2(PHI2));
  ABH_BIT _4 (.Ax(A12), .ADH_ABH(ADH_ABH), .ADHx(ADH4), .PHI1(PHI1), .PHI2(PHI2));
  ABH_BIT _5 (.Ax(A13), .ADH_ABH(ADH_ABH), .ADHx(ADH5), .PHI1(PHI1), .PHI2(PHI2));
  ABH_BIT _6 (.Ax(A14), .ADH_ABH(ADH_ABH), .ADHx(ADH6), .PHI1(PHI1), .PHI2(PHI2));
  ABH_BIT _7 (.Ax(A15), .ADH_ABH(ADH_ABH), .ADHx(ADH7), .PHI1(PHI1), .PHI2(PHI2));
endmodule

module EXTENDED_CYCLE_COUNTER (
  input  PHI1,
  input  PHI2,
  input  TRES2,
  input  n_READY,
  input  T1,
  output n_T2,
  output n_T3,
  output n_T4,
  output n_T5
);

  wire d_latch_1_not_q, d_latch_2_not_q, d_latch_3_q, d_latch_4_not_q, d_latch_5_q, d_latch_6_not_q,
       d_latch_7_q, d_latch_8_not_q, d_latch_9_q, multiplexer_1_out, multiplexer_2_out, multiplexer_3_out,
       multiplexer_4_out, nor_1_out, nor_2_out, nor_3_out, nor_4_out, not_5_out, undriven;

  D_Latch d_latch_1 (.NOT_Q(d_latch_1_not_q), .D(T1), .EN(PHI2));  // open: Q
  Multiplexer multiplexer_1 (.in0(d_latch_1_not_q), .in1(d_latch_2_not_q), .out(multiplexer_1_out), .sel(n_READY));
  Multiplexer multiplexer_2 (.in0(d_latch_2_not_q), .in1(d_latch_4_not_q), .out(multiplexer_2_out), .sel(n_READY));
  Multiplexer multiplexer_3 (.in0(d_latch_4_not_q), .in1(d_latch_6_not_q), .out(multiplexer_3_out), .sel(n_READY));
  Multiplexer multiplexer_4 (.in0(d_latch_6_not_q), .in1(d_latch_8_not_q), .out(multiplexer_4_out), .sel(n_READY));
  nor nor_1 (nor_1_out, TRES2, d_latch_3_q);
  nor nor_2 (nor_2_out, TRES2, d_latch_5_q);
  nor nor_3 (nor_3_out, TRES2, d_latch_7_q);
  nor nor_4 (nor_4_out, TRES2, d_latch_9_q);
  D_Latch d_latch_2 (.NOT_Q(d_latch_2_not_q), .D(nor_1_out), .EN(PHI2));  // open: Q
  D_Latch d_latch_3 (.Q(d_latch_3_q), .D(multiplexer_1_out), .EN(PHI1));  // open: NOT_Q
  D_Latch d_latch_4 (.NOT_Q(d_latch_4_not_q), .D(nor_2_out), .EN(PHI2));  // open: Q
  D_Latch d_latch_5 (.Q(d_latch_5_q), .D(multiplexer_2_out), .EN(PHI1));  // open: NOT_Q
  D_Latch d_latch_6 (.NOT_Q(d_latch_6_not_q), .D(nor_3_out), .EN(PHI2));  // open: Q
  D_Latch d_latch_7 (.Q(d_latch_7_q), .D(multiplexer_3_out), .EN(PHI1));  // open: NOT_Q
  D_Latch d_latch_8 (.NOT_Q(d_latch_8_not_q), .D(nor_4_out), .EN(PHI2));  // open: Q
  D_Latch d_latch_9 (.Q(d_latch_9_q), .D(multiplexer_4_out), .EN(PHI1));  // open: NOT_Q
  not not_1 (n_T2, nor_1_out);
  not not_2 (n_T3, nor_2_out);
  not not_3 (n_T4, nor_3_out);
  not not_4 (n_T5, nor_4_out);
  not not_5 (not_5_out, undriven);

  // Notes on the sheet:
  //   To test the shift register you must disconnect PHI1 and instead connect PHI2 via an inverter:
  //   PHI2
  //   PHI2
  //   PHI1
endmodule

module ALU_SETUP (
  input  PHI1,
  input  PHI2,
  input  BRFW,
  input  L_READY_a37d69a3,
  input  BRK6E,
  input  STKOP,
  input  D26,
  input  D27,
  input  D29,
  input  D30,
  input  D31,
  input  D32,
  input  D33,
  input  D34,
  input  D35,
  input  D36,
  input  D37,
  input  D38,
  input  D39,
  input  D40,
  input  D41,
  input  D42,
  input  D43,
  input  D44,
  input  D45,
  input  D47,
  input  D48,
  input  D49,
  input  D50,
  input  D51,
  input  D52,
  input  D53,
  input  D54,
  input  D56,
  input  D69,
  input  D70,
  input  D75,
  input  D76,
  input  D84,
  input  D85,
  input  D86,
  input  D87,
  input  D88,
  input  D89,
  input  T0,
  input  T1,
  input  T5,
  input  T6,
  input  PGX,
  input  BR3,
  input  L_D_OUT_7d61c6e7,
  input  L_C_OUT_f91ece9c,
  output NDB_ADD_ee0a1870,
  output DB_ADD_48d85b7e,
  output L_0_ADD_81d17e61,
  output SB_ADD_0eab26ac,
  output ADL_ADD_e28b8a30,
  output AND,
  output ANDS,
  output EORS,
  output ORS,
  output L_ACIN_e173f520,
  output SRS,
  output SUMS,
  output L_DAA_82b80d94,
  output ADD_SB7_a8f4b77a,
  output ADD_SB06_a3738230,
  output ADD_ADL_3fac4345,
  output L_DSA_ea96e89b,
  output INC_SB,
  output SR
);

  wire and_1_out, buffer_1_out, buffer_2_out, buffer_3_out, buffer_4_out, buffer_5_out, d_latch_1_q,
       d_latch_2_q, d_latch_3_q, d_latch_4_q, d_latch_5_not_q, d_latch_6_q, d_latch_7_q, d_latch_8_q,
       d_latch_9_q, d_latch_10_not_q, d_latch_11_not_q, d_latch_12_not_q, d_latch_13_not_q, d_latch_14_not_q,
       d_latch_15_not_q, d_latch_16_not_q, d_latch_17_not_q, d_latch_18_not_q, d_latch_19_not_q,
       d_latch_20_not_q, d_latch_21_not_q, d_latch_22_not_q, d_latch_23_not_q, d_latch_24_not_q,
       d_latch_25_not_q, d_latch_26_not_q, d_latch_27_not_q, d_latch_28_not_q, d_latch_29_not_q,
       d_latch_30_not_q, d_latch_31_not_q, d_latch_32_not_q, d_latch_33_not_q, L_1_28cbbb7d_out,
       L_3_39a566ac_out, L_4_558283f2_out, L_8_05eb4f56_out, L_11_aa2e7fa3_out, L_14_4f483598_out,
       L_15_5dad5732_out, L_17_0f5278c7_out, L_19_e094c090_out, L_20_adeacd1b_out, L_22_f545d19e_out,
       L_24_b6efc2f4_out, L_25_f5ad6aee_out, L_27_6492a6f4_out, L_29_1d3a3eb3_out, L_31_e958c8e2_out,
       L_32_7de83e69_out, L_33_cae225fb_out, L_34_97db28cb_out, L_35_8b2262aa_out, L_37_acfb42d2_out,
       L_40_1e6b68e0_out, L_41_b24af141_out, L_42_ae8bf3e0_out, L_44_bb416d4b_out, L_45_e516ed8c_out,
       L_48_330a6f3f_out, L_56_35bf93dd_out, L_61_ef440803_out, L_73_3c19a6e4_out, multiplexer_1_out,
       nor_1_out, nor_2_out, nor_3_out, nor_4_out, nor_5_out, not_1_out, not_3_out, not_4_out, not_5_out,
       not_8_out, not_9_out, not_10_out, not_11_out, not_12_out, not_13_out, not_14_out, not_15_out,
       not_16_out, not_17_out;

  and L_17_0f5278c7 (L_17_0f5278c7_out, D33, not_1_out);
  not not_1 (not_1_out, D34);
  and and_1 (and_1_out, T5, D44);
  or L_31_e958c8e2 (L_31_e958c8e2_out, D52, D53);
  nor L_1_28cbbb7d (L_1_28cbbb7d_out, D69, D70);
  not not_2 (AND, L_1_28cbbb7d_out);
  and L_3_39a566ac (L_3_39a566ac_out, D76, T5);
  not not_3 (not_3_out, D27);
  nor L_15_5dad5732 (L_15_5dad5732_out, D32, L_READY_a37d69a3);
  not not_4 (not_4_out, L_15_5dad5732_out);
  not not_5 (not_5_out, BR3);
  nor L_4_558283f2 (L_4_558283f2_out, D75, L_3_39a566ac_out);
  not not_6 (SR, L_4_558283f2_out);
  nor L_42_ae8bf3e0 (L_42_ae8bf3e0_out, D84, D85, D86, D87, D88, D89, D26);
  nor L_19_e094c090 (L_19_e094c090_out, L_17_0f5278c7_out, D35, D36, D37, D38, D39, L_READY_a37d69a3);
  nor L_20_adeacd1b (L_20_adeacd1b_out, D39, D40, D41, D42, D43, and_1_out);
  not not_7 (INC_SB, L_20_adeacd1b_out);
  nor L_29_1d3a3eb3 (L_29_1d3a3eb3_out, not_5_out, BRFW);
  nor L_34_97db28cb (L_34_97db28cb_out, T0, T5);
  not not_8 (not_8_out, D47);
  nor L_27_6492a6f4 (L_27_6492a6f4_out, D49, D50, L_29_1d3a3eb3_out);
  not not_9 (not_9_out, L_27_6492a6f4_out);
  nor L_35_8b2262aa (L_35_8b2262aa_out, L_C_OUT_f91ece9c, L_34_97db28cb_out);
  nor L_14_4f483598 (L_14_4f483598_out, STKOP, D30, D31, D45, D48, INC_SB, D47, BRK6E, L_READY_a37d69a3);
  nor L_24_b6efc2f4 (L_24_b6efc2f4_out, L_19_e094c090_out, not_8_out);
  nor L_32_7de83e69 (L_32_7de83e69_out, L_35_8b2262aa_out, L_31_e958c8e2_out);
  not not_10 (not_10_out, D54);
  nand L_33_cae225fb (L_33_cae225fb_out, L_32_7de83e69_out, not_10_out);
  nand L_40_1e6b68e0 (L_40_1e6b68e0_out, D52, L_D_OUT_7d61c6e7);
  or L_44_bb416d4b (L_44_bb416d4b_out, not_9_out, D56, D51);
  D_Latch d_latch_1 (.Q(d_latch_1_q), .D(L_24_b6efc2f4_out), .EN(PHI2));  // open: NOT_Q
  D_Latch d_latch_2 (.Q(d_latch_2_q), .D(INC_SB), .EN(PHI2));  // open: NOT_Q
  D_Latch d_latch_3 (.Q(d_latch_3_q), .D(not_9_out), .EN(PHI2));  // open: NOT_Q
  D_Latch d_latch_4 (.Q(d_latch_4_q), .D(L_33_cae225fb_out), .EN(PHI2));  // open: NOT_Q
  D_Latch d_latch_5 (.NOT_Q(d_latch_5_not_q), .D(SR), .EN(PHI2));  // open: Q
  not not_11 (not_11_out, SR);
  D_Latch d_latch_6 (.Q(d_latch_6_q), .D(L_READY_a37d69a3), .EN(PHI1));  // open: NOT_Q
  nor L_41_b24af141 (L_41_b24af141_out, L_42_ae8bf3e0_out, PGX);
  nor L_56_35bf93dd (L_56_35bf93dd_out, L_40_1e6b68e0_out, D51);
  nand L_37_acfb42d2 (L_37_acfb42d2_out, D51, L_D_OUT_7d61c6e7);
  not not_12 (not_12_out, L_READY_a37d69a3);
  nor L_8_05eb4f56 (L_8_05eb4f56_out, not_11_out, d_latch_6_q);
  not not_13 (not_13_out, L_C_OUT_f91ece9c);
  not not_14 (not_14_out, L_41_b24af141_out);
  not not_15 (not_15_out, L_56_35bf93dd_out);
  nand L_45_e516ed8c (L_45_e516ed8c_out, L_44_bb416d4b_out, not_12_out);
  nor L_25_f5ad6aee (L_25_f5ad6aee_out, d_latch_1_q, d_latch_2_q, d_latch_3_q, d_latch_4_q);
  D_Latch d_latch_7 (.Q(d_latch_7_q), .D(d_latch_5_not_q), .EN(PHI1));  // open: NOT_Q
  D_Latch d_latch_8 (.Q(d_latch_8_q), .D(L_8_05eb4f56_out), .EN(PHI2));  // open: NOT_Q
  D_Latch d_latch_9 (.Q(d_latch_9_q), .D(d_latch_11_not_q), .EN(PHI2));  // open: NOT_Q
  D_Latch d_latch_10 (.NOT_Q(d_latch_10_not_q), .D(not_13_out), .EN(PHI2));  // open: Q
  not not_16 (not_16_out, multiplexer_1_out);
  Multiplexer multiplexer_1 (.in0(d_latch_9_q), .in1(d_latch_10_not_q), .out(multiplexer_1_out), .sel(d_latch_8_q));
  nand L_48_330a6f3f (L_48_330a6f3f_out, L_45_e516ed8c_out, L_19_e094c090_out);
  nor L_73_3c19a6e4 (L_73_3c19a6e4_out, AND, D29, not_4_out, SR);
  nor L_22_f545d19e (L_22_f545d19e_out, T6, PGX);
  nor L_11_aa2e7fa3 (L_11_aa2e7fa3_out, not_3_out, d_latch_7_q, d_latch_11_not_q);
  D_Latch d_latch_11 (.NOT_Q(d_latch_11_not_q), .D(not_16_out), .EN(PHI1));  // open: Q
  not not_17 (not_17_out, L_14_4f483598_out);
  nor L_61_ef440803 (L_61_ef440803_out, L_11_aa2e7fa3_out, L_22_f545d19e_out);
  D_Latch d_latch_12 (.NOT_Q(d_latch_12_not_q), .D(L_45_e516ed8c_out), .EN(PHI2));  // open: Q
  D_Latch d_latch_13 (.NOT_Q(d_latch_13_not_q), .D(L_48_330a6f3f_out), .EN(PHI2));  // open: Q
  D_Latch d_latch_14 (.NOT_Q(d_latch_14_not_q), .D(L_14_4f483598_out), .EN(PHI2));  // open: Q
  D_Latch d_latch_15 (.NOT_Q(d_latch_15_not_q), .D(not_17_out), .EN(PHI2));  // open: Q
  D_Latch d_latch_16 (.NOT_Q(d_latch_16_not_q), .D(L_19_e094c090_out), .EN(PHI2));  // open: Q
  D_Latch d_latch_17 (.NOT_Q(d_latch_17_not_q), .D(AND), .EN(PHI2));  // open: Q
  D_Latch d_latch_18 (.NOT_Q(d_latch_18_not_q), .D(D29), .EN(PHI2));  // open: Q
  D_Latch d_latch_19 (.NOT_Q(d_latch_19_not_q), .D(not_4_out), .EN(PHI2));  // open: Q
  D_Latch d_latch_20 (.NOT_Q(d_latch_20_not_q), .D(SR), .EN(PHI2));  // open: Q
  D_Latch d_latch_21 (.NOT_Q(d_latch_21_not_q), .D(L_73_3c19a6e4_out), .EN(PHI2));  // open: Q
  D_Latch d_latch_22 (.NOT_Q(d_latch_22_not_q), .D(not_15_out), .EN(PHI2));  // open: Q
  D_Latch d_latch_23 (.NOT_Q(d_latch_23_not_q), .D(L_61_ef440803_out), .EN(PHI2));  // open: Q
  D_Latch d_latch_24 (.NOT_Q(d_latch_24_not_q), .D(L_22_f545d19e_out), .EN(PHI2));  // open: Q
  D_Latch d_latch_25 (.NOT_Q(d_latch_25_not_q), .D(not_14_out), .EN(PHI2));  // open: Q
  D_Latch d_latch_26 (.NOT_Q(d_latch_26_not_q), .D(L_37_acfb42d2_out), .EN(PHI2));  // open: Q
  nor nor_1 (nor_1_out, PHI2, d_latch_12_not_q);
  nor nor_2 (nor_2_out, PHI2, d_latch_13_not_q);
  nor nor_3 (nor_3_out, PHI2, d_latch_14_not_q);
  nor nor_4 (nor_4_out, PHI2, d_latch_15_not_q);
  nor nor_5 (nor_5_out, PHI2, d_latch_16_not_q);
  D_Latch d_latch_27 (.NOT_Q(d_latch_27_not_q), .D(d_latch_17_not_q), .EN(PHI1));  // open: Q
  D_Latch d_latch_28 (.NOT_Q(d_latch_28_not_q), .D(d_latch_18_not_q), .EN(PHI1));  // open: Q
  D_Latch d_latch_29 (.NOT_Q(d_latch_29_not_q), .D(d_latch_19_not_q), .EN(PHI1));  // open: Q
  D_Latch d_latch_30 (.NOT_Q(d_latch_30_not_q), .D(L_25_f5ad6aee_out), .EN(PHI1));  // open: Q
  D_Latch d_latch_31 (.NOT_Q(d_latch_31_not_q), .D(d_latch_20_not_q), .EN(PHI1));  // open: Q
  D_Latch d_latch_32 (.NOT_Q(d_latch_32_not_q), .D(d_latch_21_not_q), .EN(PHI1));  // open: Q
  D_Latch d_latch_33 (.NOT_Q(d_latch_33_not_q), .D(d_latch_22_not_q), .EN(PHI1));  // open: Q
  D_Latch d_latch_34 (.NOT_Q(L_DSA_ea96e89b), .D(d_latch_26_not_q), .EN(PHI1));  // open: Q
  nor nor_6 (NDB_ADD_ee0a1870, PHI2, buffer_1_out);
  buf buffer_1 (buffer_1_out, nor_1_out);
  nor nor_7 (DB_ADD_48d85b7e, PHI2, buffer_2_out);
  buf buffer_2 (buffer_2_out, nor_2_out);
  nor nor_8 (L_0_ADD_81d17e61, PHI2, buffer_3_out);
  buf buffer_3 (buffer_3_out, nor_3_out);
  nor nor_9 (SB_ADD_0eab26ac, PHI2, buffer_4_out);
  buf buffer_4 (buffer_4_out, nor_4_out);
  nor nor_10 (ADL_ADD_e28b8a30, PHI2, buffer_5_out);
  buf buffer_5 (buffer_5_out, nor_5_out);
  buf buffer_6 (ANDS, d_latch_27_not_q);
  buf buffer_7 (EORS, d_latch_28_not_q);
  buf buffer_8 (ORS, d_latch_29_not_q);
  not not_18 (L_ACIN_e173f520, d_latch_30_not_q);
  buf buffer_9 (SRS, d_latch_31_not_q);
  buf buffer_10 (SUMS, d_latch_32_not_q);
  buf buffer_11 (L_DAA_82b80d94, d_latch_33_not_q);
  buf buffer_12 (ADD_SB7_a8f4b77a, d_latch_23_not_q);
  buf buffer_13 (ADD_SB06_a3738230, d_latch_24_not_q);
  buf buffer_14 (ADD_ADL_3fac4345, d_latch_25_not_q);

  // Other names for the same wires on the sheet: JSR_5_a4d207ab = D56; L_ready_9a3f8f92 = L_READY_a37d69a3;
  //   RTI_5_727c5a3b = D26; RTS_5_475d8b78 = D84; SBC0 = D51

  // Notes on the sheet:
  //   ROR
  //   EOR
  //   18
  //   STK2
  //   JSR2
  //   RET
  //   JSR2
  //   2
  //   6
  //   16
  //   OR
  //   5
  //   NOADL
  //   21
  //   23
  //   28
  //   #ADL/ADD
  //   BRX
  //   30
  //   SB/ADD
  //   CSET
  //   25,1
  //   25,2
  //   25,3
  //   25,4
  //   PGX
  //   10
  //   9
  //   8
  //   62
  //   39
  //   43
  //   /ACIN
  //   11
  //   13,3 13,1
  //   13,2
  //   7
  //   #NDB/ADD
  //   12
  //   51
  //   #ADL/ADD
  //   66
  //   67
  //   68
  //   69
  //   70
  //   64
  //   #ADD/SB7
  //   58
  //   #ADD/SB06
  //   59
  //   60
  //   38
  //   46
  //   47
  //   49
  //   50
  //   53
  //   55
  //   /ACIN
  //   72
  //   57
  //   54
  //   71
  //   56
  //   63
  //   65
endmodule

module BRANCH_LOGIC (
  input  n_IR5,
  input  D121,
  input  D126,
  input  n_C_OUT,
  input  n_V_OUT,
  input  n_N_OUT,
  input  n_Z_OUT,
  input  PHI1,
  input  PHI2,
  input  DB7,
  input  BR2,
  output n_BRTAKEN,
  output BRFW
);

  wire d_latch_1_q, d_latch_2_q, d_latch_3_not_q, multiplexer_1_out, nor_1_out, nor_2_out, nor_3_out,
       nor_4_out, nor_5_out, not_1_out, not_2_out, not_3_out, not_4_out, not_5_out, not_6_out;

  not not_1 (not_1_out, D121);
  not not_2 (not_2_out, D126);
  not not_3 (not_3_out, D126);
  not not_4 (not_4_out, D121);
  not not_5 (not_5_out, DB7);
  D_Latch d_latch_1 (.Q(d_latch_1_q), .D(BR2), .EN(PHI2));  // open: NOT_Q
  D_Latch d_latch_2 (.Q(d_latch_2_q), .D(d_latch_3_not_q), .EN(PHI2));  // open: NOT_Q
  nor nor_1 (nor_1_out, n_C_OUT, D126, not_1_out);
  nor nor_2 (nor_2_out, n_V_OUT, D121, not_2_out);
  nor nor_3 (nor_3_out, n_N_OUT, not_3_out, not_4_out);
  nor nor_4 (nor_4_out, D126, D121, n_Z_OUT);
  nor nor_5 (nor_5_out, nor_1_out, nor_2_out, nor_3_out, nor_4_out);
  Multiplexer multiplexer_1 (.in0(d_latch_2_q), .in1(not_5_out), .out(multiplexer_1_out), .sel(d_latch_1_q));
  xor xor_1 (n_BRTAKEN, n_IR5, nor_5_out);
  not not_6 (not_6_out, multiplexer_1_out);
  D_Latch d_latch_3 (.NOT_Q(d_latch_3_not_q), .D(not_6_out), .EN(PHI1));  // open: Q
  not not_7 (BRFW, d_latch_3_not_q);

  // Notes on the sheet:
  //   /IR7
endmodule

// PROGRAM COUNTER SETUP
module PC_SETUP (
  input  PHI1,
  input  PHI2,
  input  D56,
  input  D77,
  input  D78,
  input  D83,
  input  D84,
  input  D94,
  input  D95,
  input  D96,
  input  D129,
  input  L_READY_a37d69a3,
  input  BR3,
  input  BR2,
  input  T0,
  input  T1,
  input  BR0,
  output PCL_DB_4172714e,
  output PCH_DB_a81fefa0,
  output PC_DB_a835deaa,
  output PCL_ADL_ee043dbc,
  output PCH_ADH_ead93594,
  output PCL_PCL_4f350f4d,
  output ADL_PCL_9a95c372,
  output L_ADL_PCL_a2520980,
  output DL_PCH_0dc37cb4,
  output ADH_PCH_61520abf,
  output PCH_PCH_807b9fbd,
  output L_PCH_PCH_e0d9e687
);

  wire buffer_5_out, buffer_6_out, buffer_7_out, buffer_8_out, d_latch_1_q, d_latch_2_q, d_latch_3_not_q,
       d_latch_4_not_q, d_latch_5_not_q, d_latch_6_not_q, d_latch_7_not_q, d_latch_8_not_q, d_latch_9_not_q,
       d_latch_10_not_q, d_latch_11_not_q, L_1_28cbbb7d_out, L_2_143403ae_out, L_3_39a566ac_out,
       L_4_558283f2_out, L_9_0082242d_out, L_11_aa2e7fa3_out, L_12_85a3418f_out, L_14_4f483598_out,
       L_16_c7396848_out, L_17_0f5278c7_out, nor_2_out, nor_3_out, nor_4_out, nor_5_out, nor_6_out,
       not_1_out, not_2_out, not_3_out, not_5_out;

  nor L_3_39a566ac (L_3_39a566ac_out, D94, D95, D96);
  nor L_1_28cbbb7d (L_1_28cbbb7d_out, D77, D78);
  nor L_2_143403ae (L_2_143403ae_out, D83, D129);
  D_Latch d_latch_1 (.Q(d_latch_1_q), .D(L_1_28cbbb7d_out), .EN(PHI2));  // open: NOT_Q
  D_Latch d_latch_2 (.Q(d_latch_2_q), .D(L_READY_a37d69a3), .EN(PHI1));  // open: NOT_Q
  nor L_4_558283f2 (L_4_558283f2_out, d_latch_1_q, L_READY_a37d69a3);
  nor L_16_c7396848 (L_16_c7396848_out, L_3_39a566ac_out, d_latch_2_q);
  not not_1 (not_1_out, d_latch_2_q);
  not not_2 (not_2_out, T0);
  nor L_14_4f483598 (L_14_4f483598_out, L_16_c7396848_out, not_2_out);
  and L_9_0082242d (L_9_0082242d_out, not_1_out, BR3);
  nor L_15_5dad5732 (DL_PCH_0dc37cb4, not_2_out, L_3_39a566ac_out);
  D_Latch d_latch_3 (.NOT_Q(d_latch_3_not_q), .D(L_4_558283f2_out), .EN(PHI1));  // open: Q
  not not_3 (not_3_out, L_12_85a3418f_out);
  nand L_6_5b7e39b9 (PC_DB_a835deaa, d_latch_3_not_q, L_1_28cbbb7d_out);
  nor L_12_85a3418f (L_12_85a3418f_out, T1, BR2);
  nor nor_1 (L_ADL_PCL_a2520980, not_3_out, D84, T0, L_9_0082242d_out);
  nor nor_2 (nor_2_out, D84, L_2_143403ae_out, T0, T1, BR2, BR3);
  nor L_11_aa2e7fa3 (L_11_aa2e7fa3_out, L_12_85a3418f_out, DL_PCH_0dc37cb4, BR0);
  not not_4 (L_PCH_PCH_e0d9e687, nor_2_out);
  nor L_17_0f5278c7 (L_17_0f5278c7_out, L_11_aa2e7fa3_out, BR3);
  not not_5 (not_5_out, L_ADL_PCL_a2520980);
  D_Latch d_latch_4 (.NOT_Q(d_latch_4_not_q), .D(d_latch_3_not_q), .EN(PHI2));  // open: Q
  D_Latch d_latch_5 (.NOT_Q(d_latch_5_not_q), .D(L_1_28cbbb7d_out), .EN(PHI2));  // open: Q
  D_Latch d_latch_6 (.NOT_Q(d_latch_6_not_q), .D(L_12_85a3418f_out), .EN(PHI2));  // open: Q
  D_Latch d_latch_7 (.NOT_Q(d_latch_7_not_q), .D(L_17_0f5278c7_out), .EN(PHI2));  // open: Q
  D_Latch d_latch_8 (.NOT_Q(d_latch_8_not_q), .D(not_5_out), .EN(PHI2));  // open: Q
  D_Latch d_latch_9 (.NOT_Q(d_latch_9_not_q), .D(L_ADL_PCL_a2520980), .EN(PHI2));  // open: Q
  D_Latch d_latch_10 (.NOT_Q(d_latch_10_not_q), .D(nor_2_out), .EN(PHI2));  // open: Q
  D_Latch d_latch_11 (.NOT_Q(d_latch_11_not_q), .D(L_PCH_PCH_e0d9e687), .EN(PHI2));  // open: Q
  buf buffer_1 (PCL_DB_4172714e, d_latch_4_not_q);
  buf buffer_2 (PCH_DB_a81fefa0, d_latch_5_not_q);
  buf buffer_3 (PCL_ADL_ee043dbc, d_latch_6_not_q);
  buf buffer_4 (PCH_ADH_ead93594, d_latch_7_not_q);
  nor nor_3 (nor_3_out, PHI2, d_latch_8_not_q);
  buf buffer_5 (buffer_5_out, nor_3_out);
  nor nor_4 (nor_4_out, PHI2, d_latch_9_not_q);
  buf buffer_6 (buffer_6_out, nor_4_out);
  nor nor_5 (nor_5_out, PHI2, d_latch_10_not_q);
  buf buffer_7 (buffer_7_out, nor_5_out);
  nor nor_6 (nor_6_out, PHI2, d_latch_11_not_q);
  buf buffer_8 (buffer_8_out, nor_6_out);
  nor nor_7 (PCL_PCL_4f350f4d, PHI2, buffer_5_out);
  nor nor_8 (ADL_PCL_9a95c372, PHI2, buffer_6_out);
  nor nor_9 (ADH_PCH_61520abf, PHI2, buffer_7_out);
  nor nor_10 (PCH_PCH_807b9fbd, PHI2, buffer_8_out);

  // Other names for the same wires on the sheet: RTS_5_475d8b78 = D84

  // Notes on the sheet:
  //   JRS5
  //   Push/pull
  //   JB
  //   4
  //   16
  //   #PCH/DB
  //   ABS/2
  //   16
  //   3
  //   5
  //   18
  //   DL/PCH
  //   #PCL/DB
  //   PC/DB
  //   DL/PCH
  //   #PCL/ADL
  //   #ADL/PCL
  //   #ADH/PCH
  //   7
  //   8
endmodule

module DISPATCH (
  input  PHI1,
  input  PHI2,
  input  BRK6E,
  input  BR2,
  input  RESP,
  input  ACR,
  input  DORES,
  input  PC_DB,
  input  D91,
  input  D92,
  input  BR3,
  input  D96,
  input  D97,
  input  D98,
  input  D100,
  input  D101,
  input  D102,
  input  D103,
  input  D104,
  input  D105,
  input  D106,
  input  D107,
  input  D111,
  input  D122,
  input  D123,
  input  D124,
  input  D125,
  input  RDY,
  input  B_OUT,
  input  BRFW,
  input  n_BRTAKEN,
  input  n_TWOCYCLE,
  input  ADL_PCL,
  input  n_IMPLIED,
  output ACRL2,
  output T5,
  output T6,
  output TRES2,
  output TRESX,
  output STOR,
  output ENDX_Debug,
  output ENDS_Debug,
  output L_0_IR_c32b8001,
  output FETCH,
  output L_READY_a37d69a3,
  output RD,
  output R_W_47630a0a,
  output WR,
  output T1,
  output TRES1,
  output L_T0_5a901129,
  output T0,
  output L_T1X_624de7e6,
  output L_1_PC_1c371e3f
);

  wire and_1_out, d_latch_1_not_q, d_latch_2_not_q, d_latch_4_q, d_latch_5_q, d_latch_6_q, d_latch_7_q,
       d_latch_8_q, d_latch_9_not_q, d_latch_11_q, d_latch_12_q, d_latch_13_q, d_latch_14_q, d_latch_15_q,
       d_latch_16_not_q, d_latch_17_not_q, d_latch_18_not_q, d_latch_19_not_q, d_latch_20_q, d_latch_21_q,
       d_latch_22_q, d_latch_24_q, d_latch_25_q, d_latch_26_q, d_latch_27_q, d_latch_28_q, d_latch_29_q,
       d_latch_31_not_q, d_latch_33_not_q, L_1_28cbbb7d_out, L_2_143403ae_out, L_5_9518e519_out,
       L_6_5b7e39b9_out, L_9_0082242d_out, L_11_aa2e7fa3_out, L_13_587da886_out, L_15_5dad5732_out,
       L_17_0f5278c7_out, L_21_ada5c31c_out, L_22_f545d19e_out, L_24_b6efc2f4_out, L_25_f5ad6aee_out,
       L_26_ffeee2da_out, L_30_3bf8f3d0_out, L_31_e958c8e2_out, L_33_cae225fb_out, L_37_acfb42d2_out,
       L_38_43aa51c3_out, L_39_c97a3f22_out, L_43_fdaf143b_out, L_47_7c60183d_out, L_50_6b408103_out,
       L_53_d08b6e35_out, L_54_01afe50f_out, L_56_35bf93dd_out, L_65_6a42b4dc_out, L_MemOP_bf72a9c8,
       L_SHIFT_2aa3590c, multiplexer_1_out, nor73_out, nor78_out, nor_1_out, nor_2_out, nor_3_out, nor_4_out,
       not_1_out, not_2_out, not_3_out, not_4_out, not_5_out, not_6_out, not_7_out, not_8_out, not_9_out,
       not_10_out, not_11_out, NotReadyPhi1, or_1_out, xor_1_out;

  nor L_1_28cbbb7d (L_1_28cbbb7d_out, D91, D92);
  not not_1 (not_1_out, D97);
  nor L_13_587da886 (L_13_587da886_out, BR2, BR3);
  not not_2 (not_2_out, NotReadyPhi1);
  nor L_33_cae225fb (L_33_cae225fb_out, D100, D101, D102, D103, D104, D105);
  nor L_32_7de83e69 (L_SHIFT_2aa3590c, D106, D107);
  nor L_51_79fb832a (L_MemOP_bf72a9c8, D111, D125);
  not not_3 (not_3_out, L_13_587da886_out);
  not not_4 (not_4_out, n_IMPLIED);
  not not_5 (not_5_out, ACR);
  and nor73 (nor73_out, not_5_out, not_2_out);
  nor nor78 (nor78_out, not_2_out, ACRL2);
  not not_6 (not_6_out, L_33_cae225fb_out);
  and L_9_0082242d (L_9_0082242d_out, n_BRTAKEN, BR2);
  not not_7 (not_7_out, BR3);
  and L_17_0f5278c7 (L_17_0f5278c7_out, n_BRTAKEN, BR2);
  nor L_15_5dad5732 (L_15_5dad5732_out, ADL_PCL, not_3_out);
  nor nor_1 (nor_1_out, nor73_out, nor78_out);
  nor L_37_acfb42d2 (L_37_acfb42d2_out, T5, T6, D100, D98, PC_DB, STOR);
  nor nor_2 (nor_2_out, T0, L_9_0082242d_out);
  Multiplexer multiplexer_1 (.in0(nor_2_out), .in1(not_8_out), .out(multiplexer_1_out), .sel(L_READY_a37d69a3));
  not not_8 (not_8_out, T1);
  nor L_21_ada5c31c (L_21_ada5c31c_out, not_7_out, NotReadyPhi1);
  D_Latch d_latch_1 (.NOT_Q(d_latch_1_not_q), .D(L_READY_a37d69a3), .EN(PHI1));  // open: Q
  nor nor_3 (nor_3_out, L_17_0f5278c7_out, L_15_5dad5732_out);
  not not_9 (not_9_out, L_SHIFT_2aa3590c);
  not not_10 (not_10_out, L_READY_a37d69a3);
  D_Latch d_latch_2 (.NOT_Q(d_latch_2_not_q), .D(nor_1_out), .EN(PHI1));  // open: Q
  D_Latch d_latch_3 (.NOT_Q(ACRL2), .D(d_latch_2_not_q), .EN(PHI2));  // open: Q
  D_Latch d_latch_4 (.Q(d_latch_4_q), .D(L_1_28cbbb7d_out), .EN(PHI2));  // open: NOT_Q
  nor L_11_aa2e7fa3 (L_11_aa2e7fa3_out, D96, not_9_out, L_MemOP_bf72a9c8);
  D_Latch d_latch_5 (.Q(d_latch_5_q), .D(L_37_acfb42d2_out), .EN(PHI2));  // open: NOT_Q
  D_Latch d_latch_6 (.Q(d_latch_6_q), .D(multiplexer_1_out), .EN(PHI2));  // open: NOT_Q
  D_Latch d_latch_7 (.Q(d_latch_7_q), .D(RESP), .EN(PHI2));  // open: NOT_Q
  D_Latch d_latch_8 (.Q(d_latch_8_q), .D(not_10_out), .EN(PHI1));  // open: NOT_Q
  D_Latch d_latch_9 (.NOT_Q(d_latch_9_not_q), .D(L_21_ada5c31c_out), .EN(PHI2));  // open: Q
  xor xor_1 (xor_1_out, BRFW, ACR);
  D_Latch d_latch_10 (.NOT_Q(NotReadyPhi1), .D(d_latch_1_not_q), .EN(PHI2));  // open: Q
  D_Latch d_latch_11 (.Q(d_latch_11_q), .D(TRES1), .EN(PHI1));  // open: NOT_Q
  D_Latch d_latch_12 (.Q(d_latch_12_q), .D(n_TWOCYCLE), .EN(PHI1));  // open: NOT_Q
  D_Latch d_latch_13 (.Q(d_latch_13_q), .D(TRESX), .EN(PHI1));  // open: NOT_Q
  D_Latch d_latch_14 (.Q(d_latch_14_q), .D(nor_3_out), .EN(PHI2));  // open: NOT_Q
  nand L_38_43aa51c3 (L_38_43aa51c3_out, L_SHIFT_2aa3590c, not_1_out);
  nor L_12_85a3418f (ENDX_Debug, L_11_aa2e7fa3_out, T6, not_6_out, BR3);
  nor L_8_05eb4f56 (ENDS_Debug, d_latch_6_q, d_latch_7_q);
  nor L_24_b6efc2f4 (L_24_b6efc2f4_out, d_latch_9_not_q, xor_1_out);
  and and_1 (and_1_out, d_latch_12_q, d_latch_13_q);
  nor L_43_fdaf143b (L_43_fdaf143b_out, L_SHIFT_2aa3590c, L_MemOP_bf72a9c8, L_READY_a37d69a3);
  not not_11 (not_11_out, L_READY_a37d69a3);
  nor L_56_35bf93dd (L_56_35bf93dd_out, d_latch_11_q, and_1_out);
  nor L_54_01afe50f (L_54_01afe50f_out, d_latch_24_q, d_latch_25_q);
  D_Latch d_latch_15 (.Q(d_latch_15_q), .D(L_43_fdaf143b_out), .EN(PHI2));  // open: NOT_Q
  nand L_47_7c60183d (L_47_7c60183d_out, T5, not_11_out);
  nor L_2_143403ae (L_2_143403ae_out, nor_1_out, d_latch_4_q, L_READY_a37d69a3, L_38_43aa51c3_out);
  nor L_5_9518e519 (L_5_9518e519_out, RESP, ENDS_Debug, L_6_5b7e39b9_out);
  nor L_39_c97a3f22 (L_39_c97a3f22_out, RDY, d_latch_20_q);
  nor L_40_1e6b68e0 (WR, L_READY_a37d69a3, d_latch_5_q, DORES);
  nor L_26_ffeee2da (L_26_ffeee2da_out, d_latch_8_q, RESP, d_latch_22_q);
  nor L_25_f5ad6aee (L_25_f5ad6aee_out, d_latch_21_q, L_24_b6efc2f4_out);
  nor L_31_e958c8e2 (L_31_e958c8e2_out, L_25_f5ad6aee_out, L_READY_a37d69a3);
  nor L_30_3bf8f3d0 (L_30_3bf8f3d0_out, L_31_e958c8e2_out, ENDS_Debug);
  nor L_57_0f0af090 (L_T0_5a901129, L_56_35bf93dd_out, L_54_01afe50f_out);
  nor L_53_d08b6e35 (L_53_d08b6e35_out, d_latch_24_q, L_READY_a37d69a3);
  nor L_22_f545d19e (L_22_f545d19e_out, L_READY_a37d69a3, d_latch_14_q, not_4_out);
  and L_50_6b408103 (L_50_6b408103_out, d_latch_29_q, L_READY_a37d69a3);
  D_Latch d_latch_16 (.NOT_Q(d_latch_16_not_q), .D(L_47_7c60183d_out), .EN(PHI2));  // open: Q
  D_Latch d_latch_17 (.NOT_Q(d_latch_17_not_q), .D(L_5_9518e519_out), .EN(PHI2));  // open: Q
  D_Latch d_latch_18 (.NOT_Q(d_latch_18_not_q), .D(T1), .EN(PHI2));  // open: Q
  D_Latch d_latch_19 (.NOT_Q(d_latch_19_not_q), .D(L_39_c97a3f22_out), .EN(PHI2));  // open: Q
  D_Latch d_latch_20 (.Q(d_latch_20_q), .D(WR), .EN(PHI1));  // open: NOT_Q
  D_Latch d_latch_21 (.Q(d_latch_21_q), .D(L_26_ffeee2da_out), .EN(PHI2));  // open: NOT_Q
  D_Latch d_latch_22 (.Q(d_latch_22_q), .D(L_25_f5ad6aee_out), .EN(PHI1));  // open: NOT_Q
  D_Latch d_latch_23 (.NOT_Q(T1), .D(L_30_3bf8f3d0_out), .EN(PHI1));  // open: Q
  not not_12 (TRES1, L_30_3bf8f3d0_out);
  D_Latch d_latch_24 (.Q(d_latch_24_q), .D(L_T0_5a901129), .EN(PHI2));  // open: NOT_Q
  D_Latch d_latch_25 (.Q(d_latch_25_q), .NOT_Q(L_T1X_624de7e6), .D(L_53_d08b6e35_out), .EN(PHI1));
  D_Latch d_latch_26 (.Q(d_latch_26_q), .D(B_OUT), .EN(PHI1));  // open: NOT_Q
  D_Latch d_latch_27 (.Q(d_latch_27_q), .D(L_24_b6efc2f4_out), .EN(PHI1));  // open: NOT_Q
  D_Latch d_latch_28 (.Q(d_latch_28_q), .D(L_22_f545d19e_out), .EN(PHI1));  // open: NOT_Q
  nor nor_4 (nor_4_out, L_50_6b408103_out, d_latch_15_q);
  nor L_3_39a566ac (TRESX, L_2_143403ae_out, BRK6E, d_latch_17_not_q);
  nor L_36_34609549 (STOR, L_MemOP_bf72a9c8, not_1_out);
  not not_13 (L_READY_a37d69a3, d_latch_19_not_q);
  D_Latch d_latch_29 (.Q(d_latch_29_q), .D(T5), .EN(PHI2));  // open: NOT_Q
  D_Latch d_latch_30 (.NOT_Q(T5), .D(nor_4_out), .EN(PHI1));  // open: Q
  D_Latch d_latch_31 (.NOT_Q(d_latch_31_not_q), .D(d_latch_16_not_q), .EN(PHI1));  // open: Q
  not not_14 (T6, d_latch_31_not_q);
  D_Latch d_latch_32 (.NOT_Q(TRES2), .D(TRESX), .EN(PHI1));  // open: Q
  nor L_6_5b7e39b9 (L_6_5b7e39b9_out, L_READY_a37d69a3, ENDX_Debug);
  nor L_60_8c46ae22 (FETCH, d_latch_18_not_q, L_READY_a37d69a3);
  D_Latch d_latch_33 (.NOT_Q(d_latch_33_not_q), .D(WR), .EN(PHI1));  // open: Q
  not not_15 (T0, L_T0_5a901129);
  or or_1 (or_1_out, d_latch_27_q, d_latch_28_q);
  nand L_61_ef440803 (L_0_IR_c32b8001, B_OUT, FETCH);
  nor L_65_6a42b4dc (L_65_6a42b4dc_out, PHI1, d_latch_33_not_q);
  not not_16 (RD, L_65_6a42b4dc_out);
  buf buffer_1 (R_W_47630a0a, d_latch_33_not_q);
  nand L_23_d0835dd9 (L_1_PC_1c371e3f, d_latch_26_q, or_1_out);

  // Other names for the same wires on the sheet: L_ready_9a3f8f92 = L_READY_a37d69a3

  // Notes on the sheet:
  //   35
  //   16
  //   72
  //   /STORE
  //   14
  //   !!!
  //   7
  //   9
  //   70
  //   74
  //   78
  //   2
  //   10
  //   27
  //   26
  //   20
  //   ReadyDelay
  //   71
  //   TRES1
  //   22
  //   40
  //   8,1
  //   8,2
  //   56,1
  //   56,3
  //   56,2
  //   ACRL1
  //   !!!
  //   REST
  //   ENDS
  //   48
  //   ENDS
  //   RDY
  //   !!!
  //   ENDS
  //   50,1
  //   46
  //   4
  //   59
  //   42
  //   39
  //   WR
  //   26,2
  //   26,1
  //   29
  //   28
  //   53
  //   50,2
  //   49
  //   45
  //   7
  //   41
  //   67
  //   52
  //   23
  //   23,1
  //   23,2
  //   44
  //   55
  //   66
endmodule

// BUS CONTROL
module BUS_CONTROL (
  input  PHI1,
  input  PHI2,
  input  SBXY,
  input  D55,
  input  D57,
  input  D58,
  input  D59,
  input  D60,
  input  D61,
  input  D62,
  input  D63,
  input  D64,
  input  D65,
  input  D66,
  input  D67,
  input  D68,
  input  AND,
  input  D71,
  input  D72,
  input  D73,
  input  D74,
  input  D79,
  input  STOR,
  input  D81,
  input  D82,
  input  D84,
  input  D89,
  input  D90,
  input  D91,
  input  D83,
  input  D128,
  input  D129,
  input  L_0_ADL0_f8fabdab,
  input  BR2,
  input  ACRL2,
  input  DL_PCH,
  input  BR3,
  input  n_READY,
  input  T2,
  input  INC_SB,
  input  D45,
  input  BRK6E,
  input  D46,
  input  D47,
  input  D48,
  input  STXY,
  input  D101,
  input  PCH_PCH,
  input  T0,
  input  T1,
  input  T5,
  input  T6,
  input  D56,
  output L_0_ADH0_e340c71e,
  output L_0_ADH17_f181a8fa,
  output SB_AC_b159eec5,
  output ZTST,
  output ADL_ABL_5bea59e2,
  output AC_SB_c49f602a,
  output SB_DB_641efa5a,
  output AC_DB_519ce409,
  output PGX,
  output SB_ADH_4f1456ff,
  output DL_ADH_3839a3d0,
  output DL_ADL_6c5e0116,
  output ADH_ABH_8f72aca9,
  output DL_DB_69522204
);

  wire and_1_out, buffer_2_out, buffer_4_out, buffer_6_out, d_latch_1_not_q, d_latch_3_not_q,
       d_latch_4_not_q, d_latch_5_not_q, d_latch_6_not_q, d_latch_7_not_q, d_latch_8_not_q, d_latch_9_not_q,
       d_latch_10_not_q, d_latch_11_not_q, d_latch_12_not_q, d_latch_13_not_q, L_1_28cbbb7d_out,
       L_3_39a566ac_out, L_4_558283f2_out, L_5_9518e519_out, L_8_05eb4f56_out, L_9_0082242d_out,
       L_10_57b0d741_out, L_12_85a3418f_out, L_14_4f483598_out, L_15_5dad5732_out, L_25_f5ad6aee_out,
       L_27_6492a6f4_out, L_28_647e552a_out, L_31_e958c8e2_out, L_32_7de83e69_out, L_33_cae225fb_out,
       L_35_8b2262aa_out, L_36_34609549_out, L_37_acfb42d2_out, L_38_43aa51c3_out, L_40_1e6b68e0_out,
       L_41_b24af141_out, L_42_ae8bf3e0_out, L_43_fdaf143b_out, L_47_7c60183d_out, L_48_330a6f3f_out,
       L_49_f70f8148_out, nor_1_out, nor_2_out, nor_3_out, nor_4_out, nor_5_out, nor_6_out, nor_7_out,
       not_1_out, not_2_out, not_3_out, not_4_out, not_5_out, not_6_out, not_7_out, not_8_out, not_9_out,
       or_1_out;

  not not_1 (not_1_out, D64);
  nor L_40_1e6b68e0 (L_40_1e6b68e0_out, D71, D72);
  not not_2 (not_2_out, D73);
  and L_47_7c60183d (L_47_7c60183d_out, D79, STOR);
  nor L_48_330a6f3f (L_48_330a6f3f_out, D81, D82);
  nor nor_1 (nor_1_out, D90, D129);
  nor nor_2 (nor_2_out, D83, D129);
  nor nor_3 (nor_3_out, D128, D129);
  not not_3 (not_3_out, D48);
  nor L_36_34609549 (L_36_34609549_out, D58, D59, D60, D61, D62, D63, D64);
  and L_38_43aa51c3 (L_38_43aa51c3_out, not_1_out, D65);
  not not_4 (not_4_out, L_40_1e6b68e0_out);
  nand L_45_e516ed8c (PGX, L_40_1e6b68e0_out, not_2_out);
  nor nor_4 (nor_4_out, D74, L_47_7c60183d_out);
  nor L_49_f70f8148 (L_49_f70f8148_out, D89, nor_1_out, D91, D84);
  nor L_5_9518e519 (L_5_9518e519_out, nor_2_out, T0);
  D_Latch d_latch_1 (.NOT_Q(d_latch_1_not_q), .D(n_READY), .EN(PHI1));  // open: Q
  nor L_1_28cbbb7d (L_1_28cbbb7d_out, INC_SB, D45, BRK6E, D46, D47, D48);
  not not_5 (not_5_out, L_36_34609549_out);
  nor L_37_acfb42d2 (L_37_acfb42d2_out, L_38_43aa51c3_out, AND);
  not not_6 (not_6_out, L_49_f70f8148_out);
  nor L_4_558283f2 (L_4_558283f2_out, L_5_9518e519_out, nor_3_out);
  nand L_14_4f483598 (L_14_4f483598_out, ACRL2, d_latch_1_not_q);
  not not_7 (not_7_out, L_1_28cbbb7d_out);
  nand L_27_6492a6f4 (L_27_6492a6f4_out, not_3_out, STXY);
  nor L_33_cae225fb (L_33_cae225fb_out, SBXY, not_5_out, T6, AND);
  nor L_43_fdaf143b (L_43_fdaf143b_out, not_4_out, n_READY);
  nor L_12_85a3418f (L_12_85a3418f_out, PGX, BR3);
  nor L_10_57b0d741 (L_10_57b0d741_out, not_6_out, T2, PCH_PCH, D56);
  nand L_28_647e552a (L_28_647e552a_out, T5, D55);
  not not_8 (not_8_out, L_28_647e552a_out);
  not not_9 (not_9_out, L_48_330a6f3f_out);
  nor L_15_5dad5732 (L_15_5dad5732_out, L_12_85a3418f_out, L_14_4f483598_out);
  nor L_9_0082242d (L_9_0082242d_out, n_READY, L_10_57b0d741_out);
  nor L_35_8b2262aa (L_35_8b2262aa_out, D57, not_9_out);
  nor L_31_e958c8e2 (L_31_e958c8e2_out, L_33_cae225fb_out, AND);
  or or_1 (or_1_out, L_15_5dad5732_out, L_9_0082242d_out);
  nor L_41_b24af141 (L_41_b24af141_out, T6, T5);
  nand L_42_ae8bf3e0 (L_42_ae8bf3e0_out, L_41_b24af141_out, L_43_fdaf143b_out);
  nor L_32_7de83e69 (L_32_7de83e69_out, not_8_out, L_31_e958c8e2_out, D67, T1, BR2, L_27_6492a6f4_out);
  nor L_25_f5ad6aee (L_25_f5ad6aee_out, DL_PCH, not_6_out);
  nor L_8_05eb4f56 (L_8_05eb4f56_out, L_0_ADL0_f8fabdab, and_1_out);
  and and_1 (and_1_out, or_1_out, BR3);
  nor L_3_39a566ac (L_3_39a566ac_out, BR2, T5);
  D_Latch d_latch_2 (.NOT_Q(L_0_ADH0_e340c71e), .D(L_48_330a6f3f_out), .EN(PHI2));  // open: Q
  D_Latch d_latch_3 (.NOT_Q(d_latch_3_not_q), .D(L_35_8b2262aa_out), .EN(PHI2));  // open: Q
  D_Latch d_latch_4 (.NOT_Q(d_latch_4_not_q), .D(L_36_34609549_out), .EN(PHI2));  // open: Q
  D_Latch d_latch_5 (.NOT_Q(d_latch_5_not_q), .D(L_42_ae8bf3e0_out), .EN(PHI2));  // open: Q
  D_Latch d_latch_6 (.NOT_Q(d_latch_6_not_q), .D(L_37_acfb42d2_out), .EN(PHI2));  // open: Q
  D_Latch d_latch_7 (.NOT_Q(d_latch_7_not_q), .D(L_32_7de83e69_out), .EN(PHI2));  // open: Q
  D_Latch d_latch_8 (.NOT_Q(d_latch_8_not_q), .D(nor_4_out), .EN(PHI2));  // open: Q
  D_Latch d_latch_9 (.NOT_Q(d_latch_9_not_q), .D(L_12_85a3418f_out), .EN(PHI2));  // open: Q
  D_Latch d_latch_10 (.NOT_Q(d_latch_10_not_q), .D(L_25_f5ad6aee_out), .EN(PHI2));  // open: Q
  D_Latch d_latch_11 (.NOT_Q(d_latch_11_not_q), .D(L_48_330a6f3f_out), .EN(PHI2));  // open: Q
  D_Latch d_latch_12 (.NOT_Q(d_latch_12_not_q), .D(L_8_05eb4f56_out), .EN(PHI2));  // open: Q
  D_Latch d_latch_13 (.NOT_Q(d_latch_13_not_q), .D(L_3_39a566ac_out), .EN(PHI2));  // open: Q
  buf buffer_1 (L_0_ADH17_f181a8fa, d_latch_3_not_q);
  nor nor_5 (nor_5_out, PHI2, d_latch_4_not_q);
  buf buffer_2 (buffer_2_out, nor_5_out);
  not not_10 (ZTST, L_33_cae225fb_out);
  buf buffer_3 (ADL_ABL_5bea59e2, d_latch_5_not_q);
  nor nor_6 (nor_6_out, PHI2, d_latch_6_not_q);
  buf buffer_4 (buffer_4_out, nor_6_out);
  buf buffer_5 (SB_DB_641efa5a, d_latch_7_not_q);
  nor nor_7 (nor_7_out, PHI2, d_latch_8_not_q);
  buf buffer_6 (buffer_6_out, nor_7_out);
  buf buffer_7 (SB_ADH_4f1456ff, d_latch_9_not_q);
  buf buffer_8 (DL_ADH_3839a3d0, d_latch_10_not_q);
  buf buffer_9 (DL_ADL_6c5e0116, d_latch_11_not_q);
  buf buffer_10 (ADH_ABH_8f72aca9, d_latch_12_not_q);
  buf buffer_11 (DL_DB_69522204, d_latch_13_not_q);
  nor nor_8 (SB_AC_b159eec5, PHI2, buffer_2_out);
  nor nor_9 (AC_SB_c49f602a, PHI2, buffer_4_out);
  nor nor_10 (AC_DB_519ce409, PHI2, buffer_6_out);

  // Other names for the same wires on the sheet: DL_PCH_0dc37cb4 = DL_PCH; L_ready_9a3f8f92 = n_READY;
  //   RTS_5_475d8b78 = D84

  // Notes on the sheet:
  //   !!!
  //   BR0
  //   STA
  //   JSR2
  //   39
  //   46
  //   ABS/2
  //   IMPLED
  //   push/pull
  //   26
  //   44
  //   PGX
  //   #DL/ADL
  //   13
  //   #SB/AC
  //   33,1
  //   SBXY
  //   50
  //   IND
  //   2
  //   JSR/5
  //   #DL/ADL
  //   AND
  //   T2
  //   29
  //   34
  //   #ZTST
  //   SBA
  //   JSXY
  //   JMP/4
  //   JSXY
  //   #DL/ADL
  //   #SB/AC
  //   #ADL/ABL
  //   #AC/SB
  //   #SB/DB
  //   #DL/ADL
  //   #DL/DB
  //   19
  //   17
  //   7
  //   20
  //   16
  //   21
  //   18
  //   23
  //   22
  //   6
  //   24
endmodule

// FLAGS CONTROL
module FLAGS_CONTROL (
  input  PHI2,
  input  D98,
  input  D99,
  input  D108,
  input  D110,
  input  D120,
  input  D127,
  input  D107,
  input  T6,
  input  D112,
  input  D116,
  input  D117,
  input  D118,
  input  D119,
  input  ZTST,
  input  D109,
  input  n_READY,
  input  SR,
  input  D114,
  input  D115,
  input  D113,
  output P_DB_42279b60,
  output IR5_I_e7eeeda5,
  output IR5_C_8cbf3e52,
  output IR5_D_ec89b364,
  output L_0_V_f0a8dd83,
  output ACR_C_5cb02b46,
  output DBZ_Z_a7859eb1,
  output DB_N_68ba26fc,
  output DB_P_37e5c1ba,
  output DB_C_01ed158e,
  output DB_V_92adf01b
);

  wire and_1_out, d_latch_7_q, d_latch_8_q, d_latch_10_q, d_latch_11_q, L_1_28cbbb7d_out, L_3_39a566ac_out,
       L_4_558283f2_out, L_9_0082242d_out, L_14_4f483598_out, L_15_5dad5732_out, L_21_ada5c31c_out,
       not_1_out, not_2_out, not_3_out, not_4_out;

  nor L_4_558283f2 (L_4_558283f2_out, D98, D99);
  not not_1 (not_1_out, D108);
  not not_2 (not_2_out, D110);
  not not_3 (not_3_out, D120);
  not L_9_0082242d (L_9_0082242d_out, D127);
  and and_1 (and_1_out, D107, T6);
  nor L_3_39a566ac (L_3_39a566ac_out, D114, D115);
  not not_4 (not_4_out, D113);
  nor L_1_28cbbb7d (L_1_28cbbb7d_out, and_1_out, D112, D116, D117, D118, D119);
  nor L_14_4f483598 (L_14_4f483598_out, ACR_C_5cb02b46, ZTST, D109);
  nor L_15_5dad5732 (L_15_5dad5732_out, SR, DB_P_37e5c1ba);
  D_Latch d_latch_1 (.NOT_Q(P_DB_42279b60), .D(L_4_558283f2_out), .EN(PHI2));  // open: Q
  D_Latch d_latch_2 (.NOT_Q(IR5_I_e7eeeda5), .D(not_1_out), .EN(PHI2));  // open: Q
  D_Latch d_latch_3 (.NOT_Q(IR5_C_8cbf3e52), .D(not_2_out), .EN(PHI2));  // open: Q
  D_Latch d_latch_4 (.NOT_Q(IR5_D_ec89b364), .D(not_3_out), .EN(PHI2));  // open: Q
  D_Latch d_latch_5 (.NOT_Q(L_0_V_f0a8dd83), .D(L_9_0082242d_out), .EN(PHI2));  // open: Q
  D_Latch d_latch_6 (.NOT_Q(ACR_C_5cb02b46), .D(L_1_28cbbb7d_out), .EN(PHI2));  // open: Q
  D_Latch d_latch_7 (.Q(d_latch_7_q), .NOT_Q(DBZ_Z_a7859eb1), .D(L_14_4f483598_out), .EN(PHI2));
  D_Latch d_latch_8 (.Q(d_latch_8_q), .D(D109), .EN(PHI2));  // open: NOT_Q
  D_Latch d_latch_9 (.NOT_Q(DB_C_01ed158e), .D(L_15_5dad5732_out), .EN(PHI2));  // open: Q
  D_Latch d_latch_10 (.Q(d_latch_10_q), .D(L_3_39a566ac_out), .EN(PHI2));  // open: NOT_Q
  D_Latch d_latch_11 (.Q(d_latch_11_q), .D(not_4_out), .EN(PHI2));  // open: NOT_Q
  and L_21_ada5c31c (L_21_ada5c31c_out, d_latch_7_q, d_latch_10_q);
  nor L_20_adeacd1b (DB_P_37e5c1ba, d_latch_10_q, n_READY);
  nand L_12_85a3418f (DB_V_92adf01b, d_latch_10_q, d_latch_11_q);
  nor L_22_f545d19e (DB_N_68ba26fc, L_21_ada5c31c_out, d_latch_8_q);

  // Notes on the sheet:
  //   AVR/V
  //   BIT1
  //   BIT0
  //   /POUT
  //   2
  //   /CSI
  //   5
  //   19
  //   11
  //   /PIN
  //   /ARIT
  //   ZTST
  //   BIT1
  //   8
  //   7
  //   6
  //   18
  //   10
  //   13
  //   17
  //   22
  //   16
  //   12
  //   12,2
  //   21
  //   20
  //   21,1
endmodule

module FLAGS (
  input  P_DB,
  input  B_OUT,
  input  DB0_In,
  input  DB1_In,
  input  DB2_In,
  input  DB3_In,
  input  DB4_In,
  input  DB5_In,
  input  DB6_In,
  input  DB7_In,
  input  DB_P_37e5c1ba,
  input  DBZ_Z_a7859eb1,
  input  DB_N_68ba26fc,
  input  IR5_C_8cbf3e52,
  input  ACR,
  input  DB_C_01ed158e,
  input  ACR_C_5cb02b46,
  input  IR5_D_ec89b364,
  input  PHI1,
  input  PHI2,
  input  L_IR5_9e15d54c,
  input  IR5_I_e7eeeda5,
  input  AVR,
  input  DB_V_92adf01b,
  input  D112,
  input  L_0_V_f0a8dd83,
  input  SO,
  output DB0_Out,
  output DB1_Out,
  output DB2_Out,
  output DB3_Out,
  output DB4_Out,
  output DB5_Out,
  output DB6_Out,
  output DB7_Out,
  output n_Z_OUT,
  output n_N_OUT,
  output n_C_OUT,
  output n_D_OUT,
  output n_I_OUT,
  output n_V_OUT
);

  wire and_1_out, and_2_out, and_3_out, and_4_out, and_5_out, d_latch_1_not_q, d_latch_2_not_q,
       d_latch_3_not_q, d_latch_4_q, d_latch_6_not_q, d_latch_8_not_q, d_latch_10_q, d_latch_12_q,
       d_latch_14_q, d_latch_16_q, d_latch_17_q, multiplexer_1_out, multiplexer_2_out, nand_1_out,
       nand_2_out, nand_3_out, nand_4_out, nand_5_out, nand_6_out, nand_7_out, nand_8_out, nand_9_out,
       nand_10_out, nand_11_out, nand_12_out, nand_13_out, nand_14_out, nand_15_out, nand_16_out, nor_1_out,
       nor_2_out, nor_3_out, nor_4_out, nor_5_out, nor_6_out, not_1_out, not_2_out, not_3_out, not_4_out,
       not_5_out, not_6_out, not_7_out, not_8_out, not_9_out, not_10_out, not_11_out, not_12_out, not_13_out,
       not_14_out, not_15_out, not_16_out, not_17_out, or_1_out;

  not not_1 (not_1_out, SO);
  D_Latch d_latch_1 (.NOT_Q(d_latch_1_not_q), .D(D112), .EN(PHI2));  // open: Q
  nor nor_1 (nor_1_out, DB0_In, DB1_In, DB2_In, DB3_In, DB4_In, DB5_In, DB6_In, DB7_In);
  not not_2 (not_2_out, DB1_In);
  not not_3 (not_3_out, nor_1_out);
  not not_4 (not_4_out, DB7_In);
  D_Latch d_latch_2 (.NOT_Q(d_latch_2_not_q), .D(not_1_out), .EN(PHI1));  // open: Q
  nand nand_1 (nand_1_out, not_2_out, DB_P_37e5c1ba);
  nand nand_2 (nand_2_out, not_3_out, DBZ_Z_a7859eb1);
  nand nand_3 (nand_3_out, not_4_out, DB_N_68ba26fc);
  not not_5 (not_5_out, ACR);
  not not_6 (not_6_out, DB0_In);
  nor nor_2 (nor_2_out, DB_C_01ed158e, IR5_C_8cbf3e52, ACR_C_5cb02b46);
  not not_7 (not_7_out, DB3_In);
  nor nor_3 (nor_3_out, IR5_D_ec89b364, DB_P_37e5c1ba);
  not not_8 (not_8_out, DB2_In);
  nor nor_4 (nor_4_out, DB_P_37e5c1ba, IR5_I_e7eeeda5);
  not not_9 (not_9_out, AVR);
  not not_10 (not_10_out, DB6_In);
  nor nor_5 (nor_5_out, DB_V_92adf01b, d_latch_1_not_q, d_latch_17_q);
  and and_1 (and_1_out, nand_1_out, nand_2_out);
  nand nand_4 (nand_4_out, L_IR5_9e15d54c, IR5_C_8cbf3e52);
  nand nand_5 (nand_5_out, not_5_out, ACR_C_5cb02b46);
  nand nand_6 (nand_6_out, not_6_out, DB_C_01ed158e);
  nand nand_7 (nand_7_out, nor_2_out, d_latch_10_q);
  nand nand_8 (nand_8_out, IR5_D_ec89b364, L_IR5_9e15d54c);
  nand nand_9 (nand_9_out, not_7_out, DB_P_37e5c1ba);
  nand nand_10 (nand_10_out, nor_3_out, d_latch_12_q);
  nand nand_11 (nand_11_out, L_IR5_9e15d54c, IR5_I_e7eeeda5);
  nand nand_12 (nand_12_out, not_8_out, DB_P_37e5c1ba);
  nand nand_13 (nand_13_out, nor_4_out, d_latch_14_q);
  nand nand_14 (nand_14_out, not_9_out, d_latch_1_not_q);
  nand nand_15 (nand_15_out, not_10_out, DB_V_92adf01b);
  nand nand_16 (nand_16_out, nor_5_out, d_latch_16_q);
  not not_11 (not_11_out, L_0_V_f0a8dd83);
  D_Latch d_latch_3 (.NOT_Q(d_latch_3_not_q), .D(d_latch_2_not_q), .EN(PHI2));  // open: Q
  or or_1 (or_1_out, DB_P_37e5c1ba, DBZ_Z_a7859eb1);
  and and_2 (and_2_out, nand_4_out, nand_5_out, nand_6_out, nand_7_out);
  and and_3 (and_3_out, nand_8_out, nand_9_out, nand_10_out);
  and and_4 (and_4_out, nand_11_out, nand_12_out, nand_13_out);
  and and_5 (and_5_out, nand_14_out, nand_15_out, nand_16_out, not_11_out);
  D_Latch d_latch_4 (.Q(d_latch_4_q), .D(d_latch_3_not_q), .EN(PHI1));  // open: NOT_Q
  Multiplexer multiplexer_1 (.in0(d_latch_6_not_q), .in1(and_1_out), .out(multiplexer_1_out), .sel(or_1_out));
  Multiplexer multiplexer_2 (.in0(d_latch_8_not_q), .in1(nand_3_out), .out(multiplexer_2_out), .sel(DB_N_68ba26fc));
  nor nor_6 (nor_6_out, d_latch_4_q, d_latch_2_not_q);
  D_Latch d_latch_5 (.NOT_Q(n_Z_OUT), .D(multiplexer_1_out), .EN(PHI1));  // open: Q
  D_Latch d_latch_6 (.NOT_Q(d_latch_6_not_q), .D(n_Z_OUT), .EN(PHI2));  // open: Q
  D_Latch d_latch_7 (.NOT_Q(n_N_OUT), .D(multiplexer_2_out), .EN(PHI1));  // open: Q
  D_Latch d_latch_8 (.NOT_Q(d_latch_8_not_q), .D(n_N_OUT), .EN(PHI2));  // open: Q
  D_Latch d_latch_9 (.NOT_Q(n_C_OUT), .D(and_2_out), .EN(PHI1));  // open: Q
  D_Latch d_latch_10 (.Q(d_latch_10_q), .D(n_C_OUT), .EN(PHI2));  // open: NOT_Q
  D_Latch d_latch_11 (.NOT_Q(n_D_OUT), .D(and_3_out), .EN(PHI1));  // open: Q
  D_Latch d_latch_12 (.Q(d_latch_12_q), .D(n_D_OUT), .EN(PHI2));  // open: NOT_Q
  D_Latch d_latch_13 (.NOT_Q(n_I_OUT), .D(and_4_out), .EN(PHI1));  // open: Q
  D_Latch d_latch_14 (.Q(d_latch_14_q), .D(n_I_OUT), .EN(PHI2));  // open: NOT_Q
  D_Latch d_latch_15 (.NOT_Q(n_V_OUT), .D(and_5_out), .EN(PHI1));  // open: Q
  D_Latch d_latch_16 (.Q(d_latch_16_q), .D(n_V_OUT), .EN(PHI2));  // open: NOT_Q
  D_Latch d_latch_17 (.Q(d_latch_17_q), .D(nor_6_out), .EN(PHI2));  // open: NOT_Q
  not not_12 (not_12_out, n_C_OUT);
  assign DB0_Out = P_DB ? not_12_out : 1'bz;  // Controlled_Buffer controlled_buffer_1
  not not_13 (not_13_out, n_Z_OUT);
  assign DB1_Out = P_DB ? not_13_out : 1'bz;  // Controlled_Buffer controlled_buffer_2
  not not_14 (not_14_out, n_I_OUT);
  assign DB2_Out = P_DB ? not_14_out : 1'bz;  // Controlled_Buffer controlled_buffer_3
  not not_15 (not_15_out, n_D_OUT);
  assign DB3_Out = P_DB ? not_15_out : 1'bz;  // Controlled_Buffer controlled_buffer_4
  assign DB4_Out = P_DB ? B_OUT : 1'bz;  // Controlled_Buffer controlled_buffer_5
  not not_16 (not_16_out, n_V_OUT);
  assign DB6_Out = P_DB ? not_16_out : 1'bz;  // Controlled_Buffer controlled_buffer_6
  not not_17 (not_17_out, n_N_OUT);
  assign DB7_Out = P_DB ? not_17_out : 1'bz;  // Controlled_Buffer controlled_buffer_7

  // Other names for the same wires on the sheet: DB0 = DB0_In; DB2 = DB2_In; DB3 = DB3_In; DB6 = DB6_In

  // Notes on the sheet:
  //   ACR/C
  //   AVR/V
  //   /DB1
  //   /DBZ
  //   /DB7
  //   DB/C
  //   IR5/D
  //   IR5/I
  //   DB/V
  //   1/V
  //   IR5/C
  //   /ACR
  //   ACR/C
  //   /DB0
  //   DB/C
  //   IR5/D
  //   /DB3
  //   IR5/I
  //   /DB2
  //   /AVR
  //   AVR/V
  //   /DB6
  //   DB/V
  //   0/V
  //   V FLAG
  //   Z FLAG
  //   /Z_OUT
  //   N FLAG
  //   /N_OUT
  //   C FLAG
  //   /C_OUT
  //   D FLAG
  //   /D_OUT
  //   I FLAG
  //   /I_OUT
  //   /V_OUT
  //   N.C.
endmodule

module ABL (
  input  PHI1,
  input  PHI2,
  input  ADL_ABL,
  input  L_0_ADL0,
  input  L_0_ADL1,
  input  L_0_ADL2,
  input  ADL0,
  input  ADL1,
  input  ADL2,
  input  ADL3,
  input  ADL4,
  input  ADL5,
  input  ADL6,
  input  ADL7,
  output A0,
  output A1,
  output A2,
  output A3,
  output A4,
  output A5,
  output A6,
  output A7
);

  ABL_LOW_BIT _0 (.Ax(A0), .ADL_ABL(ADL_ABL), .ZERO_ADLx(L_0_ADL0), .ADLx(ADL0), .PHI1(PHI1), .PHI2(PHI2));
  ABL_LOW_BIT _1 (.Ax(A1), .ADL_ABL(ADL_ABL), .ZERO_ADLx(L_0_ADL1), .ADLx(ADL1), .PHI1(PHI1), .PHI2(PHI2));
  ABL_LOW_BIT _2 (.Ax(A2), .ADL_ABL(ADL_ABL), .ZERO_ADLx(L_0_ADL2), .ADLx(ADL2), .PHI1(PHI1), .PHI2(PHI2));
  ABL_BIT _3 (.Ax(A3), .ADL_ABL(ADL_ABL), .ADLx(ADL3), .PHI1(PHI1), .PHI2(PHI2));
  ABL_BIT _4 (.Ax(A4), .ADL_ABL(ADL_ABL), .ADLx(ADL4), .PHI1(PHI1), .PHI2(PHI2));
  ABL_BIT _5 (.Ax(A5), .ADL_ABL(ADL_ABL), .ADLx(ADL5), .PHI1(PHI1), .PHI2(PHI2));
  ABL_BIT _6 (.Ax(A6), .ADL_ABL(ADL_ABL), .ADLx(ADL6), .PHI1(PHI1), .PHI2(PHI2));
  ABL_BIT _7 (.Ax(A7), .ADL_ABL(ADL_ABL), .ADLx(ADL7), .PHI1(PHI1), .PHI2(PHI2));
endmodule

module REGS_BIT (
  input  PHI2,
  input  Y_SB,
  input  SB_Y,
  input  X_SB,
  input  SB_X,
  input  S_ADL,
  input  S_S,
  input  SB_S,
  input  S_SB,
  input  SBx_In,
  output SBx_Out,
  output ADLx,
  output Y_Debug,
  output X_Debug,
  output S_Debug
);

  wire and_1_out, and_2_out, and_3_out, not_1_out, not_2_out, not_3_out;

  not not_1 (not_1_out, PHI2);
  not not_2 (not_2_out, PHI2);
  not not_3 (not_3_out, PHI2);
  and and_1 (and_1_out, not_1_out, SB_Y);
  and and_2 (and_2_out, not_2_out, SB_X);
  and and_3 (and_3_out, not_3_out, SB_S);
  D_Flip_Flop #(.trigger("high")) Y (.D(SBx_In), .clk(and_1_out), .Q(Y_Debug));  // open: Qn, preset, reset
  D_Flip_Flop #(.trigger("high")) X (.D(SBx_In), .clk(and_2_out), .Q(X_Debug));  // open: Qn, preset, reset
  D_Flip_Flop #(.trigger("high")) S (.D(SBx_In), .clk(and_3_out), .Q(S_Debug));  // open: Qn, preset, reset
  assign SBx_Out = Y_SB ? Y_Debug : 1'bz;  // Controlled_Buffer controlled_buffer_1
  assign SBx_Out = X_SB ? X_Debug : 1'bz;  // Controlled_Buffer controlled_buffer_2
  assign SBx_Out = S_SB ? S_Debug : 1'bz;  // Controlled_Buffer controlled_buffer_3
  assign ADLx = S_ADL ? S_Debug : 1'bz;  // Controlled_Buffer controlled_buffer_4

  // Notes on the sheet:
  //   unused
endmodule

module REGS (
  input  PHI2,
  input  Y_SB,
  input  SB_Y,
  input  X_SB,
  input  SB_X,
  input  S_ADL,
  input  S_S,
  input  SB_S,
  input  S_SB,
  input  SB0_In,
  input  SB1_In,
  input  SB2_In,
  input  SB3_In,
  input  SB4_In,
  input  SB5_In,
  input  SB6_In,
  input  SB7_In,
  output SB0_Out,
  output SB1_Out,
  output SB2_Out,
  output SB3_Out,
  output SB4_Out,
  output SB5_Out,
  output SB6_Out,
  output SB7_Out,
  output ADL0,
  output ADL1,
  output ADL2,
  output ADL3,
  output ADL4,
  output ADL5,
  output ADL6,
  output ADL7,
  output [7:0] S_Debug,
  output [7:0] Y_Debug,
  output [7:0] X_Debug
);

  REGS_BIT _0 (
    .ADLx(ADL0), .Y_Debug(Y_Debug[0]), .X_Debug(X_Debug[0]), .S_Debug(S_Debug[0]), .SBx_Out(SB0_Out),
    .Y_SB(Y_SB), .SB_Y(SB_Y), .X_SB(X_SB), .SB_X(SB_X), .S_ADL(S_ADL), .S_S(S_S), .SB_S(SB_S), .S_SB(S_SB),
    .SBx_In(SB0_In), .PHI2(PHI2));
  REGS_BIT _4 (
    .ADLx(ADL4), .Y_Debug(Y_Debug[4]), .X_Debug(X_Debug[4]), .S_Debug(S_Debug[4]), .SBx_Out(SB4_Out),
    .Y_SB(Y_SB), .SB_Y(SB_Y), .X_SB(X_SB), .SB_X(SB_X), .S_ADL(S_ADL), .S_S(S_S), .SB_S(SB_S), .S_SB(S_SB),
    .SBx_In(SB4_In), .PHI2(PHI2));
  REGS_BIT _1 (
    .ADLx(ADL1), .Y_Debug(Y_Debug[1]), .X_Debug(X_Debug[1]), .S_Debug(S_Debug[1]), .SBx_Out(SB1_Out),
    .Y_SB(Y_SB), .SB_Y(SB_Y), .X_SB(X_SB), .SB_X(SB_X), .S_ADL(S_ADL), .S_S(S_S), .SB_S(SB_S), .S_SB(S_SB),
    .SBx_In(SB1_In), .PHI2(PHI2));
  REGS_BIT _5 (
    .ADLx(ADL5), .Y_Debug(Y_Debug[5]), .X_Debug(X_Debug[5]), .S_Debug(S_Debug[5]), .SBx_Out(SB5_Out),
    .Y_SB(Y_SB), .SB_Y(SB_Y), .X_SB(X_SB), .SB_X(SB_X), .S_ADL(S_ADL), .S_S(S_S), .SB_S(SB_S), .S_SB(S_SB),
    .SBx_In(SB5_In), .PHI2(PHI2));
  REGS_BIT _2 (
    .ADLx(ADL2), .Y_Debug(Y_Debug[2]), .X_Debug(X_Debug[2]), .S_Debug(S_Debug[2]), .SBx_Out(SB2_Out),
    .Y_SB(Y_SB), .SB_Y(SB_Y), .X_SB(X_SB), .SB_X(SB_X), .S_ADL(S_ADL), .S_S(S_S), .SB_S(SB_S), .S_SB(S_SB),
    .SBx_In(SB2_In), .PHI2(PHI2));
  REGS_BIT _6 (
    .ADLx(ADL6), .Y_Debug(Y_Debug[6]), .X_Debug(X_Debug[6]), .S_Debug(S_Debug[6]), .SBx_Out(SB6_Out),
    .Y_SB(Y_SB), .SB_Y(SB_Y), .X_SB(X_SB), .SB_X(SB_X), .S_ADL(S_ADL), .S_S(S_S), .SB_S(SB_S), .S_SB(S_SB),
    .SBx_In(SB6_In), .PHI2(PHI2));
  REGS_BIT _3 (
    .ADLx(ADL3), .Y_Debug(Y_Debug[3]), .X_Debug(X_Debug[3]), .S_Debug(S_Debug[3]), .SBx_Out(SB3_Out),
    .Y_SB(Y_SB), .SB_Y(SB_Y), .X_SB(X_SB), .SB_X(SB_X), .S_ADL(S_ADL), .S_S(S_S), .SB_S(SB_S), .S_SB(S_SB),
    .SBx_In(SB3_In), .PHI2(PHI2));
  REGS_BIT _7 (
    .ADLx(ADL7), .Y_Debug(Y_Debug[7]), .X_Debug(X_Debug[7]), .S_Debug(S_Debug[7]), .SBx_Out(SB7_Out),
    .Y_SB(Y_SB), .SB_Y(SB_Y), .X_SB(X_SB), .SB_X(SB_X), .S_ADL(S_ADL), .S_S(S_S), .SB_S(SB_S), .S_SB(S_SB),
    .SBx_In(SB7_In), .PHI2(PHI2));

  // Other names for the same wires on the sheet: S_ADL_07acd992 = S_ADL; S_S_09f08a69 = S_S; S_SB_e37affed = S_SB;
  //   SB_S_4c94ee46 = SB_S; SB_X_cf392641 = SB_X; SB_Y_9a33ae5e = SB_Y; X_SB_222038db = X_SB; Y_SB_d628d28f = Y_SB
endmodule

module DL_BIT (
  input  PHI1,
  input  PHI2,
  input  DL_ADL,
  input  DL_ADH,
  input  DL_DB,
  input  RD,
  input  DBx_In,
  input  Dx_In,
  output ADLx_Out,
  output ADHx_Out,
  output DBx_Out,
  output Dx_Out,
  output DOR_Debug,
  output DL_Debug
);

  wire and_1_out, and_2_out, and_3_out, not_1_out, not_2_out, not_3_out;

  D_Latch DL (.NOT_Q(DL_Debug), .D(not_1_out), .EN(PHI2));  // open: Q
  not not_1 (not_1_out, Dx_In);
  D_Latch DOR (.NOT_Q(DOR_Debug), .D(not_2_out), .EN(PHI1));  // open: Q
  not not_2 (not_2_out, DBx_In);
  and and_1 (and_1_out, DL_ADL, PHI1);
  and and_2 (and_2_out, DL_ADH, PHI1);
  and and_3 (and_3_out, DL_DB, PHI1);
  not not_3 (not_3_out, RD);
  assign ADLx_Out = and_1_out ? DL_Debug : 1'bz;  // Controlled_Buffer controlled_buffer_1
  assign ADHx_Out = and_2_out ? DL_Debug : 1'bz;  // Controlled_Buffer controlled_buffer_2
  assign DBx_Out = and_3_out ? DL_Debug : 1'bz;  // Controlled_Buffer controlled_buffer_3
  assign Dx_Out = not_3_out ? DOR_Debug : 1'bz;  // Controlled_Buffer controlled_buffer_4
endmodule

module DL (
  input  PHI1,
  input  PHI2,
  input  WR,
  input  DL_ADL_6c5e0116,
  input  DL_ADH_3839a3d0,
  input  DL_DB_69522204,
  input  DB0_In,
  input  DB1_In,
  input  DB2_In,
  input  DB3_In,
  input  DB4_In,
  input  DB5_In,
  input  DB6_In,
  input  DB7_In,
  input  D0_In,
  input  D1_In,
  input  D2_In,
  input  D3_In,
  input  D4_In,
  input  D5_In,
  input  D6_In,
  input  D7_In,
  output DB0_Out,
  output DB1_Out,
  output DB2_Out,
  output DB3_Out,
  output DB4_Out,
  output DB5_Out,
  output DB6_Out,
  output DB7_Out,
  output ADL0,
  output ADL1,
  output ADL2,
  output ADL3,
  output ADL4,
  output ADL5,
  output ADL6,
  output ADL7,
  output ADH0,
  output ADH1,
  output ADH2,
  output ADH3,
  output ADH4,
  output ADH5,
  output ADH6,
  output ADH7,
  output D0_Out,
  output D1_Out,
  output D2_Out,
  output D3_Out,
  output D4_Out,
  output D5_Out,
  output D6_Out,
  output D7_Out,
  output [7:0] DL_Debug,
  output [7:0] DOR_Debug
);

  wire d_latch_1_not_q, RD;

  D_Latch d_latch_1 (.NOT_Q(d_latch_1_not_q), .D(WR), .EN(PHI1));  // open: Q
  Multiplexer multiplexer_1 (.in0(d_latch_1_not_q), .in1(1'b1), .out(RD), .sel(PHI2));
  DL_BIT _0 (
    .ADLx_Out(ADL0), .ADHx_Out(ADH0), .DBx_Out(DB0_Out), .Dx_Out(D0_Out), .DOR_Debug(DOR_Debug[0]),
    .DL_Debug(DL_Debug[0]), .DL_ADL(DL_ADL_6c5e0116), .DL_ADH(DL_ADH_3839a3d0), .DL_DB(DL_DB_69522204),
    .RD(RD), .DBx_In(DB0_In), .Dx_In(D0_In), .PHI1(PHI1), .PHI2(PHI2));
  DL_BIT _1 (
    .ADLx_Out(ADL1), .ADHx_Out(ADH1), .DBx_Out(DB1_Out), .Dx_Out(D1_Out), .DOR_Debug(DOR_Debug[1]),
    .DL_Debug(DL_Debug[1]), .DL_ADL(DL_ADL_6c5e0116), .DL_ADH(DL_ADH_3839a3d0), .DL_DB(DL_DB_69522204),
    .RD(RD), .DBx_In(DB1_In), .Dx_In(D1_In), .PHI1(PHI1), .PHI2(PHI2));
  DL_BIT _2 (
    .ADLx_Out(ADL2), .ADHx_Out(ADH2), .DBx_Out(DB2_Out), .Dx_Out(D2_Out), .DOR_Debug(DOR_Debug[2]),
    .DL_Debug(DL_Debug[2]), .DL_ADL(DL_ADL_6c5e0116), .DL_ADH(DL_ADH_3839a3d0), .DL_DB(DL_DB_69522204),
    .RD(RD), .DBx_In(DB2_In), .Dx_In(D2_In), .PHI1(PHI1), .PHI2(PHI2));
  DL_BIT _3 (
    .ADLx_Out(ADL3), .ADHx_Out(ADH3), .DBx_Out(DB3_Out), .Dx_Out(D3_Out), .DOR_Debug(DOR_Debug[3]),
    .DL_Debug(DL_Debug[3]), .DL_ADL(DL_ADL_6c5e0116), .DL_ADH(DL_ADH_3839a3d0), .DL_DB(DL_DB_69522204),
    .RD(RD), .DBx_In(DB3_In), .Dx_In(D3_In), .PHI1(PHI1), .PHI2(PHI2));
  DL_BIT _4 (
    .ADLx_Out(ADL4), .ADHx_Out(ADH4), .DBx_Out(DB4_Out), .Dx_Out(D4_Out), .DOR_Debug(DOR_Debug[4]),
    .DL_Debug(DL_Debug[4]), .DL_ADL(DL_ADL_6c5e0116), .DL_ADH(DL_ADH_3839a3d0), .DL_DB(DL_DB_69522204),
    .RD(RD), .DBx_In(DB4_In), .Dx_In(D4_In), .PHI1(PHI1), .PHI2(PHI2));
  DL_BIT _5 (
    .ADLx_Out(ADL5), .ADHx_Out(ADH5), .DBx_Out(DB5_Out), .Dx_Out(D5_Out), .DOR_Debug(DOR_Debug[5]),
    .DL_Debug(DL_Debug[5]), .DL_ADL(DL_ADL_6c5e0116), .DL_ADH(DL_ADH_3839a3d0), .DL_DB(DL_DB_69522204),
    .RD(RD), .DBx_In(DB5_In), .Dx_In(D5_In), .PHI1(PHI1), .PHI2(PHI2));
  DL_BIT _6 (
    .ADLx_Out(ADL6), .ADHx_Out(ADH6), .DBx_Out(DB6_Out), .Dx_Out(D6_Out), .DOR_Debug(DOR_Debug[6]),
    .DL_Debug(DL_Debug[6]), .DL_ADL(DL_ADL_6c5e0116), .DL_ADH(DL_ADH_3839a3d0), .DL_DB(DL_DB_69522204),
    .RD(RD), .DBx_In(DB6_In), .Dx_In(D6_In), .PHI1(PHI1), .PHI2(PHI2));
  DL_BIT _7 (
    .ADLx_Out(ADL7), .ADHx_Out(ADH7), .DBx_Out(DB7_Out), .Dx_Out(D7_Out), .DOR_Debug(DOR_Debug[7]),
    .DL_Debug(DL_Debug[7]), .DL_ADL(DL_ADL_6c5e0116), .DL_ADH(DL_ADH_3839a3d0), .DL_DB(DL_DB_69522204),
    .RD(RD), .DBx_In(DB7_In), .Dx_In(D7_In), .PHI1(PHI1), .PHI2(PHI2));
endmodule

module ALU (
  input  PHI2,
  input  NDB_ADD_ee0a1870,
  input  DB_ADD_48d85b7e,
  input  L_0_ADD_81d17e61,
  input  SB_ADD_0eab26ac,
  input  ADL_ADD_e28b8a30,
  input  ADD_SB06_a3738230,
  input  ADD_SB7_a8f4b77a,
  input  ADD_ADL_3fac4345,
  input  ANDS,
  input  EORS,
  input  ORS,
  input  SRS,
  input  SUMS,
  input  SB_AC_b159eec5,
  input  AC_SB_c49f602a,
  input  AC_DB_519ce409,
  input  SB_DB_641efa5a,
  input  SB_ADH_4f1456ff,
  input  L_0_ADH0_e340c71e,
  input  L_0_ADH17_f181a8fa,
  input  n_ACIN,
  input  n_DAA,
  input  n_DSA,
  input  SB0,
  input  in_26,
  input  ADL0,
  input  in_28,
  input  DB1,
  input  ADL1,
  input  SB2,
  input  in_32,
  input  in_33,
  input  SB3,
  input  in_35,
  input  ADL3,
  input  in_37,
  input  in_38,
  input  in_39,
  input  SB5,
  input  DB5,
  input  ADL5,
  input  SB6,
  input  DB6,
  input  in_45,
  input  in_46,
  input  in_47,
  input  ADL7,
  output ACR,
  output AVR,
  output [7:0] ADD_Debug,
  output [7:0] AC_Debug,
  output [7:0] AI_Debug,
  output [7:0] BI_Debug,
  output out_55,
  output DB0,
  output out_57,
  output ADH0,
  output SB1,
  output out_60,
  output out_61,
  output ADH1,
  output out_63,
  output DB2,
  output ADL2,
  output ADH2,
  output out_67,
  output DB3,
  output out_69,
  output ADH3,
  output SB4,
  output DB4,
  output ADL4,
  output ADH4,
  output out_75,
  output out_76,
  output out_77,
  output ADH5,
  output out_79,
  output out_80,
  output ADL6,
  output ADH6,
  output SB7,
  output DB7,
  output out_85,
  output ADH7
);

  wire ACLatch_q, ALU_OPS_inst_carry4, ALU_OPS_inst_carry6, ALU_OPS_inst_l_carry3_9e435978,
       ALU_OPS_inst_l_carry7_b3181e70, and_1_out, BCD_Carry_inst_dc3, BCD_Carry_inst_dc7, DCLatch_q,
       nand_1_out, nor_1_out, nor_2_out, not_1_out, not_2_out;
  wire [7:0] Adder_Hold_inst_n_addx_out, ALU_OPS_inst_nand0, ALU_OPS_inst_nor0, ALU_OPS_inst_res0,
       ALU_OPS_inst_xor0, BCD_inst_out0;

  ALU_OPS ALU_OPS_inst (
    .BI_Debug(BI_Debug), .L_carry3_9e435978(ALU_OPS_inst_l_carry3_9e435978),
    .L_carry7_b3181e70(ALU_OPS_inst_l_carry7_b3181e70), .xor2(ALU_OPS_inst_xor0[2]),
    .xor3(ALU_OPS_inst_xor0[3]), .xor4(ALU_OPS_inst_xor0[4]), .xor5(ALU_OPS_inst_xor0[5]),
    .xor6(ALU_OPS_inst_xor0[6]), .xor7(ALU_OPS_inst_xor0[7]), .res0(ALU_OPS_inst_res0[0]),
    .res1(ALU_OPS_inst_res0[1]), .res2(ALU_OPS_inst_res0[2]), .res3(ALU_OPS_inst_res0[3]),
    .res4(ALU_OPS_inst_res0[4]), .res5(ALU_OPS_inst_res0[5]), .res6(ALU_OPS_inst_res0[6]),
    .res7(ALU_OPS_inst_res0[7]), .carry4(ALU_OPS_inst_carry4), .nor0(ALU_OPS_inst_nor0[0]),
    .nor1(ALU_OPS_inst_nor0[1]), .nor2(ALU_OPS_inst_nor0[2]), .nor3(ALU_OPS_inst_nor0[3]),
    .nor4(ALU_OPS_inst_nor0[4]), .nor5(ALU_OPS_inst_nor0[5]), .nor6(ALU_OPS_inst_nor0[6]),
    .nor7(ALU_OPS_inst_nor0[7]), .nand0(ALU_OPS_inst_nand0[0]), .carry6(ALU_OPS_inst_carry6),
    .nand1(ALU_OPS_inst_nand0[1]), .nand2(ALU_OPS_inst_nand0[2]), .nand3(ALU_OPS_inst_nand0[3]),
    .nand4(ALU_OPS_inst_nand0[4]), .nand5(ALU_OPS_inst_nand0[5]), .nand6(ALU_OPS_inst_nand0[6]),
    .nand7(ALU_OPS_inst_nand0[7]), .xor0(ALU_OPS_inst_xor0[0]), .xor1(ALU_OPS_inst_xor0[1]),
    .AI_Debug(AI_Debug), .DB_ADD_48d85b7e(DB_ADD_48d85b7e), .DB5(DB5), .DB6(DB6), .DB7(in_47), .ADL0(ADL0),
    .ADL1(ADL1), .ADL2(in_33), .ADL3(ADL3), .ADL4(in_39), .ADL5(ADL5), .L_0_ADD_81d17e61(L_0_ADD_81d17e61),
    .ADL6(in_45), .ADL7(ADL7), .SB_ADD_0eab26ac(SB_ADD_0eab26ac), .ADL_ADD_e28b8a30(ADL_ADD_e28b8a30),
    .ANDS(ANDS), .EORS(EORS), .ORS(ORS), .SRS(SRS), .SUMS(SUMS), .L_cin_af3836dd(n_ACIN),
    .DC3(BCD_Carry_inst_dc3), .SB0(SB0), .SB1(in_28), .SB2(SB2), .SB3(SB3),
    .NDB_ADD_ee0a1870(NDB_ADD_ee0a1870), .SB4(in_37), .SB5(SB5), .SB6(SB6), .SB7(in_46), .DB0(in_26),
    .DB1(DB1), .DB2(in_32), .DB3(in_35), .DB4(in_38));
  BCD_CARRY BCD_Carry_inst (
    .DC3(BCD_Carry_inst_dc3), .DC7(BCD_Carry_inst_dc7), .n_ACIN(n_ACIN), .carry4(ALU_OPS_inst_carry4),
    .n_DAA(n_DAA), .\nor (ALU_OPS_inst_nor0), .\nand (ALU_OPS_inst_nand0), .\xor (ALU_OPS_inst_xor0));
  nand nand_1 (nand_1_out, ALU_OPS_inst_carry6, ALU_OPS_inst_nor0[7]);
  nor nor_1 (nor_1_out, ALU_OPS_inst_carry6, ALU_OPS_inst_l_carry7_b3181e70);
  not not_1 (not_1_out, nor_1_out);
  ALU_ADD Adder_Hold_inst (
    .n_ADDx_Out(Adder_Hold_inst_n_addx_out), .SB0(out_55), .SB1(SB1), .SB2(out_63), .SB3(out_67), .SB4(SB4),
    .SB5(out_75), .SB6(out_79), .SB7(SB7), .ADL0(out_57), .ADL1(out_61), .ADL2(ADL2), .ADL3(out_69),
    .ADL4(ADL4), .ADL5(out_77), .ADL6(ADL6), .ADL7(out_85), .ADD_Debug(ADD_Debug),
    .ADD_SB06(ADD_SB06_a3738230), .ADD_SB7(ADD_SB7_a8f4b77a), .ADD_ADL(ADD_ADL_3fac4345), .PHI2(PHI2),
    .n_res(ALU_OPS_inst_res0));
  D_Latch DCLatch (.Q(DCLatch_q), .D(BCD_Carry_inst_dc7), .EN(PHI2));  // open: NOT_Q
  D_Latch ACLatch (.Q(ACLatch_q), .D(not_2_out), .EN(PHI2));  // open: NOT_Q
  not not_2 (not_2_out, ALU_OPS_inst_l_carry7_b3181e70);
  D_Latch AVRLatch (.NOT_Q(AVR), .D(and_1_out), .EN(PHI2));  // open: Q
  and and_1 (and_1_out, nand_1_out, not_1_out);
  nor nor_2 (nor_2_out, DCLatch_q, ACLatch_q);
  not not_3 (ACR, nor_2_out);
  ALU_BCD BCD_inst (
    .out0(BCD_inst_out0[0]), .out1(BCD_inst_out0[1]), .out2(BCD_inst_out0[2]), .out3(BCD_inst_out0[3]),
    .out4(BCD_inst_out0[4]), .out5(BCD_inst_out0[5]), .out6(BCD_inst_out0[6]), .out7(BCD_inst_out0[7]),
    .n_carry3(ALU_OPS_inst_l_carry3_9e435978), .ACR(ACR), .n_DAA(n_DAA), .n_DSA(n_DSA), .SB0(SB0),
    .SB1(in_28), .SB2(SB2), .SB3(SB3), .SB4(in_37), .SB5(SB5), .SB6(SB6), .PHI2(PHI2), .SB7(in_46),
    .n_ADDx_In(Adder_Hold_inst_n_addx_out));
  ALU_AC AC_inst (
    .AC_Debug(AC_Debug), .SB1_Out(SB1), .SB2_Out(out_63), .SB3_Out(out_67), .SB4_Out(SB4), .SB5_Out(out_75),
    .SB6_Out(out_79), .SB7_Out(SB7), .ADH0(ADH0), .ADH1(ADH1), .ADH2(ADH2), .ADH3(ADH3), .ADH4(ADH4),
    .ADH5(ADH5), .SB0_Out(out_55), .ADH6(ADH6), .ADH7(ADH7), .DB0(DB0), .DB1(out_60), .DB2(DB2), .DB3(DB3),
    .DB4(DB4), .DB5(out_76), .DB6(out_80), .DB7(DB7), .SB_AC(SB_AC_b159eec5), .AC_SB(AC_SB_c49f602a),
    .AC_DB(AC_DB_519ce409), .SB_DB(SB_DB_641efa5a), .SB_ADH(SB_ADH_4f1456ff), .ZR_ADH0(L_0_ADH0_e340c71e),
    .ZR_ADH17(L_0_ADH17_f181a8fa), .SB0_In(SB0), .SB1_In(in_28), .SB2_In(SB2), .SB3_In(SB3), .SB4_In(in_37),
    .SB5_In(SB5), .SB6_In(SB6), .SB7_In(in_46), .PHI2(PHI2), .BCD_in(BCD_inst_out0));

  // Notes on the sheet:
  //   x8
  //   AVR
  //   ACR
  //   x8
  //   x8
endmodule

module PC (
  input  PHI2,
  input  ADL_PCL_9a95c372,
  input  PCL_PCL_4f350f4d,
  input  PCL_ADL_ee043dbc,
  input  PCL_DB_4172714e,
  input  ADH_PCH_61520abf,
  input  PCH_PCH_807b9fbd,
  input  PCH_ADH_ead93594,
  input  PCH_DB_a81fefa0,
  input  n_1_PC,
  input  ADL0_In,
  input  ADL1_In,
  input  ADL2_In,
  input  ADL3_In,
  input  ADL4_In,
  input  ADL5_In,
  input  ADL6_In,
  input  ADL7_In,
  input  ADH0_In,
  input  ADH1_In,
  input  ADH2_In,
  input  ADH3_In,
  input  ADH4_In,
  input  ADH5_In,
  input  ADH6_In,
  input  ADH7_In,
  output DB0,
  output DB1,
  output DB2,
  output DB3,
  output DB4,
  output DB5,
  output DB6,
  output DB7,
  output ADL0_Out,
  output ADL1_Out,
  output ADL2_Out,
  output ADL3_Out,
  output ADL4_Out,
  output ADL5_Out,
  output ADL6_Out,
  output ADL7_Out,
  output ADH0_Out,
  output ADH1_Out,
  output ADH2_Out,
  output ADH3_Out,
  output ADH4_Out,
  output ADH5_Out,
  output ADH6_Out,
  output ADH7_Out,
  output [15:0] PC_Debug,
  output [15:0] PCS_Debug
);

  wire PC_PCL_pclc;

  PCL PC_PCL (
    .PCL_Debug(PC_Debug[7:0]), .PCLS_Debug(PCS_Debug[7:0]), .ADL0(ADL0_Out), .ADL1(ADL1_Out),
    .out_17(ADL2_Out), .ADL3(ADL3_Out), .out_19(ADL4_Out), .ADL5(ADL5_Out), .out_21(ADL6_Out),
    .ADL7(ADL7_Out), .DB0(DB0), .DB1(DB1), .DB2(DB2), .DB3(DB3), .DB4(DB4), .DB5(DB5), .DB6(DB6), .DB7(DB7),
    .PCLC(PC_PCL_pclc), .cin(n_1_PC), .ADL_PCL_9a95c372(ADL_PCL_9a95c372),
    .PCL_PCL_4f350f4d(PCL_PCL_4f350f4d), .PCL_ADL_ee043dbc(PCL_ADL_ee043dbc),
    .PCL_DB_4172714e(PCL_DB_4172714e), .PHI2(PHI2), .ADL0_In(ADL0_In), .ADL1_In(ADL1_In), .ADL2_In(ADL2_In),
    .ADL3_In(ADL3_In), .ADL4_In(ADL4_In), .ADL5_In(ADL5_In), .ADL6_In(ADL6_In), .ADL7_In(ADL7_In));
  PCH PC_PCH (
    .ADH0(ADH0_Out), .out_16(ADH1_Out), .out_17(ADH2_Out), .out_18(ADH3_Out), .out_19(ADH4_Out),
    .out_20(ADH5_Out), .ADH6(ADH6_Out), .ADH7(ADH7_Out), .DB0(DB0), .DB1(DB1), .DB2(DB2), .DB3(DB3),
    .DB4(DB4), .DB5(DB5), .DB6(DB6), .DB7(DB7), .PCH_Debug(PC_Debug[15:8]), .PCHS_Debug(PCS_Debug[15:8]),
    .cin(PC_PCL_pclc), .ADH_PCH(ADH_PCH_61520abf), .PCH_PCH(PCH_PCH_807b9fbd), .PCH_ADH(PCH_ADH_ead93594),
    .PCH_DB(PCH_DB_a81fefa0), .PHI2(PHI2), .in_7(ADH0_In), .ADH1(ADH1_In), .ADH2(ADH2_In), .ADH3(ADH3_In),
    .ADH4(ADH4_In), .ADH5(ADH5_In), .in_13(ADH6_In), .in_14(ADH7_In));
endmodule

module ABL_LOW_BIT (
  input  PHI1,
  input  PHI2,
  input  ADL_ABL,
  input  ZERO_ADLx,
  input  ADLx,
  output Ax
);

  wire and_1_out, and_2_out, not1_out, not_1_out;

  not not_1 (not_1_out, ZERO_ADLx);
  and and_1 (and_1_out, not_1_out, ADLx);
  not not1 (not1_out, and_1_out);
  and and_2 (and_2_out, PHI1, ADL_ABL);
  D_Flip_Flop #(.trigger("high")) d_ff_1 (.D(not1_out), .clk(and_2_out), .Qn(Ax));  // open: Q, preset, reset

  // Notes on the sheet:
  //   not used
endmodule

module ABL_BIT (
  input  PHI1,
  input  PHI2,
  input  ADL_ABL,
  input  ADLx,
  output Ax
);

  wire and_1_out, not1_out;

  and and_1 (and_1_out, PHI1, ADL_ABL);
  not not1 (not1_out, ADLx);
  D_Flip_Flop #(.trigger("high")) d_ff_1 (.D(not1_out), .clk(and_1_out), .Qn(Ax));  // open: Q, preset, reset

  // Notes on the sheet:
  //   not used
endmodule

module ABH_BIT (
  input  PHI1,
  input  PHI2,
  input  ADH_ABH,
  input  ADHx,
  output Ax
);

  wire and_1_out, not1_out;

  and and_1 (and_1_out, PHI1, ADH_ABH);
  not not1 (not1_out, ADHx);
  D_Flip_Flop #(.trigger("high")) d_ff_1 (.D(not1_out), .clk(and_1_out), .Qn(Ax));  // open: Q, preset, reset

  // Notes on the sheet:
  //   not used
endmodule

module PCL_EVEN_BIT (
  input  PHI2,
  input  cin,
  input  ADL_PCL,
  input  PCL_PCL,
  input  PCL_ADL,
  input  PCL_DB,
  input  ADLx_In,
  output DBx,
  output ADLx_Out,
  output cout,
  output sout,
  output PCL_Debug,
  output PCLS_Debug
);

  wire and_1_out, controlled_buffer_1_out, nand_1_out, not_1_out, PCL_Even_qn;

  nor nor_1 (cout, cin, sout);
  assign controlled_buffer_1_out = PCL_PCL ? PCL_Debug : 1'bz;  // Controlled_Buffer controlled_buffer_1
  assign controlled_buffer_1_out = ADL_PCL ? ADLx_In : 1'bz;  // Controlled_Buffer controlled_buffer_2
  nand nand_1 (nand_1_out, cin, sout);
  not not_1 (not_1_out, cout);
  D_Flip_Flop #(.trigger("falling")) PCL_Even (.D(and_1_out), .clk(PHI2), .Qn(PCL_Even_qn));  // open: Q, preset, reset
  D_Flip_Flop #(.trigger("high")) PCLS_Even (
    .D(controlled_buffer_1_out), .clk(1'b1), .Q(PCLS_Debug), .Qn(sout));  // open: preset, reset
  and and_1 (and_1_out, nand_1_out, not_1_out);
  not not_2 (PCL_Debug, PCL_Even_qn);
  assign DBx = PCL_DB ? PCL_Debug : 1'bz;  // Controlled_Buffer controlled_buffer_3
  assign ADLx_Out = PCL_ADL ? PCL_Debug : 1'bz;  // Controlled_Buffer controlled_buffer_4

  // Notes on the sheet:
  //   posedge
endmodule

module PCL_ODD_BIT (
  input  PHI2,
  input  cin,
  input  ADL_PCL,
  input  PCL_PCL,
  input  PCL_ADL,
  input  PCL_DB,
  input  ADLx_In,
  output DBx,
  output ADLx_Out,
  output cout,
  output sout,
  output PCL_Debug,
  output PCLS_Debug
);

  wire controlled_buffer_1_out, nor_1_out, not_1_out, not_2_out, not_3_out, or_1_out;

  nand nand_1 (cout, cin, not_1_out);
  not not_1 (not_1_out, sout);
  not not_2 (not_2_out, sout);
  not not_3 (not_3_out, cout);
  D_Flip_Flop #(.trigger("falling")) PCL_Odd (.D(or_1_out), .clk(PHI2), .Qn(PCL_Debug));  // open: Q, preset, reset
  assign controlled_buffer_1_out = PCL_PCL ? PCL_Debug : 1'bz;  // Controlled_Buffer controlled_buffer_1
  D_Flip_Flop #(.trigger("high")) PCLS_Odd (
    .D(controlled_buffer_1_out), .clk(1'b1), .Q(PCLS_Debug), .Qn(sout));  // open: preset, reset
  assign controlled_buffer_1_out = ADL_PCL ? ADLx_In : 1'bz;  // Controlled_Buffer controlled_buffer_2
  nor nor_1 (nor_1_out, cin, not_2_out);
  or or_1 (or_1_out, nor_1_out, not_3_out);
  assign DBx = PCL_DB ? PCL_Debug : 1'bz;  // Controlled_Buffer controlled_buffer_3
  assign ADLx_Out = PCL_ADL ? PCL_Debug : 1'bz;  // Controlled_Buffer controlled_buffer_4

  // Notes on the sheet:
  //   posedge
endmodule

module PCH_EVEN_BIT (
  input  PHI2,
  input  cin,
  input  ADH_PCH,
  input  PCH_PCH,
  input  PCH_ADH,
  input  PCH_DB,
  input  ADHx_In,
  output DBx,
  output ADHx_Out,
  output cout,
  output sout,
  output PCH_Debug,
  output PCHS_Debug
);

  wire controlled_buffer_1_out, nor_1_out, not_1_out, not_2_out, not_3_out, or_1_out;

  nand nand_1 (cout, cin, not_1_out);
  not not_1 (not_1_out, sout);
  not not_2 (not_2_out, sout);
  not not_3 (not_3_out, cout);
  D_Flip_Flop #(.trigger("falling")) PCH_Even (.D(or_1_out), .clk(PHI2), .Qn(PCH_Debug));  // open: Q, preset, reset
  assign controlled_buffer_1_out = PCH_PCH ? PCH_Debug : 1'bz;  // Controlled_Buffer controlled_buffer_1
  D_Flip_Flop #(.trigger("high")) PCHS_Even (
    .D(controlled_buffer_1_out), .clk(1'b1), .Q(PCHS_Debug), .Qn(sout));  // open: preset, reset
  assign controlled_buffer_1_out = ADH_PCH ? ADHx_In : 1'bz;  // Controlled_Buffer controlled_buffer_2
  nor nor_1 (nor_1_out, cin, not_2_out);
  or or_1 (or_1_out, nor_1_out, not_3_out);
  assign DBx = PCH_DB ? PCH_Debug : 1'bz;  // Controlled_Buffer controlled_buffer_3
  assign ADHx_Out = PCH_ADH ? PCH_Debug : 1'bz;  // Controlled_Buffer controlled_buffer_4

  // Notes on the sheet:
  //   posedge
endmodule

module PCH_ODD_BIT (
  input  PHI2,
  input  cin,
  input  ADH_PCH,
  input  PCH_PCH,
  input  PCH_ADH,
  input  PCH_DB,
  input  ADHx_In,
  output DBx,
  output ADHx_Out,
  output cout,
  output sout,
  output PCH_Debug,
  output PCHS_Debug
);

  wire and_1_out, controlled_buffer_1_out, nand_1_out, not_1_out, PCH_Odd_qn;

  nor nor_1 (cout, cin, sout);
  assign controlled_buffer_1_out = PCH_PCH ? PCH_Debug : 1'bz;  // Controlled_Buffer controlled_buffer_1
  assign controlled_buffer_1_out = ADH_PCH ? ADHx_In : 1'bz;  // Controlled_Buffer controlled_buffer_2
  nand nand_1 (nand_1_out, cin, sout);
  not not_1 (not_1_out, cout);
  D_Flip_Flop #(.trigger("falling")) PCH_Odd (.D(and_1_out), .clk(PHI2), .Qn(PCH_Odd_qn));  // open: Q, preset, reset
  D_Flip_Flop #(.trigger("high")) PCHS_Odd (
    .D(controlled_buffer_1_out), .clk(1'b1), .Q(PCHS_Debug), .Qn(sout));  // open: preset, reset
  and and_1 (and_1_out, nand_1_out, not_1_out);
  not not_2 (PCH_Debug, PCH_Odd_qn);
  assign DBx = PCH_DB ? PCH_Debug : 1'bz;  // Controlled_Buffer controlled_buffer_3
  assign ADHx_Out = PCH_ADH ? PCH_Debug : 1'bz;  // Controlled_Buffer controlled_buffer_4

  // Notes on the sheet:
  //   posedge
endmodule

module PCL (
  input  PHI2,
  input  cin,
  input  ADL_PCL_9a95c372,
  input  PCL_PCL_4f350f4d,
  input  PCL_ADL_ee043dbc,
  input  PCL_DB_4172714e,
  input  ADL0_In,
  input  ADL1_In,
  input  ADL2_In,
  input  ADL3_In,
  input  ADL4_In,
  input  ADL5_In,
  input  ADL6_In,
  input  ADL7_In,
  output ADL0,
  output ADL1,
  output out_17,
  output ADL3,
  output out_19,
  output ADL5,
  output out_21,
  output ADL7,
  output DB0,
  output DB1,
  output DB2,
  output DB3,
  output DB4,
  output DB5,
  output DB6,
  output DB7,
  output PCLC,
  output [7:0] PCL_Debug,
  output [7:0] PCLS_Debug
);

  wire PCL0_cout, PCL0_sout, PCL1_cout, PCL1_sout, PCL2_cout, PCL2_sout, PCL3_cout, PCL3_sout, PCL4_cout,
       PCL4_sout, PCL5_cout, PCL5_sout, PCL6_cout, PCL6_sout, PCL7_sout;

  PCL_EVEN_BIT PCL0 (
    .DBx(DB0), .ADLx_Out(ADL0), .cout(PCL0_cout), .sout(PCL0_sout), .PCL_Debug(PCL_Debug[0]),
    .PCLS_Debug(PCLS_Debug[0]), .cin(cin), .ADL_PCL(ADL_PCL_9a95c372), .PCL_PCL(PCL_PCL_4f350f4d),
    .PCL_ADL(PCL_ADL_ee043dbc), .PCL_DB(PCL_DB_4172714e), .ADLx_In(ADL0_In), .PHI2(PHI2));
  PCL_ODD_BIT PCL1 (
    .ADLx_Out(ADL1), .cout(PCL1_cout), .sout(PCL1_sout), .PCL_Debug(PCL_Debug[1]),
    .PCLS_Debug(PCLS_Debug[1]), .DBx(DB1), .cin(PCL0_cout), .ADL_PCL(ADL_PCL_9a95c372),
    .PCL_PCL(PCL_PCL_4f350f4d), .PCL_ADL(PCL_ADL_ee043dbc), .PCL_DB(PCL_DB_4172714e), .ADLx_In(ADL1_In),
    .PHI2(PHI2));
  PCL_EVEN_BIT PCL2 (
    .DBx(DB2), .ADLx_Out(out_17), .cout(PCL2_cout), .sout(PCL2_sout), .PCL_Debug(PCL_Debug[2]),
    .PCLS_Debug(PCLS_Debug[2]), .cin(PCL1_cout), .ADL_PCL(ADL_PCL_9a95c372), .PCL_PCL(PCL_PCL_4f350f4d),
    .PCL_ADL(PCL_ADL_ee043dbc), .PCL_DB(PCL_DB_4172714e), .ADLx_In(ADL2_In), .PHI2(PHI2));
  PCL_ODD_BIT PCL3 (
    .ADLx_Out(ADL3), .cout(PCL3_cout), .sout(PCL3_sout), .PCL_Debug(PCL_Debug[3]),
    .PCLS_Debug(PCLS_Debug[3]), .DBx(DB3), .cin(PCL2_cout), .ADL_PCL(ADL_PCL_9a95c372),
    .PCL_PCL(PCL_PCL_4f350f4d), .PCL_ADL(PCL_ADL_ee043dbc), .PCL_DB(PCL_DB_4172714e), .ADLx_In(ADL3_In),
    .PHI2(PHI2));
  PCL_EVEN_BIT PCL4 (
    .DBx(DB4), .ADLx_Out(out_19), .cout(PCL4_cout), .sout(PCL4_sout), .PCL_Debug(PCL_Debug[4]),
    .PCLS_Debug(PCLS_Debug[4]), .cin(PCL3_cout), .ADL_PCL(ADL_PCL_9a95c372), .PCL_PCL(PCL_PCL_4f350f4d),
    .PCL_ADL(PCL_ADL_ee043dbc), .PCL_DB(PCL_DB_4172714e), .ADLx_In(ADL4_In), .PHI2(PHI2));
  PCL_ODD_BIT PCL5 (
    .ADLx_Out(ADL5), .cout(PCL5_cout), .sout(PCL5_sout), .PCL_Debug(PCL_Debug[5]),
    .PCLS_Debug(PCLS_Debug[5]), .DBx(DB5), .cin(PCL4_cout), .ADL_PCL(ADL_PCL_9a95c372),
    .PCL_PCL(PCL_PCL_4f350f4d), .PCL_ADL(PCL_ADL_ee043dbc), .PCL_DB(PCL_DB_4172714e), .ADLx_In(ADL5_In),
    .PHI2(PHI2));
  PCL_EVEN_BIT PCL6 (
    .DBx(DB6), .ADLx_Out(out_21), .cout(PCL6_cout), .sout(PCL6_sout), .PCL_Debug(PCL_Debug[6]),
    .PCLS_Debug(PCLS_Debug[6]), .cin(PCL5_cout), .ADL_PCL(ADL_PCL_9a95c372), .PCL_PCL(PCL_PCL_4f350f4d),
    .PCL_ADL(PCL_ADL_ee043dbc), .PCL_DB(PCL_DB_4172714e), .ADLx_In(ADL6_In), .PHI2(PHI2));
  PCL_ODD_BIT PCL7 (
    .ADLx_Out(ADL7), .sout(PCL7_sout), .PCL_Debug(PCL_Debug[7]), .PCLS_Debug(PCLS_Debug[7]), .DBx(DB7),
    .cin(PCL6_cout), .ADL_PCL(ADL_PCL_9a95c372), .PCL_PCL(PCL_PCL_4f350f4d), .PCL_ADL(PCL_ADL_ee043dbc),
    .PCL_DB(PCL_DB_4172714e), .ADLx_In(ADL7_In), .PHI2(PHI2));  // open: cout
  or or_1 (PCLC, PCL0_sout, PCL1_sout, PCL2_sout, PCL3_sout, PCL4_sout, PCL5_sout, PCL6_sout, PCL7_sout);
endmodule

module PCH (
  input  PHI2,
  input  cin,
  input  ADH_PCH,
  input  PCH_PCH,
  input  PCH_ADH,
  input  PCH_DB,
  input  in_7,
  input  ADH1,
  input  ADH2,
  input  ADH3,
  input  ADH4,
  input  ADH5,
  input  in_13,
  input  in_14,
  output ADH0,
  output out_16,
  output out_17,
  output out_18,
  output out_19,
  output out_20,
  output ADH6,
  output ADH7,
  output DB0,
  output DB1,
  output DB2,
  output DB3,
  output DB4,
  output DB5,
  output DB6,
  output DB7,
  output [7:0] PCH_Debug,
  output [7:0] PCHS_Debug
);

  wire not_1_out, or_1_out, PCH0_cout, PCH0_sout, PCH1_cout, PCH1_sout, PCH2_cout, PCH2_sout, PCH3_sout,
       PCH4_cout, PCH5_cout, PCH6_cout;

  not not_1 (not_1_out, cin);
  PCH_EVEN_BIT PCH0 (
    .ADHx_Out(ADH0), .cout(PCH0_cout), .sout(PCH0_sout), .PCH_Debug(PCH_Debug[0]),
    .PCHS_Debug(PCHS_Debug[0]), .DBx(DB0), .cin(cin), .ADH_PCH(ADH_PCH), .PCH_PCH(PCH_PCH),
    .PCH_ADH(PCH_ADH), .PCH_DB(PCH_DB), .ADHx_In(in_7), .PHI2(PHI2));
  PCH_ODD_BIT PCH1 (
    .DBx(DB1), .ADHx_Out(out_16), .cout(PCH1_cout), .sout(PCH1_sout), .PCH_Debug(PCH_Debug[1]),
    .PCHS_Debug(PCHS_Debug[1]), .cin(PCH0_cout), .ADH_PCH(ADH_PCH), .PCH_PCH(PCH_PCH), .PCH_ADH(PCH_ADH),
    .PCH_DB(PCH_DB), .ADHx_In(ADH1), .PHI2(PHI2));
  PCH_EVEN_BIT PCH2 (
    .ADHx_Out(out_17), .cout(PCH2_cout), .sout(PCH2_sout), .PCH_Debug(PCH_Debug[2]),
    .PCHS_Debug(PCHS_Debug[2]), .DBx(DB2), .cin(PCH1_cout), .ADH_PCH(ADH_PCH), .PCH_PCH(PCH_PCH),
    .PCH_ADH(PCH_ADH), .PCH_DB(PCH_DB), .ADHx_In(ADH2), .PHI2(PHI2));
  PCH_ODD_BIT PCH3 (
    .DBx(DB3), .ADHx_Out(out_18), .sout(PCH3_sout), .PCH_Debug(PCH_Debug[3]), .PCHS_Debug(PCHS_Debug[3]),
    .cin(PCH2_cout), .ADH_PCH(ADH_PCH), .PCH_PCH(PCH_PCH), .PCH_ADH(PCH_ADH), .PCH_DB(PCH_DB),
    .ADHx_In(ADH3), .PHI2(PHI2));  // open: cout
  PCH_ODD_BIT PCH4 (
    .DBx(DB4), .ADHx_Out(out_19), .cout(PCH4_cout), .PCH_Debug(PCH_Debug[4]), .PCHS_Debug(PCHS_Debug[4]),
    .cin(or_1_out), .ADH_PCH(ADH_PCH), .PCH_PCH(PCH_PCH), .PCH_ADH(PCH_ADH), .PCH_DB(PCH_DB), .ADHx_In(ADH4),
    .PHI2(PHI2));  // open: sout
  PCH_EVEN_BIT PCH5 (
    .ADHx_Out(out_20), .cout(PCH5_cout), .PCH_Debug(PCH_Debug[5]), .PCHS_Debug(PCHS_Debug[5]), .DBx(DB5),
    .cin(PCH4_cout), .ADH_PCH(ADH_PCH), .PCH_PCH(PCH_PCH), .PCH_ADH(PCH_ADH), .PCH_DB(PCH_DB),
    .ADHx_In(ADH5), .PHI2(PHI2));  // open: sout
  PCH_ODD_BIT PCH6 (
    .DBx(DB6), .ADHx_Out(ADH6), .cout(PCH6_cout), .PCH_Debug(PCH_Debug[6]), .PCHS_Debug(PCHS_Debug[6]),
    .cin(PCH5_cout), .ADH_PCH(ADH_PCH), .PCH_PCH(PCH_PCH), .PCH_ADH(PCH_ADH), .PCH_DB(PCH_DB),
    .ADHx_In(in_13), .PHI2(PHI2));  // open: sout
  PCH_EVEN_BIT PCH7 (
    .ADHx_Out(ADH7), .PCH_Debug(PCH_Debug[7]), .PCHS_Debug(PCHS_Debug[7]), .DBx(DB7), .cin(PCH6_cout),
    .ADH_PCH(ADH_PCH), .PCH_PCH(PCH_PCH), .PCH_ADH(PCH_ADH), .PCH_DB(PCH_DB), .ADHx_In(in_14), .PHI2(PHI2));  // open: cout, sout
  or or_1 (or_1_out, not_1_out, PCH0_sout, PCH1_sout, PCH2_sout, PCH3_sout);

  // Other names for the same wires on the sheet: ADH_PCH_61520abf = ADH_PCH; PCH_ADH_ead93594 = PCH_ADH;
  //   PCH_DB_a81fefa0 = PCH_DB; PCH_PCH_807b9fbd = PCH_PCH

  // Notes on the sheet:
  //   PCHC
endmodule

module ALU_OPS (
  input  NDB_ADD_ee0a1870,
  input  DB_ADD_48d85b7e,
  input  L_0_ADD_81d17e61,
  input  SB_ADD_0eab26ac,
  input  ADL_ADD_e28b8a30,
  input  ANDS,
  input  EORS,
  input  ORS,
  input  SRS,
  input  SUMS,
  input  L_cin_af3836dd,
  input  DC3,
  input  SB0,
  input  SB1,
  input  SB2,
  input  SB3,
  input  SB4,
  input  SB5,
  input  SB6,
  input  SB7,
  input  DB0,
  input  DB1,
  input  DB2,
  input  DB3,
  input  DB4,
  input  DB5,
  input  DB6,
  input  DB7,
  input  ADL0,
  input  ADL1,
  input  ADL2,
  input  ADL3,
  input  ADL4,
  input  ADL5,
  input  ADL6,
  input  ADL7,
  output L_carry3_9e435978,
  output carry4,
  output carry6,
  output L_carry7_b3181e70,
  output res0,
  output res1,
  output res2,
  output res3,
  output res4,
  output res5,
  output res6,
  output res7,
  output nor0,
  output nor1,
  output nor2,
  output nor3,
  output nor4,
  output nor5,
  output nor6,
  output nor7,
  output nand0,
  output nand1,
  output nand2,
  output nand3,
  output nand4,
  output nand5,
  output nand6,
  output nand7,
  output xor0,
  output xor1,
  output xor2,
  output xor3,
  output xor4,
  output xor5,
  output xor6,
  output xor7,
  output [7:0] AI_Debug,
  output [7:0] BI_Debug
);

  wire _0_cout, _1_l_cout_4dd9971a, _2_cout, _5_l_cout_4dd9971a, and_1_out, not_1_out;

  ALU_EVEN_BIT _0 (
    .AI_Debug(AI_Debug[0]), .BI_Debug(BI_Debug[0]), .L_res_da3ec8b2(res0), .cout(_0_cout), .\nor (nor0),
    .\nand (nand0), .\xor (xor0), .L_0_ADD_81d17e61(L_0_ADD_81d17e61), .SB_ADD_0eab26ac(SB_ADD_0eab26ac),
    .ADL_ADD_e28b8a30(ADL_ADD_e28b8a30), .ANDS(ANDS), .EORS(EORS), .ORS(ORS), .SRS(SRS), .SUMS(SUMS),
    .L_cin_af3836dd(L_cin_af3836dd), .prev_res(nand1), .SBx(SB0), .NDB_ADD_ee0a1870(NDB_ADD_ee0a1870),
    .DBx(DB0), .ADLx(ADL0), .DB_ADD_48d85b7e(DB_ADD_48d85b7e));
  ALU_ODD_BIT _1 (
    .AI_Debug(AI_Debug[1]), .BI_Debug(BI_Debug[1]), .L_res_da3ec8b2(res1),
    .L_cout_4dd9971a(_1_l_cout_4dd9971a), .\nor (nor1), .\nand (nand1), .\xor (xor1),
    .L_0_ADD_81d17e61(L_0_ADD_81d17e61), .SB_ADD_0eab26ac(SB_ADD_0eab26ac),
    .ADL_ADD_e28b8a30(ADL_ADD_e28b8a30), .ANDS(ANDS), .EORS(EORS), .ORS(ORS), .SRS(SRS), .SUMS(SUMS),
    .cin(_0_cout), .prev_res(nand2), .SBx(SB1), .NDB_ADD_ee0a1870(NDB_ADD_ee0a1870), .DBx(DB1), .ADLx(ADL1),
    .DB_ADD_48d85b7e(DB_ADD_48d85b7e));
  ALU_EVEN_BIT _2 (
    .AI_Debug(AI_Debug[2]), .BI_Debug(BI_Debug[2]), .L_res_da3ec8b2(res2), .cout(_2_cout), .\nor (nor2),
    .\nand (nand2), .\xor (xor2), .L_0_ADD_81d17e61(L_0_ADD_81d17e61), .SB_ADD_0eab26ac(SB_ADD_0eab26ac),
    .ADL_ADD_e28b8a30(ADL_ADD_e28b8a30), .ANDS(ANDS), .EORS(EORS), .ORS(ORS), .SRS(SRS), .SUMS(SUMS),
    .L_cin_af3836dd(_1_l_cout_4dd9971a), .prev_res(nand3), .SBx(SB2), .NDB_ADD_ee0a1870(NDB_ADD_ee0a1870),
    .DBx(DB2), .ADLx(ADL2), .DB_ADD_48d85b7e(DB_ADD_48d85b7e));
  ALU_ODD_BIT _3 (
    .AI_Debug(AI_Debug[3]), .BI_Debug(BI_Debug[3]), .L_res_da3ec8b2(res3),
    .L_cout_4dd9971a(L_carry3_9e435978), .\nor (nor3), .\nand (nand3), .\xor (xor3),
    .L_0_ADD_81d17e61(L_0_ADD_81d17e61), .SB_ADD_0eab26ac(SB_ADD_0eab26ac),
    .ADL_ADD_e28b8a30(ADL_ADD_e28b8a30), .ANDS(ANDS), .EORS(EORS), .ORS(ORS), .SRS(SRS), .SUMS(SUMS),
    .cin(_2_cout), .prev_res(nand4), .SBx(SB3), .NDB_ADD_ee0a1870(NDB_ADD_ee0a1870), .DBx(DB3), .ADLx(ADL3),
    .DB_ADD_48d85b7e(DB_ADD_48d85b7e));
  not not_1 (not_1_out, DC3);
  and and_1 (and_1_out, L_carry3_9e435978, not_1_out);
  ALU_EVEN_BIT _4 (
    .AI_Debug(AI_Debug[4]), .BI_Debug(BI_Debug[4]), .L_res_da3ec8b2(res4), .cout(carry4), .\nor (nor4),
    .\nand (nand4), .\xor (xor4), .L_0_ADD_81d17e61(L_0_ADD_81d17e61), .SB_ADD_0eab26ac(SB_ADD_0eab26ac),
    .ADL_ADD_e28b8a30(ADL_ADD_e28b8a30), .ANDS(ANDS), .EORS(EORS), .ORS(ORS), .SRS(SRS), .SUMS(SUMS),
    .L_cin_af3836dd(and_1_out), .prev_res(nand5), .SBx(SB4), .NDB_ADD_ee0a1870(NDB_ADD_ee0a1870), .DBx(DB4),
    .ADLx(ADL4), .DB_ADD_48d85b7e(DB_ADD_48d85b7e));
  ALU_ODD_BIT _5 (
    .AI_Debug(AI_Debug[5]), .BI_Debug(BI_Debug[5]), .L_res_da3ec8b2(res5),
    .L_cout_4dd9971a(_5_l_cout_4dd9971a), .\nor (nor5), .\nand (nand5), .\xor (xor5),
    .L_0_ADD_81d17e61(L_0_ADD_81d17e61), .SB_ADD_0eab26ac(SB_ADD_0eab26ac),
    .ADL_ADD_e28b8a30(ADL_ADD_e28b8a30), .ANDS(ANDS), .EORS(EORS), .ORS(ORS), .SRS(SRS), .SUMS(SUMS),
    .cin(carry4), .prev_res(nand6), .SBx(SB5), .NDB_ADD_ee0a1870(NDB_ADD_ee0a1870), .DBx(DB5), .ADLx(ADL5),
    .DB_ADD_48d85b7e(DB_ADD_48d85b7e));
  ALU_EVEN_BIT _6 (
    .AI_Debug(AI_Debug[6]), .BI_Debug(BI_Debug[6]), .L_res_da3ec8b2(res6), .cout(carry6), .\nor (nor6),
    .\nand (nand6), .\xor (xor6), .L_0_ADD_81d17e61(L_0_ADD_81d17e61), .SB_ADD_0eab26ac(SB_ADD_0eab26ac),
    .ADL_ADD_e28b8a30(ADL_ADD_e28b8a30), .ANDS(ANDS), .EORS(EORS), .ORS(ORS), .SRS(SRS), .SUMS(SUMS),
    .L_cin_af3836dd(_5_l_cout_4dd9971a), .prev_res(nand7), .SBx(SB6), .NDB_ADD_ee0a1870(NDB_ADD_ee0a1870),
    .DBx(DB6), .ADLx(ADL6), .DB_ADD_48d85b7e(DB_ADD_48d85b7e));
  ALU_ODD_BIT _7 (
    .AI_Debug(AI_Debug[7]), .BI_Debug(BI_Debug[7]), .L_res_da3ec8b2(res7),
    .L_cout_4dd9971a(L_carry7_b3181e70), .\nor (nor7), .\nand (nand7), .\xor (xor7),
    .L_0_ADD_81d17e61(L_0_ADD_81d17e61), .SB_ADD_0eab26ac(SB_ADD_0eab26ac),
    .ADL_ADD_e28b8a30(ADL_ADD_e28b8a30), .ANDS(ANDS), .EORS(EORS), .ORS(ORS), .SRS(SRS), .SUMS(SUMS),
    .cin(carry6), .prev_res(1'b1), .SBx(SB7), .NDB_ADD_ee0a1870(NDB_ADD_ee0a1870), .DBx(DB7), .ADLx(ADL7),
    .DB_ADD_48d85b7e(DB_ADD_48d85b7e));
endmodule

module ALU_EVEN_BIT (
  input  NDB_ADD_ee0a1870,
  input  DB_ADD_48d85b7e,
  input  L_0_ADD_81d17e61,
  input  SB_ADD_0eab26ac,
  input  ADL_ADD_e28b8a30,
  input  ANDS,
  input  EORS,
  input  ORS,
  input  SRS,
  input  SUMS,
  input  L_cin_af3836dd,
  input  prev_res,
  input  SBx,
  input  DBx,
  input  ADLx,
  output L_res_da3ec8b2,
  output cout,
  output AI_Debug,
  output \nor ,
  output \nand ,
  output BI_Debug,
  output \xor 
);

  wire and_1_out, controlled_buffer_1_out, controlled_buffer_3_out, nand_2_out, nand_3_out, nand_4_out,
       nor_2_out, not_1_out, not_2_out, not_3_out, not_4_out, not_5_out;

  not not_1 (not_1_out, DBx);
  assign controlled_buffer_1_out = L_0_ADD_81d17e61 ? 1'b0 : 1'bz;  // Controlled_Buffer controlled_buffer_1
  assign controlled_buffer_1_out = SB_ADD_0eab26ac ? SBx : 1'bz;  // Controlled_Buffer controlled_buffer_2
  assign controlled_buffer_3_out = DB_ADD_48d85b7e ? DBx : 1'bz;  // Controlled_Buffer controlled_buffer_3
  assign controlled_buffer_3_out = NDB_ADD_ee0a1870 ? not_1_out : 1'bz;  // Controlled_Buffer controlled_buffer_4
  assign controlled_buffer_3_out = ADL_ADD_e28b8a30 ? ADLx : 1'bz;  // Controlled_Buffer controlled_buffer_5
  D_Latch AI (.Q(AI_Debug), .D(controlled_buffer_1_out), .EN(1'b1));  // open: NOT_Q
  D_Latch BI (.Q(BI_Debug), .D(controlled_buffer_3_out), .EN(1'b1));  // open: NOT_Q
  not not_2 (not_2_out, \nor );
  not not_3 (not_3_out, L_cin_af3836dd);
  nand nand_1 (\nand , AI_Debug, BI_Debug);
  nor nor_1 (\nor , AI_Debug, BI_Debug);
  nand nand_2 (nand_2_out, not_2_out, \nand );
  nand nand_3 (nand_3_out, not_3_out, nand_2_out);
  not not_4 (not_4_out, nor_2_out);
  nor nor_2 (nor_2_out, not_3_out, nand_2_out);
  nand nand_4 (nand_4_out, L_cin_af3836dd, \nand );
  not not_5 (not_5_out, \nor );
  and and_1 (and_1_out, nand_3_out, not_4_out);
  and and_2 (cout, nand_4_out, not_5_out);
  assign L_res_da3ec8b2 = ANDS ? \nand  : 1'bz;  // Controlled_Buffer controlled_buffer_6
  assign L_res_da3ec8b2 = ORS ? \nor  : 1'bz;  // Controlled_Buffer controlled_buffer_7
  assign L_res_da3ec8b2 = EORS ? nand_2_out : 1'bz;  // Controlled_Buffer controlled_buffer_8
  assign L_res_da3ec8b2 = SRS ? prev_res : 1'bz;  // Controlled_Buffer controlled_buffer_9
  assign L_res_da3ec8b2 = SUMS ? and_1_out : 1'bz;  // Controlled_Buffer controlled_buffer_10
  not not_6 (\xor , nand_2_out);

  // Notes on the sheet:
  //   xnor
  //   xor
endmodule

module ALU_ODD_BIT (
  input  NDB_ADD_ee0a1870,
  input  DB_ADD_48d85b7e,
  input  L_0_ADD_81d17e61,
  input  SB_ADD_0eab26ac,
  input  ADL_ADD_e28b8a30,
  input  ANDS,
  input  EORS,
  input  ORS,
  input  SRS,
  input  SUMS,
  input  cin,
  input  prev_res,
  input  SBx,
  input  DBx,
  input  ADLx,
  output L_res_da3ec8b2,
  output L_cout_4dd9971a,
  output AI_Debug,
  output \nor ,
  output \nand ,
  output BI_Debug,
  output \xor 
);

  wire and_1_out, controlled_buffer_1_out, controlled_buffer_3_out, nand_2_out, nand_3_out, nor_3_out,
       not_1_out, not_2_out, not_3_out, not_4_out, not_5_out, not_6_out;

  not not_1 (not_1_out, DBx);
  assign controlled_buffer_1_out = L_0_ADD_81d17e61 ? 1'b0 : 1'bz;  // Controlled_Buffer controlled_buffer_1
  assign controlled_buffer_1_out = SB_ADD_0eab26ac ? SBx : 1'bz;  // Controlled_Buffer controlled_buffer_2
  assign controlled_buffer_3_out = DB_ADD_48d85b7e ? DBx : 1'bz;  // Controlled_Buffer controlled_buffer_3
  assign controlled_buffer_3_out = NDB_ADD_ee0a1870 ? not_1_out : 1'bz;  // Controlled_Buffer controlled_buffer_4
  assign controlled_buffer_3_out = ADL_ADD_e28b8a30 ? ADLx : 1'bz;  // Controlled_Buffer controlled_buffer_5
  D_Latch AI (.Q(AI_Debug), .D(controlled_buffer_1_out), .EN(1'b1));  // open: NOT_Q
  D_Latch BI (.Q(BI_Debug), .D(controlled_buffer_3_out), .EN(1'b1));  // open: NOT_Q
  not not_2 (not_2_out, \nand );
  not not_3 (not_3_out, cin);
  not not_4 (not_4_out, \nor );
  nand nand_1 (\nand , AI_Debug, BI_Debug);
  nor nor_1 (\nor , AI_Debug, BI_Debug);
  nor nor_2 (\xor , not_2_out, \nor );
  nand nand_2 (nand_2_out, not_3_out, \xor );
  not not_5 (not_5_out, nor_3_out);
  nor nor_3 (nor_3_out, not_3_out, \xor );
  nand nand_3 (nand_3_out, cin, not_4_out);
  not not_6 (not_6_out, not_2_out);
  and and_1 (and_1_out, nand_2_out, not_5_out);
  and and_2 (L_cout_4dd9971a, nand_3_out, not_6_out);
  assign L_res_da3ec8b2 = ANDS ? \nand  : 1'bz;  // Controlled_Buffer controlled_buffer_6
  assign L_res_da3ec8b2 = ORS ? \nor  : 1'bz;  // Controlled_Buffer controlled_buffer_7
  assign L_res_da3ec8b2 = EORS ? \xor  : 1'bz;  // Controlled_Buffer controlled_buffer_8
  assign L_res_da3ec8b2 = SRS ? prev_res : 1'bz;  // Controlled_Buffer controlled_buffer_9
  assign L_res_da3ec8b2 = SUMS ? and_1_out : 1'bz;  // Controlled_Buffer controlled_buffer_10

  // Notes on the sheet:
  //   xor
  //   xor
endmodule

module BCD_CARRY (
  input  n_ACIN,
  input  carry4,
  input  n_DAA,
  input  [7:0] \nor ,
  input  [7:0] \nand ,
  input  [7:0] \xor ,
  output DC3,
  output DC7
);

  wire and_1_out, nand_1_out, nand_2_out, nand_3_out, nor_1_out, nor_2_out, nor_3_out, nor_4_out, nor_5_out,
       nor_6_out, nor_7_out, nor_8_out, nor_9_out, not_1_out, not_2_out, not_3_out, not_4_out, not_5_out,
       not_6_out, not_7_out, not_8_out, not_9_out, or_1_out, or_2_out;

  nand nand_1 (nand_1_out, n_ACIN, \nand [0]);
  not not_1 (not_1_out, \nor [0]);
  not not_2 (not_2_out, \nand [5]);
  not not_3 (not_3_out, \nand [2]);
  not not_4 (not_4_out, \nand [1]);
  and and_1 (and_1_out, nand_1_out, not_1_out);
  nor nor_1 (nor_1_out, not_3_out, \nor [2]);
  nor nor_2 (nor_2_out, and_1_out, nor_1_out, not_4_out, \xor [1]);
  not not_5 (not_5_out, \nand [1]);
  not not_6 (not_6_out, \nand [6]);
  nor nor_3 (nor_3_out, carry4, not_2_out, \xor [5], \xor [6]);
  nor nor_4 (nor_4_out, not_3_out, \xor [3]);
  nor nor_5 (nor_5_out, nor_4_out, nor_2_out);
  nor nor_6 (nor_6_out, \nor [2], nand_2_out);
  nand nand_2 (nand_2_out, not_5_out, and_1_out);
  nor nor_7 (nor_7_out, \xor [7], not_6_out);
  nor nor_8 (nor_8_out, nor_7_out, nor_3_out);
  not not_7 (not_7_out, \xor [6]);
  nor nor_9 (nor_9_out, not_7_out, nand_3_out);
  nand nand_3 (nand_3_out, not_2_out, carry4);
  or or_1 (or_1_out, nor_5_out, nor_6_out);
  or or_2 (or_2_out, nor_8_out, nor_9_out);
  and and_2 (DC3, or_1_out, not_8_out);
  not not_8 (not_8_out, n_DAA);
  and and_3 (DC7, or_2_out, not_9_out);
  not not_9 (not_9_out, n_DAA);

  // Notes on the sheet:
  //   c
  //   b
  //   ~(b | c)
  //   a
endmodule
module ALU_ADD (
  input  PHI2,
  input  ADD_SB06,
  input  ADD_SB7,
  input  ADD_ADL,
  input  [7:0] n_res,
  output [7:0] n_ADDx_Out,
  output SB0,
  output SB1,
  output SB2,
  output SB3,
  output SB4,
  output SB5,
  output SB6,
  output SB7,
  output ADL0,
  output ADL1,
  output ADL2,
  output ADL3,
  output ADL4,
  output ADL5,
  output ADL6,
  output ADL7,
  output [7:0] ADD_Debug
);

  D_Latch d_latch_1 (.Q(n_ADDx_Out[0]), .NOT_Q(ADD_Debug[0]), .D(n_res[0]), .EN(PHI2));
  D_Latch d_latch_2 (.Q(n_ADDx_Out[1]), .NOT_Q(ADD_Debug[1]), .D(n_res[1]), .EN(PHI2));
  D_Latch d_latch_3 (.Q(n_ADDx_Out[2]), .NOT_Q(ADD_Debug[2]), .D(n_res[2]), .EN(PHI2));
  D_Latch d_latch_4 (.Q(n_ADDx_Out[3]), .NOT_Q(ADD_Debug[3]), .D(n_res[3]), .EN(PHI2));
  D_Latch d_latch_5 (.Q(n_ADDx_Out[4]), .NOT_Q(ADD_Debug[4]), .D(n_res[4]), .EN(PHI2));
  D_Latch d_latch_6 (.Q(n_ADDx_Out[5]), .NOT_Q(ADD_Debug[5]), .D(n_res[5]), .EN(PHI2));
  D_Latch d_latch_7 (.Q(n_ADDx_Out[6]), .NOT_Q(ADD_Debug[6]), .D(n_res[6]), .EN(PHI2));
  D_Latch d_latch_8 (.Q(n_ADDx_Out[7]), .NOT_Q(ADD_Debug[7]), .D(n_res[7]), .EN(PHI2));
  assign SB0 = ADD_SB06 ? ADD_Debug[0] : 1'bz;  // Controlled_Buffer controlled_buffer_1
  assign SB1 = ADD_SB06 ? ADD_Debug[1] : 1'bz;  // Controlled_Buffer controlled_buffer_2
  assign SB2 = ADD_SB06 ? ADD_Debug[2] : 1'bz;  // Controlled_Buffer controlled_buffer_3
  assign SB3 = ADD_SB06 ? ADD_Debug[3] : 1'bz;  // Controlled_Buffer controlled_buffer_4
  assign SB4 = ADD_SB06 ? ADD_Debug[4] : 1'bz;  // Controlled_Buffer controlled_buffer_5
  assign SB5 = ADD_SB06 ? ADD_Debug[5] : 1'bz;  // Controlled_Buffer controlled_buffer_6
  assign SB6 = ADD_SB06 ? ADD_Debug[6] : 1'bz;  // Controlled_Buffer controlled_buffer_7
  assign SB7 = ADD_SB7 ? ADD_Debug[7] : 1'bz;  // Controlled_Buffer controlled_buffer_8
  assign ADL0 = ADD_ADL ? ADD_Debug[0] : 1'bz;  // Controlled_Buffer controlled_buffer_9
  assign ADL1 = ADD_ADL ? ADD_Debug[1] : 1'bz;  // Controlled_Buffer controlled_buffer_10
  assign ADL2 = ADD_ADL ? ADD_Debug[2] : 1'bz;  // Controlled_Buffer controlled_buffer_11
  assign ADL3 = ADD_ADL ? ADD_Debug[3] : 1'bz;  // Controlled_Buffer controlled_buffer_12
  assign ADL4 = ADD_ADL ? ADD_Debug[4] : 1'bz;  // Controlled_Buffer controlled_buffer_13
  assign ADL5 = ADD_ADL ? ADD_Debug[5] : 1'bz;  // Controlled_Buffer controlled_buffer_14
  assign ADL6 = ADD_ADL ? ADD_Debug[6] : 1'bz;  // Controlled_Buffer controlled_buffer_15
  assign ADL7 = ADD_ADL ? ADD_Debug[7] : 1'bz;  // Controlled_Buffer controlled_buffer_16
endmodule

module ALU_BCD (
  input  PHI2,
  input  n_carry3,
  input  ACR,
  input  n_DAA,
  input  n_DSA,
  input  SB0,
  input  SB1,
  input  SB2,
  input  SB3,
  input  SB4,
  input  SB5,
  input  SB6,
  input  SB7,
  input  [7:0] n_ADDx_In,
  output out0,
  output out1,
  output out2,
  output out3,
  output out4,
  output out5,
  output out6,
  output out7
);

  wire and_1_out, and_2_out, and_3_out, and_4_out, DAAH_Latch_not_q, DAAL_Latch_not_q, DSAH_Latch_not_q,
       DSAL_Latch_q, nand_1_out, nand_2_out, nand_3_out, nand_4_out, nand_5_out, nand_6_out, nand_7_out,
       nand_8_out, nand_9_out, nand_10_out, nand_11_out, nor_1_out, nor_2_out, nor_3_out, nor_4_out,
       nor_5_out, nor_6_out, nor_7_out, not_1_out, not_2_out, not_3_out, not_4_out, not_5_out, not_6_out,
       not_7_out, not_8_out, not_9_out, not_10_out, not_11_out, not_12_out;

  not not_1 (not_1_out, n_carry3);
  not not_2 (not_2_out, n_DAA);
  nor nor_1 (nor_1_out, n_ADDx_In[1], n_ADDx_In[2]);
  not not_3 (not_3_out, nor_1_out);
  nand nand_1 (nand_1_out, n_ADDx_In[1], n_ADDx_In[2]);
  nand nand_2 (nand_2_out, n_ADDx_In[5], n_ADDx_In[6]);
  nor nor_2 (nor_2_out, n_ADDx_In[5], n_ADDx_In[6]);
  D_Latch DAAL_Latch (.NOT_Q(DAAL_Latch_not_q), .D(nand_3_out), .EN(PHI2));  // open: Q
  nand nand_3 (nand_3_out, not_2_out, not_1_out);
  D_Latch DAAH_Latch (.NOT_Q(DAAH_Latch_not_q), .D(not_2_out), .EN(PHI2));  // open: Q
  D_Latch DSAL_Latch (.Q(DSAL_Latch_q), .D(nor_3_out), .EN(PHI2));  // open: NOT_Q
  nor nor_3 (nor_3_out, not_1_out, n_DSA);
  D_Latch DSAH_Latch (.NOT_Q(DSAH_Latch_not_q), .D(not_4_out), .EN(PHI2));  // open: Q
  not not_4 (not_4_out, n_DSA);
  nand nand_4 (nand_4_out, n_ADDx_In[1], DAAL_Latch_not_q);
  nand nand_5 (nand_5_out, ~n_ADDx_In[1], DSAL_Latch_q);  // NAND_Gate
  nand nand_6 (nand_6_out, not_3_out, DSAL_Latch_q);
  nand nand_7 (nand_7_out, nand_1_out, DAAL_Latch_not_q);
  nand nand_8 (nand_8_out, n_ADDx_In[5], nor_4_out);
  nand nand_9 (nand_9_out, ~n_ADDx_In[5], nor_5_out);  // NAND_Gate
  nand nand_10 (nand_10_out, nand_2_out, nor_4_out);
  not not_5 (not_5_out, nor_2_out);
  nand nand_11 (nand_11_out, not_5_out, nor_5_out);
  not not_6 (not_6_out, ACR);
  and and_1 (and_1_out, nand_4_out, nand_5_out);
  and and_2 (and_2_out, nand_6_out, nand_7_out);
  and and_3 (and_3_out, nand_8_out, nand_9_out);
  and and_4 (and_4_out, nand_10_out, nand_11_out);
  nor nor_4 (nor_4_out, not_6_out, DAAH_Latch_not_q);
  nor nor_5 (nor_5_out, ACR, DSAH_Latch_not_q);
  nor nor_6 (nor_6_out, DSAL_Latch_q, DAAL_Latch_not_q);
  not not_7 (not_7_out, SB1);
  not not_8 (not_8_out, SB2);
  not not_9 (not_9_out, SB3);
  nor nor_7 (nor_7_out, nor_4_out, nor_5_out);
  not not_10 (not_10_out, SB5);
  not not_11 (not_11_out, SB6);
  not not_12 (not_12_out, SB7);
  xor xor_1 (out1, nor_6_out, not_7_out);
  xor xor_2 (out2, and_1_out, not_8_out);
  xor xor_3 (out3, and_2_out, not_9_out);
  xor xor_4 (out5, nor_7_out, not_10_out);
  xor xor_5 (out6, and_3_out, not_11_out);
  xor xor_6 (out7, and_4_out, not_12_out);

  assign out0 = SB0;
  assign out4 = SB4;

  // Notes on the sheet:
  //   DAAL
  //   DAAL
  //   DAAH
  //   DSAL
  //   DSAH
  //   DSAL
  //   DAAH
  //   DSAH
endmodule

module ALU_AC (
  input  PHI2,
  input  SB_AC,
  input  AC_SB,
  input  AC_DB,
  input  SB_DB,
  input  SB_ADH,
  input  ZR_ADH0,
  input  ZR_ADH17,
  input  [7:0] BCD_in,
  input  SB0_In,
  input  SB1_In,
  input  SB2_In,
  input  SB3_In,
  input  SB4_In,
  input  SB5_In,
  input  SB6_In,
  input  SB7_In,
  output [7:0] AC_Debug,
  output SB0_Out,
  output SB1_Out,
  output SB2_Out,
  output SB3_Out,
  output SB4_Out,
  output SB5_Out,
  output SB6_Out,
  output SB7_Out,
  output DB0,
  output DB1,
  output DB2,
  output DB3,
  output DB4,
  output DB5,
  output DB6,
  output DB7,
  output ADH0,
  output ADH1,
  output ADH2,
  output ADH3,
  output ADH4,
  output ADH5,
  output ADH6,
  output ADH7
);

  wire and_1_out, and_2_out, and_3_out, and_4_out, and_5_out, and_6_out, and_7_out, and_8_out,
       controlled_buffer_1_out, controlled_buffer_2_out, controlled_buffer_3_out, controlled_buffer_4_out,
       controlled_buffer_5_out, controlled_buffer_6_out, controlled_buffer_7_out, controlled_buffer_8_out;

  assign controlled_buffer_1_out = SB_AC ? BCD_in[0] : 1'bz;  // Controlled_Buffer controlled_buffer_1
  assign controlled_buffer_2_out = SB_AC ? BCD_in[1] : 1'bz;  // Controlled_Buffer controlled_buffer_2
  assign controlled_buffer_3_out = SB_AC ? BCD_in[2] : 1'bz;  // Controlled_Buffer controlled_buffer_3
  assign controlled_buffer_4_out = SB_AC ? BCD_in[3] : 1'bz;  // Controlled_Buffer controlled_buffer_4
  assign controlled_buffer_5_out = SB_AC ? BCD_in[4] : 1'bz;  // Controlled_Buffer controlled_buffer_5
  assign controlled_buffer_6_out = SB_AC ? BCD_in[5] : 1'bz;  // Controlled_Buffer controlled_buffer_6
  assign controlled_buffer_7_out = SB_AC ? BCD_in[6] : 1'bz;  // Controlled_Buffer controlled_buffer_7
  assign controlled_buffer_8_out = SB_AC ? BCD_in[7] : 1'bz;  // Controlled_Buffer controlled_buffer_8
  D_Latch AC0 (.Q(AC_Debug[0]), .D(controlled_buffer_1_out), .EN(PHI2));  // open: NOT_Q
  D_Latch AC1 (.Q(AC_Debug[1]), .D(controlled_buffer_2_out), .EN(PHI2));  // open: NOT_Q
  D_Latch AC2 (.Q(AC_Debug[2]), .D(controlled_buffer_3_out), .EN(PHI2));  // open: NOT_Q
  D_Latch AC3 (.Q(AC_Debug[3]), .D(controlled_buffer_4_out), .EN(PHI2));  // open: NOT_Q
  D_Latch AC4 (.Q(AC_Debug[4]), .D(controlled_buffer_5_out), .EN(PHI2));  // open: NOT_Q
  D_Latch AC5 (.Q(AC_Debug[5]), .D(controlled_buffer_6_out), .EN(PHI2));  // open: NOT_Q
  D_Latch AC6 (.Q(AC_Debug[6]), .D(controlled_buffer_7_out), .EN(PHI2));  // open: NOT_Q
  D_Latch AC7 (.Q(AC_Debug[7]), .D(controlled_buffer_8_out), .EN(PHI2));  // open: NOT_Q
  assign DB0 = SB_DB ? SB0_In : 1'bz;  // Controlled_Buffer controlled_buffer_9
  assign DB1 = SB_DB ? SB1_In : 1'bz;  // Controlled_Buffer controlled_buffer_10
  assign DB2 = SB_DB ? SB2_In : 1'bz;  // Controlled_Buffer controlled_buffer_11
  assign DB3 = SB_DB ? SB3_In : 1'bz;  // Controlled_Buffer controlled_buffer_12
  assign DB4 = SB_DB ? SB4_In : 1'bz;  // Controlled_Buffer controlled_buffer_13
  assign DB5 = SB_DB ? SB5_In : 1'bz;  // Controlled_Buffer controlled_buffer_14
  assign DB6 = SB_DB ? SB6_In : 1'bz;  // Controlled_Buffer controlled_buffer_15
  assign DB7 = SB_DB ? SB7_In : 1'bz;  // Controlled_Buffer controlled_buffer_16
  assign DB0 = AC_DB ? AC_Debug[0] : 1'bz;  // Controlled_Buffer controlled_buffer_17
  assign DB1 = AC_DB ? AC_Debug[1] : 1'bz;  // Controlled_Buffer controlled_buffer_18
  assign DB2 = AC_DB ? AC_Debug[2] : 1'bz;  // Controlled_Buffer controlled_buffer_19
  assign DB3 = AC_DB ? AC_Debug[3] : 1'bz;  // Controlled_Buffer controlled_buffer_20
  assign DB4 = AC_DB ? AC_Debug[4] : 1'bz;  // Controlled_Buffer controlled_buffer_21
  assign DB5 = AC_DB ? AC_Debug[5] : 1'bz;  // Controlled_Buffer controlled_buffer_22
  assign DB6 = AC_DB ? AC_Debug[6] : 1'bz;  // Controlled_Buffer controlled_buffer_23
  assign DB7 = AC_DB ? AC_Debug[7] : 1'bz;  // Controlled_Buffer controlled_buffer_24
  and and_1 (and_1_out, SB0_In, ~ZR_ADH0);  // AND_Gate
  and and_2 (and_2_out, SB1_In, ~ZR_ADH17);  // AND_Gate
  and and_3 (and_3_out, SB2_In, ~ZR_ADH17);  // AND_Gate
  and and_4 (and_4_out, SB3_In, ~ZR_ADH17);  // AND_Gate
  and and_5 (and_5_out, SB4_In, ~ZR_ADH17);  // AND_Gate
  and and_6 (and_6_out, SB5_In, ~ZR_ADH17);  // AND_Gate
  and and_7 (and_7_out, SB6_In, ~ZR_ADH17);  // AND_Gate
  and and_8 (and_8_out, SB7_In, ~ZR_ADH17);  // AND_Gate
  assign SB0_Out = AC_SB ? AC_Debug[0] : 1'bz;  // Controlled_Buffer controlled_buffer_25
  assign SB1_Out = AC_SB ? AC_Debug[1] : 1'bz;  // Controlled_Buffer controlled_buffer_26
  assign SB2_Out = AC_SB ? AC_Debug[2] : 1'bz;  // Controlled_Buffer controlled_buffer_27
  assign SB3_Out = AC_SB ? AC_Debug[3] : 1'bz;  // Controlled_Buffer controlled_buffer_28
  assign SB4_Out = AC_SB ? AC_Debug[4] : 1'bz;  // Controlled_Buffer controlled_buffer_29
  assign SB5_Out = AC_SB ? AC_Debug[5] : 1'bz;  // Controlled_Buffer controlled_buffer_30
  assign SB6_Out = AC_SB ? AC_Debug[6] : 1'bz;  // Controlled_Buffer controlled_buffer_31
  assign SB7_Out = AC_SB ? AC_Debug[7] : 1'bz;  // Controlled_Buffer controlled_buffer_32
  assign ADH0 = SB_ADH ? and_1_out : 1'bz;  // Controlled_Buffer controlled_buffer_33
  assign ADH1 = SB_ADH ? and_2_out : 1'bz;  // Controlled_Buffer controlled_buffer_34
  assign ADH2 = SB_ADH ? and_3_out : 1'bz;  // Controlled_Buffer controlled_buffer_35
  assign ADH3 = SB_ADH ? and_4_out : 1'bz;  // Controlled_Buffer controlled_buffer_36
  assign ADH4 = SB_ADH ? and_5_out : 1'bz;  // Controlled_Buffer controlled_buffer_37
  assign ADH5 = SB_ADH ? and_6_out : 1'bz;  // Controlled_Buffer controlled_buffer_38
  assign ADH6 = SB_ADH ? and_7_out : 1'bz;  // Controlled_Buffer controlled_buffer_39
  assign ADH7 = SB_ADH ? and_8_out : 1'bz;  // Controlled_Buffer controlled_buffer_40
endmodule
