// Logisim project APUPlayer.circ as structural Verilog: 7 circuits, main circuit APUPlayer
module APUPlayer (
  input  nRES
);

  wire apu_p2, apu_p3, apu_p8, apu_p12, apu_p13, apu_p14, apu_p15, apu_p16, apu_p29, apu_p30, apu_p31,
       apu_p32, apu_p34, apu_p35, apu_p38, Next_RegOp_out, XTAL_out;
  wire [1:0] apu_p19, apu_p20;
  wire [3:0] apu_p28, transp_latch_q_2, transp_latch_q_3;
  wire [5:0] apu_p25, apu_p26, apu_p27;
  wire [7:0] apu_p9, apu_p10, apu_p17, apu_p21, apu_p22, apu_p36, apu_p37, apu_p39, transp_latch_q;
  wire [10:0] apu_p18, apu_p23, apu_p24;
  wire [14:0] apu_p40;
  wire [15:0] apu_p7, apu_p33;
  wire [23:0] dumper_addr;
  wire [31:0] core_out_15, dumper_data;

  Clock XTAL (.out(XTAL_out));
  LED DMC (.in(apu_p12));
  LED TRI (.in(apu_p13));
  LED SQB (.in(apu_p14));
  LED SQA (.in(apu_p15));
  LED RND (.in(apu_p16));
  LED led_1 (.in(apu_p18[0]));
  LED led_2 (.in(apu_p18[1]));
  LED led_3 (.in(apu_p18[2]));
  LED led_4 (.in(apu_p18[3]));
  LED led_5 (.in(apu_p18[4]));
  LED led_6 (.in(apu_p18[5]));
  LED led_7 (.in(apu_p18[6]));
  LED led_8 (.in(apu_p18[7]));
  LED led_9 (.in(apu_p18[8]));
  LED led_10 (.in(apu_p18[9]));
  LED led_11 (.in(apu_p18[10]));
  LED led_12 (.in(apu_p17[0]));
  LED led_13 (.in(apu_p17[1]));
  LED led_14 (.in(apu_p17[2]));
  LED led_15 (.in(apu_p17[3]));
  LED led_16 (.in(apu_p17[4]));
  LED led_17 (.in(apu_p17[5]));
  LED led_18 (.in(apu_p17[6]));
  LED TRI_RELOAD (.in(apu_p17[7]));
  // _2A03_APU apu: pin names not known; wires that end beside it: XTAL_out, apu_p2, apu_p3, nRES, 1'b1, 1'b1, apu_p7, apu_p8, apu_p9, apu_p10, 1'b0, apu_p12, apu_p13, apu_p14, apu_p15, apu_p16, apu_p17, apu_p18, apu_p19, apu_p20, apu_p21, apu_p22, apu_p23, apu_p24, apu_p25, apu_p26, apu_p27, apu_p28, apu_p29, apu_p30, apu_p31, apu_p32, apu_p33, apu_p34, apu_p35, apu_p36, apu_p37, apu_p38, apu_p39, apu_p40
  LED led_19 (.in(apu_p23[0]));
  LED led_20 (.in(apu_p23[1]));
  LED led_21 (.in(apu_p23[2]));
  LED led_22 (.in(apu_p23[3]));
  LED led_23 (.in(apu_p23[4]));
  LED led_24 (.in(apu_p23[5]));
  LED led_25 (.in(apu_p23[6]));
  LED led_26 (.in(apu_p23[7]));
  LED led_27 (.in(apu_p23[8]));
  LED led_28 (.in(apu_p23[9]));
  LED led_29 (.in(apu_p23[10]));
  LED SQA_ENV (.in(apu_p26[0]));
  LED led_30 (.in(apu_p26[1]));
  LED led_31 (.in(apu_p26[2]));
  LED led_32 (.in(apu_p26[3]));
  LED ENVDIS (.in(apu_p26[4]));
  LED HALT_SQA (.in(apu_p26[5]));
  LED SQA_DUTY (.in(apu_p19[0]));
  LED led_33 (.in(apu_p19[1]));
  LED led_34 (.in(apu_p21[0]));
  LED led_35 (.in(apu_p21[1]));
  LED led_36 (.in(apu_p21[2]));
  LED led_37 (.in(apu_p21[3]));
  LED led_38 (.in(apu_p21[4]));
  LED led_39 (.in(apu_p21[5]));
  LED led_40 (.in(apu_p21[6]));
  LED led_41 (.in(apu_p21[7]));
  LED led_42 (.in(apu_p24[0]));
  LED led_43 (.in(apu_p24[1]));
  LED led_44 (.in(apu_p24[2]));
  LED led_45 (.in(apu_p24[3]));
  LED led_46 (.in(apu_p24[4]));
  LED led_47 (.in(apu_p24[5]));
  LED led_48 (.in(apu_p24[6]));
  LED led_49 (.in(apu_p24[7]));
  LED led_50 (.in(apu_p24[8]));
  LED led_51 (.in(apu_p24[9]));
  LED led_52 (.in(apu_p24[10]));
  LED SQB_ENV (.in(apu_p25[0]));
  LED led_53 (.in(apu_p25[1]));
  LED led_54 (.in(apu_p25[2]));
  LED led_55 (.in(apu_p25[3]));
  LED ENVDIS_2 (.in(apu_p25[4]));
  LED HALT_SQB (.in(apu_p25[5]));
  WRAM wram (.M2(apu_p30), .Addr(apu_p33), .DB_in(apu_p37), .R_W(apu_p34), .nRES(nRES), .DB_out(apu_p10));
  Fake6502 core (
    .PHI0(apu_p31), .RDY(apu_p38), .SO(1'b1), .nNMI(apu_p32), .nIRQ(apu_p35), .nRES(nRES), .DB_in(apu_p36),
    .PHI1(apu_p2), .PHI2(apu_p3), .R_W(apu_p8), .Addr(apu_p7), .DB_out(apu_p9), .out_15(core_out_15),
    .in_8(Next_RegOp_out));  // open: SYNC
  Button Next_RegOp (.out(Next_RegOp_out));
  LED SQB_DUTY (.in(apu_p20[0]));
  LED led_56 (.in(apu_p20[1]));
  LED led_57 (.in(apu_p22[0]));
  LED led_58 (.in(apu_p22[1]));
  LED led_59 (.in(apu_p22[2]));
  LED led_60 (.in(apu_p22[3]));
  LED led_61 (.in(apu_p22[4]));
  LED led_62 (.in(apu_p22[5]));
  LED led_63 (.in(apu_p22[6]));
  LED led_64 (.in(apu_p22[7]));
  // Probe on core_out_15
  LED RMODE (.in(apu_p29));
  LED NFREQ (.in(apu_p28[0]));
  LED led_65 (.in(apu_p28[1]));
  LED led_66 (.in(apu_p28[2]));
  LED led_67 (.in(apu_p28[3]));
  LED N_ENV (.in(apu_p27[0]));
  LED led_68 (.in(apu_p27[1]));
  LED led_69 (.in(apu_p27[2]));
  LED led_70 (.in(apu_p27[3]));
  LED ENVDIS_3 (.in(apu_p27[4]));
  LED HALT_NOISE (.in(apu_p27[5]));
  AUXDumper dumper (.PHI1(apu_p2), .AUX({1'b0, apu_p40, apu_p39}), .Addr(dumper_addr), .Data(dumper_data));
  Hex_Digit_Display hex_digit_display_1 (.value(transp_latch_q_3));  // open: dp
  Register #(.width(16), .trigger("high")) transp_latch (
    .D(apu_p7), .en(apu_p7[14]), .Q({transp_latch_q_3, transp_latch_q_2, transp_latch_q}), .clk(apu_p3));  // open: clr
  Hex_Digit_Display hex_digit_display_2 (.value(transp_latch_q_2));  // open: dp
  Hex_Digit_Display hex_digit_display_3 (.value(transp_latch_q[7:4]));  // open: dp
  Hex_Digit_Display hex_digit_display_4 (.value(transp_latch_q[3:0]));  // open: dp
  RAM #(.addrWidth(24), .dataWidth(32), .bus("asynch")) ram_1 (
    .addr(dumper_addr), .data(dumper_data), .sel(1'b1), .ld(1'b0), .clr(1'b0));

  // Notes on the sheet:
  //   TRI_F
  //   TRI_LIN
  //   SQA_F
  //   SW_A
  //   N.C.
  //   SQB_F
  //   SW_B
  //   Load regdump here
  //   Last APU Register
  //   Taram-param-pam. Pam! Peep, peep, peep. Pipipipip, pip, pibibip
endmodule

module AUXDumper (
  input  PHI1,
  input  [23:0] AUX,
  output [23:0] Addr,
  output [31:0] Data
);

  wire adder_1_p3, counter_2_q, counter_3_q;
  wire [31:0] aux_a_1_a, aux_b_1_a;

  AUX_A aux_a_1 (.d(AUX[7:0]), .a(aux_a_1_a));
  AUX_B aux_b_1 (.d(AUX[23:8]), .a(aux_b_1_a));
  Counter #(.width(23), .max('h7fffff)) counter_1 (.Q(Addr[23:1]), .clk(PHI1));  // open: load, D, count, carry, clr
  Counter #(.width(1), .max('h1)) counter_2 (.Q(counter_2_q), .clk(PHI1));  // open: load, D, count, carry, clr
  Counter #(.width(1), .max('h1), .trigger("falling")) counter_3 (
    .Q(counter_3_q), .clk(PHI1));  // open: load, D, count, carry, clr
  // Adder adder_1: pin names not known; wires that end beside it: aux_a_1_a, aux_b_1_a, adder_1_p3
  // Divider divider_1: pin names not known; wires that end beside it: adder_1_p3, 32'h40000000, Data
  xnor xnor_1 (Addr[0], counter_2_q, counter_3_q);

  // Notes on the sheet:
  //   a + b
  //   The invention of the org to make the ADDR tick EVERY half cycle.
  //    : 2
  //   normalized samples in range [0.0f; 1.0f]
endmodule

module AUX_A (
  input  [7:0] d,
  output [31:0] a
);

  ROM #(.dataWidth(32)) rom_1 (.addr(d), .data(a), .sel(1'b1));

  // Notes on the sheet:
  //   0...255
  //   contents of rom_1 (hex, n*v repeats v):
  //   3ab77b8e 3d12a8ec 3d924925 3ddadec7 3e118b0c 3e3577e6 3e59364e 3e7cc69c 3e901495 3ea1af28 3eb33333
  //   3ec4a0e1 3ed5f85c 3ee739ce 3ef86563 3f04bda1 3d12a8ec 3d924925 3ddadec7 3e118b0c 3e3577e6 3e59364e
  //   3e7cc69c 3e901495 3ea1af28 3eb33333 3ec4a0e1 3ed5f85c 3ee739ce 3ef86563 3f04bda1 3f0d3dcb 3d924925
  //   3ddadec7 3e118b0c 3e3577e6 3e59364e 3e7cc69c 3e901495 3ea1af28 3eb33333 3ec4a0e1 3ed5f85c 3ee739ce
  //   3ef86563 3f04bda1 3f0d3dcb 3f15b343 3ddadec7 3e118b0c 3e3577e6 3e59364e 3e7cc69c 3e901495 3ea1af28
  //   3eb33333 3ec4a0e1 3ed5f85c 3ee739ce 3ef86563 3f04bda1 3f0d3dcb 3f15b343 3f1e1e1e 3e118b0c 3e3577e6
  //   3e59364e 3e7cc69c 3e901495 3ea1af28 3eb33333 3ec4a0e1 3ed5f85c 3ee739ce 3ef86563 3f04bda1 3f0d3dcb
  //   3f15b343 3f1e1e1e 3f267e6f 3e3577e6 3e59364e 3e7cc69c 3e901495 3ea1af28 3eb33333 3ec4a0e1 3ed5f85c
  //   3ee739ce 3ef86563 3f04bda1 3f0d3dcb 3f15b343 3f1e1e1e 3f267e6f 3f2ed44b 3e59364e 3e7cc69c 3e901495
  //   3ea1af28 3eb33333 3ec4a0e1 3ed5f85c 3ee739ce 3ef86563 3f04bda1 3f0d3dcb 3f15b343 3f1e1e1e 3f267e6f
  //   3f2ed44b 3f371fc4 3e7cc69c 3e901495 3ea1af28 3eb33333 3ec4a0e1 3ed5f85c 3ee739ce 3ef86563 3f04bda1
  //   3f0d3dcb 3f15b343 3f1e1e1e 3f267e6f 3f2ed44b 3f371fc4 3f3f60ef 3e901495 3ea1af28 3eb33333 3ec4a0e1
  //   3ed5f85c 3ee739ce 3ef86563 3f04bda1 3f0d3dcb 3f15b343 3f1e1e1e 3f267e6f 3f2ed44b 3f371fc4 3f3f60ef
  //   3f4797dd 3ea1af28 3eb33333 3ec4a0e1 3ed5f85c 3ee739ce 3ef86563 3f04bda1 3f0d3dcb 3f15b343 3f1e1e1e
  //   3f267e6f 3f2ed44b 3f371fc4 3f3f60ef 3f4797dd 3f4fc4a3 3eb33333 3ec4a0e1 3ed5f85c 3ee739ce 3ef86563
  //   3f04bda1 3f0d3dcb 3f15b343 3f1e1e1e 3f267e6f 3f2ed44b 3f371fc4 3f3f60ef 3f4797dd 3f4fc4a3 3f57e753
  //   3ec4a0e1 3ed5f85c 3ee739ce 3ef86563 3f04bda1 3f0d3dcb 3f15b343 3f1e1e1e 3f267e6f 3f2ed44b 3f371fc4
  //   3f3f60ef 3f4797dd 3f4fc4a3 3f57e753 3f600000 3ed5f85c 3ee739ce 3ef86563 3f04bda1 3f0d3dcb 3f15b343
  //   3f1e1e1e 3f267e6f 3f2ed44b 3f371fc4 3f3f60ef 3f4797dd 3f4fc4a3 3f57e753 3f600000 3f680ebc 3ee739ce
  //   3ef86563 3f04bda1 3f0d3dcb 3f15b343 3f1e1e1e 3f267e6f 3f2ed44b 3f371fc4 3f3f60ef 3f4797dd 3f4fc4a3
  //   3f57e753 3f600000 3f680ebc 3f701399 3ef86563 3f04bda1 3f0d3dcb 3f15b343 3f1e1e1e 3f267e6f 3f2ed44b
  //   3f371fc4 3f3f60ef 3f4797dd 3f4fc4a3 3f57e753 3f600000 3f680ebc 3f701399 3f780eaa 3f04bda1 3f0d3dcb
  //   3f15b343 3f1e1e1e 3f267e6f 3f2ed44b 3f371fc4 3f3f60ef 3f4797dd 3f4fc4a3 3f57e753 3f600000 3f680ebc
  //   3f701399 3f780eaa 3f800000
endmodule

module AUX_B (
  input  [15:0] d,
  output [31:0] a
);

  ROM #(.addrWidth(15), .dataWidth(32)) rom_1 (.addr(d[14:0]), .data(a), .sel(1'b1));

  // Notes on the sheet:
  //   0...32767
  //   contents of rom_1 (hex, n*v repeats v):
  //   39f0dbd4 3cc007b4 3d3f0e2a 3d8e915b 3dbd229a 3deb3ca3 3e0c709f 3e230913 3e39688b 3e4f8fdb 3e657fd7
  //   3e7b394d 3e885e84 3e9305e6 3e9d932f 3ea806be 3c40856f 3d0fa7f6 3d6e36ed 3da5e8fe 3dd43e69 3e010ec1
  //   3e17c406 3e2e3fe1 3e44832b 3e5a8eb7 3e706356 3e8300eb 3e8db57e 3e984fc8 3ea2d028 3ead36fd 3cc007b4
  //   3d3f0e2a 3d8e915b 3dbd229a 3deb3ca3 3e0c709f 3e230913 3e39688b 3e4f8fdb 3e657fd7 3e7b394d 3e885e84
  //   3e9305e6 3e9d932f 3ea806be 3eb260f0 3d0fa7f6 3d6e36ed 3da5e8fe 3dd43e69 3e010ec1 3e17c406 3e2e3fe1
  //   3e44832b 3e5a8eb7 3e706356 3e8300eb 3e8db57e 3e984fc8 3ea2d028 3ead36fd 3eb784a4 3d3f0e2a 3d8e915b
  //   3dbd229a 3deb3ca3 3e0c709f 3e230913 3e39688b 3e4f8fdb 3e657fd7 3e7b394d 3e885e84 3e9305e6 3e9d932f
  //   3ea806be 3eb260f0 3ebca222 3d6e36ed 3da5e8fe 3dd43e69 3e010ec1 3e17c406 3e2e3fe1 3e44832b 3e5a8eb7
  //   3e706356 3e8300eb 3e8db57e 3e984fc8 3ea2d028 3ead36fd 3eb784a4 3ec1b977 3d8e915b 3dbd229a 3deb3ca3
  //   3e0c709f 3e230913 3e39688b 3e4f8fdb 3e657fd7 3e7b394d 3e885e84 3e9305e6 3e9d932f 3ea806be 3eb260f0
  //   3ebca222 3ec6caae 3da5e8fe 3dd43e69 3e010ec1 3e17c406 3e2e3fe1 3e44832b 3e5a8eb7 3e706356 3e8300eb
  //   3e8db57e 3e984fc8 3ea2d028 3ead36fd 3eb784a4 3ec1b977 3ecbd5d1 3dbd229a 3deb3ca3 3e0c709f 3e230913
  //   3e39688b 3e4f8fdb 3e657fd7 3e7b394d 3e885e84 3e9305e6 3e9d932f 3ea806be 3eb260f0 3ebca222 3ec6caae
  //   3ed0daec 3dd43e69 3e010ec1 3e17c406 3e2e3fe1 3e44832b 3e5a8eb7 3e706356 3e8300eb 3e8db57e 3e984fc8
  //   3ea2d028 3ead36fd 3eb784a4 3ec1b977 3ecbd5d1 3ed5da09 3deb3ca3 3e0c709f 3e230913 3e39688b 3e4f8fdb
  //   3e657fd7 3e7b394d 3e885e84 3e9305e6 3e9d932f 3ea806be 3eb260f0 3ebca222 3ec6caae 3ed0daec 3edad333
  //   3e010ec1 3e17c406 3e2e3fe1 3e44832b 3e5a8eb7 3e706356 3e8300eb 3e8db57e 3e984fc8 3ea2d028 3ead36fd
  //   3eb784a4 3ec1b977 3ecbd5d1 3ed5da09 3edfc674 3e0c709f 3e230913 3e39688b 3e4f8fdb 3e657fd7 3e7b394d
  //   3e885e84 3e9305e6 3e9d932f 3ea806be 3eb260f0 3ebca222 3ec6caae 3ed0daec 3edad333 3ee4b3d8 3e17c406
  //   3e2e3fe1 3e44832b 3e5a8eb7 3e706356 3e8300eb 3e8db57e 3e984fc8 3ea2d028 3ead36fd 3eb784a4 3ec1b977
  //   3ecbd5d1 3ed5da09 3edfc674 3ee99b68 3e230913 3e39688b 3e4f8fdb 3e657fd7 3e7b394d 3e885e84 3e9305e6
  //   3e9d932f 3ea806be 3eb260f0 3ebca222 3ec6caae 3ed0daec 3edad333 3ee4b3d8 3eee7d2e 3e2e3fe1 3e44832b
  //   3e5a8eb7 3e706356 3e8300eb 3e8db57e 3e984fc8 3ea2d028 3ead36fd 3eb784a4 3ec1b977 3ecbd5d1 3ed5da09
  //   3edfc674 3ee99b68 3ef35936 3bc0c48a 3cefbb5a 3d56aa32 3d9a40f1 3dc8b438 3df6b0bb 3e121c1f 3e28a641
  //   3e3ef79a 3e551102 3e6af34a 3e804f9f 3e8b0ad4 3e95aba7 3ea03278 3eaa9fa7 3c9034de 3d2762c6 3d82da35
  //   3db1898a 3ddfc135 3e06c180 3e1d6856 3e33d5f9 3e4a0b3f 3e6008fd 3e75d001 3e85b08c 3e905e84 3e9af24a
  //   3ea56c3e 3eafccbf 3cefbb5a 3d56aa32 3d9a40f1 3dc8b438 3df6b0bb 3e121c1f 3e28a641 3e3ef79a 3e551102
  //   3e6af34a 3e804f9f 3e8b0ad4 3e95aba7 3ea03278 3eaa9fa7 3eb4f391 3d2762c6 3d82da35 3db1898a 3ddfc135
  //   3e06c180 3e1d6856 3e33d5f9 3e4a0b3f 3e6008fd 3e75d001 3e85b08c 3e905e84 3e9af24a 3ea56c3e 3eafccbf
  //   3eba1429 3d56aa32 3d9a40f1 3dc8b438 3df6b0bb 3e121c1f 3e28a641 3e3ef79a 3e551102 3e6af34a 3e804f9f
  //   3e8b0ad4 3e95aba7 3ea03278 3eaa9fa7 3eb4f391 3ebf2e91 3d82da35 3db1898a 3ddfc135 3e06c180 3e1d6856
  //   3e33d5f9 3e4a0b3f 3e6008fd 3e75d001 3e85b08c 3e905e84 3e9af24a 3ea56c3e 3eafccbf 3eba1429 3ec442d6
  //   3d9a40f1 3dc8b438 3df6b0bb 3e121c1f 3e28a641 3e3ef79a 3e551102 3e6af34a 3e804f9f 3e8b0ad4 3e95aba7
  //   3ea03278 3eaa9fa7 3eb4f391 3ebf2e91 3ec95101 3db1898a 3ddfc135 3e06c180 3e1d6856 3e33d5f9 3e4a0b3f
  //   3e6008fd 3e75d001 3e85b08c 3e905e84 3e9af24a 3ea56c3e 3eafccbf 3eba1429 3ec442d6 3ece591f 3dc8b438
  //   3df6b0bb 3e121c1f 3e28a641 3e3ef79a 3e551102 3e6af34a 3e804f9f 3e8b0ad4 3e95aba7 3ea03278 3eaa9fa7
  //   3eb4f391 3ebf2e91 3ec95101 3ed35b39 3ddfc135 3e06c180 3e1d6856 3e33d5f9 3e4a0b3f 3e6008fd 3e75d001
  //   3e85b08c 3e905e84 3e9af24a 3ea56c3e 3eafccbf 3eba1429 3ec442d6 3ece591f 3ed8575b 3df6b0bb 3e121c1f
  //   3e28a641 3e3ef79a 3e551102 3e6af34a 3e804f9f 3e8b0ad4 3e95aba7 3ea03278 3eaa9fa7 3eb4f391 3ebf2e91
  //   3ec95101 3ed35b39 3edd4d90 3e06c180 3e1d6856 3e33d5f9 3e4a0b3f 3e6008fd 3e75d001 3e85b08c 3e905e84
  //   3e9af24a 3ea56c3e 3eafccbf 3eba1429 3ec4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
endmodule

module Fake6502 (
  input  PHI0,
  input  RDY,
  input  SO,
  input  nNMI,
  input  nIRQ,
  input  nRES,
  input  [7:0] DB_in,
  input  in_8,
  output PHI1,
  output PHI2,
  output R_W,
  output SYNC,
  output [15:0] Addr,
  output [7:0] DB_out,
  output [31:0] out_15
);

  wire [23:0] redump_redump_addr;
  wire [31:0] rom_1_data;

  ROM #(.addrWidth(24), .dataWidth(32)) rom_1 (.addr(redump_redump_addr), .data(rom_1_data), .sel(1'b1));
  RegDumpProcessor redump (
    .PHI0(PHI0), .regdump_data(rom_1_data), .Core_R_W(R_W), .Core_AB(Addr), .Core_DB(DB_out),
    .redump_addr(redump_redump_addr), .out_8(out_15), .in_2(in_8));
  not not_1 (PHI1, PHI0);

  assign PHI2 = PHI0;
  assign SYNC = 1'b0;

  // Notes on the sheet:
  //   N.C.
  //   N.C.
  //   N.C.
  //   Load regdump here
  //   contents of rom_1 (hex, n*v repeats v):
  //   8 ff17 c 15 5e 15 fff 13 a 12 a 11 a 10 a f a e a d a c a b a a a 9 a 8 a 7 a 6 a 5 a 4 a 3 a 2 a 1
  //   a 0 79 f15 74dd c017 42b 1000 4 1004 4 100c 6 8 4 11 2cd f302 9 d03 9 7f01 14d 5e06 9 807 9 7f05 15f
  //   ff08 11 fc0a 9 90b 9 9 f8 c 8 10e 8 380f a5 b400 b6 fa04 68f b500 b6 f904 60b0 c017 dbc b600 b6 f804
  //   65e1 c017 dbc b700 b6 f704 65e4 c017 dbc b800 b6 f604 65e1 c017 dbc b700 b6 f504 65e1 c017 dbc b600
  //   b6 f404 65e4 c017 dbc b500 b6 f304 65e1 c017 dae b600 b6 f204 65f0 c017 dae b600 b6 f704 65f0 c017
  //   dae b600 b6 f704 65f0 c017 dae b600 b6 f604 65f0 c017 dae b600 b6 f504 65f0 c017 dae b600 b6 f404
  //   65f0 c017 dae b600 b6 f404 65f0 c017 dae b600 b6 f304 65f0 c017 dae b600 b6 f204 65f0 c017 dae b600
  //   b6 f204 65f0 c017 dae b600 b6 f204 65f0 c017 dae b600 b6 f504 65f0 c017 dae b600 b6 f504 65f0 c017
  //   dae b600 b6 f504 65f0 c017 dae b600 b6 f404 65f0 c017 dae b600 b6 f304 65f0 c017 dae b600 b6 f204
  //   65f0 c017 dae b600 b6 f204 65f0 c017 dae b600 b6 f204 65f0 c017 dae b600 b6 f104 65f0 c017 dae b600
  //   b6 f104 65f0 c017 dae b600 b6 f404 65f0 c017 dae b600 b6 f404 65f0 c017 dae b600 b6 f304 65f0 c017
  //   dae b600 b6 f204 65f0 c017 dae b600 b6 f104 65f0 c017 dae b600 b6 f204 65f0 c017 dae b600 b6 f204
  //   65f0 c017 dae b600 b6 f104 65f0 c017 dae b600 b6 f104 65f0 c017 dae b600 b6 f104 65f0 c017 dae b600
  //   b6 f204 65f0 c017 dae b600 b6 f204 65f0 c017 dae b600 b6 f204 65f0 c017 dae b600 b6 f104 65f0 c017
  //   dae b600 b6 f104 65f0 c017 dae b600 aa 1004 65fc c017 dae b600 aa 1004 65fc c017 dae b600 aa 1004
  //   65fc c017 dae b600 aa 1004 65fc c017 dae b600 aa 1004 65fc c017 dae b600 aa 1004 65fc c017 dae b600
  //   aa 1004 65fc c017 dae b600 aa 1004 65fc c017 dae b600 aa 1004 65fc c017 dae b600 aa 1004 65fc c017
  //   dae b600 aa 1004 65fc c017 dae b600 aa 1004 65fc c017 dae b600 aa 1004 65fc c017 dae b600 aa 1004
  //   65fc c017 dae b600 aa 1004 65fc c017 dae b600 aa 1004 65fc c017 dae b600 aa 1004 65fc c017 dae b600
  //   aa 1004 65fc c017 dae b600 aa 1004 65fc c017 dae b600 aa 1004 65fc c017 dae b600 aa 1004 65fc c017
  //   dae b600 aa 1004 65fc c017 dae b600 aa 1004 65fc c017 dae b600 aa 1004 65fc c017 dae b600 aa 1004
  //   65fc c017 dae b600 aa 1004 65fc c017 dae b600 aa 1004 65fc c017 dae b600 aa 1004 65fc c017 dae b600
  //   aa 1004 65fc c017 dae b600 aa 1004 65fc c017 dae b600 aa 1004 65fc c017 dae b600 aa 1004 65fc c017
  //   dae b600 aa 1004 65fc c017 dae b600 aa 1004 65fc c017 dae b600 aa 1004 65fc c017 dae b600 aa 1004
  //   65fc c017 dae b600 aa 1004 65fc c017 dae b600 aa 1004 65fc c017 dae b600 aa 1004 65fc c017 dae b600
  //   aa 1004 65fc c017 d32 f302 9 d03 9 7f01 161 ff08 11 fc0a 9 90b 9 9 a1 1000 aa 1004 6440 c017 d7d
  //   1000 aa 1004 662f c017 d7d 1000 aa 1004 662c c017 d7d 1000 aa 1004 662c c017 d7d 1000 aa 1004 662f
  //   c017 d7d 1000 aa 1004 662c c017 d7d 1000 aa 1004 662c c017 d7d 1000 aa 1004 662f c017 d7d 1000 aa
  //   1004 662c c017 d7d 1000 aa 1004 662c c017 d7d 1000 aa 1004 662f c017 d7d 1000 aa 1004 662c c017 d7d
  //   1000 aa 1004 662c c017 d7d 1000 aa 1004 662f c017 db6 8 11 fc0a 9 90b 9 9 a1 1000 aa 1004 6530 c017
  //   d7d 1000 aa 1004 662c c017 d7d 1000 aa 1004 662c c017 d7d 1000 aa 1004 662f c017 d7d 1000 aa 1004
  //   662c c017 d7d 1000 aa 1004 662c c017 d7d 1000 aa 1004 662f c017 d7d 1000 aa 1004 662c c017 d7d 1000
  //   aa 1004 662c c017 d7d 1000 aa 1004 662f c017 d7d 1000 aa 1004 662c c017 d7d 1000 aa 1004 662c c017
  //   d7d 1000 aa 1004 662f c017 d7d 1000 aa 1004 662c c017 d6e f302 9 d03 9 7f01 e2 3a06 9 807 9 7f05 158
  //   ff08 11 fc0a 9 90b 9 9 f1 c 8 10e 8 380f a5 b400 b6 fa04 6209 c017 dbc b500 b6 f904 65e1 c017 dbc
  //   b600 b6 f804 65e4 c017 dbc b700 b6 f704 65e1 c017 dbc b800 b6 f604 65e1 c017 dbc b700 b6 f504 65e4
  //   c017 dbc b600 b6 f404 65e1 c017 dbc b500 b6 f304 65e1 c017 dae b600 b6 f204 65f0 c017 dae b600 b6
  //   f704 65f0 c017 dae b600 b6 f704 65f0 c017 dae b600 b6 f604 65f0 c017 dae b600 b6 f504 65f0 c017 dae
  //   b600 b6 f404 65f0 c017 dae b600 b6 f404 65f0 c017 dae b600 b6 f304 65f0 c017 dae b600 b6 f204 65f0
  //   c017 dae b600 b6 f204 65f0 c017 dae b600 b6 f204 65f0 c017 dae b600 b6 f504 65f0 c017 dae b600 b6
  //   f504 65f0 c017 dae b600 b6 f504 65f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
endmodule

module WRAM (
  input  M2,
  input  [15:0] Addr,
  input  [7:0] DB_in,
  input  R_W,
  input  nRES,
  output [7:0] DB_out
);

  wire nor_1_out, not_1_out, not_2_out;

  not not_1 (not_1_out, nRES);
  nor nor_1 (nor_1_out, Addr[11], Addr[12], Addr[13], Addr[14], Addr[15]);
  not not_2 (not_2_out, R_W);
  RAM #(.addrWidth(11), .bus("separate")) ram_1 (
    .addr(Addr[10:0]), .din(DB_in), .data(DB_out), .str(not_2_out), .sel(nor_1_out), .clk(M2), .ld(R_W),
    .clr(not_1_out));
endmodule

module RegDumpProcessor (
  input  PHI0,
  input  in_2,
  input  [31:0] regdump_data,
  output Core_R_W,
  output [15:0] Core_AB,
  output [7:0] Core_DB,
  output [23:0] redump_addr,
  output [31:0] out_8
);

  wire and_1_out, and_2_out, cnt_ovf_reg_q, comparator_1_eq, comparator_2_gt, multiplexer_1_out,
       multiplexer_2_out, not_1_out, or_1_out, or_2_out;
  wire [7:0] regop_word_q_2, undriven;
  wire [15:0] or_3_out;
  wire [31:0] delta_phi_word_q, multiplexer_3_out, regop_word_q;

  or or_1 (or_1_out, in_2, cnt_ovf_reg_q);
  Multiplexer #(.enable("false")) multiplexer_1 (.in0(1'b1), .in1(1'b1), .out(multiplexer_1_out), .sel(or_1_out));
  Multiplexer #(.enable("false")) multiplexer_2 (.in0(1'b1), .in1(1'b0), .out(multiplexer_2_out), .sel(or_1_out));
  Register #(.width(32)) delta_phi_word (.D(regdump_data), .Q(delta_phi_word_q), .clk(cnt_ovf_reg_q));  // open: en, clr
  Multiplexer #(.width(32), .enable("false")) multiplexer_3 (
    .in0(regdump_data), .in1(32'h20), .out(multiplexer_3_out), .sel(in_2));
  Counter #(.width(32), .max('hffffffff), .ongoal("stay")) phi_dec_cnt (
    .load(multiplexer_1_out), .D(multiplexer_3_out), .count(multiplexer_2_out), .Q(out_8), .clk(PHI0));  // open: carry, clr
  Register #(.width(32)) regop_word (
    .D(regdump_data), .Q({regop_word_q[31:16], regop_word_q_2, regop_word_q[7:0]}), .clk(and_1_out),
    .clr(cnt_ovf_reg_q));  // open: en
  Comparator #(.width(32)) comparator_1 (.a(out_8), .b({32{1'b0}}), .eq(comparator_1_eq));  // open: gt, lt
  Comparator #(.width(32)) comparator_2 (.a(delta_phi_word_q), .b({32{1'b0}}), .gt(comparator_2_gt));  // open: eq, lt
  Register #(.width(1)) cnt_ovf_reg (.D(comparator_1_eq), .Q(cnt_ovf_reg_q), .clk(PHI0));  // open: en, clr
  and and_1 (and_1_out, PHI0, comparator_2_gt, comparator_1_eq, ~cnt_ovf_reg_q);  // AND_Gate
  or or_2 (or_2_out, and_1_out, cnt_ovf_reg_q);
  assign or_3_out = 16'h4000 | {{11{1'b0}}, regop_word_q[4:0]};  // OR_Gate or_3, 16 bits wide
  not not_1 (not_1_out, regop_word_q[7]);
  Multiplexer #(.enable("false")) multiplexer_4 (.in0(1'b1), .in1(regop_word_q[7]), .out(Core_R_W), .sel(and_1_out));
  Multiplexer #(.width(16), .enable("false")) multiplexer_5 (
    .in0({16{1'b0}}), .in1(or_3_out), .out(Core_AB), .sel(and_1_out));
  Multiplexer #(.width(8), .enable("false")) multiplexer_6 (
    .in0(undriven), .in1(regop_word_q_2), .out(Core_DB), .sel(and_2_out));
  and and_2 (and_2_out, and_1_out, not_1_out);
  Counter #(.width(24), .max('hffffff), .ongoal("stay"), .trigger("falling")) addr_cnt (
    .load(1'b0), .count(1'b1), .Q(redump_addr), .clk(or_2_out));  // open: D, carry, clr

  // Notes on the sheet:
  //   https://github.com/emu-russia/breaknes/blob/main/BreaksAPU/NSFPlayerInterop/RegDumpProcessor.cpp
  //   Load/Decrement Setup (1: Load; 0: Decrement)
  //   Do RegOp
  //   Load PHI Counter
  //   RegOp Setup
  //   Reg Index (0-0x1f)
  //   Reg Address
  //   Value (if write)
  //   1: Read register
  //   Default: Read address 0x0000
  //   1: RegOp + Write
  //   Falling edge
endmodule
