// Logisim project 2C0x_PPU.circ as structural Verilog
// 2C02G NTSC
module _2C02_NTSC (
  input  RS2,
  input  RS1,
  input  RS0,
  input  R_W,
  input  nDBE,
  input  D0,
  input  D1,
  input  D2,
  input  D3,
  input  D4,
  input  D5,
  input  D6,
  input  D7,
  input  EXT0,
  input  EXT1,
  input  EXT2,
  input  EXT3,
  input  CLK,
  input  nRES,
  input  PD7,
  input  PD6,
  input  PD5,
  input  PD4,
  input  PD3,
  input  PD2,
  input  PD1,
  input  PD0,
  output D0_2,
  output D1_2,
  output D2_2,
  output D3_2,
  output D4_2,
  output D5_2,
  output D6_2,
  output D7_2,
  output EXT0_2,
  output EXT1_2,
  output EXT2_2,
  output EXT3_2,
  output [10:0] VOUT,
  output nINT,
  output nRD,
  output nWR,
  output PA13,
  output PA12,
  output PA11,
  output PA10,
  output PA9,
  output PA8,
  output PA7,
  output PA6,
  output PA5,
  output PA4,
  output PA3,
  output PA2,
  output PA1,
  output PA0,
  output ALE,
  output PD7_W,
  output PD6_W,
  output PD5_W,
  output PD4_W,
  output PD3_W,
  output PD2_W,
  output PD1_W,
  output PD0_W
);

  wire BLNK, button_1_out, button_2_out, CLK_out, color_control_1_color_en, color_control_1_ncb_db,
       color_control_1_ndb_cb, color_io_1_nout0, color_io_1_nout1, color_io_1_nout2, color_io_1_nout3,
       color_io_1_nout4, color_io_1_nout5, control_regs_ntsc_1_bgclip, control_regs_ntsc_1_bgsel,
       control_regs_ntsc_1_black, control_regs_ntsc_1_bw, control_regs_ntsc_1_clpb,
       control_regs_ntsc_1_i1_32, control_regs_ntsc_1_nclpo, control_regs_ntsc_1_nslave,
       control_regs_ntsc_1_o8_16, control_regs_ntsc_1_obclip, control_regs_ntsc_1_obsel,
       control_regs_ntsc_1_vbl, control_unit_ntsc_1__0_hpos, control_unit_ntsc_1_burst,
       control_unit_ntsc_1_clip_b, control_unit_ntsc_1_clip_o, control_unit_ntsc_1_e_ev,
       control_unit_ntsc_1_e_out, control_unit_ntsc_1_eval, control_unit_ntsc_1_f_at,
       control_unit_ntsc_1_f_ta, control_unit_ntsc_1_f_tb, control_unit_ntsc_1_hc, control_unit_ntsc_1_nf_nt,
       control_unit_ntsc_1_nfo, control_unit_ntsc_1_npicture, control_unit_ntsc_1_nvset,
       control_unit_ntsc_1_s_ev, control_unit_ntsc_1_sc_cnt, control_unit_ntsc_1_sync,
       control_unit_ntsc_1_vb, control_unit_ntsc_1_vc, control_unit_ntsc_1_vin, DB_PAR, H0_prime,
       H0_prime_prime, h_counter_1_h0, h_counter_1_h1, h_counter_1_h2, h_counter_1_h3, h_counter_1_h4,
       h_counter_1_h5, h_counter_1_h6, h_counter_1_h7, h_counter_1_h8, hv_select_ntsc_1_hpla_0,
       hv_select_ntsc_1_hpla_1, hv_select_ntsc_1_hpla_2, hv_select_ntsc_1_hpla_3, hv_select_ntsc_1_hpla_4,
       hv_select_ntsc_1_hpla_5, hv_select_ntsc_1_hpla_6, hv_select_ntsc_1_hpla_7, hv_select_ntsc_1_hpla_8,
       hv_select_ntsc_1_hpla_9, hv_select_ntsc_1_hpla_10, hv_select_ntsc_1_hpla_11, hv_select_ntsc_1_hpla_12,
       hv_select_ntsc_1_hpla_13, hv_select_ntsc_1_hpla_14, hv_select_ntsc_1_hpla_15,
       hv_select_ntsc_1_hpla_16, hv_select_ntsc_1_hpla_17, hv_select_ntsc_1_hpla_18,
       hv_select_ntsc_1_hpla_19, hv_select_ntsc_1_hpla_20, hv_select_ntsc_1_hpla_21,
       hv_select_ntsc_1_hpla_22, hv_select_ntsc_1_hpla_23, hv_select_ntsc_1_vpla_0, hv_select_ntsc_1_vpla_1,
       hv_select_ntsc_1_vpla_2, hv_select_ntsc_1_vpla_3, hv_select_ntsc_1_vpla_4, hv_select_ntsc_1_vpla_5,
       hv_select_ntsc_1_vpla_6, hv_select_ntsc_1_vpla_7, hv_select_ntsc_1_vpla_8, I_OAM2,
       interrupt_control_1_int, nH1_prime, nH2_prime, not_1_out, not_3_out, not_4_out, not_6_out, not_22_out,
       not_23_out, not_24_out, not_25_out, not_26_out, nR2, nR7, nVIS, nW7, oam_buf_control_1_nwe,
       oam_buf_control_1_ob_oam, oam_buf_control_1_ofetch, oam_control_ntsc_1_oamctr2,
       oam_control_ntsc_1_spr_ov, oam_eval_1__0_fifo, oam_eval_1_i2sev, oam_eval_1_omfg, oam_eval_1_test,
       oam_fifo_1_nspr0hit, or_1_out, PAR_O, picture_address_gen_1_tvo1, PIXEL_CLOCK_npclk,
       PIXEL_CLOCK_pclk_2, R2DB5, R2DB6, R2DB7, RC, register_select_1_nr4, register_select_1_nw0,
       register_select_1_nw1, register_select_1_nw3, register_select_1_nw4, register_select_1_nw5_1,
       register_select_1_nw5_2, register_select_1_nw6_1, register_select_1_nw6_2, RES, RESCL,
       rw_control_1_nrd, rw_control_1_nwr, TH_MUX, v_counter_1_v0, v_counter_1_v1, v_counter_1_v2,
       v_counter_1_v3, v_counter_1_v4, v_counter_1_v5, v_counter_1_v6, v_counter_1_v7, v_counter_1_v8,
       vram_bus_control_1_nale, vram_bus_control_1_pd_rb, vram_bus_control_1_tstep, vram_bus_control_1_xrb;
  wire [1:0] PCLK;
  wire [2:0] control_regs_ntsc_1_ntr, picture_address_gen_1_fh0;
  wire [3:0] bg_color_1_bgc0, oam_eval_1_ov0, select_2_3_5_7_pixel_1_nsh2;
  wire [4:0] color_io_1_db0_2, controlled_buffer_2_out, mux_1_pal0, oam_fifo_1_nzcol0, TH;
  wire [5:0] color_io_1_cb_ram0, hv_select_ntsc_1_hnn, ram_1_data;
  wire [5:1] Hnn_BUS;
  wire [7:0] controlled_buffer_1_out, cpu_data_io_1_cpu_ppu, demultiplexer_1_out0, demultiplexer_1_out1,
       h_inversion_1_nt0, hv_select_ntsc_1_vpos, multiplexer_1_out, mux_1_ext0_out, oam_buffer_1_ob_bit_out,
       oam_buffer_1_ram_write, PPU_DATA, ram_2_data, ram_3_data, rom_1_data;
  wire [8:0] oam_control_ntsc_1_noam3;
  wire [11:0] not_5_out;
  wire [12:12] not_5_out_2;
  wire [13:0] PPU_ADR, undriven;
  wire [13:13] not_5_out_3;

  Clock u_CLK (.out(CLK_out));
  Button button_1 (.out(button_1_out));
  not not_1 (not_1_out, CLK_out);
  not not_2 (nINT, interrupt_control_1_int);
  or or_1 (or_1_out, RESCL, button_1_out);
  VIDEO_OUT_NTSC video_out_ntsc_1 (
    .nCLK(not_1_out), .RES(RES), .nTR(control_regs_ntsc_1_ntr[0]), .nTG(control_regs_ntsc_1_ntr[1]),
    .nTB(control_regs_ntsc_1_ntr[2]), .PCLK(PCLK), .nCC0(color_io_1_nout0), .nCC1(color_io_1_nout1),
    .nCC2(color_io_1_nout2), .nCC3(color_io_1_nout3), .nPICTURE(control_unit_ntsc_1_npicture),
    .SYNC(control_unit_ntsc_1_sync), .BURST(control_unit_ntsc_1_burst), .nLL0(color_io_1_nout5),
    .nLL1(color_io_1_nout4), .out_16(VOUT));
  COLOR_IO color_io_1 (
    .PCLK(PCLK), .nDB_CB(color_control_1_ndb_cb), .nCB_DB(color_control_1_ncb_db),
    .nBW(color_control_1_color_en), .RAM_CB0(ram_1_data[0]), .DB0(cpu_data_io_1_cpu_ppu[0]),
    .RAM_CB1(ram_1_data[1]), .DB1(cpu_data_io_1_cpu_ppu[1]), .RAM_CB2(ram_1_data[2]),
    .DB2(cpu_data_io_1_cpu_ppu[2]), .RAM_CB3(ram_1_data[3]), .DB3(cpu_data_io_1_cpu_ppu[3]),
    .RAM_CB4(ram_1_data[4]), .DB4(cpu_data_io_1_cpu_ppu[4]), .RAM_CB5(ram_1_data[5]),
    .DB5(cpu_data_io_1_cpu_ppu[5]), .nout0(color_io_1_nout0), .DB0_2(color_io_1_db0_2[0]),
    .CB_RAM0(color_io_1_cb_ram0[0]), .nout1(color_io_1_nout1), .DB1_2(color_io_1_db0_2[1]),
    .CB_RAM1(color_io_1_cb_ram0[1]), .nout2(color_io_1_nout2), .DB2_2(color_io_1_db0_2[2]),
    .CB_RAM2(color_io_1_cb_ram0[2]), .nout3(color_io_1_nout3), .DB3_2(color_io_1_db0_2[3]),
    .CB_RAM3(color_io_1_cb_ram0[3]), .nout4(color_io_1_nout4), .DB4_2(color_io_1_db0_2[4]),
    .CB_RAM4(color_io_1_cb_ram0[4]), .nout5(color_io_1_nout5), .DB5_2(R2DB5), .CB_RAM5(color_io_1_cb_ram0[5]));
  RESET_FF reset_ff_1 (.nRES(nRES), .RESCL(or_1_out), .RES(RES), .RC(RC));
  not not_3 (not_3_out, color_control_1_ndb_cb);
  PIXEL_CLOCK_NTSC PIXEL_CLOCK (
    .nCLK(not_1_out), .RES(RES), .PCLK(PCLK), .nPCLK(PIXEL_CLOCK_npclk), .PCLK_2(PIXEL_CLOCK_pclk_2));
  RAM #(.addrWidth(5), .dataWidth(6), .bus("separate")) ram_1 (
    .addr(mux_1_pal0), .din(color_io_1_cb_ram0), .data(ram_1_data), .str(not_3_out), .sel(1'b1),
    .clk(PCLK[0]), .ld(color_control_1_ndb_cb));  // open: clr
  CONTROL_UNIT_NTSC control_unit_ntsc_1 (
    .PCLK(PCLK), .Hnn(hv_select_ntsc_1_hnn), .nOBCLIP(control_regs_ntsc_1_bgclip),
    .nBGCLIP(control_regs_ntsc_1_obclip), .HPLA_2(hv_select_ntsc_1_hpla_2), .HPLA_3(hv_select_ntsc_1_hpla_3),
    .HPLA_4(hv_select_ntsc_1_hpla_4), .HPLA_5(hv_select_ntsc_1_hpla_5), .HPLA_6(hv_select_ntsc_1_hpla_6),
    .HPLA_7(hv_select_ntsc_1_hpla_7), .HPLA_8(hv_select_ntsc_1_hpla_8), .HPLA_9(hv_select_ntsc_1_hpla_9),
    .HPLA_10(hv_select_ntsc_1_hpla_10), .HPLA_11(hv_select_ntsc_1_hpla_11),
    .HPLA_16(hv_select_ntsc_1_hpla_16), .HPLA_13(hv_select_ntsc_1_hpla_13),
    .HPLA_12(hv_select_ntsc_1_hpla_12), .HPLA_14(hv_select_ntsc_1_hpla_14),
    .HPLA_15(hv_select_ntsc_1_hpla_15), .HPLA_19(hv_select_ntsc_1_hpla_19),
    .HPLA_20(hv_select_ntsc_1_hpla_20), .HPLA_0(hv_select_ntsc_1_hpla_0), .HPLA_1(hv_select_ntsc_1_hpla_1),
    .HPLA_21(hv_select_ntsc_1_hpla_21), .HPLA_22(hv_select_ntsc_1_hpla_22),
    .HPLA_17(hv_select_ntsc_1_hpla_17), .HPLA_18(hv_select_ntsc_1_hpla_18), .VPLA_1(hv_select_ntsc_1_vpla_1),
    .VPLA_0(hv_select_ntsc_1_vpla_0), .VPLA_3(hv_select_ntsc_1_vpla_3), .VPLA_2(hv_select_ntsc_1_vpla_2),
    .VPLA_4(hv_select_ntsc_1_vpla_4), .VPLA_5(hv_select_ntsc_1_vpla_5), .VPLA_6(hv_select_ntsc_1_vpla_6),
    .VPLA_7(hv_select_ntsc_1_vpla_7), .VPLA_8(hv_select_ntsc_1_vpla_8), .BLACK(control_regs_ntsc_1_black),
    .HPLA_23(hv_select_ntsc_1_hpla_23), .V8(v_counter_1_v8), .RES(RES), .H0_prime_prime(H0_prime_prime),
    .H1_prime_prime(Hnn_BUS[1]), .H2_prime_prime(Hnn_BUS[2]), .H3_prime_prime(Hnn_BUS[3]),
    .H4_prime_prime(Hnn_BUS[4]), .H5_prime_prime(Hnn_BUS[5]), .H0_prime(H0_prime), .nH1_prime(nH1_prime),
    .nH2_prime(nH2_prime), .S_EV(control_unit_ntsc_1_s_ev), .CLIP_O(control_unit_ntsc_1_clip_o),
    .CLIP_B(control_unit_ntsc_1_clip_b), ._0_HPOS(control_unit_ntsc_1__0_hpos),
    .EVAL(control_unit_ntsc_1_eval), .E_EV(control_unit_ntsc_1_e_ev), .I_OAM2(I_OAM2), .PAR_O(PAR_O),
    .nVIS(nVIS), .nF_NT(control_unit_ntsc_1_nf_nt), .F_AT(control_unit_ntsc_1_f_at),
    .F_TA(control_unit_ntsc_1_f_ta), .F_TB(control_unit_ntsc_1_f_tb), .nFO(control_unit_ntsc_1_nfo),
    .SC_CNT(control_unit_ntsc_1_sc_cnt), .SYNC(control_unit_ntsc_1_sync), .BURST(control_unit_ntsc_1_burst),
    .nPICTURE(control_unit_ntsc_1_npicture), .nVSET(control_unit_ntsc_1_nvset), .VB(control_unit_ntsc_1_vb),
    .BLNK(BLNK), .RESCL(RESCL), .VC(control_unit_ntsc_1_vc), .VIN(control_unit_ntsc_1_vin),
    .HC(control_unit_ntsc_1_hc), .E_OUT(control_unit_ntsc_1_e_out), .CFG(control_unit_ntsc_1_e_out));
  H_COUNTER h_counter_1 (
    .RES(RES), .HC(control_unit_ntsc_1_hc), .PCLK(PCLK), .H0(h_counter_1_h0), .H1(h_counter_1_h1),
    .H2(h_counter_1_h2), .H3(h_counter_1_h3), .H4(h_counter_1_h4), .H5(h_counter_1_h5), .H6(h_counter_1_h6),
    .H7(h_counter_1_h7), .H8(h_counter_1_h8));
  OAM_FIFO oam_fifo_1 (
    .PCLK(PCLK), ._0_HPOS(control_unit_ntsc_1__0_hpos), .H3_prime_prime(Hnn_BUS[3]),
    .H4_prime_prime(Hnn_BUS[4]), .H5_prime_prime(Hnn_BUS[5]), .nSH2(select_2_3_5_7_pixel_1_nsh2[0]),
    .nSH3(select_2_3_5_7_pixel_1_nsh2[1]), .nSH5(select_2_3_5_7_pixel_1_nsh2[2]),
    .nSH7(select_2_3_5_7_pixel_1_nsh2[3]), .nVIS(nVIS), .nCLPO(control_regs_ntsc_1_nclpo),
    .OB0(oam_buffer_1_ob_bit_out[0]), .OB1(oam_buffer_1_ob_bit_out[1]), .OB2(oam_buffer_1_ob_bit_out[2]),
    .OB3(oam_buffer_1_ob_bit_out[3]), .OB4(oam_buffer_1_ob_bit_out[4]), .OB5(oam_buffer_1_ob_bit_out[5]),
    .OB6(oam_buffer_1_ob_bit_out[6]), .OB7(oam_buffer_1_ob_bit_out[7]), .nT0(h_inversion_1_nt0[0]),
    .nT1(h_inversion_1_nt0[1]), .nT2(h_inversion_1_nt0[2]), .nT3(h_inversion_1_nt0[3]),
    .nT4(h_inversion_1_nt0[4]), .nT5(h_inversion_1_nt0[5]), .nT6(h_inversion_1_nt0[6]),
    .nT7(h_inversion_1_nt0[7]), .nSPR0HIT(oam_fifo_1_nspr0hit), .nZCOL0(oam_fifo_1_nzcol0[0]),
    .nZCOL1(oam_fifo_1_nzcol0[1]), .ZCOL2(oam_fifo_1_nzcol0[2]), .ZCOL3(oam_fifo_1_nzcol0[3]),
    .nZPRIO(oam_fifo_1_nzcol0[4]));
  V_COUNTER v_counter_1 (
    .VIN(control_unit_ntsc_1_vin), .PCLK(PCLK), .RES(RES), .VC(control_unit_ntsc_1_vc), .V0(v_counter_1_v0),
    .V1(v_counter_1_v1), .V2(v_counter_1_v2), .V3(v_counter_1_v3), .V4(v_counter_1_v4), .V5(v_counter_1_v5),
    .V6(v_counter_1_v6), .V7(v_counter_1_v7), .V8(v_counter_1_v8));
  INTERRUPT_CONTROL interrupt_control_1 (
    .VBL_EN(control_regs_ntsc_1_vbl), .VSET(control_unit_ntsc_1_nvset), .RESCL(RESCL), .nDBE(nDBE),
    .nR2(nR2), .INT(interrupt_control_1_int), .DB7(R2DB7), .PCLK(PCLK));
  COLOR_CONTROL color_control_1 (
    .PCLK(PCLK), .DB_PAR(DB_PAR), .TH_MUX(TH_MUX), .nR7(nR7), .nDBE(nDBE),
    .nPICTURE(control_unit_ntsc_1_npicture), .BW(control_regs_ntsc_1_bw), .nDB_CB(color_control_1_ndb_cb),
    .nCB_DB(color_control_1_ncb_db), .COLOR_EN(color_control_1_color_en));
  HV_SELECT_NTSC hv_select_ntsc_1 (
    .H8(h_counter_1_h8), .H7(h_counter_1_h7), .H6(h_counter_1_h6), .H5(h_counter_1_h5), .H4(h_counter_1_h4),
    .H3(h_counter_1_h3), .H2(h_counter_1_h2), .H1(h_counter_1_h1), .H0(h_counter_1_h0),
    .VB(control_unit_ntsc_1_vb), .BLNK(BLNK), .V8(v_counter_1_v8), .V7(v_counter_1_v7), .V6(v_counter_1_v6),
    .V5(v_counter_1_v5), .V4(v_counter_1_v4), .V3(v_counter_1_v3), .V2(v_counter_1_v2), .V1(v_counter_1_v1),
    .V0(v_counter_1_v0), .VPOS(hv_select_ntsc_1_vpos), .Hnn(hv_select_ntsc_1_hnn),
    .HPLA_0(hv_select_ntsc_1_hpla_0), .VPLA_0(hv_select_ntsc_1_vpla_0), .HPLA_1(hv_select_ntsc_1_hpla_1),
    .VPLA_1(hv_select_ntsc_1_vpla_1), .HPLA_2(hv_select_ntsc_1_hpla_2), .VPLA_2(hv_select_ntsc_1_vpla_2),
    .HPLA_3(hv_select_ntsc_1_hpla_3), .VPLA_3(hv_select_ntsc_1_vpla_3), .HPLA_4(hv_select_ntsc_1_hpla_4),
    .VPLA_4(hv_select_ntsc_1_vpla_4), .HPLA_5(hv_select_ntsc_1_hpla_5), .VPLA_5(hv_select_ntsc_1_vpla_5),
    .HPLA_6(hv_select_ntsc_1_hpla_6), .VPLA_6(hv_select_ntsc_1_vpla_6), .HPLA_7(hv_select_ntsc_1_hpla_7),
    .VPLA_7(hv_select_ntsc_1_vpla_7), .HPLA_8(hv_select_ntsc_1_hpla_8), .VPLA_8(hv_select_ntsc_1_vpla_8),
    .HPLA_9(hv_select_ntsc_1_hpla_9), .HPLA_10(hv_select_ntsc_1_hpla_10), .HPLA_11(hv_select_ntsc_1_hpla_11),
    .HPLA_12(hv_select_ntsc_1_hpla_12), .HPLA_13(hv_select_ntsc_1_hpla_13),
    .HPLA_14(hv_select_ntsc_1_hpla_14), .HPLA_15(hv_select_ntsc_1_hpla_15),
    .HPLA_16(hv_select_ntsc_1_hpla_16), .HPLA_17(hv_select_ntsc_1_hpla_17),
    .HPLA_18(hv_select_ntsc_1_hpla_18), .HPLA_19(hv_select_ntsc_1_hpla_19),
    .HPLA_20(hv_select_ntsc_1_hpla_20), .HPLA_21(hv_select_ntsc_1_hpla_21),
    .HPLA_22(hv_select_ntsc_1_hpla_22), .HPLA_23(hv_select_ntsc_1_hpla_23));
  H_INVERSION h_inversion_1 (
    .PCLK(PCLK), .nSH2(select_2_3_5_7_pixel_1_nsh2[0]), .OB6(oam_buffer_1_ob_bit_out[6]),
    ._0_FIFO(oam_eval_1__0_fifo), .PD0(PPU_DATA[0]), .PD1(PPU_DATA[1]), .PD2(PPU_DATA[2]), .PD3(PPU_DATA[3]),
    .PD4(PPU_DATA[4]), .PD5(PPU_DATA[5]), .PD6(PPU_DATA[6]), .PD7(PPU_DATA[7]), .nT0(h_inversion_1_nt0[0]),
    .nT1(h_inversion_1_nt0[1]), .nT2(h_inversion_1_nt0[2]), .nT3(h_inversion_1_nt0[3]),
    .nT4(h_inversion_1_nt0[4]), .nT5(h_inversion_1_nt0[5]), .nT6(h_inversion_1_nt0[6]),
    .nT7(h_inversion_1_nt0[7]));
  READ__2007 read__2007_1 (
    .XRB(vram_bus_control_1_xrb), .RC(RC), .PD_RB(vram_bus_control_1_pd_rb), .PD0(PPU_DATA[0]),
    .PD1(PPU_DATA[1]), .PD2(PPU_DATA[2]), .PD3(PPU_DATA[3]), .PD4(PPU_DATA[4]), .PD5(PPU_DATA[5]),
    .PD6(PPU_DATA[6]), .PD7(PPU_DATA[7]), .DB0(color_io_1_db0_2[0]), .DB1(color_io_1_db0_2[1]),
    .DB2(color_io_1_db0_2[2]), .DB3(color_io_1_db0_2[3]), .DB4(color_io_1_db0_2[4]), .DB5(R2DB5),
    .DB6(R2DB6), .DB7(R2DB7));
  not not_4 (not_4_out, not_5_out_3[13]);
  assign {not_5_out_3[13], not_5_out_2[12], not_5_out} = ~undriven;  // NOT_Gate not_5, 14 bits wide
  ROM #(.addrWidth(13)) rom_1 (.addr({not_5_out_2[12], not_5_out}), .data(rom_1_data), .sel(not_4_out));
  ROM #(.addrWidth(12)) rom_2 (.addr(not_5_out), .data(rom_1_data), .sel(not_5_out_3[13]));
  not not_6 (not_6_out, nRD);
  REGISTER_SELECT register_select_1 (
    .nDBE(nDBE), .RC(RC), .RS0(RS0), .RS1(RS1), .RS2(RS2), .R_W(R_W), .nW6_1(register_select_1_nw6_1),
    .nW6_2(register_select_1_nw6_2), .nW5_1(register_select_1_nw5_1), .nW5_2(register_select_1_nw5_2),
    .nR7(nR7), .nW7(nW7), .nW4(register_select_1_nw4), .nW3(register_select_1_nw3), .nR2(nR2),
    .nW1(register_select_1_nw1), .nW0(register_select_1_nw0), .nR4(register_select_1_nr4));
  Hex_Digit_Display hex_digit_display_1 (.value(rom_1_data[7:4]));  // open: dp
  Hex_Digit_Display hex_digit_display_2 (.value(rom_1_data[3:0]));  // open: dp
  not not_7 (PA13, PPU_ADR[13]);
  not not_8 (PA12, PPU_ADR[12]);
  RW_CONTROL rw_control_1 (.R_W(R_W), .nDBE(nDBE), .nRD(rw_control_1_nrd), .nWR(rw_control_1_nwr));
  not not_9 (PA10, PPU_ADR[10]);
  not not_10 (PA11, PPU_ADR[11]);
  not not_11 (PA9, PPU_ADR[9]);
  not not_12 (PA8, PPU_ADR[8]);
  not not_13 (PA7, PPU_ADR[7]);
  OAM_EVAL oam_eval_1 (
    .PCLK(PCLK), .nF_NT(control_unit_ntsc_1_nf_nt), .H0_prime_prime(H0_prime_prime), .I_OAM2(I_OAM2),
    .nVIS(nVIS), .SPR_OV(oam_control_ntsc_1_spr_ov), .S_EV(control_unit_ntsc_1_s_ev), .PAR_O(PAR_O),
    .O8_16(control_regs_ntsc_1_o8_16), .OB0(oam_buffer_1_ob_bit_out[0]), .OB1(oam_buffer_1_ob_bit_out[1]),
    .OB2(oam_buffer_1_ob_bit_out[2]), .OB3(oam_buffer_1_ob_bit_out[3]), .OB4(oam_buffer_1_ob_bit_out[4]),
    .OB5(oam_buffer_1_ob_bit_out[5]), .OB6(oam_buffer_1_ob_bit_out[6]), .OB7(oam_buffer_1_ob_bit_out[7]),
    .V0(hv_select_ntsc_1_vpos[0]), .V1(hv_select_ntsc_1_vpos[1]), .V2(hv_select_ntsc_1_vpos[2]),
    .V3(hv_select_ntsc_1_vpos[3]), .V4(hv_select_ntsc_1_vpos[4]), .V5(hv_select_ntsc_1_vpos[5]),
    .V6(hv_select_ntsc_1_vpos[6]), .V7(hv_select_ntsc_1_vpos[7]), ._0_FIFO(oam_eval_1__0_fifo),
    .OMFG(oam_eval_1_omfg), .I2SEV(oam_eval_1_i2sev), .OV0(oam_eval_1_ov0[0]), .OV1(oam_eval_1_ov0[1]),
    .OV2(oam_eval_1_ov0[2]), .OV3(oam_eval_1_ov0[3]), .TEST(oam_eval_1_test));
  not not_14 (PA6, PPU_ADR[6]);
  CPU_DATA_IO cpu_data_io_1 (
    .nRD(rw_control_1_nrd), .nWR(rw_control_1_nwr), .PPU_CPU({R2DB7, R2DB6, R2DB5, color_io_1_db0_2}),
    .CPU_PPU(cpu_data_io_1_cpu_ppu), .D6_2(D6_2), .D7_2(D7_2), .D0(D0), .D1(D1), .D2(D2), .D3(D3), .D4(D4),
    .D5(D5), .D6(D6), .D7(D7), .D4_2(D4_2), .D5_2(D5_2), .D2_2(D2_2), .D3_2(D3_2), .D0_2(D0_2), .D1_2(D1_2));
  OAM_CONTROL_NTSC oam_control_ntsc_1 (
    .PCLK(PCLK), .OFETCH(oam_buf_control_1_ofetch), .BLNK(BLNK), .nVIS(nVIS),
    .H0_prime_prime(H0_prime_prime), .I_OAM2(I_OAM2), .OMFG(oam_eval_1_omfg), .nDBE(nDBE),
    .nW3(register_select_1_nw3), .PAR_O(PAR_O), .DB0(cpu_data_io_1_cpu_ppu[0]),
    .DB1(cpu_data_io_1_cpu_ppu[1]), .DB2(cpu_data_io_1_cpu_ppu[2]), .DB3(cpu_data_io_1_cpu_ppu[3]),
    .DB4(cpu_data_io_1_cpu_ppu[4]), .DB5(cpu_data_io_1_cpu_ppu[5]), .DB6(cpu_data_io_1_cpu_ppu[6]),
    .DB7(cpu_data_io_1_cpu_ppu[7]), .EVAL(control_unit_ntsc_1_eval), .nH2_prime(nH2_prime),
    .H0_prime(H0_prime), .RESCL(RESCL), .nR2(nR2), .nOAM0(oam_control_ntsc_1_noam3[0]),
    .nOAM1(oam_control_ntsc_1_noam3[1]), .nOAM2(oam_control_ntsc_1_noam3[2]),
    .nOAM3(oam_control_ntsc_1_noam3[3]), .nOAM4(oam_control_ntsc_1_noam3[4]),
    .nOAM5(oam_control_ntsc_1_noam3[5]), .nOAM6(oam_control_ntsc_1_noam3[6]),
    .nOAM7(oam_control_ntsc_1_noam3[7]), .OAM8(oam_control_ntsc_1_noam3[8]),
    .SPR_OV(oam_control_ntsc_1_spr_ov), .OAMCTR2(oam_control_ntsc_1_oamctr2), .DB5_2(R2DB5));
  CONTROL_REGS_NTSC control_regs_ntsc_1 (
    .RC(RC), .nDBE(nDBE), .nW0(register_select_1_nw0), .DB0(cpu_data_io_1_cpu_ppu[0]),
    .DB1(cpu_data_io_1_cpu_ppu[1]), .DB2(cpu_data_io_1_cpu_ppu[2]), .DB3(cpu_data_io_1_cpu_ppu[3]),
    .DB4(cpu_data_io_1_cpu_ppu[4]), .DB5(cpu_data_io_1_cpu_ppu[5]), .DB6(cpu_data_io_1_cpu_ppu[6]),
    .DB7(cpu_data_io_1_cpu_ppu[7]), .nW1(register_select_1_nw1), .PCLK(PCLK), .nVIS(nVIS),
    .CLIP_B(control_unit_ntsc_1_clip_b), .CLIP_O(control_unit_ntsc_1_clip_o),
    .I1_32(control_regs_ntsc_1_i1_32), .OBSEL(control_regs_ntsc_1_obsel), .BGSEL(control_regs_ntsc_1_bgsel),
    .O8_16(control_regs_ntsc_1_o8_16), .nSLAVE(control_regs_ntsc_1_nslave), .VBL(control_regs_ntsc_1_vbl),
    .BW(control_regs_ntsc_1_bw), .BGCLIP(control_regs_ntsc_1_bgclip), .OBCLIP(control_regs_ntsc_1_obclip),
    .CLPB(control_regs_ntsc_1_clpb), .nCLPO(control_regs_ntsc_1_nclpo), .nTR(control_regs_ntsc_1_ntr[0]),
    .nTG(control_regs_ntsc_1_ntr[1]), .nTB(control_regs_ntsc_1_ntr[2]), .BLACK(control_regs_ntsc_1_black));
  SELECT_2_3_5_7_PIXEL select_2_3_5_7_pixel_1 (
    .PCLK(PCLK), .PAR_O(PAR_O), .H0_prime_prime(H0_prime_prime), .H1_prime_prime(Hnn_BUS[1]),
    .H2_prime_prime(Hnn_BUS[2]), .nSH2(select_2_3_5_7_pixel_1_nsh2[0]),
    .nSH3(select_2_3_5_7_pixel_1_nsh2[1]), .nSH5(select_2_3_5_7_pixel_1_nsh2[2]),
    .nSH7(select_2_3_5_7_pixel_1_nsh2[3]));
  MUX mux_1 (
    .EXT3_IN(mux_1_ext0_out[7]), .EXT2_IN(mux_1_ext0_out[5]), .EXT1_IN(mux_1_ext0_out[3]),
    .EXT0_IN(mux_1_ext0_out[1]), .PCLK(PCLK), .BGC0(bg_color_1_bgc0[0]), .BGC1(bg_color_1_bgc0[1]),
    .BGC2(bg_color_1_bgc0[2]), .BGC3(bg_color_1_bgc0[3]), .nZCOL0(oam_fifo_1_nzcol0[0]),
    .nZCOL1(oam_fifo_1_nzcol0[1]), .ZCOL2(oam_fifo_1_nzcol0[2]), .ZCOL3(oam_fifo_1_nzcol0[3]),
    .nZPRIO(oam_fifo_1_nzcol0[4]), .THO0(TH[0]), .THO1(TH[1]), .THO2(TH[2]), .THO3(TH[3]), .THO4(TH[4]),
    .TH_MUX(TH_MUX), .nSPR0HIT(oam_fifo_1_nspr0hit), .I2SEV(oam_eval_1_i2sev), .nVIS(nVIS), .RESCL(RESCL),
    .nDBE(nDBE), .nR2(nR2), .EXT0_OUT(mux_1_ext0_out[0]), .EXT1_OUT(mux_1_ext0_out[2]),
    .EXT2_OUT(mux_1_ext0_out[4]), .EXT3_OUT(mux_1_ext0_out[6]), .PAL0(mux_1_pal0[0]), .PAL1(mux_1_pal0[1]),
    .PAL2(mux_1_pal0[2]), .PAL3(mux_1_pal0[3]), .PAL4(mux_1_pal0[4]), .DB6(R2DB6));
  VRAM_BUS_CONTROL vram_bus_control_1 (
    .PCLK(PCLK), .nR7(nR7), .nDBE(nDBE), .nW7(nW7), .BLNK(BLNK), .H0_prime(H0_prime), .nPA8(PPU_ADR[8]),
    .nPA9(PPU_ADR[9]), .nPA10(PPU_ADR[10]), .nPA11(PPU_ADR[11]), .nPA12(PPU_ADR[12]), .nPA13(PPU_ADR[13]),
    .TSTEP(vram_bus_control_1_tstep), .PD_RB(vram_bus_control_1_pd_rb), .DB_PAR(DB_PAR),
    .nALE(vram_bus_control_1_nale), .RD(nRD), .WR(nWR), .XRB(vram_bus_control_1_xrb), .TH_MUX(TH_MUX));
  not not_15 (PA5, PPU_ADR[5]);
  not not_16 (PA4, PPU_ADR[4]);
  not not_17 (PA2, PPU_ADR[2]);
  not not_18 (PA3, PPU_ADR[3]);
  not not_19 (PA1, PPU_ADR[1]);
  Counter counter_1 (.count(1'b1), .clk(oam_eval_1_test), .clr(button_2_out));  // open: load, D, Q, carry
  Button button_2 (.out(button_2_out));
  not not_20 (PA0, PPU_ADR[0]);
  not not_21 (ALE, vram_bus_control_1_nale);
  not not_22 (not_22_out, oam_buf_control_1_nwe);
  assign controlled_buffer_1_out = not_23_out ? oam_control_ntsc_1_noam3[7:0] : 8'bz;  // Controlled_Buffer controlled_buffer_1
  not not_23 (not_23_out, oam_control_ntsc_1_noam3[8]);
  Demultiplexer #(.width(8), .enable("false")) demultiplexer_1 (
    .out0(demultiplexer_1_out0), .out1(demultiplexer_1_out1), .in(oam_buffer_1_ram_write),
    .sel(oam_control_ntsc_1_noam3[8]));
  assign controlled_buffer_2_out = oam_control_ntsc_1_noam3[8] ? oam_control_ntsc_1_noam3[7:3] : 5'bz;  // Controlled_Buffer controlled_buffer_2
  EXT_IO ext_io_1 (
    .PCLK(PCLK), .EXT0_OUT(mux_1_ext0_out[0]), .EXT0_IN(mux_1_ext0_out[1]), .EXT1_OUT(mux_1_ext0_out[2]),
    .EXT1_IN(mux_1_ext0_out[3]), .EXT2_OUT(mux_1_ext0_out[4]), .EXT2_IN(mux_1_ext0_out[5]),
    .EXT3_OUT(mux_1_ext0_out[6]), .EXT3_IN(mux_1_ext0_out[7]), .nSLAVE(control_regs_ntsc_1_nslave),
    .EXT0_2(EXT0_2), .EXT0(EXT0), .EXT1_2(EXT1_2), .EXT1(EXT1), .EXT2_2(EXT2_2), .EXT2(EXT2),
    .EXT3_2(EXT3_2), .EXT3(EXT3));
  OAM_BUF_CONTROL oam_buf_control_1 (
    .PCLK(PCLK), .BLNK(BLNK), .SPR_OV(oam_control_ntsc_1_spr_ov), .nVIS(nVIS),
    .OAMCTR2(oam_control_ntsc_1_oamctr2), .H0_prime_prime(H0_prime_prime), .nW4(register_select_1_nw4),
    .nDBE(nDBE), .OB_OAM(oam_buf_control_1_ob_oam), .nWE(oam_buf_control_1_nwe),
    .OFETCH(oam_buf_control_1_ofetch));
  Hex_Digit_Display hex_digit_display_3 (.value({3'b000, oam_control_ntsc_1_noam3[8]}));  // open: dp
  Hex_Digit_Display hex_digit_display_4 (.value(oam_control_ntsc_1_noam3[7:4]));  // open: dp
  not not_24 (not_24_out, oam_control_ntsc_1_noam3[8]);
  WRITE__2007 write__2007_1 (
    .PCLK(PCLK), .DB_PAR(DB_PAR), .D0(cpu_data_io_1_cpu_ppu[0]), .D1(cpu_data_io_1_cpu_ppu[1]),
    .D2(cpu_data_io_1_cpu_ppu[2]), .D3(cpu_data_io_1_cpu_ppu[3]), .D4(cpu_data_io_1_cpu_ppu[4]),
    .D5(cpu_data_io_1_cpu_ppu[5]), .D6(cpu_data_io_1_cpu_ppu[6]), .D7(cpu_data_io_1_cpu_ppu[7]), .PD0(PD0_W),
    .PD1(PD1_W), .PD2(PD2_W), .PD3(PD3_W), .PD4(PD4_W), .PD5(PD5_W), .PD6(PD6_W), .PD7(PD7_W));
  OAM_BUFFER oam_buffer_1 (
    .PCLK(PCLK), .nR4(register_select_1_nr4), .OAM___DB({R2DB7, R2DB6, R2DB5, color_io_1_db0_2}),
    .I_OAM2(I_OAM2), .OB_bit_out(oam_buffer_1_ob_bit_out), .RAM_read(multiplexer_1_out),
    .OB_OAM(oam_buf_control_1_ob_oam), .DB___OAM(cpu_data_io_1_cpu_ppu), .BLNK(BLNK),
    .nWE(oam_buf_control_1_nwe), .RAM_write(oam_buffer_1_ram_write));
  Hex_Digit_Display hex_digit_display_5 (.value(oam_control_ntsc_1_noam3[3:0]));  // open: dp
  not not_25 (not_25_out, not_22_out);
  not not_26 (not_26_out, not_22_out);
  RAM #(.bus("separate")) ram_2 (
    .addr(controlled_buffer_1_out), .din(demultiplexer_1_out0), .data(ram_2_data), .str(not_22_out),
    .sel(not_24_out), .clk(PCLK[0]), .ld(not_25_out));  // open: clr
  RAM #(.addrWidth(5), .bus("separate")) ram_3 (
    .addr(controlled_buffer_2_out), .din(demultiplexer_1_out1), .data(ram_3_data), .str(not_22_out),
    .sel(oam_control_ntsc_1_noam3[8]), .clk(PCLK[0]), .ld(not_26_out));  // open: clr
  PICTURE_ADDRESS_GEN picture_address_gen_1 (
    .PCLK(PCLK), .SC_CNT(control_unit_ntsc_1_sc_cnt), .RESCL(RESCL), .E_EV(control_unit_ntsc_1_e_ev),
    .TSTEP(vram_bus_control_1_tstep), .F_TB(control_unit_ntsc_1_f_tb), .H0_prime_prime(H0_prime_prime),
    .BLNK(BLNK), .l1_32(control_regs_ntsc_1_i1_32), .PD0(PPU_DATA[0]), .PD1(PPU_DATA[1]), .PD2(PPU_DATA[2]),
    .PD3(PPU_DATA[3]), .PD4(PPU_DATA[4]), .PD5(PPU_DATA[5]), .PD6(PPU_DATA[6]), .PD7(PPU_DATA[7]),
    .OB0(oam_buffer_1_ob_bit_out[0]), .OB1(oam_buffer_1_ob_bit_out[1]), .OB2(oam_buffer_1_ob_bit_out[2]),
    .OB3(oam_buffer_1_ob_bit_out[3]), .OB4(oam_buffer_1_ob_bit_out[4]), .OB5(oam_buffer_1_ob_bit_out[5]),
    .OB6(oam_buffer_1_ob_bit_out[6]), .OB7(oam_buffer_1_ob_bit_out[7]), .OV0(oam_eval_1_ov0[0]),
    .OV1(oam_eval_1_ov0[1]), .OV2(oam_eval_1_ov0[2]), .OV3(oam_eval_1_ov0[3]),
    .DB0(cpu_data_io_1_cpu_ppu[0]), .DB1(cpu_data_io_1_cpu_ppu[1]), .DB2(cpu_data_io_1_cpu_ppu[2]),
    .DB3(cpu_data_io_1_cpu_ppu[3]), .DB4(cpu_data_io_1_cpu_ppu[4]), .DB5(cpu_data_io_1_cpu_ppu[5]),
    .DB6(cpu_data_io_1_cpu_ppu[6]), .DB7(cpu_data_io_1_cpu_ppu[7]), .nW0(register_select_1_nw0),
    .nW5_2(register_select_1_nw5_2), .nW6_1(register_select_1_nw6_1), .nW5_1(register_select_1_nw5_1),
    .nW6_2(register_select_1_nw6_2), .nDBE(nDBE), .RC(RC), .nPA0(PPU_ADR[0]), .nPA1(PPU_ADR[1]),
    .nPA2(PPU_ADR[2]), .nPA3(PPU_ADR[3]), .nPA4(PPU_ADR[4]), .nPA5(PPU_ADR[5]), .nPA6(PPU_ADR[6]),
    .nPA7(PPU_ADR[7]), .nPA8(PPU_ADR[8]), .nPA9(PPU_ADR[9]), .nPA10(PPU_ADR[10]), .nPA11(PPU_ADR[11]),
    .nPA12(PPU_ADR[12]), .FH0(picture_address_gen_1_fh0[0]), .nPA13(PPU_ADR[13]),
    .FH1(picture_address_gen_1_fh0[1]), .FH2(picture_address_gen_1_fh0[2]), .THO0(TH[0]), .THO1(TH[1]),
    .THO2(TH[2]), .THO3(TH[3]), .THO4(TH[4]), .TVO1(picture_address_gen_1_tvo1),
    .F_AT(control_unit_ntsc_1_f_at), .nF_NT(control_unit_ntsc_1_nf_nt), .PAR_O(PAR_O),
    .nSH2(select_2_3_5_7_pixel_1_nsh2[0]), .O8_16(control_regs_ntsc_1_o8_16),
    .OBSEL(control_regs_ntsc_1_obsel), .BGSEL(control_regs_ntsc_1_bgsel), .nH2_prime(nH2_prime),
    .nH1_prime(nH1_prime), .DB_PAR(1'b0));
  BG_COLOR bg_color_1 (
    .PCLK(PCLK), .CLPB(control_regs_ntsc_1_clpb), .FH0(picture_address_gen_1_fh0[0]),
    .FH1(picture_address_gen_1_fh0[1]), .FH2(picture_address_gen_1_fh0[2]), .PD0(PPU_DATA[0]),
    .PD1(PPU_DATA[1]), .PD2(PPU_DATA[2]), .PD3(PPU_DATA[3]), .PD4(PPU_DATA[4]), .PD5(PPU_DATA[5]),
    .PD6(PPU_DATA[6]), .PD7(PPU_DATA[7]), .THO1(TH[0]), .TVO1(picture_address_gen_1_tvo1),
    .F_AT(control_unit_ntsc_1_f_at), .H0_prime_prime(H0_prime_prime), .F_TA(control_unit_ntsc_1_f_ta),
    .F_TB(control_unit_ntsc_1_f_tb), .nFO(control_unit_ntsc_1_nfo), .BGC0(bg_color_1_bgc0[0]),
    .BGC1(bg_color_1_bgc0[1]), .BGC2(bg_color_1_bgc0[2]), .BGC3(bg_color_1_bgc0[3]));
  Hex_Digit_Display hex_digit_display_6 (.value(multiplexer_1_out[7:4]));  // open: dp
  Hex_Digit_Display hex_digit_display_7 (.value(multiplexer_1_out[3:0]));  // open: dp
  Multiplexer #(.width(8), .enable("false")) multiplexer_1 (
    .in0(ram_2_data), .in1(ram_3_data), .out(multiplexer_1_out), .sel(oam_control_ntsc_1_noam3[8]));

  // Other names for the same wires on the sheet: Hnn_BUS[0] = H0_prime_prime;
  //   PPU_DATA_W[7:0] = {PD7_W, PD6_W, PD5_W, PD4_W, PD3_W, PD2_W, PD1_W, PD0_W}

  // Notes on the sheet:
  //   Manual cleaning
  //   2C02 PPU
  //   CHR  ROM
  //   NT  RAM
  //   contents of rom_1 (hex, n*v repeats v):
  //   1f 3f 2b 2b 3f 1f 0 33 0 0 2b 2a 0 0 f 34 6*fd 0 fd 10 4*0 40 fd 60 1f 3f 2b 2b 3f 1f 0 11 0 0 2b 2a
  //   0 0 f e 5*fd 0 0 fd 10 4*0 fd fd 20 0 1f 3f 2b 2b 3f 1f 4*0 2b 2a 0 0 7 10 5*fd 0 fd 10 20 4*0 fd 20
  //   7 f d d f 7 0 8 0 0 5 5 0 0 3 7 4*fd 0 3c 0 0 fd fd 0 0 fd fd 7 f d d f 7 0 c 0 0 5 5 0 0 3 3 4*fd 0
  //   30 0 0 fd fd 0 0 fd fd 7 f d d f 7 0 3c 0 0 5 5 0 0 3 33 4*fd 0 10 0 0 fd fd 0 0 fd fd 7 e f f f 7 0
  //   8 0 1 4*0 3 7 fd 70 4*fd 0 1c 0 fd 40 0 0 0 fd fd 7 e f f f 7 0 8 0 1 4*0 3 7 fd 70 4*fd 0 10 0 fd
  //   40 0 0 0 fd fd 3f f 20 38 3c 38 0 0 30 0 27 37 33 36 0 0 fd 18 0 fd fd fd 30 60 78 fd fd 60 0 18 30
  //   60 10 30 31 1 6 6 e 1 f 3f 3f f 1 6 e 1 8*fd 0 fd fd fd 0 0 fd fd 0 30 38 8 3 3 1 3 f 3f 37 7 0 0 1
  //   3 fd 70 38 18 18 fd fd fd 0 4*fd c fd fd 18 18 30 30 6 6 6 0 7 7 37 37 1 6 6 0 1c 0 0 5*60 5*fd 0 60
  //   60 18 38 30 0 4*6 7 37 37 7 1 0 6 6 18 1c c 0 4*60 5*fd 0 60 60 38 0 0 5*6 37 7 7 1 1 0 6 6 18 18 c
  //   c 60 60 60 0 4*fd 60 60 0 19 19 37 30 6 6 6 0 7 7 30 37 1 6 6 0 fd fd fd 0 4*60 fd fd 0 fd fd 0 60
  //   60 18 39 37 0 4*6 7 37 30 7 1 0 6 6 18 fd fd 0 4*60 fd fd c fd fd 0 60 60 7 e f f f 7 0 38 0 1 4*0 3
  //   37 fd 70 4*fd 0 10 0 fd 40 0 0 0 fd fd f 1f 1b 1f 1f f 30 38 6*0 33 37 6*fd c 3c 6*0 fd fd f 15 1b
  //   15 1f f 30 30 6*0 37 3f fd 58 fd 58 fd fd c c 6*0 fd fd f 15 1b 15 1f 8 30 34 5*0 7 3f 3b fd 58 fd
  //   58 fd 10 c c 5*0 fd 3c f 15 1b 15 18 0 30 32 4*0 7 f 3f 38 fd 58 fd 58 8 8 c 2c 4*0 fd fd 1c 1c 0 f
  //   15 18 12 4 30 30 0 0 0 7 c 18 38 38 0 fd 58 18 8 0 c 3c 0 0 0 fd fd 38 c c 0 6 8 0 0 0 30 30 0 1 7
  //   62 40 0 30 78 0 18 8 0 0 c 1c 0 20 40 26 2 0 c c 6*0 30 30 6*0 30 38 6*0 c c 6*0 c 1c 38 1 7 0 4*6
  //   37 7 0 7 1 0 6 6 18 fd fd c 60 60 60 0 fd fd c fd 60 60 6*0 8 1c 18 f 1f 1f 1f f 7 1b 18 5*0 10 38
  //   18 7*fd 18 0 6 2 0 0 0 18 18 19 38 3c 3d 1f f 1f 1b 0 fd 0 40 fd 0 18 18 78 7c fd 3c 78 fd fd fd 1 8
  //   4 4 1 4 18 18 72 70 78 78 32 1b 1f 1f 0 0 40 0 40 0 18 18 7e 7e fd 3e c 78 fd fd 0 8 4 0 0 1 18 18
  //   10 30 38 30 30 1a 1f 1f 40 20 0 0 fd 40 18 18 38 1c 1c 1c c fd fd fd 0 0 10 0 0 4 19 18 4*60 0 18 18
  //   1b 40 10 0 0 0 fd 18 18 38 c c c 0 10 fd fd 20 40 0 0 20 0 19 18 fd fd 40 0 0 60 58 1b 0 0 0 8 0 0
  //   fd 18 9 4 4 5 1 2 18 fd 6*0 18 18 6*0 18 18 6*0 18 18 6*0 18 18 f 1f 1 1 1 0 0 3 f 1f f b 1b f 7 30
  //   6*fd 0 fd fd fd 30 30 fd fd fd 40 f 1f 1 1 1 0 0 3 f 1f f b 1b f 7 0 6*fd 0 fd fd fd 30 30 4*fd 0 f
  //   1f 1 1 1 0 0 0 f 1f f b 1b f 7 0 6*fd 0 0 fd fd 30 30 fd fd fd 0 0 0 77 55 55 55 77 0 0 0 77 55 55
  //   55 77 0 0 0 70 50 50 50 70 0 0 0 70 50 50 50 70 0 c 12 21 2e 2e 1e 1e 0 0 c 1e 1f 1f b f 0 30 48 fd
  //   74 74 78 78 0 0 30 78 4*fd 4*0 e e 6 2 0 0 4 e f d 7 3 4*0 70 70 60 40 0 0 20 70 fd fd fd 4*0 6 6 2
  //   4*0 4 6 5 3 1 4*0 60 60 40 4*0 20 60 fd fd fd 4*0 c 4 6*0 c 6 6*0 30 20 6*0 30 60 0 0 f 1f 27 3f 3f
  //   3c 0 0 30 0 4 f f c 0 0 6*fd 30 60 48 58 4*fd 0 0 7 f b e 6 6 e 1 1 31 3f f 7 0 0 0 fd fd 60 60 60
  //   fd fd fd 0 5*fd 0 0 3 7 f e 7 3 1 3 0 31 33 7 7 3 0 0 9*fd 0 18 fd fd 34*0 11 13 23 20 21 12 c 0 e c
  //   1c 1f 1e c 0 0 fd fd fd 4 fd 48 30 0 70 30 38 fd 78 30 0 0 1 3 6*0 2 4 f e c 0 0 0 fd fd 6*0 40 20
  //   fd 70 30 0 0 0 1 7*0 2 7 6 4 4*0 fd 7*0 40 fd 60 20 13*0 6 c 14*0 60 30 5*0 7 1c 30 60 40 46 46 46 0
  //   3 f 1f 3f 3f 3d 3d fd 38 c 6 2 62 62 62 0 7*fd f 38 20 60 40 46 46 46 0 7 1f 1f 3f 3f 3d 3d fd 1c 4
  //   6 2 62 62 62 0 7*fd f 38 60 5*fd 0 7 1f 3f 7f 7d 7d 3f fd 1c 6 3 61 61 61 3 0 7*fd 7 1c 30 6a 4*4e 0
  //   3 f 15 3f 3b 3b 3f fd 38 c 56 4*72 0 6*fd 1 3 3 7 1d 38 40 fd 0 1 1 3 7 1f 3f 7f 4*fd 38 fd 2 61 0
  //   7*fd 0 1 3 7 1d 38 40 fd 0 0 1 3 7 1f 3f 7f fd 10 fd 38 fd 2 61 0 7*fd 1 3 3 7 1d 38 40 fd 0 1 1 3 7
  //   1f 3f 7d 4*fd 38 fd 2 61 0 7*fd 1 3 3 7 1d 30 4e fd 0 1 1 3 7 1f 3f 7b 4*fd 38 fd 72 71 0 7*fd 40 60
  //   31 18 c 6 3 3 3f 1f e 7 3 1 1 0 2 6 fd 18 30 60 4*fd 70 4*fd 0 60 20 31 18 e 3 3 0 1f 1f e 7 1 1 0 0
  //   6 4 fd 18 70 fd fd 0 fd fd 70 fd fd fd 0 0 40 61 38 e 3 3 0 0 3f 1e 7 1 1 0 0 0 2 fd 1c 70 fd fd 0 0
  //   fd 78 fd fd fd 0 0 0 40 63 33 19 c 6 3 3 3f 1c c 6 3 1 1 0 2 fd 18 30 60 fd fd fd 38 30 60 fd fd fd
  //   0 fd fd fd 41 20 1f 22 3e 7d 7d 7f 3e 1f 0 1c 0 61 61 1 fd 3c fd 7c 0 fd fd fd 7c fd 38 0 0 fd fd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
  //   contents of rom_2 (hex, n*v repeats v):
  //   65*3a 54 49 4d 45 3a 31 36 39 9*3a 30 30 4*3a 4c 45 46 54 3a 32 34*3a 64 65 64 65 64 65 64 65 64 65
  //   64 65 64 65 64 65 64 65 64 65 64 65 64 65 64 65 64 65 64 65 64 65 66 67 66 67 66 67 66 67 66 67 66
  //   67 66 67 66 67 66 67 66 67 66 67 66 67 66 67 66 67 66 67 66 67 64 65 16*5f 68 69 68 69 68 69 68 69
  //   68 69 5f 5f 68 69 66 67 16*5f 6a 6b 6a 6b 6a 6b 6a 6b 6a 6b 5f 5f 6a 6b 64 65 5f 5f 64 65 5f 5f 64
  //   65 5f 5f 64 65 5f 5f 64 65 5f 5f 64 65 5f 5f 64 65 5f 5f 64 65 68 69 66 67 5f 5f 66 67 5f 5f 66 67
  //   5f 5f 66 67 5f 5f 66 67 5f 5f 66 67 5f 5f 66 67 5f 5f 66 67 6a 6b 64 65 16*5f 68 69 5f 5f 68 69 4*5f
  //   68 69 5f 5f 66 67 16*5f 6a 6b 5f 5f 6a 6b 4*5f 6a 6b 5f 5f 64 65 5f 5f 64 65 5f 5f 64 65 5f 5f 64 65
  //   5f 5f 64 65 5f 5f 64 65 5f 5f 64 65 5f 5f 64 65 5f 5f 66 67 5f 5f 66 67 5f 5f 66 67 5f 5f 66 67 5f
  //   5f 66 67 5f 5f 66 67 5f 5f 66 67 5f 5f 66 67 5f 5f 64 65 30*5f 66 67 30*5f 64 65 5f 5f 64 65 5f 5f
  //   64 65 5f 5f 64 65 5f 5f 64 65 68 69 64 65 5f 5f 64 65 5f 5f 64 65 5f 5f 66 67 5f 5f 66 67 5f 5f 66
  //   67 5f 5f 66 67 5f 5f 66 67 6a 6b 66 67 5f 5f 66 67 5f 5f 66 67 5f 5f 64 65 30*5f 66 67 30*5f 64 65
  //   5f 5f 64 65 5f 5f 64 65 5f 5f 64 65 5f 5f 64 65 5f 5f 64 65 5f 5f 64 65 5f 5f 64 65 5f 5f 66 67 5f
  //   5f 66 67 5f 5f 66 67 5f 5f 66 67 5f 5f 66 67 5f 5f 66 67 5f 5f 66 67 5f 5f 66 67 5f 5f 64 65 14*5f
  //   68 69 14*5f 66 67 14*5f 6a 6b 14*5f 64 65 5f 5f 64 65 5f 5f 64 65 5f 5f 64 65 5f 5f 64 65 68 69 64
  //   65 68 69 64 65 5f 5f 64 65 68 69 66 67 5f 5f 66 67 5f 5f 66 67 5f 5f 66 67 5f 5f 66 67 6a 6b 66 67
  //   6a 6b 66 67 5f 5f 66 67 6a 6b 64 65 30*5f 66 67 30*5f 64 65 64 65 64 65 64 65 64 65 64 65 64 65 64
  //   65 64 65 64 65 64 65 64 65 64 65 64 65 64 65 64 65 66 67 66 67 66 67 66 67 66 67 66 67 66 67 66 67
  //   66 67 66 67 66 67 66 67 66 67 66 67 66 67 66 67 64*0 128*fd 64 65 64 65 64 65 64 65 64 65 64 65 64
  //   65 64 65 64 65 64 65 64 65 64 65 64 65 64 65 64 65 64 65 66 67 66 67 66 67 66 67 66 67 66 67 66 67
  //   66 67 66 67 66 67 66 67 66 67 66 67 66 67 66 67 66 67 68 69 22*5f 68 69 5f 5f 64 65 64 65 6a 6b
  //   22*5f 6a 6b 5f 5f 66 67 66 67 64 65 5f 5f 64 65 5f 5f 64 65 5f 5f 64 65 5f 5f 64 65 5f 5f 64 65 5f
  //   5f 64 65 5f 5f 64 65 64 65 66 67 5f 5f 66 67 5f 5f 66 67 5f 5f 66 67 5f 5f 66 67 5f 5f 66 67 5f 5f
  //   66 67 5f 5f 66 67 66 67 4*5f 68 69 68 69 68 69 18*5f 64 65 64 65 4*5f 6a 6b 6a 6b 6a 6b 18*5f 66 67
  //   66 67 64 65 5f 5f 64 65 5f 5f 64 65 5f 5f 64 65 68 69 64 65 5f 5f 64 65 5f 5f 64 65 5f 5f 64 65 64
  //   65 66 67 5f 5f 66 67 5f 5f 66 67 5f 5f 66 67 6a 6b 66 67 5f 5f 66 67 5f 5f 66 67 5f 5f 66 67 66 67
  //   14*5f 68 69 68 69 68 69 5f 5f 68 69 4*5f 64 65 64 65 14*5f 6a 6b 6a 6b 6a 6b 5f 5f 6a 6b 4*5f 66 67
  //   66 67 64 65 5f 5f 64 65 5f 5f 64 65 5f 5f 64 65 5f 5f 64 65 68 69 64 65 68 69 64 65 5f 5f 64 65 64
  //   65 66 67 5f 5f 66 67 5f 5f 66 67 5f 5f 66 67 5f 5f 66 67 6a 6b 66 67 6a 6b 66 67 5f 5f 66 67 66 67
  //   14*5f fd fd 12*5f 64 65 64 65 14*5f fd fd 12*5f 66 67 66 67 64 65 5f 5f 64 65 5f 5f 64 65 5f 5f 64
  //   65 68 69 64 65 68 69 64 65 68 69 64 65 5f 5f 64 65 64 65 66 67 5f 5f 66 67 5f 5f 66 67 5f 5f 66 67
  //   6a 6b 66 67 6a 6b 66 67 6a 6b 66 67 5f 5f 66 67 66 67 14*5f 68 69 68 69 5f 5f 68 69 68 69 68 69 5f
  //   5f 64 65 64 65 14*5f 6a 6b 6a 6b 5f 5f 6a 6b 6a 6b 6a 6b 5f 5f 66 67 66 67 64 65 5f 5f 64 65 5f 5f
  //   64 65 5f 5f 64 65 5f 5f 64 65 68 69 64 65 5f 5f 64 65 68 69 64 65 64 65 66 67 5f 5f 66 67 5f 5f 66
  //   67 5f 5f 66 67 5f 5f 66 67 6a 6b 66 67 5f 5f 66 67 6a 6b 66 67 66 67 28*5f 64 65 64 65 28*5f 66 67
  //   66 67 64 65 64 65 64 65 64 65 64 65 64 65 64 65 64 65 64 65 64 65 64 65 64 65 64 65 64 65 64 65 64
  //   65 66 67 66 67 66 67 66 67 66 67 66 67 66 67 66 67 66 67 66 67 66 67 66 67 66 67 66 67 66 67 66 67
  //   8*fd 48*0 8*fd
  //   CPU INTERFACE
  //   Logisim doesn't support bidirectional pads and wires
  //   So we have to add workaround by separate I/O wires
  //   VRAM INTERFACE
  //   EXT INTERFACE
  //   Logisim doesn't support bidirectional pads and wires
  //   So we have to add workaround by separate I/O wires
endmodule

// 2C04-0003 RGB
module _2C04_0003_RGB (
  input  nDBE,
  input  RS2,
  input  RS1,
  input  RS0,
  input  R_W,
  input  D0,
  input  D1,
  input  D2,
  input  D3,
  input  D4,
  input  D5,
  input  D6,
  input  D7,
  input  AGND,
  input  CLK,
  input  nRES,
  input  PD7,
  input  PD6,
  input  PD5,
  input  PD4,
  input  PD3,
  input  PD2,
  input  PD1,
  input  PD0,
  output D0_2,
  output D1_2,
  output D2_2,
  output D3_2,
  output D4_2,
  output D5_2,
  output D6_2,
  output D7_2,
  output SYNC,
  output [7:0] BLUE,
  output [7:0] GREEN,
  output [7:0] RED,
  output nINT,
  output PD7_W,
  output PD6_W,
  output PD5_W,
  output PD4_W,
  output PD3_W,
  output PD2_W,
  output PD1_W,
  output PD0_W,
  output nWR,
  output nRD,
  output PA13,
  output PA12,
  output PA11,
  output PA10,
  output PA9,
  output PA8,
  output PA7,
  output PA6,
  output PA5,
  output PA4,
  output PA3,
  output PA2,
  output PA1,
  output PA0,
  output ALE
);

  wire BLNK, button_1_out, color_control_rgb_1_color_en, color_control_rgb_1_ndb_cb, color_io_1_nout0,
       color_io_1_nout1, color_io_1_nout2, color_io_1_nout3, color_io_1_nout4, color_io_1_nout5,
       control_regs_ntsc_1_bgclip, control_regs_ntsc_1_bgsel, control_regs_ntsc_1_black,
       control_regs_ntsc_1_bw, control_regs_ntsc_1_clpb, control_regs_ntsc_1_i1_32,
       control_regs_ntsc_1_nclpo, control_regs_ntsc_1_nslave, control_regs_ntsc_1_o8_16,
       control_regs_ntsc_1_obclip, control_regs_ntsc_1_obsel, control_regs_ntsc_1_vbl,
       control_unit_ntsc_1__0_hpos, control_unit_ntsc_1_burst, control_unit_ntsc_1_clip_b,
       control_unit_ntsc_1_clip_o, control_unit_ntsc_1_e_ev, control_unit_ntsc_1_e_out,
       control_unit_ntsc_1_eval, control_unit_ntsc_1_f_at, control_unit_ntsc_1_f_ta,
       control_unit_ntsc_1_f_tb, control_unit_ntsc_1_hc, control_unit_ntsc_1_nf_nt, control_unit_ntsc_1_nfo,
       control_unit_ntsc_1_npicture, control_unit_ntsc_1_nvset, control_unit_ntsc_1_s_ev,
       control_unit_ntsc_1_sc_cnt, control_unit_ntsc_1_sync, control_unit_ntsc_1_vb, control_unit_ntsc_1_vc,
       control_unit_ntsc_1_vin, DB_PAR, H0_prime, H0_prime_prime, h_counter_1_h0, h_counter_1_h1,
       h_counter_1_h2, h_counter_1_h3, h_counter_1_h4, h_counter_1_h5, h_counter_1_h6, h_counter_1_h7,
       h_counter_1_h8, hv_select_ntsc_1_hpla_0, hv_select_ntsc_1_hpla_1, hv_select_ntsc_1_hpla_2,
       hv_select_ntsc_1_hpla_3, hv_select_ntsc_1_hpla_4, hv_select_ntsc_1_hpla_5, hv_select_ntsc_1_hpla_6,
       hv_select_ntsc_1_hpla_7, hv_select_ntsc_1_hpla_8, hv_select_ntsc_1_hpla_9, hv_select_ntsc_1_hpla_10,
       hv_select_ntsc_1_hpla_11, hv_select_ntsc_1_hpla_12, hv_select_ntsc_1_hpla_13,
       hv_select_ntsc_1_hpla_14, hv_select_ntsc_1_hpla_15, hv_select_ntsc_1_hpla_16,
       hv_select_ntsc_1_hpla_17, hv_select_ntsc_1_hpla_18, hv_select_ntsc_1_hpla_19,
       hv_select_ntsc_1_hpla_20, hv_select_ntsc_1_hpla_21, hv_select_ntsc_1_hpla_22,
       hv_select_ntsc_1_hpla_23, hv_select_ntsc_1_vpla_0, hv_select_ntsc_1_vpla_1, hv_select_ntsc_1_vpla_2,
       hv_select_ntsc_1_vpla_3, hv_select_ntsc_1_vpla_4, hv_select_ntsc_1_vpla_5, hv_select_ntsc_1_vpla_6,
       hv_select_ntsc_1_vpla_7, hv_select_ntsc_1_vpla_8, I_OAM2, interrupt_control_1_int, mux_1_ext0_out,
       mux_1_ext1_out, mux_1_ext2_out, mux_1_ext3_out, nH1_prime, nH2_prime, not_1_out, not_3_out,
       not_19_out, not_20_out, not_21_out, not_22_out, not_23_out, nR2, nR7, nVIS, nW7,
       oam_buf_control_rgb_1_nwe, oam_buf_control_rgb_1_ob_oam, oam_buf_control_rgb_1_ofetch,
       oam_control_ntsc_1_oamctr2, oam_control_ntsc_1_spr_ov, oam_eval_1__0_fifo, oam_eval_1_i2sev,
       oam_eval_1_omfg, oam_fifo_1_nspr0hit, or_1_out, PAR_O, picture_address_gen_1_tvo1,
       pixel_clock_ntsc_1_npclk, pixel_clock_ntsc_1_pclk_2, R2DB5, R2DB6, R2DB7, RC, register_select_1_nw0,
       register_select_1_nw1, register_select_1_nw3, register_select_1_nw4, register_select_1_nw5_1,
       register_select_1_nw5_2, register_select_1_nw6_1, register_select_1_nw6_2, RES, RESCL,
       rw_control_1_nrd, rw_control_1_nwr, TH_MUX, undriven, undriven_2, v_counter_1_v0, v_counter_1_v1,
       v_counter_1_v2, v_counter_1_v3, v_counter_1_v4, v_counter_1_v5, v_counter_1_v6, v_counter_1_v7,
       v_counter_1_v8, vram_bus_control_1_nale, vram_bus_control_1_pd_rb, vram_bus_control_1_tstep,
       vram_bus_control_1_xrb;
  wire [1:0] PCLK;
  wire [2:0] control_regs_ntsc_1_ntr, picture_address_gen_1_fh0;
  wire [3:0] bg_color_1_bgc0, oam_eval_1_ov0, select_2_3_5_7_pixel_1_nsh2;
  wire [4:0] controlled_buffer_2_out, mux_1_pal0, oam_fifo_1_nzcol0, read__2007_1_db0, TH;
  wire [5:0] color_io_1_cb_ram0, hv_select_ntsc_1_hnn, ram_1_data;
  wire [5:1] Hnn_BUS;
  wire [7:0] controlled_buffer_1_out, cpu_data_io_1_cpu_ppu, demultiplexer_1_out0, demultiplexer_1_out1,
       h_inversion_1_nt0, hv_select_ntsc_1_vpos, multiplexer_1_out, oam_buffer_1_ob_bit_out,
       oam_buffer_1_ram_write, ram_2_data, ram_3_data;
  wire [8:0] oam_control_ntsc_1_noam0;
  wire [13:0] PPU_ADR;

  not not_1 (not_1_out, undriven);
  Clock clock_1 ();  // open: out
  Button button_1 (.out(button_1_out));
  not not_2 (nINT, interrupt_control_1_int);
  RESET_FF reset_ff_1 (.nRES(nRES), .RESCL(or_1_out), .RES(RES), .RC(RC));
  or or_1 (or_1_out, RESCL, button_1_out);
  COLOR_IO color_io_1 (
    .PCLK(PCLK), .nDB_CB(color_control_rgb_1_ndb_cb), .nCB_DB(undriven_2),
    .nBW(color_control_rgb_1_color_en), .RAM_CB0(ram_1_data[0]), .DB0(cpu_data_io_1_cpu_ppu[0]),
    .RAM_CB1(ram_1_data[1]), .DB1(cpu_data_io_1_cpu_ppu[1]), .RAM_CB2(ram_1_data[2]),
    .DB2(cpu_data_io_1_cpu_ppu[2]), .RAM_CB3(ram_1_data[3]), .DB3(cpu_data_io_1_cpu_ppu[3]),
    .RAM_CB4(ram_1_data[4]), .DB4(cpu_data_io_1_cpu_ppu[4]), .RAM_CB5(ram_1_data[5]),
    .DB5(cpu_data_io_1_cpu_ppu[5]), .nout0(color_io_1_nout0), .CB_RAM0(color_io_1_cb_ram0[0]),
    .nout1(color_io_1_nout1), .CB_RAM1(color_io_1_cb_ram0[1]), .nout2(color_io_1_nout2),
    .CB_RAM2(color_io_1_cb_ram0[2]), .nout3(color_io_1_nout3), .CB_RAM3(color_io_1_cb_ram0[3]),
    .nout4(color_io_1_nout4), .CB_RAM4(color_io_1_cb_ram0[4]), .nout5(color_io_1_nout5),
    .CB_RAM5(color_io_1_cb_ram0[5]));  // open: DB0_2, DB1_2, DB2_2, DB3_2, DB4_2, DB5_2
  INTERRUPT_CONTROL interrupt_control_1 (
    .VBL_EN(control_regs_ntsc_1_vbl), .VSET(control_unit_ntsc_1_nvset), .RESCL(RESCL), .nDBE(nDBE),
    .nR2(nR2), .INT(interrupt_control_1_int), .DB7(R2DB7), .PCLK(PCLK));
  VIDEO_OUT_RGB video_out_rgb_1 (
    .PCLK(PCLK), .nPICTURE(control_unit_ntsc_1_npicture), .nTR(control_regs_ntsc_1_ntr[0]),
    .nTG(control_regs_ntsc_1_ntr[1]), .nTB(control_regs_ntsc_1_ntr[2]), .nCC0(color_io_1_nout0),
    .nCC1(color_io_1_nout1), .nCC2(color_io_1_nout3), .nCC3(color_io_1_nout2), .nLL0(color_io_1_nout5),
    .nLL1(color_io_1_nout4), .SYNC(control_unit_ntsc_1_sync), .R0(RED[0]), .R1(RED[1]), .R2(RED[2]),
    .R3(RED[3]), .R4(RED[4]), .R5(RED[5]), .R6(RED[6]), .R7(RED[7]), .G0(GREEN[0]), .G1(GREEN[1]),
    .G2(GREEN[2]), .G3(GREEN[3]), .G4(GREEN[4]), .G5(GREEN[5]), .G6(GREEN[6]), .G7(GREEN[7]), .B0(BLUE[0]),
    .B1(BLUE[1]), .B2(BLUE[2]), .B3(BLUE[3]), .B4(BLUE[4]), .B5(BLUE[5]), .B6(BLUE[6]), .B7(BLUE[7]),
    .SYNC_2(SYNC));
  not not_3 (not_3_out, color_control_rgb_1_ndb_cb);
  PIXEL_CLOCK_NTSC pixel_clock_ntsc_1 (
    .nCLK(not_1_out), .RES(RES), .PCLK(PCLK), .nPCLK(pixel_clock_ntsc_1_npclk),
    .PCLK_2(pixel_clock_ntsc_1_pclk_2));
  RAM #(.addrWidth(5), .dataWidth(6), .bus("separate")) ram_1 (
    .addr(mux_1_pal0), .din(color_io_1_cb_ram0), .data(ram_1_data), .str(not_3_out), .sel(1'b1),
    .clk(PCLK[0]), .ld(color_control_rgb_1_ndb_cb));  // open: clr
  CONTROL_UNIT_NTSC control_unit_ntsc_1 (
    .PCLK(PCLK), .Hnn(hv_select_ntsc_1_hnn), .nOBCLIP(control_regs_ntsc_1_bgclip),
    .nBGCLIP(control_regs_ntsc_1_obclip), .HPLA_2(hv_select_ntsc_1_hpla_2), .HPLA_3(hv_select_ntsc_1_hpla_3),
    .HPLA_4(hv_select_ntsc_1_hpla_4), .HPLA_5(hv_select_ntsc_1_hpla_5), .HPLA_6(hv_select_ntsc_1_hpla_6),
    .HPLA_7(hv_select_ntsc_1_hpla_7), .HPLA_8(hv_select_ntsc_1_hpla_8), .HPLA_9(hv_select_ntsc_1_hpla_9),
    .HPLA_10(hv_select_ntsc_1_hpla_10), .HPLA_11(hv_select_ntsc_1_hpla_11),
    .HPLA_16(hv_select_ntsc_1_hpla_16), .HPLA_13(hv_select_ntsc_1_hpla_13),
    .HPLA_12(hv_select_ntsc_1_hpla_12), .HPLA_14(hv_select_ntsc_1_hpla_14),
    .HPLA_15(hv_select_ntsc_1_hpla_15), .HPLA_19(hv_select_ntsc_1_hpla_19),
    .HPLA_20(hv_select_ntsc_1_hpla_20), .HPLA_0(hv_select_ntsc_1_hpla_0), .HPLA_1(hv_select_ntsc_1_hpla_1),
    .HPLA_21(hv_select_ntsc_1_hpla_21), .HPLA_22(hv_select_ntsc_1_hpla_22),
    .HPLA_17(hv_select_ntsc_1_hpla_17), .HPLA_18(hv_select_ntsc_1_hpla_18), .VPLA_1(hv_select_ntsc_1_vpla_1),
    .VPLA_0(hv_select_ntsc_1_vpla_0), .VPLA_3(hv_select_ntsc_1_vpla_3), .VPLA_2(hv_select_ntsc_1_vpla_2),
    .VPLA_4(hv_select_ntsc_1_vpla_4), .VPLA_5(hv_select_ntsc_1_vpla_5), .VPLA_6(hv_select_ntsc_1_vpla_6),
    .VPLA_7(hv_select_ntsc_1_vpla_7), .VPLA_8(hv_select_ntsc_1_vpla_8), .BLACK(control_regs_ntsc_1_black),
    .HPLA_23(hv_select_ntsc_1_hpla_23), .V8(v_counter_1_v8), .RES(RES), .H0_prime_prime(H0_prime_prime),
    .H1_prime_prime(Hnn_BUS[1]), .H2_prime_prime(Hnn_BUS[2]), .H3_prime_prime(Hnn_BUS[3]),
    .H4_prime_prime(Hnn_BUS[4]), .H5_prime_prime(Hnn_BUS[5]), .H0_prime(H0_prime), .nH1_prime(nH1_prime),
    .nH2_prime(nH2_prime), .S_EV(control_unit_ntsc_1_s_ev), .CLIP_O(control_unit_ntsc_1_clip_o),
    .CLIP_B(control_unit_ntsc_1_clip_b), ._0_HPOS(control_unit_ntsc_1__0_hpos),
    .EVAL(control_unit_ntsc_1_eval), .E_EV(control_unit_ntsc_1_e_ev), .I_OAM2(I_OAM2), .PAR_O(PAR_O),
    .nVIS(nVIS), .nF_NT(control_unit_ntsc_1_nf_nt), .F_AT(control_unit_ntsc_1_f_at),
    .F_TA(control_unit_ntsc_1_f_ta), .F_TB(control_unit_ntsc_1_f_tb), .nFO(control_unit_ntsc_1_nfo),
    .SC_CNT(control_unit_ntsc_1_sc_cnt), .SYNC(control_unit_ntsc_1_sync), .BURST(control_unit_ntsc_1_burst),
    .nPICTURE(control_unit_ntsc_1_npicture), .nVSET(control_unit_ntsc_1_nvset), .VB(control_unit_ntsc_1_vb),
    .BLNK(BLNK), .RESCL(RESCL), .VC(control_unit_ntsc_1_vc), .VIN(control_unit_ntsc_1_vin),
    .HC(control_unit_ntsc_1_hc), .E_OUT(control_unit_ntsc_1_e_out), .CFG(1'b0));
  H_COUNTER h_counter_1 (
    .RES(RES), .HC(control_unit_ntsc_1_hc), .PCLK(PCLK), .H0(h_counter_1_h0), .H1(h_counter_1_h1),
    .H2(h_counter_1_h2), .H3(h_counter_1_h3), .H4(h_counter_1_h4), .H5(h_counter_1_h5), .H6(h_counter_1_h6),
    .H7(h_counter_1_h7), .H8(h_counter_1_h8));
  OAM_FIFO oam_fifo_1 (
    .PCLK(PCLK), ._0_HPOS(control_unit_ntsc_1__0_hpos), .H3_prime_prime(Hnn_BUS[3]),
    .H4_prime_prime(Hnn_BUS[4]), .H5_prime_prime(Hnn_BUS[5]), .nSH2(select_2_3_5_7_pixel_1_nsh2[0]),
    .nSH3(select_2_3_5_7_pixel_1_nsh2[1]), .nSH5(select_2_3_5_7_pixel_1_nsh2[2]),
    .nSH7(select_2_3_5_7_pixel_1_nsh2[3]), .nVIS(nVIS), .nCLPO(control_regs_ntsc_1_nclpo),
    .OB0(oam_buffer_1_ob_bit_out[0]), .OB1(oam_buffer_1_ob_bit_out[1]), .OB2(oam_buffer_1_ob_bit_out[2]),
    .OB3(oam_buffer_1_ob_bit_out[3]), .OB4(oam_buffer_1_ob_bit_out[4]), .OB5(oam_buffer_1_ob_bit_out[5]),
    .OB6(oam_buffer_1_ob_bit_out[6]), .OB7(oam_buffer_1_ob_bit_out[7]), .nT0(h_inversion_1_nt0[0]),
    .nT1(h_inversion_1_nt0[1]), .nT2(h_inversion_1_nt0[2]), .nT3(h_inversion_1_nt0[3]),
    .nT4(h_inversion_1_nt0[4]), .nT5(h_inversion_1_nt0[5]), .nT6(h_inversion_1_nt0[6]),
    .nT7(h_inversion_1_nt0[7]), .nSPR0HIT(oam_fifo_1_nspr0hit), .nZCOL0(oam_fifo_1_nzcol0[0]),
    .nZCOL1(oam_fifo_1_nzcol0[1]), .ZCOL2(oam_fifo_1_nzcol0[2]), .ZCOL3(oam_fifo_1_nzcol0[3]),
    .nZPRIO(oam_fifo_1_nzcol0[4]));
  V_COUNTER v_counter_1 (
    .VIN(control_unit_ntsc_1_vin), .PCLK(PCLK), .RES(RES), .VC(control_unit_ntsc_1_vc), .V0(v_counter_1_v0),
    .V1(v_counter_1_v1), .V2(v_counter_1_v2), .V3(v_counter_1_v3), .V4(v_counter_1_v4), .V5(v_counter_1_v5),
    .V6(v_counter_1_v6), .V7(v_counter_1_v7), .V8(v_counter_1_v8));
  HV_SELECT_NTSC hv_select_ntsc_1 (
    .H8(h_counter_1_h8), .H7(h_counter_1_h7), .H6(h_counter_1_h6), .H5(h_counter_1_h5), .H4(h_counter_1_h4),
    .H3(h_counter_1_h3), .H2(h_counter_1_h2), .H1(h_counter_1_h1), .H0(h_counter_1_h0),
    .VB(control_unit_ntsc_1_vb), .BLNK(BLNK), .V8(v_counter_1_v8), .V7(v_counter_1_v7), .V6(v_counter_1_v6),
    .V5(v_counter_1_v5), .V4(v_counter_1_v4), .V3(v_counter_1_v3), .V2(v_counter_1_v2), .V1(v_counter_1_v1),
    .V0(v_counter_1_v0), .VPOS(hv_select_ntsc_1_vpos), .Hnn(hv_select_ntsc_1_hnn),
    .HPLA_0(hv_select_ntsc_1_hpla_0), .VPLA_0(hv_select_ntsc_1_vpla_0), .HPLA_1(hv_select_ntsc_1_hpla_1),
    .VPLA_1(hv_select_ntsc_1_vpla_1), .HPLA_2(hv_select_ntsc_1_hpla_2), .VPLA_2(hv_select_ntsc_1_vpla_2),
    .HPLA_3(hv_select_ntsc_1_hpla_3), .VPLA_3(hv_select_ntsc_1_vpla_3), .HPLA_4(hv_select_ntsc_1_hpla_4),
    .VPLA_4(hv_select_ntsc_1_vpla_4), .HPLA_5(hv_select_ntsc_1_hpla_5), .VPLA_5(hv_select_ntsc_1_vpla_5),
    .HPLA_6(hv_select_ntsc_1_hpla_6), .VPLA_6(hv_select_ntsc_1_vpla_6), .HPLA_7(hv_select_ntsc_1_hpla_7),
    .VPLA_7(hv_select_ntsc_1_vpla_7), .HPLA_8(hv_select_ntsc_1_hpla_8), .VPLA_8(hv_select_ntsc_1_vpla_8),
    .HPLA_9(hv_select_ntsc_1_hpla_9), .HPLA_10(hv_select_ntsc_1_hpla_10), .HPLA_11(hv_select_ntsc_1_hpla_11),
    .HPLA_12(hv_select_ntsc_1_hpla_12), .HPLA_13(hv_select_ntsc_1_hpla_13),
    .HPLA_14(hv_select_ntsc_1_hpla_14), .HPLA_15(hv_select_ntsc_1_hpla_15),
    .HPLA_16(hv_select_ntsc_1_hpla_16), .HPLA_17(hv_select_ntsc_1_hpla_17),
    .HPLA_18(hv_select_ntsc_1_hpla_18), .HPLA_19(hv_select_ntsc_1_hpla_19),
    .HPLA_20(hv_select_ntsc_1_hpla_20), .HPLA_21(hv_select_ntsc_1_hpla_21),
    .HPLA_22(hv_select_ntsc_1_hpla_22), .HPLA_23(hv_select_ntsc_1_hpla_23));
  COLOR_CONTROL_RGB color_control_rgb_1 (
    .PCLK(PCLK), .DB_PAR(DB_PAR), .TH_MUX(TH_MUX), .nPICTURE(control_unit_ntsc_1_npicture),
    .B_W(control_regs_ntsc_1_bw), .nDB_CB(color_control_rgb_1_ndb_cb), .COLOR_EN(color_control_rgb_1_color_en));
  H_INVERSION h_inversion_1 (
    .PCLK(PCLK), .nSH2(select_2_3_5_7_pixel_1_nsh2[0]), .OB6(oam_buffer_1_ob_bit_out[6]),
    ._0_FIFO(oam_eval_1__0_fifo), .PD0(PD0), .PD1(PD1), .PD2(PD2), .PD3(PD3), .PD4(PD4), .PD5(PD5),
    .PD6(PD6), .PD7(PD7), .nT0(h_inversion_1_nt0[0]), .nT1(h_inversion_1_nt0[1]), .nT2(h_inversion_1_nt0[2]),
    .nT3(h_inversion_1_nt0[3]), .nT4(h_inversion_1_nt0[4]), .nT5(h_inversion_1_nt0[5]),
    .nT6(h_inversion_1_nt0[6]), .nT7(h_inversion_1_nt0[7]));
  READ__2007 read__2007_1 (
    .XRB(vram_bus_control_1_xrb), .RC(RC), .PD_RB(vram_bus_control_1_pd_rb), .PD0(PD0), .PD1(PD1), .PD2(PD2),
    .PD3(PD3), .PD4(PD4), .PD5(PD5), .PD6(PD6), .PD7(PD7), .DB0(read__2007_1_db0[0]),
    .DB1(read__2007_1_db0[1]), .DB2(read__2007_1_db0[2]), .DB3(read__2007_1_db0[3]),
    .DB4(read__2007_1_db0[4]), .DB5(R2DB5), .DB6(R2DB6), .DB7(R2DB7));
  REGISTER_SELECT register_select_1 (
    .nDBE(nDBE), .RC(RC), .RS0(RS0), .RS1(RS1), .RS2(RS2), .R_W(R_W), .nW6_1(register_select_1_nw6_1),
    .nW6_2(register_select_1_nw6_2), .nW5_1(register_select_1_nw5_1), .nW5_2(register_select_1_nw5_2),
    .nR7(nR7), .nW7(nW7), .nW4(register_select_1_nw4), .nW3(register_select_1_nw3), .nR2(nR2),
    .nW1(register_select_1_nw1), .nW0(register_select_1_nw0));  // open: nR4
  not not_4 (PA13, PPU_ADR[13]);
  not not_5 (PA12, PPU_ADR[12]);
  RW_CONTROL rw_control_1 (.R_W(R_W), .nDBE(nDBE), .nRD(rw_control_1_nrd), .nWR(rw_control_1_nwr));
  not not_6 (PA11, PPU_ADR[11]);
  not not_7 (PA10, PPU_ADR[10]);
  not not_8 (PA9, PPU_ADR[9]);
  not not_9 (PA8, PPU_ADR[8]);
  not not_10 (PA7, PPU_ADR[7]);
  OAM_EVAL oam_eval_1 (
    .PCLK(PCLK), .nF_NT(control_unit_ntsc_1_nf_nt), .H0_prime_prime(H0_prime_prime), .I_OAM2(I_OAM2),
    .nVIS(nVIS), .SPR_OV(oam_control_ntsc_1_spr_ov), .S_EV(control_unit_ntsc_1_s_ev), .PAR_O(PAR_O),
    .O8_16(control_regs_ntsc_1_o8_16), .OB0(oam_buffer_1_ob_bit_out[0]), .OB1(oam_buffer_1_ob_bit_out[1]),
    .OB2(oam_buffer_1_ob_bit_out[2]), .OB3(oam_buffer_1_ob_bit_out[3]), .OB4(oam_buffer_1_ob_bit_out[4]),
    .OB5(oam_buffer_1_ob_bit_out[5]), .OB6(oam_buffer_1_ob_bit_out[6]), .OB7(oam_buffer_1_ob_bit_out[7]),
    .V0(hv_select_ntsc_1_vpos[0]), .V1(hv_select_ntsc_1_vpos[1]), .V2(hv_select_ntsc_1_vpos[2]),
    .V3(hv_select_ntsc_1_vpos[3]), .V4(hv_select_ntsc_1_vpos[4]), .V5(hv_select_ntsc_1_vpos[5]),
    .V6(hv_select_ntsc_1_vpos[6]), .V7(hv_select_ntsc_1_vpos[7]), ._0_FIFO(oam_eval_1__0_fifo),
    .OMFG(oam_eval_1_omfg), .I2SEV(oam_eval_1_i2sev), .OV0(oam_eval_1_ov0[0]), .OV1(oam_eval_1_ov0[1]),
    .OV2(oam_eval_1_ov0[2]), .OV3(oam_eval_1_ov0[3]));  // open: TEST
  CONTROL_REGS_NTSC control_regs_ntsc_1 (
    .RC(RC), .nDBE(nDBE), .nW0(register_select_1_nw0), .DB0(cpu_data_io_1_cpu_ppu[0]),
    .DB1(cpu_data_io_1_cpu_ppu[1]), .DB2(cpu_data_io_1_cpu_ppu[2]), .DB3(cpu_data_io_1_cpu_ppu[3]),
    .DB4(cpu_data_io_1_cpu_ppu[4]), .DB5(cpu_data_io_1_cpu_ppu[5]), .DB6(cpu_data_io_1_cpu_ppu[6]),
    .DB7(cpu_data_io_1_cpu_ppu[7]), .nW1(register_select_1_nw1), .PCLK(PCLK), .nVIS(nVIS),
    .CLIP_B(control_unit_ntsc_1_clip_b), .CLIP_O(control_unit_ntsc_1_clip_o),
    .I1_32(control_regs_ntsc_1_i1_32), .OBSEL(control_regs_ntsc_1_obsel), .BGSEL(control_regs_ntsc_1_bgsel),
    .O8_16(control_regs_ntsc_1_o8_16), .nSLAVE(control_regs_ntsc_1_nslave), .VBL(control_regs_ntsc_1_vbl),
    .BW(control_regs_ntsc_1_bw), .BGCLIP(control_regs_ntsc_1_bgclip), .OBCLIP(control_regs_ntsc_1_obclip),
    .CLPB(control_regs_ntsc_1_clpb), .nCLPO(control_regs_ntsc_1_nclpo), .nTR(control_regs_ntsc_1_ntr[0]),
    .nTG(control_regs_ntsc_1_ntr[1]), .nTB(control_regs_ntsc_1_ntr[2]), .BLACK(control_regs_ntsc_1_black));
  not not_11 (PA6, PPU_ADR[6]);
  not not_12 (PA5, PPU_ADR[5]);
  CPU_DATA_IO cpu_data_io_1 (
    .nRD(rw_control_1_nrd), .nWR(rw_control_1_nwr), .PPU_CPU({R2DB7, R2DB6, R2DB5, read__2007_1_db0}),
    .CPU_PPU(cpu_data_io_1_cpu_ppu), .D6_2(D6_2), .D7_2(D7_2), .D0(D0), .D1(D1), .D2(D2), .D3(D3), .D4(D4),
    .D5(D5), .D6(D6), .D7(D7), .D4_2(D4_2), .D5_2(D5_2), .D2_2(D2_2), .D3_2(D3_2), .D0_2(D0_2), .D1_2(D1_2));
  SELECT_2_3_5_7_PIXEL select_2_3_5_7_pixel_1 (
    .PCLK(PCLK), .PAR_O(PAR_O), .H0_prime_prime(H0_prime_prime), .H1_prime_prime(Hnn_BUS[1]),
    .H2_prime_prime(Hnn_BUS[2]), .nSH2(select_2_3_5_7_pixel_1_nsh2[0]),
    .nSH3(select_2_3_5_7_pixel_1_nsh2[1]), .nSH5(select_2_3_5_7_pixel_1_nsh2[2]),
    .nSH7(select_2_3_5_7_pixel_1_nsh2[3]));
  MUX mux_1 (
    .EXT3_IN(1'b0), .EXT2_IN(1'b0), .EXT1_IN(1'b0), .EXT0_IN(1'b0), .PCLK(PCLK), .BGC0(bg_color_1_bgc0[0]),
    .BGC1(bg_color_1_bgc0[1]), .BGC2(bg_color_1_bgc0[2]), .BGC3(bg_color_1_bgc0[3]),
    .nZCOL0(oam_fifo_1_nzcol0[0]), .nZCOL1(oam_fifo_1_nzcol0[1]), .ZCOL2(oam_fifo_1_nzcol0[2]),
    .ZCOL3(oam_fifo_1_nzcol0[3]), .nZPRIO(oam_fifo_1_nzcol0[4]), .THO0(TH[0]), .THO1(TH[1]), .THO2(TH[2]),
    .THO3(TH[3]), .THO4(TH[4]), .TH_MUX(TH_MUX), .nSPR0HIT(oam_fifo_1_nspr0hit), .I2SEV(oam_eval_1_i2sev),
    .nVIS(nVIS), .RESCL(RESCL), .nDBE(nDBE), .nR2(nR2), .EXT0_OUT(mux_1_ext0_out), .EXT1_OUT(mux_1_ext1_out),
    .EXT2_OUT(mux_1_ext2_out), .EXT3_OUT(mux_1_ext3_out), .PAL0(mux_1_pal0[0]), .PAL1(mux_1_pal0[1]),
    .PAL2(mux_1_pal0[2]), .PAL3(mux_1_pal0[3]), .PAL4(mux_1_pal0[4]), .DB6(R2DB6));
  VRAM_BUS_CONTROL vram_bus_control_1 (
    .PCLK(PCLK), .nR7(nR7), .nDBE(nDBE), .nW7(nW7), .BLNK(BLNK), .H0_prime(H0_prime), .nPA8(PPU_ADR[8]),
    .nPA9(PPU_ADR[9]), .nPA10(PPU_ADR[10]), .nPA11(PPU_ADR[11]), .nPA12(PPU_ADR[12]), .nPA13(PPU_ADR[13]),
    .TSTEP(vram_bus_control_1_tstep), .PD_RB(vram_bus_control_1_pd_rb), .DB_PAR(DB_PAR),
    .nALE(vram_bus_control_1_nale), .RD(nRD), .WR(nWR), .XRB(vram_bus_control_1_xrb), .TH_MUX(TH_MUX));
  not not_13 (PA4, PPU_ADR[4]);
  OAM_CONTROL_NTSC oam_control_ntsc_1 (
    .PCLK(PCLK), .OFETCH(oam_buf_control_rgb_1_ofetch), .BLNK(BLNK), .nVIS(nVIS),
    .H0_prime_prime(H0_prime_prime), .I_OAM2(I_OAM2), .OMFG(oam_eval_1_omfg), .nDBE(nDBE),
    .nW3(register_select_1_nw3), .PAR_O(PAR_O), .DB0(cpu_data_io_1_cpu_ppu[0]),
    .DB1(cpu_data_io_1_cpu_ppu[1]), .DB2(cpu_data_io_1_cpu_ppu[2]), .DB3(cpu_data_io_1_cpu_ppu[3]),
    .DB4(cpu_data_io_1_cpu_ppu[4]), .DB5(cpu_data_io_1_cpu_ppu[5]), .DB6(cpu_data_io_1_cpu_ppu[6]),
    .DB7(cpu_data_io_1_cpu_ppu[7]), .EVAL(control_unit_ntsc_1_eval), .nH2_prime(nH2_prime),
    .H0_prime(H0_prime), .RESCL(RESCL), .nR2(nR2), .nOAM0(oam_control_ntsc_1_noam0[0]),
    .nOAM1(oam_control_ntsc_1_noam0[1]), .nOAM2(oam_control_ntsc_1_noam0[2]),
    .nOAM3(oam_control_ntsc_1_noam0[3]), .nOAM4(oam_control_ntsc_1_noam0[4]),
    .nOAM5(oam_control_ntsc_1_noam0[5]), .nOAM6(oam_control_ntsc_1_noam0[6]),
    .nOAM7(oam_control_ntsc_1_noam0[7]), .OAM8(oam_control_ntsc_1_noam0[8]),
    .SPR_OV(oam_control_ntsc_1_spr_ov), .OAMCTR2(oam_control_ntsc_1_oamctr2), .DB5_2(R2DB5));
  not not_14 (PA3, PPU_ADR[3]);
  not not_15 (PA2, PPU_ADR[2]);
  not not_16 (PA1, PPU_ADR[1]);
  not not_17 (PA0, PPU_ADR[0]);
  not not_18 (ALE, vram_bus_control_1_nale);
  assign controlled_buffer_1_out = not_19_out ? oam_control_ntsc_1_noam0[7:0] : 8'bz;  // Controlled_Buffer controlled_buffer_1
  not not_19 (not_19_out, oam_control_ntsc_1_noam0[8]);
  Demultiplexer #(.width(8), .enable("false")) demultiplexer_1 (
    .out0(demultiplexer_1_out0), .out1(demultiplexer_1_out1), .in(oam_buffer_1_ram_write),
    .sel(oam_control_ntsc_1_noam0[8]));
  assign controlled_buffer_2_out = oam_control_ntsc_1_noam0[8] ? oam_control_ntsc_1_noam0[7:3] : 5'bz;  // Controlled_Buffer controlled_buffer_2
  not not_20 (not_20_out, oam_buf_control_rgb_1_nwe);
  Hex_Digit_Display hex_digit_display_1 (.value(oam_control_ntsc_1_noam0[7:4]));  // open: dp
  Hex_Digit_Display hex_digit_display_2 (.value({3'b000, oam_control_ntsc_1_noam0[8]}));  // open: dp
  not not_21 (not_21_out, oam_control_ntsc_1_noam0[8]);
  Hex_Digit_Display hex_digit_display_3 (.value(oam_control_ntsc_1_noam0[3:0]));  // open: dp
  not not_22 (not_22_out, not_20_out);
  not not_23 (not_23_out, not_20_out);
  WRITE__2007 write__2007_1 (
    .PCLK(PCLK), .DB_PAR(DB_PAR), .D0(cpu_data_io_1_cpu_ppu[0]), .D1(cpu_data_io_1_cpu_ppu[1]),
    .D2(cpu_data_io_1_cpu_ppu[2]), .D3(cpu_data_io_1_cpu_ppu[3]), .D4(cpu_data_io_1_cpu_ppu[4]),
    .D5(cpu_data_io_1_cpu_ppu[5]), .D6(cpu_data_io_1_cpu_ppu[6]), .D7(cpu_data_io_1_cpu_ppu[7]), .PD0(PD0_W),
    .PD1(PD1_W), .PD2(PD2_W), .PD3(PD3_W), .PD4(PD4_W), .PD5(PD5_W), .PD6(PD6_W), .PD7(PD7_W));
  OAM_BUF_CONTROL_RGB oam_buf_control_rgb_1 (
    .PCLK(PCLK), .BLNK(BLNK), .SPR_OV(oam_control_ntsc_1_spr_ov), .nVIS(nVIS),
    .OAMCTR2(oam_control_ntsc_1_oamctr2), .H0_prime_prime(H0_prime_prime), .nW4(register_select_1_nw4),
    .nDBE(nDBE), .OB_OAM(oam_buf_control_rgb_1_ob_oam), .nWE(oam_buf_control_rgb_1_nwe),
    .OFETCH(oam_buf_control_rgb_1_ofetch));
  OAM_BUFFER oam_buffer_1 (
    .PCLK(PCLK), .nR4(1'b1), .OAM___DB({R2DB7, R2DB6, R2DB5, read__2007_1_db0}), .I_OAM2(I_OAM2),
    .OB_bit_out(oam_buffer_1_ob_bit_out), .RAM_read(multiplexer_1_out),
    .OB_OAM(oam_buf_control_rgb_1_ob_oam), .DB___OAM(cpu_data_io_1_cpu_ppu), .BLNK(BLNK),
    .nWE(oam_buf_control_rgb_1_nwe), .RAM_write(oam_buffer_1_ram_write));
  RAM #(.bus("separate")) ram_2 (
    .addr(controlled_buffer_1_out), .din(demultiplexer_1_out0), .data(ram_2_data), .str(not_20_out),
    .sel(not_21_out), .clk(PCLK[0]), .ld(not_22_out));  // open: clr
  RAM #(.addrWidth(5), .bus("separate")) ram_3 (
    .addr(controlled_buffer_2_out), .din(demultiplexer_1_out1), .data(ram_3_data), .str(not_20_out),
    .sel(oam_control_ntsc_1_noam0[8]), .clk(PCLK[0]), .ld(not_23_out));  // open: clr
  BG_COLOR bg_color_1 (
    .PCLK(PCLK), .CLPB(control_regs_ntsc_1_clpb), .FH0(picture_address_gen_1_fh0[0]),
    .FH1(picture_address_gen_1_fh0[1]), .FH2(picture_address_gen_1_fh0[2]), .PD0(PD0), .PD1(PD1), .PD2(PD2),
    .PD3(PD3), .PD4(PD4), .PD5(PD5), .PD6(PD6), .PD7(PD7), .THO1(TH[0]), .TVO1(picture_address_gen_1_tvo1),
    .F_AT(control_unit_ntsc_1_f_at), .H0_prime_prime(H0_prime_prime), .F_TA(control_unit_ntsc_1_f_ta),
    .F_TB(control_unit_ntsc_1_f_tb), .nFO(control_unit_ntsc_1_nfo), .BGC0(bg_color_1_bgc0[0]),
    .BGC1(bg_color_1_bgc0[1]), .BGC2(bg_color_1_bgc0[2]), .BGC3(bg_color_1_bgc0[3]));
  Hex_Digit_Display hex_digit_display_4 (.value(multiplexer_1_out[3:0]));  // open: dp
  Hex_Digit_Display hex_digit_display_5 (.value(multiplexer_1_out[7:4]));  // open: dp
  Multiplexer #(.width(8), .enable("false")) multiplexer_1 (
    .in0(ram_2_data), .in1(ram_3_data), .out(multiplexer_1_out), .sel(oam_control_ntsc_1_noam0[8]));
  PICTURE_ADDRESS_GEN picture_address_gen_1 (
    .PCLK(PCLK), .SC_CNT(control_unit_ntsc_1_sc_cnt), .RESCL(RESCL), .E_EV(control_unit_ntsc_1_e_ev),
    .TSTEP(vram_bus_control_1_tstep), .F_TB(control_unit_ntsc_1_f_tb), .H0_prime_prime(H0_prime_prime),
    .BLNK(BLNK), .l1_32(control_regs_ntsc_1_i1_32), .PD0(PD0), .PD1(PD1), .PD2(PD2), .PD3(PD3), .PD4(PD4),
    .PD5(PD5), .PD6(PD6), .PD7(PD7), .OB0(oam_buffer_1_ob_bit_out[0]), .OB1(oam_buffer_1_ob_bit_out[1]),
    .OB2(oam_buffer_1_ob_bit_out[2]), .OB3(oam_buffer_1_ob_bit_out[3]), .OB4(oam_buffer_1_ob_bit_out[4]),
    .OB5(oam_buffer_1_ob_bit_out[5]), .OB6(oam_buffer_1_ob_bit_out[6]), .OB7(oam_buffer_1_ob_bit_out[7]),
    .OV0(oam_eval_1_ov0[0]), .OV1(oam_eval_1_ov0[1]), .OV2(oam_eval_1_ov0[2]), .OV3(oam_eval_1_ov0[3]),
    .DB0(cpu_data_io_1_cpu_ppu[0]), .DB1(cpu_data_io_1_cpu_ppu[1]), .DB2(cpu_data_io_1_cpu_ppu[2]),
    .DB3(cpu_data_io_1_cpu_ppu[3]), .DB4(cpu_data_io_1_cpu_ppu[4]), .DB5(cpu_data_io_1_cpu_ppu[5]),
    .DB6(cpu_data_io_1_cpu_ppu[6]), .DB7(cpu_data_io_1_cpu_ppu[7]), .nW0(register_select_1_nw0),
    .nW5_2(register_select_1_nw5_2), .nW6_1(register_select_1_nw6_1), .nW5_1(register_select_1_nw5_1),
    .nW6_2(register_select_1_nw6_2), .nDBE(nDBE), .RC(RC), .nPA0(PPU_ADR[0]), .nPA1(PPU_ADR[1]),
    .nPA2(PPU_ADR[2]), .nPA3(PPU_ADR[3]), .nPA4(PPU_ADR[4]), .nPA5(PPU_ADR[5]), .nPA6(PPU_ADR[6]),
    .nPA7(PPU_ADR[7]), .nPA8(PPU_ADR[8]), .nPA9(PPU_ADR[9]), .nPA10(PPU_ADR[10]), .nPA11(PPU_ADR[11]),
    .nPA12(PPU_ADR[12]), .FH0(picture_address_gen_1_fh0[0]), .nPA13(PPU_ADR[13]),
    .FH1(picture_address_gen_1_fh0[1]), .FH2(picture_address_gen_1_fh0[2]), .THO0(TH[0]), .THO1(TH[1]),
    .THO2(TH[2]), .THO3(TH[3]), .THO4(TH[4]), .TVO1(picture_address_gen_1_tvo1),
    .F_AT(control_unit_ntsc_1_f_at), .nF_NT(control_unit_ntsc_1_nf_nt), .PAR_O(PAR_O),
    .nSH2(select_2_3_5_7_pixel_1_nsh2[0]), .O8_16(control_regs_ntsc_1_o8_16),
    .OBSEL(control_regs_ntsc_1_obsel), .BGSEL(control_regs_ntsc_1_bgsel), .nH2_prime(nH2_prime),
    .nH1_prime(nH1_prime), .DB_PAR(1'b0));

  // Other names for the same wires on the sheet: Hnn_BUS[0] = H0_prime_prime;
  //   PPU_DATA[7:0] = {PD7, PD6, PD5, PD4, PD3, PD2, PD1, PD0};
  //   PPU_DATA_W[7:0] = {PD7_W, PD6_W, PD5_W, PD4_W, PD3_W, PD2_W, PD1_W, PD0_W}

  // Notes on the sheet:
  //   Manual cleaning
  //   2C04 - 0003  RGB  PPU
  //   not used
  //   not used
  //   READ FUNCTION IS NOT USED
  //   CPU INTERFACE
  //   /R4 NOT USED
  //   Logisim doesn't support bidirectional pads and wires
  //   So we have to add workaround by separate I/O wires
  //   NOT USED
  //   NOT USED
  //   VRAM INTERFACE
  //   Logisim doesn't support bidirectional pads and wires
  //   So we have to add workaround by separate I/O wires
endmodule

// 2C07 PAL
module _2C07_PAL (
  input  nDBE,
  input  RS2,
  input  RS1,
  input  RS0,
  input  R_W,
  input  D0,
  input  D1,
  input  D2,
  input  D3,
  input  D4,
  input  D5,
  input  D6,
  input  D7,
  input  EXT0,
  input  EXT1,
  input  EXT2,
  input  EXT3,
  input  CLK,
  input  nRES,
  input  PD7,
  input  PD6,
  input  PD5,
  input  PD4,
  input  PD3,
  input  PD2,
  input  PD1,
  input  PD0,
  output D0_2,
  output D1_2,
  output D2_2,
  output D3_2,
  output D4_2,
  output D5_2,
  output D6_2,
  output D7_2,
  output EXT0_2,
  output EXT1_2,
  output EXT2_2,
  output EXT3_2,
  output [10:0] VOUT,
  output nINT,
  output nRD,
  output nWR,
  output PA13,
  output PA12,
  output PA11,
  output PA10,
  output PA9,
  output PA8,
  output PA7,
  output PA6,
  output PA5,
  output PA4,
  output PA3,
  output PA2,
  output PA1,
  output PA0,
  output ALE,
  output PD7_W,
  output PD6_W,
  output PD5_W,
  output PD4_W,
  output PD3_W,
  output PD2_W,
  output PD1_W,
  output PD0_W
);

  wire BLNK, button_1_out, color_control_1_color_en, color_control_1_ncb_db, color_control_1_ndb_cb,
       color_io_1_nout0, color_io_1_nout1, color_io_1_nout2, color_io_1_nout3, color_io_1_nout4,
       color_io_1_nout5, control_regs_pal_1_bgsel, control_regs_pal_1_black, control_regs_pal_1_bw,
       control_regs_pal_1_clpb, control_regs_pal_1_i1_32, control_regs_pal_1_nbgclip,
       control_regs_pal_1_nclpo, control_regs_pal_1_nobclip, control_regs_pal_1_nslave,
       control_regs_pal_1_o8_16, control_regs_pal_1_obsel, control_regs_pal_1_vbl,
       control_unit_pal_1__0_hpos, control_unit_pal_1_burst, control_unit_pal_1_clip_b,
       control_unit_pal_1_clip_o, control_unit_pal_1_e_ev, control_unit_pal_1_eval, control_unit_pal_1_f_at,
       control_unit_pal_1_f_ta, control_unit_pal_1_f_tb, control_unit_pal_1_hc, control_unit_pal_1_nf_nt,
       control_unit_pal_1_nfo, control_unit_pal_1_npicture, control_unit_pal_1_nvset,
       control_unit_pal_1_s_ev, control_unit_pal_1_sc_cnt, control_unit_pal_1_sync, control_unit_pal_1_vb,
       control_unit_pal_1_vc, control_unit_pal_1_vin, control_unit_pal_1_zomg_pal, DB_PAR, H0_prime,
       H0_prime_prime, h_counter_1_h0, h_counter_1_h1, h_counter_1_h2, h_counter_1_h3, h_counter_1_h4,
       h_counter_1_h5, h_counter_1_h6, h_counter_1_h7, h_counter_1_h8, hv_select_pal_1_hpla_0,
       hv_select_pal_1_hpla_1, hv_select_pal_1_hpla_2, hv_select_pal_1_hpla_3, hv_select_pal_1_hpla_4,
       hv_select_pal_1_hpla_5, hv_select_pal_1_hpla_6, hv_select_pal_1_hpla_7, hv_select_pal_1_hpla_8,
       hv_select_pal_1_hpla_9, hv_select_pal_1_hpla_10, hv_select_pal_1_hpla_11, hv_select_pal_1_hpla_12,
       hv_select_pal_1_hpla_13, hv_select_pal_1_hpla_14, hv_select_pal_1_hpla_15, hv_select_pal_1_hpla_16,
       hv_select_pal_1_hpla_17, hv_select_pal_1_hpla_18, hv_select_pal_1_hpla_19, hv_select_pal_1_hpla_20,
       hv_select_pal_1_hpla_21, hv_select_pal_1_hpla_22, hv_select_pal_1_hpla_23, hv_select_pal_1_vpla_0,
       hv_select_pal_1_vpla_1, hv_select_pal_1_vpla_2, hv_select_pal_1_vpla_3, hv_select_pal_1_vpla_4,
       hv_select_pal_1_vpla_5, hv_select_pal_1_vpla_6, hv_select_pal_1_vpla_7, hv_select_pal_1_vpla_8,
       hv_select_pal_1_vpla_9, I_OAM2, interrupt_control_1_int, nH1_prime, nH2_prime, not_1_out, not_3_out,
       not_6_out, not_20_out, not_21_out, not_22_out, not_23_out, not_24_out, not_25_out, not_26_out, nR2,
       nR7, nVIS, nW7, oam_buf_control_1_nwe, oam_buf_control_1_ob_oam, oam_buf_control_1_ofetch,
       oam_control_pal_1_oamctr2, oam_control_pal_1_spr_ov, oam_eval_1__0_fifo, oam_eval_1_i2sev,
       oam_eval_1_omfg, oam_eval_1_test, oam_fifo_1_nspr0hit, or_1_out, PAR_O, picture_address_gen_1_tvo1,
       pixel_clock_pal_1_npclk, pixel_clock_pal_1_pclk_2, R2DB5, R2DB6, R2DB7, RC, register_select_1_nr4,
       register_select_1_nw0, register_select_1_nw1, register_select_1_nw3, register_select_1_nw4,
       register_select_1_nw5_1, register_select_1_nw5_2, register_select_1_nw6_1, register_select_1_nw6_2,
       RES, RESCL, rw_control_1_nrd, rw_control_1_nwr, TH_MUX, undriven, v_counter_1_v0, v_counter_1_v1,
       v_counter_1_v2, v_counter_1_v3, v_counter_1_v4, v_counter_1_v5, v_counter_1_v6, v_counter_1_v7,
       v_counter_1_v8, VCLR, vram_bus_control_1_nale, vram_bus_control_1_pd_rb, vram_bus_control_1_tstep,
       vram_bus_control_1_xrb;
  wire [1:0] PCLK;
  wire [2:0] control_regs_pal_1_ntr, picture_address_gen_1_fh0;
  wire [3:0] bg_color_1_bgc0, oam_eval_1_ov0, select_2_3_5_7_pixel_1_nsh2;
  wire [4:0] color_io_1_db0_2, controlled_buffer_2_out, mux_1_pal0, oam_fifo_1_nzcol0, TH;
  wire [5:0] color_io_1_cb_ram0, hv_select_pal_1_hnn, ram_1_data;
  wire [5:1] Hnn_BUS;
  wire [7:0] controlled_buffer_1_out, cpu_data_io_1_cpu_ppu, demultiplexer_1_out0, demultiplexer_1_out1,
       h_inversion_1_nt0, hv_select_pal_1_vpos, multiplexer_1_out, mux_1_ext0_out, oam_buffer_1_ob_bit_out,
       oam_buffer_1_ram_write, ram_2_data, ram_3_data;
  wire [8:0] oam_control_pal_1_noam0;
  wire [13:0] PPU_ADR;

  Clock clock_1 ();  // open: out
  Button button_1 (.out(button_1_out));
  not not_1 (not_1_out, undriven);
  not not_2 (nINT, interrupt_control_1_int);
  or or_1 (or_1_out, VCLR, button_1_out);
  COLOR_IO color_io_1 (
    .PCLK(PCLK), .nDB_CB(color_control_1_ndb_cb), .nCB_DB(color_control_1_ncb_db),
    .nBW(color_control_1_color_en), .RAM_CB0(ram_1_data[0]), .DB0(cpu_data_io_1_cpu_ppu[0]),
    .RAM_CB1(ram_1_data[1]), .DB1(cpu_data_io_1_cpu_ppu[1]), .RAM_CB2(ram_1_data[2]),
    .DB2(cpu_data_io_1_cpu_ppu[2]), .RAM_CB3(ram_1_data[3]), .DB3(cpu_data_io_1_cpu_ppu[3]),
    .RAM_CB4(ram_1_data[4]), .DB4(cpu_data_io_1_cpu_ppu[4]), .RAM_CB5(ram_1_data[5]),
    .DB5(cpu_data_io_1_cpu_ppu[5]), .nout0(color_io_1_nout0), .DB0_2(color_io_1_db0_2[0]),
    .CB_RAM0(color_io_1_cb_ram0[0]), .nout1(color_io_1_nout1), .DB1_2(color_io_1_db0_2[1]),
    .CB_RAM1(color_io_1_cb_ram0[1]), .nout2(color_io_1_nout2), .DB2_2(color_io_1_db0_2[2]),
    .CB_RAM2(color_io_1_cb_ram0[2]), .nout3(color_io_1_nout3), .DB3_2(color_io_1_db0_2[3]),
    .CB_RAM3(color_io_1_cb_ram0[3]), .nout4(color_io_1_nout4), .DB4_2(color_io_1_db0_2[4]),
    .CB_RAM4(color_io_1_cb_ram0[4]), .nout5(color_io_1_nout5), .DB5_2(R2DB5), .CB_RAM5(color_io_1_cb_ram0[5]));
  RESET_FF reset_ff_1 (.nRES(nRES), .RESCL(or_1_out), .RES(RES), .RC(RC));
  VIDEO_OUT_PAL video_out_pal_1 (
    .nCLK(not_1_out), .RES(RES), .nTR(control_regs_pal_1_ntr[0]), .nTG(control_regs_pal_1_ntr[1]),
    .nTB(control_regs_pal_1_ntr[2]), .V0(v_counter_1_v0), .PCLK(PCLK), .nCC0(color_io_1_nout0),
    .nCC1(color_io_1_nout1), .nCC2(color_io_1_nout2), .nCC3(color_io_1_nout3),
    .nPICTURE(control_unit_pal_1_npicture), .SYNC(control_unit_pal_1_sync), .BURST(control_unit_pal_1_burst),
    .nLL0(color_io_1_nout5), .nLL1(color_io_1_nout4), .out_17(VOUT));
  not not_3 (not_3_out, color_control_1_ndb_cb);
  PIXEL_CLOCK_PAL pixel_clock_pal_1 (
    .nCLK(not_1_out), .RES(RES), .PCLK(PCLK), .nPCLK(pixel_clock_pal_1_npclk),
    .PCLK_2(pixel_clock_pal_1_pclk_2));
  RAM #(.addrWidth(5), .dataWidth(6), .bus("separate")) ram_1 (
    .addr(mux_1_pal0), .din(color_io_1_cb_ram0), .data(ram_1_data), .str(not_3_out), .sel(1'b1),
    .clk(PCLK[0]), .ld(color_control_1_ndb_cb));  // open: clr
  H_COUNTER h_counter_1 (
    .RES(RES), .HC(control_unit_pal_1_hc), .PCLK(PCLK), .H0(h_counter_1_h0), .H1(h_counter_1_h1),
    .H2(h_counter_1_h2), .H3(h_counter_1_h3), .H4(h_counter_1_h4), .H5(h_counter_1_h5), .H6(h_counter_1_h6),
    .H7(h_counter_1_h7), .H8(h_counter_1_h8));
  OAM_FIFO oam_fifo_1 (
    .PCLK(PCLK), ._0_HPOS(control_unit_pal_1__0_hpos), .H3_prime_prime(Hnn_BUS[3]),
    .H4_prime_prime(Hnn_BUS[4]), .H5_prime_prime(Hnn_BUS[5]), .nSH2(select_2_3_5_7_pixel_1_nsh2[0]),
    .nSH3(select_2_3_5_7_pixel_1_nsh2[1]), .nSH5(select_2_3_5_7_pixel_1_nsh2[2]),
    .nSH7(select_2_3_5_7_pixel_1_nsh2[3]), .nVIS(nVIS), .nCLPO(control_regs_pal_1_nclpo),
    .OB0(oam_buffer_1_ob_bit_out[0]), .OB1(oam_buffer_1_ob_bit_out[1]), .OB2(oam_buffer_1_ob_bit_out[2]),
    .OB3(oam_buffer_1_ob_bit_out[3]), .OB4(oam_buffer_1_ob_bit_out[4]), .OB5(oam_buffer_1_ob_bit_out[5]),
    .OB6(oam_buffer_1_ob_bit_out[6]), .OB7(oam_buffer_1_ob_bit_out[7]), .nT0(h_inversion_1_nt0[0]),
    .nT1(h_inversion_1_nt0[1]), .nT2(h_inversion_1_nt0[2]), .nT3(h_inversion_1_nt0[3]),
    .nT4(h_inversion_1_nt0[4]), .nT5(h_inversion_1_nt0[5]), .nT6(h_inversion_1_nt0[6]),
    .nT7(h_inversion_1_nt0[7]), .nSPR0HIT(oam_fifo_1_nspr0hit), .nZCOL0(oam_fifo_1_nzcol0[0]),
    .nZCOL1(oam_fifo_1_nzcol0[1]), .ZCOL2(oam_fifo_1_nzcol0[2]), .ZCOL3(oam_fifo_1_nzcol0[3]),
    .nZPRIO(oam_fifo_1_nzcol0[4]));
  V_COUNTER v_counter_1 (
    .VIN(control_unit_pal_1_vin), .PCLK(PCLK), .RES(RES), .VC(control_unit_pal_1_vc), .V0(v_counter_1_v0),
    .V1(v_counter_1_v1), .V2(v_counter_1_v2), .V3(v_counter_1_v3), .V4(v_counter_1_v4), .V5(v_counter_1_v5),
    .V6(v_counter_1_v6), .V7(v_counter_1_v7), .V8(v_counter_1_v8));
  INTERRUPT_CONTROL interrupt_control_1 (
    .VBL_EN(control_regs_pal_1_vbl), .VSET(control_unit_pal_1_nvset), .RESCL(RESCL), .nDBE(nDBE), .nR2(nR2),
    .INT(interrupt_control_1_int), .DB7(R2DB7), .PCLK(PCLK));
  COLOR_CONTROL color_control_1 (
    .PCLK(PCLK), .DB_PAR(DB_PAR), .TH_MUX(TH_MUX), .nR7(nR7), .nDBE(nDBE),
    .nPICTURE(control_unit_pal_1_npicture), .BW(control_regs_pal_1_bw), .nDB_CB(color_control_1_ndb_cb),
    .nCB_DB(color_control_1_ncb_db), .COLOR_EN(color_control_1_color_en));
  HV_SELECT_PAL hv_select_pal_1 (
    .H8(h_counter_1_h8), .H7(h_counter_1_h7), .H6(h_counter_1_h6), .H5(h_counter_1_h5), .H4(h_counter_1_h4),
    .H3(h_counter_1_h3), .H2(h_counter_1_h2), .H1(h_counter_1_h1), .H0(h_counter_1_h0),
    .VB(control_unit_pal_1_vb), .BLNK(BLNK), .V8(v_counter_1_v8), .V7(v_counter_1_v7), .V6(v_counter_1_v6),
    .V5(v_counter_1_v5), .V4(v_counter_1_v4), .V3(v_counter_1_v3), .V2(v_counter_1_v2), .V1(v_counter_1_v1),
    .V0(v_counter_1_v0), .VPOS(hv_select_pal_1_vpos), .Hnn(hv_select_pal_1_hnn),
    .HPLA_0(hv_select_pal_1_hpla_0), .VPLA_0(hv_select_pal_1_vpla_0), .HPLA_1(hv_select_pal_1_hpla_1),
    .VPLA_1(hv_select_pal_1_vpla_1), .HPLA_2(hv_select_pal_1_hpla_2), .VPLA_2(hv_select_pal_1_vpla_2),
    .HPLA_3(hv_select_pal_1_hpla_3), .VPLA_3(hv_select_pal_1_vpla_3), .HPLA_4(hv_select_pal_1_hpla_4),
    .VPLA_4(hv_select_pal_1_vpla_4), .HPLA_5(hv_select_pal_1_hpla_5), .VPLA_5(hv_select_pal_1_vpla_5),
    .HPLA_6(hv_select_pal_1_hpla_6), .VPLA_6(hv_select_pal_1_vpla_6), .HPLA_7(hv_select_pal_1_hpla_7),
    .VPLA_7(hv_select_pal_1_vpla_7), .HPLA_8(hv_select_pal_1_hpla_8), .VPLA_8(hv_select_pal_1_vpla_8),
    .HPLA_9(hv_select_pal_1_hpla_9), .VPLA_9(hv_select_pal_1_vpla_9), .HPLA_10(hv_select_pal_1_hpla_10),
    .HPLA_11(hv_select_pal_1_hpla_11), .HPLA_12(hv_select_pal_1_hpla_12), .HPLA_13(hv_select_pal_1_hpla_13),
    .HPLA_14(hv_select_pal_1_hpla_14), .HPLA_15(hv_select_pal_1_hpla_15), .HPLA_16(hv_select_pal_1_hpla_16),
    .HPLA_17(hv_select_pal_1_hpla_17), .HPLA_18(hv_select_pal_1_hpla_18), .HPLA_19(hv_select_pal_1_hpla_19),
    .HPLA_20(hv_select_pal_1_hpla_20), .HPLA_21(hv_select_pal_1_hpla_21), .HPLA_22(hv_select_pal_1_hpla_22),
    .HPLA_23(hv_select_pal_1_hpla_23));
  CONTROL_UNIT_PAL control_unit_pal_1 (
    .PCLK(PCLK), .Hnn(hv_select_pal_1_hnn), .nOBCLIP(control_regs_pal_1_nbgclip),
    .nBGCLIP(control_regs_pal_1_nobclip), .HPLA_2(hv_select_pal_1_hpla_2), .HPLA_3(hv_select_pal_1_hpla_3),
    .HPLA_4(hv_select_pal_1_hpla_4), .HPLA_5(hv_select_pal_1_hpla_5), .HPLA_6(hv_select_pal_1_hpla_6),
    .HPLA_7(hv_select_pal_1_hpla_7), .HPLA_8(hv_select_pal_1_hpla_8), .HPLA_9(hv_select_pal_1_hpla_9),
    .HPLA_10(hv_select_pal_1_hpla_10), .HPLA_11(hv_select_pal_1_hpla_11), .HPLA_16(hv_select_pal_1_hpla_16),
    .HPLA_13(hv_select_pal_1_hpla_13), .HPLA_12(hv_select_pal_1_hpla_12), .HPLA_14(hv_select_pal_1_hpla_14),
    .HPLA_15(hv_select_pal_1_hpla_15), .HPLA_19(hv_select_pal_1_hpla_19), .HPLA_20(hv_select_pal_1_hpla_20),
    .HPLA_0(hv_select_pal_1_hpla_0), .HPLA_1(hv_select_pal_1_hpla_1), .HPLA_21(hv_select_pal_1_hpla_21),
    .HPLA_22(hv_select_pal_1_hpla_22), .HPLA_17(hv_select_pal_1_hpla_17), .HPLA_18(hv_select_pal_1_hpla_18),
    .VPLA_1(hv_select_pal_1_vpla_1), .VPLA_0(hv_select_pal_1_vpla_0), .VPLA_3(hv_select_pal_1_vpla_3),
    .VPLA_2(hv_select_pal_1_vpla_2), .VPLA_4(hv_select_pal_1_vpla_4), .VPLA_5(hv_select_pal_1_vpla_5),
    .VPLA_6(hv_select_pal_1_vpla_6), .VPLA_7(hv_select_pal_1_vpla_7), .VPLA_8(hv_select_pal_1_vpla_8),
    .BLACK(control_regs_pal_1_black), .HPLA_23(hv_select_pal_1_hpla_23), .VPLA_9(hv_select_pal_1_vpla_9),
    .H0_prime_prime(H0_prime_prime), .H1_prime_prime(Hnn_BUS[1]), .H2_prime_prime(Hnn_BUS[2]),
    .H3_prime_prime(Hnn_BUS[3]), .H4_prime_prime(Hnn_BUS[4]), .H5_prime_prime(Hnn_BUS[5]),
    .H0_prime(H0_prime), .nH1_prime(nH1_prime), .nH2_prime(nH2_prime), .S_EV(control_unit_pal_1_s_ev),
    .CLIP_O(control_unit_pal_1_clip_o), .CLIP_B(control_unit_pal_1_clip_b),
    ._0_HPOS(control_unit_pal_1__0_hpos), .EVAL(control_unit_pal_1_eval), .E_EV(control_unit_pal_1_e_ev),
    .I_OAM2(I_OAM2), .PAR_O(PAR_O), .nVIS(nVIS), .nF_NT(control_unit_pal_1_nf_nt),
    .F_AT(control_unit_pal_1_f_at), .F_TA(control_unit_pal_1_f_ta), .F_TB(control_unit_pal_1_f_tb),
    .nFO(control_unit_pal_1_nfo), .SC_CNT(control_unit_pal_1_sc_cnt), .SYNC(control_unit_pal_1_sync),
    .BURST(control_unit_pal_1_burst), .nPICTURE(control_unit_pal_1_npicture),
    .nVSET(control_unit_pal_1_nvset), .VB(control_unit_pal_1_vb), .BLNK(BLNK), .RESCL(RESCL),
    .VIN(control_unit_pal_1_vin), .HC(control_unit_pal_1_hc), .VC(control_unit_pal_1_vc),
    .ZOMG_PAL(control_unit_pal_1_zomg_pal));
  H_INVERSION h_inversion_1 (
    .PCLK(PCLK), .nSH2(select_2_3_5_7_pixel_1_nsh2[0]), .OB6(oam_buffer_1_ob_bit_out[6]),
    ._0_FIFO(oam_eval_1__0_fifo), .PD0(PD0), .PD1(PD1), .PD2(PD2), .PD3(PD3), .PD4(PD4), .PD5(PD5),
    .PD6(PD6), .PD7(PD7), .nT0(h_inversion_1_nt0[0]), .nT1(h_inversion_1_nt0[1]), .nT2(h_inversion_1_nt0[2]),
    .nT3(h_inversion_1_nt0[3]), .nT4(h_inversion_1_nt0[4]), .nT5(h_inversion_1_nt0[5]),
    .nT6(h_inversion_1_nt0[6]), .nT7(h_inversion_1_nt0[7]));
  READ__2007 read__2007_1 (
    .XRB(vram_bus_control_1_xrb), .RC(RC), .PD_RB(vram_bus_control_1_pd_rb), .PD0(PD0), .PD1(PD1), .PD2(PD2),
    .PD3(PD3), .PD4(PD4), .PD5(PD5), .PD6(PD6), .PD7(PD7), .DB0(color_io_1_db0_2[0]),
    .DB1(color_io_1_db0_2[1]), .DB2(color_io_1_db0_2[2]), .DB3(color_io_1_db0_2[3]),
    .DB4(color_io_1_db0_2[4]), .DB5(R2DB5), .DB6(R2DB6), .DB7(R2DB7));
  REGISTER_SELECT register_select_1 (
    .nDBE(nDBE), .RC(RC), .RS0(RS0), .RS1(RS1), .RS2(RS2), .R_W(R_W), .nW6_1(register_select_1_nw6_1),
    .nW6_2(register_select_1_nw6_2), .nW5_1(register_select_1_nw5_1), .nW5_2(register_select_1_nw5_2),
    .nR7(nR7), .nW7(nW7), .nW4(register_select_1_nw4), .nW3(register_select_1_nw3), .nR2(nR2),
    .nW1(register_select_1_nw1), .nW0(register_select_1_nw0), .nR4(register_select_1_nr4));
  RW_CONTROL rw_control_1 (.R_W(R_W), .nDBE(nDBE), .nRD(rw_control_1_nrd), .nWR(rw_control_1_nwr));
  not not_4 (PA13, PPU_ADR[13]);
  not not_5 (PA12, PPU_ADR[12]);
  not not_6 (not_6_out, control_regs_pal_1_o8_16);
  not not_7 (PA11, PPU_ADR[11]);
  not not_8 (PA10, PPU_ADR[10]);
  not not_9 (PA9, PPU_ADR[9]);
  not not_10 (PA7, PPU_ADR[7]);
  not not_11 (PA8, PPU_ADR[8]);
  OAM_EVAL oam_eval_1 (
    .PCLK(PCLK), .nF_NT(control_unit_pal_1_nf_nt), .H0_prime_prime(H0_prime_prime), .I_OAM2(I_OAM2),
    .nVIS(nVIS), .SPR_OV(oam_control_pal_1_spr_ov), .S_EV(control_unit_pal_1_s_ev), .PAR_O(PAR_O),
    .O8_16(not_6_out), .OB0(oam_buffer_1_ob_bit_out[0]), .OB1(oam_buffer_1_ob_bit_out[1]),
    .OB2(oam_buffer_1_ob_bit_out[2]), .OB3(oam_buffer_1_ob_bit_out[3]), .OB4(oam_buffer_1_ob_bit_out[4]),
    .OB5(oam_buffer_1_ob_bit_out[5]), .OB6(oam_buffer_1_ob_bit_out[6]), .OB7(oam_buffer_1_ob_bit_out[7]),
    .V0(hv_select_pal_1_vpos[0]), .V1(hv_select_pal_1_vpos[1]), .V2(hv_select_pal_1_vpos[2]),
    .V3(hv_select_pal_1_vpos[3]), .V4(hv_select_pal_1_vpos[4]), .V5(hv_select_pal_1_vpos[5]),
    .V6(hv_select_pal_1_vpos[6]), .V7(hv_select_pal_1_vpos[7]), ._0_FIFO(oam_eval_1__0_fifo),
    .OMFG(oam_eval_1_omfg), .I2SEV(oam_eval_1_i2sev), .OV0(oam_eval_1_ov0[0]), .OV1(oam_eval_1_ov0[1]),
    .OV2(oam_eval_1_ov0[2]), .OV3(oam_eval_1_ov0[3]), .TEST(oam_eval_1_test));
  not not_12 (PA6, PPU_ADR[6]);
  CPU_DATA_IO cpu_data_io_1 (
    .nRD(rw_control_1_nrd), .nWR(rw_control_1_nwr), .PPU_CPU({R2DB7, R2DB6, R2DB5, color_io_1_db0_2}),
    .CPU_PPU(cpu_data_io_1_cpu_ppu), .D6_2(D6_2), .D7_2(D7_2), .D0(D0), .D1(D1), .D2(D2), .D3(D3), .D4(D4),
    .D5(D5), .D6(D6), .D7(D7), .D4_2(D4_2), .D5_2(D5_2), .D2_2(D2_2), .D3_2(D3_2), .D0_2(D0_2), .D1_2(D1_2));
  OAM_CONTROL_PAL oam_control_pal_1 (
    .PCLK(PCLK), .OFETCH(oam_buf_control_1_ofetch), .ZOMG_PAL(control_unit_pal_1_zomg_pal), .BLNK(BLNK),
    .nVIS(nVIS), .H0_prime_prime(H0_prime_prime), .I_OAM2(I_OAM2), .OMFG(oam_eval_1_omfg), .nDBE(nDBE),
    .nW3(register_select_1_nw3), .PAR_O(PAR_O), .DB0(cpu_data_io_1_cpu_ppu[0]),
    .DB1(cpu_data_io_1_cpu_ppu[1]), .DB2(cpu_data_io_1_cpu_ppu[2]), .DB3(cpu_data_io_1_cpu_ppu[3]),
    .DB4(cpu_data_io_1_cpu_ppu[4]), .DB5(cpu_data_io_1_cpu_ppu[5]), .DB6(cpu_data_io_1_cpu_ppu[6]),
    .DB7(cpu_data_io_1_cpu_ppu[7]), .EVAL(control_unit_pal_1_eval), .nH2_prime(nH2_prime),
    .H0_prime(H0_prime), .RESCL(RESCL), .nR2(nR2), .nOAM0(oam_control_pal_1_noam0[0]),
    .nOAM1(oam_control_pal_1_noam0[1]), .nOAM2(oam_control_pal_1_noam0[2]),
    .nOAM3(oam_control_pal_1_noam0[3]), .nOAM4(oam_control_pal_1_noam0[4]),
    .nOAM5(oam_control_pal_1_noam0[5]), .nOAM6(oam_control_pal_1_noam0[6]),
    .nOAM7(oam_control_pal_1_noam0[7]), .nOAM8(oam_control_pal_1_noam0[8]),
    .SPR_OV(oam_control_pal_1_spr_ov), .OAMCTR2(oam_control_pal_1_oamctr2), .DB5_2(R2DB5));
  CONTROL_REGS_PAL control_regs_pal_1 (
    .RC(RC), .nDBE(nDBE), .nW0(register_select_1_nw0), .DB0(cpu_data_io_1_cpu_ppu[0]),
    .DB1(cpu_data_io_1_cpu_ppu[1]), .DB2(cpu_data_io_1_cpu_ppu[2]), .DB3(cpu_data_io_1_cpu_ppu[3]),
    .DB4(cpu_data_io_1_cpu_ppu[4]), .DB5(cpu_data_io_1_cpu_ppu[5]), .DB6(cpu_data_io_1_cpu_ppu[6]),
    .DB7(cpu_data_io_1_cpu_ppu[7]), .nW1(register_select_1_nw1), .PCLK(PCLK), .nVIS(nVIS),
    .CLIP_B(control_unit_pal_1_clip_b), .CLIP_O(control_unit_pal_1_clip_o), .I1_32(control_regs_pal_1_i1_32),
    .OBSEL(control_regs_pal_1_obsel), .BGSEL(control_regs_pal_1_bgsel), .O8_16(control_regs_pal_1_o8_16),
    .nSLAVE(control_regs_pal_1_nslave), .VBL(control_regs_pal_1_vbl), .BW(control_regs_pal_1_bw),
    .nBGCLIP(control_regs_pal_1_nbgclip), .nOBCLIP(control_regs_pal_1_nobclip),
    .CLPB(control_regs_pal_1_clpb), .nCLPO(control_regs_pal_1_nclpo), .nTR(control_regs_pal_1_ntr[0]),
    .nTG(control_regs_pal_1_ntr[1]), .nTB(control_regs_pal_1_ntr[2]), .BLACK(control_regs_pal_1_black));
  SELECT_2_3_5_7_PIXEL select_2_3_5_7_pixel_1 (
    .PCLK(PCLK), .PAR_O(PAR_O), .H0_prime_prime(H0_prime_prime), .H1_prime_prime(Hnn_BUS[1]),
    .H2_prime_prime(Hnn_BUS[2]), .nSH2(select_2_3_5_7_pixel_1_nsh2[0]),
    .nSH3(select_2_3_5_7_pixel_1_nsh2[1]), .nSH5(select_2_3_5_7_pixel_1_nsh2[2]),
    .nSH7(select_2_3_5_7_pixel_1_nsh2[3]));
  MUX mux_1 (
    .EXT3_IN(mux_1_ext0_out[7]), .EXT2_IN(mux_1_ext0_out[5]), .EXT1_IN(mux_1_ext0_out[3]),
    .EXT0_IN(mux_1_ext0_out[1]), .PCLK(PCLK), .BGC0(bg_color_1_bgc0[0]), .BGC1(bg_color_1_bgc0[1]),
    .BGC2(bg_color_1_bgc0[2]), .BGC3(bg_color_1_bgc0[3]), .nZCOL0(oam_fifo_1_nzcol0[0]),
    .nZCOL1(oam_fifo_1_nzcol0[1]), .ZCOL2(oam_fifo_1_nzcol0[2]), .ZCOL3(oam_fifo_1_nzcol0[3]),
    .nZPRIO(oam_fifo_1_nzcol0[4]), .THO0(TH[0]), .THO1(TH[1]), .THO2(TH[2]), .THO3(TH[3]), .THO4(TH[4]),
    .TH_MUX(TH_MUX), .nSPR0HIT(oam_fifo_1_nspr0hit), .I2SEV(oam_eval_1_i2sev), .nVIS(nVIS), .RESCL(RESCL),
    .nDBE(nDBE), .nR2(nR2), .EXT0_OUT(mux_1_ext0_out[0]), .EXT1_OUT(mux_1_ext0_out[2]),
    .EXT2_OUT(mux_1_ext0_out[4]), .EXT3_OUT(mux_1_ext0_out[6]), .PAL0(mux_1_pal0[0]), .PAL1(mux_1_pal0[1]),
    .PAL2(mux_1_pal0[2]), .PAL3(mux_1_pal0[3]), .PAL4(mux_1_pal0[4]), .DB6(R2DB6));
  VRAM_BUS_CONTROL vram_bus_control_1 (
    .PCLK(PCLK), .nR7(nR7), .nDBE(nDBE), .nW7(nW7), .BLNK(BLNK), .H0_prime(H0_prime), .nPA8(PPU_ADR[8]),
    .nPA9(PPU_ADR[9]), .nPA10(PPU_ADR[10]), .nPA11(PPU_ADR[11]), .nPA12(PPU_ADR[12]), .nPA13(PPU_ADR[13]),
    .TSTEP(vram_bus_control_1_tstep), .PD_RB(vram_bus_control_1_pd_rb), .DB_PAR(DB_PAR),
    .nALE(vram_bus_control_1_nale), .RD(nRD), .WR(nWR), .XRB(vram_bus_control_1_xrb), .TH_MUX(TH_MUX));
  not not_13 (PA4, PPU_ADR[4]);
  not not_14 (PA5, PPU_ADR[5]);
  not not_15 (PA2, PPU_ADR[2]);
  not not_16 (PA3, PPU_ADR[3]);
  not not_17 (PA1, PPU_ADR[1]);
  not not_18 (PA0, PPU_ADR[0]);
  not not_19 (ALE, vram_bus_control_1_nale);
  not not_20 (not_20_out, control_regs_pal_1_o8_16);
  not not_21 (not_21_out, control_regs_pal_1_i1_32);
  not not_22 (not_22_out, oam_buf_control_1_nwe);
  assign controlled_buffer_1_out = not_23_out ? oam_control_pal_1_noam0[7:0] : 8'bz;  // Controlled_Buffer controlled_buffer_1
  not not_23 (not_23_out, oam_control_pal_1_noam0[8]);
  Demultiplexer #(.width(8), .enable("false")) demultiplexer_1 (
    .out0(demultiplexer_1_out0), .out1(demultiplexer_1_out1), .in(oam_buffer_1_ram_write),
    .sel(oam_control_pal_1_noam0[8]));
  assign controlled_buffer_2_out = oam_control_pal_1_noam0[8] ? oam_control_pal_1_noam0[7:3] : 5'bz;  // Controlled_Buffer controlled_buffer_2
  Hex_Digit_Display hex_digit_display_1 (.value(oam_control_pal_1_noam0[7:4]));  // open: dp
  Hex_Digit_Display hex_digit_display_2 (.value({3'b000, oam_control_pal_1_noam0[8]}));  // open: dp
  not not_24 (not_24_out, oam_control_pal_1_noam0[8]);
  EXT_IO ext_io_1 (
    .PCLK(PCLK), .EXT0_OUT(mux_1_ext0_out[0]), .EXT0_IN(mux_1_ext0_out[1]), .EXT1_OUT(mux_1_ext0_out[2]),
    .EXT1_IN(mux_1_ext0_out[3]), .EXT2_OUT(mux_1_ext0_out[4]), .EXT2_IN(mux_1_ext0_out[5]),
    .EXT3_OUT(mux_1_ext0_out[6]), .EXT3_IN(mux_1_ext0_out[7]), .nSLAVE(control_regs_pal_1_nslave),
    .EXT0_2(EXT0_2), .EXT0(EXT0), .EXT1_2(EXT1_2), .EXT1(EXT1), .EXT2_2(EXT2_2), .EXT2(EXT2),
    .EXT3_2(EXT3_2), .EXT3(EXT3));
  OAM_BUF_CONTROL oam_buf_control_1 (
    .PCLK(PCLK), .BLNK(BLNK), .SPR_OV(oam_control_pal_1_spr_ov), .nVIS(nVIS),
    .OAMCTR2(oam_control_pal_1_oamctr2), .H0_prime_prime(H0_prime_prime), .nW4(register_select_1_nw4),
    .nDBE(nDBE), .OB_OAM(oam_buf_control_1_ob_oam), .nWE(oam_buf_control_1_nwe),
    .OFETCH(oam_buf_control_1_ofetch));
  Hex_Digit_Display hex_digit_display_3 (.value(oam_control_pal_1_noam0[3:0]));  // open: dp
  not not_25 (not_25_out, not_22_out);
  not not_26 (not_26_out, not_22_out);
  WRITE__2007 write__2007_1 (
    .PCLK(PCLK), .DB_PAR(DB_PAR), .D0(cpu_data_io_1_cpu_ppu[0]), .D1(cpu_data_io_1_cpu_ppu[1]),
    .D2(cpu_data_io_1_cpu_ppu[2]), .D3(cpu_data_io_1_cpu_ppu[3]), .D4(cpu_data_io_1_cpu_ppu[4]),
    .D5(cpu_data_io_1_cpu_ppu[5]), .D6(cpu_data_io_1_cpu_ppu[6]), .D7(cpu_data_io_1_cpu_ppu[7]), .PD0(PD0_W),
    .PD1(PD1_W), .PD2(PD2_W), .PD3(PD3_W), .PD4(PD4_W), .PD5(PD5_W), .PD6(PD6_W), .PD7(PD7_W));
  OAM_BUFFER oam_buffer_1 (
    .PCLK(PCLK), .nR4(register_select_1_nr4), .OAM___DB({R2DB7, R2DB6, R2DB5, color_io_1_db0_2}),
    .I_OAM2(I_OAM2), .OB_bit_out(oam_buffer_1_ob_bit_out), .RAM_read(multiplexer_1_out),
    .OB_OAM(oam_buf_control_1_ob_oam), .DB___OAM(cpu_data_io_1_cpu_ppu), .BLNK(BLNK),
    .nWE(oam_buf_control_1_nwe), .RAM_write(oam_buffer_1_ram_write));
  RAM #(.bus("separate")) ram_2 (
    .addr(controlled_buffer_1_out), .din(demultiplexer_1_out0), .data(ram_2_data), .str(not_22_out),
    .sel(not_24_out), .clk(PCLK[0]), .ld(not_25_out));  // open: clr
  RAM #(.addrWidth(5), .bus("separate")) ram_3 (
    .addr(controlled_buffer_2_out), .din(demultiplexer_1_out1), .data(ram_3_data), .str(not_22_out),
    .sel(oam_control_pal_1_noam0[8]), .clk(PCLK[0]), .ld(not_26_out));  // open: clr
  Hex_Digit_Display hex_digit_display_4 (.value(multiplexer_1_out[3:0]));  // open: dp
  Hex_Digit_Display hex_digit_display_5 (.value(multiplexer_1_out[7:4]));  // open: dp
  Multiplexer #(.width(8), .enable("false")) multiplexer_1 (
    .in0(ram_2_data), .in1(ram_3_data), .out(multiplexer_1_out), .sel(oam_control_pal_1_noam0[8]));
  PICTURE_ADDRESS_GEN picture_address_gen_1 (
    .PCLK(PCLK), .SC_CNT(control_unit_pal_1_sc_cnt), .RESCL(RESCL), .E_EV(control_unit_pal_1_e_ev),
    .TSTEP(vram_bus_control_1_tstep), .F_TB(control_unit_pal_1_f_tb), .H0_prime_prime(H0_prime_prime),
    .BLNK(BLNK), .l1_32(not_21_out), .PD0(PD0), .PD1(PD1), .PD2(PD2), .PD3(PD3), .PD4(PD4), .PD5(PD5),
    .PD6(PD6), .PD7(PD7), .OB0(oam_buffer_1_ob_bit_out[0]), .OB1(oam_buffer_1_ob_bit_out[1]),
    .OB2(oam_buffer_1_ob_bit_out[2]), .OB3(oam_buffer_1_ob_bit_out[3]), .OB4(oam_buffer_1_ob_bit_out[4]),
    .OB5(oam_buffer_1_ob_bit_out[5]), .OB6(oam_buffer_1_ob_bit_out[6]), .OB7(oam_buffer_1_ob_bit_out[7]),
    .OV0(oam_eval_1_ov0[0]), .OV1(oam_eval_1_ov0[1]), .OV2(oam_eval_1_ov0[2]), .OV3(oam_eval_1_ov0[3]),
    .DB0(cpu_data_io_1_cpu_ppu[0]), .DB1(cpu_data_io_1_cpu_ppu[1]), .DB2(cpu_data_io_1_cpu_ppu[2]),
    .DB3(cpu_data_io_1_cpu_ppu[3]), .DB4(cpu_data_io_1_cpu_ppu[4]), .DB5(cpu_data_io_1_cpu_ppu[5]),
    .DB6(cpu_data_io_1_cpu_ppu[6]), .DB7(cpu_data_io_1_cpu_ppu[7]), .nW0(register_select_1_nw0),
    .nW5_2(register_select_1_nw5_2), .nW6_1(register_select_1_nw6_1), .nW5_1(register_select_1_nw5_1),
    .nW6_2(register_select_1_nw6_2), .nDBE(nDBE), .RC(RC), .nPA0(PPU_ADR[0]), .nPA1(PPU_ADR[1]),
    .nPA2(PPU_ADR[2]), .nPA3(PPU_ADR[3]), .nPA4(PPU_ADR[4]), .nPA5(PPU_ADR[5]), .nPA6(PPU_ADR[6]),
    .nPA7(PPU_ADR[7]), .nPA8(PPU_ADR[8]), .nPA9(PPU_ADR[9]), .nPA10(PPU_ADR[10]), .nPA11(PPU_ADR[11]),
    .nPA12(PPU_ADR[12]), .FH0(picture_address_gen_1_fh0[0]), .nPA13(PPU_ADR[13]),
    .FH1(picture_address_gen_1_fh0[1]), .FH2(picture_address_gen_1_fh0[2]), .THO0(TH[0]), .THO1(TH[1]),
    .THO2(TH[2]), .THO3(TH[3]), .THO4(TH[4]), .TVO1(picture_address_gen_1_tvo1),
    .F_AT(control_unit_pal_1_f_at), .nF_NT(control_unit_pal_1_nf_nt), .PAR_O(PAR_O),
    .nSH2(select_2_3_5_7_pixel_1_nsh2[0]), .O8_16(not_20_out), .OBSEL(control_regs_pal_1_obsel),
    .BGSEL(control_regs_pal_1_bgsel), .nH2_prime(nH2_prime), .nH1_prime(nH1_prime), .DB_PAR(1'b0));
  BG_COLOR bg_color_1 (
    .PCLK(PCLK), .CLPB(control_regs_pal_1_clpb), .FH0(picture_address_gen_1_fh0[0]),
    .FH1(picture_address_gen_1_fh0[1]), .FH2(picture_address_gen_1_fh0[2]), .PD0(PD0), .PD1(PD1), .PD2(PD2),
    .PD3(PD3), .PD4(PD4), .PD5(PD5), .PD6(PD6), .PD7(PD7), .THO1(TH[0]), .TVO1(picture_address_gen_1_tvo1),
    .F_AT(control_unit_pal_1_f_at), .H0_prime_prime(H0_prime_prime), .F_TA(control_unit_pal_1_f_ta),
    .F_TB(control_unit_pal_1_f_tb), .nFO(control_unit_pal_1_nfo), .BGC0(bg_color_1_bgc0[0]),
    .BGC1(bg_color_1_bgc0[1]), .BGC2(bg_color_1_bgc0[2]), .BGC3(bg_color_1_bgc0[3]));

  // Other names for the same wires on the sheet: Hnn_BUS[0] = H0_prime_prime;
  //   PPU_DATA[7:0] = {PD7, PD6, PD5, PD4, PD3, PD2, PD1, PD0};
  //   PPU_DATA_W[7:0] = {PD7_W, PD6_W, PD5_W, PD4_W, PD3_W, PD2_W, PD1_W, PD0_W}

  // Notes on the sheet:
  //   Manual cleaning
  //   2C07 PPU
  //   CPU INTERFACE
  //   !!!PAL
  //   Logisim doesn't support bidirectional pads and wires
  //   So we have to add workaround by separate I/O wires
  //   VRAM INTERFACE
  //   PAL!!!
  //   EXT INTERFACE
  //   Logisim doesn't support bidirectional pads and wires
  //   So we have to add workaround by separate I/O wires
endmodule

module D_latch (
  input  EN,
  input  D,
  output Q,
  output nQ
);

  D_Flip_Flop #(.trigger("high")) d_ff_1 (.clk(EN), .D(D), .Q(Q), .Qn(nQ));  // open: preset, en, reset
endmodule

module PIXEL_CLOCK_NTSC (
  input  nCLK,
  input  RES,
  output [1:0] PCLK,
  output PCLK_2,
  output nPCLK
);

  wire _2_out, _3_out, d_latch_1_nq, d_latch_2_nq, d_latch_3_nq, nor_1_out, not_1_out, not_2_out,
       transistor_1_out, transistor_3_out, transistor_5_out, transistor_6_out, transistor_14_out;

  not not_1 (not_1_out, nCLK);
  nor nor_1 (nor_1_out, RES, PCLK[0]);
  not not_2 (not_2_out, PCLK[0]);
  D_latch d_latch_1 (.EN(not_1_out), .D(nor_1_out), .nQ(d_latch_1_nq));  // open: Q
  nor _3 (_3_out, PCLK[0], _2_out);
  nor _2 (_2_out, _3_out, not_2_out);
  D_latch d_latch_2 (.EN(nCLK), .D(d_latch_1_nq), .nQ(d_latch_2_nq));  // open: Q
  D_latch d_latch_3 (.EN(not_1_out), .D(d_latch_2_nq), .nQ(d_latch_3_nq));  // open: Q
  D_latch d_latch_4 (.EN(nCLK), .D(d_latch_3_nq), .Q(PCLK[1]), .nQ(PCLK[0]));
  Transistor #(.\type ("n")) transistor_1 (.in(1'b1), .out(transistor_1_out), .gate(_3_out));
  Transistor #(.\type ("n")) transistor_2 (.in(1'b0), .out(transistor_1_out), .gate(_2_out));
  Transistor #(.\type ("n")) transistor_3 (.in(1'b1), .out(transistor_3_out), .gate(_2_out));
  Transistor #(.\type ("n")) transistor_4 (.in(1'b0), .out(transistor_3_out), .gate(_3_out));
  Transistor #(.\type ("n")) transistor_5 (.in(1'b1), .out(transistor_5_out), .gate(transistor_3_out));
  Transistor #(.\type ("n")) transistor_6 (.in(1'b1), .out(transistor_6_out), .gate(transistor_3_out));
  Transistor #(.\type ("n")) transistor_7 (.in(1'b0), .out(transistor_5_out), .gate(transistor_1_out));
  Transistor #(.\type ("n")) transistor_8 (.in(1'b0), .out(transistor_6_out), .gate(transistor_1_out));
  Transistor #(.\type ("n")) transistor_9 (.in(1'b1), .out(nPCLK), .gate(transistor_1_out));
  Transistor #(.\type ("n")) transistor_10 (.in(1'b1), .out(nPCLK), .gate(transistor_1_out));
  Transistor #(.\type ("n")) transistor_11 (.in(1'b0), .out(nPCLK), .gate(transistor_3_out));
  Transistor #(.\type ("n")) transistor_12 (.in(1'b0), .out(nPCLK), .gate(transistor_3_out));
  Transistor #(.\type ("n")) transistor_13 (.in(1'b1), .out(PCLK_2), .gate(transistor_3_out));
  Transistor #(.\type ("n")) transistor_14 (.in(1'b1), .out(transistor_14_out), .gate(transistor_3_out));
  Transistor #(.\type ("n")) transistor_15 (.in(1'b0), .out(PCLK_2), .gate(transistor_1_out));
  Transistor #(.\type ("n")) transistor_16 (.in(1'b0), .out(transistor_14_out), .gate(transistor_1_out));
  Transistor #(.\type ("n")) transistor_17 (.in(1'b1), .out(nPCLK), .gate(transistor_1_out));
  Transistor #(.\type ("n")) transistor_18 (.in(1'b1), .out(nPCLK), .gate(transistor_1_out));
  Transistor #(.\type ("n")) transistor_19 (.in(1'b0), .out(nPCLK), .gate(transistor_3_out));
  Transistor #(.\type ("n")) transistor_20 (.in(1'b0), .out(nPCLK), .gate(transistor_3_out));

  // Notes on the sheet:
  //   1
  //   PCLK = CLK / 4
  //   Pixel clock is disabled during RESET (PPU stall)
  //   PCLK DISTRIBUTION
  //   I
  //   II
  //   PCLK
endmodule

module PIXEL_CLOCK_PAL (
  input  nCLK,
  input  RES,
  output [1:0] PCLK,
  output PCLK_2,
  output nPCLK
);

  wire _2_out, _3_2_out, _3_out, d_latch_1_q, d_latch_2_nq, d_latch_3_nq, d_latch_4_nq, d_latch_5_nq,
       d_latch_6_nq, nor_1_out, not_1_out, not_2_out, not_3_out, transistor_1_out, transistor_3_out;

  not not_1 (not_1_out, nCLK);
  not not_2 (not_2_out, PCLK[0]);
  D_latch d_latch_1 (.EN(nCLK), .D(_3_2_out), .Q(d_latch_1_q));  // open: nQ
  D_latch d_latch_2 (.EN(not_1_out), .D(nor_1_out), .nQ(d_latch_2_nq));  // open: Q
  nor nor_1 (nor_1_out, d_latch_1_q, RES);
  nor _3 (_3_out, PCLK[0], _2_out);
  nor _2 (_2_out, _3_out, not_2_out);
  D_latch d_latch_3 (.EN(nCLK), .D(d_latch_2_nq), .nQ(d_latch_3_nq));  // open: Q
  D_latch d_latch_4 (.EN(not_1_out), .D(d_latch_3_nq), .nQ(d_latch_4_nq));  // open: Q
  Transistor #(.\type ("n")) transistor_1 (.in(1'b1), .out(transistor_1_out), .gate(_3_out));
  Transistor #(.\type ("n")) transistor_2 (.in(1'b0), .out(transistor_1_out), .gate(_2_out));
  Transistor #(.\type ("n")) transistor_3 (.in(1'b1), .out(transistor_3_out), .gate(_2_out));
  Transistor #(.\type ("n")) transistor_4 (.in(1'b0), .out(transistor_3_out), .gate(_3_out));
  D_latch d_latch_5 (.EN(nCLK), .D(d_latch_4_nq), .nQ(d_latch_5_nq));  // open: Q
  Transistor #(.\type ("n")) transistor_5 (.in(1'b1), .out(PCLK_2), .gate(transistor_3_out));
  Transistor #(.\type ("n")) transistor_6 (.in(1'b0), .out(PCLK_2), .gate(transistor_1_out));
  Transistor #(.\type ("n")) transistor_7 (.in(1'b1), .out(nPCLK), .gate(transistor_1_out));
  Transistor #(.\type ("n")) transistor_8 (.in(1'b0), .out(nPCLK), .gate(transistor_3_out));
  D_latch d_latch_6 (.EN(not_1_out), .D(d_latch_5_nq), .nQ(d_latch_6_nq));  // open: Q
  not not_3 (not_3_out, d_latch_5_nq);
  Transistor #(.\type ("n")) transistor_9 (.in(1'b1), .out(PCLK_2), .gate(transistor_3_out));
  Transistor #(.\type ("n")) transistor_10 (.in(1'b1), .out(PCLK_2), .gate(transistor_3_out));
  Transistor #(.\type ("n")) transistor_11 (.in(1'b0), .out(PCLK_2), .gate(transistor_1_out));
  Transistor #(.\type ("n")) transistor_12 (.in(1'b0), .out(PCLK_2), .gate(transistor_1_out));
  Transistor #(.\type ("n")) transistor_13 (.in(1'b1), .out(nPCLK), .gate(transistor_1_out));
  Transistor #(.\type ("n")) transistor_14 (.in(1'b1), .out(nPCLK), .gate(transistor_1_out));
  Transistor #(.\type ("n")) transistor_15 (.in(1'b0), .out(nPCLK), .gate(transistor_3_out));
  Transistor #(.\type ("n")) transistor_16 (.in(1'b0), .out(nPCLK), .gate(transistor_3_out));
  nor _2_2 (PCLK[0], d_latch_6_nq, not_3_out);
  nor _3_2 (_3_2_out, d_latch_6_nq, d_latch_4_nq);
  Transistor #(.\type ("n")) transistor_17 (.in(1'b1), .out(PCLK_2), .gate(transistor_3_out));
  Transistor #(.\type ("n")) transistor_18 (.in(1'b0), .out(PCLK_2), .gate(transistor_1_out));
  Transistor #(.\type ("n")) transistor_19 (.in(1'b1), .out(nPCLK), .gate(transistor_1_out));
  Transistor #(.\type ("n")) transistor_20 (.in(1'b0), .out(nPCLK), .gate(transistor_3_out));
  not not_4 (PCLK[1], PCLK[0]);

  // Notes on the sheet:
  //   9
  //   1
  //   8
  //   Pixel clock is disabled during RESET (PPU stall)
  //   7
  //   PCLK = CLK / 5
  //   PCLK DISTRIBUTION
  //   6
  //   I
  //   II
  //   5
  //   4
  //   1
  //   !
endmodule

module RESET_FF (
  input  nRES,
  input  RESCL,
  output RES,
  output RC
);

  wire nor_1_out;

  not not_1 (RES, nRES);
  nor nor_1 (nor_1_out, RES, RC);
  nor nor_2 (RC, nor_1_out, RESCL);

  // Notes on the sheet:
  //   Reset flip/flop remains set after RESET, until not cleared by RESCL
  //   Reset flip/flop
  //   (REG CLEAR)
endmodule

module HV_COUNTER_BIT (
  input  [1:0] PCLK,
  input  clear,
  input  in,
  input  RES,
  output Q,
  output nQ,
  output carry_out
);

  wire d_latch_1_q, d_latch_2_q, multiplexer_1_out, multiplexer_2_out, nor_1_out, nor_2_out, nor_3_out,
       nor_4_out, not_1_out, not_2_out, not_3_out, undriven, undriven_2, undriven_4, xor_1_out;
  wire [1:0] undriven_3;

  xor xor_1 (xor_1_out, in, nQ);
  D_latch d_latch_1 (.EN(PCLK[1]), .D(xor_1_out), .Q(d_latch_1_q));  // open: nQ
  not not_1 (not_1_out, multiplexer_1_out);
  nor nor_1 (nor_1_out, not_1_out, undriven_2);
  nor nor_2 (nor_2_out, not_1_out, not_2_out);
  not not_2 (not_2_out, undriven);
  nor nor_3 (nor_3_out, clear, d_latch_1_q);
  Multiplexer #(.enable("false")) multiplexer_1 (
    .in0(nor_1_out), .in1(nor_4_out), .out(multiplexer_1_out), .sel(undriven_3[0]));
  D_Flip_Flop #(.trigger("high")) d_ff_1 (
    .clk(PCLK[0]), .D(nor_3_out), .Q(Q), .Qn(nQ), .reset(RES));  // open: preset, en
  Multiplexer #(.enable("false")) multiplexer_2 (
    .in0(not_1_out), .in1(nor_1_out), .out(multiplexer_2_out), .sel(undriven));
  nor nor_4 (nor_4_out, d_latch_2_q, undriven_4);
  nor nor_5 (carry_out, nQ, not_3_out);
  not not_3 (not_3_out, in);
  D_latch d_latch_2 (.EN(undriven_3[1]), .D(multiplexer_2_out), .Q(d_latch_2_q));  // open: nQ

  // Notes on the sheet:
  //   clear manually
  //   carry_in
  //   global RESET
  //   carry_in
  //   global RESET
  //   clear manually
endmodule
module H_COUNTER (
  input  RES,
  input  HC,
  input  [1:0] PCLK,
  output H0,
  output H1,
  output H2,
  output H3,
  output H4,
  output H5,
  output H6,
  output H7,
  output H8
);

  wire hv_counter_bit_1_carry_out, hv_counter_bit_1_nq, hv_counter_bit_2_carry_out, hv_counter_bit_2_nq,
       hv_counter_bit_3_carry_out, hv_counter_bit_3_nq, hv_counter_bit_4_carry_out, hv_counter_bit_4_nq,
       hv_counter_bit_5_nq, hv_counter_bit_6_carry_out, hv_counter_bit_6_nq, hv_counter_bit_7_carry_out,
       hv_counter_bit_7_nq, hv_counter_bit_8_carry_out, hv_counter_bit_8_nq, hv_counter_bit_9_nq, nor_1_out;

  HV_COUNTER_BIT hv_counter_bit_1 (
    .PCLK(PCLK), .in(1'b1), .RES(RES), .clear(HC), .Q(H0), .nQ(hv_counter_bit_1_nq),
    .carry_out(hv_counter_bit_1_carry_out));
  HV_COUNTER_BIT hv_counter_bit_2 (
    .PCLK(PCLK), .in(hv_counter_bit_1_carry_out), .RES(RES), .clear(HC), .Q(H1), .nQ(hv_counter_bit_2_nq),
    .carry_out(hv_counter_bit_2_carry_out));
  HV_COUNTER_BIT hv_counter_bit_3 (
    .PCLK(PCLK), .in(hv_counter_bit_2_carry_out), .RES(RES), .clear(HC), .Q(H2), .nQ(hv_counter_bit_3_nq),
    .carry_out(hv_counter_bit_3_carry_out));
  HV_COUNTER_BIT hv_counter_bit_4 (
    .PCLK(PCLK), .in(hv_counter_bit_3_carry_out), .RES(RES), .clear(HC), .Q(H3), .nQ(hv_counter_bit_4_nq),
    .carry_out(hv_counter_bit_4_carry_out));
  HV_COUNTER_BIT hv_counter_bit_5 (
    .PCLK(PCLK), .in(hv_counter_bit_4_carry_out), .RES(RES), .clear(HC), .Q(H4), .nQ(hv_counter_bit_5_nq));  // open: carry_out
  nor nor_1 (nor_1_out, hv_counter_bit_5_nq, hv_counter_bit_4_nq, hv_counter_bit_3_nq, hv_counter_bit_2_nq, hv_counter_bit_1_nq);
  HV_COUNTER_BIT hv_counter_bit_6 (
    .PCLK(PCLK), .in(nor_1_out), .RES(RES), .clear(HC), .Q(H5), .nQ(hv_counter_bit_6_nq),
    .carry_out(hv_counter_bit_6_carry_out));
  HV_COUNTER_BIT hv_counter_bit_7 (
    .PCLK(PCLK), .in(hv_counter_bit_6_carry_out), .RES(RES), .clear(HC), .Q(H6), .nQ(hv_counter_bit_7_nq),
    .carry_out(hv_counter_bit_7_carry_out));
  HV_COUNTER_BIT hv_counter_bit_8 (
    .PCLK(PCLK), .in(hv_counter_bit_7_carry_out), .RES(RES), .clear(HC), .Q(H7), .nQ(hv_counter_bit_8_nq),
    .carry_out(hv_counter_bit_8_carry_out));
  HV_COUNTER_BIT hv_counter_bit_9 (
    .PCLK(PCLK), .in(hv_counter_bit_8_carry_out), .RES(RES), .clear(HC), .Q(H8), .nQ(hv_counter_bit_9_nq));  // open: carry_out

  // Notes on the sheet:
  //   reduce propagation delay
endmodule

module V_COUNTER (
  input  VIN,
  input  [1:0] PCLK,
  input  VC,
  input  RES,
  output V0,
  output V1,
  output V2,
  output V3,
  output V4,
  output V5,
  output V6,
  output V7,
  output V8
);

  wire hv_counter_bit_1_carry_out, hv_counter_bit_1_nq, hv_counter_bit_2_carry_out, hv_counter_bit_2_nq,
       hv_counter_bit_3_carry_out, hv_counter_bit_3_nq, hv_counter_bit_4_carry_out, hv_counter_bit_4_nq,
       hv_counter_bit_5_nq, hv_counter_bit_6_carry_out, hv_counter_bit_6_nq, hv_counter_bit_7_carry_out,
       hv_counter_bit_7_nq, hv_counter_bit_8_carry_out, hv_counter_bit_8_nq, hv_counter_bit_9_nq, nor_1_out,
       not_1_out;

  HV_COUNTER_BIT hv_counter_bit_1 (
    .PCLK(PCLK), .in(VIN), .RES(RES), .clear(VC), .Q(V0), .nQ(hv_counter_bit_1_nq),
    .carry_out(hv_counter_bit_1_carry_out));
  HV_COUNTER_BIT hv_counter_bit_2 (
    .PCLK(PCLK), .in(hv_counter_bit_1_carry_out), .RES(RES), .clear(VC), .Q(V1), .nQ(hv_counter_bit_2_nq),
    .carry_out(hv_counter_bit_2_carry_out));
  HV_COUNTER_BIT hv_counter_bit_3 (
    .PCLK(PCLK), .in(hv_counter_bit_2_carry_out), .RES(RES), .clear(VC), .Q(V2), .nQ(hv_counter_bit_3_nq),
    .carry_out(hv_counter_bit_3_carry_out));
  HV_COUNTER_BIT hv_counter_bit_4 (
    .PCLK(PCLK), .in(hv_counter_bit_3_carry_out), .RES(RES), .clear(VC), .Q(V3), .nQ(hv_counter_bit_4_nq),
    .carry_out(hv_counter_bit_4_carry_out));
  HV_COUNTER_BIT hv_counter_bit_5 (
    .PCLK(PCLK), .in(hv_counter_bit_4_carry_out), .RES(RES), .clear(VC), .Q(V4), .nQ(hv_counter_bit_5_nq));  // open: carry_out
  HV_COUNTER_BIT hv_counter_bit_6 (
    .PCLK(PCLK), .in(nor_1_out), .RES(RES), .clear(VC), .Q(V5), .nQ(hv_counter_bit_6_nq),
    .carry_out(hv_counter_bit_6_carry_out));
  HV_COUNTER_BIT hv_counter_bit_7 (
    .PCLK(PCLK), .in(hv_counter_bit_6_carry_out), .RES(RES), .clear(VC), .Q(V6), .nQ(hv_counter_bit_7_nq),
    .carry_out(hv_counter_bit_7_carry_out));
  HV_COUNTER_BIT hv_counter_bit_8 (
    .PCLK(PCLK), .in(hv_counter_bit_7_carry_out), .RES(RES), .clear(VC), .Q(V7), .nQ(hv_counter_bit_8_nq),
    .carry_out(hv_counter_bit_8_carry_out));
  HV_COUNTER_BIT hv_counter_bit_9 (
    .PCLK(PCLK), .in(hv_counter_bit_8_carry_out), .RES(RES), .clear(VC), .Q(V8), .nQ(hv_counter_bit_9_nq));  // open: carry_out
  not not_1 (not_1_out, VIN);
  nor nor_1 (nor_1_out, hv_counter_bit_5_nq, hv_counter_bit_4_nq, hv_counter_bit_3_nq, hv_counter_bit_2_nq, hv_counter_bit_1_nq, not_1_out);

  // Notes on the sheet:
  //   reduce propagation delay
endmodule

// HV SELECT
module HV_SELECT_NTSC (
  input  H8,
  input  H7,
  input  H6,
  input  H5,
  input  H4,
  input  H3,
  input  H2,
  input  H1,
  input  H0,
  input  VB,
  input  BLNK,
  input  V8,
  input  V7,
  input  V6,
  input  V5,
  input  V4,
  input  V3,
  input  V2,
  input  V1,
  input  V0,
  output [5:0] Hnn,
  output HPLA_0,
  output HPLA_1,
  output HPLA_2,
  output HPLA_3,
  output HPLA_4,
  output HPLA_5,
  output HPLA_6,
  output HPLA_7,
  output HPLA_8,
  output HPLA_9,
  output HPLA_10,
  output HPLA_11,
  output HPLA_12,
  output HPLA_13,
  output HPLA_14,
  output HPLA_15,
  output HPLA_16,
  output HPLA_17,
  output HPLA_18,
  output HPLA_19,
  output HPLA_20,
  output HPLA_21,
  output HPLA_22,
  output HPLA_23,
  output [7:0] VPOS,
  output VPLA_0,
  output VPLA_1,
  output VPLA_2,
  output VPLA_3,
  output VPLA_4,
  output VPLA_5,
  output VPLA_6,
  output VPLA_7,
  output VPLA_8
);

  wire not_1_out, not_2_out, not_3_out, not_4_out, not_5_out, not_6_out, not_7_out, not_8_out, not_9_out,
       not_10_out, not_11_out, not_12_out, not_13_out, not_14_out, not_15_out, not_16_out, not_17_out;

  not not_1 (not_1_out, H8);
  not not_2 (not_2_out, H7);
  not not_3 (not_3_out, H6);
  not not_4 (not_4_out, H5);
  not not_5 (not_5_out, H4);
  not not_6 (not_6_out, H3);
  not not_7 (not_7_out, H2);
  not not_8 (not_8_out, H1);
  not not_9 (not_9_out, H0);
  not not_10 (not_10_out, V8);
  not not_11 (not_11_out, V7);
  not not_12 (not_12_out, V6);
  not not_13 (not_13_out, V5);
  not not_14 (not_14_out, V4);
  not not_15 (not_15_out, V2);
  not not_16 (not_16_out, V1);
  not not_17 (not_17_out, V0);
  Pull_Resistor #(.pull(1)) pull_resistor_1 (.node(HPLA_0));
  Transistor #(.\type ("n")) transistor_1 (.in(1'b0), .out(HPLA_0), .gate(not_1_out));
  Transistor #(.\type ("n")) transistor_2 (.in(1'b0), .out(HPLA_0), .gate(H7));
  Transistor #(.\type ("n")) transistor_3 (.in(1'b0), .out(HPLA_0), .gate(H6));
  Transistor #(.\type ("n")) transistor_4 (.in(1'b0), .out(HPLA_0), .gate(H5));
  Transistor #(.\type ("n")) transistor_5 (.in(1'b0), .out(HPLA_0), .gate(not_5_out));
  Transistor #(.\type ("n")) transistor_6 (.in(1'b0), .out(HPLA_0), .gate(H3));
  Transistor #(.\type ("n")) transistor_7 (.in(1'b0), .out(HPLA_0), .gate(not_7_out));
  Transistor #(.\type ("n")) transistor_8 (.in(1'b0), .out(HPLA_0), .gate(not_8_out));
  Transistor #(.\type ("n")) transistor_9 (.in(1'b0), .out(HPLA_0), .gate(not_9_out));
  Pull_Resistor #(.pull(1)) pull_resistor_2 (.node(VPLA_0));
  Transistor #(.\type ("n")) transistor_10 (.in(1'b0), .out(VPLA_0), .gate(not_11_out));
  Transistor #(.\type ("n")) transistor_11 (.in(1'b0), .out(VPLA_0), .gate(not_12_out));
  Transistor #(.\type ("n")) transistor_12 (.in(1'b0), .out(VPLA_0), .gate(not_13_out));
  Transistor #(.\type ("n")) transistor_13 (.in(1'b0), .out(VPLA_0), .gate(not_14_out));
  Transistor #(.\type ("n")) transistor_14 (.in(1'b0), .out(VPLA_0), .gate(V3));
  Transistor #(.\type ("n")) transistor_15 (.in(1'b0), .out(VPLA_0), .gate(not_15_out));
  Transistor #(.\type ("n")) transistor_16 (.in(1'b0), .out(VPLA_0), .gate(not_16_out));
  Transistor #(.\type ("n")) transistor_17 (.in(1'b0), .out(VPLA_0), .gate(not_17_out));
  Pull_Resistor #(.pull(1)) pull_resistor_3 (.node(HPLA_1));
  Transistor #(.\type ("n")) transistor_18 (.in(1'b0), .out(HPLA_1), .gate(not_1_out));
  Transistor #(.\type ("n")) transistor_19 (.in(1'b0), .out(HPLA_1), .gate(H7));
  Transistor #(.\type ("n")) transistor_20 (.in(1'b0), .out(HPLA_1), .gate(H6));
  Transistor #(.\type ("n")) transistor_21 (.in(1'b0), .out(HPLA_1), .gate(H5));
  Transistor #(.\type ("n")) transistor_22 (.in(1'b0), .out(HPLA_1), .gate(H4));
  Transistor #(.\type ("n")) transistor_23 (.in(1'b0), .out(HPLA_1), .gate(H3));
  Transistor #(.\type ("n")) transistor_24 (.in(1'b0), .out(HPLA_1), .gate(H2));
  Transistor #(.\type ("n")) transistor_25 (.in(1'b0), .out(HPLA_1), .gate(H1));
  Transistor #(.\type ("n")) transistor_26 (.in(1'b0), .out(HPLA_1), .gate(H0));
  Pull_Resistor #(.pull(1)) pull_resistor_4 (.node(VPLA_1));
  Transistor #(.\type ("n")) transistor_27 (.in(1'b0), .out(VPLA_1), .gate(not_11_out));
  Transistor #(.\type ("n")) transistor_28 (.in(1'b0), .out(VPLA_1), .gate(not_12_out));
  Transistor #(.\type ("n")) transistor_29 (.in(1'b0), .out(VPLA_1), .gate(not_13_out));
  Transistor #(.\type ("n")) transistor_30 (.in(1'b0), .out(VPLA_1), .gate(not_14_out));
  Transistor #(.\type ("n")) transistor_31 (.in(1'b0), .out(VPLA_1), .gate(V3));
  Transistor #(.\type ("n")) transistor_32 (.in(1'b0), .out(VPLA_1), .gate(not_15_out));
  Transistor #(.\type ("n")) transistor_33 (.in(1'b0), .out(VPLA_1), .gate(V1));
  Transistor #(.\type ("n")) transistor_34 (.in(1'b0), .out(VPLA_1), .gate(V0));
  Pull_Resistor #(.pull(1)) pull_resistor_5 (.node(HPLA_2));
  Transistor #(.\type ("n")) transistor_35 (.in(1'b0), .out(HPLA_2), .gate(H8));
  Transistor #(.\type ("n")) transistor_36 (.in(1'b0), .out(HPLA_2), .gate(H7));
  Transistor #(.\type ("n")) transistor_37 (.in(1'b0), .out(HPLA_2), .gate(not_3_out));
  Transistor #(.\type ("n")) transistor_38 (.in(1'b0), .out(HPLA_2), .gate(H5));
  Transistor #(.\type ("n")) transistor_39 (.in(1'b0), .out(HPLA_2), .gate(H4));
  Transistor #(.\type ("n")) transistor_40 (.in(1'b0), .out(HPLA_2), .gate(H3));
  Transistor #(.\type ("n")) transistor_41 (.in(1'b0), .out(HPLA_2), .gate(H2));
  Transistor #(.\type ("n")) transistor_42 (.in(1'b0), .out(HPLA_2), .gate(H1));
  Transistor #(.\type ("n")) transistor_43 (.in(1'b0), .out(HPLA_2), .gate(not_9_out));
  Transistor #(.\type ("n")) transistor_44 (.in(1'b0), .out(HPLA_2), .gate(BLNK));
  Pull_Resistor #(.pull(1)) pull_resistor_6 (.node(VPLA_2));
  Transistor #(.\type ("n")) transistor_45 (.in(1'b0), .out(VPLA_2), .gate(not_10_out));
  Transistor #(.\type ("n")) transistor_46 (.in(1'b0), .out(VPLA_2), .gate(V7));
  Transistor #(.\type ("n")) transistor_47 (.in(1'b0), .out(VPLA_2), .gate(V6));
  Transistor #(.\type ("n")) transistor_48 (.in(1'b0), .out(VPLA_2), .gate(V5));
  Transistor #(.\type ("n")) transistor_49 (.in(1'b0), .out(VPLA_2), .gate(V4));
  Transistor #(.\type ("n")) transistor_50 (.in(1'b0), .out(VPLA_2), .gate(V3));
  Transistor #(.\type ("n")) transistor_51 (.in(1'b0), .out(VPLA_2), .gate(not_15_out));
  Transistor #(.\type ("n")) transistor_52 (.in(1'b0), .out(VPLA_2), .gate(V1));
  Transistor #(.\type ("n")) transistor_53 (.in(1'b0), .out(VPLA_2), .gate(not_17_out));
  Pull_Resistor #(.pull(1)) pull_resistor_7 (.node(HPLA_3));
  Transistor #(.\type ("n")) transistor_54 (.in(1'b0), .out(HPLA_3), .gate(H7));
  Transistor #(.\type ("n")) transistor_55 (.in(1'b0), .out(HPLA_3), .gate(H6));
  Transistor #(.\type ("n")) transistor_56 (.in(1'b0), .out(HPLA_3), .gate(H5));
  Transistor #(.\type ("n")) transistor_57 (.in(1'b0), .out(HPLA_3), .gate(H4));
  Transistor #(.\type ("n")) transistor_58 (.in(1'b0), .out(HPLA_3), .gate(H3));
  Pull_Resistor #(.pull(1)) pull_resistor_8 (.node(VPLA_3));
  Transistor #(.\type ("n")) transistor_59 (.in(1'b0), .out(VPLA_3), .gate(not_11_out));
  Transistor #(.\type ("n")) transistor_60 (.in(1'b0), .out(VPLA_3), .gate(not_12_out));
  Transistor #(.\type ("n")) transistor_61 (.in(1'b0), .out(VPLA_3), .gate(not_13_out));
  Transistor #(.\type ("n")) transistor_62 (.in(1'b0), .out(VPLA_3), .gate(not_14_out));
  Transistor #(.\type ("n")) transistor_63 (.in(1'b0), .out(VPLA_3), .gate(V3));
  Transistor #(.\type ("n")) transistor_64 (.in(1'b0), .out(VPLA_3), .gate(V2));
  Transistor #(.\type ("n")) transistor_65 (.in(1'b0), .out(VPLA_3), .gate(V1));
  Transistor #(.\type ("n")) transistor_66 (.in(1'b0), .out(VPLA_3), .gate(not_17_out));
  Pull_Resistor #(.pull(1)) pull_resistor_9 (.node(HPLA_5));
  Pull_Resistor #(.pull(1)) pull_resistor_10 (.node(HPLA_4));
  Transistor #(.\type ("n")) transistor_67 (.in(1'b0), .out(HPLA_4), .gate(H8));
  Transistor #(.\type ("n")) transistor_68 (.in(1'b0), .out(HPLA_5), .gate(not_1_out));
  Transistor #(.\type ("n")) transistor_69 (.in(1'b0), .out(HPLA_5), .gate(H7));
  Transistor #(.\type ("n")) transistor_70 (.in(1'b0), .out(HPLA_5), .gate(not_3_out));
  Transistor #(.\type ("n")) transistor_71 (.in(1'b0), .out(HPLA_5), .gate(H5));
  Transistor #(.\type ("n")) transistor_72 (.in(1'b0), .out(HPLA_5), .gate(not_5_out));
  Transistor #(.\type ("n")) transistor_73 (.in(1'b0), .out(HPLA_5), .gate(H3));
  Transistor #(.\type ("n")) transistor_74 (.in(1'b0), .out(HPLA_5), .gate(H2));
  Transistor #(.\type ("n")) transistor_75 (.in(1'b0), .out(HPLA_5), .gate(not_8_out));
  Transistor #(.\type ("n")) transistor_76 (.in(1'b0), .out(HPLA_5), .gate(not_9_out));
  Transistor #(.\type ("n")) transistor_77 (.in(1'b0), .out(HPLA_4), .gate(VB));
  Transistor #(.\type ("n")) transistor_78 (.in(1'b0), .out(HPLA_5), .gate(BLNK));
  Pull_Resistor #(.pull(1)) pull_resistor_11 (.node(VPLA_5));
  Pull_Resistor #(.pull(1)) pull_resistor_12 (.node(VPLA_4));
  Transistor #(.\type ("n")) transistor_79 (.in(1'b0), .out(VPLA_5), .gate(V8));
  Transistor #(.\type ("n")) transistor_80 (.in(1'b0), .out(VPLA_5), .gate(V7));
  Transistor #(.\type ("n")) transistor_81 (.in(1'b0), .out(VPLA_4), .gate(not_11_out));
  Transistor #(.\type ("n")) transistor_82 (.in(1'b0), .out(VPLA_5), .gate(V6));
  Transistor #(.\type ("n")) transistor_83 (.in(1'b0), .out(VPLA_4), .gate(not_12_out));
  Transistor #(.\type ("n")) transistor_84 (.in(1'b0), .out(VPLA_5), .gate(V5));
  Transistor #(.\type ("n")) transistor_85 (.in(1'b0), .out(VPLA_4), .gate(not_13_out));
  Transistor #(.\type ("n")) transistor_86 (.in(1'b0), .out(VPLA_5), .gate(V4));
  Transistor #(.\type ("n")) transistor_87 (.in(1'b0), .out(VPLA_4), .gate(not_14_out));
  Transistor #(.\type ("n")) transistor_88 (.in(1'b0), .out(VPLA_4), .gate(V3));
  Transistor #(.\type ("n")) transistor_89 (.in(1'b0), .out(VPLA_5), .gate(V3));
  Transistor #(.\type ("n")) transistor_90 (.in(1'b0), .out(VPLA_4), .gate(V2));
  Transistor #(.\type ("n")) transistor_91 (.in(1'b0), .out(VPLA_5), .gate(V2));
  Transistor #(.\type ("n")) transistor_92 (.in(1'b0), .out(VPLA_4), .gate(V1));
  Transistor #(.\type ("n")) transistor_93 (.in(1'b0), .out(VPLA_5), .gate(V1));
  Transistor #(.\type ("n")) transistor_94 (.in(1'b0), .out(VPLA_5), .gate(V0));
  Transistor #(.\type ("n")) transistor_95 (.in(1'b0), .out(VPLA_4), .gate(not_17_out));
  Pull_Resistor #(.pull(1)) pull_resistor_13 (.node(HPLA_6));
  Transistor #(.\type ("n")) transistor_96 (.in(1'b0), .out(HPLA_6), .gate(H8));
  Transistor #(.\type ("n")) transistor_97 (.in(1'b0), .out(HPLA_6), .gate(H7));
  Transistor #(.\type ("n")) transistor_98 (.in(1'b0), .out(HPLA_6), .gate(H6));
  Transistor #(.\type ("n")) transistor_99 (.in(1'b0), .out(HPLA_6), .gate(not_4_out));
  Transistor #(.\type ("n")) transistor_100 (.in(1'b0), .out(HPLA_6), .gate(not_5_out));
  Transistor #(.\type ("n")) transistor_101 (.in(1'b0), .out(HPLA_6), .gate(not_6_out));
  Transistor #(.\type ("n")) transistor_102 (.in(1'b0), .out(HPLA_6), .gate(not_7_out));
  Transistor #(.\type ("n")) transistor_103 (.in(1'b0), .out(HPLA_6), .gate(not_8_out));
  Transistor #(.\type ("n")) transistor_104 (.in(1'b0), .out(HPLA_6), .gate(not_9_out));
  Transistor #(.\type ("n")) transistor_105 (.in(1'b0), .out(HPLA_6), .gate(BLNK));
  Pull_Resistor #(.pull(1)) pull_resistor_14 (.node(VPLA_6));
  Transistor #(.\type ("n")) transistor_106 (.in(1'b0), .out(VPLA_6), .gate(not_11_out));
  Transistor #(.\type ("n")) transistor_107 (.in(1'b0), .out(VPLA_6), .gate(not_12_out));
  Transistor #(.\type ("n")) transistor_108 (.in(1'b0), .out(VPLA_6), .gate(not_13_out));
  Transistor #(.\type ("n")) transistor_109 (.in(1'b0), .out(VPLA_6), .gate(not_14_out));
  Transistor #(.\type ("n")) transistor_110 (.in(1'b0), .out(VPLA_6), .gate(V3));
  Transistor #(.\type ("n")) transistor_111 (.in(1'b0), .out(VPLA_6), .gate(V2));
  Transistor #(.\type ("n")) transistor_112 (.in(1'b0), .out(VPLA_6), .gate(V1));
  Transistor #(.\type ("n")) transistor_113 (.in(1'b0), .out(VPLA_6), .gate(V0));
  Pull_Resistor #(.pull(1)) pull_resistor_15 (.node(HPLA_7));
  Transistor #(.\type ("n")) transistor_114 (.in(1'b0), .out(HPLA_7), .gate(not_2_out));
  Transistor #(.\type ("n")) transistor_115 (.in(1'b0), .out(HPLA_7), .gate(not_3_out));
  Transistor #(.\type ("n")) transistor_116 (.in(1'b0), .out(HPLA_7), .gate(not_4_out));
  Transistor #(.\type ("n")) transistor_117 (.in(1'b0), .out(HPLA_7), .gate(not_5_out));
  Transistor #(.\type ("n")) transistor_118 (.in(1'b0), .out(HPLA_7), .gate(not_6_out));
  Transistor #(.\type ("n")) transistor_119 (.in(1'b0), .out(HPLA_7), .gate(not_7_out));
  Transistor #(.\type ("n")) transistor_120 (.in(1'b0), .out(HPLA_7), .gate(not_8_out));
  Transistor #(.\type ("n")) transistor_121 (.in(1'b0), .out(HPLA_7), .gate(not_9_out));
  Transistor #(.\type ("n")) transistor_122 (.in(1'b0), .out(HPLA_7), .gate(BLNK));
  Pull_Resistor #(.pull(1)) pull_resistor_16 (.node(VPLA_7));
  Transistor #(.\type ("n")) transistor_123 (.in(1'b0), .out(VPLA_7), .gate(not_10_out));
  Transistor #(.\type ("n")) transistor_124 (.in(1'b0), .out(VPLA_7), .gate(V7));
  Transistor #(.\type ("n")) transistor_125 (.in(1'b0), .out(VPLA_7), .gate(V6));
  Transistor #(.\type ("n")) transistor_126 (.in(1'b0), .out(VPLA_7), .gate(V5));
  Transistor #(.\type ("n")) transistor_127 (.in(1'b0), .out(VPLA_7), .gate(V4));
  Transistor #(.\type ("n")) transistor_128 (.in(1'b0), .out(VPLA_7), .gate(V3));
  Transistor #(.\type ("n")) transistor_129 (.in(1'b0), .out(VPLA_7), .gate(not_15_out));
  Transistor #(.\type ("n")) transistor_130 (.in(1'b0), .out(VPLA_7), .gate(V1));
  Transistor #(.\type ("n")) transistor_131 (.in(1'b0), .out(VPLA_7), .gate(not_17_out));
  Pull_Resistor #(.pull(1)) pull_resistor_17 (.node(HPLA_8));
  Transistor #(.\type ("n")) transistor_132 (.in(1'b0), .out(HPLA_8), .gate(H8));
  Transistor #(.\type ("n")) transistor_133 (.in(1'b0), .out(HPLA_8), .gate(H7));
  Transistor #(.\type ("n")) transistor_134 (.in(1'b0), .out(HPLA_8), .gate(H6));
  Transistor #(.\type ("n")) transistor_135 (.in(1'b0), .out(HPLA_8), .gate(BLNK));
  Pull_Resistor #(.pull(1)) pull_resistor_18 (.node(VPLA_8));
  Transistor #(.\type ("n")) transistor_136 (.in(1'b0), .out(VPLA_8), .gate(not_10_out));
  Transistor #(.\type ("n")) transistor_137 (.in(1'b0), .out(VPLA_8), .gate(V7));
  Transistor #(.\type ("n")) transistor_138 (.in(1'b0), .out(VPLA_8), .gate(V6));
  Transistor #(.\type ("n")) transistor_139 (.in(1'b0), .out(VPLA_8), .gate(V5));
  Transistor #(.\type ("n")) transistor_140 (.in(1'b0), .out(VPLA_8), .gate(V4));
  Transistor #(.\type ("n")) transistor_141 (.in(1'b0), .out(VPLA_8), .gate(V3));
  Transistor #(.\type ("n")) transistor_142 (.in(1'b0), .out(VPLA_8), .gate(not_15_out));
  Transistor #(.\type ("n")) transistor_143 (.in(1'b0), .out(VPLA_8), .gate(V1));
  Transistor #(.\type ("n")) transistor_144 (.in(1'b0), .out(VPLA_8), .gate(not_17_out));
  Pull_Resistor #(.pull(1)) pull_resistor_19 (.node(HPLA_9));
  Transistor #(.\type ("n")) transistor_145 (.in(1'b0), .out(HPLA_9), .gate(not_1_out));
  Transistor #(.\type ("n")) transistor_146 (.in(1'b0), .out(HPLA_9), .gate(H7));
  Transistor #(.\type ("n")) transistor_147 (.in(1'b0), .out(HPLA_9), .gate(H6));
  Transistor #(.\type ("n")) transistor_148 (.in(1'b0), .out(HPLA_9), .gate(BLNK));
  Pull_Resistor #(.pull(1)) pull_resistor_20 (.node(HPLA_10));
  Transistor #(.\type ("n")) transistor_149 (.in(1'b0), .out(HPLA_10), .gate(H8));
  Transistor #(.\type ("n")) transistor_150 (.in(1'b0), .out(HPLA_10), .gate(VB));
  Transistor #(.\type ("n")) transistor_151 (.in(1'b0), .out(HPLA_10), .gate(BLNK));
  Pull_Resistor #(.pull(1)) pull_resistor_21 (.node(HPLA_11));
  Transistor #(.\type ("n")) transistor_152 (.in(1'b0), .out(HPLA_11), .gate(H2));
  Transistor #(.\type ("n")) transistor_153 (.in(1'b0), .out(HPLA_11), .gate(H1));
  Transistor #(.\type ("n")) transistor_154 (.in(1'b0), .out(HPLA_11), .gate(BLNK));
  Pull_Resistor #(.pull(1)) pull_resistor_22 (.node(HPLA_13));
  Pull_Resistor #(.pull(1)) pull_resistor_23 (.node(HPLA_12));
  Transistor #(.\type ("n")) transistor_155 (.in(1'b0), .out(HPLA_13), .gate(not_7_out));
  Transistor #(.\type ("n")) transistor_156 (.in(1'b0), .out(HPLA_12), .gate(not_7_out));
  Transistor #(.\type ("n")) transistor_157 (.in(1'b0), .out(HPLA_13), .gate(H1));
  Transistor #(.\type ("n")) transistor_158 (.in(1'b0), .out(HPLA_12), .gate(not_8_out));
  Pull_Resistor #(.pull(1)) pull_resistor_24 (.node(HPLA_14));
  Transistor #(.\type ("n")) transistor_159 (.in(1'b0), .out(HPLA_14), .gate(not_1_out));
  Transistor #(.\type ("n")) transistor_160 (.in(1'b0), .out(HPLA_14), .gate(not_3_out));
  Transistor #(.\type ("n")) transistor_161 (.in(1'b0), .out(HPLA_14), .gate(H5));
  Transistor #(.\type ("n")) transistor_162 (.in(1'b0), .out(HPLA_14), .gate(H4));
  Transistor #(.\type ("n")) transistor_163 (.in(1'b0), .out(HPLA_14), .gate(BLNK));
  Pull_Resistor #(.pull(1)) pull_resistor_25 (.node(HPLA_15));
  Transistor #(.\type ("n")) transistor_164 (.in(1'b0), .out(HPLA_15), .gate(H8));
  Transistor #(.\type ("n")) transistor_165 (.in(1'b0), .out(HPLA_15), .gate(BLNK));
  Pull_Resistor #(.pull(1)) pull_resistor_26 (.node(HPLA_16));
  Transistor #(.\type ("n")) transistor_166 (.in(1'b0), .out(HPLA_16), .gate(H2));
  Transistor #(.\type ("n")) transistor_167 (.in(1'b0), .out(HPLA_16), .gate(not_8_out));
  Pull_Resistor #(.pull(1)) pull_resistor_27 (.node(HPLA_17));
  Transistor #(.\type ("n")) transistor_168 (.in(1'b0), .out(HPLA_17), .gate(not_1_out));
  Transistor #(.\type ("n")) transistor_169 (.in(1'b0), .out(HPLA_17), .gate(H7));
  Transistor #(.\type ("n")) transistor_170 (.in(1'b0), .out(HPLA_17), .gate(H6));
  Transistor #(.\type ("n")) transistor_171 (.in(1'b0), .out(HPLA_17), .gate(H5));
  Transistor #(.\type ("n")) transistor_172 (.in(1'b0), .out(HPLA_17), .gate(H4));
  Transistor #(.\type ("n")) transistor_173 (.in(1'b0), .out(HPLA_17), .gate(not_6_out));
  Transistor #(.\type ("n")) transistor_174 (.in(1'b0), .out(HPLA_17), .gate(not_7_out));
  Transistor #(.\type ("n")) transistor_175 (.in(1'b0), .out(HPLA_17), .gate(not_8_out));
  Transistor #(.\type ("n")) transistor_176 (.in(1'b0), .out(HPLA_17), .gate(H0));
  Pull_Resistor #(.pull(1)) pull_resistor_28 (.node(HPLA_18));
  Transistor #(.\type ("n")) transistor_177 (.in(1'b0), .out(HPLA_18), .gate(not_1_out));
  Transistor #(.\type ("n")) transistor_178 (.in(1'b0), .out(HPLA_18), .gate(H7));
  Transistor #(.\type ("n")) transistor_179 (.in(1'b0), .out(HPLA_18), .gate(not_3_out));
  Transistor #(.\type ("n")) transistor_180 (.in(1'b0), .out(HPLA_18), .gate(H5));
  Transistor #(.\type ("n")) transistor_181 (.in(1'b0), .out(HPLA_18), .gate(H4));
  Transistor #(.\type ("n")) transistor_182 (.in(1'b0), .out(HPLA_18), .gate(not_6_out));
  Transistor #(.\type ("n")) transistor_183 (.in(1'b0), .out(HPLA_18), .gate(H2));
  Transistor #(.\type ("n")) transistor_184 (.in(1'b0), .out(HPLA_18), .gate(H1));
  Transistor #(.\type ("n")) transistor_185 (.in(1'b0), .out(HPLA_18), .gate(H0));
  Pull_Resistor #(.pull(1)) pull_resistor_29 (.node(HPLA_19));
  Transistor #(.\type ("n")) transistor_186 (.in(1'b0), .out(HPLA_19), .gate(not_1_out));
  Transistor #(.\type ("n")) transistor_187 (.in(1'b0), .out(HPLA_19), .gate(H7));
  Transistor #(.\type ("n")) transistor_188 (.in(1'b0), .out(HPLA_19), .gate(H6));
  Transistor #(.\type ("n")) transistor_189 (.in(1'b0), .out(HPLA_19), .gate(H5));
  Transistor #(.\type ("n")) transistor_190 (.in(1'b0), .out(HPLA_19), .gate(not_5_out));
  Transistor #(.\type ("n")) transistor_191 (.in(1'b0), .out(HPLA_19), .gate(H3));
  Transistor #(.\type ("n")) transistor_192 (.in(1'b0), .out(HPLA_19), .gate(not_7_out));
  Transistor #(.\type ("n")) transistor_193 (.in(1'b0), .out(HPLA_19), .gate(not_8_out));
  Transistor #(.\type ("n")) transistor_194 (.in(1'b0), .out(HPLA_19), .gate(not_9_out));
  Pull_Resistor #(.pull(1)) pull_resistor_30 (.node(HPLA_21));
  Pull_Resistor #(.pull(1)) pull_resistor_31 (.node(HPLA_20));
  Transistor #(.\type ("n")) transistor_195 (.in(1'b0), .out(HPLA_21), .gate(not_1_out));
  Transistor #(.\type ("n")) transistor_196 (.in(1'b0), .out(HPLA_20), .gate(not_1_out));
  Transistor #(.\type ("n")) transistor_197 (.in(1'b0), .out(HPLA_21), .gate(H7));
  Transistor #(.\type ("n")) transistor_198 (.in(1'b0), .out(HPLA_20), .gate(H7));
  Transistor #(.\type ("n")) transistor_199 (.in(1'b0), .out(HPLA_20), .gate(H6));
  Transistor #(.\type ("n")) transistor_200 (.in(1'b0), .out(HPLA_21), .gate(not_3_out));
  Transistor #(.\type ("n")) transistor_201 (.in(1'b0), .out(HPLA_21), .gate(H5));
  Transistor #(.\type ("n")) transistor_202 (.in(1'b0), .out(HPLA_20), .gate(not_4_out));
  Transistor #(.\type ("n")) transistor_203 (.in(1'b0), .out(HPLA_21), .gate(H4));
  Transistor #(.\type ("n")) transistor_204 (.in(1'b0), .out(HPLA_20), .gate(not_5_out));
  Transistor #(.\type ("n")) transistor_205 (.in(1'b0), .out(HPLA_21), .gate(H3));
  Transistor #(.\type ("n")) transistor_206 (.in(1'b0), .out(HPLA_20), .gate(H3));
  Transistor #(.\type ("n")) transistor_207 (.in(1'b0), .out(HPLA_20), .gate(H2));
  Transistor #(.\type ("n")) transistor_208 (.in(1'b0), .out(HPLA_21), .gate(H2));
  Transistor #(.\type ("n")) transistor_209 (.in(1'b0), .out(HPLA_20), .gate(H1));
  Transistor #(.\type ("n")) transistor_210 (.in(1'b0), .out(HPLA_21), .gate(not_8_out));
  Transistor #(.\type ("n")) transistor_211 (.in(1'b0), .out(HPLA_20), .gate(H0));
  Transistor #(.\type ("n")) transistor_212 (.in(1'b0), .out(HPLA_21), .gate(not_9_out));
  Pull_Resistor #(.pull(1)) pull_resistor_32 (.node(HPLA_22));
  Transistor #(.\type ("n")) transistor_213 (.in(1'b0), .out(HPLA_22), .gate(not_1_out));
  Transistor #(.\type ("n")) transistor_214 (.in(1'b0), .out(HPLA_22), .gate(H7));
  Transistor #(.\type ("n")) transistor_215 (.in(1'b0), .out(HPLA_22), .gate(H6));
  Transistor #(.\type ("n")) transistor_216 (.in(1'b0), .out(HPLA_22), .gate(not_4_out));
  Transistor #(.\type ("n")) transistor_217 (.in(1'b0), .out(HPLA_22), .gate(not_5_out));
  Transistor #(.\type ("n")) transistor_218 (.in(1'b0), .out(HPLA_22), .gate(H3));
  Transistor #(.\type ("n")) transistor_219 (.in(1'b0), .out(HPLA_22), .gate(not_7_out));
  Transistor #(.\type ("n")) transistor_220 (.in(1'b0), .out(HPLA_22), .gate(H1));
  Transistor #(.\type ("n")) transistor_221 (.in(1'b0), .out(HPLA_22), .gate(H0));
  Pull_Resistor #(.pull(1)) pull_resistor_33 (.node(HPLA_23));
  Transistor #(.\type ("n")) transistor_222 (.in(1'b0), .out(HPLA_23), .gate(not_1_out));
  Transistor #(.\type ("n")) transistor_223 (.in(1'b0), .out(HPLA_23), .gate(H7));
  Transistor #(.\type ("n")) transistor_224 (.in(1'b0), .out(HPLA_23), .gate(not_3_out));
  Transistor #(.\type ("n")) transistor_225 (.in(1'b0), .out(HPLA_23), .gate(H5));
  Transistor #(.\type ("n")) transistor_226 (.in(1'b0), .out(HPLA_23), .gate(not_5_out));
  Transistor #(.\type ("n")) transistor_227 (.in(1'b0), .out(HPLA_23), .gate(H3));
  Transistor #(.\type ("n")) transistor_228 (.in(1'b0), .out(HPLA_23), .gate(not_7_out));
  Transistor #(.\type ("n")) transistor_229 (.in(1'b0), .out(HPLA_23), .gate(H1));
  Transistor #(.\type ("n")) transistor_230 (.in(1'b0), .out(HPLA_23), .gate(H0));

  assign Hnn = {H5, H4, H3, H2, H1, H0};
  assign VPOS = {V7, V6, V5, V4, V3, V2, V1, V0};

  // Notes on the sheet:
  //   279
  //   247
  //   256
  //   244
  //   65
  //   261
  //   0-255
  //   0-7, 256-263
  //   241
  //   339
  //   241
  //   0
  //   63
  //   240
  //   255
  //   261
  //   0-63
  //   261
  //   256-319
  //   0-255
  //   0/1
  //   4/5
  //   6/7
  //   320-355
  //   0-255
  //   2/3
  //   270
  //   328
  //   279
  //   304
  //   323
  //   308
  //   340
endmodule

module HV_SELECT_PAL (
  input  H8,
  input  H7,
  input  H6,
  input  H5,
  input  H4,
  input  H3,
  input  H2,
  input  H1,
  input  H0,
  input  VB,
  input  BLNK,
  input  V8,
  input  V7,
  input  V6,
  input  V5,
  input  V4,
  input  V3,
  input  V2,
  input  V1,
  input  V0,
  output [5:0] Hnn,
  output HPLA_0,
  output HPLA_1,
  output HPLA_2,
  output HPLA_3,
  output HPLA_4,
  output HPLA_5,
  output HPLA_6,
  output HPLA_7,
  output HPLA_8,
  output HPLA_9,
  output HPLA_10,
  output HPLA_11,
  output HPLA_12,
  output HPLA_13,
  output HPLA_14,
  output HPLA_15,
  output HPLA_16,
  output HPLA_17,
  output HPLA_18,
  output HPLA_19,
  output HPLA_20,
  output HPLA_21,
  output HPLA_22,
  output HPLA_23,
  output [7:0] VPOS,
  output VPLA_0,
  output VPLA_1,
  output VPLA_2,
  output VPLA_3,
  output VPLA_4,
  output VPLA_5,
  output VPLA_6,
  output VPLA_7,
  output VPLA_8,
  output VPLA_9
);

  wire not_1_out, not_2_out, not_3_out, not_4_out, not_5_out, not_6_out, not_7_out, not_8_out, not_9_out,
       not_10_out, not_11_out, not_12_out, not_13_out, not_14_out, not_15_out, not_16_out, not_17_out,
       not_18_out;

  not not_1 (not_1_out, H8);
  not not_2 (not_2_out, H7);
  not not_3 (not_3_out, H6);
  not not_4 (not_4_out, H5);
  not not_5 (not_5_out, H4);
  not not_6 (not_6_out, H3);
  not not_7 (not_7_out, H2);
  not not_8 (not_8_out, H1);
  not not_9 (not_9_out, H0);
  not not_10 (not_10_out, V8);
  not not_11 (not_11_out, V7);
  not not_12 (not_12_out, V6);
  not not_13 (not_13_out, V5);
  not not_14 (not_14_out, V4);
  not not_15 (not_15_out, V3);
  not not_16 (not_16_out, V2);
  not not_17 (not_17_out, V1);
  not not_18 (not_18_out, V0);
  Pull_Resistor #(.pull(1)) pull_resistor_1 (.node(HPLA_0));
  Transistor #(.\type ("n")) transistor_1 (.in(1'b0), .out(HPLA_0), .gate(not_1_out));
  Transistor #(.\type ("n")) transistor_2 (.in(1'b0), .out(HPLA_0), .gate(H7));
  Transistor #(.\type ("n")) transistor_3 (.in(1'b0), .out(HPLA_0), .gate(H6));
  Transistor #(.\type ("n")) transistor_4 (.in(1'b0), .out(HPLA_0), .gate(H5));
  Transistor #(.\type ("n")) transistor_5 (.in(1'b0), .out(HPLA_0), .gate(not_5_out));
  Transistor #(.\type ("n")) transistor_6 (.in(1'b0), .out(HPLA_0), .gate(H3));
  Transistor #(.\type ("n")) transistor_7 (.in(1'b0), .out(HPLA_0), .gate(not_7_out));
  Transistor #(.\type ("n")) transistor_8 (.in(1'b0), .out(HPLA_0), .gate(H1));
  Transistor #(.\type ("n")) transistor_9 (.in(1'b0), .out(HPLA_0), .gate(not_9_out));
  Pull_Resistor #(.pull(1)) pull_resistor_2 (.node(VPLA_0));
  Transistor #(.\type ("n")) transistor_10 (.in(1'b0), .out(VPLA_0), .gate(not_10_out));
  Transistor #(.\type ("n")) transistor_11 (.in(1'b0), .out(VPLA_0), .gate(V7));
  Transistor #(.\type ("n")) transistor_12 (.in(1'b0), .out(VPLA_0), .gate(V6));
  Transistor #(.\type ("n")) transistor_13 (.in(1'b0), .out(VPLA_0), .gate(V5));
  Transistor #(.\type ("n")) transistor_14 (.in(1'b0), .out(VPLA_0), .gate(not_14_out));
  Transistor #(.\type ("n")) transistor_15 (.in(1'b0), .out(VPLA_0), .gate(V3));
  Transistor #(.\type ("n")) transistor_16 (.in(1'b0), .out(VPLA_0), .gate(V2));
  Transistor #(.\type ("n")) transistor_17 (.in(1'b0), .out(VPLA_0), .gate(V1));
  Transistor #(.\type ("n")) transistor_18 (.in(1'b0), .out(VPLA_0), .gate(V0));
  Pull_Resistor #(.pull(1)) pull_resistor_3 (.node(HPLA_1));
  Transistor #(.\type ("n")) transistor_19 (.in(1'b0), .out(HPLA_1), .gate(not_1_out));
  Transistor #(.\type ("n")) transistor_20 (.in(1'b0), .out(HPLA_1), .gate(H7));
  Transistor #(.\type ("n")) transistor_21 (.in(1'b0), .out(HPLA_1), .gate(H6));
  Transistor #(.\type ("n")) transistor_22 (.in(1'b0), .out(HPLA_1), .gate(H5));
  Transistor #(.\type ("n")) transistor_23 (.in(1'b0), .out(HPLA_1), .gate(H4));
  Transistor #(.\type ("n")) transistor_24 (.in(1'b0), .out(HPLA_1), .gate(H3));
  Transistor #(.\type ("n")) transistor_25 (.in(1'b0), .out(HPLA_1), .gate(H2));
  Transistor #(.\type ("n")) transistor_26 (.in(1'b0), .out(HPLA_1), .gate(H1));
  Transistor #(.\type ("n")) transistor_27 (.in(1'b0), .out(HPLA_1), .gate(H0));
  Pull_Resistor #(.pull(1)) pull_resistor_4 (.node(VPLA_1));
  Transistor #(.\type ("n")) transistor_28 (.in(1'b0), .out(VPLA_1), .gate(not_10_out));
  Transistor #(.\type ("n")) transistor_29 (.in(1'b0), .out(VPLA_1), .gate(V7));
  Transistor #(.\type ("n")) transistor_30 (.in(1'b0), .out(VPLA_1), .gate(V6));
  Transistor #(.\type ("n")) transistor_31 (.in(1'b0), .out(VPLA_1), .gate(V5));
  Transistor #(.\type ("n")) transistor_32 (.in(1'b0), .out(VPLA_1), .gate(V4));
  Transistor #(.\type ("n")) transistor_33 (.in(1'b0), .out(VPLA_1), .gate(not_15_out));
  Transistor #(.\type ("n")) transistor_34 (.in(1'b0), .out(VPLA_1), .gate(not_16_out));
  Transistor #(.\type ("n")) transistor_35 (.in(1'b0), .out(VPLA_1), .gate(V1));
  Transistor #(.\type ("n")) transistor_36 (.in(1'b0), .out(VPLA_1), .gate(not_18_out));
  Pull_Resistor #(.pull(1)) pull_resistor_5 (.node(HPLA_2));
  Transistor #(.\type ("n")) transistor_37 (.in(1'b0), .out(HPLA_2), .gate(H8));
  Transistor #(.\type ("n")) transistor_38 (.in(1'b0), .out(HPLA_2), .gate(H7));
  Transistor #(.\type ("n")) transistor_39 (.in(1'b0), .out(HPLA_2), .gate(not_3_out));
  Transistor #(.\type ("n")) transistor_40 (.in(1'b0), .out(HPLA_2), .gate(H5));
  Transistor #(.\type ("n")) transistor_41 (.in(1'b0), .out(HPLA_2), .gate(H4));
  Transistor #(.\type ("n")) transistor_42 (.in(1'b0), .out(HPLA_2), .gate(H3));
  Transistor #(.\type ("n")) transistor_43 (.in(1'b0), .out(HPLA_2), .gate(H2));
  Transistor #(.\type ("n")) transistor_44 (.in(1'b0), .out(HPLA_2), .gate(H1));
  Transistor #(.\type ("n")) transistor_45 (.in(1'b0), .out(HPLA_2), .gate(not_9_out));
  Transistor #(.\type ("n")) transistor_46 (.in(1'b0), .out(HPLA_2), .gate(BLNK));
  Pull_Resistor #(.pull(1)) pull_resistor_6 (.node(VPLA_2));
  Transistor #(.\type ("n")) transistor_47 (.in(1'b0), .out(VPLA_2), .gate(V8));
  Transistor #(.\type ("n")) transistor_48 (.in(1'b0), .out(VPLA_2), .gate(V7));
  Transistor #(.\type ("n")) transistor_49 (.in(1'b0), .out(VPLA_2), .gate(V6));
  Transistor #(.\type ("n")) transistor_50 (.in(1'b0), .out(VPLA_2), .gate(V5));
  Transistor #(.\type ("n")) transistor_51 (.in(1'b0), .out(VPLA_2), .gate(V4));
  Transistor #(.\type ("n")) transistor_52 (.in(1'b0), .out(VPLA_2), .gate(V3));
  Transistor #(.\type ("n")) transistor_53 (.in(1'b0), .out(VPLA_2), .gate(V2));
  Transistor #(.\type ("n")) transistor_54 (.in(1'b0), .out(VPLA_2), .gate(V1));
  Transistor #(.\type ("n")) transistor_55 (.in(1'b0), .out(VPLA_2), .gate(not_18_out));
  Pull_Resistor #(.pull(1)) pull_resistor_7 (.node(HPLA_3));
  Transistor #(.\type ("n")) transistor_56 (.in(1'b0), .out(HPLA_3), .gate(H7));
  Transistor #(.\type ("n")) transistor_57 (.in(1'b0), .out(HPLA_3), .gate(H6));
  Transistor #(.\type ("n")) transistor_58 (.in(1'b0), .out(HPLA_3), .gate(H5));
  Transistor #(.\type ("n")) transistor_59 (.in(1'b0), .out(HPLA_3), .gate(H4));
  Transistor #(.\type ("n")) transistor_60 (.in(1'b0), .out(HPLA_3), .gate(H3));
  Pull_Resistor #(.pull(1)) pull_resistor_8 (.node(VPLA_3));
  Transistor #(.\type ("n")) transistor_61 (.in(1'b0), .out(VPLA_3), .gate(not_11_out));
  Transistor #(.\type ("n")) transistor_62 (.in(1'b0), .out(VPLA_3), .gate(not_12_out));
  Transistor #(.\type ("n")) transistor_63 (.in(1'b0), .out(VPLA_3), .gate(not_13_out));
  Transistor #(.\type ("n")) transistor_64 (.in(1'b0), .out(VPLA_3), .gate(not_14_out));
  Transistor #(.\type ("n")) transistor_65 (.in(1'b0), .out(VPLA_3), .gate(V3));
  Transistor #(.\type ("n")) transistor_66 (.in(1'b0), .out(VPLA_3), .gate(V2));
  Transistor #(.\type ("n")) transistor_67 (.in(1'b0), .out(VPLA_3), .gate(V1));
  Transistor #(.\type ("n")) transistor_68 (.in(1'b0), .out(VPLA_3), .gate(V0));
  Pull_Resistor #(.pull(1)) pull_resistor_9 (.node(HPLA_5));
  Pull_Resistor #(.pull(1)) pull_resistor_10 (.node(HPLA_4));
  Transistor #(.\type ("n")) transistor_69 (.in(1'b0), .out(HPLA_4), .gate(H8));
  Transistor #(.\type ("n")) transistor_70 (.in(1'b0), .out(HPLA_5), .gate(not_1_out));
  Transistor #(.\type ("n")) transistor_71 (.in(1'b0), .out(HPLA_5), .gate(H7));
  Transistor #(.\type ("n")) transistor_72 (.in(1'b0), .out(HPLA_5), .gate(not_3_out));
  Transistor #(.\type ("n")) transistor_73 (.in(1'b0), .out(HPLA_5), .gate(H5));
  Transistor #(.\type ("n")) transistor_74 (.in(1'b0), .out(HPLA_5), .gate(not_5_out));
  Transistor #(.\type ("n")) transistor_75 (.in(1'b0), .out(HPLA_5), .gate(H3));
  Transistor #(.\type ("n")) transistor_76 (.in(1'b0), .out(HPLA_5), .gate(H2));
  Transistor #(.\type ("n")) transistor_77 (.in(1'b0), .out(HPLA_5), .gate(not_8_out));
  Transistor #(.\type ("n")) transistor_78 (.in(1'b0), .out(HPLA_5), .gate(not_9_out));
  Transistor #(.\type ("n")) transistor_79 (.in(1'b0), .out(HPLA_4), .gate(VB));
  Transistor #(.\type ("n")) transistor_80 (.in(1'b0), .out(HPLA_5), .gate(BLNK));
  Pull_Resistor #(.pull(1)) pull_resistor_11 (.node(VPLA_5));
  Pull_Resistor #(.pull(1)) pull_resistor_12 (.node(VPLA_4));
  Transistor #(.\type ("n")) transistor_81 (.in(1'b0), .out(VPLA_5), .gate(V8));
  Transistor #(.\type ("n")) transistor_82 (.in(1'b0), .out(VPLA_5), .gate(V7));
  Transistor #(.\type ("n")) transistor_83 (.in(1'b0), .out(VPLA_4), .gate(not_11_out));
  Transistor #(.\type ("n")) transistor_84 (.in(1'b0), .out(VPLA_5), .gate(V6));
  Transistor #(.\type ("n")) transistor_85 (.in(1'b0), .out(VPLA_4), .gate(not_12_out));
  Transistor #(.\type ("n")) transistor_86 (.in(1'b0), .out(VPLA_5), .gate(V5));
  Transistor #(.\type ("n")) transistor_87 (.in(1'b0), .out(VPLA_4), .gate(not_13_out));
  Transistor #(.\type ("n")) transistor_88 (.in(1'b0), .out(VPLA_5), .gate(V4));
  Transistor #(.\type ("n")) transistor_89 (.in(1'b0), .out(VPLA_4), .gate(not_14_out));
  Transistor #(.\type ("n")) transistor_90 (.in(1'b0), .out(VPLA_4), .gate(V3));
  Transistor #(.\type ("n")) transistor_91 (.in(1'b0), .out(VPLA_5), .gate(V3));
  Transistor #(.\type ("n")) transistor_92 (.in(1'b0), .out(VPLA_4), .gate(V2));
  Transistor #(.\type ("n")) transistor_93 (.in(1'b0), .out(VPLA_5), .gate(V2));
  Transistor #(.\type ("n")) transistor_94 (.in(1'b0), .out(VPLA_5), .gate(V1));
  Transistor #(.\type ("n")) transistor_95 (.in(1'b0), .out(VPLA_4), .gate(V1));
  Transistor #(.\type ("n")) transistor_96 (.in(1'b0), .out(VPLA_5), .gate(V0));
  Transistor #(.\type ("n")) transistor_97 (.in(1'b0), .out(VPLA_4), .gate(not_18_out));
  Pull_Resistor #(.pull(1)) pull_resistor_13 (.node(HPLA_6));
  Transistor #(.\type ("n")) transistor_98 (.in(1'b0), .out(HPLA_6), .gate(H8));
  Transistor #(.\type ("n")) transistor_99 (.in(1'b0), .out(HPLA_6), .gate(H7));
  Transistor #(.\type ("n")) transistor_100 (.in(1'b0), .out(HPLA_6), .gate(H6));
  Transistor #(.\type ("n")) transistor_101 (.in(1'b0), .out(HPLA_6), .gate(not_4_out));
  Transistor #(.\type ("n")) transistor_102 (.in(1'b0), .out(HPLA_6), .gate(not_5_out));
  Transistor #(.\type ("n")) transistor_103 (.in(1'b0), .out(HPLA_6), .gate(not_6_out));
  Transistor #(.\type ("n")) transistor_104 (.in(1'b0), .out(HPLA_6), .gate(not_7_out));
  Transistor #(.\type ("n")) transistor_105 (.in(1'b0), .out(HPLA_6), .gate(not_8_out));
  Transistor #(.\type ("n")) transistor_106 (.in(1'b0), .out(HPLA_6), .gate(not_9_out));
  Transistor #(.\type ("n")) transistor_107 (.in(1'b0), .out(HPLA_6), .gate(BLNK));
  Pull_Resistor #(.pull(1)) pull_resistor_14 (.node(VPLA_6));
  Transistor #(.\type ("n")) transistor_108 (.in(1'b0), .out(VPLA_6), .gate(not_11_out));
  Transistor #(.\type ("n")) transistor_109 (.in(1'b0), .out(VPLA_6), .gate(not_12_out));
  Transistor #(.\type ("n")) transistor_110 (.in(1'b0), .out(VPLA_6), .gate(not_13_out));
  Transistor #(.\type ("n")) transistor_111 (.in(1'b0), .out(VPLA_6), .gate(not_14_out));
  Transistor #(.\type ("n")) transistor_112 (.in(1'b0), .out(VPLA_6), .gate(V3));
  Transistor #(.\type ("n")) transistor_113 (.in(1'b0), .out(VPLA_6), .gate(V2));
  Transistor #(.\type ("n")) transistor_114 (.in(1'b0), .out(VPLA_6), .gate(V1));
  Transistor #(.\type ("n")) transistor_115 (.in(1'b0), .out(VPLA_6), .gate(V0));
  Pull_Resistor #(.pull(1)) pull_resistor_15 (.node(HPLA_7));
  Transistor #(.\type ("n")) transistor_116 (.in(1'b0), .out(HPLA_7), .gate(not_2_out));
  Transistor #(.\type ("n")) transistor_117 (.in(1'b0), .out(HPLA_7), .gate(not_3_out));
  Transistor #(.\type ("n")) transistor_118 (.in(1'b0), .out(HPLA_7), .gate(not_4_out));
  Transistor #(.\type ("n")) transistor_119 (.in(1'b0), .out(HPLA_7), .gate(not_5_out));
  Transistor #(.\type ("n")) transistor_120 (.in(1'b0), .out(HPLA_7), .gate(not_6_out));
  Transistor #(.\type ("n")) transistor_121 (.in(1'b0), .out(HPLA_7), .gate(not_7_out));
  Transistor #(.\type ("n")) transistor_122 (.in(1'b0), .out(HPLA_7), .gate(not_8_out));
  Transistor #(.\type ("n")) transistor_123 (.in(1'b0), .out(HPLA_7), .gate(not_9_out));
  Transistor #(.\type ("n")) transistor_124 (.in(1'b0), .out(HPLA_7), .gate(BLNK));
  Pull_Resistor #(.pull(1)) pull_resistor_16 (.node(VPLA_7));
  Transistor #(.\type ("n")) transistor_125 (.in(1'b0), .out(VPLA_7), .gate(not_10_out));
  Transistor #(.\type ("n")) transistor_126 (.in(1'b0), .out(VPLA_7), .gate(V7));
  Transistor #(.\type ("n")) transistor_127 (.in(1'b0), .out(VPLA_7), .gate(V6));
  Transistor #(.\type ("n")) transistor_128 (.in(1'b0), .out(VPLA_7), .gate(not_13_out));
  Transistor #(.\type ("n")) transistor_129 (.in(1'b0), .out(VPLA_7), .gate(not_14_out));
  Transistor #(.\type ("n")) transistor_130 (.in(1'b0), .out(VPLA_7), .gate(V3));
  Transistor #(.\type ("n")) transistor_131 (.in(1'b0), .out(VPLA_7), .gate(not_16_out));
  Transistor #(.\type ("n")) transistor_132 (.in(1'b0), .out(VPLA_7), .gate(not_17_out));
  Transistor #(.\type ("n")) transistor_133 (.in(1'b0), .out(VPLA_7), .gate(not_18_out));
  Pull_Resistor #(.pull(1)) pull_resistor_17 (.node(HPLA_8));
  Transistor #(.\type ("n")) transistor_134 (.in(1'b0), .out(HPLA_8), .gate(H8));
  Transistor #(.\type ("n")) transistor_135 (.in(1'b0), .out(HPLA_8), .gate(H7));
  Transistor #(.\type ("n")) transistor_136 (.in(1'b0), .out(HPLA_8), .gate(H6));
  Transistor #(.\type ("n")) transistor_137 (.in(1'b0), .out(HPLA_8), .gate(BLNK));
  Pull_Resistor #(.pull(1)) pull_resistor_18 (.node(VPLA_8));
  Transistor #(.\type ("n")) transistor_138 (.in(1'b0), .out(VPLA_8), .gate(not_10_out));
  Transistor #(.\type ("n")) transistor_139 (.in(1'b0), .out(VPLA_8), .gate(V7));
  Transistor #(.\type ("n")) transistor_140 (.in(1'b0), .out(VPLA_8), .gate(V6));
  Transistor #(.\type ("n")) transistor_141 (.in(1'b0), .out(VPLA_8), .gate(not_13_out));
  Transistor #(.\type ("n")) transistor_142 (.in(1'b0), .out(VPLA_8), .gate(not_14_out));
  Transistor #(.\type ("n")) transistor_143 (.in(1'b0), .out(VPLA_8), .gate(V3));
  Transistor #(.\type ("n")) transistor_144 (.in(1'b0), .out(VPLA_8), .gate(not_16_out));
  Transistor #(.\type ("n")) transistor_145 (.in(1'b0), .out(VPLA_8), .gate(not_17_out));
  Transistor #(.\type ("n")) transistor_146 (.in(1'b0), .out(VPLA_8), .gate(not_18_out));
  Pull_Resistor #(.pull(1)) pull_resistor_19 (.node(HPLA_9));
  Transistor #(.\type ("n")) transistor_147 (.in(1'b0), .out(HPLA_9), .gate(not_1_out));
  Transistor #(.\type ("n")) transistor_148 (.in(1'b0), .out(HPLA_9), .gate(H7));
  Transistor #(.\type ("n")) transistor_149 (.in(1'b0), .out(HPLA_9), .gate(H6));
  Transistor #(.\type ("n")) transistor_150 (.in(1'b0), .out(HPLA_9), .gate(BLNK));
  Pull_Resistor #(.pull(1)) pull_resistor_20 (.node(VPLA_9));
  Transistor #(.\type ("n")) transistor_151 (.in(1'b0), .out(VPLA_9), .gate(not_10_out));
  Transistor #(.\type ("n")) transistor_152 (.in(1'b0), .out(VPLA_9), .gate(V7));
  Transistor #(.\type ("n")) transistor_153 (.in(1'b0), .out(VPLA_9), .gate(V6));
  Transistor #(.\type ("n")) transistor_154 (.in(1'b0), .out(VPLA_9), .gate(V5));
  Transistor #(.\type ("n")) transistor_155 (.in(1'b0), .out(VPLA_9), .gate(V4));
  Transistor #(.\type ("n")) transistor_156 (.in(1'b0), .out(VPLA_9), .gate(not_15_out));
  Transistor #(.\type ("n")) transistor_157 (.in(1'b0), .out(VPLA_9), .gate(V2));
  Transistor #(.\type ("n")) transistor_158 (.in(1'b0), .out(VPLA_9), .gate(V1));
  Transistor #(.\type ("n")) transistor_159 (.in(1'b0), .out(VPLA_9), .gate(not_18_out));
  Pull_Resistor #(.pull(1)) pull_resistor_21 (.node(HPLA_10));
  Transistor #(.\type ("n")) transistor_160 (.in(1'b0), .out(HPLA_10), .gate(H8));
  Transistor #(.\type ("n")) transistor_161 (.in(1'b0), .out(HPLA_10), .gate(VB));
  Transistor #(.\type ("n")) transistor_162 (.in(1'b0), .out(HPLA_10), .gate(BLNK));
  Pull_Resistor #(.pull(1)) pull_resistor_22 (.node(HPLA_11));
  Transistor #(.\type ("n")) transistor_163 (.in(1'b0), .out(HPLA_11), .gate(H2));
  Transistor #(.\type ("n")) transistor_164 (.in(1'b0), .out(HPLA_11), .gate(H1));
  Transistor #(.\type ("n")) transistor_165 (.in(1'b0), .out(HPLA_11), .gate(BLNK));
  Pull_Resistor #(.pull(1)) pull_resistor_23 (.node(HPLA_13));
  Pull_Resistor #(.pull(1)) pull_resistor_24 (.node(HPLA_12));
  Transistor #(.\type ("n")) transistor_166 (.in(1'b0), .out(HPLA_13), .gate(not_7_out));
  Transistor #(.\type ("n")) transistor_167 (.in(1'b0), .out(HPLA_12), .gate(not_7_out));
  Transistor #(.\type ("n")) transistor_168 (.in(1'b0), .out(HPLA_13), .gate(H1));
  Transistor #(.\type ("n")) transistor_169 (.in(1'b0), .out(HPLA_12), .gate(not_8_out));
  Pull_Resistor #(.pull(1)) pull_resistor_25 (.node(HPLA_14));
  Transistor #(.\type ("n")) transistor_170 (.in(1'b0), .out(HPLA_14), .gate(not_1_out));
  Transistor #(.\type ("n")) transistor_171 (.in(1'b0), .out(HPLA_14), .gate(not_3_out));
  Transistor #(.\type ("n")) transistor_172 (.in(1'b0), .out(HPLA_14), .gate(H5));
  Transistor #(.\type ("n")) transistor_173 (.in(1'b0), .out(HPLA_14), .gate(H4));
  Transistor #(.\type ("n")) transistor_174 (.in(1'b0), .out(HPLA_14), .gate(BLNK));
  Pull_Resistor #(.pull(1)) pull_resistor_26 (.node(HPLA_15));
  Transistor #(.\type ("n")) transistor_175 (.in(1'b0), .out(HPLA_15), .gate(H8));
  Transistor #(.\type ("n")) transistor_176 (.in(1'b0), .out(HPLA_15), .gate(BLNK));
  Pull_Resistor #(.pull(1)) pull_resistor_27 (.node(HPLA_16));
  Transistor #(.\type ("n")) transistor_177 (.in(1'b0), .out(HPLA_16), .gate(H2));
  Transistor #(.\type ("n")) transistor_178 (.in(1'b0), .out(HPLA_16), .gate(not_8_out));
  Pull_Resistor #(.pull(1)) pull_resistor_28 (.node(HPLA_17));
  Transistor #(.\type ("n")) transistor_179 (.in(1'b0), .out(HPLA_17), .gate(not_1_out));
  Transistor #(.\type ("n")) transistor_180 (.in(1'b0), .out(HPLA_17), .gate(H7));
  Transistor #(.\type ("n")) transistor_181 (.in(1'b0), .out(HPLA_17), .gate(H6));
  Transistor #(.\type ("n")) transistor_182 (.in(1'b0), .out(HPLA_17), .gate(H5));
  Transistor #(.\type ("n")) transistor_183 (.in(1'b0), .out(HPLA_17), .gate(H4));
  Transistor #(.\type ("n")) transistor_184 (.in(1'b0), .out(HPLA_17), .gate(H3));
  Transistor #(.\type ("n")) transistor_185 (.in(1'b0), .out(HPLA_17), .gate(H2));
  Transistor #(.\type ("n")) transistor_186 (.in(1'b0), .out(HPLA_17), .gate(H1));
  Transistor #(.\type ("n")) transistor_187 (.in(1'b0), .out(HPLA_17), .gate(H0));
  Pull_Resistor #(.pull(1)) pull_resistor_29 (.node(HPLA_18));
  Transistor #(.\type ("n")) transistor_188 (.in(1'b0), .out(HPLA_18), .gate(H8));
  Transistor #(.\type ("n")) transistor_189 (.in(1'b0), .out(HPLA_18), .gate(H7));
  Transistor #(.\type ("n")) transistor_190 (.in(1'b0), .out(HPLA_18), .gate(H6));
  Transistor #(.\type ("n")) transistor_191 (.in(1'b0), .out(HPLA_18), .gate(H5));
  Transistor #(.\type ("n")) transistor_192 (.in(1'b0), .out(HPLA_18), .gate(H4));
  Transistor #(.\type ("n")) transistor_193 (.in(1'b0), .out(HPLA_18), .gate(H3));
  Transistor #(.\type ("n")) transistor_194 (.in(1'b0), .out(HPLA_18), .gate(not_7_out));
  Transistor #(.\type ("n")) transistor_195 (.in(1'b0), .out(HPLA_18), .gate(H1));
  Transistor #(.\type ("n")) transistor_196 (.in(1'b0), .out(HPLA_18), .gate(H0));
  Pull_Resistor #(.pull(1)) pull_resistor_30 (.node(HPLA_19));
  Transistor #(.\type ("n")) transistor_197 (.in(1'b0), .out(HPLA_19), .gate(not_1_out));
  Transistor #(.\type ("n")) transistor_198 (.in(1'b0), .out(HPLA_19), .gate(H7));
  Transistor #(.\type ("n")) transistor_199 (.in(1'b0), .out(HPLA_19), .gate(H6));
  Transistor #(.\type ("n")) transistor_200 (.in(1'b0), .out(HPLA_19), .gate(H5));
  Transistor #(.\type ("n")) transistor_201 (.in(1'b0), .out(HPLA_19), .gate(not_5_out));
  Transistor #(.\type ("n")) transistor_202 (.in(1'b0), .out(HPLA_19), .gate(H3));
  Transistor #(.\type ("n")) transistor_203 (.in(1'b0), .out(HPLA_19), .gate(not_7_out));
  Transistor #(.\type ("n")) transistor_204 (.in(1'b0), .out(HPLA_19), .gate(H1));
  Transistor #(.\type ("n")) transistor_205 (.in(1'b0), .out(HPLA_19), .gate(not_9_out));
  Pull_Resistor #(.pull(1)) pull_resistor_31 (.node(HPLA_21));
  Pull_Resistor #(.pull(1)) pull_resistor_32 (.node(HPLA_20));
  Transistor #(.\type ("n")) transistor_206 (.in(1'b0), .out(HPLA_21), .gate(not_1_out));
  Transistor #(.\type ("n")) transistor_207 (.in(1'b0), .out(HPLA_20), .gate(not_1_out));
  Transistor #(.\type ("n")) transistor_208 (.in(1'b0), .out(HPLA_20), .gate(H7));
  Transistor #(.\type ("n")) transistor_209 (.in(1'b0), .out(HPLA_21), .gate(H7));
  Transistor #(.\type ("n")) transistor_210 (.in(1'b0), .out(HPLA_20), .gate(H6));
  Transistor #(.\type ("n")) transistor_211 (.in(1'b0), .out(HPLA_21), .gate(not_3_out));
  Transistor #(.\type ("n")) transistor_212 (.in(1'b0), .out(HPLA_21), .gate(H5));
  Transistor #(.\type ("n")) transistor_213 (.in(1'b0), .out(HPLA_20), .gate(not_4_out));
  Transistor #(.\type ("n")) transistor_214 (.in(1'b0), .out(HPLA_20), .gate(H4));
  Transistor #(.\type ("n")) transistor_215 (.in(1'b0), .out(HPLA_21), .gate(H4));
  Transistor #(.\type ("n")) transistor_216 (.in(1'b0), .out(HPLA_21), .gate(H3));
  Transistor #(.\type ("n")) transistor_217 (.in(1'b0), .out(HPLA_20), .gate(not_6_out));
  Transistor #(.\type ("n")) transistor_218 (.in(1'b0), .out(HPLA_21), .gate(H2));
  Transistor #(.\type ("n")) transistor_219 (.in(1'b0), .out(HPLA_20), .gate(not_7_out));
  Transistor #(.\type ("n")) transistor_220 (.in(1'b0), .out(HPLA_21), .gate(H1));
  Transistor #(.\type ("n")) transistor_221 (.in(1'b0), .out(HPLA_20), .gate(not_8_out));
  Transistor #(.\type ("n")) transistor_222 (.in(1'b0), .out(HPLA_20), .gate(H0));
  Transistor #(.\type ("n")) transistor_223 (.in(1'b0), .out(HPLA_21), .gate(not_9_out));
  Pull_Resistor #(.pull(1)) pull_resistor_33 (.node(HPLA_22));
  Transistor #(.\type ("n")) transistor_224 (.in(1'b0), .out(HPLA_22), .gate(not_1_out));
  Transistor #(.\type ("n")) transistor_225 (.in(1'b0), .out(HPLA_22), .gate(H7));
  Transistor #(.\type ("n")) transistor_226 (.in(1'b0), .out(HPLA_22), .gate(H6));
  Transistor #(.\type ("n")) transistor_227 (.in(1'b0), .out(HPLA_22), .gate(not_4_out));
  Transistor #(.\type ("n")) transistor_228 (.in(1'b0), .out(HPLA_22), .gate(not_5_out));
  Transistor #(.\type ("n")) transistor_229 (.in(1'b0), .out(HPLA_22), .gate(H3));
  Transistor #(.\type ("n")) transistor_230 (.in(1'b0), .out(HPLA_22), .gate(H2));
  Transistor #(.\type ("n")) transistor_231 (.in(1'b0), .out(HPLA_22), .gate(not_8_out));
  Transistor #(.\type ("n")) transistor_232 (.in(1'b0), .out(HPLA_22), .gate(H0));
  Pull_Resistor #(.pull(1)) pull_resistor_34 (.node(HPLA_23));
  Transistor #(.\type ("n")) transistor_233 (.in(1'b0), .out(HPLA_23), .gate(not_1_out));
  Transistor #(.\type ("n")) transistor_234 (.in(1'b0), .out(HPLA_23), .gate(H7));
  Transistor #(.\type ("n")) transistor_235 (.in(1'b0), .out(HPLA_23), .gate(not_3_out));
  Transistor #(.\type ("n")) transistor_236 (.in(1'b0), .out(HPLA_23), .gate(H5));
  Transistor #(.\type ("n")) transistor_237 (.in(1'b0), .out(HPLA_23), .gate(not_5_out));
  Transistor #(.\type ("n")) transistor_238 (.in(1'b0), .out(HPLA_23), .gate(H3));
  Transistor #(.\type ("n")) transistor_239 (.in(1'b0), .out(HPLA_23), .gate(not_7_out));
  Transistor #(.\type ("n")) transistor_240 (.in(1'b0), .out(HPLA_23), .gate(H1));
  Transistor #(.\type ("n")) transistor_241 (.in(1'b0), .out(HPLA_23), .gate(H0));

  assign Hnn = {H5, H4, H3, H2, H1, H0};
  assign VPOS = {V7, V6, V5, V4, V3, V2, V1, V0};

  // Notes on the sheet:
  //   277
  //   272
  //   256
  //   269
  //   65
  //   1
  //   0-255
  //   0-7,256-263
  //   240
  //   339
  //   0
  //   241
  //   63
  //   240
  //   255
  //   311
  //   0-63
  //   311
  //   256-319
  //   265
  //   0-255
  //   0/1
  //   6/7
  //   4/5
  //   320-355
  //   0-255
  //   2/3
  //   256
  //   4
  //   277
  //   302
  //   321
  //   306
  //   H8
  //   H7
  //   H6
  //   H5
  //   H4
  //   H3
  //   H2
  //   H1
  //   H0
  //   340
endmodule

module REGISTER_SELECT (
  input  nDBE,
  input  RC,
  input  RS0,
  input  RS1,
  input  RS2,
  input  R_W,
  output nW0,
  output nW1,
  output nW3,
  output nW4,
  output nW5_1,
  output nW5_2,
  output nW6_1,
  output nW6_2,
  output nW7,
  output nR2,
  output nR4,
  output nR7
);

  wire d_ff_1_q, d_ff_2_q, d_ff_2_qn, decoder_1_out0, decoder_1_out1, decoder_1_out3, decoder_1_out4,
       decoder_1_out5, decoder_1_out6, decoder_1_out7, decoder_2_out2, decoder_2_out4, decoder_2_out7,
       nor_1_out, nor_2_out, nor_3_out, not_1_out, not_2_out, or_1_out;

  D_Flip_Flop #(.trigger("high")) d_ff_1 (
    .clk(nor_2_out), .D(d_ff_2_qn), .Q(d_ff_1_q), .preset(or_1_out));  // open: Qn, en, reset
  not not_1 (not_1_out, nor_2_out);
  not not_2 (not_2_out, R_W);
  Decoder #(.select(3), .disabled(0)) decoder_1 (
    .out0(decoder_1_out0), .out1(decoder_1_out1), .out3(decoder_1_out3), .out4(decoder_1_out4),
    .out5(decoder_1_out5), .out6(decoder_1_out6), .out7(decoder_1_out7), .sel({RS2, RS1, RS0}), .en(not_2_out));  // open: out2
  Decoder #(.select(3), .disabled(0)) decoder_2 (
    .out2(decoder_2_out2), .out4(decoder_2_out4), .out7(decoder_2_out7), .sel({RS2, RS1, RS0}), .en(R_W));  // open: out0, out1, out3, out5, out6
  D_Flip_Flop #(.trigger("high")) d_ff_2 (
    .clk(not_1_out), .D(d_ff_1_q), .Q(d_ff_2_q), .Qn(d_ff_2_qn), .preset(or_1_out));  // open: en, reset
  or or_1 (or_1_out, nor_3_out, RC);
  nor nor_1 (nor_1_out, decoder_1_out6, decoder_1_out5);
  nor nor_2 (nor_2_out, nDBE, nor_1_out);
  nor nor_3 (nor_3_out, nDBE, nR2);
  not not_3 (nW0, decoder_1_out0);
  not not_4 (nW1, decoder_1_out1);
  not not_5 (nW3, decoder_1_out3);
  not not_6 (nW4, decoder_1_out4);
  nand nand_1 (nW5_1, decoder_1_out5, d_ff_2_q);
  nand nand_2 (nW5_2, decoder_1_out5, d_ff_2_qn);
  nand nand_3 (nW6_1, decoder_1_out6, d_ff_2_q);
  nand nand_4 (nW6_2, decoder_1_out6, d_ff_2_qn);
  not not_7 (nW7, decoder_1_out7);
  not not_8 (nR2, decoder_2_out2);
  not not_9 (nR4, decoder_2_out4);
  not not_10 (nR7, decoder_2_out7);

  // Notes on the sheet:
  //   $2005/$2006 first/second write latch
  //   W
  //   R
  //   1ST
  //   2ND
  //   W5/6
  //   R2
endmodule

// VIDEO OUT
module VIDEO_OUT_NTSC (
  input  nCLK,
  input  RES,
  input  nTR,
  input  nTG,
  input  nTB,
  input  [1:0] PCLK,
  input  nCC0,
  input  nCC1,
  input  nCC2,
  input  nCC3,
  input  nPICTURE,
  input  SYNC,
  input  BURST,
  input  nLL0,
  input  nLL1,
  output [10:0] out_16
);

  wire _1, _2, _3, _4, _5, _6, _7, _8, _9, _10, _11, _12, d_latch_1_nq, d_latch_2_nq, d_latch_3_nq,
       d_latch_4_nq, d_latch_8_q, d_latch_9_q, d_latch_10_nq, d_latch_11_nq, d_latch_12_nq, d_latch_13_nq,
       d_latch_14_q, d_latch_15_q, d_latch_16_q, d_latch_18_q, d_latch_20_q, d_latch_22_q, d_latch_24_q,
       decoder_1_out0, decoder_1_out1, decoder_1_out2, decoder_1_out3, multiplexer_1_out, nor_1_out,
       nor_2_out, nor_3_out, nor_4_out, nor_6_out, nor_7_out, nor_10_out, nor_11_out, nor_12_out, nor_15_out,
       nor_16_out, nor_17_out, nor_18_out, nor_21_out, nor_22_out, nor_23_out, nor_24_out, not_1_out,
       not_3_out, not_4_out, not_5_out, not_6_out, not_7_out, not_8_out, not_9_out, not_13_out, not_14_out,
       not_16_out, not_19_out, not_20_out, or_1_out;
  wire [3:0] d_latch_5_nq;

  D_latch d_latch_1 (.EN(PCLK[0]), .D(nCC0), .nQ(d_latch_1_nq));  // open: Q
  D_latch d_latch_2 (.EN(PCLK[0]), .D(nCC1), .nQ(d_latch_2_nq));  // open: Q
  D_latch d_latch_3 (.EN(PCLK[0]), .D(nCC2), .nQ(d_latch_3_nq));  // open: Q
  D_latch d_latch_4 (.EN(PCLK[0]), .D(nCC3), .nQ(d_latch_4_nq));  // open: Q
  or or_1 (or_1_out, SYNC, BURST, nor_6_out);
  not not_1 (not_1_out, SYNC);
  nor nor_1 (nor_1_out, _1, nTR, d_latch_11_nq);
  nor nor_2 (nor_2_out, d_latch_11_nq, nTG, _9);
  nor nor_3 (nor_3_out, d_latch_11_nq, nTB, _5);
  D_latch d_latch_5 (.EN(PCLK[1]), .D(d_latch_1_nq), .nQ(d_latch_5_nq[0]));  // open: Q
  D_latch d_latch_6 (.EN(PCLK[1]), .D(d_latch_2_nq), .nQ(d_latch_5_nq[1]));  // open: Q
  D_latch d_latch_7 (.EN(PCLK[1]), .D(d_latch_3_nq), .nQ(d_latch_5_nq[2]));  // open: Q
  D_latch d_latch_8 (.EN(PCLK[1]), .D(d_latch_4_nq), .Q(d_latch_8_q));  // open: nQ
  D_latch d_latch_9 (.EN(PCLK[1]), .D(BURST), .Q(d_latch_9_q));  // open: nQ
  D_latch d_latch_10 (.EN(PCLK[1]), .D(or_1_out), .nQ(d_latch_10_nq));  // open: Q
  D_latch d_latch_11 (.EN(PCLK[1]), .D(nor_6_out), .nQ(d_latch_11_nq));  // open: Q
  D_latch d_latch_12 (.EN(PCLK[1]), .D(not_1_out), .nQ(d_latch_12_nq));  // open: Q
  D_latch d_latch_13 (.EN(PCLK[1]), .D(BURST), .nQ(d_latch_13_nq));  // open: Q
  nor nor_4 (nor_4_out, nor_1_out, nor_2_out, nor_3_out);
  nor nor_5 (d_latch_5_nq[3], d_latch_8_q, d_latch_9_q);
  nor nor_6 (nor_6_out, nPICTURE, nor_7_out);
  not not_2 (out_16[0], nor_4_out);
  nor nor_7 (nor_7_out, d_latch_5_nq[3], d_latch_5_nq[2], d_latch_5_nq[1]);
  not not_3 (not_3_out, d_latch_11_nq);
  not not_4 (not_4_out, nCLK);
  Decoder #(.select(2), .disabled(0)) decoder_1 (
    .out0(decoder_1_out0), .out1(decoder_1_out1), .out2(decoder_1_out2), .out3(decoder_1_out3),
    .sel({nLL1, nLL0}), .en(not_3_out));
  D_latch d_latch_14 (.EN(not_4_out), .D(not_13_out), .Q(d_latch_14_q));  // open: nQ
  nor nor_8 (_1, d_latch_14_q, RES);
  not not_5 (not_5_out, d_latch_10_nq);
  not not_6 (not_6_out, decoder_1_out0);
  not not_7 (not_7_out, decoder_1_out1);
  not not_8 (not_8_out, decoder_1_out2);
  not not_9 (not_9_out, decoder_1_out3);
  not not_10 (out_16[10], d_latch_12_nq);
  D_latch d_latch_15 (.EN(nCLK), .D(_1), .Q(d_latch_15_q));  // open: nQ
  nor nor_9 (_2, d_latch_15_q, nor_10_out);
  nor nor_10 (nor_10_out, not_13_out, _4);
  D_latch d_latch_16 (.EN(not_4_out), .D(_2), .Q(d_latch_16_q));  // open: nQ
  nor nor_11 (nor_11_out, not_20_out, d_latch_13_nq);
  not not_11 (out_16[6], nor_11_out);
  nor nor_12 (nor_12_out, nor_11_out, d_latch_13_nq);
  not not_12 (out_16[9], nor_12_out);
  nor nor_13 (_3, d_latch_16_q, RES);
  not not_13 (not_13_out, _6);
  or or_2 (out_16[7], not_5_out, not_19_out);
  D_latch d_latch_17 (.EN(nCLK), .D(_3), .nQ(_4));  // open: Q
  or or_3 (out_16[1], not_14_out, not_16_out);
  D_latch d_latch_18 (.EN(not_4_out), .D(_4), .Q(d_latch_18_q));  // open: nQ
  nor nor_14 (_5, d_latch_18_q, RES);
  nor nor_15 (nor_15_out, not_20_out, not_6_out);
  not not_14 (not_14_out, nor_15_out);
  nor nor_16 (nor_16_out, nor_15_out, not_6_out);
  not not_15 (out_16[2], nor_16_out);
  D_latch d_latch_19 (.EN(nCLK), .D(_5), .nQ(_6));  // open: Q
  D_latch d_latch_20 (.EN(not_4_out), .D(_6), .Q(d_latch_20_q));  // open: nQ
  nor nor_17 (nor_17_out, not_20_out, not_7_out);
  nor nor_18 (nor_18_out, nor_17_out, not_7_out);
  nor nor_19 (_7, d_latch_20_q, RES);
  not not_16 (not_16_out, nor_17_out);
  not not_17 (out_16[5], nor_18_out);
  D_latch d_latch_21 (.EN(nCLK), .D(_7), .nQ(_8));  // open: Q
  D_latch d_latch_22 (.EN(not_4_out), .D(_8), .Q(d_latch_22_q));  // open: nQ
  nor nor_20 (_9, d_latch_22_q, RES);
  Multiplexer #(.select(4), .enable("false")) multiplexer_1 (
    .in0(1'b0), .in1(1'b0), .in2(1'b0), .in3(_1), .in4(_8), .in5(_3), .in6(_10), .in7(_5), .in8(_12),
    .in9(_7), .in10(_2), .in11(_9), .in12(_4), .in13(_11), .in14(_6), .in15(1'b1), .out(multiplexer_1_out),
    .sel(d_latch_5_nq));
  not not_18 (out_16[3], nor_21_out);
  nor nor_21 (nor_21_out, not_20_out, not_8_out);
  nor nor_22 (nor_22_out, nor_21_out, not_8_out);
  not not_19 (not_19_out, nor_22_out);
  D_latch d_latch_23 (.EN(nCLK), .D(_9), .nQ(_10));  // open: Q
  not not_20 (not_20_out, multiplexer_1_out);
  D_latch d_latch_24 (.EN(not_4_out), .D(_10), .Q(d_latch_24_q));  // open: nQ
  nor nor_23 (nor_23_out, not_20_out, not_9_out);
  nor nor_24 (nor_24_out, nor_23_out, not_9_out);
  nor nor_25 (_11, d_latch_24_q, RES);
  not not_21 (out_16[4], nor_23_out);
  not not_22 (out_16[8], nor_24_out);
  D_latch d_latch_25 (.EN(nCLK), .D(_11), .nQ(_12));  // open: Q

  // Notes on the sheet:
  //   Emphasis
  //   PCLK
  //   /PCLK
  //   /PR
  //   /PB
  //   /PG
  //   TINT
  //   P123
  //   /POUT
  //   0
  //   1
  //   2
  //   3
  //   Color 1D (black)
  //   Color burst
  //   Synch
  //   /LU0
  //   /LU2
  //   /LU1
  //   /LU3
  //   NTSC
  //   /PZ
endmodule

// VIDEO OUT
module VIDEO_OUT_PAL (
  input  nCLK,
  input  RES,
  input  nTR,
  input  nTG,
  input  nTB,
  input  [1:0] PCLK,
  input  V0,
  input  nCC0,
  input  nCC1,
  input  nCC2,
  input  nCC3,
  input  nPICTURE,
  input  SYNC,
  input  BURST,
  input  nLL0,
  input  nLL1,
  output [10:0] out_17
);

  wire _1, _2, _3, _4, _5, _6, _7, _8, _9, _10, _11, _12, _16_out, _24_out, _31_out, _32_out, _33_out,
       _34_out, _42_out, _44_out, d_latch_1_nq, d_latch_2_nq, d_latch_3_nq, d_latch_4_nq, d_latch_5_nq,
       d_latch_6_nq, d_latch_8_q, d_latch_10_q, d_latch_11_q, d_latch_12_q, d_latch_13_nq, d_latch_14_nq,
       d_latch_15_nq, d_latch_16_nq, d_latch_17_q, d_latch_18_q, d_latch_19_q, d_latch_21_q, d_latch_23_q,
       d_latch_25_q, d_latch_27_q, decoder_1_out0, decoder_1_out1, decoder_1_out2, decoder_1_out3,
       multiplexer_1_out, multiplexer_2_out, multiplexer_3_out, multiplexer_4_out, multiplexer_5_out,
       nor_1_out, nor_2_out, nor_5_out, nor_6_out, nor_8_out, nor_9_out, nor_11_out, nor_12_out, nor_14_out,
       nor_15_out, not_1_out, not_2_out, not_3_out, not_4_out, not_5_out, not_6_out, not_7_out, not_8_out,
       not_10_out, not_11_out, not_12_out, not_13_out, not_17_out, not_19_out, not_20_out, not_22_out,
       not_24_out;
  wire [3:0] d_latch_7_nq;

  not not_1 (not_1_out, nPICTURE);
  D_latch d_latch_1 (.EN(PCLK[0]), .D(nCC0), .nQ(d_latch_1_nq));  // open: Q
  D_latch d_latch_2 (.EN(PCLK[0]), .D(nCC1), .nQ(d_latch_2_nq));  // open: Q
  D_latch d_latch_3 (.EN(PCLK[0]), .D(nCC2), .nQ(d_latch_3_nq));  // open: Q
  D_latch d_latch_4 (.EN(PCLK[0]), .D(nCC3), .nQ(d_latch_4_nq));  // open: Q
  D_latch d_latch_5 (.EN(PCLK[1]), .D(not_1_out), .nQ(d_latch_5_nq));  // open: Q
  or _42 (_42_out, _44_out, SYNC, BURST);
  not not_2 (not_2_out, SYNC);
  nor _31 (_31_out, not_4_out, nTR, d_latch_13_nq);
  nor _32 (_32_out, d_latch_13_nq, nTG, not_5_out);
  nor _33 (_33_out, d_latch_13_nq, nTB, _5);
  D_latch d_latch_6 (.EN(PCLK[1]), .D(V0), .nQ(d_latch_6_nq));  // open: Q
  D_latch d_latch_7 (.EN(PCLK[1]), .D(d_latch_1_nq), .nQ(d_latch_7_nq[0]));  // open: Q
  D_latch d_latch_8 (.EN(PCLK[1]), .D(d_latch_2_nq), .Q(d_latch_8_q));  // open: nQ
  D_latch d_latch_9 (.EN(PCLK[1]), .D(d_latch_3_nq), .nQ(d_latch_7_nq[2]));  // open: Q
  D_latch d_latch_10 (.EN(PCLK[1]), .D(d_latch_4_nq), .Q(d_latch_10_q));  // open: nQ
  D_latch d_latch_11 (.EN(PCLK[0]), .D(d_latch_5_nq), .Q(d_latch_11_q));  // open: nQ
  D_latch d_latch_12 (.EN(PCLK[1]), .D(BURST), .Q(d_latch_12_q));  // open: nQ
  D_latch d_latch_13 (.EN(PCLK[1]), .D(_44_out), .nQ(d_latch_13_nq));  // open: Q
  D_latch d_latch_14 (.EN(PCLK[1]), .D(_42_out), .nQ(d_latch_14_nq));  // open: Q
  D_latch d_latch_15 (.EN(PCLK[1]), .D(not_2_out), .nQ(d_latch_15_nq));  // open: Q
  D_latch d_latch_16 (.EN(PCLK[1]), .D(BURST), .nQ(d_latch_16_nq));  // open: Q
  nor _34 (_34_out, _31_out, _32_out, _33_out);
  not not_3 (not_3_out, _34_out);
  nor _18 (d_latch_7_nq[1], d_latch_8_q, d_latch_12_q);
  nor _20 (d_latch_7_nq[3], d_latch_10_q, d_latch_12_q);
  nor _44 (_44_out, d_latch_11_q, _24_out);
  not not_4 (not_4_out, multiplexer_1_out);
  not not_5 (not_5_out, multiplexer_2_out);
  nor _24 (_24_out, d_latch_7_nq[3], d_latch_7_nq[2], d_latch_7_nq[1]);
  not not_6 (not_6_out, d_latch_13_nq);
  Decoder #(.select(2), .disabled(0)) decoder_1 (
    .out0(decoder_1_out0), .out1(decoder_1_out1), .out2(decoder_1_out2), .out3(decoder_1_out3),
    .sel({nLL1, nLL0}), .en(not_6_out));
  Multiplexer #(.enable("false")) multiplexer_1 (.in0(_7), .in1(_3), .out(multiplexer_1_out), .sel(d_latch_6_nq));
  Multiplexer #(.enable("false")) multiplexer_2 (.in0(_3), .in1(_7), .out(multiplexer_2_out), .sel(d_latch_6_nq));
  not not_7 (not_7_out, nCLK);
  not not_8 (not_8_out, d_latch_14_nq);
  not not_9 (out_17[10], d_latch_15_nq);
  not not_10 (not_10_out, decoder_1_out0);
  not not_11 (not_11_out, decoder_1_out1);
  not not_12 (not_12_out, decoder_1_out2);
  not not_13 (not_13_out, decoder_1_out3);
  D_latch d_latch_17 (.EN(not_7_out), .D(not_22_out), .Q(d_latch_17_q));  // open: nQ
  not not_14 (out_17[0], not_3_out);
  nor nor_1 (nor_1_out, not_19_out, d_latch_16_nq);
  nor nor_2 (nor_2_out, nor_1_out, d_latch_16_nq);
  nor nor_3 (_1, RES, d_latch_17_q);
  or or_1 (out_17[7], not_8_out, not_24_out);
  not not_15 (out_17[6], nor_1_out);
  not not_16 (out_17[9], nor_2_out);
  D_latch d_latch_18 (.EN(nCLK), .D(_1), .Q(d_latch_18_q));  // open: nQ
  nor _16 (_16_out, not_22_out, _4);
  nor nor_4 (_2, d_latch_18_q, _16_out);
  Multiplexer #(.select(4), .enable("false")) multiplexer_3 (
    .in0(1'b0), .in1(1'b0), .in2(1'b0), .in3(_2), .in4(_7), .in5(_12), .in6(_5), .in7(_10), .in8(_3),
    .in9(_8), .in10(_1), .in11(_6), .in12(_11), .in13(_4), .in14(_9), .in15(1'b1), .out(multiplexer_3_out),
    .sel(d_latch_7_nq));
  Multiplexer #(.select(4), .enable("false")) multiplexer_4 (
    .in0(1'b0), .in1(1'b0), .in2(1'b0), .in3(_1), .in4(_8), .in5(_3), .in6(_10), .in7(_5), .in8(_12),
    .in9(_7), .in10(_2), .in11(_9), .in12(_4), .in13(_11), .in14(_6), .in15(1'b1), .out(multiplexer_4_out),
    .sel(d_latch_7_nq));
  nor nor_5 (nor_5_out, not_19_out, not_10_out);
  nor nor_6 (nor_6_out, nor_5_out, not_10_out);
  or or_2 (out_17[1], not_17_out, not_20_out);
  D_latch d_latch_19 (.EN(not_7_out), .D(_2), .Q(d_latch_19_q));  // open: nQ
  Multiplexer #(.enable("false")) multiplexer_5 (
    .in0(multiplexer_3_out), .in1(multiplexer_4_out), .out(multiplexer_5_out), .sel(d_latch_6_nq));
  not not_17 (not_17_out, nor_5_out);
  not not_18 (out_17[2], nor_6_out);
  nor nor_7 (_3, RES, d_latch_19_q);
  D_latch d_latch_20 (.EN(nCLK), .D(_3), .nQ(_4));  // open: Q
  not not_19 (not_19_out, multiplexer_5_out);
  D_latch d_latch_21 (.EN(not_7_out), .D(_4), .Q(d_latch_21_q));  // open: nQ
  nor nor_8 (nor_8_out, not_19_out, not_11_out);
  not not_20 (not_20_out, nor_8_out);
  not not_21 (out_17[5], nor_9_out);
  nor nor_9 (nor_9_out, nor_8_out, not_11_out);
  nor nor_10 (_5, RES, d_latch_21_q);
  D_latch d_latch_22 (.EN(nCLK), .D(_5), .nQ(_6));  // open: Q
  not not_22 (not_22_out, _6);
  nor nor_11 (nor_11_out, not_19_out, not_12_out);
  nor nor_12 (nor_12_out, nor_11_out, not_12_out);
  D_latch d_latch_23 (.EN(not_7_out), .D(_6), .Q(d_latch_23_q));  // open: nQ
  not not_23 (out_17[3], nor_11_out);
  not not_24 (not_24_out, nor_12_out);
  nor nor_13 (_7, RES, d_latch_23_q);
  nor nor_14 (nor_14_out, not_19_out, not_13_out);
  nor nor_15 (nor_15_out, nor_14_out, not_13_out);
  D_latch d_latch_24 (.EN(nCLK), .D(_7), .nQ(_8));  // open: Q
  not not_25 (out_17[4], nor_14_out);
  not not_26 (out_17[8], nor_15_out);
  D_latch d_latch_25 (.EN(not_7_out), .D(_8), .Q(d_latch_25_q));  // open: nQ
  nor nor_16 (_9, RES, d_latch_25_q);
  D_latch d_latch_26 (.EN(nCLK), .D(_9), .nQ(_10));  // open: Q
  D_latch d_latch_27 (.EN(not_7_out), .D(_10), .Q(d_latch_27_q));  // open: nQ
  nor nor_17 (_11, RES, d_latch_27_q);
  D_latch d_latch_28 (.EN(nCLK), .D(_11), .nQ(_12));  // open: Q

  // Notes on the sheet:
  //   Emphasis
  //   PCLK
  //   23
  //   25
  //   22
  //   21
  //   50
  //   !
  //   17
  //   18
  //   19
  //   20
  //   51
  //   !
  //   41
  //   /PCLK
  //   52
  //   !
  //   45
  //   47
  //   46
  //   48
  //   /PR
  //   /PG
  //   35
  //   /PB
  //   /POUT
  //   14
  //   13
  //   TINT
  //   /POUT
  //   P123
  //   /V0'
  //   Color 1D (black)
  //   Synch
  //   Color burst
  //   0
  //   1
  //   2
  //   3
  //   /LU0
  //   /LU1
  //   /LU2
  //   /LU3
  //   1
  //   49
  //   TINT
  //   2
  //   PAL
  //   3
  //   4
  //   5
  //   6
  //   15
  //   7
  //   8
  //   9
  //   10
  //   11
  //   12
endmodule

module VIDEO_OUT_RGB (
  input  [1:0] PCLK,
  input  nPICTURE,
  input  nTR,
  input  nTG,
  input  nTB,
  input  nCC0,
  input  nCC1,
  input  nCC2,
  input  nCC3,
  input  nLL0,
  input  nLL1,
  input  SYNC,
  output R0,
  output R1,
  output R2,
  output R3,
  output R4,
  output R5,
  output R6,
  output R7,
  output G0,
  output G1,
  output G2,
  output G3,
  output G4,
  output G5,
  output G6,
  output G7,
  output B0,
  output B1,
  output B2,
  output B3,
  output B4,
  output B5,
  output B6,
  output B7,
  output SYNC_2
);

  wire d_latch_5_nq, d_latch_6_nq, d_latch_7_nq, decoder_1_out0, decoder_1_out1, decoder_1_out2,
       decoder_1_out3, decoder_1_out4, decoder_1_out5, decoder_1_out6, decoder_1_out7, decoder_1_out8,
       decoder_1_out9, decoder_1_out10, decoder_1_out11, decoder_1_out12, decoder_1_out13, decoder_1_out14,
       decoder_1_out15, decoder_2_out0, decoder_2_out1, decoder_2_out2, decoder_2_out3, decoder_2_out4,
       decoder_2_out5, decoder_2_out6, decoder_2_out7, decoder_3_out0, decoder_3_out1, decoder_3_out2,
       decoder_3_out3, decoder_3_out4, decoder_3_out5, decoder_3_out6, decoder_3_out7, decoder_4_out0,
       decoder_4_out1, decoder_4_out2, decoder_4_out3, decoder_4_out4, decoder_4_out5, decoder_4_out6,
       decoder_4_out7, nor_1_out, nor_2_out, not_1_out, sel16x12_b_1_out0, sel16x12_b_1_out1,
       sel16x12_b_1_out2, sel16x12_b_1_out3, sel16x12_b_1_out4, sel16x12_b_1_out5, sel16x12_b_1_out6,
       sel16x12_b_1_out7, sel16x12_b_1_out8, sel16x12_b_1_out9, sel16x12_b_1_out10, sel16x12_b_1_out11,
       sel16x12_g_1_out0, sel16x12_g_1_out1, sel16x12_g_1_out2, sel16x12_g_1_out3, sel16x12_g_1_out4,
       sel16x12_g_1_out5, sel16x12_g_1_out6, sel16x12_g_1_out7, sel16x12_g_1_out8, sel16x12_g_1_out9,
       sel16x12_g_1_out10, sel16x12_g_1_out11, sel16x12_r_1_out0, sel16x12_r_1_out1, sel16x12_r_1_out2,
       sel16x12_r_1_out3, sel16x12_r_1_out4, sel16x12_r_1_out5, sel16x12_r_1_out6, sel16x12_r_1_out7,
       sel16x12_r_1_out8, sel16x12_r_1_out9, sel16x12_r_1_out10, sel16x12_r_1_out11;
  wire [2:0] sel12x3_1_out0, sel12x3_2_out0, sel12x3_3_out0;
  wire [3:0] d_latch_1_nq;

  not not_1 (not_1_out, nPICTURE);
  D_latch d_latch_1 (.EN(PCLK[1]), .D(nCC0), .nQ(d_latch_1_nq[0]));  // open: Q
  D_latch d_latch_2 (.EN(PCLK[1]), .D(nCC1), .nQ(d_latch_1_nq[1]));  // open: Q
  D_latch d_latch_3 (.EN(PCLK[1]), .D(nCC2), .nQ(d_latch_1_nq[2]));  // open: Q
  D_latch d_latch_4 (.EN(PCLK[1]), .D(nCC3), .nQ(d_latch_1_nq[3]));  // open: Q
  D_latch d_latch_5 (.EN(PCLK[1]), .D(SYNC), .nQ(d_latch_5_nq));  // open: Q
  D_latch d_latch_6 (.EN(PCLK[0]), .D(d_latch_5_nq), .nQ(d_latch_6_nq));  // open: Q
  Decoder #(.select(4), .disabled(0)) decoder_1 (
    .out0(decoder_1_out0), .out1(decoder_1_out1), .out2(decoder_1_out2), .out3(decoder_1_out3),
    .out4(decoder_1_out4), .out5(decoder_1_out5), .out6(decoder_1_out6), .out7(decoder_1_out7),
    .out8(decoder_1_out8), .out9(decoder_1_out9), .out10(decoder_1_out10), .out11(decoder_1_out11),
    .out12(decoder_1_out12), .out13(decoder_1_out13), .out14(decoder_1_out14), .out15(decoder_1_out15),
    .sel(d_latch_1_nq), .en(PCLK[0]));
  D_latch d_latch_7 (.EN(PCLK[1]), .D(d_latch_6_nq), .nQ(d_latch_7_nq));  // open: Q
  SEL16x12_R sel16x12_r_1 (
    .PCLK(PCLK[0]), .OUT0(sel16x12_r_1_out0), .OUT1(sel16x12_r_1_out1), .OUT2(sel16x12_r_1_out2),
    .OUT3(sel16x12_r_1_out3), .OUT4(sel16x12_r_1_out4), .OUT5(sel16x12_r_1_out5), .OUT6(sel16x12_r_1_out6),
    .OUT7(sel16x12_r_1_out7), .OUT8(sel16x12_r_1_out8), .OUT9(sel16x12_r_1_out9), .OUT10(sel16x12_r_1_out10),
    .OUT11(sel16x12_r_1_out11), ._15(decoder_1_out15), ._14(decoder_1_out14), ._13(decoder_1_out13),
    ._12(decoder_1_out12), ._11(decoder_1_out11), ._10(decoder_1_out10), ._9(decoder_1_out9),
    ._8(decoder_1_out8), ._7(decoder_1_out7), ._6(decoder_1_out6), ._5(decoder_1_out5), ._4(decoder_1_out4),
    ._3(decoder_1_out3), ._2(decoder_1_out2), ._1(decoder_1_out1), ._0(decoder_1_out0));
  SEL16x12_G sel16x12_g_1 (
    .PCLK(PCLK[0]), .OUT0(sel16x12_g_1_out0), .OUT1(sel16x12_g_1_out1), .OUT2(sel16x12_g_1_out2),
    .OUT3(sel16x12_g_1_out3), .OUT4(sel16x12_g_1_out4), .OUT5(sel16x12_g_1_out5), .OUT6(sel16x12_g_1_out6),
    .OUT7(sel16x12_g_1_out7), .OUT8(sel16x12_g_1_out8), .OUT9(sel16x12_g_1_out9), .OUT10(sel16x12_g_1_out10),
    .OUT11(sel16x12_g_1_out11), ._15(decoder_1_out15), ._14(decoder_1_out14), ._13(decoder_1_out13),
    ._12(decoder_1_out12), ._11(decoder_1_out11), ._10(decoder_1_out10), ._9(decoder_1_out9),
    ._8(decoder_1_out8), ._7(decoder_1_out7), ._6(decoder_1_out6), ._5(decoder_1_out5), ._4(decoder_1_out4),
    ._3(decoder_1_out3), ._2(decoder_1_out2), ._1(decoder_1_out1), ._0(decoder_1_out0));
  SEL16x12_B sel16x12_b_1 (
    .PCLK(PCLK[0]), .OUT0(sel16x12_b_1_out0), .OUT1(sel16x12_b_1_out1), .OUT2(sel16x12_b_1_out2),
    .OUT3(sel16x12_b_1_out3), .OUT4(sel16x12_b_1_out4), .OUT5(sel16x12_b_1_out5), .OUT6(sel16x12_b_1_out6),
    .OUT7(sel16x12_b_1_out7), .OUT8(sel16x12_b_1_out8), .OUT9(sel16x12_b_1_out9), .OUT10(sel16x12_b_1_out10),
    .OUT11(sel16x12_b_1_out11), ._15(decoder_1_out15), ._14(decoder_1_out14), ._13(decoder_1_out13),
    ._12(decoder_1_out12), ._11(decoder_1_out11), ._10(decoder_1_out10), ._9(decoder_1_out9),
    ._8(decoder_1_out8), ._7(decoder_1_out7), ._6(decoder_1_out6), ._5(decoder_1_out5), ._4(decoder_1_out4),
    ._3(decoder_1_out3), ._2(decoder_1_out2), ._1(decoder_1_out1), ._0(decoder_1_out0));
  nor nor_1 (nor_1_out, PCLK[1], nLL0);
  nor nor_2 (nor_2_out, PCLK[1], nLL1);
  SEL12x3 sel12x3_1 (
    .PCLK(PCLK[0]), .nTx(nTR), .IN0(sel16x12_r_1_out0), .IN1(sel16x12_r_1_out1), .IN2(sel16x12_r_1_out2),
    .IN3(sel16x12_r_1_out3), .IN4(sel16x12_r_1_out4), .IN5(sel16x12_r_1_out5), .IN6(sel16x12_r_1_out6),
    .IN7(sel16x12_r_1_out7), .IN8(sel16x12_r_1_out8), .IN9(sel16x12_r_1_out9), .IN10(sel16x12_r_1_out10),
    .IN11(sel16x12_r_1_out11), .OUT2(sel12x3_1_out0[2]), .OUT1(sel12x3_1_out0[1]), .OUT0(sel12x3_1_out0[0]),
    ._0(nor_1_out), ._1(nor_2_out));
  SEL12x3 sel12x3_2 (
    .PCLK(PCLK[0]), .nTx(nTG), .IN0(sel16x12_g_1_out0), .IN1(sel16x12_g_1_out1), .IN2(sel16x12_g_1_out2),
    .IN3(sel16x12_g_1_out3), .IN4(sel16x12_g_1_out4), .IN5(sel16x12_g_1_out5), .IN6(sel16x12_g_1_out6),
    .IN7(sel16x12_g_1_out7), .IN8(sel16x12_g_1_out8), .IN9(sel16x12_g_1_out9), .IN10(sel16x12_g_1_out10),
    .IN11(sel16x12_g_1_out11), .OUT2(sel12x3_2_out0[2]), .OUT1(sel12x3_2_out0[1]), .OUT0(sel12x3_2_out0[0]),
    ._0(nor_1_out), ._1(nor_2_out));
  SEL12x3 sel12x3_3 (
    .PCLK(PCLK[0]), .nTx(nTB), .IN0(sel16x12_b_1_out0), .IN1(sel16x12_b_1_out1), .IN2(sel16x12_b_1_out2),
    .IN3(sel16x12_b_1_out3), .IN4(sel16x12_b_1_out4), .IN5(sel16x12_b_1_out5), .IN6(sel16x12_b_1_out6),
    .IN7(sel16x12_b_1_out7), .IN8(sel16x12_b_1_out8), .IN9(sel16x12_b_1_out9), .IN10(sel16x12_b_1_out10),
    .IN11(sel16x12_b_1_out11), .OUT2(sel12x3_3_out0[2]), .OUT1(sel12x3_3_out0[1]), .OUT0(sel12x3_3_out0[0]),
    ._0(nor_1_out), ._1(nor_2_out));
  Decoder #(.select(3), .disabled(0)) decoder_2 (
    .out0(decoder_2_out0), .out1(decoder_2_out1), .out2(decoder_2_out2), .out3(decoder_2_out3),
    .out4(decoder_2_out4), .out5(decoder_2_out5), .out6(decoder_2_out6), .out7(decoder_2_out7),
    .sel(sel12x3_1_out0), .en(not_1_out));
  Decoder #(.select(3), .disabled(0)) decoder_3 (
    .out0(decoder_3_out0), .out1(decoder_3_out1), .out2(decoder_3_out2), .out3(decoder_3_out3),
    .out4(decoder_3_out4), .out5(decoder_3_out5), .out6(decoder_3_out6), .out7(decoder_3_out7),
    .sel(sel12x3_2_out0), .en(not_1_out));
  Decoder #(.select(3), .disabled(0)) decoder_4 (
    .out0(decoder_4_out0), .out1(decoder_4_out1), .out2(decoder_4_out2), .out3(decoder_4_out3),
    .out4(decoder_4_out4), .out5(decoder_4_out5), .out6(decoder_4_out6), .out7(decoder_4_out7),
    .sel(sel12x3_3_out0), .en(not_1_out));
  D_latch d_latch_8 (.EN(PCLK[1]), .D(decoder_2_out0), .Q(R0));  // open: nQ
  D_latch d_latch_9 (.EN(PCLK[1]), .D(decoder_2_out1), .Q(R1));  // open: nQ
  D_latch d_latch_10 (.EN(PCLK[1]), .D(decoder_2_out2), .Q(R2));  // open: nQ
  D_latch d_latch_11 (.EN(PCLK[1]), .D(decoder_2_out3), .Q(R3));  // open: nQ
  D_latch d_latch_12 (.EN(PCLK[1]), .D(decoder_2_out4), .Q(R4));  // open: nQ
  D_latch d_latch_13 (.EN(PCLK[1]), .D(decoder_2_out5), .Q(R5));  // open: nQ
  D_latch d_latch_14 (.EN(PCLK[1]), .D(decoder_2_out6), .Q(R6));  // open: nQ
  D_latch d_latch_15 (.EN(PCLK[1]), .D(decoder_2_out7), .Q(R7));  // open: nQ
  D_latch d_latch_16 (.EN(PCLK[1]), .D(decoder_3_out0), .Q(G0));  // open: nQ
  D_latch d_latch_17 (.EN(PCLK[1]), .D(decoder_3_out1), .Q(G1));  // open: nQ
  D_latch d_latch_18 (.EN(PCLK[1]), .D(decoder_3_out2), .Q(G2));  // open: nQ
  D_latch d_latch_19 (.EN(PCLK[1]), .D(decoder_3_out3), .Q(G3));  // open: nQ
  D_latch d_latch_20 (.EN(PCLK[1]), .D(decoder_3_out4), .Q(G4));  // open: nQ
  D_latch d_latch_21 (.EN(PCLK[1]), .D(decoder_3_out5), .Q(G5));  // open: nQ
  D_latch d_latch_22 (.EN(PCLK[1]), .D(decoder_3_out6), .Q(G6));  // open: nQ
  D_latch d_latch_23 (.EN(PCLK[1]), .D(decoder_3_out7), .Q(G7));  // open: nQ
  D_latch d_latch_24 (.EN(PCLK[1]), .D(decoder_4_out0), .Q(B0));  // open: nQ
  D_latch d_latch_25 (.EN(PCLK[1]), .D(decoder_4_out1), .Q(B1));  // open: nQ
  D_latch d_latch_26 (.EN(PCLK[1]), .D(decoder_4_out2), .Q(B2));  // open: nQ
  D_latch d_latch_27 (.EN(PCLK[1]), .D(decoder_4_out3), .Q(B3));  // open: nQ
  D_latch d_latch_28 (.EN(PCLK[1]), .D(decoder_4_out4), .Q(B4));  // open: nQ
  D_latch d_latch_29 (.EN(PCLK[1]), .D(decoder_4_out5), .Q(B5));  // open: nQ
  D_latch d_latch_30 (.EN(PCLK[1]), .D(decoder_4_out6), .Q(B6));  // open: nQ
  D_latch d_latch_31 (.EN(PCLK[1]), .D(decoder_4_out7), .Q(B7));  // open: nQ
  not not_2 (SYNC_2, d_latch_7_nq);

  // Other names for the same wires on the sheet: PCLK_t = PCLK[0]; nPCLK = PCLK[1]

  // Notes on the sheet:
  //   0
  //   1
  //   2
  //   0
  //   1
  //   2
  //   0
  //   1
  //   2
  //   R
  //   G
  //   B
endmodule

module RW_CONTROL (
  input  R_W,
  input  nDBE,
  output nRD,
  output nWR
);

  wire nor_1_out, nor_2_out, not_1_out;

  not not_1 (not_1_out, R_W);
  nor nor_1 (nor_1_out, not_1_out, nDBE);
  nor nor_2 (nor_2_out, R_W, nDBE);
  not not_2 (nRD, nor_1_out);
  not not_3 (nWR, nor_2_out);

  // Notes on the sheet:
  //   R/W = 0: write data to PPU
  //   /RD = 0: CPU read data from PPU
  //   /WR = 0: CPU write data to PPU
endmodule

// CPU DATA IO
module CPU_DATA_IO (
  input  nRD,
  input  nWR,
  input  [7:0] PPU_CPU,
  input  D0,
  input  D1,
  input  D2,
  input  D3,
  input  D4,
  input  D5,
  input  D6,
  input  D7,
  output D0_2,
  output D1_2,
  output D2_2,
  output D3_2,
  output D4_2,
  output D5_2,
  output D6_2,
  output D7_2,
  output [7:0] CPU_PPU
);

  wire not_1_out, not_2_out;

  not not_1 (not_1_out, nRD);
  not not_2 (not_2_out, nWR);
  assign CPU_PPU = not_2_out ? {D7, D6, D5, D4, D3, D2, D1, D0} : 8'bz;  // Controlled_Buffer controlled_buffer_1
  assign {D7_2, D6_2, D5_2, D4_2, D3_2, D2_2, D1_2, D0_2} = not_1_out ? PPU_CPU : 8'bz;  // Controlled_Buffer controlled_buffer_2

  // Notes on the sheet:
  //   /RD = 0: CPU read data from PPU
  //   /WR = 0: CPU write data to PPU
endmodule

module INTERRUPT_CONTROL (
  input  VBL_EN,
  input  [1:0] PCLK,
  input  VSET,
  input  RESCL,
  input  nDBE,
  input  nR2,
  output INT,
  output DB7
);

  wire d_latch_1_nq, d_latch_2_q, d_latch_3_q, nor_1_out, nor_2_out, not_1_out, not_2_out, or_1_out,
       s_r_ff_1_qn;

  not not_1 (not_1_out, VBL_EN);
  D_latch d_latch_1 (.EN(PCLK[0]), .D(VSET), .nQ(d_latch_1_nq));  // open: Q
  nor nor_1 (nor_1_out, nDBE, nR2);
  D_latch d_latch_2 (.EN(PCLK[1]), .D(d_latch_1_nq), .Q(d_latch_2_q));  // open: nQ
  nor nor_2 (nor_2_out, PCLK[1], d_latch_2_q, VSET);
  or or_1 (or_1_out, RESCL, nor_1_out);
  S_R_Flip_Flop #(.trigger("high")) s_r_ff_1 (
    .Qn(s_r_ff_1_qn), .preset(nor_2_out), .reset(or_1_out));  // open: S, clk, R, Q, en
  not not_2 (not_2_out, nor_1_out);
  nor nor_3 (INT, not_1_out, s_r_ff_1_qn);
  D_latch d_latch_3 (.EN(not_2_out), .D(s_r_ff_1_qn), .Q(d_latch_3_q));  // open: nQ
  Multiplexer multiplexer_1 (.in0(1'b0), .in1(1'b1), .out(DB7), .sel(d_latch_3_q), .en(nor_1_out));

  // Notes on the sheet:
  //   R2_EN
  //   VBLANK FLIP/FLOP
  //   TRI-STATE
endmodule

module COLOR_IO (
  input  [1:0] PCLK,
  input  nDB_CB,
  input  nCB_DB,
  input  nBW,
  input  RAM_CB0,
  input  DB0,
  input  RAM_CB1,
  input  DB1,
  input  RAM_CB2,
  input  DB2,
  input  RAM_CB3,
  input  DB3,
  input  RAM_CB4,
  input  DB4,
  input  RAM_CB5,
  input  DB5,
  output nout0,
  output DB0_2,
  output CB_RAM0,
  output nout1,
  output DB1_2,
  output CB_RAM1,
  output nout2,
  output DB2_2,
  output CB_RAM2,
  output nout3,
  output DB3_2,
  output CB_RAM3,
  output nout4,
  output DB4_2,
  output CB_RAM4,
  output nout5,
  output DB5_2,
  output CB_RAM5
);

  wire _11_2_out, _11_3_out, _11_4_out, _11_5_out, _11_6_out, _11_out, d_ff_1_q, d_ff_2_q, d_ff_3_q,
       d_ff_4_q, d_ff_5_q, d_ff_6_q, d_latch_5_nq, d_latch_6_nq, d_latch_7_nq, d_latch_8_nq, d_latch_9_nq,
       d_latch_10_nq, d_latch_11_nq, d_latch_12_nq, d_latch_13_nq, d_latch_14_nq, d_latch_15_nq,
       d_latch_16_nq, d_latch_17_nq, d_latch_18_nq, d_latch_20_nq, d_latch_22_nq, not_1_out, not_2_out,
       not_3_out, not_4_out, not_5_out, not_6_out, not_7_out, not_8_out, not_9_out, not_10_out, not_11_out,
       not_12_out, not_13_out;

  D_Flip_Flop #(.trigger("high")) d_ff_1 (.clk(PCLK[0]), .D(RAM_CB0), .Q(d_ff_1_q));  // open: Qn, preset, en, reset
  D_Flip_Flop #(.trigger("high")) d_ff_2 (.clk(PCLK[0]), .D(RAM_CB1), .Q(d_ff_2_q));  // open: Qn, preset, en, reset
  D_Flip_Flop #(.trigger("high")) d_ff_3 (.clk(PCLK[0]), .D(RAM_CB2), .Q(d_ff_3_q));  // open: Qn, preset, en, reset
  D_Flip_Flop #(.trigger("high")) d_ff_4 (.clk(PCLK[0]), .D(RAM_CB3), .Q(d_ff_4_q));  // open: Qn, preset, en, reset
  D_Flip_Flop #(.trigger("high")) d_ff_5 (.clk(PCLK[0]), .D(RAM_CB4), .Q(d_ff_5_q));  // open: Qn, preset, en, reset
  D_Flip_Flop #(.trigger("high")) d_ff_6 (.clk(PCLK[0]), .D(RAM_CB5), .Q(d_ff_6_q));  // open: Qn, preset, en, reset
  nand _11 (_11_out, d_ff_1_q, nBW);
  nand _11_2 (_11_2_out, d_ff_2_q, nBW);
  nand _11_3 (_11_3_out, d_ff_3_q, nBW);
  nand _11_4 (_11_4_out, d_ff_4_q, nBW);
  nand _11_5 (_11_5_out, d_ff_5_q, 1'b1);
  nand _11_6 (_11_6_out, d_ff_6_q, 1'b1);
  not not_1 (not_1_out, _11_out);
  not not_2 (not_2_out, DB0);
  not not_3 (not_3_out, _11_2_out);
  not not_4 (not_4_out, DB1);
  not not_5 (not_5_out, _11_3_out);
  not not_6 (not_6_out, DB2);
  not not_7 (not_7_out, _11_4_out);
  not not_8 (not_8_out, DB3);
  not not_9 (not_9_out, _11_5_out);
  not not_10 (not_10_out, DB4);
  not not_11 (not_11_out, _11_6_out);
  not not_12 (not_12_out, DB5);
  D_latch d_latch_1 (.EN(PCLK[1]), .D(not_1_out), .nQ(nout0));  // open: Q
  D_latch d_latch_2 (.EN(PCLK[1]), .D(not_3_out), .nQ(nout1));  // open: Q
  D_latch d_latch_3 (.EN(PCLK[1]), .D(not_5_out), .nQ(nout2));  // open: Q
  D_latch d_latch_4 (.EN(PCLK[1]), .D(not_7_out), .nQ(nout3));  // open: Q
  D_latch d_latch_5 (.EN(PCLK[1]), .D(not_9_out), .nQ(d_latch_5_nq));  // open: Q
  D_latch d_latch_6 (.EN(PCLK[1]), .D(not_11_out), .nQ(d_latch_6_nq));  // open: Q
  D_latch d_latch_7 (.EN(PCLK[0]), .D(not_1_out), .nQ(d_latch_7_nq));  // open: Q
  D_latch d_latch_8 (.EN(PCLK[0]), .D(not_3_out), .nQ(d_latch_8_nq));  // open: Q
  D_latch d_latch_9 (.EN(PCLK[0]), .D(not_5_out), .nQ(d_latch_9_nq));  // open: Q
  D_latch d_latch_10 (.EN(PCLK[0]), .D(not_7_out), .nQ(d_latch_10_nq));  // open: Q
  D_latch d_latch_11 (.EN(PCLK[0]), .D(d_latch_5_nq), .nQ(d_latch_11_nq));  // open: Q
  D_latch d_latch_12 (.EN(PCLK[0]), .D(not_9_out), .nQ(d_latch_12_nq));  // open: Q
  D_latch d_latch_13 (.EN(PCLK[0]), .D(d_latch_6_nq), .nQ(d_latch_13_nq));  // open: Q
  D_latch d_latch_14 (.EN(PCLK[0]), .D(not_11_out), .nQ(d_latch_14_nq));  // open: Q
  not not_13 (not_13_out, nCB_DB);
  D_latch d_latch_15 (.EN(PCLK[1]), .D(d_latch_7_nq), .nQ(d_latch_15_nq));  // open: Q
  D_latch d_latch_16 (.EN(PCLK[1]), .D(d_latch_8_nq), .nQ(d_latch_16_nq));  // open: Q
  D_latch d_latch_17 (.EN(PCLK[1]), .D(d_latch_9_nq), .nQ(d_latch_17_nq));  // open: Q
  D_latch d_latch_18 (.EN(PCLK[1]), .D(d_latch_10_nq), .nQ(d_latch_18_nq));  // open: Q
  D_latch d_latch_19 (.EN(PCLK[1]), .D(d_latch_11_nq), .nQ(nout4));  // open: Q
  D_latch d_latch_20 (.EN(PCLK[1]), .D(d_latch_12_nq), .nQ(d_latch_20_nq));  // open: Q
  D_latch d_latch_21 (.EN(PCLK[1]), .D(d_latch_13_nq), .nQ(nout5));  // open: Q
  D_latch d_latch_22 (.EN(PCLK[1]), .D(d_latch_14_nq), .nQ(d_latch_22_nq));  // open: Q
  assign DB0_2 = not_13_out ? d_latch_15_nq : 1'bz;  // Controlled_Buffer controlled_buffer_1
  assign DB1_2 = not_13_out ? d_latch_16_nq : 1'bz;  // Controlled_Buffer controlled_buffer_2
  assign DB2_2 = not_13_out ? d_latch_17_nq : 1'bz;  // Controlled_Buffer controlled_buffer_3
  assign DB3_2 = not_13_out ? d_latch_18_nq : 1'bz;  // Controlled_Buffer controlled_buffer_4
  assign DB4_2 = not_13_out ? d_latch_20_nq : 1'bz;  // Controlled_Buffer controlled_buffer_5
  assign DB5_2 = not_13_out ? d_latch_22_nq : 1'bz;  // Controlled_Buffer controlled_buffer_6
  nor nor_1 (CB_RAM0, nDB_CB, not_2_out);
  nor nor_2 (CB_RAM1, nDB_CB, not_4_out);
  nor nor_3 (CB_RAM2, nDB_CB, not_6_out);
  nor nor_4 (CB_RAM3, nDB_CB, not_8_out);
  nor nor_5 (CB_RAM4, nDB_CB, not_10_out);
  nor nor_6 (CB_RAM5, nDB_CB, not_12_out);

  // Notes on the sheet:
  //   14
  //   6
  //   14
  //   6
  //   14
  //   6
  //   14
  //   6
  //   14
  //   6
  //   14
  //   6
  //   4
  //   4
  //   4
  //   4
  //   7
  //   4
  //   7
  //   4
  //   3
  //   3
  //   3
  //   3
  //   8
  //   3
  //   8
  //   3
endmodule

module COLOR_CONTROL (
  input  [1:0] PCLK,
  input  DB_PAR,
  input  TH_MUX,
  input  nR7,
  input  nDBE,
  input  nPICTURE,
  input  BW,
  output nDB_CB,
  output nCB_DB,
  output COLOR_EN
);

  wire d_latch_1_q, nand_1_out, nor_1_out, not_1_out, not_3_out;

  D_latch d_latch_1 (.EN(PCLK[0]), .D(DB_PAR), .Q(d_latch_1_q));  // open: nQ
  not not_1 (not_1_out, TH_MUX);
  nor nor_1 (nor_1_out, not_1_out, nR7, nDBE);
  not not_2 (nCB_DB, nor_1_out);
  nand nand_1 (nand_1_out, nCB_DB, nPICTURE);
  not not_3 (not_3_out, BW);
  nand nand_2 (nDB_CB, d_latch_1_q, TH_MUX);
  and and_1 (COLOR_EN, nand_1_out, not_3_out);
endmodule

module CONTROL_REGS_NTSC (
  input  RC,
  input  nDBE,
  input  nW0,
  input  DB0,
  input  DB1,
  input  DB2,
  input  DB3,
  input  DB4,
  input  DB5,
  input  DB6,
  input  DB7,
  input  nW1,
  input  [1:0] PCLK,
  input  nVIS,
  input  CLIP_B,
  input  CLIP_O,
  output I1_32,
  output OBSEL,
  output BGSEL,
  output O8_16,
  output nSLAVE,
  output VBL,
  output BW,
  output BGCLIP,
  output OBCLIP,
  output BLACK,
  output CLPB,
  output nCLPO,
  output nTR,
  output nTG,
  output nTB
);

  wire d_ff_1_q, d_ff_2_q, d_ff_3_q, d_ff_4_q, d_ff_8_q, d_ff_9_q, d_ff_10_q, d_ff_11_q, d_ff_12_q,
       d_ff_13_q, d_ff_14_q, d_latch_7_nq, d_latch_7_q, d_latch_8_nq, d_latch_8_q, d_latch_11_q,
       d_latch_12_q, nor_1_out, nor_2_out, nor_5_out, not_1_out, not_2_out;

  nor nor_1 (nor_1_out, nDBE, nW0);
  nor nor_2 (nor_2_out, nDBE, nW1);
  not not_1 (not_1_out, nor_1_out);
  D_Flip_Flop #(.trigger("high")) d_ff_1 (.clk(nor_1_out), .D(DB2), .Q(d_ff_1_q), .reset(RC));  // open: Qn, preset, en
  D_Flip_Flop #(.trigger("high")) d_ff_2 (.clk(nor_1_out), .D(DB3), .Q(d_ff_2_q), .reset(RC));  // open: Qn, preset, en
  D_Flip_Flop #(.trigger("high")) d_ff_3 (.clk(nor_1_out), .D(DB4), .Q(d_ff_3_q), .reset(RC));  // open: Qn, preset, en
  D_Flip_Flop #(.trigger("high")) d_ff_4 (.clk(nor_1_out), .D(DB5), .Q(d_ff_4_q), .reset(RC));  // open: Qn, preset, en
  D_Flip_Flop #(.trigger("high")) d_ff_5 (.clk(nor_1_out), .D(DB6), .Q(nSLAVE), .reset(RC));  // open: Qn, preset, en
  D_Flip_Flop #(.trigger("high")) d_ff_6 (.clk(nor_1_out), .D(DB7), .Q(VBL), .reset(RC));  // open: Qn, preset, en
  not not_2 (not_2_out, nor_2_out);
  D_Flip_Flop #(.trigger("high")) d_ff_7 (.clk(nor_2_out), .D(DB0), .Q(BW), .reset(RC));  // open: Qn, preset, en
  D_Flip_Flop #(.trigger("high")) d_ff_8 (.clk(nor_2_out), .D(DB1), .Q(d_ff_8_q), .reset(RC));  // open: Qn, preset, en
  D_Flip_Flop #(.trigger("high")) d_ff_9 (.clk(nor_2_out), .D(DB2), .Q(d_ff_9_q), .reset(RC));  // open: Qn, preset, en
  D_Flip_Flop #(.trigger("high")) d_ff_10 (
    .clk(nor_2_out), .D(DB3), .Q(d_ff_10_q), .reset(RC));  // open: Qn, preset, en
  D_Flip_Flop #(.trigger("high")) d_ff_11 (
    .clk(nor_2_out), .D(DB4), .Q(d_ff_11_q), .reset(RC));  // open: Qn, preset, en
  D_Flip_Flop #(.trigger("high")) d_ff_12 (
    .clk(nor_2_out), .D(DB5), .Q(d_ff_12_q), .reset(RC));  // open: Qn, preset, en
  D_Flip_Flop #(.trigger("high")) d_ff_13 (
    .clk(nor_2_out), .D(DB6), .Q(d_ff_13_q), .reset(RC));  // open: Qn, preset, en
  D_Flip_Flop #(.trigger("high")) d_ff_14 (
    .clk(nor_2_out), .D(DB7), .Q(d_ff_14_q), .reset(RC));  // open: Qn, preset, en
  D_latch d_latch_1 (.EN(not_1_out), .D(d_ff_1_q), .Q(I1_32));  // open: nQ
  D_latch d_latch_2 (.EN(not_1_out), .D(d_ff_2_q), .nQ(OBSEL));  // open: Q
  D_latch d_latch_3 (.EN(not_1_out), .D(d_ff_3_q), .nQ(BGSEL));  // open: Q
  D_latch d_latch_4 (.EN(not_1_out), .D(d_ff_4_q), .Q(O8_16));  // open: nQ
  D_latch d_latch_5 (.EN(not_2_out), .D(d_ff_8_q), .Q(BGCLIP));  // open: nQ
  D_latch d_latch_6 (.EN(not_2_out), .D(d_ff_9_q), .Q(OBCLIP));  // open: nQ
  D_latch d_latch_7 (.EN(not_2_out), .D(d_ff_10_q), .Q(d_latch_7_q), .nQ(d_latch_7_nq));
  D_latch d_latch_8 (.EN(not_2_out), .D(d_ff_11_q), .Q(d_latch_8_q), .nQ(d_latch_8_nq));
  D_latch d_latch_9 (.EN(not_2_out), .D(d_ff_12_q), .nQ(nTR));  // open: Q
  D_latch d_latch_10 (.EN(not_2_out), .D(d_ff_13_q), .nQ(nTG));  // open: Q
  not not_3 (nTB, d_ff_14_q);
  D_latch d_latch_11 (.EN(PCLK[1]), .D(nVIS), .Q(d_latch_11_q));  // open: nQ
  D_latch d_latch_12 (.EN(PCLK[1]), .D(CLIP_B), .Q(d_latch_12_q));  // open: nQ
  nor nor_3 (BLACK, d_latch_7_q, d_latch_8_q);
  nor nor_4 (CLPB, d_latch_11_q, d_latch_7_nq, d_latch_12_q);
  nor nor_5 (nor_5_out, d_latch_11_q, d_latch_8_nq, CLIP_O);
  D_latch d_latch_13 (.EN(PCLK[1]), .D(nor_5_out), .nQ(nCLPO));  // open: Q

  // Notes on the sheet:
  //   /PCLK
  //   bits 0 and 1 are in the PPU address generator circuit
  //   BGE
  //   OBE
  //   $2000
  //   $2001
endmodule

module MUX (
  input  EXT3_IN,
  input  EXT2_IN,
  input  EXT1_IN,
  input  EXT0_IN,
  input  [1:0] PCLK,
  input  BGC0,
  input  BGC1,
  input  BGC2,
  input  BGC3,
  input  nZCOL0,
  input  nZCOL1,
  input  ZCOL2,
  input  ZCOL3,
  input  nZPRIO,
  input  THO0,
  input  THO1,
  input  THO2,
  input  THO3,
  input  THO4,
  input  TH_MUX,
  input  nSPR0HIT,
  input  I2SEV,
  input  nVIS,
  input  RESCL,
  input  nDBE,
  input  nR2,
  output EXT0_OUT,
  output EXT1_OUT,
  output EXT2_OUT,
  output EXT3_OUT,
  output PAL0,
  output PAL1,
  output PAL2,
  output PAL3,
  output PAL4,
  output DB6
);

  wire _1_out, _2_out, _5_2_out, _5_out, _6_out, d_latch_1_nq, d_latch_2_nq, d_latch_3_nq, d_latch_4_nq,
       d_latch_5_nq, d_latch_6_nq, d_latch_7_nq, d_latch_8_nq, d_latch_9_nq, d_latch_10_nq, d_latch_11_nq,
       d_latch_12_nq, d_latch_13_nq, d_latch_14_q, d_latch_15_q, d_latch_16_nq, d_latch_17_nq, d_latch_18_nq,
       d_latch_19_nq, d_latch_20_nq, d_latch_21_nq, d_latch_22_nq, d_latch_23_nq, d_latch_24_nq,
       multiplexer_1_out, multiplexer_2_out, multiplexer_3_out, multiplexer_4_out, multiplexer_5_out,
       multiplexer_6_out, multiplexer_7_out, multiplexer_8_out, multiplexer_9_out, multiplexer_10_out,
       multiplexer_11_out, multiplexer_12_out, multiplexer_13_out, nor_1_out, nor_2_out, nor_3_out,
       nor_4_out, not_5_out, not_6_out;

  D_latch d_latch_1 (.EN(1'b1), .D(ZCOL2), .nQ(d_latch_1_nq));  // open: Q
  D_latch d_latch_2 (.EN(1'b1), .D(ZCOL3), .nQ(d_latch_2_nq));  // open: Q
  D_latch d_latch_3 (.EN(1'b1), .D(nZPRIO), .nQ(d_latch_3_nq));  // open: Q
  nor nor_1 (nor_1_out, nDBE, nR2);
  D_latch d_latch_4 (.EN(PCLK[0]), .D(nZCOL0), .nQ(d_latch_4_nq));  // open: Q
  D_latch d_latch_5 (.EN(PCLK[0]), .D(nZCOL1), .nQ(d_latch_5_nq));  // open: Q
  D_latch d_latch_6 (.EN(PCLK[0]), .D(d_latch_1_nq), .nQ(d_latch_6_nq));  // open: Q
  D_latch d_latch_7 (.EN(PCLK[0]), .D(d_latch_2_nq), .nQ(d_latch_7_nq));  // open: Q
  D_latch d_latch_8 (.EN(PCLK[0]), .D(d_latch_3_nq), .nQ(d_latch_8_nq));  // open: Q
  nor _2 (_2_out, BGC1, BGC0);
  Multiplexer #(.enable("false")) multiplexer_1 (
    .in0(BGC0), .in1(d_latch_4_nq), .out(multiplexer_1_out), .sel(_5_2_out));
  not not_1 (EXT0_OUT, multiplexer_1_out);
  Multiplexer #(.enable("false")) multiplexer_2 (
    .in0(BGC1), .in1(d_latch_5_nq), .out(multiplexer_2_out), .sel(_5_2_out));
  not not_2 (EXT1_OUT, multiplexer_2_out);
  Multiplexer #(.enable("false")) multiplexer_3 (
    .in0(BGC2), .in1(d_latch_6_nq), .out(multiplexer_3_out), .sel(_5_2_out));
  not not_3 (EXT2_OUT, multiplexer_3_out);
  Multiplexer #(.enable("false")) multiplexer_4 (
    .in0(BGC3), .in1(d_latch_7_nq), .out(multiplexer_4_out), .sel(_5_2_out));
  not not_4 (EXT3_OUT, multiplexer_4_out);
  not not_5 (not_5_out, _2_out);
  nor _1 (_1_out, d_latch_4_nq, d_latch_5_nq);
  nor nor_2 (nor_2_out, _2_out, PCLK[0], nSPR0HIT, I2SEV, nVIS);
  and _5 (_5_out, not_5_out, d_latch_8_nq);
  nor nor_3 (nor_3_out, nor_2_out, nor_4_out);
  nor nor_4 (nor_4_out, nor_3_out, RESCL);
  nor _5_2 (_5_2_out, _5_out, _1_out);
  not not_6 (not_6_out, _1_out);
  D_latch d_latch_9 (.EN(PCLK[1]), .D(EXT0_OUT), .nQ(d_latch_9_nq));  // open: Q
  D_latch d_latch_10 (.EN(PCLK[1]), .D(EXT1_OUT), .nQ(d_latch_10_nq));  // open: Q
  D_latch d_latch_11 (.EN(PCLK[1]), .D(EXT2_OUT), .nQ(d_latch_11_nq));  // open: Q
  D_latch d_latch_12 (.EN(PCLK[1]), .D(EXT3_OUT), .nQ(d_latch_12_nq));  // open: Q
  D_latch d_latch_13 (.EN(PCLK[1]), .D(_5_2_out), .nQ(d_latch_13_nq));  // open: Q
  D_latch d_latch_14 (.EN(PCLK[1]), .D(not_5_out), .Q(d_latch_14_q));  // open: nQ
  D_latch d_latch_15 (.EN(PCLK[1]), .D(not_6_out), .Q(d_latch_15_q));  // open: nQ
  nor _6 (_6_out, d_latch_14_q, d_latch_15_q);
  Multiplexer #(.enable("false")) multiplexer_5 (
    .in0(d_latch_9_nq), .in1(EXT0_IN), .out(multiplexer_5_out), .sel(_6_out));
  Multiplexer #(.enable("false")) multiplexer_6 (
    .in0(d_latch_10_nq), .in1(EXT1_IN), .out(multiplexer_6_out), .sel(_6_out));
  Multiplexer #(.enable("false")) multiplexer_7 (
    .in0(d_latch_11_nq), .in1(EXT2_IN), .out(multiplexer_7_out), .sel(_6_out));
  Multiplexer #(.enable("false")) multiplexer_8 (
    .in0(d_latch_12_nq), .in1(EXT3_IN), .out(multiplexer_8_out), .sel(_6_out));
  D_latch d_latch_16 (.EN(PCLK[0]), .D(multiplexer_5_out), .nQ(d_latch_16_nq));  // open: Q
  D_latch d_latch_17 (.EN(PCLK[0]), .D(multiplexer_6_out), .nQ(d_latch_17_nq));  // open: Q
  D_latch d_latch_18 (.EN(PCLK[0]), .D(multiplexer_7_out), .nQ(d_latch_18_nq));  // open: Q
  D_latch d_latch_19 (.EN(PCLK[0]), .D(multiplexer_8_out), .nQ(d_latch_19_nq));  // open: Q
  D_latch d_latch_20 (.EN(PCLK[0]), .D(THO0), .nQ(d_latch_20_nq));  // open: Q
  D_latch d_latch_21 (.EN(PCLK[0]), .D(THO1), .nQ(d_latch_21_nq));  // open: Q
  D_latch d_latch_22 (.EN(PCLK[0]), .D(THO2), .nQ(d_latch_22_nq));  // open: Q
  D_latch d_latch_23 (.EN(PCLK[0]), .D(THO3), .nQ(d_latch_23_nq));  // open: Q
  D_latch d_latch_24 (.EN(PCLK[0]), .D(THO4), .nQ(d_latch_24_nq));  // open: Q
  not not_7 (PAL0, multiplexer_9_out);
  Multiplexer #(.enable("false")) multiplexer_9 (
    .in0(d_latch_16_nq), .in1(d_latch_20_nq), .out(multiplexer_9_out), .sel(TH_MUX));
  Multiplexer #(.enable("false")) multiplexer_10 (
    .in0(d_latch_17_nq), .in1(d_latch_21_nq), .out(multiplexer_10_out), .sel(TH_MUX));
  not not_8 (PAL1, multiplexer_10_out);
  Multiplexer #(.enable("false")) multiplexer_11 (
    .in0(d_latch_18_nq), .in1(d_latch_22_nq), .out(multiplexer_11_out), .sel(TH_MUX));
  not not_9 (PAL2, multiplexer_11_out);
  not not_10 (PAL3, multiplexer_12_out);
  Multiplexer #(.enable("false")) multiplexer_12 (
    .in0(d_latch_19_nq), .in1(d_latch_23_nq), .out(multiplexer_12_out), .sel(TH_MUX));
  Multiplexer #(.enable("false")) multiplexer_13 (
    .in0(d_latch_13_nq), .in1(d_latch_24_nq), .out(multiplexer_13_out), .sel(TH_MUX));
  Multiplexer multiplexer_14 (.in0(1'b0), .in1(1'b1), .out(DB6), .sel(nor_4_out), .en(nor_1_out));
  D_latch d_latch_25 (.EN(PCLK[0]), .D(multiplexer_13_out), .nQ(PAL4));  // open: Q

  // Notes on the sheet:
  //   TH contain directly loaded color
  //   R2'
  //   Sprite/background
  //   4
  //   MUX - select one of 4 sources for final color output
  //   /PCLK
  //   OCOL
  //   3
  //   3
  //   2
  //   STRIKE TEST
  //   External/Prev
  //   EXT
  //   Direct/Prev
  //   TRI-STATE
  //   PCLK
endmodule
// OAM EVAL
module OAM_EVAL (
  input  [1:0] PCLK,
  input  nF_NT,
  input  H0_prime_prime,
  input  I_OAM2,
  input  nVIS,
  input  SPR_OV,
  input  S_EV,
  input  PAR_O,
  input  O8_16,
  input  V0,
  input  V1,
  input  V2,
  input  V3,
  input  V4,
  input  V5,
  input  V6,
  input  V7,
  input  OB0,
  input  OB1,
  input  OB2,
  input  OB3,
  input  OB4,
  input  OB5,
  input  OB6,
  input  OB7,
  output _0_FIFO,
  output TEST,
  output OMFG,
  output I2SEV,
  output OV0,
  output OV1,
  output OV2,
  output OV3
);

  wire _2_out, _3_out, _14_out, _18_out, _19_out, _20_out, _24_out, _29_out, d_ff_1_q, d_ff_1_qn, d_ff_2_qn,
       d_ff_3_qn, d_latch_1_nq, d_latch_2_nq, d_latch_3_nq, d_latch_4_nq, d_latch_5_nq, d_latch_6_q,
       d_latch_7_nq, d_latch_8_nq, d_latch_9_nq, nor_1_out, not_1_out, not_2_out, not_3_out, not_4_out,
       not_5_out, not_6_out, not_7_out, not_8_out, nOVZ, oam_substractor_1_ov4, oam_substractor_1_ov5,
       oam_substractor_1_ov6, oam_substractor_1_ov7;

  not not_1 (not_1_out, H0_prime_prime);
  not not_2 (not_2_out, O8_16);
  nor _29 (_29_out, I_OAM2, nVIS, SPR_OV, nOVZ);
  not not_3 (not_3_out, S_EV);
  not not_4 (not_4_out, PAR_O);
  nor _19 (_19_out, PCLK[0], not_1_out);
  nor _20 (_20_out, nF_NT, not_1_out);
  D_latch d_latch_1 (.EN(_19_out), .D(_29_out), .nQ(d_latch_1_nq));  // open: Q
  nor _24 (_24_out, not_3_out, PCLK[0]);
  nor _2 (_2_out, PCLK[0], not_4_out);
  D_latch d_latch_2 (.EN(PCLK[0]), .D(OB7), .nQ(d_latch_2_nq));  // open: Q
  not not_5 (not_5_out, PCLK[0]);
  not not_6 (not_6_out, _20_out);
  D_latch d_latch_3 (.EN(PCLK[0]), .D(d_latch_1_nq), .nQ(d_latch_3_nq));  // open: Q
  D_latch d_latch_4 (.EN(_19_out), .D(d_latch_3_nq), .nQ(d_latch_4_nq));  // open: Q
  OAM_SUBSTRACTOR oam_substractor_1 (
    .PCLK(PCLK[0]), .OB0(OB0), .OB1(OB1), .OB2(OB2), .OB3(OB3), .OB4(OB4), .OB5(OB5), .OB6(OB6), .OB7(OB7),
    .V0(V0), .V1(V1), .V2(V2), .V3(V3), .V4(V4), .V5(V5), .V6(V6), .V7(V7), .OV0(OV0), .OV1(OV1), .OV2(OV2),
    .OV3(OV3), .OV4(oam_substractor_1_ov4), .OV5(oam_substractor_1_ov5), .OV6(oam_substractor_1_ov6),
    .OV7(oam_substractor_1_ov7));
  nor _14 (_14_out, V7, d_latch_2_nq);
  not not_7 (not_7_out, not_5_out);
  D_latch d_latch_5 (.EN(not_5_out), .D(nOVZ), .nQ(d_latch_5_nq));  // open: Q
  D_latch d_latch_6 (.EN(PCLK[1]), .D(not_6_out), .Q(d_latch_6_q));  // open: nQ
  D_latch d_latch_7 (.EN(PCLK[0]), .D(d_latch_4_nq), .nQ(d_latch_7_nq));  // open: Q
  D_Flip_Flop #(.trigger("high")) d_ff_1 (
    .clk(PCLK[1]), .D(_29_out), .Q(d_ff_1_q), .Qn(d_ff_1_qn), .en(_24_out));  // open: preset, reset
  nor _18 (_18_out, PCLK[1], d_latch_6_q);
  D_latch d_latch_8 (.EN(_19_out), .D(d_latch_7_nq), .nQ(d_latch_8_nq));  // open: Q
  and _3 (_3_out, not_2_out, OV3);
  D_Flip_Flop #(.trigger("high")) d_ff_2 (
    .clk(not_7_out), .D(d_latch_5_nq), .Q(_0_FIFO), .Qn(d_ff_2_qn), .en(_18_out));  // open: preset, reset
  D_latch d_latch_9 (.EN(PCLK[0]), .D(d_latch_8_nq), .nQ(d_latch_9_nq));  // open: Q
  D_Flip_Flop #(.trigger("high")) d_ff_3 (
    .clk(PCLK[1]), .D(d_ff_1_qn), .Q(I2SEV), .Qn(d_ff_3_qn), .en(_2_out));  // open: preset, reset
  nor _10 (TEST, d_latch_9_nq, d_latch_7_nq, d_latch_3_nq);
  not not_8 (not_8_out, TEST);
  nor nor_1 (nor_1_out, not_8_out, _3_out, oam_substractor_1_ov4, oam_substractor_1_ov5, oam_substractor_1_ov6, oam_substractor_1_ov7, _14_out);
  not not_9 (nOVZ, nor_1_out);
  nor _12 (OMFG, not_8_out, _29_out);

  // Other names for the same wires on the sheet: PCLK_t = PCLK[0]; nPCLK = PCLK[1]

  // Notes on the sheet:
  //   22
  //   3
  //   copy condition
  //   23
  //   1
  //   /PCLKH
  //   1
  //   COPY_SPRITE
  //   PCLK
  //   2
  //   7
  //   /PCLK2
  //   21
  //   3
  //   8
  //   9
  //   4
  //   FF2
  //   5
  //   SPRITE 0 NOT FOUND ON CURRENT SCANLINE
  //   IN  RANGE
  //   PCLK2
  //   FF3
  //   6
  //   FF1
  //   0/FIFO CIRCUIT
  //   COPY ENABLE COUNTER
  //   OVZ
  //   11
  //   29
  //   SPTITE EVAL COPY SPRITE
endmodule

// OAM SUBSTRACTOR
module OAM_SUBSTRACTOR (
  input  PCLK,
  input  OB0,
  input  OB1,
  input  OB2,
  input  OB3,
  input  OB4,
  input  OB5,
  input  OB6,
  input  OB7,
  input  V0,
  input  V1,
  input  V2,
  input  V3,
  input  V4,
  input  V5,
  input  V6,
  input  V7,
  output OV0,
  output OV1,
  output OV2,
  output OV3,
  output OV4,
  output OV5,
  output OV6,
  output OV7
);

  wire and_1_out, and_2_out, and_3_out, and_4_out, d_latch_1_nq, d_latch_2_nq, d_latch_3_nq, d_latch_4_nq,
       d_latch_5_nq, d_latch_6_nq, d_latch_7_nq, d_latch_8_nq, nand_1_out, nand_2_out, nand_3_out,
       nand_4_out, nor_1_out, nor_2_out, nor_3_out, nor_4_out, nor_5_out, nor_6_out, nor_7_out, nor_8_out,
       nor_9_out, nor_10_out, nor_11_out, nor_12_out, nor_13_out, nor_14_out, nor_15_out, nor_16_out,
       nor_17_out, nor_18_out, nor_19_out, nor_20_out, nor_21_out, nor_22_out, nor_23_out, nor_24_out,
       nor_25_out, nor_26_out, nor_27_out, nor_28_out, nor_29_out, nor_30_out, nor_31_out, nor_32_out,
       nor_33_out, nor_34_out, nor_35_out, nor_36_out, not_1_out, not_2_out, not_3_out, not_4_out;

  D_latch d_latch_1 (.EN(PCLK), .D(OB0), .nQ(d_latch_1_nq));  // open: Q
  D_latch d_latch_2 (.EN(PCLK), .D(OB1), .nQ(d_latch_2_nq));  // open: Q
  D_latch d_latch_3 (.EN(PCLK), .D(OB2), .nQ(d_latch_3_nq));  // open: Q
  D_latch d_latch_4 (.EN(PCLK), .D(OB3), .nQ(d_latch_4_nq));  // open: Q
  D_latch d_latch_5 (.EN(PCLK), .D(OB4), .nQ(d_latch_5_nq));  // open: Q
  D_latch d_latch_6 (.EN(PCLK), .D(OB5), .nQ(d_latch_6_nq));  // open: Q
  D_latch d_latch_7 (.EN(PCLK), .D(OB6), .nQ(d_latch_7_nq));  // open: Q
  D_latch d_latch_8 (.EN(PCLK), .D(OB7), .nQ(d_latch_8_nq));  // open: Q
  nor nor_1 (nor_1_out, d_latch_1_nq, V0);
  nand nand_1 (nand_1_out, V0, d_latch_1_nq);
  nor nor_2 (nor_2_out, d_latch_2_nq, V1);
  and and_1 (and_1_out, V1, d_latch_2_nq);
  nor nor_3 (nor_3_out, d_latch_3_nq, V2);
  nand nand_2 (nand_2_out, V2, d_latch_3_nq);
  nor nor_4 (nor_4_out, d_latch_4_nq, V3);
  and and_2 (and_2_out, V3, d_latch_4_nq);
  nor nor_5 (nor_5_out, d_latch_5_nq, V4);
  nand nand_3 (nand_3_out, V4, d_latch_5_nq);
  nor nor_6 (nor_6_out, d_latch_6_nq, V5);
  and and_3 (and_3_out, V5, d_latch_6_nq);
  nor nor_7 (nor_7_out, d_latch_7_nq, V6);
  nand nand_4 (nand_4_out, V6, d_latch_7_nq);
  nor nor_8 (nor_8_out, d_latch_8_nq, V7);
  and and_4 (and_4_out, V7, d_latch_8_nq);
  not not_1 (not_1_out, nand_1_out);
  not not_2 (not_2_out, nand_2_out);
  not not_3 (not_3_out, nand_3_out);
  not not_4 (not_4_out, nand_4_out);
  nor nor_9 (nor_9_out, nor_1_out, not_1_out);
  nor nor_10 (nor_10_out, 1'b0, nor_1_out);
  nor nor_11 (nor_11_out, nor_2_out, and_1_out);
  nor nor_12 (nor_12_out, nor_2_out, nand_1_out);
  nor nor_13 (nor_13_out, nor_2_out, 1'b0, nor_1_out);
  nor nor_14 (nor_14_out, nor_3_out, not_2_out);
  nor nor_15 (nor_15_out, nor_30_out, nor_3_out);
  nor nor_16 (nor_16_out, nor_4_out, and_2_out);
  nor nor_17 (nor_17_out, nor_4_out, nand_2_out);
  nor nor_18 (nor_18_out, nor_4_out, nor_30_out, nor_3_out);
  nor nor_19 (nor_19_out, nor_5_out, not_3_out);
  nor nor_20 (nor_20_out, nor_32_out, nor_5_out);
  nor nor_21 (nor_21_out, nor_6_out, and_3_out);
  nor nor_22 (nor_22_out, nor_6_out, nand_3_out);
  nor nor_23 (nor_23_out, nor_6_out, nor_32_out, nor_5_out);
  nor nor_24 (nor_24_out, nor_7_out, not_4_out);
  nor nor_25 (nor_25_out, nor_34_out, nor_7_out);
  nor nor_26 (nor_26_out, nor_8_out, and_4_out);
  nor nor_27 (nor_27_out, nor_8_out, nand_4_out);
  nor nor_28 (nor_28_out, nor_8_out, nor_34_out, nor_7_out);
  xnor xnor_1 (OV0, 1'b0, nor_9_out);
  nor nor_29 (nor_29_out, nor_10_out, not_1_out);
  xnor xnor_2 (OV1, nor_29_out, nor_11_out);
  nor nor_30 (nor_30_out, and_1_out, nor_12_out, nor_13_out);
  xnor xnor_3 (OV2, nor_30_out, nor_14_out);
  nor nor_31 (nor_31_out, nor_15_out, not_2_out);
  xnor xnor_4 (OV3, nor_31_out, nor_16_out);
  nor nor_32 (nor_32_out, and_2_out, nor_17_out, nor_18_out);
  xnor xnor_5 (OV4, nor_32_out, nor_19_out);
  nor nor_33 (nor_33_out, nor_20_out, not_3_out);
  xnor xnor_6 (OV5, nor_33_out, nor_21_out);
  nor nor_34 (nor_34_out, and_3_out, nor_22_out, nor_23_out);
  xnor xnor_7 (OV6, nor_34_out, nor_24_out);
  nor nor_35 (nor_35_out, nor_25_out, not_4_out);
  xnor xnor_8 (OV7, nor_35_out, nor_26_out);
  nor nor_36 (nor_36_out, and_4_out, nor_27_out, nor_28_out);

  // Notes on the sheet:
  //   S=V-OB
  //   8-BIT SIGNED SUBTRACT
  //   not used
endmodule

// OAM CONTROL
module OAM_CONTROL_NTSC (
  input  [1:0] PCLK,
  input  OFETCH,
  input  I_OAM2,
  input  H0_prime_prime,
  input  nVIS,
  input  BLNK,
  input  OMFG,
  input  nDBE,
  input  nW3,
  input  PAR_O,
  input  DB0,
  input  DB1,
  input  DB2,
  input  DB3,
  input  DB4,
  input  DB5,
  input  DB6,
  input  DB7,
  input  EVAL,
  input  nH2_prime,
  input  H0_prime,
  input  RESCL,
  input  nR2,
  output nOAM0,
  output nOAM1,
  output nOAM2,
  output nOAM3,
  output nOAM4,
  output nOAM5,
  output nOAM6,
  output nOAM7,
  output OAM8,
  output SPR_OV,
  output OAMCTR2,
  output DB5_2
);

  wire _14_out, _27_out, and_1_out, d_latch_1_nq, d_latch_2_q, d_latch_3_q, d_latch_4_q, d_latch_5_q,
       d_latch_6_q, d_latch_7_q, d_latch_8_q, d_latch_9_q, d_latch_10_q, multiplexer_1_out,
       multiplexer_2_out, multiplexer_3_out, multiplexer_4_out, multiplexer_5_out, nand_1_out, nand_2_out,
       nand_3_out, nand_4_out, nor_1_out, nor_2_out, nor_3_out, nor_4_out, nor_5_out, nor_6_out, nor_7_out,
       nor_8_out, nor_9_out, nor_10_out, nor_11_out, nor_12_out, nor_13_out, nor_15_out, nor_16_out,
       not_1_out, not_2_out, not_3_out, not_4_out, not_5_out, not_7_out, oam2_counter_1_carry_out,
       oam2_counter_1_q0, oam2_counter_1_q1, oam2_counter_1_q2, oam2_counter_1_q3, oam2_counter_1_q4,
       oam_counter_1_cout, oam_counter_1_out0, oam_counter_1_out1, oam_counter_1_out2, oam_counter_1_out3,
       oam_counter_1_out4, oam_counter_1_out5, oam_counter_1_out6, oam_counter_1_out7, or_1_out, or_2_out;

  nor nor_1 (nor_1_out, I_OAM2, nVIS);
  or or_1 (or_1_out, H0_prime_prime, nVIS);
  not not_1 (not_1_out, BLNK);
  not not_2 (not_2_out, OMFG);
  nor nor_2 (nor_2_out, nDBE, nW3);
  nand nand_1 (nand_1_out, EVAL, nor_16_out);
  and and_1 (and_1_out, PAR_O, nH2_prime);
  not not_3 (not_3_out, OMFG);
  not not_4 (not_4_out, nor_3_out);
  nor nor_3 (nor_3_out, nR2, nDBE);
  D_latch d_latch_1 (.EN(PCLK[1]), .D(OFETCH), .nQ(d_latch_1_nq));  // open: Q
  nand nand_2 (nand_2_out, nor_1_out, H0_prime_prime);
  nand nand_3 (nand_3_out, or_1_out, not_1_out);
  nor nor_4 (nor_4_out, BLNK, not_2_out);
  D_latch d_latch_2 (.EN(PCLK[1]), .D(EVAL), .Q(d_latch_2_q));  // open: nQ
  D_latch d_latch_3 (.EN(PCLK[1]), .D(nand_1_out), .Q(d_latch_3_q));  // open: nQ
  nor nor_5 (nor_5_out, and_1_out, nor_10_out);
  D_latch d_latch_4 (.EN(PCLK[1]), .D(not_3_out), .Q(d_latch_4_q));  // open: nQ
  D_latch d_latch_5 (.EN(PCLK[1]), .D(I_OAM2), .Q(d_latch_5_q));  // open: nQ
  nor nor_6 (nor_6_out, PCLK[1], d_latch_1_nq);
  D_latch d_latch_6 (.EN(PCLK[1]), .D(nand_2_out), .Q(d_latch_6_q));  // open: nQ
  nor nor_7 (nor_7_out, PCLK[1], d_latch_2_q);
  nor nor_8 (nor_8_out, PCLK[1], d_latch_3_q, nor_5_out);
  nor nor_9 (nor_9_out, d_latch_4_q, d_latch_5_q);
  not not_5 (not_5_out, nor_6_out);
  or or_2 (or_2_out, PCLK[1], d_latch_6_q);
  not not_6 (OAM8, nand_3_out);
  nor nor_10 (nor_10_out, nor_9_out, H0_prime);
  nand nand_4 (nand_4_out, not_5_out, or_2_out);
  D_latch d_latch_7 (.EN(PCLK[1]), .D(nor_16_out), .Q(d_latch_7_q));  // open: nQ
  D_latch d_latch_8 (.EN(PCLK[1]), .D(OMFG), .Q(d_latch_8_q));  // open: nQ
  OAM_COUNTER oam_counter_1 (
    .MODE4(nor_4_out), .STEP(nand_4_out), .LOAD(nor_2_out), .D0(DB0), .RES(PAR_O), .D1(DB1), .D2(DB2),
    .D3(DB3), .D4(DB4), .D5(DB5), .D6(DB6), .D7(DB7), .out0(oam_counter_1_out0), .out1(oam_counter_1_out1),
    .out2(oam_counter_1_out2), .out3(oam_counter_1_out3), .out4(oam_counter_1_out4),
    .out5(oam_counter_1_out5), .out6(oam_counter_1_out6), .COUT(oam_counter_1_cout), .out7(oam_counter_1_out7));
  OAM2_COUNTER oam2_counter_1 (
    .STEP(nor_8_out), .nPCLK(PCLK[1]), .RES(nor_7_out), .Q0(oam2_counter_1_q0), .Q1(oam2_counter_1_q1),
    .Q2(oam2_counter_1_q2), .Q3(oam2_counter_1_q3), .Q4(oam2_counter_1_q4),
    .CARRY_OUT(oam2_counter_1_carry_out));
  nor nor_11 (nor_11_out, PCLK[1], d_latch_7_q, d_latch_8_q, H0_prime);
  nor nor_12 (nor_12_out, nor_11_out, nor_13_out);
  nor nor_13 (nor_13_out, nor_12_out, RESCL);
  not not_7 (not_7_out, not_4_out);
  D_latch d_latch_9 (.EN(PCLK[1]), .D(oam_counter_1_cout), .Q(d_latch_9_q));  // open: nQ
  D_latch d_latch_10 (.EN(PCLK[1]), .D(oam2_counter_1_carry_out), .Q(d_latch_10_q));  // open: nQ
  Multiplexer #(.enable("false")) multiplexer_1 (
    .in0(oam_counter_1_out3), .in1(oam2_counter_1_q0), .out(multiplexer_1_out), .sel(OAM8));
  Multiplexer #(.enable("false")) multiplexer_2 (
    .in0(oam_counter_1_out4), .in1(oam2_counter_1_q1), .out(multiplexer_2_out), .sel(OAM8));
  Multiplexer #(.enable("false")) multiplexer_3 (
    .in0(oam_counter_1_out5), .in1(oam2_counter_1_q2), .out(multiplexer_3_out), .sel(OAM8));
  Multiplexer #(.enable("false")) multiplexer_4 (
    .in0(oam_counter_1_out6), .in1(oam2_counter_1_q3), .out(multiplexer_4_out), .sel(OAM8));
  Multiplexer #(.enable("false")) multiplexer_5 (
    .in0(oam_counter_1_out7), .in1(oam2_counter_1_q4), .out(multiplexer_5_out), .sel(OAM8));
  and _27 (_27_out, nand_4_out, d_latch_9_q);
  and _14 (_14_out, d_latch_10_q, nor_8_out);
  Multiplexer multiplexer_6 (.in0(1'b0), .in1(1'b1), .out(DB5_2), .sel(nor_13_out), .en(not_7_out));
  not not_8 (nOAM0, oam_counter_1_out0);
  not not_9 (nOAM1, oam_counter_1_out1);
  not not_10 (nOAM2, oam_counter_1_out2);
  not not_11 (nOAM3, multiplexer_1_out);
  not not_12 (nOAM4, multiplexer_2_out);
  not not_13 (nOAM5, multiplexer_3_out);
  not not_14 (nOAM6, multiplexer_4_out);
  not not_15 (nOAM7, multiplexer_5_out);
  nor nor_14 (SPR_OV, I_OAM2, nor_15_out);
  nor nor_15 (nor_15_out, SPR_OV, _27_out, nor_11_out);
  nor nor_16 (nor_16_out, _14_out, OAMCTR2);
  nor nor_17 (OAMCTR2, nor_16_out, nor_7_out);

  // Other names for the same wires on the sheet: nPCLK = PCLK[1]

  // Notes on the sheet:
  //   1
  //   6
  //   8
  //   10
  //   20
  //   17
  //   W3'
  //   4
  //   3
  //   4
  //   9
  //   1
  //   2
  //   OAM CNT2 STEP CONTROL
  //   10
  //   21
  //   4
  //   /R2'
  //   24
  //   8
  //   OAP
  //   7
  //   5
  //   2
  //   3
  //   23
  //   ORES
  //   OSTEP
  //   OMSTEP
  //   OAM CNT1 STEP CONTROL
  //   5
  //   6
  //   SPRITE OVERFLOW FLAG
  //   OMV
  //   OMV
  //   TMV
  //   13
  //   9
  //   7
  //   Sprite overflow flag
  //   3
  //   OMV'
  //   TMV'
  //   TRI-STATE
  //   1
  //   2
  //   more than 8 sprites
  //   sprites less than 8 pieces
  //   CNT_OAM2_OVERFLOW
endmodule

// OAM COUNTER
module OAM_COUNTER (
  input  MODE4,
  input  LOAD,
  input  STEP,
  input  RES,
  input  D0,
  input  D1,
  input  D2,
  input  D3,
  input  D4,
  input  D5,
  input  D6,
  input  D7,
  output out0,
  output out1,
  output out2,
  output out3,
  output out4,
  output out5,
  output out6,
  output out7,
  output COUT
);

  wire _5_out, _7_2_out, _7_out, _8_out, _9_out, _10_out, _11_out, d_ff_1_qn, d_ff_2_qn, d_ff_3_qn,
       d_ff_4_qn, d_ff_5_qn, d_ff_6_qn, d_ff_7_qn, d_ff_8_qn, d_latch_1_q, d_latch_2_q, d_latch_3_nq,
       d_latch_4_nq, d_latch_5_nq, d_latch_6_nq, d_latch_7_nq, d_latch_8_nq, demultiplexer_1_out0,
       demultiplexer_1_out1, demultiplexer_2_out0, demultiplexer_2_out1, demultiplexer_3_out0,
       demultiplexer_3_out1, demultiplexer_4_out0, demultiplexer_4_out1, demultiplexer_5_out0,
       demultiplexer_5_out1, demultiplexer_6_out0, demultiplexer_6_out1, demultiplexer_7_out0,
       demultiplexer_7_out1, demultiplexer_8_out0, demultiplexer_8_out1, nor_1_out, nor_2_out, nor_3_out,
       nor_4_out, not_1_out, not_2_out, not_3_out, or_1_out, or_2_out, or_3_out, or_4_out, or_5_out,
       or_6_out, or_7_out, or_8_out, or_9_out, xor_1_out, xor_2_out, xor_3_out, xor_4_out, xor_5_out,
       xor_6_out, xor_7_out, xor_8_out;

  Demultiplexer #(.enable("false")) demultiplexer_1 (
    .out0(demultiplexer_1_out0), .out1(demultiplexer_1_out1), .in(LOAD), .sel(D0));
  Demultiplexer #(.enable("false")) demultiplexer_2 (
    .out0(demultiplexer_2_out0), .out1(demultiplexer_2_out1), .in(LOAD), .sel(D1));
  Demultiplexer #(.enable("false")) demultiplexer_3 (
    .out0(demultiplexer_3_out0), .out1(demultiplexer_3_out1), .in(LOAD), .sel(D2));
  Demultiplexer #(.enable("false")) demultiplexer_4 (
    .out0(demultiplexer_4_out0), .out1(demultiplexer_4_out1), .in(LOAD), .sel(D3));
  Demultiplexer #(.enable("false")) demultiplexer_5 (
    .out0(demultiplexer_5_out0), .out1(demultiplexer_5_out1), .in(LOAD), .sel(D4));
  Demultiplexer #(.enable("false")) demultiplexer_6 (
    .out0(demultiplexer_6_out0), .out1(demultiplexer_6_out1), .in(LOAD), .sel(D5));
  Demultiplexer #(.enable("false")) demultiplexer_7 (
    .out0(demultiplexer_7_out0), .out1(demultiplexer_7_out1), .in(LOAD), .sel(D6));
  Demultiplexer #(.enable("false")) demultiplexer_8 (
    .out0(demultiplexer_8_out0), .out1(demultiplexer_8_out1), .in(LOAD), .sel(D7));
  or or_1 (or_1_out, RES, demultiplexer_1_out0);
  or or_2 (or_2_out, RES, demultiplexer_2_out0);
  or or_3 (or_3_out, RES, demultiplexer_3_out0);
  or or_4 (or_4_out, RES, demultiplexer_4_out0);
  or or_5 (or_5_out, RES, demultiplexer_5_out0);
  or or_6 (or_6_out, RES, demultiplexer_6_out0);
  or or_7 (or_7_out, RES, demultiplexer_7_out0);
  or or_8 (or_8_out, RES, demultiplexer_8_out0);
  nor nor_1 (nor_1_out, LOAD, STEP);
  D_Flip_Flop d_ff_1 (
    .clk(STEP), .D(nor_2_out), .Q(out0), .Qn(d_ff_1_qn), .preset(demultiplexer_1_out1), .reset(or_1_out));  // open: en
  D_Flip_Flop d_ff_2 (
    .clk(STEP), .D(nor_3_out), .Q(out1), .Qn(d_ff_2_qn), .preset(demultiplexer_2_out1), .reset(or_2_out));  // open: en
  D_Flip_Flop d_ff_3 (
    .clk(STEP), .D(d_latch_3_nq), .Q(out2), .Qn(d_ff_3_qn), .preset(demultiplexer_3_out1), .reset(or_3_out));  // open: en
  D_Flip_Flop d_ff_4 (
    .clk(STEP), .D(d_latch_4_nq), .Q(out3), .Qn(d_ff_4_qn), .preset(demultiplexer_4_out1), .reset(or_4_out));  // open: en
  D_Flip_Flop d_ff_5 (
    .clk(STEP), .D(d_latch_5_nq), .Q(out4), .Qn(d_ff_5_qn), .preset(demultiplexer_5_out1), .reset(or_5_out));  // open: en
  D_Flip_Flop d_ff_6 (
    .clk(STEP), .D(d_latch_6_nq), .Q(out5), .Qn(d_ff_6_qn), .preset(demultiplexer_6_out1), .reset(or_6_out));  // open: en
  D_Flip_Flop d_ff_7 (
    .clk(STEP), .D(d_latch_7_nq), .Q(out6), .Qn(d_ff_7_qn), .preset(demultiplexer_7_out1), .reset(or_7_out));  // open: en
  D_Flip_Flop d_ff_8 (
    .clk(STEP), .D(d_latch_8_nq), .Q(out7), .Qn(d_ff_8_qn), .preset(demultiplexer_8_out1), .reset(or_8_out));  // open: en
  xor xor_1 (xor_1_out, 1'b1, d_ff_1_qn);
  xor xor_2 (xor_2_out, nor_4_out, d_ff_2_qn);
  xor xor_3 (xor_3_out, _5_out, d_ff_3_qn);
  xor xor_4 (xor_4_out, _7_2_out, d_ff_4_qn);
  xor xor_5 (xor_5_out, _8_out, d_ff_5_qn);
  xor xor_6 (xor_6_out, _9_out, d_ff_6_qn);
  xor xor_7 (xor_7_out, _10_out, d_ff_7_qn);
  xor xor_8 (xor_8_out, _11_out, d_ff_8_qn);
  D_latch d_latch_1 (.EN(nor_1_out), .D(xor_1_out), .Q(d_latch_1_q));  // open: nQ
  nor nor_2 (nor_2_out, d_latch_1_q, MODE4);
  D_latch d_latch_2 (.EN(nor_1_out), .D(xor_2_out), .Q(d_latch_2_q));  // open: nQ
  nor nor_3 (nor_3_out, d_latch_2_q, MODE4);
  D_latch d_latch_3 (.EN(nor_1_out), .D(xor_3_out), .nQ(d_latch_3_nq));  // open: Q
  D_latch d_latch_4 (.EN(nor_1_out), .D(xor_4_out), .nQ(d_latch_4_nq));  // open: Q
  D_latch d_latch_5 (.EN(nor_1_out), .D(xor_5_out), .nQ(d_latch_5_nq));  // open: Q
  D_latch d_latch_6 (.EN(nor_1_out), .D(xor_6_out), .nQ(d_latch_6_nq));  // open: Q
  D_latch d_latch_7 (.EN(nor_1_out), .D(xor_7_out), .nQ(d_latch_7_nq));  // open: Q
  D_latch d_latch_8 (.EN(nor_1_out), .D(xor_8_out), .nQ(d_latch_8_nq));  // open: Q
  not not_1 (not_1_out, MODE4);
  or or_9 (or_9_out, d_ff_1_qn, d_ff_2_qn);
  and _7 (_7_out, not_1_out, or_9_out);
  not not_2 (not_2_out, 1'b1);
  not not_3 (not_3_out, _11_out);
  nor nor_4 (nor_4_out, not_2_out, d_ff_1_qn);
  nand _5 (_5_out, not_1_out, or_9_out);
  nor _7_2 (_7_2_out, _7_out, d_ff_3_qn);
  nor _8 (_8_out, _7_out, d_ff_3_qn, d_ff_4_qn);
  nor _9 (_9_out, _7_out, d_ff_3_qn, d_ff_4_qn, d_ff_5_qn);
  nor _10 (_10_out, _7_out, d_ff_3_qn, d_ff_4_qn, d_ff_5_qn, d_ff_6_qn);
  nor _11 (_11_out, _7_out, d_ff_3_qn, d_ff_4_qn, d_ff_5_qn, d_ff_6_qn, d_ff_7_qn);
  nor nor_5 (COUT, not_3_out, d_ff_8_qn);
endmodule

// OAM2 COUNTER
module OAM2_COUNTER (
  input  nPCLK,
  input  RES,
  input  STEP,
  output Q0,
  output Q1,
  output Q2,
  output Q3,
  output Q4,
  output CARRY_OUT
);

  wire d_ff_1_qn, d_ff_2_qn, d_ff_3_qn, d_ff_4_qn, d_ff_5_qn, d_latch_1_nq, d_latch_2_nq, d_latch_3_nq,
       d_latch_4_nq, d_latch_5_nq, nor_1_out, nor_2_out, nor_3_out, nor_4_out, not_1_out, not_2_out,
       not_3_out, not_4_out, not_5_out, xor_1_out, xor_2_out, xor_3_out, xor_4_out, xor_5_out;

  D_Flip_Flop d_ff_1 (.clk(STEP), .D(d_latch_1_nq), .Q(Q0), .Qn(d_ff_1_qn), .reset(RES));  // open: preset, en
  D_Flip_Flop d_ff_2 (.clk(STEP), .D(d_latch_2_nq), .Q(Q1), .Qn(d_ff_2_qn), .reset(RES));  // open: preset, en
  D_Flip_Flop d_ff_3 (.clk(STEP), .D(d_latch_3_nq), .Q(Q2), .Qn(d_ff_3_qn), .reset(RES));  // open: preset, en
  D_Flip_Flop d_ff_4 (.clk(STEP), .D(d_latch_4_nq), .Q(Q3), .Qn(d_ff_4_qn), .reset(RES));  // open: preset, en
  D_Flip_Flop d_ff_5 (.clk(STEP), .D(d_latch_5_nq), .Q(Q4), .Qn(d_ff_5_qn), .reset(RES));  // open: preset, en
  not not_1 (not_1_out, 1'b1);
  not not_2 (not_2_out, nor_1_out);
  not not_3 (not_3_out, nor_2_out);
  not not_4 (not_4_out, nor_3_out);
  not not_5 (not_5_out, nor_4_out);
  xor xor_1 (xor_1_out, 1'b1, d_ff_1_qn);
  nor nor_1 (nor_1_out, not_1_out, d_ff_1_qn);
  xor xor_2 (xor_2_out, nor_1_out, d_ff_2_qn);
  nor nor_2 (nor_2_out, not_2_out, d_ff_2_qn);
  xor xor_3 (xor_3_out, nor_2_out, d_ff_3_qn);
  nor nor_3 (nor_3_out, not_3_out, d_ff_3_qn);
  xor xor_4 (xor_4_out, nor_3_out, d_ff_4_qn);
  nor nor_4 (nor_4_out, not_4_out, d_ff_4_qn);
  xor xor_5 (xor_5_out, nor_4_out, d_ff_5_qn);
  nor nor_5 (CARRY_OUT, not_5_out, d_ff_5_qn);
  D_latch d_latch_1 (.EN(nPCLK), .D(xor_1_out), .nQ(d_latch_1_nq));  // open: Q
  D_latch d_latch_2 (.EN(nPCLK), .D(xor_2_out), .nQ(d_latch_2_nq));  // open: Q
  D_latch d_latch_3 (.EN(nPCLK), .D(xor_3_out), .nQ(d_latch_3_nq));  // open: Q
  D_latch d_latch_4 (.EN(nPCLK), .D(xor_4_out), .nQ(d_latch_4_nq));  // open: Q
  D_latch d_latch_5 (.EN(nPCLK), .D(xor_5_out), .nQ(d_latch_5_nq));  // open: Q
endmodule

// OAM BUF CONTROL
module OAM_BUF_CONTROL (
  input  [1:0] PCLK,
  input  BLNK,
  input  SPR_OV,
  input  nVIS,
  input  OAMCTR2,
  input  H0_prime_prime,
  input  nW4,
  input  nDBE,
  output OB_OAM,
  output nWE,
  output OFETCH
);

  wire _1_out, _4_out, _6_out, _8_out, _9_out, d_ff_1_qn, d_latch_1_nq, d_latch_2_nq, d_latch_3_nq,
       d_latch_4_q, not_1_out;

  not not_1 (not_1_out, H0_prime_prime);
  nor _1 (_1_out, nW4, nDBE);
  nor _7 (OB_OAM, PCLK[1], BLNK);
  nor _4 (_4_out, BLNK, PCLK[0], SPR_OV, nVIS, OAMCTR2, not_1_out);
  nor _8 (_8_out, _1_out, _9_out);
  nor _9 (_9_out, _8_out, d_latch_3_nq);
  nor _6 (_6_out, _1_out, _8_out);
  D_Flip_Flop #(.trigger("high")) d_ff_1 (.clk(PCLK[0]), .D(_6_out), .Qn(d_ff_1_qn));  // open: Q, preset, en, reset
  D_latch d_latch_1 (.EN(PCLK[1]), .D(d_ff_1_qn), .nQ(d_latch_1_nq));  // open: Q
  D_latch d_latch_2 (.EN(PCLK[0]), .D(d_latch_1_nq), .nQ(d_latch_2_nq));  // open: Q
  D_latch d_latch_3 (.EN(PCLK[1]), .D(d_latch_2_nq), .nQ(d_latch_3_nq));  // open: Q
  D_latch d_latch_4 (.EN(PCLK[0]), .D(d_latch_3_nq), .Q(d_latch_4_q));  // open: nQ
  nor _10 (OFETCH, d_latch_4_q, d_latch_2_nq);
  nor _3 (nWE, _4_out, OFETCH);

  // Notes on the sheet:
  //   5
  //   FF1
  //   FF2
  //   1
  //   2
  //   3
  //   4
endmodule

// OAM BUFFER
module OAM_BUFFER (
  input  [1:0] PCLK,
  input  [7:0] RAM_read,
  input  I_OAM2,
  input  nR4,
  input  OB_OAM,
  input  [7:0] DB___OAM,
  input  BLNK,
  input  nWE,
  output [7:0] OAM___DB,
  output [7:0] OB_bit_out,
  output [7:0] RAM_write
);

  wire and_2_out, controlled_buffer_3_out, controlled_buffer_4_out, d_ff_9_q, d_latch_17_nq, d_latch_18_q,
       multiplexer_2_out, nor_4_out, nor_5_out, nor_6_out, not_2_out, not_3_out, not_4_out, not_5_out,
       not_6_out, transistor_1_out, transistor_2_out, transistor_3_out, transistor_4_out, transistor_6_out,
       transistor_7_out, transistor_9_out, transistor_10_out, transistor_11_out, transistor_13_out,
       transistor_14_out, transistor_15_out, transistor_16_out, transistor_19_out, transistor_20_out,
       transistor_21_out, transistor_22_out, transistor_24_out, transistor_25_out, transistor_26_out,
       transistor_27_out, transistor_28_out, transistor_29_out, undriven_2, undriven_3, undriven_4,
       undriven_5, undriven_6, undriven_7, undriven_8, undriven_9, undriven_10, undriven_11, undriven_12,
       undriven_13;
  wire [1:0] undriven;
  wire [7:0] and_1_out, d_ff_1_q, d_latch_9_q, multiplexer_1_out, nor_1_out, nor_2_out, nor_3_out, not_1_out;

  assign not_1_out = ~RAM_read;  // NOT_Gate not_1, 8 bits wide
  assign nor_1_out = ~(not_1_out | {8{PCLK[0]}} | nor_2_out);  // NOR_Gate nor_1, 8 bits wide
  assign nor_2_out = ~(nor_1_out | {8{PCLK[0]}} | RAM_read);  // NOR_Gate nor_2, 8 bits wide
  assign nor_3_out = ~(nor_1_out | {8{I_OAM2}});  // NOR_Gate nor_3, 8 bits wide
  assign and_1_out = OB_bit_out & {8{OB_OAM}};  // AND_Gate and_1, 8 bits wide
  D_latch d_latch_1 (.EN(PCLK[1]), .D(nor_3_out[0]), .nQ(OB_bit_out[0]));  // open: Q
  D_latch d_latch_2 (.EN(PCLK[1]), .D(nor_3_out[1]), .nQ(OB_bit_out[1]));  // open: Q
  D_latch d_latch_3 (.EN(PCLK[1]), .D(nor_3_out[2]), .nQ(OB_bit_out[2]));  // open: Q
  D_latch d_latch_4 (.EN(PCLK[1]), .D(nor_3_out[3]), .nQ(OB_bit_out[3]));  // open: Q
  D_latch d_latch_5 (.EN(PCLK[1]), .D(nor_3_out[4]), .nQ(OB_bit_out[4]));  // open: Q
  D_latch d_latch_6 (.EN(PCLK[1]), .D(nor_3_out[5]), .nQ(OB_bit_out[5]));  // open: Q
  D_latch d_latch_7 (.EN(PCLK[1]), .D(nor_3_out[6]), .nQ(OB_bit_out[6]));  // open: Q
  D_latch d_latch_8 (.EN(PCLK[1]), .D(nor_3_out[7]), .nQ(OB_bit_out[7]));  // open: Q
  Multiplexer #(.width(8), .disabled(0), .enable("false")) multiplexer_1 (
    .in0(and_1_out), .in1(DB___OAM), .out(multiplexer_1_out), .sel(BLNK));
  D_latch d_latch_9 (.EN(PCLK[0]), .D(OB_bit_out[0]), .Q(d_latch_9_q[0]));  // open: nQ
  D_latch d_latch_10 (.EN(PCLK[0]), .D(OB_bit_out[1]), .Q(d_latch_9_q[1]));  // open: nQ
  D_latch d_latch_11 (.EN(PCLK[0]), .D(OB_bit_out[2]), .Q(d_latch_9_q[2]));  // open: nQ
  D_latch d_latch_12 (.EN(PCLK[0]), .D(OB_bit_out[3]), .Q(d_latch_9_q[3]));  // open: nQ
  D_latch d_latch_13 (.EN(PCLK[0]), .D(OB_bit_out[4]), .Q(d_latch_9_q[4]));  // open: nQ
  D_latch d_latch_14 (.EN(PCLK[0]), .D(OB_bit_out[5]), .Q(d_latch_9_q[5]));  // open: nQ
  D_latch d_latch_15 (.EN(PCLK[0]), .D(OB_bit_out[6]), .Q(d_latch_9_q[6]));  // open: nQ
  D_latch d_latch_16 (.EN(PCLK[0]), .D(OB_bit_out[7]), .Q(d_latch_9_q[7]));  // open: nQ
  not not_2 (not_2_out, nR4);
  D_Flip_Flop #(.trigger("high")) d_ff_1 (
    .clk(PCLK[0]), .D(multiplexer_1_out[0]), .Q(d_ff_1_q[0]));  // open: Qn, preset, en, reset
  D_Flip_Flop #(.trigger("high")) d_ff_2 (
    .clk(PCLK[0]), .D(multiplexer_1_out[1]), .Q(d_ff_1_q[1]));  // open: Qn, preset, en, reset
  D_Flip_Flop #(.trigger("high")) d_ff_3 (
    .clk(PCLK[0]), .D(multiplexer_1_out[2]), .Q(d_ff_1_q[2]));  // open: Qn, preset, en, reset
  D_Flip_Flop #(.trigger("high")) d_ff_4 (
    .clk(PCLK[0]), .D(multiplexer_1_out[3]), .Q(d_ff_1_q[3]));  // open: Qn, preset, en, reset
  D_Flip_Flop #(.trigger("high")) d_ff_5 (
    .clk(PCLK[0]), .D(multiplexer_1_out[4]), .Q(d_ff_1_q[4]));  // open: Qn, preset, en, reset
  D_Flip_Flop #(.trigger("high")) d_ff_6 (
    .clk(PCLK[0]), .D(multiplexer_1_out[5]), .Q(d_ff_1_q[5]));  // open: Qn, preset, en, reset
  D_Flip_Flop #(.trigger("high")) d_ff_7 (
    .clk(PCLK[0]), .D(multiplexer_1_out[6]), .Q(d_ff_1_q[6]));  // open: Qn, preset, en, reset
  D_Flip_Flop #(.trigger("high")) d_ff_8 (
    .clk(PCLK[0]), .D(multiplexer_1_out[7]), .Q(d_ff_1_q[7]));  // open: Qn, preset, en, reset
  not not_3 (not_3_out, nWE);
  assign OAM___DB = not_2_out ? d_latch_9_q : 8'bz;  // Controlled_Buffer controlled_buffer_1
  assign RAM_write = not_3_out ? d_ff_1_q : 8'bz;  // Controlled_Buffer controlled_buffer_2
  Transistor #(.\type ("n")) transistor_1 (.in(undriven_2), .out(transistor_1_out));  // open: gate
  not not_4 (not_4_out, undriven_3);
  nor nor_4 (nor_4_out, not_4_out, undriven[0], nor_5_out);
  nor nor_5 (nor_5_out, nor_4_out, undriven[0], undriven_3);
  and and_2 (and_2_out, d_latch_17_nq, undriven_6);
  Transistor #(.\type ("n")) transistor_2 (.in(transistor_1_out), .out(transistor_2_out));  // open: gate
  Transistor #(.\type ("n")) transistor_3 (.in(transistor_16_out), .out(transistor_3_out));  // open: gate
  nor nor_6 (nor_6_out, nor_4_out, undriven_4);
  Multiplexer #(.disabled(0), .enable("false")) multiplexer_2 (
    .in0(and_2_out), .in1(undriven_8), .out(multiplexer_2_out), .sel(undriven_7));
  Transistor #(.\type ("n")) transistor_4 (.in(transistor_2_out), .out(transistor_4_out), .gate(transistor_2_out));
  Transistor #(.\type ("n")) transistor_5 (.in(1'b0), .out(transistor_2_out), .gate(transistor_3_out));
  D_latch d_latch_17 (.EN(undriven[1]), .D(nor_6_out), .nQ(d_latch_17_nq));  // open: Q
  D_Flip_Flop #(.trigger("high")) d_ff_9 (
    .clk(undriven[0]), .D(multiplexer_2_out), .Q(d_ff_9_q));  // open: Qn, preset, en, reset
  Transistor #(.\type ("n")) transistor_6 (.in(transistor_7_out), .out(transistor_6_out), .gate(transistor_7_out));
  Transistor #(.\type ("n")) transistor_7 (.in(1'b0), .out(transistor_7_out), .gate(transistor_1_out));
  Transistor #(.\type ("n")) transistor_8 (.in(transistor_9_out), .out(transistor_4_out), .gate(transistor_2_out));
  Transistor #(.\type ("n")) transistor_9 (.in(1'b0), .out(transistor_9_out), .gate(transistor_3_out));
  Transistor #(.\type ("n")) transistor_10 (.in(transistor_11_out), .out(transistor_10_out), .gate(transistor_11_out));
  Transistor #(.\type ("n")) transistor_11 (.in(1'b0), .out(transistor_11_out), .gate(undriven_11));
  Transistor #(.\type ("n")) transistor_12 (.in(1'b0), .out(transistor_11_out), .gate(transistor_7_out));
  assign controlled_buffer_3_out = not_5_out ? d_latch_18_q : 1'bz;  // Controlled_Buffer controlled_buffer_3
  D_latch d_latch_18 (.EN(undriven[0]), .D(d_latch_17_nq), .Q(d_latch_18_q));  // open: nQ
  not not_5 (not_5_out, undriven_5);
  assign controlled_buffer_4_out = not_6_out ? d_ff_9_q : 1'bz;  // Controlled_Buffer controlled_buffer_4
  not not_6 (not_6_out, undriven_9);
  Transistor #(.\type ("n")) transistor_13 (.in(transistor_14_out), .out(transistor_13_out), .gate(transistor_14_out));
  Transistor #(.\type ("n")) transistor_14 (.in(1'b0), .out(transistor_14_out), .gate(transistor_11_out));
  Transistor #(.\type ("n")) transistor_15 (.in(transistor_16_out), .out(transistor_15_out), .gate(transistor_16_out));
  Transistor #(.\type ("n")) transistor_16 (.in(1'b0), .out(transistor_16_out), .gate(undriven_10));
  Transistor #(.\type ("n")) transistor_17 (.in(1'b0), .out(transistor_14_out), .gate(undriven_11));
  Transistor #(.\type ("n"), .gate("br")) transistor_18 (.in(1'b0), .out(transistor_16_out), .gate(transistor_26_out));
  Transistor #(.\type ("n")) transistor_19 (.in(transistor_11_out), .out(transistor_19_out), .gate(undriven_12));
  Transistor #(.\type ("n")) transistor_20 (.in(transistor_14_out), .out(transistor_20_out), .gate(undriven_13));
  Transistor #(.\type ("n")) transistor_21 (.in(transistor_22_out), .out(transistor_21_out), .gate(transistor_22_out));
  Transistor #(.\type ("n")) transistor_22 (.in(1'b0), .out(transistor_22_out), .gate(transistor_25_out));
  Transistor #(.\type ("n"), .gate("br")) transistor_23 (.in(1'b0), .out(transistor_22_out), .gate(transistor_26_out));
  Transistor #(.\type ("n")) transistor_24 (.in(transistor_25_out), .out(transistor_24_out), .gate(transistor_11_out));
  Transistor #(.\type ("n")) transistor_25 (.in(1'b0), .out(transistor_25_out), .gate(transistor_14_out));
  Transistor #(.\type ("n")) transistor_26 (.in(transistor_22_out), .out(transistor_26_out));  // open: gate
  Transistor #(.\type ("n")) transistor_27 (.in(transistor_28_out), .out(transistor_27_out), .gate(transistor_14_out));
  Transistor #(.\type ("n")) transistor_28 (.in(1'b0), .out(transistor_28_out), .gate(transistor_11_out));
  Transistor #(.\type ("n")) transistor_29 (.in(transistor_26_out), .out(transistor_29_out), .gate(transistor_26_out));
  Transistor #(.\type ("n"), .gate("br")) transistor_30 (.in(1'b0), .out(transistor_26_out), .gate(transistor_28_out));
  Transistor #(.\type ("n")) transistor_31 (.in(1'b0), .out(transistor_26_out), .gate(transistor_22_out));
  // also tied to VCC on the sheet: {transistor_4_out, transistor_6_out, transistor_10_out, transistor_15_out, transistor_13_out, transistor_21_out, transistor_19_out, transistor_20_out, transistor_24_out, transistor_29_out, transistor_27_out}

  // Notes on the sheet:
  //   PCLK
  //   RAM Read
  //   I/OAM2
  //   /R4
  //   OB/OAM
  //   BLNK
  //   DB--->OAM
  //   /WE
  //   DBx
  //   BLNK
  //   2C04-0003  OAM BIT BUF
  //   OB/OAM
  //   /PCLK
  //   /WR
  //   OBx
  //   I/OAM2
  //   OAM--->DB
  //   OB bit out
  //   RAM Write
  //   PCLK
  //   PCLK
  //   PCLK
  //   VAL
  //   /VAL
endmodule

// OAM FIFO
module OAM_FIFO (
  input  [1:0] PCLK,
  input  _0_HPOS,
  input  H3_prime_prime,
  input  H4_prime_prime,
  input  H5_prime_prime,
  input  nSH2,
  input  nSH3,
  input  nSH5,
  input  nSH7,
  input  nVIS,
  input  nCLPO,
  input  OB0,
  input  OB1,
  input  OB2,
  input  OB3,
  input  OB4,
  input  OB5,
  input  OB6,
  input  OB7,
  input  nT0,
  input  nT1,
  input  nT2,
  input  nT3,
  input  nT4,
  input  nT5,
  input  nT6,
  input  nT7,
  output nSPR0HIT,
  output nZCOL0,
  output nZCOL1,
  output ZCOL2,
  output ZCOL3,
  output nZPRIO
);

  wire _0_H, and_1_out, and_2_out, and_3_out, and_4_out, and_5_out, and_6_out, and_7_out, and_8_out,
       d_latch_1_nq, d_latch_2_nq, nor_1_out, nor_2_out, nor_3_out, nor_4_out, nor_5_out, nor_6_out,
       nor_7_out, nor_8_out, nor_9_out, oam_fifo_pipeline_1_nx_col0, oam_fifo_pipeline_1_nx_col1,
       oam_fifo_pipeline_1_nx_en, oam_fifo_pipeline_1_x_col2, oam_fifo_pipeline_1_x_col3,
       oam_fifo_pipeline_1_x_prio, oam_fifo_pipeline_2_nx_col0, oam_fifo_pipeline_2_nx_col1,
       oam_fifo_pipeline_2_nx_en, oam_fifo_pipeline_2_x_col2, oam_fifo_pipeline_2_x_col3,
       oam_fifo_pipeline_2_x_prio, oam_fifo_pipeline_3_nx_col0, oam_fifo_pipeline_3_nx_col1,
       oam_fifo_pipeline_3_nx_en, oam_fifo_pipeline_3_x_col2, oam_fifo_pipeline_3_x_col3,
       oam_fifo_pipeline_3_x_prio, oam_fifo_pipeline_4_nx_col0, oam_fifo_pipeline_4_nx_col1,
       oam_fifo_pipeline_4_nx_en, oam_fifo_pipeline_4_x_col2, oam_fifo_pipeline_4_x_col3,
       oam_fifo_pipeline_4_x_prio, oam_fifo_pipeline_5_nx_col0, oam_fifo_pipeline_5_nx_col1,
       oam_fifo_pipeline_5_nx_en, oam_fifo_pipeline_5_x_col2, oam_fifo_pipeline_5_x_col3,
       oam_fifo_pipeline_5_x_prio, oam_fifo_pipeline_6_nx_col0, oam_fifo_pipeline_6_nx_col1,
       oam_fifo_pipeline_6_nx_en, oam_fifo_pipeline_6_x_col2, oam_fifo_pipeline_6_x_col3,
       oam_fifo_pipeline_6_x_prio, oam_fifo_pipeline_7_nx_col0, oam_fifo_pipeline_7_nx_col1,
       oam_fifo_pipeline_7_nx_en, oam_fifo_pipeline_7_x_col2, oam_fifo_pipeline_7_x_col3,
       oam_fifo_pipeline_7_x_prio, oam_fifo_pipeline_8_nx_col0, oam_fifo_pipeline_8_nx_col1,
       oam_fifo_pipeline_8_nx_en, oam_fifo_pipeline_8_x_col2, oam_fifo_pipeline_8_x_col3,
       oam_fifo_pipeline_8_x_prio, SEL0, SEL1, SEL2, SEL3, SEL4, SEL5, SEL6, SEL7;

  Decoder #(.select(3), .disabled(0), .enable("false")) decoder_1 (
    .out0(SEL0), .out1(SEL1), .out2(SEL2), .out3(SEL3), .out4(SEL4), .out5(SEL5), .out6(SEL6), .out7(SEL7),
    .sel({H5_prime_prime, H4_prime_prime, H3_prime_prime}));
  D_latch d_latch_1 (.EN(PCLK[1]), .D(_0_HPOS), .nQ(d_latch_1_nq));  // open: Q
  D_latch d_latch_2 (.EN(PCLK[0]), .D(d_latch_1_nq), .nQ(d_latch_2_nq));  // open: Q
  D_latch d_latch_3 (.EN(PCLK[1]), .D(d_latch_2_nq), .nQ(_0_H));  // open: Q
  OAM_FIFO_PIPELINE oam_fifo_pipeline_1 (
    .PCLK(PCLK), .nSH5(nSH5), .SEL(SEL0), .nSH7(nSH7), .nSH3(nSH3), .nSH2(nSH2), ._0_H(_0_H), .nVIS(nVIS),
    .OB0(OB0), .OB1(OB1), .OB2(OB2), .OB3(OB3), .OB4(OB4), .OB5(OB5), .OB6(OB6), .OB7(OB7),
    .nX_COL0(oam_fifo_pipeline_1_nx_col0), .nX_COL1(oam_fifo_pipeline_1_nx_col1),
    .nX_EN(oam_fifo_pipeline_1_nx_en), .X_COL2(oam_fifo_pipeline_1_x_col2),
    .X_COL3(oam_fifo_pipeline_1_x_col3), .X_PRIO(oam_fifo_pipeline_1_x_prio), .nT0(nT0), .nT1(nT1),
    .nT2(nT2), .nT3(nT3), .nT4(nT4), .nT5(nT5), .nT6(nT6), .nT7(nT7));
  OAM_FIFO_PIPELINE oam_fifo_pipeline_2 (
    .PCLK(PCLK), .nSH5(nSH5), .SEL(SEL1), .nSH7(nSH7), .nSH3(nSH3), .nSH2(nSH2), ._0_H(_0_H), .nVIS(nVIS),
    .OB0(OB0), .OB1(OB1), .OB2(OB2), .OB3(OB3), .OB4(OB4), .OB5(OB5), .OB6(OB6), .OB7(OB7),
    .nX_COL0(oam_fifo_pipeline_2_nx_col0), .nX_COL1(oam_fifo_pipeline_2_nx_col1),
    .nX_EN(oam_fifo_pipeline_2_nx_en), .X_COL2(oam_fifo_pipeline_2_x_col2),
    .X_COL3(oam_fifo_pipeline_2_x_col3), .X_PRIO(oam_fifo_pipeline_2_x_prio), .nT0(nT0), .nT1(nT1),
    .nT2(nT2), .nT3(nT3), .nT4(nT4), .nT5(nT5), .nT6(nT6), .nT7(nT7));
  OAM_FIFO_PIPELINE oam_fifo_pipeline_3 (
    .PCLK(PCLK), .nSH5(nSH5), .SEL(SEL2), .nSH7(nSH7), .nSH3(nSH3), .nSH2(nSH2), ._0_H(_0_H), .nVIS(nVIS),
    .OB0(OB0), .OB1(OB1), .OB2(OB2), .OB3(OB3), .OB4(OB4), .OB5(OB5), .OB6(OB6), .OB7(OB7),
    .nX_COL0(oam_fifo_pipeline_3_nx_col0), .nX_COL1(oam_fifo_pipeline_3_nx_col1),
    .nX_EN(oam_fifo_pipeline_3_nx_en), .X_COL2(oam_fifo_pipeline_3_x_col2),
    .X_COL3(oam_fifo_pipeline_3_x_col3), .X_PRIO(oam_fifo_pipeline_3_x_prio), .nT0(nT0), .nT1(nT1),
    .nT2(nT2), .nT3(nT3), .nT4(nT4), .nT5(nT5), .nT6(nT6), .nT7(nT7));
  OAM_FIFO_PIPELINE oam_fifo_pipeline_4 (
    .PCLK(PCLK), .nSH5(nSH5), .SEL(SEL3), .nSH7(nSH7), .nSH3(nSH3), .nSH2(nSH2), ._0_H(_0_H), .nVIS(nVIS),
    .OB0(OB0), .OB1(OB1), .OB2(OB2), .OB3(OB3), .OB4(OB4), .OB5(OB5), .OB6(OB6), .OB7(OB7),
    .nX_COL0(oam_fifo_pipeline_4_nx_col0), .nX_COL1(oam_fifo_pipeline_4_nx_col1),
    .nX_EN(oam_fifo_pipeline_4_nx_en), .X_COL2(oam_fifo_pipeline_4_x_col2),
    .X_COL3(oam_fifo_pipeline_4_x_col3), .X_PRIO(oam_fifo_pipeline_4_x_prio), .nT0(nT0), .nT1(nT1),
    .nT2(nT2), .nT3(nT3), .nT4(nT4), .nT5(nT5), .nT6(nT6), .nT7(nT7));
  OAM_FIFO_PIPELINE oam_fifo_pipeline_5 (
    .PCLK(PCLK), .nSH5(nSH5), .SEL(SEL4), .nSH7(nSH7), .nSH3(nSH3), .nSH2(nSH2), ._0_H(_0_H), .nVIS(nVIS),
    .OB0(OB0), .OB1(OB1), .OB2(OB2), .OB3(OB3), .OB4(OB4), .OB5(OB5), .OB6(OB6), .OB7(OB7),
    .nX_COL0(oam_fifo_pipeline_5_nx_col0), .nX_COL1(oam_fifo_pipeline_5_nx_col1),
    .nX_EN(oam_fifo_pipeline_5_nx_en), .X_COL2(oam_fifo_pipeline_5_x_col2),
    .X_COL3(oam_fifo_pipeline_5_x_col3), .X_PRIO(oam_fifo_pipeline_5_x_prio), .nT0(nT0), .nT1(nT1),
    .nT2(nT2), .nT3(nT3), .nT4(nT4), .nT5(nT5), .nT6(nT6), .nT7(nT7));
  OAM_FIFO_PIPELINE oam_fifo_pipeline_6 (
    .PCLK(PCLK), .nSH5(nSH5), .SEL(SEL5), .nSH7(nSH7), .nSH3(nSH3), .nSH2(nSH2), ._0_H(_0_H), .nVIS(nVIS),
    .OB0(OB0), .OB1(OB1), .OB2(OB2), .OB3(OB3), .OB4(OB4), .OB5(OB5), .OB6(OB6), .OB7(OB7),
    .nX_COL0(oam_fifo_pipeline_6_nx_col0), .nX_COL1(oam_fifo_pipeline_6_nx_col1),
    .nX_EN(oam_fifo_pipeline_6_nx_en), .X_COL2(oam_fifo_pipeline_6_x_col2),
    .X_COL3(oam_fifo_pipeline_6_x_col3), .X_PRIO(oam_fifo_pipeline_6_x_prio), .nT0(nT0), .nT1(nT1),
    .nT2(nT2), .nT3(nT3), .nT4(nT4), .nT5(nT5), .nT6(nT6), .nT7(nT7));
  OAM_FIFO_PIPELINE oam_fifo_pipeline_7 (
    .PCLK(PCLK), .nSH5(nSH5), .SEL(SEL6), .nSH7(nSH7), .nSH3(nSH3), .nSH2(nSH2), ._0_H(_0_H), .nVIS(nVIS),
    .OB0(OB0), .OB1(OB1), .OB2(OB2), .OB3(OB3), .OB4(OB4), .OB5(OB5), .OB6(OB6), .OB7(OB7),
    .nX_COL0(oam_fifo_pipeline_7_nx_col0), .nX_COL1(oam_fifo_pipeline_7_nx_col1),
    .nX_EN(oam_fifo_pipeline_7_nx_en), .X_COL2(oam_fifo_pipeline_7_x_col2),
    .X_COL3(oam_fifo_pipeline_7_x_col3), .X_PRIO(oam_fifo_pipeline_7_x_prio), .nT0(nT0), .nT1(nT1),
    .nT2(nT2), .nT3(nT3), .nT4(nT4), .nT5(nT5), .nT6(nT6), .nT7(nT7));
  OAM_FIFO_PIPELINE oam_fifo_pipeline_8 (
    .PCLK(PCLK), .nSH5(nSH5), .SEL(SEL7), .nSH7(nSH7), .nSH3(nSH3), .nSH2(nSH2), ._0_H(_0_H), .nVIS(nVIS),
    .OB0(OB0), .OB1(OB1), .OB2(OB2), .OB3(OB3), .OB4(OB4), .OB5(OB5), .OB6(OB6), .OB7(OB7),
    .nX_COL0(oam_fifo_pipeline_8_nx_col0), .nX_COL1(oam_fifo_pipeline_8_nx_col1),
    .nX_EN(oam_fifo_pipeline_8_nx_en), .X_COL2(oam_fifo_pipeline_8_x_col2),
    .X_COL3(oam_fifo_pipeline_8_x_col3), .X_PRIO(oam_fifo_pipeline_8_x_prio), .nT0(nT0), .nT1(nT1),
    .nT2(nT2), .nT3(nT3), .nT4(nT4), .nT5(nT5), .nT6(nT6), .nT7(nT7));
  and and_1 (and_1_out, oam_fifo_pipeline_1_nx_col0, oam_fifo_pipeline_1_nx_col1);
  and and_2 (and_2_out, oam_fifo_pipeline_2_nx_col0, oam_fifo_pipeline_2_nx_col1);
  and and_3 (and_3_out, oam_fifo_pipeline_3_nx_col0, oam_fifo_pipeline_3_nx_col1);
  and and_4 (and_4_out, oam_fifo_pipeline_4_nx_col0, oam_fifo_pipeline_4_nx_col1);
  and and_5 (and_5_out, oam_fifo_pipeline_5_nx_col0, oam_fifo_pipeline_5_nx_col1);
  and and_6 (and_6_out, oam_fifo_pipeline_6_nx_col0, oam_fifo_pipeline_6_nx_col1);
  and and_7 (and_7_out, oam_fifo_pipeline_7_nx_col0, oam_fifo_pipeline_7_nx_col1);
  and and_8 (and_8_out, oam_fifo_pipeline_8_nx_col0, oam_fifo_pipeline_8_nx_col1);
  nor nor_1 (nor_1_out, nCLPO, oam_fifo_pipeline_1_nx_en, and_1_out);
  nor nor_2 (nor_2_out, nor_1_out, nCLPO, oam_fifo_pipeline_2_nx_en, and_2_out);
  nor nor_3 (nor_3_out, nor_2_out, nor_1_out, nCLPO, oam_fifo_pipeline_3_nx_en, and_3_out);
  nor nor_4 (nor_4_out, nor_3_out, nor_2_out, nor_1_out, nCLPO, oam_fifo_pipeline_4_nx_en, and_4_out);
  nor nor_5 (nor_5_out, nor_4_out, nor_3_out, nor_2_out, nor_1_out, nCLPO, oam_fifo_pipeline_5_nx_en, and_5_out);
  nor nor_6 (nor_6_out, nor_5_out, nor_4_out, nor_3_out, nor_2_out, nor_1_out, nCLPO, oam_fifo_pipeline_6_nx_en, and_6_out);
  nor nor_7 (nor_7_out, nor_6_out, nor_5_out, nor_4_out, nor_3_out, nor_2_out, nor_1_out, nCLPO, oam_fifo_pipeline_7_nx_en, and_7_out);
  nor nor_8 (nor_8_out, nor_7_out, nor_6_out, nor_5_out, nor_4_out, nor_3_out, nor_2_out, nor_1_out, nCLPO, oam_fifo_pipeline_8_nx_en, and_8_out);
  nor nor_9 (nor_9_out, nor_8_out, nor_7_out, nor_6_out, nor_5_out, nor_4_out, nor_3_out, nor_2_out, nor_1_out);
  D_latch d_latch_4 (.EN(PCLK[0]), .D(nor_1_out), .nQ(nSPR0HIT));  // open: Q
  assign nZCOL0 = nor_1_out ? oam_fifo_pipeline_1_nx_col0 : 1'bz;  // Controlled_Buffer controlled_buffer_1
  assign nZCOL1 = nor_1_out ? oam_fifo_pipeline_1_nx_col1 : 1'bz;  // Controlled_Buffer controlled_buffer_2
  assign ZCOL2 = nor_1_out ? oam_fifo_pipeline_1_x_col2 : 1'bz;  // Controlled_Buffer controlled_buffer_3
  assign ZCOL3 = nor_1_out ? oam_fifo_pipeline_1_x_col3 : 1'bz;  // Controlled_Buffer controlled_buffer_4
  assign nZPRIO = nor_1_out ? oam_fifo_pipeline_1_x_prio : 1'bz;  // Controlled_Buffer controlled_buffer_5
  assign nZCOL0 = nor_2_out ? oam_fifo_pipeline_2_nx_col0 : 1'bz;  // Controlled_Buffer controlled_buffer_6
  assign nZCOL1 = nor_2_out ? oam_fifo_pipeline_2_nx_col1 : 1'bz;  // Controlled_Buffer controlled_buffer_7
  assign ZCOL2 = nor_2_out ? oam_fifo_pipeline_2_x_col2 : 1'bz;  // Controlled_Buffer controlled_buffer_8
  assign ZCOL3 = nor_2_out ? oam_fifo_pipeline_2_x_col3 : 1'bz;  // Controlled_Buffer controlled_buffer_9
  assign nZPRIO = nor_2_out ? oam_fifo_pipeline_2_x_prio : 1'bz;  // Controlled_Buffer controlled_buffer_10
  assign nZCOL0 = nor_3_out ? oam_fifo_pipeline_3_nx_col0 : 1'bz;  // Controlled_Buffer controlled_buffer_11
  assign nZCOL1 = nor_3_out ? oam_fifo_pipeline_3_nx_col1 : 1'bz;  // Controlled_Buffer controlled_buffer_12
  assign ZCOL2 = nor_3_out ? oam_fifo_pipeline_3_x_col2 : 1'bz;  // Controlled_Buffer controlled_buffer_13
  assign ZCOL3 = nor_3_out ? oam_fifo_pipeline_3_x_col3 : 1'bz;  // Controlled_Buffer controlled_buffer_14
  assign nZPRIO = nor_3_out ? oam_fifo_pipeline_3_x_prio : 1'bz;  // Controlled_Buffer controlled_buffer_15
  assign nZCOL0 = nor_4_out ? oam_fifo_pipeline_4_nx_col0 : 1'bz;  // Controlled_Buffer controlled_buffer_16
  assign nZCOL1 = nor_4_out ? oam_fifo_pipeline_4_nx_col1 : 1'bz;  // Controlled_Buffer controlled_buffer_17
  assign ZCOL2 = nor_4_out ? oam_fifo_pipeline_4_x_col2 : 1'bz;  // Controlled_Buffer controlled_buffer_18
  assign ZCOL3 = nor_4_out ? oam_fifo_pipeline_4_x_col3 : 1'bz;  // Controlled_Buffer controlled_buffer_19
  assign nZPRIO = nor_4_out ? oam_fifo_pipeline_4_x_prio : 1'bz;  // Controlled_Buffer controlled_buffer_20
  assign nZCOL0 = nor_5_out ? oam_fifo_pipeline_5_nx_col0 : 1'bz;  // Controlled_Buffer controlled_buffer_21
  assign nZCOL1 = nor_5_out ? oam_fifo_pipeline_5_nx_col1 : 1'bz;  // Controlled_Buffer controlled_buffer_22
  assign ZCOL2 = nor_5_out ? oam_fifo_pipeline_5_x_col2 : 1'bz;  // Controlled_Buffer controlled_buffer_23
  assign ZCOL3 = nor_5_out ? oam_fifo_pipeline_5_x_col3 : 1'bz;  // Controlled_Buffer controlled_buffer_24
  assign nZPRIO = nor_5_out ? oam_fifo_pipeline_5_x_prio : 1'bz;  // Controlled_Buffer controlled_buffer_25
  assign nZCOL0 = nor_6_out ? oam_fifo_pipeline_6_nx_col0 : 1'bz;  // Controlled_Buffer controlled_buffer_26
  assign nZCOL1 = nor_6_out ? oam_fifo_pipeline_6_nx_col1 : 1'bz;  // Controlled_Buffer controlled_buffer_27
  assign ZCOL2 = nor_6_out ? oam_fifo_pipeline_6_x_col2 : 1'bz;  // Controlled_Buffer controlled_buffer_28
  assign ZCOL3 = nor_6_out ? oam_fifo_pipeline_6_x_col3 : 1'bz;  // Controlled_Buffer controlled_buffer_29
  assign nZPRIO = nor_6_out ? oam_fifo_pipeline_6_x_prio : 1'bz;  // Controlled_Buffer controlled_buffer_30
  assign nZCOL0 = nor_7_out ? oam_fifo_pipeline_7_nx_col0 : 1'bz;  // Controlled_Buffer controlled_buffer_31
  assign nZCOL1 = nor_7_out ? oam_fifo_pipeline_7_nx_col1 : 1'bz;  // Controlled_Buffer controlled_buffer_32
  assign ZCOL2 = nor_7_out ? oam_fifo_pipeline_7_x_col2 : 1'bz;  // Controlled_Buffer controlled_buffer_33
  assign ZCOL3 = nor_7_out ? oam_fifo_pipeline_7_x_col3 : 1'bz;  // Controlled_Buffer controlled_buffer_34
  assign nZPRIO = nor_7_out ? oam_fifo_pipeline_7_x_prio : 1'bz;  // Controlled_Buffer controlled_buffer_35
  assign nZCOL0 = nor_8_out ? oam_fifo_pipeline_8_nx_col0 : 1'bz;  // Controlled_Buffer controlled_buffer_36
  assign nZCOL1 = nor_8_out ? oam_fifo_pipeline_8_nx_col1 : 1'bz;  // Controlled_Buffer controlled_buffer_37
  assign ZCOL2 = nor_8_out ? oam_fifo_pipeline_8_x_col2 : 1'bz;  // Controlled_Buffer controlled_buffer_38
  assign ZCOL3 = nor_8_out ? oam_fifo_pipeline_8_x_col3 : 1'bz;  // Controlled_Buffer controlled_buffer_39
  assign nZPRIO = nor_8_out ? oam_fifo_pipeline_8_x_prio : 1'bz;  // Controlled_Buffer controlled_buffer_40
  assign nZCOL0 = nor_9_out ? 1'b1 : 1'bz;  // Controlled_Buffer controlled_buffer_41
  assign nZCOL1 = nor_9_out ? 1'b1 : 1'bz;  // Controlled_Buffer controlled_buffer_42

  // Other names for the same wires on the sheet: OBJ_BUS[7:0] = {OB7, OB6, OB5, OB4, OB3, OB2, OB1, OB0};
  //   T_BUS[7:0] = {nT7, nT6, nT5, nT4, nT3, nT2, nT1, nT0}

  // Notes on the sheet:
  //   PCLK
  //   /PCLK
endmodule

// FIFO PIPELINE
module OAM_FIFO_PIPELINE (
  input  [1:0] PCLK,
  input  nSH5,
  input  nSH7,
  input  nT0,
  input  nT1,
  input  nT2,
  input  nT3,
  input  nT4,
  input  nT5,
  input  nT6,
  input  nT7,
  input  nSH3,
  input  _0_H,
  input  nVIS,
  input  SEL,
  input  nSH2,
  input  OB0,
  input  OB1,
  input  OB2,
  input  OB3,
  input  OB4,
  input  OB5,
  input  OB6,
  input  OB7,
  output nX_COL0,
  output nX_COL1,
  output nX_EN,
  output X_COL2,
  output X_COL3,
  output X_PRIO
);

  wire d_latch_1_nq, d_latch_2_nq, d_latch_3_nq, d_latch_4_nq, nor_1_out, nor_2_out, nor_3_out, nor_4_out,
       nor_5_out;

  D_latch d_latch_1 (.EN(PCLK[1]), .D(SEL), .nQ(d_latch_1_nq));  // open: Q
  nor nor_1 (nor_1_out, PCLK[1], nSH5, d_latch_1_nq);
  nor nor_2 (nor_2_out, PCLK[1], d_latch_1_nq, nSH7);
  nor nor_3 (nor_3_out, PCLK[1], nX_EN);
  nor nor_4 (nor_4_out, d_latch_1_nq, PCLK[1], nSH3);
  nor nor_5 (nor_5_out, PCLK[1], d_latch_1_nq, nSH2);
  D_latch d_latch_2 (.EN(nor_5_out), .D(OB0), .nQ(d_latch_2_nq));  // open: Q
  D_latch d_latch_3 (.EN(nor_5_out), .D(OB1), .nQ(d_latch_3_nq));  // open: Q
  D_latch d_latch_4 (.EN(nor_5_out), .D(OB5), .nQ(d_latch_4_nq));  // open: Q
  D_latch d_latch_5 (.EN(PCLK[1]), .D(d_latch_2_nq), .nQ(X_COL2));  // open: Q
  D_latch d_latch_6 (.EN(PCLK[1]), .D(d_latch_3_nq), .nQ(X_COL3));  // open: Q
  D_latch d_latch_7 (.EN(PCLK[1]), .D(d_latch_4_nq), .nQ(X_PRIO));  // open: Q
  SHIFT_REG_LOAD shift_reg_load_1 (
    .LOAD(nor_1_out), .STEP(nor_3_out), .NEXT(PCLK[1]), .OUT(nX_COL0), ._0(nT0), ._1(nT1), ._2(nT2),
    ._3(nT3), ._4(nT4), ._5(nT5), ._6(nT6), ._7(nT7));
  SHIFT_REG_LOAD shift_reg_load_2 (
    .LOAD(nor_2_out), .STEP(nor_3_out), .NEXT(PCLK[1]), .OUT(nX_COL1), ._0(nT0), ._1(nT1), ._2(nT2),
    ._3(nT3), ._4(nT4), ._5(nT5), ._6(nT6), ._7(nT7));
  OAM_FIFO_COUNTER oam_fifo_counter_1 (
    .PCLK(PCLK), .nVIS(nVIS), ._0_H(_0_H), .LOAD(nor_4_out), .IN0(OB0), .IN1(OB1), .IN2(OB2), .IN3(OB3),
    .IN4(OB4), .IN5(OB5), .IN6(OB6), .IN7(OB7), .nX_EN(nX_EN));

  // Notes on the sheet:
  //   /PCLK
  //   T/SR0
  //   T/SR1
  //   EN
  //   LOAD
  //   LDAT
  //   /PCLK
endmodule

// FIFO COUNTER
module OAM_FIFO_COUNTER (
  input  [1:0] PCLK,
  input  nVIS,
  input  _0_H,
  input  LOAD,
  input  IN0,
  input  IN1,
  input  IN2,
  input  IN3,
  input  IN4,
  input  IN5,
  input  IN6,
  input  IN7,
  output nX_EN
);

  wire and_1_out, controlled_inverter_1_out, controlled_inverter_2_out, controlled_inverter_3_out,
       controlled_inverter_4_out, controlled_inverter_5_out, controlled_inverter_6_out,
       controlled_inverter_7_out, controlled_inverter_8_out, d_latch_1_nq, d_latch_2_nq, d_latch_3_nq,
       d_latch_4_nq, d_latch_5_nq, d_latch_6_nq, d_latch_7_nq, d_latch_8_nq, d_latch_10_nq, d_latch_10_q,
       d_latch_11_nq, d_latch_11_q, d_latch_12_nq, d_latch_12_q, d_latch_13_nq, d_latch_13_q, d_latch_14_nq,
       d_latch_14_q, d_latch_15_nq, d_latch_15_q, d_latch_16_nq, d_latch_16_q, d_latch_17_nq, d_latch_17_q,
       nor_1_out, nor_2_out, nor_3_out, nor_4_out, nor_5_out, nor_6_out, nor_7_out, nor_8_out, nor_9_out,
       nor_10_out, nor_11_out, nor_12_out, nor_13_out, not_1_out, not_2_out, not_3_out, not_4_out, not_5_out,
       not_6_out, not_7_out, not_8_out, s_r_ff_1_q, s_r_ff_1_qn, xor_1_out, xor_2_out, xor_3_out, xor_4_out,
       xor_5_out, xor_6_out, xor_7_out, xor_8_out;

  nor nor_1 (nor_1_out, PCLK[1], _0_H, nor_13_out);
  and and_1 (and_1_out, PCLK[0], nor_13_out);
  xor xor_1 (xor_1_out, 1'b1, d_latch_10_nq);
  xor xor_2 (xor_2_out, nor_6_out, d_latch_11_nq);
  xor xor_3 (xor_3_out, nor_7_out, d_latch_12_nq);
  xor xor_4 (xor_4_out, nor_8_out, d_latch_13_nq);
  xor xor_5 (xor_5_out, nor_9_out, d_latch_14_nq);
  xor xor_6 (xor_6_out, nor_5_out, d_latch_15_nq);
  xor xor_7 (xor_7_out, nor_11_out, d_latch_16_nq);
  xor xor_8 (xor_8_out, nor_12_out, d_latch_17_nq);
  S_R_Flip_Flop s_r_ff_1 (
    .Q(s_r_ff_1_q), .Qn(s_r_ff_1_qn), .preset(nor_1_out), .reset(and_1_out));  // open: S, clk, R, en
  nor nor_2 (nor_2_out, nor_4_out, LOAD);
  D_latch d_latch_1 (.EN(nor_2_out), .D(xor_1_out), .nQ(d_latch_1_nq));  // open: Q
  assign controlled_inverter_1_out = nor_2_out ? ~d_latch_10_nq : 1'bz;  // Controlled_Inverter controlled_inverter_1
  D_latch d_latch_2 (.EN(nor_2_out), .D(xor_2_out), .nQ(d_latch_2_nq));  // open: Q
  assign controlled_inverter_2_out = nor_2_out ? ~d_latch_11_nq : 1'bz;  // Controlled_Inverter controlled_inverter_2
  D_latch d_latch_3 (.EN(nor_2_out), .D(xor_3_out), .nQ(d_latch_3_nq));  // open: Q
  assign controlled_inverter_3_out = nor_2_out ? ~d_latch_12_nq : 1'bz;  // Controlled_Inverter controlled_inverter_3
  D_latch d_latch_4 (.EN(nor_2_out), .D(xor_4_out), .nQ(d_latch_4_nq));  // open: Q
  assign controlled_inverter_4_out = nor_2_out ? ~d_latch_13_nq : 1'bz;  // Controlled_Inverter controlled_inverter_4
  D_latch d_latch_5 (.EN(nor_2_out), .D(xor_5_out), .nQ(d_latch_5_nq));  // open: Q
  assign controlled_inverter_5_out = nor_2_out ? ~d_latch_14_nq : 1'bz;  // Controlled_Inverter controlled_inverter_5
  D_latch d_latch_6 (.EN(nor_2_out), .D(xor_6_out), .nQ(d_latch_6_nq));  // open: Q
  assign controlled_inverter_6_out = nor_2_out ? ~d_latch_15_nq : 1'bz;  // Controlled_Inverter controlled_inverter_6
  D_latch d_latch_7 (.EN(nor_2_out), .D(xor_7_out), .nQ(d_latch_7_nq));  // open: Q
  assign controlled_inverter_7_out = nor_2_out ? ~d_latch_16_nq : 1'bz;  // Controlled_Inverter controlled_inverter_7
  D_latch d_latch_8 (.EN(nor_2_out), .D(xor_8_out), .nQ(d_latch_8_nq));  // open: Q
  assign controlled_inverter_8_out = nor_2_out ? ~d_latch_17_nq : 1'bz;  // Controlled_Inverter controlled_inverter_8
  nor nor_3 (nor_3_out, nVIS, s_r_ff_1_q);
  nor nor_4 (nor_4_out, PCLK[0], s_r_ff_1_qn);
  assign controlled_inverter_1_out = LOAD ? IN0 : 1'bz;  // Controlled_Buffer controlled_buffer_1
  assign controlled_inverter_1_out = nor_4_out ? d_latch_1_nq : 1'bz;  // Controlled_Buffer controlled_buffer_2
  assign controlled_inverter_2_out = LOAD ? IN1 : 1'bz;  // Controlled_Buffer controlled_buffer_3
  assign controlled_inverter_2_out = nor_4_out ? d_latch_2_nq : 1'bz;  // Controlled_Buffer controlled_buffer_4
  assign controlled_inverter_3_out = LOAD ? IN2 : 1'bz;  // Controlled_Buffer controlled_buffer_5
  assign controlled_inverter_3_out = nor_4_out ? d_latch_3_nq : 1'bz;  // Controlled_Buffer controlled_buffer_6
  assign controlled_inverter_4_out = LOAD ? IN3 : 1'bz;  // Controlled_Buffer controlled_buffer_7
  assign controlled_inverter_4_out = nor_4_out ? d_latch_4_nq : 1'bz;  // Controlled_Buffer controlled_buffer_8
  assign controlled_inverter_5_out = LOAD ? IN4 : 1'bz;  // Controlled_Buffer controlled_buffer_9
  assign controlled_inverter_5_out = nor_4_out ? d_latch_5_nq : 1'bz;  // Controlled_Buffer controlled_buffer_10
  assign controlled_inverter_6_out = LOAD ? IN5 : 1'bz;  // Controlled_Buffer controlled_buffer_11
  assign controlled_inverter_6_out = nor_4_out ? d_latch_6_nq : 1'bz;  // Controlled_Buffer controlled_buffer_12
  assign controlled_inverter_7_out = LOAD ? IN6 : 1'bz;  // Controlled_Buffer controlled_buffer_13
  assign controlled_inverter_7_out = nor_4_out ? d_latch_7_nq : 1'bz;  // Controlled_Buffer controlled_buffer_14
  assign controlled_inverter_8_out = LOAD ? IN7 : 1'bz;  // Controlled_Buffer controlled_buffer_15
  assign controlled_inverter_8_out = nor_4_out ? d_latch_8_nq : 1'bz;  // Controlled_Buffer controlled_buffer_16
  not not_1 (not_1_out, 1'b1);
  not not_2 (not_2_out, nor_6_out);
  not not_3 (not_3_out, nor_7_out);
  not not_4 (not_4_out, nor_8_out);
  not not_5 (not_5_out, nor_9_out);
  nor nor_5 (nor_5_out, d_latch_14_q, d_latch_13_q, d_latch_12_q, d_latch_11_q, d_latch_10_q);
  not not_6 (not_6_out, nor_5_out);
  not not_7 (not_7_out, nor_11_out);
  not not_8 (not_8_out, nor_12_out);
  D_latch d_latch_9 (.EN(PCLK[1]), .D(nor_3_out), .nQ(nX_EN));  // open: Q
  D_latch d_latch_10 (.EN(1'b1), .D(controlled_inverter_1_out), .Q(d_latch_10_q), .nQ(d_latch_10_nq));
  nor nor_6 (nor_6_out, d_latch_10_nq, not_1_out);
  D_latch d_latch_11 (.EN(1'b1), .D(controlled_inverter_2_out), .Q(d_latch_11_q), .nQ(d_latch_11_nq));
  nor nor_7 (nor_7_out, d_latch_11_nq, not_2_out);
  D_latch d_latch_12 (.EN(1'b1), .D(controlled_inverter_3_out), .Q(d_latch_12_q), .nQ(d_latch_12_nq));
  nor nor_8 (nor_8_out, d_latch_12_nq, not_3_out);
  D_latch d_latch_13 (.EN(1'b1), .D(controlled_inverter_4_out), .Q(d_latch_13_q), .nQ(d_latch_13_nq));
  nor nor_9 (nor_9_out, d_latch_13_nq, not_4_out);
  D_latch d_latch_14 (.EN(1'b1), .D(controlled_inverter_5_out), .Q(d_latch_14_q), .nQ(d_latch_14_nq));
  nor nor_10 (nor_10_out, d_latch_14_nq, not_5_out);
  D_latch d_latch_15 (.EN(1'b1), .D(controlled_inverter_6_out), .Q(d_latch_15_q), .nQ(d_latch_15_nq));
  nor nor_11 (nor_11_out, d_latch_15_nq, not_6_out);
  D_latch d_latch_16 (.EN(1'b1), .D(controlled_inverter_7_out), .Q(d_latch_16_q), .nQ(d_latch_16_nq));
  nor nor_12 (nor_12_out, d_latch_16_nq, not_7_out);
  D_latch d_latch_17 (.EN(1'b1), .D(controlled_inverter_8_out), .Q(d_latch_17_q), .nQ(d_latch_17_nq));
  nor nor_13 (nor_13_out, d_latch_17_nq, not_8_out);

  // Notes on the sheet:
  //   PCLK
  //   UPD
  //   STEP
  //   LOAD
  //   /PCLK
  //   CARRY OUT
endmodule

// SELECT PIXEL
module SELECT_2_3_5_7_PIXEL (
  input  [1:0] PCLK,
  input  H0_prime_prime,
  input  H1_prime_prime,
  input  H2_prime_prime,
  input  PAR_O,
  output nSH2,
  output nSH3,
  output nSH5,
  output nSH7
);

  wire decoder_1_out2, decoder_1_out3, decoder_1_out5, decoder_1_out7;

  Decoder #(.select(3), .disabled(0)) decoder_1 (
    .out2(decoder_1_out2), .out3(decoder_1_out3), .out5(decoder_1_out5), .out7(decoder_1_out7),
    .sel({H2_prime_prime, H1_prime_prime, H0_prime_prime}), .en(PAR_O));  // open: out0, out1, out4, out6
  D_latch sh2_latch (.EN(PCLK[1]), .D(decoder_1_out2), .nQ(nSH2));  // open: Q
  D_latch sh3_latch (.EN(PCLK[1]), .D(decoder_1_out3), .nQ(nSH3));  // open: Q
  D_latch sh5_latch (.EN(PCLK[1]), .D(decoder_1_out5), .nQ(nSH5));  // open: Q
  D_latch sh7_latch (.EN(PCLK[1]), .D(decoder_1_out7), .nQ(nSH7));  // open: Q

  // Notes on the sheet:
  //   /PCLK
  //   SPR Load FLAG (ATTRIBUTE)
  //   SPR Load X POSITION
  //   SPR Load Low Tile Byte
  //   SPR Load High Tile Byte
endmodule

// H INVERSION
module H_INVERSION (
  input  [1:0] PCLK,
  input  nSH2,
  input  OB6,
  input  _0_FIFO,
  input  PD0,
  input  PD1,
  input  PD2,
  input  PD3,
  input  PD4,
  input  PD5,
  input  PD6,
  input  PD7,
  output nT0,
  output nT1,
  output nT2,
  output nT3,
  output nT4,
  output nT5,
  output nT6,
  output nT7
);

  wire d_ff_1_q, d_latch_1_q, d_latch_2_q, d_latch_3_q, d_latch_4_q, d_latch_5_q, d_latch_6_q, d_latch_7_q,
       d_latch_8_q, multiplexer_1_out, multiplexer_2_out, multiplexer_3_out, multiplexer_4_out,
       multiplexer_5_out, multiplexer_6_out, multiplexer_7_out, multiplexer_8_out, nor_1_out;

  nor nor_1 (nor_1_out, PCLK[1], nSH2);
  D_Flip_Flop #(.trigger("low")) d_ff_1 (.clk(nor_1_out), .D(OB6), .Q(d_ff_1_q));  // open: Qn, preset, en, reset
  Multiplexer #(.disabled(0), .enable("false")) multiplexer_1 (
    .in0(PD0), .in1(PD7), .out(multiplexer_1_out), .sel(d_ff_1_q));
  Multiplexer #(.disabled(0), .enable("false")) multiplexer_2 (
    .in0(PD1), .in1(PD6), .out(multiplexer_2_out), .sel(d_ff_1_q));
  Multiplexer #(.disabled(0), .enable("false")) multiplexer_3 (
    .in0(PD2), .in1(PD5), .out(multiplexer_3_out), .sel(d_ff_1_q));
  Multiplexer #(.disabled(0), .enable("false")) multiplexer_4 (
    .in0(PD3), .in1(PD4), .out(multiplexer_4_out), .sel(d_ff_1_q));
  Multiplexer #(.disabled(0), .enable("false")) multiplexer_5 (
    .in0(PD4), .in1(PD3), .out(multiplexer_5_out), .sel(d_ff_1_q));
  Multiplexer #(.disabled(0), .enable("false")) multiplexer_6 (
    .in0(PD5), .in1(PD2), .out(multiplexer_6_out), .sel(d_ff_1_q));
  Multiplexer #(.disabled(0), .enable("false")) multiplexer_7 (
    .in0(PD6), .in1(PD1), .out(multiplexer_7_out), .sel(d_ff_1_q));
  Multiplexer #(.disabled(0), .enable("false")) multiplexer_8 (
    .in0(PD7), .in1(PD0), .out(multiplexer_8_out), .sel(d_ff_1_q));
  D_latch d_latch_1 (.EN(PCLK[1]), .D(multiplexer_1_out), .Q(d_latch_1_q));  // open: nQ
  D_latch d_latch_2 (.EN(PCLK[1]), .D(multiplexer_2_out), .Q(d_latch_2_q));  // open: nQ
  D_latch d_latch_3 (.EN(PCLK[1]), .D(multiplexer_3_out), .Q(d_latch_3_q));  // open: nQ
  D_latch d_latch_4 (.EN(PCLK[1]), .D(multiplexer_4_out), .Q(d_latch_4_q));  // open: nQ
  D_latch d_latch_5 (.EN(PCLK[1]), .D(multiplexer_5_out), .Q(d_latch_5_q));  // open: nQ
  D_latch d_latch_6 (.EN(PCLK[1]), .D(multiplexer_6_out), .Q(d_latch_6_q));  // open: nQ
  D_latch d_latch_7 (.EN(PCLK[1]), .D(multiplexer_7_out), .Q(d_latch_7_q));  // open: nQ
  D_latch d_latch_8 (.EN(PCLK[1]), .D(multiplexer_8_out), .Q(d_latch_8_q));  // open: nQ
  nand nand_1 (nT0, _0_FIFO, d_latch_1_q);
  nand nand_2 (nT1, _0_FIFO, d_latch_2_q);
  nand nand_3 (nT2, _0_FIFO, d_latch_3_q);
  nand nand_4 (nT3, _0_FIFO, d_latch_4_q);
  nand nand_5 (nT4, _0_FIFO, d_latch_5_q);
  nand nand_6 (nT5, _0_FIFO, d_latch_6_q);
  nand nand_7 (nT6, _0_FIFO, d_latch_7_q);
  nand nand_8 (nT7, _0_FIFO, d_latch_8_q);

  // Notes on the sheet:
  //   /PCLK
  //   HINV
endmodule

module VRAM_BUS_CONTROL (
  input  [1:0] PCLK,
  input  nR7,
  input  nDBE,
  input  nW7,
  input  BLNK,
  input  H0_prime,
  input  nPA8,
  input  nPA9,
  input  nPA10,
  input  nPA11,
  input  nPA12,
  input  nPA13,
  output TSTEP,
  output PD_RB,
  output DB_PAR,
  output nALE,
  output RD,
  output WR,
  output XRB,
  output TH_MUX
);

  wire and_1_out, d_ff_1_qn, d_ff_2_qn, d_latch_1_nq, d_latch_2_nq, d_latch_3_nq, d_latch_4_nq, d_latch_4_q,
       d_latch_5_nq, d_latch_6_nq, d_latch_7_nq, d_latch_7_q, d_latch_8_nq, d_latch_8_q, d_latch_9_q,
       d_latch_10_q, d_latch_11_q, nand_1_out, nor_1_out, nor_2_out, nor_4_out, nor_5_out, nor_7_out,
       nor_9_out, nor_10_out, nor_12_out, nor_14_out, not_1_out, not_2_out, not_3_out, not_4_out, s_r_ff_1_q,
       s_r_ff_2_q;

  nor nor_1 (nor_1_out, nR7, nDBE);
  nor nor_2 (nor_2_out, nDBE, nW7);
  nor nor_3 (TH_MUX, d_latch_1_nq, nPA8, nPA9, nPA10, nPA11, nPA12, nPA13);
  S_R_Flip_Flop #(.trigger("high")) s_r_ff_1 (
    .Q(s_r_ff_1_q), .preset(d_latch_6_nq), .reset(nor_1_out));  // open: S, clk, R, Qn, en
  S_R_Flip_Flop #(.trigger("high")) s_r_ff_2 (
    .Q(s_r_ff_2_q), .preset(d_latch_7_nq), .reset(nor_2_out));  // open: S, clk, R, Qn, en
  nor nor_4 (nor_4_out, s_r_ff_1_q, nor_1_out);
  nor nor_5 (nor_5_out, s_r_ff_2_q, nor_2_out);
  D_Flip_Flop #(.trigger("high")) d_ff_1 (.clk(PCLK[0]), .D(nor_4_out), .Qn(d_ff_1_qn));  // open: Q, preset, en, reset
  D_Flip_Flop #(.trigger("high")) d_ff_2 (.clk(PCLK[0]), .D(nor_5_out), .Qn(d_ff_2_qn));  // open: Q, preset, en, reset
  D_latch d_latch_1 (.EN(PCLK[0]), .D(BLNK), .nQ(d_latch_1_nq));  // open: Q
  D_latch d_latch_2 (.EN(PCLK[1]), .D(d_ff_1_qn), .nQ(d_latch_2_nq));  // open: Q
  D_latch d_latch_3 (.EN(PCLK[1]), .D(d_ff_2_qn), .nQ(d_latch_3_nq));  // open: Q
  D_latch d_latch_4 (.EN(PCLK[0]), .D(d_latch_2_nq), .Q(d_latch_4_q), .nQ(d_latch_4_nq));
  D_latch d_latch_5 (.EN(PCLK[0]), .D(d_latch_3_nq), .nQ(d_latch_5_nq));  // open: Q
  D_latch d_latch_6 (.EN(PCLK[1]), .D(d_latch_4_nq), .nQ(d_latch_6_nq));  // open: Q
  D_latch d_latch_7 (.EN(PCLK[1]), .D(d_latch_5_nq), .Q(d_latch_7_q), .nQ(d_latch_7_nq));
  D_latch d_latch_8 (.EN(PCLK[0]), .D(d_latch_6_nq), .Q(d_latch_8_q), .nQ(d_latch_8_nq));
  D_latch d_latch_9 (.EN(PCLK[0]), .D(d_latch_7_nq), .Q(d_latch_9_q));  // open: nQ
  D_latch d_latch_10 (.EN(PCLK[0]), .D(H0_prime), .Q(d_latch_10_q));  // open: nQ
  nor nor_6 (PD_RB, d_latch_4_q, d_latch_8_nq);
  nor nor_7 (nor_7_out, d_latch_8_q, d_latch_4_nq);
  nor nor_8 (DB_PAR, d_latch_3_nq, d_latch_7_q);
  nor nor_9 (nor_9_out, d_latch_9_q, d_latch_5_nq);
  nor nor_10 (nor_10_out, PCLK[1], H0_prime, BLNK);
  not not_1 (not_1_out, BLNK);
  nor nor_11 (nALE, nor_7_out, nor_9_out, nor_10_out);
  nand nand_1 (nand_1_out, not_1_out, d_latch_10_q);
  D_latch d_latch_11 (.EN(PCLK[0]), .D(DB_PAR), .Q(d_latch_11_q));  // open: nQ
  nor nor_12 (nor_12_out, d_latch_11_q, PD_RB);
  not not_2 (not_2_out, PD_RB);
  and and_1 (and_1_out, not_2_out, nand_1_out);
  not not_3 (not_3_out, DB_PAR);
  nor nor_13 (WR, not_3_out, TH_MUX);
  not not_4 (not_4_out, nor_1_out);
  nor nor_14 (nor_14_out, not_4_out, TH_MUX);
  not not_5 (TSTEP, nor_12_out);
  not not_6 (RD, and_1_out);
  not not_7 (XRB, nor_14_out);

  // Notes on the sheet:
  //   R7_EN
  //   W7_EN
  //   PCLK
  //   /PCLK
  //   /PCLK
  //   /PCLK
  //   PCLK
  //   PCLK
  //   /PCLK
  //   /PCLK
  //   H0'
  //   PCLK
  //   PCLK
  //   H0'
  //   BLNK
  //   H0''
  //   PD/RB
  //   DB/PAR
  //   /ALE
endmodule

module READ__2007 (
  input  XRB,
  input  RC,
  input  PD_RB,
  input  PD0,
  input  PD1,
  input  PD2,
  input  PD3,
  input  PD4,
  input  PD5,
  input  PD6,
  input  PD7,
  output DB0,
  output DB1,
  output DB2,
  output DB3,
  output DB4,
  output DB5,
  output DB6,
  output DB7
);

  wire d_ff_1_q, d_ff_2_q, d_ff_3_q, d_ff_4_q, d_ff_5_q, d_ff_6_q, d_ff_7_q, d_ff_8_q, not_1_out;

  not not_1 (not_1_out, XRB);
  D_Flip_Flop #(.trigger("high")) d_ff_1 (.clk(PD_RB), .D(PD0), .Q(d_ff_1_q), .reset(RC));  // open: Qn, preset, en
  D_Flip_Flop #(.trigger("high")) d_ff_2 (.clk(PD_RB), .D(PD1), .Q(d_ff_2_q), .reset(RC));  // open: Qn, preset, en
  D_Flip_Flop #(.trigger("high")) d_ff_3 (.clk(PD_RB), .D(PD2), .Q(d_ff_3_q), .reset(RC));  // open: Qn, preset, en
  D_Flip_Flop #(.trigger("high")) d_ff_4 (.clk(PD_RB), .D(PD3), .Q(d_ff_4_q), .reset(RC));  // open: Qn, preset, en
  D_Flip_Flop #(.trigger("high")) d_ff_5 (.clk(PD_RB), .D(PD4), .Q(d_ff_5_q), .reset(RC));  // open: Qn, preset, en
  D_Flip_Flop #(.trigger("high")) d_ff_6 (.clk(PD_RB), .D(PD5), .Q(d_ff_6_q), .reset(RC));  // open: Qn, preset, en
  D_Flip_Flop #(.trigger("high")) d_ff_7 (.clk(PD_RB), .D(PD6), .Q(d_ff_7_q), .reset(RC));  // open: Qn, preset, en
  D_Flip_Flop #(.trigger("high")) d_ff_8 (.clk(PD_RB), .D(PD7), .Q(d_ff_8_q), .reset(RC));  // open: Qn, preset, en
  Multiplexer multiplexer_1 (.in0(1'b0), .in1(1'b1), .out(DB0), .sel(d_ff_1_q), .en(not_1_out));
  Multiplexer multiplexer_2 (.in0(1'b0), .in1(1'b1), .out(DB1), .sel(d_ff_2_q), .en(not_1_out));
  Multiplexer multiplexer_3 (.in0(1'b0), .in1(1'b1), .out(DB2), .sel(d_ff_3_q), .en(not_1_out));
  Multiplexer multiplexer_4 (.in0(1'b0), .in1(1'b1), .out(DB3), .sel(d_ff_4_q), .en(not_1_out));
  Multiplexer multiplexer_5 (.in0(1'b0), .in1(1'b1), .out(DB4), .sel(d_ff_5_q), .en(not_1_out));
  Multiplexer multiplexer_6 (.in0(1'b0), .in1(1'b1), .out(DB5), .sel(d_ff_6_q), .en(not_1_out));
  Multiplexer multiplexer_7 (.in0(1'b0), .in1(1'b1), .out(DB6), .sel(d_ff_7_q), .en(not_1_out));
  Multiplexer multiplexer_8 (.in0(1'b0), .in1(1'b1), .out(DB7), .sel(d_ff_8_q), .en(not_1_out));
endmodule

// PICTURE ADDRESS GEN
module PICTURE_ADDRESS_GEN (
  input  nH2_prime,
  input  F_AT,
  input  DB_PAR,
  input  nF_NT,
  input  PAR_O,
  input  nSH2,
  input  O8_16,
  input  OBSEL,
  input  BGSEL,
  input  nH1_prime,
  input  [1:0] PCLK,
  input  SC_CNT,
  input  RESCL,
  input  E_EV,
  input  TSTEP,
  input  F_TB,
  input  H0_prime_prime,
  input  BLNK,
  input  l1_32,
  input  PD0,
  input  PD1,
  input  PD2,
  input  PD3,
  input  PD4,
  input  PD5,
  input  PD6,
  input  PD7,
  input  OB0,
  input  OB1,
  input  OB2,
  input  OB3,
  input  OB4,
  input  OB5,
  input  OB6,
  input  OB7,
  input  OV0,
  input  OV1,
  input  OV2,
  input  OV3,
  input  DB0,
  input  DB1,
  input  DB2,
  input  DB3,
  input  DB4,
  input  DB5,
  input  DB6,
  input  DB7,
  input  nW0,
  input  nW5_2,
  input  nW6_1,
  input  nW5_1,
  input  nW6_2,
  input  nDBE,
  input  RC,
  output THO0,
  output THO1,
  output THO2,
  output THO3,
  output THO4,
  output TVO1,
  output nPA0,
  output nPA1,
  output nPA2,
  output nPA3,
  output nPA4,
  output nPA5,
  output nPA6,
  output nPA7,
  output nPA8,
  output nPA9,
  output FH0,
  output nPA10,
  output FH1,
  output nPA11,
  output FH2,
  output nPA12,
  output nPA13
);

  wire _3_2_out, _3_out, _6_out, _11_out, _14_out, and_1_out, and_2_out, controlled_buffer_1_out,
       controlled_buffer_2_out, controlled_buffer_3_out, controlled_buffer_4_out, controlled_buffer_6_out,
       controlled_buffer_8_out, controlled_buffer_10_out, controlled_buffer_12_out, controlled_buffer_14_out,
       controlled_buffer_16_out, controlled_buffer_18_out, controlled_buffer_20_out,
       controlled_buffer_22_out, controlled_buffer_24_out, controlled_buffer_26_out,
       controlled_buffer_28_out, controlled_buffer_30_out, controlled_buffer_32_out, d_ff_4_qn, d_ff_5_q,
       d_ff_6_q, d_ff_7_q, d_ff_8_q, d_ff_9_q, d_ff_10_q, d_ff_11_q, d_ff_12_q, d_ff_13_q, d_ff_14_q,
       d_ff_15_q, d_ff_16_q, d_ff_17_q, d_ff_18_q, d_ff_19_q, d_latch_1_q, d_latch_2_nq, d_latch_3_nq,
       d_latch_4_nq, d_latch_5_q, d_latch_6_q, d_latch_7_q, d_latch_8_nq, d_latch_9_nq, d_latch_10_nq,
       d_latch_11_nq, d_latch_12_nq, d_latch_13_nq, d_latch_14_nq, d_latch_15_nq, d_latch_16_nq,
       d_latch_17_nq, d_latch_18_nq, d_latch_19_nq, d_latch_20_nq, d_latch_21_nq, DBE, multiplexer_1_out,
       multiplexer_2_out, multiplexer_3_out, multiplexer_4_out, multiplexer_5_out, multiplexer_6_out,
       multiplexer_7_out, multiplexer_8_out, multiplexer_9_out, multiplexer_10_out, multiplexer_11_out,
       multiplexer_12_out, multiplexer_13_out, multiplexer_14_out, multiplexer_15_out, multiplexer_16_out,
       multiplexer_17_out, multiplexer_18_out, multiplexer_19_out, multiplexer_20_out, multiplexer_21_out,
       multiplexer_22_out, multiplexer_23_out, multiplexer_24_out, multiplexer_25_out, multiplexer_26_out,
       multiplexer_27_out, multiplexer_28_out, multiplexer_29_out, multiplexer_30_out, multiplexer_31_out,
       multiplexer_32_out, nand_1_out, nor_6_out, nor_7_out, nor_10_out, nor_11_out, nor_12_out, nor_13_out,
       nor_14_out, nor_15_out, nor_16_out, nor_17_out, not_2_out, not_3_out, not_4_out, not_5_out, not_6_out,
       not_7_out, not_8_out, not_9_out, nW0_prime, nW5_1_prime, nW5_2_prime, nW6_1_prime, nW6_2_prime,
       par_1bit_counter_1_carry_out, par_1bit_counter_1_q, par_1bit_counter_2_carry_out,
       par_1bit_counter_2_q, par_3bit_counter_1_fvz, par_3bit_counter_1_q0, par_3bit_counter_1_q1,
       par_3bit_counter_1_q2, par_5bit_counter_1_nq1, par_5bit_counter_1_txz, par_5bit_counter_1_txzb,
       par_5bit_counter_2_nq1, par_5bit_counter_2_q0, par_5bit_counter_2_q2, par_5bit_counter_2_q3,
       par_5bit_counter_2_q4, par_5bit_counter_2_txz, par_5bit_counter_2_txzb, pattern_readout_1_pad0,
       pattern_readout_1_pad1, pattern_readout_1_pad2, pattern_readout_1_pad3, pattern_readout_1_pad4,
       pattern_readout_1_pad5, pattern_readout_1_pad6, pattern_readout_1_pad7, pattern_readout_1_pad8,
       pattern_readout_1_pad9, pattern_readout_1_pad10, pattern_readout_1_pad11, pattern_readout_1_pad12,
       s_r_ff_1_q, THLOAD, THSTEP, TVLOAD, TVSTEP;
  wire [2:0] par_3bit_counter_1_nq0;

  and and_1 (and_1_out, F_TB, H0_prime_prime);
  nor nor_1 (nW0_prime, nW0, nDBE);
  nor nor_2 (nW5_2_prime, nW5_2, nDBE);
  nor nor_3 (nW6_1_prime, nW6_1, nDBE);
  nor nor_4 (nW5_1_prime, nW5_1, nDBE);
  nor nor_5 (nW6_2_prime, nW6_2, nDBE);
  not not_1 (DBE, nDBE);
  assign controlled_buffer_1_out = nW5_1_prime ? DB0 : 1'bz;  // Controlled_Buffer controlled_buffer_1
  assign controlled_buffer_2_out = nW5_1_prime ? DB1 : 1'bz;  // Controlled_Buffer controlled_buffer_2
  assign controlled_buffer_3_out = nW5_1_prime ? DB2 : 1'bz;  // Controlled_Buffer controlled_buffer_3
  D_latch d_latch_1 (.EN(PCLK[0]), .D(SC_CNT), .Q(d_latch_1_q));  // open: nQ
  D_latch d_latch_2 (.EN(PCLK[1]), .D(E_EV), .nQ(d_latch_2_nq));  // open: Q
  nor nor_6 (nor_6_out, E_EV, TSTEP);
  nor nor_7 (nor_7_out, TSTEP, and_1_out);
  D_Flip_Flop #(.trigger("high")) d_ff_1 (
    .clk(DBE), .D(controlled_buffer_1_out), .Q(FH0), .reset(RC));  // open: Qn, preset, en
  D_Flip_Flop #(.trigger("high")) d_ff_2 (
    .clk(DBE), .D(controlled_buffer_2_out), .Q(FH1), .reset(RC));  // open: Qn, preset, en
  D_Flip_Flop #(.trigger("high")) d_ff_3 (
    .clk(DBE), .D(controlled_buffer_3_out), .Q(FH2), .reset(RC));  // open: Qn, preset, en
  and _3 (_3_out, d_latch_1_q, RESCL);
  D_latch d_latch_3 (.EN(PCLK[0]), .D(d_latch_2_nq), .nQ(d_latch_3_nq));  // open: Q
  nor nor_8 (TVSTEP, nor_6_out, PCLK[0]);
  nor nor_9 (THSTEP, PCLK[0], nor_7_out);
  and _6 (_6_out, PCLK[1], d_latch_7_q);
  S_R_Flip_Flop s_r_ff_1 (.Q(s_r_ff_1_q), .preset(nW6_2_prime), .reset(_6_out));  // open: S, clk, R, Qn, en
  nor _11 (_11_out, s_r_ff_1_q, nW6_2_prime);
  assign controlled_buffer_4_out = nW6_2_prime ? DB0 : 1'bz;  // Controlled_Buffer controlled_buffer_4
  assign controlled_buffer_4_out = nW5_1_prime ? DB3 : 1'bz;  // Controlled_Buffer controlled_buffer_5
  assign controlled_buffer_6_out = nW6_2_prime ? DB1 : 1'bz;  // Controlled_Buffer controlled_buffer_6
  assign controlled_buffer_6_out = nW5_1_prime ? DB4 : 1'bz;  // Controlled_Buffer controlled_buffer_7
  assign controlled_buffer_8_out = nW6_2_prime ? DB2 : 1'bz;  // Controlled_Buffer controlled_buffer_8
  assign controlled_buffer_8_out = nW5_1_prime ? DB5 : 1'bz;  // Controlled_Buffer controlled_buffer_9
  assign controlled_buffer_10_out = nW6_2_prime ? DB3 : 1'bz;  // Controlled_Buffer controlled_buffer_10
  assign controlled_buffer_10_out = nW5_1_prime ? DB6 : 1'bz;  // Controlled_Buffer controlled_buffer_11
  assign controlled_buffer_12_out = nW6_2_prime ? DB4 : 1'bz;  // Controlled_Buffer controlled_buffer_12
  assign controlled_buffer_12_out = nW5_1_prime ? DB7 : 1'bz;  // Controlled_Buffer controlled_buffer_13
  and and_2 (and_2_out, l1_32, BLNK);
  assign controlled_buffer_14_out = nW6_2_prime ? DB5 : 1'bz;  // Controlled_Buffer controlled_buffer_14
  assign controlled_buffer_14_out = nW5_2_prime ? DB3 : 1'bz;  // Controlled_Buffer controlled_buffer_15
  assign controlled_buffer_16_out = nW6_2_prime ? DB6 : 1'bz;  // Controlled_Buffer controlled_buffer_16
  assign controlled_buffer_16_out = nW5_2_prime ? DB4 : 1'bz;  // Controlled_Buffer controlled_buffer_17
  assign controlled_buffer_18_out = nW6_2_prime ? DB7 : 1'bz;  // Controlled_Buffer controlled_buffer_18
  assign controlled_buffer_18_out = nW5_2_prime ? DB5 : 1'bz;  // Controlled_Buffer controlled_buffer_19
  assign controlled_buffer_20_out = nW6_1_prime ? DB0 : 1'bz;  // Controlled_Buffer controlled_buffer_20
  assign controlled_buffer_20_out = nW5_2_prime ? DB6 : 1'bz;  // Controlled_Buffer controlled_buffer_21
  assign controlled_buffer_22_out = nW6_1_prime ? DB1 : 1'bz;  // Controlled_Buffer controlled_buffer_22
  assign controlled_buffer_22_out = nW5_2_prime ? DB7 : 1'bz;  // Controlled_Buffer controlled_buffer_23
  not not_2 (not_2_out, TVSTEP);
  D_latch d_latch_4 (.EN(PCLK[0]), .D(par_5bit_counter_2_txz), .nQ(d_latch_4_nq));  // open: Q
  assign controlled_buffer_24_out = nW6_1_prime ? DB2 : 1'bz;  // Controlled_Buffer controlled_buffer_24
  assign controlled_buffer_24_out = nW0_prime ? DB0 : 1'bz;  // Controlled_Buffer controlled_buffer_25
  assign controlled_buffer_26_out = nW6_1_prime ? DB3 : 1'bz;  // Controlled_Buffer controlled_buffer_26
  assign controlled_buffer_26_out = nW0_prime ? DB1 : 1'bz;  // Controlled_Buffer controlled_buffer_27
  assign controlled_buffer_28_out = nW6_1_prime ? DB4 : 1'bz;  // Controlled_Buffer controlled_buffer_28
  assign controlled_buffer_28_out = nW5_2_prime ? DB0 : 1'bz;  // Controlled_Buffer controlled_buffer_29
  assign controlled_buffer_30_out = nW6_1_prime ? DB5 : 1'bz;  // Controlled_Buffer controlled_buffer_30
  assign controlled_buffer_30_out = nW5_2_prime ? DB1 : 1'bz;  // Controlled_Buffer controlled_buffer_31
  assign controlled_buffer_32_out = nW6_1_prime ? 1'b0 : 1'bz;  // Controlled_Buffer controlled_buffer_32
  assign controlled_buffer_32_out = nW5_2_prime ? DB2 : 1'bz;  // Controlled_Buffer controlled_buffer_33
  D_Flip_Flop #(.trigger("high")) d_ff_4 (.clk(PCLK[1]), .D(_11_out), .Qn(d_ff_4_qn));  // open: Q, preset, en, reset
  D_latch d_latch_5 (.EN(PCLK[1]), .D(not_2_out), .Q(d_latch_5_q));  // open: nQ
  D_latch d_latch_6 (.EN(PCLK[1]), .D(d_latch_4_nq), .Q(d_latch_6_q));  // open: nQ
  D_latch d_latch_7 (.EN(PCLK[0]), .D(d_ff_4_qn), .Q(d_latch_7_q));  // open: nQ
  D_Flip_Flop #(.trigger("high")) d_ff_5 (
    .clk(DBE), .D(controlled_buffer_4_out), .Q(d_ff_5_q), .reset(RC));  // open: Qn, preset, en
  D_Flip_Flop #(.trigger("high")) d_ff_6 (
    .clk(DBE), .D(controlled_buffer_6_out), .Q(d_ff_6_q), .reset(RC));  // open: Qn, preset, en
  D_Flip_Flop #(.trigger("high")) d_ff_7 (
    .clk(DBE), .D(controlled_buffer_8_out), .Q(d_ff_7_q), .reset(RC));  // open: Qn, preset, en
  D_Flip_Flop #(.trigger("high")) d_ff_8 (
    .clk(DBE), .D(controlled_buffer_10_out), .Q(d_ff_8_q), .reset(RC));  // open: Qn, preset, en
  D_Flip_Flop #(.trigger("high")) d_ff_9 (
    .clk(DBE), .D(controlled_buffer_12_out), .Q(d_ff_9_q), .reset(RC));  // open: Qn, preset, en
  nor nor_10 (nor_10_out, par_5bit_counter_1_txzb, and_2_out, par_3bit_counter_1_fvz);
  not not_3 (not_3_out, nor_10_out);
  D_Flip_Flop #(.trigger("high")) d_ff_10 (
    .clk(DBE), .D(controlled_buffer_14_out), .Q(d_ff_10_q), .reset(RC));  // open: Qn, preset, en
  D_Flip_Flop #(.trigger("high")) d_ff_11 (
    .clk(DBE), .D(controlled_buffer_16_out), .Q(d_ff_11_q), .reset(RC));  // open: Qn, preset, en
  D_Flip_Flop #(.trigger("high")) d_ff_12 (
    .clk(DBE), .D(controlled_buffer_18_out), .Q(d_ff_12_q), .reset(RC));  // open: Qn, preset, en
  D_Flip_Flop #(.trigger("high")) d_ff_13 (
    .clk(DBE), .D(controlled_buffer_20_out), .Q(d_ff_13_q), .reset(RC));  // open: Qn, preset, en
  D_Flip_Flop #(.trigger("high")) d_ff_14 (
    .clk(DBE), .D(controlled_buffer_22_out), .Q(d_ff_14_q), .reset(RC));  // open: Qn, preset, en
  nor nor_11 (nor_11_out, d_latch_5_q, d_latch_6_q);
  D_Flip_Flop #(.trigger("high")) d_ff_15 (
    .clk(DBE), .D(controlled_buffer_24_out), .Q(d_ff_15_q), .reset(RC));  // open: Qn, preset, en
  D_Flip_Flop #(.trigger("high")) d_ff_16 (
    .clk(DBE), .D(controlled_buffer_26_out), .Q(d_ff_16_q), .reset(RC));  // open: Qn, preset, en
  D_Flip_Flop #(.trigger("high")) d_ff_17 (
    .clk(DBE), .D(controlled_buffer_28_out), .Q(d_ff_17_q), .reset(RC));  // open: Qn, preset, en
  D_Flip_Flop #(.trigger("high")) d_ff_18 (
    .clk(DBE), .D(controlled_buffer_30_out), .Q(d_ff_18_q), .reset(RC));  // open: Qn, preset, en
  D_Flip_Flop #(.trigger("high")) d_ff_19 (
    .clk(DBE), .D(controlled_buffer_32_out), .Q(d_ff_19_q), .reset(RC));  // open: Qn, preset, en
  nor _3_2 (_3_2_out, _3_out, d_latch_7_q);
  nor _14 (_14_out, d_latch_7_q, d_latch_3_nq);
  not not_4 (not_4_out, PCLK[1]);
  nand nand_1 (nand_1_out, BLNK, l1_32);
  nor _4 (TVLOAD, not_4_out, _3_2_out);
  nor _15 (THLOAD, PCLK[0], _14_out);
  PAR_5BIT_COUNTER par_5bit_counter_1 (
    .IN_NOR7_1(1'b1), .BLNK(BLNK), .STEP(THSTEP), .LOAD(THLOAD), .PCLK(PCLK[0]), .IN0(d_ff_5_q), .RES(1'b0),
    .CARRY_IN(nand_1_out), .IN1(d_ff_6_q), .IN2(d_ff_7_q), .IN3(d_ff_8_q), .IN4(d_ff_9_q),
    .TxZ(par_5bit_counter_1_txz), .TxZB(par_5bit_counter_1_txzb), .CFG(par_5bit_counter_1_nq1), .Q0(THO0),
    .Q1(THO1), .nQ1(par_5bit_counter_1_nq1), .Q2(THO2), .Q3(THO3), .Q4(THO4));
  PAR_5BIT_COUNTER par_5bit_counter_2 (
    .IN_NOR7_1(not_3_out), .BLNK(BLNK), .STEP(TVSTEP), .LOAD(TVLOAD), .PCLK(PCLK[0]), .IN0(d_ff_10_q),
    .RES(nor_11_out), .CARRY_IN(not_3_out), .IN1(d_ff_11_q), .IN2(d_ff_12_q), .IN3(d_ff_13_q),
    .IN4(d_ff_14_q), .TxZ(par_5bit_counter_2_txz), .TxZB(par_5bit_counter_2_txzb), .CFG(TVO1),
    .Q0(par_5bit_counter_2_q0), .Q1(TVO1), .nQ1(par_5bit_counter_2_nq1), .Q2(par_5bit_counter_2_q2),
    .Q3(par_5bit_counter_2_q3), .Q4(par_5bit_counter_2_q4));
  PAR_1BIT_COUNTER par_1bit_counter_1 (
    .STEP(THSTEP), .LOAD(THLOAD), .PCLK(PCLK[0]), .IN(d_ff_15_q), .CARRY_IN(not_6_out), .BLNK(BLNK),
    .Q(par_1bit_counter_1_q), .CARRY_OUT(par_1bit_counter_1_carry_out));
  PAR_1BIT_COUNTER par_1bit_counter_2 (
    .STEP(TVSTEP), .LOAD(TVLOAD), .PCLK(PCLK[0]), .IN(d_ff_16_q), .CARRY_IN(not_7_out), .BLNK(BLNK),
    .Q(par_1bit_counter_2_q), .CARRY_OUT(par_1bit_counter_2_carry_out));
  PAR_3BIT_COUNTER par_3bit_counter_1 (
    .FVZ_IN(nor_14_out), .BLNK(BLNK), .STEP(TVSTEP), .LOAD(TVLOAD), .PCLK(PCLK[0]), .IN0(d_ff_17_q),
    .CARRY_IN(not_8_out), .IN1(d_ff_18_q), .IN2(d_ff_19_q), .FVZ(par_3bit_counter_1_fvz),
    .Q0(par_3bit_counter_1_q0), .nQ0(par_3bit_counter_1_nq0[0]), .Q1(par_3bit_counter_1_q1),
    .nQ1(par_3bit_counter_1_nq0[1]), .Q2(par_3bit_counter_1_q2), .nQ2(par_3bit_counter_1_nq0[2]));
  nor nor_12 (nor_12_out, par_5bit_counter_1_txz, par_5bit_counter_2_txzb);
  nor nor_13 (nor_13_out, par_5bit_counter_2_txz, par_1bit_counter_1_carry_out);
  nor nor_14 (nor_14_out, par_1bit_counter_2_carry_out, not_5_out);
  nor nor_15 (nor_15_out, par_3bit_counter_1_nq0[0], not_5_out);
  not not_5 (not_5_out, BLNK);
  nor nor_16 (nor_16_out, not_5_out, par_3bit_counter_1_q1);
  not not_6 (not_6_out, nor_12_out);
  not not_7 (not_7_out, nor_13_out);
  not not_8 (not_8_out, nor_14_out);
  not not_9 (not_9_out, nor_16_out);
  nor nor_17 (nor_17_out, nH2_prime, BLNK);
  Multiplexer #(.enable("false")) multiplexer_1 (.in0(THO0), .in1(THO2), .out(multiplexer_1_out), .sel(F_AT));
  Multiplexer #(.enable("false")) multiplexer_2 (.in0(THO1), .in1(THO3), .out(multiplexer_2_out), .sel(F_AT));
  Multiplexer #(.enable("false")) multiplexer_3 (.in0(THO2), .in1(THO4), .out(multiplexer_3_out), .sel(F_AT));
  Multiplexer #(.enable("false")) multiplexer_4 (
    .in0(THO3), .in1(par_5bit_counter_2_q2), .out(multiplexer_4_out), .sel(F_AT));
  Multiplexer #(.enable("false")) multiplexer_5 (
    .in0(THO4), .in1(par_5bit_counter_2_q3), .out(multiplexer_5_out), .sel(F_AT));
  Multiplexer #(.enable("false")) multiplexer_6 (
    .in0(par_5bit_counter_2_q0), .in1(par_5bit_counter_2_q4), .out(multiplexer_6_out), .sel(F_AT));
  Multiplexer #(.enable("false")) multiplexer_7 (.in0(TVO1), .in1(1'b1), .out(multiplexer_7_out), .sel(F_AT));
  Multiplexer #(.enable("false")) multiplexer_8 (
    .in0(par_5bit_counter_2_q2), .in1(1'b1), .out(multiplexer_8_out), .sel(F_AT));
  Multiplexer #(.enable("false")) multiplexer_9 (
    .in0(par_5bit_counter_2_q3), .in1(1'b1), .out(multiplexer_9_out), .sel(F_AT));
  Multiplexer #(.enable("false")) multiplexer_10 (
    .in0(par_5bit_counter_2_q4), .in1(1'b1), .out(multiplexer_10_out), .sel(F_AT));
  Multiplexer #(.enable("false")) multiplexer_11 (
    .in0(multiplexer_1_out), .in1(pattern_readout_1_pad0), .out(multiplexer_11_out), .sel(nor_17_out));
  Multiplexer #(.enable("false")) multiplexer_12 (
    .in0(multiplexer_2_out), .in1(pattern_readout_1_pad1), .out(multiplexer_12_out), .sel(nor_17_out));
  Multiplexer #(.enable("false")) multiplexer_13 (
    .in0(multiplexer_3_out), .in1(pattern_readout_1_pad2), .out(multiplexer_13_out), .sel(nor_17_out));
  Multiplexer #(.enable("false")) multiplexer_14 (
    .in0(multiplexer_4_out), .in1(pattern_readout_1_pad3), .out(multiplexer_14_out), .sel(nor_17_out));
  Multiplexer #(.enable("false")) multiplexer_15 (
    .in0(multiplexer_5_out), .in1(pattern_readout_1_pad4), .out(multiplexer_15_out), .sel(nor_17_out));
  Multiplexer #(.enable("false")) multiplexer_16 (
    .in0(multiplexer_6_out), .in1(pattern_readout_1_pad5), .out(multiplexer_16_out), .sel(nor_17_out));
  Multiplexer #(.enable("false")) multiplexer_17 (
    .in0(multiplexer_7_out), .in1(pattern_readout_1_pad6), .out(multiplexer_17_out), .sel(nor_17_out));
  Multiplexer #(.enable("false")) multiplexer_18 (
    .in0(multiplexer_8_out), .in1(pattern_readout_1_pad7), .out(multiplexer_18_out), .sel(nor_17_out));
  Multiplexer #(.enable("false")) multiplexer_19 (
    .in0(multiplexer_9_out), .in1(pattern_readout_1_pad8), .out(multiplexer_19_out), .sel(nor_17_out));
  Multiplexer #(.enable("false")) multiplexer_20 (
    .in0(multiplexer_10_out), .in1(pattern_readout_1_pad9), .out(multiplexer_20_out), .sel(nor_17_out));
  Multiplexer #(.enable("false")) multiplexer_21 (
    .in0(par_1bit_counter_1_q), .in1(pattern_readout_1_pad10), .out(multiplexer_21_out), .sel(nor_17_out));
  Multiplexer #(.enable("false")) multiplexer_22 (
    .in0(par_1bit_counter_2_q), .in1(pattern_readout_1_pad11), .out(multiplexer_22_out), .sel(nor_17_out));
  Multiplexer #(.enable("false")) multiplexer_23 (
    .in0(nor_15_out), .in1(pattern_readout_1_pad12), .out(multiplexer_23_out), .sel(nor_17_out));
  Multiplexer #(.enable("false")) multiplexer_24 (
    .in0(not_9_out), .in1(1'b0), .out(multiplexer_24_out), .sel(nor_17_out));
  Multiplexer #(.enable("false")) multiplexer_25 (
    .in0(multiplexer_11_out), .in1(DB0), .out(multiplexer_25_out), .sel(DB_PAR));
  Multiplexer #(.enable("false")) multiplexer_26 (
    .in0(multiplexer_12_out), .in1(DB1), .out(multiplexer_26_out), .sel(DB_PAR));
  Multiplexer #(.enable("false")) multiplexer_27 (
    .in0(multiplexer_13_out), .in1(DB2), .out(multiplexer_27_out), .sel(DB_PAR));
  Multiplexer #(.enable("false")) multiplexer_28 (
    .in0(multiplexer_14_out), .in1(DB3), .out(multiplexer_28_out), .sel(DB_PAR));
  Multiplexer #(.enable("false")) multiplexer_29 (
    .in0(multiplexer_15_out), .in1(DB4), .out(multiplexer_29_out), .sel(DB_PAR));
  Multiplexer #(.enable("false")) multiplexer_30 (
    .in0(multiplexer_16_out), .in1(DB5), .out(multiplexer_30_out), .sel(DB_PAR));
  Multiplexer #(.enable("false")) multiplexer_31 (
    .in0(multiplexer_17_out), .in1(DB6), .out(multiplexer_31_out), .sel(DB_PAR));
  Multiplexer #(.enable("false")) multiplexer_32 (
    .in0(multiplexer_18_out), .in1(DB7), .out(multiplexer_32_out), .sel(DB_PAR));
  D_latch d_latch_8 (.EN(1'b1), .D(multiplexer_25_out), .nQ(d_latch_8_nq));  // open: Q
  D_latch d_latch_9 (.EN(1'b1), .D(multiplexer_26_out), .nQ(d_latch_9_nq));  // open: Q
  D_latch d_latch_10 (.EN(1'b1), .D(multiplexer_27_out), .nQ(d_latch_10_nq));  // open: Q
  D_latch d_latch_11 (.EN(1'b1), .D(multiplexer_28_out), .nQ(d_latch_11_nq));  // open: Q
  D_latch d_latch_12 (.EN(1'b1), .D(multiplexer_29_out), .nQ(d_latch_12_nq));  // open: Q
  D_latch d_latch_13 (.EN(1'b1), .D(multiplexer_30_out), .nQ(d_latch_13_nq));  // open: Q
  D_latch d_latch_14 (.EN(1'b1), .D(multiplexer_31_out), .nQ(d_latch_14_nq));  // open: Q
  D_latch d_latch_15 (.EN(1'b1), .D(multiplexer_32_out), .nQ(d_latch_15_nq));  // open: Q
  D_latch d_latch_16 (.EN(1'b1), .D(multiplexer_19_out), .nQ(d_latch_16_nq));  // open: Q
  D_latch d_latch_17 (.EN(1'b1), .D(multiplexer_20_out), .nQ(d_latch_17_nq));  // open: Q
  D_latch d_latch_18 (.EN(1'b1), .D(multiplexer_21_out), .nQ(d_latch_18_nq));  // open: Q
  D_latch d_latch_19 (.EN(1'b1), .D(multiplexer_22_out), .nQ(d_latch_19_nq));  // open: Q
  D_latch d_latch_20 (.EN(1'b1), .D(multiplexer_23_out), .nQ(d_latch_20_nq));  // open: Q
  D_latch d_latch_21 (.EN(1'b1), .D(multiplexer_24_out), .nQ(d_latch_21_nq));  // open: Q
  D_latch d_latch_22 (.EN(PCLK[0]), .D(d_latch_8_nq), .Q(nPA0));  // open: nQ
  D_latch d_latch_23 (.EN(PCLK[0]), .D(d_latch_9_nq), .Q(nPA1));  // open: nQ
  D_latch d_latch_24 (.EN(PCLK[0]), .D(d_latch_10_nq), .Q(nPA2));  // open: nQ
  D_latch d_latch_25 (.EN(PCLK[0]), .D(d_latch_11_nq), .Q(nPA3));  // open: nQ
  D_latch d_latch_26 (.EN(PCLK[0]), .D(d_latch_12_nq), .Q(nPA4));  // open: nQ
  D_latch d_latch_27 (.EN(PCLK[0]), .D(d_latch_13_nq), .Q(nPA5));  // open: nQ
  D_latch d_latch_28 (.EN(PCLK[0]), .D(d_latch_14_nq), .Q(nPA6));  // open: nQ
  D_latch d_latch_29 (.EN(PCLK[0]), .D(d_latch_15_nq), .Q(nPA7));  // open: nQ
  D_latch d_latch_30 (.EN(PCLK[0]), .D(d_latch_16_nq), .Q(nPA8));  // open: nQ
  D_latch d_latch_31 (.EN(PCLK[0]), .D(d_latch_17_nq), .Q(nPA9));  // open: nQ
  D_latch d_latch_32 (.EN(PCLK[0]), .D(d_latch_18_nq), .Q(nPA10));  // open: nQ
  D_latch d_latch_33 (.EN(PCLK[0]), .D(d_latch_19_nq), .Q(nPA11));  // open: nQ
  D_latch d_latch_34 (.EN(PCLK[0]), .D(d_latch_20_nq), .Q(nPA12));  // open: nQ
  D_latch d_latch_35 (.EN(PCLK[0]), .D(d_latch_21_nq), .Q(nPA13));  // open: nQ
  PATTERN_READOUT pattern_readout_1 (
    .PCLK(PCLK), .nH1_prime(nH1_prime), .PAR_O(PAR_O), .nF_NT(nF_NT), .H0_prime_prime(H0_prime_prime),
    .nSH2(nSH2), .nFVO0(par_3bit_counter_1_nq0[0]), .OV0(OV0), .nFVO1(par_3bit_counter_1_nq0[1]), .OV1(OV1),
    .nFVO2(par_3bit_counter_1_nq0[2]), .OV2(OV2), .OV3(OV3), .PD0(PD0), .OB0(OB0), .PD1(PD1), .OB1(OB1),
    .PD2(PD2), .OB2(OB2), .PD3(PD3), .OB3(OB3), .PD4(PD4), .OB4(OB4), .PD5(PD5), .OB5(OB5), .PD6(PD6),
    .OB6(OB6), .PD7(PD7), .OB7(OB7), .OBSEL(OBSEL), .O8_16(O8_16), .BGBSEL(BGSEL),
    .PAD0(pattern_readout_1_pad0), .PAD1(pattern_readout_1_pad1), .PAD2(pattern_readout_1_pad2),
    .PAD3(pattern_readout_1_pad3), .PAD4(pattern_readout_1_pad4), .PAD5(pattern_readout_1_pad5),
    .PAD6(pattern_readout_1_pad6), .PAD7(pattern_readout_1_pad7), .PAD8(pattern_readout_1_pad8),
    .PAD9(pattern_readout_1_pad9), .PAD10(pattern_readout_1_pad10), .PAD11(pattern_readout_1_pad11),
    .PAD12(pattern_readout_1_pad12));

  // Other names for the same wires on the sheet: OBJ_DATA[7:0] = {OB7, OB6, OB5, OB4, OB3, OB2, OB1, OB0};
  //   OV_DATA[3:0] = {OV3, OV2, OV1, OV0}; PCLK_t = PCLK[0]; nPCLK = PCLK[1];
  //   PPU_DATA[7:0] = {PD7, PD6, PD5, PD4, PD3, PD2, PD1, PD0}

  // Notes on the sheet:
  //   2
  //   13
  //   12
  //   E/EV''
  //   /W5/1'
  //   TVZ
  //   /W5/2'
  //   W6/2  LOADER
  //   /W6/2'
  //   /W6/1'
  //   FVZ
  //   /TVZ''
  //   NTH
  //   NTV
  //   TH0
  //   TH1
  //   TH2
  //   TH3
  //   TH4
  //   TV0
  //   TV1
  //   TV2
  //   TV3
  //   TV4
  //   0/TV
  //   FV0
  //   FV1
  //   FV2
  //   THIN
  //   THZB
  //   TVZB
  //   NTHIN
  //   NTVIN
  //   FVIN
  //   PCLK2
  //   THZ
  //   TVIN
  //   TVZ
  //   NTH0
  //   NTV0
  //   /FVO0
  //   /FVO1
  //   /FVO2
  //   THZ
  //   TVZ
  //   /BLNK
  //   /BLNK
  //   F/AT
  //   F/AT
  //   PARR
  //   DB/PAR
endmodule

module PATTERN_READOUT (
  input  [1:0] PCLK,
  input  nH1_prime,
  input  PAR_O,
  input  nF_NT,
  input  H0_prime_prime,
  input  nSH2,
  input  nFVO0,
  input  OV0,
  input  nFVO1,
  input  OV1,
  input  nFVO2,
  input  OV2,
  input  OV3,
  input  PD0,
  input  OB0,
  input  PD1,
  input  OB1,
  input  PD2,
  input  OB2,
  input  PD3,
  input  OB3,
  input  PD4,
  input  OB4,
  input  PD5,
  input  OB5,
  input  PD6,
  input  OB6,
  input  PD7,
  input  OB7,
  input  OBSEL,
  input  O8_16,
  input  BGBSEL,
  output PAD0,
  output PAD1,
  output PAD2,
  output PAD3,
  output PAD4,
  output PAD5,
  output PAD6,
  output PAD7,
  output PAD8,
  output PAD9,
  output PAD10,
  output PAD11,
  output PAD12
);

  wire d_ff_1_qn, d_latch_1_q, d_latch_2_nq, d_latch_3_nq, d_latch_4_nq, d_latch_5_nq, d_latch_6_nq,
       d_latch_7_nq, d_latch_8_nq, d_latch_9_nq, d_latch_10_nq, d_latch_11_nq, d_latch_12_nq, d_latch_13_nq,
       d_latch_14_nq, d_latch_15_nq, d_latch_16_nq, d_latch_17_nq, d_latch_18_nq, d_latch_19_nq,
       d_latch_20_nq, d_latch_21_nq, d_latch_22_nq, d_latch_23_nq, d_latch_24_nq, d_latch_25_nq,
       d_latch_26_nq, d_latch_27_nq, d_latch_28_nq, d_latch_29_nq, d_latch_30_nq, d_latch_31_nq,
       d_latch_32_nq, d_latch_33_nq, d_latch_34_nq, multiplexer_1_out, multiplexer_2_out, multiplexer_3_out,
       multiplexer_4_out, multiplexer_5_out, multiplexer_6_out, multiplexer_7_out, multiplexer_8_out,
       multiplexer_9_out, multiplexer_10_out, multiplexer_11_out, multiplexer_12_out, multiplexer_13_out,
       multiplexer_14_out, nor_1_out, nor_2_out, nor_3_out, not_1_out, not_2_out, not_3_out, not_4_out,
       not_5_out, not_6_out, not_7_out, not_8_out, not_9_out, not_10_out, xnor_1_out, xnor_2_out, xnor_3_out,
       xnor_4_out;

  not not_1 (not_1_out, H0_prime_prime);
  nor nor_1 (nor_1_out, nF_NT, not_1_out);
  not not_2 (not_2_out, nor_1_out);
  not not_3 (not_3_out, PD0);
  not not_4 (not_4_out, PD1);
  not not_5 (not_5_out, PD2);
  not not_6 (not_6_out, PD3);
  not not_7 (not_7_out, PD4);
  not not_8 (not_8_out, PD5);
  not not_9 (not_9_out, PD6);
  not not_10 (not_10_out, PD7);
  D_latch d_latch_1 (.EN(PCLK[1]), .D(not_2_out), .Q(d_latch_1_q));  // open: nQ
  nor nor_2 (nor_2_out, PCLK[1], nSH2);
  nor nor_3 (nor_3_out, PCLK[1], d_latch_1_q);
  D_Flip_Flop #(.trigger("high")) d_ff_1 (
    .clk(PCLK[0]), .D(OB7), .Qn(d_ff_1_qn), .en(nor_2_out));  // open: Q, preset, reset
  D_latch d_latch_2 (.EN(PCLK[1]), .D(OV0), .nQ(d_latch_2_nq));  // open: Q
  D_latch d_latch_3 (.EN(PCLK[1]), .D(OV1), .nQ(d_latch_3_nq));  // open: Q
  D_latch d_latch_4 (.EN(PCLK[1]), .D(OV2), .nQ(d_latch_4_nq));  // open: Q
  D_latch d_latch_5 (.EN(PCLK[1]), .D(OV3), .nQ(d_latch_5_nq));  // open: Q
  D_latch d_latch_6 (.EN(PCLK[1]), .D(not_3_out), .nQ(d_latch_6_nq));  // open: Q
  D_latch d_latch_7 (.EN(PCLK[1]), .D(not_4_out), .nQ(d_latch_7_nq));  // open: Q
  D_latch d_latch_8 (.EN(PCLK[1]), .D(not_5_out), .nQ(d_latch_8_nq));  // open: Q
  D_latch d_latch_9 (.EN(PCLK[1]), .D(not_6_out), .nQ(d_latch_9_nq));  // open: Q
  D_latch d_latch_10 (.EN(PCLK[1]), .D(not_7_out), .nQ(d_latch_10_nq));  // open: Q
  D_latch d_latch_11 (.EN(PCLK[1]), .D(not_8_out), .nQ(d_latch_11_nq));  // open: Q
  D_latch d_latch_12 (.EN(PCLK[1]), .D(not_9_out), .nQ(d_latch_12_nq));  // open: Q
  D_latch d_latch_13 (.EN(PCLK[1]), .D(not_10_out), .nQ(d_latch_13_nq));  // open: Q
  D_latch d_latch_14 (.EN(nor_3_out), .D(d_latch_2_nq), .nQ(d_latch_14_nq));  // open: Q
  D_latch d_latch_15 (.EN(nor_3_out), .D(d_latch_3_nq), .nQ(d_latch_15_nq));  // open: Q
  D_latch d_latch_16 (.EN(nor_3_out), .D(d_latch_4_nq), .nQ(d_latch_16_nq));  // open: Q
  D_latch d_latch_17 (.EN(nor_3_out), .D(d_latch_5_nq), .nQ(d_latch_17_nq));  // open: Q
  D_latch d_latch_18 (.EN(nor_3_out), .D(d_latch_6_nq), .nQ(d_latch_18_nq));  // open: Q
  D_latch d_latch_19 (.EN(nor_3_out), .D(OB0), .nQ(d_latch_19_nq));  // open: Q
  D_latch d_latch_20 (.EN(nor_3_out), .D(d_latch_7_nq), .nQ(d_latch_20_nq));  // open: Q
  D_latch d_latch_21 (.EN(nor_3_out), .D(OB1), .nQ(d_latch_21_nq));  // open: Q
  D_latch d_latch_22 (.EN(nor_3_out), .D(d_latch_8_nq), .nQ(d_latch_22_nq));  // open: Q
  D_latch d_latch_23 (.EN(nor_3_out), .D(OB2), .nQ(d_latch_23_nq));  // open: Q
  D_latch d_latch_24 (.EN(nor_3_out), .D(d_latch_9_nq), .nQ(d_latch_24_nq));  // open: Q
  D_latch d_latch_25 (.EN(nor_3_out), .D(OB3), .nQ(d_latch_25_nq));  // open: Q
  D_latch d_latch_26 (.EN(nor_3_out), .D(d_latch_10_nq), .nQ(d_latch_26_nq));  // open: Q
  D_latch d_latch_27 (.EN(nor_3_out), .D(OB4), .nQ(d_latch_27_nq));  // open: Q
  D_latch d_latch_28 (.EN(nor_3_out), .D(d_latch_11_nq), .nQ(d_latch_28_nq));  // open: Q
  D_latch d_latch_29 (.EN(nor_3_out), .D(OB5), .nQ(d_latch_29_nq));  // open: Q
  D_latch d_latch_30 (.EN(nor_3_out), .D(d_latch_12_nq), .nQ(d_latch_30_nq));  // open: Q
  D_latch d_latch_31 (.EN(nor_3_out), .D(OB6), .nQ(d_latch_31_nq));  // open: Q
  D_latch d_latch_32 (.EN(nor_3_out), .D(d_latch_13_nq), .nQ(d_latch_32_nq));  // open: Q
  D_latch d_latch_33 (.EN(nor_3_out), .D(OB7), .nQ(d_latch_33_nq));  // open: Q
  D_latch d_latch_34 (.EN(nor_3_out), .D(OB0), .nQ(d_latch_34_nq));  // open: Q
  xnor xnor_1 (xnor_1_out, d_ff_1_qn, d_latch_14_nq);
  xnor xnor_2 (xnor_2_out, d_ff_1_qn, d_latch_15_nq);
  xnor xnor_3 (xnor_3_out, d_ff_1_qn, d_latch_16_nq);
  xnor xnor_4 (xnor_4_out, d_ff_1_qn, d_latch_17_nq);
  Multiplexer #(.disabled(0), .enable("false")) multiplexer_1 (
    .in0(d_latch_19_nq), .in1(xnor_4_out), .out(multiplexer_1_out), .sel(O8_16));
  Multiplexer #(.enable("false")) multiplexer_2 (
    .in0(OBSEL), .in1(d_latch_34_nq), .out(multiplexer_2_out), .sel(O8_16));
  Multiplexer #(.enable("false")) multiplexer_3 (.in0(nFVO0), .in1(xnor_1_out), .out(multiplexer_3_out), .sel(PAR_O));
  Multiplexer #(.enable("false")) multiplexer_4 (.in0(nFVO1), .in1(xnor_2_out), .out(multiplexer_4_out), .sel(PAR_O));
  Multiplexer #(.enable("false")) multiplexer_5 (.in0(nFVO2), .in1(xnor_3_out), .out(multiplexer_5_out), .sel(PAR_O));
  Multiplexer #(.enable("false")) multiplexer_6 (
    .in0(d_latch_18_nq), .in1(multiplexer_1_out), .out(multiplexer_6_out), .sel(PAR_O));
  Multiplexer #(.enable("false")) multiplexer_7 (
    .in0(d_latch_20_nq), .in1(d_latch_21_nq), .out(multiplexer_7_out), .sel(PAR_O));
  Multiplexer #(.enable("false")) multiplexer_8 (
    .in0(d_latch_22_nq), .in1(d_latch_23_nq), .out(multiplexer_8_out), .sel(PAR_O));
  Multiplexer #(.enable("false")) multiplexer_9 (
    .in0(d_latch_24_nq), .in1(d_latch_25_nq), .out(multiplexer_9_out), .sel(PAR_O));
  Multiplexer #(.enable("false")) multiplexer_10 (
    .in0(d_latch_26_nq), .in1(d_latch_27_nq), .out(multiplexer_10_out), .sel(PAR_O));
  Multiplexer #(.enable("false")) multiplexer_11 (
    .in0(d_latch_28_nq), .in1(d_latch_29_nq), .out(multiplexer_11_out), .sel(PAR_O));
  Multiplexer #(.enable("false")) multiplexer_12 (
    .in0(d_latch_30_nq), .in1(d_latch_31_nq), .out(multiplexer_12_out), .sel(PAR_O));
  Multiplexer #(.enable("false")) multiplexer_13 (
    .in0(d_latch_32_nq), .in1(d_latch_33_nq), .out(multiplexer_13_out), .sel(PAR_O));
  Multiplexer #(.enable("false")) multiplexer_14 (
    .in0(BGBSEL), .in1(multiplexer_2_out), .out(multiplexer_14_out), .sel(PAR_O));
  D_latch d_latch_35 (.EN(PCLK[1]), .D(multiplexer_3_out), .Q(PAD0));  // open: nQ
  D_latch d_latch_36 (.EN(PCLK[1]), .D(multiplexer_4_out), .Q(PAD1));  // open: nQ
  D_latch d_latch_37 (.EN(PCLK[1]), .D(multiplexer_5_out), .Q(PAD2));  // open: nQ
  not not_11 (PAD3, nH1_prime);
  D_latch d_latch_38 (.EN(PCLK[1]), .D(multiplexer_6_out), .nQ(PAD4));  // open: Q
  D_latch d_latch_39 (.EN(PCLK[1]), .D(multiplexer_7_out), .nQ(PAD5));  // open: Q
  D_latch d_latch_40 (.EN(PCLK[1]), .D(multiplexer_8_out), .nQ(PAD6));  // open: Q
  D_latch d_latch_41 (.EN(PCLK[1]), .D(multiplexer_9_out), .nQ(PAD7));  // open: Q
  D_latch d_latch_42 (.EN(PCLK[1]), .D(multiplexer_10_out), .nQ(PAD8));  // open: Q
  D_latch d_latch_43 (.EN(PCLK[1]), .D(multiplexer_11_out), .nQ(PAD9));  // open: Q
  D_latch d_latch_44 (.EN(PCLK[1]), .D(multiplexer_12_out), .nQ(PAD10));  // open: Q
  D_latch d_latch_45 (.EN(PCLK[1]), .D(multiplexer_13_out), .nQ(PAD11));  // open: Q
  D_latch d_latch_46 (.EN(PCLK[1]), .D(multiplexer_14_out), .nQ(PAD12));  // open: Q

  // Other names for the same wires on the sheet: PCLK_t = PCLK[0]; nPCLK = PCLK[1]

  // Notes on the sheet:
  //   OB0
  //   CHR generator number for OB
  //   regular or double  sprite size
  //   CHR generator number for BG
  //   fetch sprite tile byte
  //   OB7
  //   O
  //   SPRITE
  //   VDIR
  //   OBSEL
  //   V. INVERSION
  //   O8/16
  //   O8/16
  //   PAR/O
  //   BGSEL
  //   PA0 - PA2 - tile line number
  //   A/B  byte string tiles
  //   PA4 - PA11 - tile number in CHR ROM
  //   PA12 - CHR generator number for OB or BG
endmodule
module WRITE__2007 (
  input  [1:0] PCLK,
  input  DB_PAR,
  input  D0,
  input  D1,
  input  D2,
  input  D3,
  input  D4,
  input  D5,
  input  D6,
  input  D7,
  output PD0,
  output PD1,
  output PD2,
  output PD3,
  output PD4,
  output PD5,
  output PD6,
  output PD7
);

  wire d_latch_1_q, d_latch_2_q, d_latch_3_q, d_latch_4_q, d_latch_5_q, d_latch_6_q, d_latch_7_q, d_latch_8_q;

  D_latch d_latch_1 (.EN(PCLK[0]), .D(D0), .Q(d_latch_1_q));  // open: nQ
  D_latch d_latch_2 (.EN(PCLK[0]), .D(D1), .Q(d_latch_2_q));  // open: nQ
  D_latch d_latch_3 (.EN(PCLK[0]), .D(D2), .Q(d_latch_3_q));  // open: nQ
  D_latch d_latch_4 (.EN(PCLK[0]), .D(D3), .Q(d_latch_4_q));  // open: nQ
  D_latch d_latch_5 (.EN(PCLK[0]), .D(D4), .Q(d_latch_5_q));  // open: nQ
  D_latch d_latch_6 (.EN(PCLK[0]), .D(D5), .Q(d_latch_6_q));  // open: nQ
  D_latch d_latch_7 (.EN(PCLK[0]), .D(D6), .Q(d_latch_7_q));  // open: nQ
  D_latch d_latch_8 (.EN(PCLK[0]), .D(D7), .Q(d_latch_8_q));  // open: nQ
  assign PD0 = DB_PAR ? d_latch_1_q : 1'bz;  // Controlled_Buffer controlled_buffer_1
  assign PD1 = DB_PAR ? d_latch_2_q : 1'bz;  // Controlled_Buffer controlled_buffer_2
  assign PD2 = DB_PAR ? d_latch_3_q : 1'bz;  // Controlled_Buffer controlled_buffer_3
  assign PD3 = DB_PAR ? d_latch_4_q : 1'bz;  // Controlled_Buffer controlled_buffer_4
  assign PD4 = DB_PAR ? d_latch_5_q : 1'bz;  // Controlled_Buffer controlled_buffer_5
  assign PD5 = DB_PAR ? d_latch_6_q : 1'bz;  // Controlled_Buffer controlled_buffer_6
  assign PD6 = DB_PAR ? d_latch_7_q : 1'bz;  // Controlled_Buffer controlled_buffer_7
  assign PD7 = DB_PAR ? d_latch_8_q : 1'bz;  // Controlled_Buffer controlled_buffer_8

  // Notes on the sheet:
  //   PCLK
endmodule

module PAR_5BIT_COUNTER (
  input  IN_NOR7_1,
  input  BLNK,
  input  STEP,
  input  LOAD,
  input  CFG,
  input  PCLK,
  input  IN0,
  input  RES,
  input  CARRY_IN,
  input  IN1,
  input  IN2,
  input  IN3,
  input  IN4,
  output TxZ,
  output TxZB,
  output Q0,
  output Q1,
  output nQ1,
  output Q2,
  output Q3,
  output Q4
);

  wire controlled_buffer_1_out, controlled_buffer_2_out, controlled_buffer_3_out, controlled_buffer_4_out,
       controlled_buffer_5_out, d_latch_1_nq, d_latch_2_nq, d_latch_3_nq, d_latch_4_nq, d_latch_5_nq,
       d_latch_6_nq, d_latch_8_nq, d_latch_9_nq, d_latch_10_nq, multiplexer_1_out, multiplexer_2_out,
       multiplexer_3_out, multiplexer_4_out, multiplexer_5_out, nor_1_out, nor_2_out, nor_3_out, nor_4_out,
       nor_5_out, nor_8_out, nor_9_out, nor_10_out, nor_11_out, not_1_out, not_2_out, not_3_out, not_4_out,
       not_5_out, not_6_out;

  nor nor_1 (nor_1_out, d_latch_6_nq, RES);
  nor nor_2 (nor_2_out, nQ1, RES);
  nor nor_3 (nor_3_out, d_latch_8_nq, RES);
  nor nor_4 (nor_4_out, d_latch_9_nq, RES);
  nor nor_5 (nor_5_out, d_latch_10_nq, RES);
  Multiplexer #(.enable("false")) multiplexer_1 (
    .in0(d_latch_6_nq), .in1(nor_1_out), .out(multiplexer_1_out), .sel(CARRY_IN));
  Multiplexer #(.enable("false")) multiplexer_2 (.in0(nQ1), .in1(nor_2_out), .out(multiplexer_2_out), .sel(nor_8_out));
  Multiplexer #(.enable("false")) multiplexer_3 (
    .in0(d_latch_8_nq), .in1(nor_3_out), .out(multiplexer_3_out), .sel(nor_9_out));
  Multiplexer #(.enable("false")) multiplexer_4 (
    .in0(d_latch_9_nq), .in1(nor_4_out), .out(multiplexer_4_out), .sel(nor_10_out));
  Multiplexer #(.enable("false")) multiplexer_5 (
    .in0(d_latch_10_nq), .in1(nor_5_out), .out(multiplexer_5_out), .sel(nor_11_out));
  assign controlled_buffer_1_out = PCLK ? nor_1_out : 1'bz;  // Controlled_Buffer controlled_buffer_1
  assign controlled_buffer_2_out = PCLK ? nor_2_out : 1'bz;  // Controlled_Buffer controlled_buffer_2
  assign controlled_buffer_3_out = PCLK ? nor_3_out : 1'bz;  // Controlled_Buffer controlled_buffer_3
  assign controlled_buffer_4_out = PCLK ? nor_4_out : 1'bz;  // Controlled_Buffer controlled_buffer_4
  assign controlled_buffer_5_out = PCLK ? nor_5_out : 1'bz;  // Controlled_Buffer controlled_buffer_5
  assign controlled_buffer_1_out = LOAD ? IN0 : 1'bz;  // Controlled_Buffer controlled_buffer_6
  D_latch d_latch_1 (.EN(PCLK), .D(multiplexer_1_out), .nQ(d_latch_1_nq));  // open: Q
  assign controlled_buffer_1_out = STEP ? d_latch_1_nq : 1'bz;  // Controlled_Buffer controlled_buffer_7
  assign controlled_buffer_2_out = LOAD ? IN1 : 1'bz;  // Controlled_Buffer controlled_buffer_8
  D_latch d_latch_2 (.EN(PCLK), .D(multiplexer_2_out), .nQ(d_latch_2_nq));  // open: Q
  assign controlled_buffer_2_out = STEP ? d_latch_2_nq : 1'bz;  // Controlled_Buffer controlled_buffer_9
  assign controlled_buffer_3_out = LOAD ? IN2 : 1'bz;  // Controlled_Buffer controlled_buffer_10
  D_latch d_latch_3 (.EN(PCLK), .D(multiplexer_3_out), .nQ(d_latch_3_nq));  // open: Q
  assign controlled_buffer_3_out = STEP ? d_latch_3_nq : 1'bz;  // Controlled_Buffer controlled_buffer_11
  assign controlled_buffer_4_out = LOAD ? IN3 : 1'bz;  // Controlled_Buffer controlled_buffer_12
  D_latch d_latch_4 (.EN(PCLK), .D(multiplexer_4_out), .nQ(d_latch_4_nq));  // open: Q
  assign controlled_buffer_4_out = STEP ? d_latch_4_nq : 1'bz;  // Controlled_Buffer controlled_buffer_13
  assign controlled_buffer_5_out = LOAD ? IN4 : 1'bz;  // Controlled_Buffer controlled_buffer_14
  D_latch d_latch_5 (.EN(PCLK), .D(multiplexer_5_out), .nQ(d_latch_5_nq));  // open: Q
  assign controlled_buffer_5_out = STEP ? d_latch_5_nq : 1'bz;  // Controlled_Buffer controlled_buffer_15
  not not_1 (not_1_out, IN_NOR7_1);
  nor nor_6 (TxZB, d_latch_10_nq, d_latch_9_nq, d_latch_8_nq, not_1_out, nQ1, d_latch_6_nq, not_2_out);
  not not_2 (not_2_out, BLNK);
  nor nor_7 (TxZ, BLNK, d_latch_10_nq, d_latch_9_nq, not_1_out, d_latch_8_nq, CFG, d_latch_6_nq);
  D_latch d_latch_6 (.EN(1'b1), .D(controlled_buffer_1_out), .Q(Q0), .nQ(d_latch_6_nq));
  nor nor_8 (nor_8_out, d_latch_6_nq, not_3_out);
  not not_3 (not_3_out, CARRY_IN);
  D_latch d_latch_7 (.EN(1'b1), .D(controlled_buffer_2_out), .Q(Q1), .nQ(nQ1));
  nor nor_9 (nor_9_out, nQ1, not_4_out);
  not not_4 (not_4_out, nor_8_out);
  D_latch d_latch_8 (.EN(1'b1), .D(controlled_buffer_3_out), .Q(Q2), .nQ(d_latch_8_nq));
  nor nor_10 (nor_10_out, d_latch_8_nq, not_5_out);
  not not_5 (not_5_out, nor_9_out);
  D_latch d_latch_9 (.EN(1'b1), .D(controlled_buffer_4_out), .Q(Q3), .nQ(d_latch_9_nq));
  nor nor_11 (nor_11_out, d_latch_9_nq, not_6_out);
  not not_6 (not_6_out, nor_10_out);
  D_latch d_latch_10 (.EN(1'b1), .D(controlled_buffer_5_out), .Q(Q4), .nQ(d_latch_10_nq));

  // Notes on the sheet:
  //   CARRY CONFIG
endmodule

module PAR_3BIT_COUNTER (
  input  FVZ_IN,
  input  BLNK,
  input  STEP,
  input  LOAD,
  input  PCLK,
  input  IN0,
  input  CARRY_IN,
  input  IN1,
  input  IN2,
  output FVZ,
  output Q0,
  output nQ0,
  output Q1,
  output nQ1,
  output Q2,
  output nQ2
);

  wire controlled_inverter_1_out, controlled_inverter_2_out, controlled_inverter_3_out, d_latch_1_nq,
       d_latch_2_nq, d_latch_3_nq, nor_2_out, nor_3_out, nor_4_out, not_1_out, not_2_out, not_3_out,
       xor_1_out, xor_2_out, xor_3_out;

  xor xor_1 (xor_1_out, CARRY_IN, nQ0);
  xor xor_2 (xor_2_out, nor_2_out, nQ1);
  xor xor_3 (xor_3_out, nor_3_out, nQ2);
  D_latch d_latch_1 (.EN(PCLK), .D(xor_1_out), .nQ(d_latch_1_nq));  // open: Q
  assign controlled_inverter_1_out = PCLK ? ~nQ0 : 1'bz;  // Controlled_Inverter controlled_inverter_1
  D_latch d_latch_2 (.EN(PCLK), .D(xor_2_out), .nQ(d_latch_2_nq));  // open: Q
  assign controlled_inverter_2_out = PCLK ? ~nQ1 : 1'bz;  // Controlled_Inverter controlled_inverter_2
  D_latch d_latch_3 (.EN(PCLK), .D(xor_3_out), .nQ(d_latch_3_nq));  // open: Q
  assign controlled_inverter_3_out = PCLK ? ~nQ2 : 1'bz;  // Controlled_Inverter controlled_inverter_3
  assign controlled_inverter_1_out = LOAD ? IN0 : 1'bz;  // Controlled_Buffer controlled_buffer_1
  assign controlled_inverter_1_out = STEP ? d_latch_1_nq : 1'bz;  // Controlled_Buffer controlled_buffer_2
  assign controlled_inverter_2_out = LOAD ? IN1 : 1'bz;  // Controlled_Buffer controlled_buffer_3
  assign controlled_inverter_2_out = STEP ? d_latch_2_nq : 1'bz;  // Controlled_Buffer controlled_buffer_4
  assign controlled_inverter_3_out = LOAD ? IN2 : 1'bz;  // Controlled_Buffer controlled_buffer_5
  assign controlled_inverter_3_out = STEP ? d_latch_3_nq : 1'bz;  // Controlled_Buffer controlled_buffer_6
  nor nor_1 (FVZ, nQ2, nQ1, nQ0, BLNK, FVZ_IN);
  not not_1 (not_1_out, CARRY_IN);
  not not_2 (not_2_out, nor_2_out);
  not not_3 (not_3_out, nor_3_out);
  D_latch d_latch_4 (.EN(1'b1), .D(controlled_inverter_1_out), .Q(Q0), .nQ(nQ0));
  nor nor_2 (nor_2_out, nQ0, not_1_out);
  D_latch d_latch_5 (.EN(1'b1), .D(controlled_inverter_2_out), .Q(Q1), .nQ(nQ1));
  nor nor_3 (nor_3_out, nQ1, not_2_out);
  D_latch d_latch_6 (.EN(1'b1), .D(controlled_inverter_3_out), .Q(Q2), .nQ(nQ2));
  nor nor_4 (nor_4_out, nQ2, not_3_out);

  // Notes on the sheet:
  //   not used
endmodule

// PAR 1BIT COUNTER
module PAR_1BIT_COUNTER (
  input  STEP,
  input  LOAD,
  input  PCLK,
  input  IN,
  input  CARRY_IN,
  input  BLNK,
  output Q,
  output CARRY_OUT
);

  wire controlled_inverter_1_out, d_latch_1_nq, d_latch_2_nq, not_1_out, not_2_out, xor_1_out;

  xor xor_1 (xor_1_out, CARRY_IN, d_latch_2_nq);
  D_latch d_latch_1 (.EN(PCLK), .D(xor_1_out), .nQ(d_latch_1_nq));  // open: Q
  assign controlled_inverter_1_out = PCLK ? ~d_latch_2_nq : 1'bz;  // Controlled_Inverter controlled_inverter_1
  not not_1 (not_1_out, CARRY_IN);
  not not_2 (not_2_out, BLNK);
  assign controlled_inverter_1_out = LOAD ? IN : 1'bz;  // Controlled_Buffer controlled_buffer_1
  assign controlled_inverter_1_out = STEP ? d_latch_1_nq : 1'bz;  // Controlled_Buffer controlled_buffer_2
  D_latch d_latch_2 (.EN(1'b1), .D(controlled_inverter_1_out), .Q(Q), .nQ(d_latch_2_nq));
  nor nor_1 (CARRY_OUT, d_latch_2_nq, not_1_out, not_2_out);

  // Notes on the sheet:
  //   carry_out
endmodule

// BG COLOR
module BG_COLOR (
  input  [1:0] PCLK,
  input  CLPB,
  input  FH0,
  input  FH1,
  input  FH2,
  input  PD0,
  input  PD1,
  input  PD2,
  input  PD3,
  input  PD4,
  input  PD5,
  input  PD6,
  input  PD7,
  input  THO1,
  input  TVO1,
  input  F_AT,
  input  H0_prime_prime,
  input  F_TA,
  input  F_TB,
  input  nFO,
  output BGC0,
  output BGC1,
  output BGC2,
  output BGC3
);

  wire d_latch_10_nq, d_latch_11_nq, d_latch_12_nq, d_latch_13_nq, d_latch_14_nq, d_latch_15_nq,
       d_latch_16_nq, d_latch_17_nq, d_latch_18_q, d_latch_19_nq, d_latch_20_nq, d_latch_21_nq,
       d_latch_22_nq, d_latch_23_nq, d_latch_24_nq, d_latch_25_nq, d_latch_26_nq, d_latch_27_nq,
       d_latch_28_q, d_latch_29_q, d_latch_30_q, d_latch_31_q, multiplexer_1_out, multiplexer_2_out,
       multiplexer_3_out, multiplexer_4_out, multiplexer_5_out, multiplexer_6_out, nor_1_out, nor_2_out,
       nor_3_out, nor_4_out, nor_5_out, nor_6_out, nor_7_out, not_2_out, not_3_out, not_4_out, not_5_out,
       not_6_out, not_7_out, not_8_out, not_9_out, nPCLK2, shift_reg_load_1_out, shift_reg_load_2_out,
       SHIFT_REGISTER_2_out_0, SHIFT_REGISTER_2_out_1, SHIFT_REGISTER_2_out_2, SHIFT_REGISTER_2_out_3,
       SHIFT_REGISTER_2_out_4, SHIFT_REGISTER_2_out_5, SHIFT_REGISTER_2_out_6, SHIFT_REGISTER_2_out_7,
       SHIFT_REGISTER_3_out_0, SHIFT_REGISTER_3_out_1, SHIFT_REGISTER_3_out_2, SHIFT_REGISTER_3_out_3,
       SHIFT_REGISTER_3_out_4, SHIFT_REGISTER_3_out_5, SHIFT_REGISTER_3_out_6, SHIFT_REGISTER_3_out_7,
       SHIFT_REGISTER_4_out_0, SHIFT_REGISTER_4_out_1, SHIFT_REGISTER_4_out_2, SHIFT_REGISTER_4_out_3,
       SHIFT_REGISTER_4_out_4, SHIFT_REGISTER_4_out_5, SHIFT_REGISTER_4_out_6, SHIFT_REGISTER_4_out_7,
       SHIFT_REGISTER_out_0, SHIFT_REGISTER_out_1, SHIFT_REGISTER_out_2, SHIFT_REGISTER_out_3,
       SHIFT_REGISTER_out_4, SHIFT_REGISTER_out_5, SHIFT_REGISTER_out_6, SHIFT_REGISTER_out_7;
  wire [0:0] d_latch_9_q;
  wire [7:0] d_latch_1_nq;

  not not_1 (nPCLK2, PCLK[0]);
  not not_2 (not_2_out, F_AT);
  not not_3 (not_3_out, H0_prime_prime);
  not not_4 (not_4_out, F_TA);
  not not_5 (not_5_out, F_TB);
  not not_6 (not_6_out, nFO);
  nor nor_1 (nor_1_out, PCLK[0], d_latch_18_q, not_3_out);
  D_latch d_latch_1 (.EN(nor_2_out), .D(PD0), .nQ(d_latch_1_nq[0]));  // open: Q
  D_latch d_latch_2 (.EN(nor_2_out), .D(PD1), .nQ(d_latch_1_nq[1]));  // open: Q
  D_latch d_latch_3 (.EN(nor_2_out), .D(PD2), .nQ(d_latch_1_nq[2]));  // open: Q
  D_latch d_latch_4 (.EN(nor_2_out), .D(PD3), .nQ(d_latch_1_nq[3]));  // open: Q
  D_latch d_latch_5 (.EN(nor_2_out), .D(PD4), .nQ(d_latch_1_nq[4]));  // open: Q
  D_latch d_latch_6 (.EN(nor_2_out), .D(PD5), .nQ(d_latch_1_nq[5]));  // open: Q
  D_latch d_latch_7 (.EN(nor_2_out), .D(PD6), .nQ(d_latch_1_nq[6]));  // open: Q
  D_latch d_latch_8 (.EN(nor_2_out), .D(PD7), .nQ(d_latch_1_nq[7]));  // open: Q
  D_latch d_latch_9 (.EN(PCLK[0]), .D(THO1), .Q(d_latch_9_q[0]));  // open: nQ
  D_latch d_latch_10 (.EN(nor_1_out), .D(PD1), .nQ(d_latch_10_nq));  // open: Q
  D_latch d_latch_11 (.EN(nor_1_out), .D(PD3), .nQ(d_latch_11_nq));  // open: Q
  D_latch d_latch_12 (.EN(nor_1_out), .D(PD5), .nQ(d_latch_12_nq));  // open: Q
  D_latch d_latch_13 (.EN(nor_1_out), .D(PD7), .nQ(d_latch_13_nq));  // open: Q
  D_latch d_latch_14 (.EN(nor_1_out), .D(PD0), .nQ(d_latch_14_nq));  // open: Q
  D_latch d_latch_15 (.EN(nor_1_out), .D(PD2), .nQ(d_latch_15_nq));  // open: Q
  D_latch d_latch_16 (.EN(nor_1_out), .D(PD4), .nQ(d_latch_16_nq));  // open: Q
  D_latch d_latch_17 (.EN(nor_1_out), .D(PD6), .nQ(d_latch_17_nq));  // open: Q
  D_latch d_latch_18 (.EN(PCLK[0]), .D(not_2_out), .Q(d_latch_18_q));  // open: nQ
  Multiplexer #(.select(2), .enable("false")) multiplexer_1 (
    .in0(d_latch_10_nq), .in1(d_latch_11_nq), .in2(d_latch_12_nq), .in3(d_latch_13_nq),
    .out(multiplexer_1_out), .sel({TVO1, d_latch_9_q[0]}));
  Multiplexer #(.select(2), .enable("false")) multiplexer_2 (
    .in0(d_latch_14_nq), .in1(d_latch_15_nq), .in2(d_latch_16_nq), .in3(d_latch_17_nq),
    .out(multiplexer_2_out), .sel({TVO1, d_latch_9_q[0]}));
  nor nor_2 (nor_2_out, PCLK[0], not_3_out, not_4_out);
  D_latch d_latch_19 (.EN(nor_3_out), .D(multiplexer_1_out), .nQ(d_latch_19_nq));  // open: Q
  D_latch d_latch_20 (.EN(nor_3_out), .D(multiplexer_2_out), .nQ(d_latch_20_nq));  // open: Q
  nor nor_3 (nor_3_out, PCLK[0], not_3_out, not_5_out);
  nor nor_4 (nor_4_out, PCLK[1], nor_5_out, nor_7_out);
  nor nor_5 (nor_5_out, PCLK[0], nor_6_out, not_6_out);
  nor nor_6 (nor_6_out, not_3_out, not_5_out);
  SHIFT_REG_LOAD shift_reg_load_1 (
    .LOAD(nor_3_out), .STEP(nor_5_out), .NEXT(nor_4_out), .OUT(shift_reg_load_1_out), ._0(d_latch_1_nq[0]),
    ._1(d_latch_1_nq[1]), ._2(d_latch_1_nq[2]), ._3(d_latch_1_nq[3]), ._4(d_latch_1_nq[4]),
    ._5(d_latch_1_nq[5]), ._6(d_latch_1_nq[6]), ._7(d_latch_1_nq[7]));
  SHIFT_REG_LOAD shift_reg_load_2 (
    .LOAD(nor_3_out), .STEP(nor_5_out), .NEXT(nor_4_out), .OUT(shift_reg_load_2_out), ._0(PD0), ._1(PD1),
    ._2(PD2), ._3(PD3), ._4(PD4), ._5(PD5), ._6(PD6), ._7(PD7));
  D_latch d_latch_21 (.EN(nor_4_out), .D(d_latch_19_nq), .nQ(d_latch_21_nq));  // open: Q
  D_latch d_latch_22 (.EN(nor_4_out), .D(d_latch_20_nq), .nQ(d_latch_22_nq));  // open: Q
  nor nor_7 (nor_7_out, PCLK[0], not_6_out);
  SHIFT_REG SHIFT_REGISTER (
    .STEP1(nor_7_out), .DATA_IN(shift_reg_load_1_out), .STEP2(nor_4_out), .OUT_0(SHIFT_REGISTER_out_0),
    .OUT_1(SHIFT_REGISTER_out_1), .OUT_2(SHIFT_REGISTER_out_2), .OUT_3(SHIFT_REGISTER_out_3),
    .OUT_4(SHIFT_REGISTER_out_4), .OUT_5(SHIFT_REGISTER_out_5), .OUT_6(SHIFT_REGISTER_out_6),
    .OUT_7(SHIFT_REGISTER_out_7));
  SHIFT_REG SHIFT_REGISTER_2 (
    .STEP1(nor_7_out), .DATA_IN(shift_reg_load_2_out), .STEP2(nor_4_out), .OUT_0(SHIFT_REGISTER_2_out_0),
    .OUT_1(SHIFT_REGISTER_2_out_1), .OUT_2(SHIFT_REGISTER_2_out_2), .OUT_3(SHIFT_REGISTER_2_out_3),
    .OUT_4(SHIFT_REGISTER_2_out_4), .OUT_5(SHIFT_REGISTER_2_out_5), .OUT_6(SHIFT_REGISTER_2_out_6),
    .OUT_7(SHIFT_REGISTER_2_out_7));
  SHIFT_REG SHIFT_REGISTER_3 (
    .STEP1(nor_7_out), .DATA_IN(d_latch_21_nq), .STEP2(nor_4_out), .OUT_0(SHIFT_REGISTER_3_out_0),
    .OUT_1(SHIFT_REGISTER_3_out_1), .OUT_2(SHIFT_REGISTER_3_out_2), .OUT_3(SHIFT_REGISTER_3_out_3),
    .OUT_4(SHIFT_REGISTER_3_out_4), .OUT_5(SHIFT_REGISTER_3_out_5), .OUT_6(SHIFT_REGISTER_3_out_6),
    .OUT_7(SHIFT_REGISTER_3_out_7));
  SHIFT_REG SHIFT_REGISTER_4 (
    .STEP1(nor_7_out), .DATA_IN(d_latch_22_nq), .STEP2(nor_4_out), .OUT_0(SHIFT_REGISTER_4_out_0),
    .OUT_1(SHIFT_REGISTER_4_out_1), .OUT_2(SHIFT_REGISTER_4_out_2), .OUT_3(SHIFT_REGISTER_4_out_3),
    .OUT_4(SHIFT_REGISTER_4_out_4), .OUT_5(SHIFT_REGISTER_4_out_5), .OUT_6(SHIFT_REGISTER_4_out_6),
    .OUT_7(SHIFT_REGISTER_4_out_7));
  Multiplexer #(.select(3), .enable("false")) multiplexer_3 (
    .in0(SHIFT_REGISTER_out_7), .in1(SHIFT_REGISTER_out_6), .in2(SHIFT_REGISTER_out_5),
    .in3(SHIFT_REGISTER_out_4), .in4(SHIFT_REGISTER_out_3), .in5(SHIFT_REGISTER_out_2),
    .in6(SHIFT_REGISTER_out_1), .in7(SHIFT_REGISTER_out_0), .out(multiplexer_3_out), .sel({FH2, FH1, FH0}));
  Multiplexer #(.select(3), .enable("false")) multiplexer_4 (
    .in0(SHIFT_REGISTER_2_out_7), .in1(SHIFT_REGISTER_2_out_6), .in2(SHIFT_REGISTER_2_out_5),
    .in3(SHIFT_REGISTER_2_out_4), .in4(SHIFT_REGISTER_2_out_3), .in5(SHIFT_REGISTER_2_out_2),
    .in6(SHIFT_REGISTER_2_out_1), .in7(SHIFT_REGISTER_2_out_0), .out(multiplexer_4_out), .sel({FH2, FH1, FH0}));
  Multiplexer #(.select(3), .enable("false")) multiplexer_5 (
    .in0(SHIFT_REGISTER_3_out_7), .in1(SHIFT_REGISTER_3_out_6), .in2(SHIFT_REGISTER_3_out_5),
    .in3(SHIFT_REGISTER_3_out_4), .in4(SHIFT_REGISTER_3_out_3), .in5(SHIFT_REGISTER_3_out_2),
    .in6(SHIFT_REGISTER_3_out_1), .in7(SHIFT_REGISTER_3_out_0), .out(multiplexer_5_out), .sel({FH2, FH1, FH0}));
  Multiplexer #(.select(3), .enable("false")) multiplexer_6 (
    .in0(SHIFT_REGISTER_4_out_7), .in1(SHIFT_REGISTER_4_out_6), .in2(SHIFT_REGISTER_4_out_5),
    .in3(SHIFT_REGISTER_4_out_4), .in4(SHIFT_REGISTER_4_out_3), .in5(SHIFT_REGISTER_4_out_2),
    .in6(SHIFT_REGISTER_4_out_1), .in7(SHIFT_REGISTER_4_out_0), .out(multiplexer_6_out), .sel({FH2, FH1, FH0}));
  not not_7 (not_7_out, multiplexer_3_out);
  not not_8 (not_8_out, multiplexer_5_out);
  not not_9 (not_9_out, multiplexer_6_out);
  D_latch d_latch_23 (.EN(nPCLK2), .D(not_7_out), .nQ(d_latch_23_nq));  // open: Q
  D_latch d_latch_24 (.EN(nPCLK2), .D(multiplexer_4_out), .nQ(d_latch_24_nq));  // open: Q
  D_latch d_latch_25 (.EN(nPCLK2), .D(not_8_out), .nQ(d_latch_25_nq));  // open: Q
  D_latch d_latch_26 (.EN(nPCLK2), .D(not_9_out), .nQ(d_latch_26_nq));  // open: Q
  D_latch d_latch_27 (.EN(PCLK[0]), .D(CLPB), .nQ(d_latch_27_nq));  // open: Q
  D_latch d_latch_28 (.EN(PCLK[0]), .D(d_latch_23_nq), .Q(d_latch_28_q));  // open: nQ
  D_latch d_latch_29 (.EN(PCLK[0]), .D(d_latch_24_nq), .Q(d_latch_29_q));  // open: nQ
  D_latch d_latch_30 (.EN(PCLK[0]), .D(d_latch_25_nq), .Q(d_latch_30_q));  // open: nQ
  D_latch d_latch_31 (.EN(PCLK[0]), .D(d_latch_26_nq), .Q(d_latch_31_q));  // open: nQ
  nor nor_8 (BGC0, d_latch_27_nq, d_latch_28_q);
  nor nor_9 (BGC1, d_latch_27_nq, d_latch_29_q);
  nor nor_10 (BGC2, d_latch_27_nq, d_latch_30_q);
  nor nor_11 (BGC3, d_latch_27_nq, d_latch_31_q);

  // Other names for the same wires on the sheet: PCLK_t = PCLK[0]; nPCLK = PCLK[1]

  // Notes on the sheet:
  //   PD/SEL
  //   PD/SR
  //   STEP
  //   SRLOAD
  //   NEXT
  //   STEP2
  //   reverse order of register outputs
  //   reverse order of register outputs
  //   reverse order of register outputs
  //   reverse order of register outputs
endmodule

module SHIFT_REG (
  input  STEP1,
  input  DATA_IN,
  input  STEP2,
  output OUT_0,
  output OUT_1,
  output OUT_2,
  output OUT_3,
  output OUT_4,
  output OUT_5,
  output OUT_6,
  output OUT_7
);

  wire d_latch_1_nq, d_latch_3_nq, d_latch_5_nq, d_latch_7_nq, d_latch_9_nq, d_latch_11_nq, d_latch_13_nq,
       d_latch_15_nq;

  D_latch d_latch_1 (.EN(STEP1), .D(DATA_IN), .nQ(d_latch_1_nq));  // open: Q
  D_latch d_latch_2 (.EN(STEP2), .D(d_latch_1_nq), .nQ(OUT_0));  // open: Q
  D_latch d_latch_3 (.EN(STEP1), .D(OUT_0), .nQ(d_latch_3_nq));  // open: Q
  D_latch d_latch_4 (.EN(STEP2), .D(d_latch_3_nq), .nQ(OUT_1));  // open: Q
  D_latch d_latch_5 (.EN(STEP1), .D(OUT_1), .nQ(d_latch_5_nq));  // open: Q
  D_latch d_latch_6 (.EN(STEP2), .D(d_latch_5_nq), .nQ(OUT_2));  // open: Q
  D_latch d_latch_7 (.EN(STEP1), .D(OUT_2), .nQ(d_latch_7_nq));  // open: Q
  D_latch d_latch_8 (.EN(STEP2), .D(d_latch_7_nq), .nQ(OUT_3));  // open: Q
  D_latch d_latch_9 (.EN(STEP1), .D(OUT_3), .nQ(d_latch_9_nq));  // open: Q
  D_latch d_latch_10 (.EN(STEP2), .D(d_latch_9_nq), .nQ(OUT_4));  // open: Q
  D_latch d_latch_11 (.EN(STEP1), .D(OUT_4), .nQ(d_latch_11_nq));  // open: Q
  D_latch d_latch_12 (.EN(STEP2), .D(d_latch_11_nq), .nQ(OUT_5));  // open: Q
  D_latch d_latch_13 (.EN(STEP1), .D(OUT_5), .nQ(d_latch_13_nq));  // open: Q
  D_latch d_latch_14 (.EN(STEP2), .D(d_latch_13_nq), .nQ(OUT_6));  // open: Q
  D_latch d_latch_15 (.EN(STEP1), .D(OUT_6), .nQ(d_latch_15_nq));  // open: Q
  D_latch d_latch_16 (.EN(STEP2), .D(d_latch_15_nq), .nQ(OUT_7));  // open: Q
endmodule

module SHIFT_REG_LOAD (
  input  _0,
  input  _1,
  input  _2,
  input  _3,
  input  _4,
  input  _5,
  input  _6,
  input  _7,
  input  LOAD,
  input  STEP,
  input  NEXT,
  output OUT
);

  wire controlled_buffer_1_out, controlled_buffer_3_out, controlled_buffer_5_out, controlled_buffer_7_out,
       controlled_buffer_9_out, controlled_buffer_11_out, controlled_buffer_13_out, controlled_buffer_15_out,
       d_latch_1_nq, d_latch_2_nq, d_latch_3_nq, d_latch_4_nq, d_latch_5_nq, d_latch_6_nq, d_latch_7_nq,
       d_latch_8_nq, d_latch_9_nq, d_latch_10_nq, d_latch_11_nq, d_latch_12_nq, d_latch_13_nq, d_latch_14_nq,
       d_latch_15_nq;

  assign controlled_buffer_1_out = STEP ? 1'b1 : 1'bz;  // Controlled_Buffer controlled_buffer_1
  assign controlled_buffer_1_out = LOAD ? _0 : 1'bz;  // Controlled_Buffer controlled_buffer_2
  D_latch d_latch_1 (.EN(1'b1), .D(controlled_buffer_1_out), .nQ(d_latch_1_nq));  // open: Q
  D_latch d_latch_2 (.EN(NEXT), .D(d_latch_1_nq), .nQ(d_latch_2_nq));  // open: Q
  assign controlled_buffer_3_out = LOAD ? _1 : 1'bz;  // Controlled_Buffer controlled_buffer_3
  assign controlled_buffer_3_out = STEP ? d_latch_2_nq : 1'bz;  // Controlled_Buffer controlled_buffer_4
  D_latch d_latch_3 (.EN(1'b1), .D(controlled_buffer_3_out), .nQ(d_latch_3_nq));  // open: Q
  D_latch d_latch_4 (.EN(NEXT), .D(d_latch_3_nq), .nQ(d_latch_4_nq));  // open: Q
  assign controlled_buffer_5_out = STEP ? d_latch_4_nq : 1'bz;  // Controlled_Buffer controlled_buffer_5
  assign controlled_buffer_5_out = LOAD ? _2 : 1'bz;  // Controlled_Buffer controlled_buffer_6
  D_latch d_latch_5 (.EN(1'b1), .D(controlled_buffer_5_out), .nQ(d_latch_5_nq));  // open: Q
  D_latch d_latch_6 (.EN(NEXT), .D(d_latch_5_nq), .nQ(d_latch_6_nq));  // open: Q
  assign controlled_buffer_7_out = LOAD ? _3 : 1'bz;  // Controlled_Buffer controlled_buffer_7
  assign controlled_buffer_7_out = STEP ? d_latch_6_nq : 1'bz;  // Controlled_Buffer controlled_buffer_8
  D_latch d_latch_7 (.EN(1'b1), .D(controlled_buffer_7_out), .nQ(d_latch_7_nq));  // open: Q
  D_latch d_latch_8 (.EN(NEXT), .D(d_latch_7_nq), .nQ(d_latch_8_nq));  // open: Q
  assign controlled_buffer_9_out = STEP ? d_latch_8_nq : 1'bz;  // Controlled_Buffer controlled_buffer_9
  assign controlled_buffer_9_out = LOAD ? _4 : 1'bz;  // Controlled_Buffer controlled_buffer_10
  D_latch d_latch_9 (.EN(1'b1), .D(controlled_buffer_9_out), .nQ(d_latch_9_nq));  // open: Q
  D_latch d_latch_10 (.EN(NEXT), .D(d_latch_9_nq), .nQ(d_latch_10_nq));  // open: Q
  assign controlled_buffer_11_out = LOAD ? _5 : 1'bz;  // Controlled_Buffer controlled_buffer_11
  assign controlled_buffer_11_out = STEP ? d_latch_10_nq : 1'bz;  // Controlled_Buffer controlled_buffer_12
  D_latch d_latch_11 (.EN(1'b1), .D(controlled_buffer_11_out), .nQ(d_latch_11_nq));  // open: Q
  D_latch d_latch_12 (.EN(NEXT), .D(d_latch_11_nq), .nQ(d_latch_12_nq));  // open: Q
  assign controlled_buffer_13_out = STEP ? d_latch_12_nq : 1'bz;  // Controlled_Buffer controlled_buffer_13
  assign controlled_buffer_13_out = LOAD ? _6 : 1'bz;  // Controlled_Buffer controlled_buffer_14
  D_latch d_latch_13 (.EN(1'b1), .D(controlled_buffer_13_out), .nQ(d_latch_13_nq));  // open: Q
  D_latch d_latch_14 (.EN(NEXT), .D(d_latch_13_nq), .nQ(d_latch_14_nq));  // open: Q
  assign controlled_buffer_15_out = LOAD ? _7 : 1'bz;  // Controlled_Buffer controlled_buffer_15
  assign controlled_buffer_15_out = STEP ? d_latch_14_nq : 1'bz;  // Controlled_Buffer controlled_buffer_16
  D_latch d_latch_15 (.EN(1'b1), .D(controlled_buffer_15_out), .nQ(d_latch_15_nq));  // open: Q
  D_latch d_latch_16 (.EN(NEXT), .D(d_latch_15_nq), .nQ(OUT));  // open: Q
endmodule

module SEL12x3 (
  input  PCLK,
  input  nTx,
  input  IN0,
  input  IN1,
  input  IN2,
  input  IN3,
  input  IN4,
  input  IN5,
  input  IN6,
  input  IN7,
  input  IN8,
  input  IN9,
  input  IN10,
  input  IN11,
  input  _0,
  input  _1,
  output OUT2,
  output OUT1,
  output OUT0
);

  wire multiplexer_1_out, multiplexer_2_out, multiplexer_3_out, not_1_out;

  not not_1 (not_1_out, nTx);
  Multiplexer #(.select(2), .enable("false")) multiplexer_1 (
    .in0(IN0), .in1(IN2), .in2(IN1), .in3(IN3), .out(multiplexer_1_out), .sel({_1, _0}));
  Multiplexer #(.select(2), .enable("false")) multiplexer_2 (
    .in0(IN4), .in1(IN6), .in2(IN5), .in3(IN7), .out(multiplexer_2_out), .sel({_1, _0}));
  Multiplexer #(.select(2), .enable("false")) multiplexer_3 (
    .in0(IN8), .in1(IN10), .in2(IN9), .in3(IN11), .out(multiplexer_3_out), .sel({_1, _0}));
  D_Flip_Flop #(.trigger("high")) d_ff_1 (
    .clk(PCLK), .D(multiplexer_1_out), .Q(OUT2), .reset(not_1_out));  // open: Qn, preset, en
  D_Flip_Flop #(.trigger("high")) d_ff_2 (
    .clk(PCLK), .D(multiplexer_2_out), .Q(OUT1), .reset(not_1_out));  // open: Qn, preset, en
  D_Flip_Flop #(.trigger("high")) d_ff_3 (
    .clk(PCLK), .D(multiplexer_3_out), .Q(OUT0), .reset(not_1_out));  // open: Qn, preset, en
endmodule

module SEL16x12_R (
  input  PCLK,
  input  _15,
  input  _14,
  input  _13,
  input  _12,
  input  _11,
  input  _10,
  input  _9,
  input  _8,
  input  _7,
  input  _6,
  input  _5,
  input  _4,
  input  _3,
  input  _2,
  input  _1,
  input  _0,
  output OUT0,
  output OUT1,
  output OUT2,
  output OUT3,
  output OUT4,
  output OUT5,
  output OUT6,
  output OUT7,
  output OUT8,
  output OUT9,
  output OUT10,
  output OUT11
);

  wire transistor_1_out, transistor_2_out, transistor_3_out, transistor_5_out, transistor_7_out,
       transistor_9_out, transistor_10_out, transistor_12_out, transistor_15_out, transistor_17_out,
       transistor_18_out, transistor_34_out;

  and and_1 (OUT0, PCLK, transistor_1_out);
  and and_2 (OUT1, PCLK, transistor_12_out);
  and and_3 (OUT2, PCLK, transistor_34_out);
  and and_4 (OUT3, PCLK, transistor_2_out);
  and and_5 (OUT4, PCLK, transistor_3_out);
  and and_6 (OUT5, PCLK, transistor_15_out);
  and and_7 (OUT6, PCLK, transistor_5_out);
  and and_8 (OUT7, PCLK, transistor_7_out);
  and and_9 (OUT8, PCLK, transistor_17_out);
  and and_10 (OUT9, PCLK, transistor_18_out);
  and and_11 (OUT10, PCLK, transistor_9_out);
  and and_12 (OUT11, PCLK, transistor_10_out);
  Transistor #(.\type ("n")) transistor_1 (.in(1'b0), .out(transistor_1_out), .gate(_14));
  Transistor #(.\type ("n")) transistor_2 (.in(1'b0), .out(transistor_2_out), .gate(_14));
  Transistor #(.\type ("n")) transistor_3 (.in(1'b0), .out(transistor_3_out), .gate(_15));
  Transistor #(.\type ("n")) transistor_4 (.in(1'b0), .out(transistor_3_out), .gate(_14));
  Transistor #(.\type ("n")) transistor_5 (.in(1'b0), .out(transistor_5_out), .gate(_14));
  Transistor #(.\type ("n")) transistor_6 (.in(1'b0), .out(transistor_5_out), .gate(_15));
  Transistor #(.\type ("n")) transistor_7 (.in(1'b0), .out(transistor_7_out), .gate(_15));
  Transistor #(.\type ("n")) transistor_8 (.in(1'b0), .out(transistor_7_out), .gate(_14));
  Transistor #(.\type ("n")) transistor_9 (.in(1'b0), .out(transistor_9_out), .gate(_15));
  Transistor #(.\type ("n")) transistor_10 (.in(1'b0), .out(transistor_10_out), .gate(_14));
  Transistor #(.\type ("n")) transistor_11 (.in(1'b0), .out(transistor_1_out), .gate(_13));
  Transistor #(.\type ("n")) transistor_12 (.in(1'b0), .out(transistor_12_out), .gate(_13));
  Transistor #(.\type ("n")) transistor_13 (.in(1'b0), .out(transistor_2_out), .gate(_13));
  Transistor #(.\type ("n")) transistor_14 (.in(1'b0), .out(transistor_3_out), .gate(_12));
  Transistor #(.\type ("n")) transistor_15 (.in(1'b0), .out(transistor_15_out), .gate(_13));
  Transistor #(.\type ("n")) transistor_16 (.in(1'b0), .out(transistor_7_out), .gate(_13));
  Transistor #(.\type ("n")) transistor_17 (.in(1'b0), .out(transistor_17_out), .gate(_12));
  Transistor #(.\type ("n")) transistor_18 (.in(1'b0), .out(transistor_18_out), .gate(_13));
  Transistor #(.\type ("n")) transistor_19 (.in(1'b0), .out(transistor_18_out), .gate(_12));
  Transistor #(.\type ("n")) transistor_20 (.in(1'b0), .out(transistor_9_out), .gate(_12));
  Transistor #(.\type ("n")) transistor_21 (.in(1'b0), .out(transistor_10_out), .gate(_13));
  Transistor #(.\type ("n")) transistor_22 (.in(1'b0), .out(transistor_1_out), .gate(_11));
  Transistor #(.\type ("n")) transistor_23 (.in(1'b0), .out(transistor_12_out), .gate(_11));
  Transistor #(.\type ("n")) transistor_24 (.in(1'b0), .out(transistor_3_out), .gate(_11));
  Transistor #(.\type ("n")) transistor_25 (.in(1'b0), .out(transistor_15_out), .gate(_11));
  Transistor #(.\type ("n")) transistor_26 (.in(1'b0), .out(transistor_5_out), .gate(_11));
  Transistor #(.\type ("n")) transistor_27 (.in(1'b0), .out(transistor_7_out), .gate(_11));
  Transistor #(.\type ("n")) transistor_28 (.in(1'b0), .out(transistor_17_out), .gate(_11));
  Transistor #(.\type ("n")) transistor_29 (.in(1'b0), .out(transistor_18_out), .gate(_11));
  Transistor #(.\type ("n")) transistor_30 (.in(1'b0), .out(transistor_10_out), .gate(_11));
  Transistor #(.\type ("n")) transistor_31 (.in(1'b0), .out(transistor_1_out), .gate(_10));
  Transistor #(.\type ("n")) transistor_32 (.in(1'b0), .out(transistor_1_out), .gate(_9));
  Transistor #(.\type ("n")) transistor_33 (.in(1'b0), .out(transistor_12_out), .gate(_9));
  Transistor #(.\type ("n")) transistor_34 (.in(1'b0), .out(transistor_34_out), .gate(_9));
  Transistor #(.\type ("n")) transistor_35 (.in(1'b0), .out(transistor_2_out), .gate(_10));
  Transistor #(.\type ("n")) transistor_36 (.in(1'b0), .out(transistor_2_out), .gate(_9));
  Transistor #(.\type ("n")) transistor_37 (.in(1'b0), .out(transistor_3_out), .gate(_9));
  Transistor #(.\type ("n")) transistor_38 (.in(1'b0), .out(transistor_3_out), .gate(_10));
  Transistor #(.\type ("n")) transistor_39 (.in(1'b0), .out(transistor_15_out), .gate(_10));
  Transistor #(.\type ("n")) transistor_40 (.in(1'b0), .out(transistor_5_out), .gate(_9));
  Transistor #(.\type ("n")) transistor_41 (.in(1'b0), .out(transistor_7_out), .gate(_10));
  Transistor #(.\type ("n")) transistor_42 (.in(1'b0), .out(transistor_17_out), .gate(_10));
  Transistor #(.\type ("n")) transistor_43 (.in(1'b0), .out(transistor_17_out), .gate(_9));
  Transistor #(.\type ("n")) transistor_44 (.in(1'b0), .out(transistor_18_out), .gate(_10));
  Transistor #(.\type ("n")) transistor_45 (.in(1'b0), .out(transistor_9_out), .gate(_10));
  Transistor #(.\type ("n")) transistor_46 (.in(1'b0), .out(transistor_9_out), .gate(_9));
  Transistor #(.\type ("n")) transistor_47 (.in(1'b0), .out(transistor_15_out), .gate(_8));
  Transistor #(.\type ("n")) transistor_48 (.in(1'b0), .out(transistor_12_out), .gate(_7));
  Transistor #(.\type ("n")) transistor_49 (.in(1'b0), .out(transistor_34_out), .gate(_7));
  Transistor #(.\type ("n")) transistor_50 (.in(1'b0), .out(transistor_2_out), .gate(_6));
  Transistor #(.\type ("n")) transistor_51 (.in(1'b0), .out(transistor_15_out), .gate(_7));
  Transistor #(.\type ("n")) transistor_52 (.in(1'b0), .out(transistor_5_out), .gate(_7));
  Transistor #(.\type ("n")) transistor_53 (.in(1'b0), .out(transistor_7_out), .gate(_6));
  Transistor #(.\type ("n")) transistor_54 (.in(1'b0), .out(transistor_18_out), .gate(_7));
  Transistor #(.\type ("n")) transistor_55 (.in(1'b0), .out(transistor_9_out), .gate(_7));
  Transistor #(.\type ("n")) transistor_56 (.in(1'b0), .out(transistor_10_out), .gate(_7));
  Transistor #(.\type ("n")) transistor_57 (.in(1'b0), .out(transistor_1_out), .gate(_4));
  Transistor #(.\type ("n")) transistor_58 (.in(1'b0), .out(transistor_34_out), .gate(_4));
  Transistor #(.\type ("n")) transistor_59 (.in(1'b0), .out(transistor_34_out), .gate(_5));
  Transistor #(.\type ("n")) transistor_60 (.in(1'b0), .out(transistor_2_out), .gate(_4));
  Transistor #(.\type ("n")) transistor_61 (.in(1'b0), .out(transistor_2_out), .gate(_5));
  Transistor #(.\type ("n")) transistor_62 (.in(1'b0), .out(transistor_15_out), .gate(_5));
  Transistor #(.\type ("n")) transistor_63 (.in(1'b0), .out(transistor_15_out), .gate(_4));
  Transistor #(.\type ("n")) transistor_64 (.in(1'b0), .out(transistor_5_out), .gate(_4));
  Transistor #(.\type ("n")) transistor_65 (.in(1'b0), .out(transistor_7_out), .gate(_4));
  Transistor #(.\type ("n")) transistor_66 (.in(1'b0), .out(transistor_18_out), .gate(_4));
  Transistor #(.\type ("n")) transistor_67 (.in(1'b0), .out(transistor_18_out), .gate(_5));
  Transistor #(.\type ("n")) transistor_68 (.in(1'b0), .out(transistor_9_out), .gate(_4));
  Transistor #(.\type ("n")) transistor_69 (.in(1'b0), .out(transistor_10_out), .gate(_4));
  Transistor #(.\type ("n")) transistor_70 (.in(1'b0), .out(transistor_12_out), .gate(_3));
  Transistor #(.\type ("n")) transistor_71 (.in(1'b0), .out(transistor_2_out), .gate(_3));
  Transistor #(.\type ("n")) transistor_72 (.in(1'b0), .out(transistor_5_out), .gate(_3));
  Transistor #(.\type ("n")) transistor_73 (.in(1'b0), .out(transistor_7_out), .gate(_3));
  Transistor #(.\type ("n")) transistor_74 (.in(1'b0), .out(transistor_18_out), .gate(_3));
  Transistor #(.\type ("n")) transistor_75 (.in(1'b0), .out(transistor_10_out), .gate(_3));
  Transistor #(.\type ("n")) transistor_76 (.in(1'b0), .out(transistor_1_out), .gate(_2));
  Transistor #(.\type ("n")) transistor_77 (.in(1'b0), .out(transistor_12_out), .gate(_1));
  Transistor #(.\type ("n")) transistor_78 (.in(1'b0), .out(transistor_12_out), .gate(_2));
  Transistor #(.\type ("n")) transistor_79 (.in(1'b0), .out(transistor_2_out), .gate(_1));
  Transistor #(.\type ("n")) transistor_80 (.in(1'b0), .out(transistor_15_out), .gate(_2));
  Transistor #(.\type ("n")) transistor_81 (.in(1'b0), .out(transistor_15_out), .gate(_1));
  Transistor #(.\type ("n")) transistor_82 (.in(1'b0), .out(transistor_7_out), .gate(_1));
  Transistor #(.\type ("n")) transistor_83 (.in(1'b0), .out(transistor_7_out), .gate(_2));
  Transistor #(.\type ("n")) transistor_84 (.in(1'b0), .out(transistor_17_out), .gate(_2));
  Transistor #(.\type ("n")) transistor_85 (.in(1'b0), .out(transistor_18_out), .gate(_2));
  Transistor #(.\type ("n")) transistor_86 (.in(1'b0), .out(transistor_18_out), .gate(_1));
  Transistor #(.\type ("n")) transistor_87 (.in(1'b0), .out(transistor_9_out), .gate(_2));
  Transistor #(.\type ("n")) transistor_88 (.in(1'b0), .out(transistor_9_out), .gate(_1));
  Transistor #(.\type ("n")) transistor_89 (.in(1'b0), .out(transistor_10_out), .gate(_1));
  Transistor #(.\type ("n")) transistor_90 (.in(1'b0), .out(transistor_10_out), .gate(_2));
  Transistor #(.\type ("n")) transistor_91 (.in(1'b0), .out(transistor_1_out), .gate(_0));
  Transistor #(.\type ("n")) transistor_92 (.in(1'b0), .out(transistor_12_out), .gate(_0));
  Transistor #(.\type ("n")) transistor_93 (.in(1'b0), .out(transistor_3_out), .gate(_0));
  Transistor #(.\type ("n")) transistor_94 (.in(1'b0), .out(transistor_7_out), .gate(_0));
  Transistor #(.\type ("n")) transistor_95 (.in(1'b0), .out(transistor_17_out), .gate(_0));
  Transistor #(.\type ("n")) transistor_96 (.in(1'b0), .out(transistor_18_out), .gate(_0));
  Transistor #(.\type ("n")) transistor_97 (.in(1'b0), .out(transistor_10_out), .gate(_0));
  Pull_Resistor #(.pull(1)) pull_resistor_1 (.node(transistor_1_out));
  Pull_Resistor #(.pull(1)) pull_resistor_2 (.node(transistor_12_out));
  Pull_Resistor #(.pull(1)) pull_resistor_3 (.node(transistor_34_out));
  Pull_Resistor #(.pull(1)) pull_resistor_4 (.node(transistor_2_out));
  Pull_Resistor #(.pull(1)) pull_resistor_5 (.node(transistor_3_out));
  Pull_Resistor #(.pull(1)) pull_resistor_6 (.node(transistor_15_out));
  Pull_Resistor #(.pull(1)) pull_resistor_7 (.node(transistor_5_out));
  Pull_Resistor #(.pull(1)) pull_resistor_8 (.node(transistor_7_out));
  Pull_Resistor #(.pull(1)) pull_resistor_9 (.node(transistor_17_out));
  Pull_Resistor #(.pull(1)) pull_resistor_10 (.node(transistor_18_out));
  Pull_Resistor #(.pull(1)) pull_resistor_11 (.node(transistor_9_out));
  Pull_Resistor #(.pull(1)) pull_resistor_12 (.node(transistor_10_out));

  // Notes on the sheet:
  //   RED
endmodule

module SEL16x12_G (
  input  PCLK,
  input  _15,
  input  _14,
  input  _13,
  input  _12,
  input  _11,
  input  _10,
  input  _9,
  input  _8,
  input  _7,
  input  _6,
  input  _5,
  input  _4,
  input  _3,
  input  _2,
  input  _1,
  input  _0,
  output OUT0,
  output OUT1,
  output OUT2,
  output OUT3,
  output OUT4,
  output OUT5,
  output OUT6,
  output OUT7,
  output OUT8,
  output OUT9,
  output OUT10,
  output OUT11
);

  wire transistor_1_out, transistor_2_out, transistor_3_out, transistor_4_out, transistor_5_out,
       transistor_7_out, transistor_8_out, transistor_9_out, transistor_15_out, transistor_16_out,
       transistor_21_out, transistor_26_out;

  and and_1 (OUT0, PCLK, transistor_1_out);
  and and_2 (OUT1, PCLK, transistor_2_out);
  and and_3 (OUT2, PCLK, transistor_26_out);
  and and_4 (OUT3, PCLK, transistor_3_out);
  and and_5 (OUT4, PCLK, transistor_4_out);
  and and_6 (OUT5, PCLK, transistor_15_out);
  and and_7 (OUT6, PCLK, transistor_16_out);
  and and_8 (OUT7, PCLK, transistor_5_out);
  and and_9 (OUT8, PCLK, transistor_7_out);
  and and_10 (OUT9, PCLK, transistor_21_out);
  and and_11 (OUT10, PCLK, transistor_8_out);
  and and_12 (OUT11, PCLK, transistor_9_out);
  Transistor #(.\type ("n")) transistor_1 (.in(1'b0), .out(transistor_1_out), .gate(_14));
  Transistor #(.\type ("n")) transistor_2 (.in(1'b0), .out(transistor_2_out), .gate(_15));
  Transistor #(.\type ("n")) transistor_3 (.in(1'b0), .out(transistor_3_out), .gate(_15));
  Transistor #(.\type ("n")) transistor_4 (.in(1'b0), .out(transistor_4_out), .gate(_15));
  Transistor #(.\type ("n")) transistor_5 (.in(1'b0), .out(transistor_5_out), .gate(_15));
  Transistor #(.\type ("n")) transistor_6 (.in(1'b0), .out(transistor_5_out), .gate(_14));
  Transistor #(.\type ("n")) transistor_7 (.in(1'b0), .out(transistor_7_out), .gate(_14));
  Transistor #(.\type ("n")) transistor_8 (.in(1'b0), .out(transistor_8_out), .gate(_14));
  Transistor #(.\type ("n")) transistor_9 (.in(1'b0), .out(transistor_9_out), .gate(_15));
  Transistor #(.\type ("n")) transistor_10 (.in(1'b0), .out(transistor_9_out), .gate(_14));
  Transistor #(.\type ("n")) transistor_11 (.in(1'b0), .out(transistor_1_out), .gate(_13));
  Transistor #(.\type ("n")) transistor_12 (.in(1'b0), .out(transistor_2_out), .gate(_13));
  Transistor #(.\type ("n")) transistor_13 (.in(1'b0), .out(transistor_3_out), .gate(_12));
  Transistor #(.\type ("n")) transistor_14 (.in(1'b0), .out(transistor_3_out), .gate(_13));
  Transistor #(.\type ("n")) transistor_15 (.in(1'b0), .out(transistor_15_out), .gate(_13));
  Transistor #(.\type ("n")) transistor_16 (.in(1'b0), .out(transistor_16_out), .gate(_12));
  Transistor #(.\type ("n")) transistor_17 (.in(1'b0), .out(transistor_5_out), .gate(_12));
  Transistor #(.\type ("n")) transistor_18 (.in(1'b0), .out(transistor_5_out), .gate(_13));
  Transistor #(.\type ("n")) transistor_19 (.in(1'b0), .out(transistor_7_out), .gate(_12));
  Transistor #(.\type ("n")) transistor_20 (.in(1'b0), .out(transistor_7_out), .gate(_13));
  Transistor #(.\type ("n")) transistor_21 (.in(1'b0), .out(transistor_21_out), .gate(_13));
  Transistor #(.\type ("n")) transistor_22 (.in(1'b0), .out(transistor_21_out), .gate(_12));
  Transistor #(.\type ("n")) transistor_23 (.in(1'b0), .out(transistor_8_out), .gate(_13));
  Transistor #(.\type ("n")) transistor_24 (.in(1'b0), .out(transistor_9_out), .gate(_12));
  Transistor #(.\type ("n")) transistor_25 (.in(1'b0), .out(transistor_1_out), .gate(_11));
  Transistor #(.\type ("n")) transistor_26 (.in(1'b0), .out(transistor_26_out), .gate(_11));
  Transistor #(.\type ("n")) transistor_27 (.in(1'b0), .out(transistor_15_out), .gate(_11));
  Transistor #(.\type ("n")) transistor_28 (.in(1'b0), .out(transistor_16_out), .gate(_11));
  Transistor #(.\type ("n")) transistor_29 (.in(1'b0), .out(transistor_5_out), .gate(_11));
  Transistor #(.\type ("n")) transistor_30 (.in(1'b0), .out(transistor_7_out), .gate(_11));
  Transistor #(.\type ("n")) transistor_31 (.in(1'b0), .out(transistor_21_out), .gate(_11));
  Transistor #(.\type ("n")) transistor_32 (.in(1'b0), .out(transistor_8_out), .gate(_11));
  Transistor #(.\type ("n")) transistor_33 (.in(1'b0), .out(transistor_9_out), .gate(_11));
  Transistor #(.\type ("n")) transistor_34 (.in(1'b0), .out(transistor_1_out), .gate(_9));
  Transistor #(.\type ("n")) transistor_35 (.in(1'b0), .out(transistor_2_out), .gate(_10));
  Transistor #(.\type ("n")) transistor_36 (.in(1'b0), .out(transistor_2_out), .gate(_9));
  Transistor #(.\type ("n")) transistor_37 (.in(1'b0), .out(transistor_26_out), .gate(_9));
  Transistor #(.\type ("n")) transistor_38 (.in(1'b0), .out(transistor_26_out), .gate(_10));
  Transistor #(.\type ("n")) transistor_39 (.in(1'b0), .out(transistor_3_out), .gate(_9));
  Transistor #(.\type ("n")) transistor_40 (.in(1'b0), .out(transistor_4_out), .gate(_10));
  Transistor #(.\type ("n")) transistor_41 (.in(1'b0), .out(transistor_4_out), .gate(_9));
  Transistor #(.\type ("n")) transistor_42 (.in(1'b0), .out(transistor_16_out), .gate(_9));
  Transistor #(.\type ("n")) transistor_43 (.in(1'b0), .out(transistor_5_out), .gate(_10));
  Transistor #(.\type ("n")) transistor_44 (.in(1'b0), .out(transistor_7_out), .gate(_9));
  Transistor #(.\type ("n")) transistor_45 (.in(1'b0), .out(transistor_21_out), .gate(_9));
  Transistor #(.\type ("n")) transistor_46 (.in(1'b0), .out(transistor_8_out), .gate(_9));
  Transistor #(.\type ("n")) transistor_47 (.in(1'b0), .out(transistor_9_out), .gate(_10));
  Transistor #(.\type ("n")) transistor_48 (.in(1'b0), .out(transistor_2_out), .gate(_8));
  Transistor #(.\type ("n")) transistor_49 (.in(1'b0), .out(transistor_3_out), .gate(_8));
  Transistor #(.\type ("n")) transistor_50 (.in(1'b0), .out(transistor_4_out), .gate(_8));
  Transistor #(.\type ("n")) transistor_51 (.in(1'b0), .out(transistor_15_out), .gate(_8));
  Transistor #(.\type ("n")) transistor_52 (.in(1'b0), .out(transistor_16_out), .gate(_8));
  Transistor #(.\type ("n")) transistor_53 (.in(1'b0), .out(transistor_5_out), .gate(_8));
  Transistor #(.\type ("n")) transistor_54 (.in(1'b0), .out(transistor_8_out), .gate(_8));
  Transistor #(.\type ("n")) transistor_55 (.in(1'b0), .out(transistor_9_out), .gate(_8));
  Transistor #(.\type ("n")) transistor_56 (.in(1'b0), .out(transistor_2_out), .gate(_7));
  Transistor #(.\type ("n")) transistor_57 (.in(1'b0), .out(transistor_26_out), .gate(_7));
  Transistor #(.\type ("n")) transistor_58 (.in(1'b0), .out(transistor_3_out), .gate(_6));
  Transistor #(.\type ("n")) transistor_59 (.in(1'b0), .out(transistor_3_out), .gate(_7));
  Transistor #(.\type ("n")) transistor_60 (.in(1'b0), .out(transistor_15_out), .gate(_6));
  Transistor #(.\type ("n")) transistor_61 (.in(1'b0), .out(transistor_16_out), .gate(_6));
  Transistor #(.\type ("n")) transistor_62 (.in(1'b0), .out(transistor_16_out), .gate(_7));
  Transistor #(.\type ("n")) transistor_63 (.in(1'b0), .out(transistor_5_out), .gate(_6));
  Transistor #(.\type ("n")) transistor_64 (.in(1'b0), .out(transistor_21_out), .gate(_7));
  Transistor #(.\type ("n")) transistor_65 (.in(1'b0), .out(transistor_8_out), .gate(_7));
  Transistor #(.\type ("n")) transistor_66 (.in(1'b0), .out(transistor_8_out), .gate(_6));
  Transistor #(.\type ("n")) transistor_67 (.in(1'b0), .out(transistor_1_out), .gate(_5));
  Transistor #(.\type ("n")) transistor_68 (.in(1'b0), .out(transistor_1_out), .gate(_4));
  Transistor #(.\type ("n")) transistor_69 (.in(1'b0), .out(transistor_2_out), .gate(_5));
  Transistor #(.\type ("n")) transistor_70 (.in(1'b0), .out(transistor_26_out), .gate(_4));
  Transistor #(.\type ("n")) transistor_71 (.in(1'b0), .out(transistor_3_out), .gate(_4));
  Transistor #(.\type ("n")) transistor_72 (.in(1'b0), .out(transistor_4_out), .gate(_5));
  Transistor #(.\type ("n")) transistor_73 (.in(1'b0), .out(transistor_4_out), .gate(_4));
  Transistor #(.\type ("n")) transistor_74 (.in(1'b0), .out(transistor_15_out), .gate(_4));
  Transistor #(.\type ("n")) transistor_75 (.in(1'b0), .out(transistor_15_out), .gate(_5));
  Transistor #(.\type ("n")) transistor_76 (.in(1'b0), .out(transistor_16_out), .gate(_4));
  Transistor #(.\type ("n")) transistor_77 (.in(1'b0), .out(transistor_16_out), .gate(_5));
  Transistor #(.\type ("n")) transistor_78 (.in(1'b0), .out(transistor_7_out), .gate(_5));
  Transistor #(.\type ("n")) transistor_79 (.in(1'b0), .out(transistor_21_out), .gate(_4));
  Transistor #(.\type ("n")) transistor_80 (.in(1'b0), .out(transistor_21_out), .gate(_5));
  Transistor #(.\type ("n")) transistor_81 (.in(1'b0), .out(transistor_8_out), .gate(_4));
  Transistor #(.\type ("n")) transistor_82 (.in(1'b0), .out(transistor_9_out), .gate(_5));
  Transistor #(.\type ("n")) transistor_83 (.in(1'b0), .out(transistor_2_out), .gate(_3));
  Transistor #(.\type ("n")) transistor_84 (.in(1'b0), .out(transistor_4_out), .gate(_3));
  Transistor #(.\type ("n")) transistor_85 (.in(1'b0), .out(transistor_15_out), .gate(_3));
  Transistor #(.\type ("n")) transistor_86 (.in(1'b0), .out(transistor_21_out), .gate(_3));
  Transistor #(.\type ("n")) transistor_87 (.in(1'b0), .out(transistor_1_out), .gate(_2));
  Transistor #(.\type ("n")) transistor_88 (.in(1'b0), .out(transistor_2_out), .gate(_1));
  Transistor #(.\type ("n")) transistor_89 (.in(1'b0), .out(transistor_3_out), .gate(_2));
  Transistor #(.\type ("n")) transistor_90 (.in(1'b0), .out(transistor_3_out), .gate(_1));
  Transistor #(.\type ("n")) transistor_91 (.in(1'b0), .out(transistor_15_out), .gate(_1));
  Transistor #(.\type ("n")) transistor_92 (.in(1'b0), .out(transistor_16_out), .gate(_1));
  Transistor #(.\type ("n")) transistor_93 (.in(1'b0), .out(transistor_7_out), .gate(_2));
  Transistor #(.\type ("n")) transistor_94 (.in(1'b0), .out(transistor_21_out), .gate(_1));
  Transistor #(.\type ("n")) transistor_95 (.in(1'b0), .out(transistor_8_out), .gate(_2));
  Transistor #(.\type ("n")) transistor_96 (.in(1'b0), .out(transistor_9_out), .gate(_2));
  Transistor #(.\type ("n")) transistor_97 (.in(1'b0), .out(transistor_1_out), .gate(_0));
  Transistor #(.\type ("n")) transistor_98 (.in(1'b0), .out(transistor_3_out), .gate(_0));
  Transistor #(.\type ("n")) transistor_99 (.in(1'b0), .out(transistor_5_out), .gate(_0));
  Transistor #(.\type ("n")) transistor_100 (.in(1'b0), .out(transistor_7_out), .gate(_0));
  Transistor #(.\type ("n")) transistor_101 (.in(1'b0), .out(transistor_8_out), .gate(_0));
  Transistor #(.\type ("n")) transistor_102 (.in(1'b0), .out(transistor_9_out), .gate(_0));
  Pull_Resistor #(.pull(1)) pull_resistor_1 (.node(transistor_1_out));
  Pull_Resistor #(.pull(1)) pull_resistor_2 (.node(transistor_2_out));
  Pull_Resistor #(.pull(1)) pull_resistor_3 (.node(transistor_26_out));
  Pull_Resistor #(.pull(1)) pull_resistor_4 (.node(transistor_3_out));
  Pull_Resistor #(.pull(1)) pull_resistor_5 (.node(transistor_4_out));
  Pull_Resistor #(.pull(1)) pull_resistor_6 (.node(transistor_15_out));
  Pull_Resistor #(.pull(1)) pull_resistor_7 (.node(transistor_16_out));
  Pull_Resistor #(.pull(1)) pull_resistor_8 (.node(transistor_5_out));
  Pull_Resistor #(.pull(1)) pull_resistor_9 (.node(transistor_7_out));
  Pull_Resistor #(.pull(1)) pull_resistor_10 (.node(transistor_21_out));
  Pull_Resistor #(.pull(1)) pull_resistor_11 (.node(transistor_8_out));
  Pull_Resistor #(.pull(1)) pull_resistor_12 (.node(transistor_9_out));

  // Notes on the sheet:
  //   GREEN
endmodule

module SEL16x12_B (
  input  PCLK,
  input  _15,
  input  _14,
  input  _13,
  input  _12,
  input  _11,
  input  _10,
  input  _9,
  input  _8,
  input  _7,
  input  _6,
  input  _5,
  input  _4,
  input  _3,
  input  _2,
  input  _1,
  input  _0,
  output OUT0,
  output OUT1,
  output OUT2,
  output OUT3,
  output OUT4,
  output OUT5,
  output OUT6,
  output OUT7,
  output OUT8,
  output OUT9,
  output OUT10,
  output OUT11
);

  wire transistor_1_out, transistor_2_out, transistor_3_out, transistor_4_out, transistor_6_out,
       transistor_7_out, transistor_8_out, transistor_10_out, transistor_13_out, transistor_14_out,
       transistor_18_out, transistor_20_out;

  and and_1 (OUT0, PCLK, transistor_1_out);
  and and_2 (OUT1, PCLK, transistor_10_out);
  and and_3 (OUT2, PCLK, transistor_2_out);
  and and_4 (OUT3, PCLK, transistor_3_out);
  and and_5 (OUT4, PCLK, transistor_4_out);
  and and_6 (OUT5, PCLK, transistor_13_out);
  and and_7 (OUT6, PCLK, transistor_14_out);
  and and_8 (OUT7, PCLK, transistor_6_out);
  and and_9 (OUT8, PCLK, transistor_7_out);
  and and_10 (OUT9, PCLK, transistor_18_out);
  and and_11 (OUT10, PCLK, transistor_20_out);
  and and_12 (OUT11, PCLK, transistor_8_out);
  Transistor #(.\type ("n")) transistor_1 (.in(1'b0), .out(transistor_1_out), .gate(_14));
  Transistor #(.\type ("n")) transistor_2 (.in(1'b0), .out(transistor_2_out), .gate(_15));
  Transistor #(.\type ("n")) transistor_3 (.in(1'b0), .out(transistor_3_out), .gate(_14));
  Transistor #(.\type ("n")) transistor_4 (.in(1'b0), .out(transistor_4_out), .gate(_15));
  Transistor #(.\type ("n")) transistor_5 (.in(1'b0), .out(transistor_4_out), .gate(_14));
  Transistor #(.\type ("n")) transistor_6 (.in(1'b0), .out(transistor_6_out), .gate(_14));
  Transistor #(.\type ("n")) transistor_7 (.in(1'b0), .out(transistor_7_out), .gate(_14));
  Transistor #(.\type ("n")) transistor_8 (.in(1'b0), .out(transistor_8_out), .gate(_14));
  Transistor #(.\type ("n")) transistor_9 (.in(1'b0), .out(transistor_1_out), .gate(_13));
  Transistor #(.\type ("n")) transistor_10 (.in(1'b0), .out(transistor_10_out), .gate(_13));
  Transistor #(.\type ("n")) transistor_11 (.in(1'b0), .out(transistor_2_out), .gate(_12));
  Transistor #(.\type ("n")) transistor_12 (.in(1'b0), .out(transistor_4_out), .gate(_13));
  Transistor #(.\type ("n")) transistor_13 (.in(1'b0), .out(transistor_13_out), .gate(_13));
  Transistor #(.\type ("n")) transistor_14 (.in(1'b0), .out(transistor_14_out), .gate(_13));
  Transistor #(.\type ("n")) transistor_15 (.in(1'b0), .out(transistor_6_out), .gate(_12));
  Transistor #(.\type ("n")) transistor_16 (.in(1'b0), .out(transistor_6_out), .gate(_13));
  Transistor #(.\type ("n")) transistor_17 (.in(1'b0), .out(transistor_7_out), .gate(_13));
  Transistor #(.\type ("n")) transistor_18 (.in(1'b0), .out(transistor_18_out), .gate(_12));
  Transistor #(.\type ("n")) transistor_19 (.in(1'b0), .out(transistor_18_out), .gate(_13));
  Transistor #(.\type ("n")) transistor_20 (.in(1'b0), .out(transistor_20_out), .gate(_13));
  Transistor #(.\type ("n")) transistor_21 (.in(1'b0), .out(transistor_8_out), .gate(_12));
  Transistor #(.\type ("n")) transistor_22 (.in(1'b0), .out(transistor_8_out), .gate(_13));
  Transistor #(.\type ("n")) transistor_23 (.in(1'b0), .out(transistor_2_out), .gate(_11));
  Transistor #(.\type ("n")) transistor_24 (.in(1'b0), .out(transistor_13_out), .gate(_11));
  Transistor #(.\type ("n")) transistor_25 (.in(1'b0), .out(transistor_18_out), .gate(_11));
  Transistor #(.\type ("n")) transistor_26 (.in(1'b0), .out(transistor_1_out), .gate(_10));
  Transistor #(.\type ("n")) transistor_27 (.in(1'b0), .out(transistor_10_out), .gate(_10));
  Transistor #(.\type ("n")) transistor_28 (.in(1'b0), .out(transistor_2_out), .gate(_9));
  Transistor #(.\type ("n")) transistor_29 (.in(1'b0), .out(transistor_2_out), .gate(_10));
  Transistor #(.\type ("n")) transistor_30 (.in(1'b0), .out(transistor_3_out), .gate(_10));
  Transistor #(.\type ("n")) transistor_31 (.in(1'b0), .out(transistor_3_out), .gate(_9));
  Transistor #(.\type ("n")) transistor_32 (.in(1'b0), .out(transistor_13_out), .gate(_10));
  Transistor #(.\type ("n")) transistor_33 (.in(1'b0), .out(transistor_14_out), .gate(_9));
  Transistor #(.\type ("n")) transistor_34 (.in(1'b0), .out(transistor_14_out), .gate(_10));
  Transistor #(.\type ("n")) transistor_35 (.in(1'b0), .out(transistor_6_out), .gate(_10));
  Transistor #(.\type ("n")) transistor_36 (.in(1'b0), .out(transistor_7_out), .gate(_9));
  Transistor #(.\type ("n")) transistor_37 (.in(1'b0), .out(transistor_18_out), .gate(_10));
  Transistor #(.\type ("n")) transistor_38 (.in(1'b0), .out(transistor_18_out), .gate(_9));
  Transistor #(.\type ("n")) transistor_39 (.in(1'b0), .out(transistor_20_out), .gate(_9));
  Transistor #(.\type ("n")) transistor_40 (.in(1'b0), .out(transistor_20_out), .gate(_10));
  Transistor #(.\type ("n")) transistor_41 (.in(1'b0), .out(transistor_8_out), .gate(_10));
  Transistor #(.\type ("n")) transistor_42 (.in(1'b0), .out(transistor_10_out), .gate(_8));
  Transistor #(.\type ("n")) transistor_43 (.in(1'b0), .out(transistor_3_out), .gate(_8));
  Transistor #(.\type ("n")) transistor_44 (.in(1'b0), .out(transistor_4_out), .gate(_8));
  Transistor #(.\type ("n")) transistor_45 (.in(1'b0), .out(transistor_13_out), .gate(_8));
  Transistor #(.\type ("n")) transistor_46 (.in(1'b0), .out(transistor_6_out), .gate(_8));
  Transistor #(.\type ("n")) transistor_47 (.in(1'b0), .out(transistor_18_out), .gate(_8));
  Transistor #(.\type ("n")) transistor_48 (.in(1'b0), .out(transistor_8_out), .gate(_8));
  Transistor #(.\type ("n")) transistor_49 (.in(1'b0), .out(transistor_1_out), .gate(_7));
  Transistor #(.\type ("n")) transistor_50 (.in(1'b0), .out(transistor_10_out), .gate(_6));
  Transistor #(.\type ("n")) transistor_51 (.in(1'b0), .out(transistor_10_out), .gate(_7));
  Transistor #(.\type ("n")) transistor_52 (.in(1'b0), .out(transistor_2_out), .gate(_6));
  Transistor #(.\type ("n")) transistor_53 (.in(1'b0), .out(transistor_2_out), .gate(_7));
  Transistor #(.\type ("n")) transistor_54 (.in(1'b0), .out(transistor_3_out), .gate(_6));
  Transistor #(.\type ("n")) transistor_55 (.in(1'b0), .out(transistor_4_out), .gate(_7));
  Transistor #(.\type ("n")) transistor_56 (.in(1'b0), .out(transistor_13_out), .gate(_6));
  Transistor #(.\type ("n")) transistor_57 (.in(1'b0), .out(transistor_13_out), .gate(_7));
  Transistor #(.\type ("n")) transistor_58 (.in(1'b0), .out(transistor_14_out), .gate(_6));
  Transistor #(.\type ("n")) transistor_59 (.in(1'b0), .out(transistor_6_out), .gate(_6));
  Transistor #(.\type ("n")) transistor_60 (.in(1'b0), .out(transistor_7_out), .gate(_7));
  Transistor #(.\type ("n")) transistor_61 (.in(1'b0), .out(transistor_18_out), .gate(_6));
  Transistor #(.\type ("n")) transistor_62 (.in(1'b0), .out(transistor_20_out), .gate(_6));
  Transistor #(.\type ("n")) transistor_63 (.in(1'b0), .out(transistor_1_out), .gate(_4));
  Transistor #(.\type ("n")) transistor_64 (.in(1'b0), .out(transistor_10_out), .gate(_5));
  Transistor #(.\type ("n")) transistor_65 (.in(1'b0), .out(transistor_2_out), .gate(_4));
  Transistor #(.\type ("n")) transistor_66 (.in(1'b0), .out(transistor_3_out), .gate(_5));
  Transistor #(.\type ("n")) transistor_67 (.in(1'b0), .out(transistor_4_out), .gate(_4));
  Transistor #(.\type ("n")) transistor_68 (.in(1'b0), .out(transistor_13_out), .gate(_4));
  Transistor #(.\type ("n")) transistor_69 (.in(1'b0), .out(transistor_14_out), .gate(_4));
  Transistor #(.\type ("n")) transistor_70 (.in(1'b0), .out(transistor_6_out), .gate(_5));
  Transistor #(.\type ("n")) transistor_71 (.in(1'b0), .out(transistor_7_out), .gate(_4));
  Transistor #(.\type ("n")) transistor_72 (.in(1'b0), .out(transistor_18_out), .gate(_4));
  Transistor #(.\type ("n")) transistor_73 (.in(1'b0), .out(transistor_20_out), .gate(_4));
  Transistor #(.\type ("n")) transistor_74 (.in(1'b0), .out(transistor_8_out), .gate(_4));
  Transistor #(.\type ("n")) transistor_75 (.in(1'b0), .out(transistor_8_out), .gate(_5));
  Transistor #(.\type ("n")) transistor_76 (.in(1'b0), .out(transistor_10_out), .gate(_3));
  Transistor #(.\type ("n")) transistor_77 (.in(1'b0), .out(transistor_2_out), .gate(_3));
  Transistor #(.\type ("n")) transistor_78 (.in(1'b0), .out(transistor_13_out), .gate(_3));
  Transistor #(.\type ("n")) transistor_79 (.in(1'b0), .out(transistor_18_out), .gate(_3));
  Transistor #(.\type ("n")) transistor_80 (.in(1'b0), .out(transistor_20_out), .gate(_3));
  Transistor #(.\type ("n")) transistor_81 (.in(1'b0), .out(transistor_1_out), .gate(_2));
  Transistor #(.\type ("n")) transistor_82 (.in(1'b0), .out(transistor_1_out), .gate(_1));
  Transistor #(.\type ("n")) transistor_83 (.in(1'b0), .out(transistor_10_out), .gate(_2));
  Transistor #(.\type ("n")) transistor_84 (.in(1'b0), .out(transistor_10_out), .gate(_1));
  Transistor #(.\type ("n")) transistor_85 (.in(1'b0), .out(transistor_2_out), .gate(_2));
  Transistor #(.\type ("n")) transistor_86 (.in(1'b0), .out(transistor_3_out), .gate(_1));
  Transistor #(.\type ("n")) transistor_87 (.in(1'b0), .out(transistor_3_out), .gate(_2));
  Transistor #(.\type ("n")) transistor_88 (.in(1'b0), .out(transistor_13_out), .gate(_1));
  Transistor #(.\type ("n")) transistor_89 (.in(1'b0), .out(transistor_13_out), .gate(_2));
  Transistor #(.\type ("n")) transistor_90 (.in(1'b0), .out(transistor_14_out), .gate(_2));
  Transistor #(.\type ("n")) transistor_91 (.in(1'b0), .out(transistor_6_out), .gate(_2));
  Transistor #(.\type ("n")) transistor_92 (.in(1'b0), .out(transistor_6_out), .gate(_1));
  Transistor #(.\type ("n")) transistor_93 (.in(1'b0), .out(transistor_7_out), .gate(_2));
  Transistor #(.\type ("n")) transistor_94 (.in(1'b0), .out(transistor_18_out), .gate(_2));
  Transistor #(.\type ("n")) transistor_95 (.in(1'b0), .out(transistor_18_out), .gate(_1));
  Transistor #(.\type ("n")) transistor_96 (.in(1'b0), .out(transistor_20_out), .gate(_2));
  Transistor #(.\type ("n")) transistor_97 (.in(1'b0), .out(transistor_8_out), .gate(_2));
  Transistor #(.\type ("n")) transistor_98 (.in(1'b0), .out(transistor_1_out), .gate(_0));
  Transistor #(.\type ("n")) transistor_99 (.in(1'b0), .out(transistor_2_out), .gate(_0));
  Transistor #(.\type ("n")) transistor_100 (.in(1'b0), .out(transistor_14_out), .gate(_0));
  Transistor #(.\type ("n")) transistor_101 (.in(1'b0), .out(transistor_7_out), .gate(_0));
  Transistor #(.\type ("n")) transistor_102 (.in(1'b0), .out(transistor_18_out), .gate(_0));
  Transistor #(.\type ("n")) transistor_103 (.in(1'b0), .out(transistor_20_out), .gate(_0));
  Pull_Resistor #(.pull(1)) pull_resistor_1 (.node(transistor_1_out));
  Pull_Resistor #(.pull(1)) pull_resistor_2 (.node(transistor_10_out));
  Pull_Resistor #(.pull(1)) pull_resistor_3 (.node(transistor_2_out));
  Pull_Resistor #(.pull(1)) pull_resistor_4 (.node(transistor_3_out));
  Pull_Resistor #(.pull(1)) pull_resistor_5 (.node(transistor_4_out));
  Pull_Resistor #(.pull(1)) pull_resistor_6 (.node(transistor_13_out));
  Pull_Resistor #(.pull(1)) pull_resistor_7 (.node(transistor_14_out));
  Pull_Resistor #(.pull(1)) pull_resistor_8 (.node(transistor_6_out));
  Pull_Resistor #(.pull(1)) pull_resistor_9 (.node(transistor_7_out));
  Pull_Resistor #(.pull(1)) pull_resistor_10 (.node(transistor_18_out));
  Pull_Resistor #(.pull(1)) pull_resistor_11 (.node(transistor_20_out));
  Pull_Resistor #(.pull(1)) pull_resistor_12 (.node(transistor_8_out));

  // Notes on the sheet:
  //   BLUE
endmodule

// CONTROL UNIT
module CONTROL_UNIT_NTSC (
  input  [1:0] PCLK,
  input  [5:0] Hnn,
  input  nOBCLIP,
  input  nBGCLIP,
  input  HPLA_2,
  input  HPLA_3,
  input  HPLA_4,
  input  HPLA_5,
  input  HPLA_6,
  input  HPLA_7,
  input  HPLA_8,
  input  HPLA_9,
  input  HPLA_10,
  input  HPLA_11,
  input  HPLA_16,
  input  HPLA_13,
  input  HPLA_12,
  input  HPLA_14,
  input  HPLA_15,
  input  HPLA_19,
  input  HPLA_20,
  input  HPLA_0,
  input  HPLA_1,
  input  HPLA_21,
  input  HPLA_22,
  input  HPLA_17,
  input  HPLA_18,
  input  VPLA_1,
  input  VPLA_0,
  input  VPLA_3,
  input  VPLA_2,
  input  VPLA_4,
  input  VPLA_5,
  input  VPLA_6,
  input  VPLA_7,
  input  VPLA_8,
  input  BLACK,
  input  CFG,
  input  HPLA_23,
  input  V8,
  input  RES,
  output H0_prime_prime,
  output H1_prime_prime,
  output H2_prime_prime,
  output H3_prime_prime,
  output H4_prime_prime,
  output H5_prime_prime,
  output H0_prime,
  output nH1_prime,
  output nH2_prime,
  output S_EV,
  output CLIP_O,
  output CLIP_B,
  output _0_HPOS,
  output EVAL,
  output E_EV,
  output I_OAM2,
  output PAR_O,
  output nVIS,
  output nF_NT,
  output F_AT,
  output F_TA,
  output F_TB,
  output nFO,
  output SC_CNT,
  output SYNC,
  output BURST,
  output nPICTURE,
  output nVSET,
  output VB,
  output BLNK,
  output RESCL,
  output VC,
  output HC,
  output E_OUT,
  output VIN
);

  wire and_1_out, and_2_out, and_3_out, and_4_out, d_ff_1_q, d_ff_1_qn, d_ff_2_q, d_latch_1_nq, d_latch_2_q,
       d_latch_3_nq, d_latch_4_nq, d_latch_4_q, d_latch_5_q, d_latch_6_nq, d_latch_6_q, d_latch_7_nq,
       d_latch_8_nq, d_latch_9_nq, d_latch_10_nq, d_latch_11_nq, d_latch_12_nq, d_latch_13_nq, d_latch_14_q,
       d_latch_15_q, d_latch_17_nq, d_latch_18_nq, d_latch_20_q, d_latch_21_q, d_latch_29_q, d_latch_30_q,
       d_latch_31_q, d_latch_32_q, d_latch_33_q, d_latch_34_q, d_latch_36_nq, d_latch_39_nq, d_latch_40_nq,
       d_latch_41_nq, d_latch_42_q, d_latch_43_q, d_latch_44_q, nor_1_out, nor_2_out, nor_3_out, nor_4_out,
       nor_12_out, not_1_out, not_2_out, not_3_out, not_4_out, not_5_out, s_r_ff_1_q, s_r_ff_2_q, s_r_ff_3_q,
       s_r_ff_4_q, s_r_ff_6_q, s_r_ff_7_q, s_r_ff_8_q;

  D_latch d_latch_1 (.EN(PCLK[1]), .D(HPLA_2), .nQ(d_latch_1_nq));  // open: Q
  D_latch d_latch_2 (.EN(PCLK[1]), .D(HPLA_3), .Q(d_latch_2_q));  // open: nQ
  D_latch d_latch_3 (.EN(PCLK[1]), .D(HPLA_4), .nQ(d_latch_3_nq));  // open: Q
  D_latch d_latch_4 (.EN(PCLK[1]), .D(HPLA_5), .Q(d_latch_4_q), .nQ(d_latch_4_nq));
  D_latch d_latch_5 (.EN(PCLK[1]), .D(HPLA_6), .Q(d_latch_5_q));  // open: nQ
  D_latch d_latch_6 (.EN(PCLK[1]), .D(HPLA_7), .Q(d_latch_6_q), .nQ(d_latch_6_nq));
  D_latch d_latch_7 (.EN(PCLK[1]), .D(HPLA_8), .nQ(d_latch_7_nq));  // open: Q
  D_latch d_latch_8 (.EN(PCLK[1]), .D(HPLA_9), .nQ(d_latch_8_nq));  // open: Q
  D_latch d_latch_9 (.EN(PCLK[1]), .D(HPLA_10), .nQ(d_latch_9_nq));  // open: Q
  D_latch d_latch_10 (.EN(PCLK[1]), .D(HPLA_11), .nQ(d_latch_10_nq));  // open: Q
  D_latch d_latch_11 (.EN(PCLK[1]), .D(HPLA_16), .nQ(d_latch_11_nq));  // open: Q
  D_latch d_latch_12 (.EN(PCLK[1]), .D(HPLA_13), .nQ(d_latch_12_nq));  // open: Q
  D_latch d_latch_13 (.EN(PCLK[1]), .D(HPLA_12), .nQ(d_latch_13_nq));  // open: Q
  D_latch d_latch_14 (.EN(PCLK[1]), .D(HPLA_14), .Q(d_latch_14_q));  // open: nQ
  D_latch d_latch_15 (.EN(PCLK[1]), .D(HPLA_15), .Q(d_latch_15_q));  // open: nQ
  D_latch d_latch_16 (.EN(PCLK[1]), .D(VPLA_4), .nQ(nVSET));  // open: Q
  D_latch d_latch_17 (.EN(PCLK[1]), .D(VPLA_8), .nQ(d_latch_17_nq));  // open: Q
  D_latch d_latch_18 (.EN(PCLK[1]), .D(VPLA_2), .nQ(d_latch_18_nq));  // open: Q
  nor nor_1 (nor_1_out, d_latch_2_q, d_latch_3_nq);
  nor nor_2 (nor_2_out, d_latch_4_q, d_latch_5_q, d_latch_6_q);
  nor nor_3 (nor_3_out, d_latch_14_q, d_latch_15_q);
  S_R_Flip_Flop #(.trigger("high")) s_r_ff_1 (
    .S(HPLA_19), .clk(PCLK[1]), .R(HPLA_20), .Q(s_r_ff_1_q));  // open: Qn, preset, reset, en
  S_R_Flip_Flop #(.trigger("high")) s_r_ff_2 (
    .S(HPLA_0), .clk(PCLK[1]), .R(HPLA_1), .Q(s_r_ff_2_q));  // open: Qn, preset, reset, en
  S_R_Flip_Flop #(.trigger("high")) s_r_ff_3 (
    .S(HPLA_21), .clk(PCLK[1]), .R(HPLA_22), .Q(s_r_ff_3_q));  // open: Qn, preset, reset, en
  S_R_Flip_Flop #(.trigger("high")) s_r_ff_4 (
    .S(HPLA_17), .clk(PCLK[1]), .R(HPLA_18), .Q(s_r_ff_4_q));  // open: Qn, preset, reset, en
  and and_1 (and_1_out, s_r_ff_4_q, VPLA_3);
  and and_2 (and_2_out, s_r_ff_4_q, VPLA_2);
  S_R_Flip_Flop #(.trigger("high")) s_r_ff_5 (
    .S(VPLA_5), .clk(PCLK[1]), .R(VPLA_6), .Qn(VB));  // open: Q, preset, reset, en
  S_R_Flip_Flop #(.trigger("high")) s_r_ff_6 (
    .S(VPLA_6), .clk(PCLK[1]), .R(VPLA_7), .Q(s_r_ff_6_q));  // open: Qn, preset, reset, en
  not not_1 (not_1_out, RESCL);
  not not_2 (not_2_out, HPLA_5);
  D_latch d_latch_19 (.EN(PCLK[0]), .D(d_latch_1_nq), .nQ(S_EV));  // open: Q
  D_latch d_latch_20 (.EN(PCLK[0]), .D(nor_1_out), .Q(d_latch_20_q));  // open: nQ
  D_latch d_latch_21 (.EN(PCLK[0]), .D(nor_1_out), .Q(d_latch_21_q));  // open: nQ
  D_latch d_latch_22 (.EN(PCLK[0]), .D(d_latch_4_nq), .nQ(_0_HPOS));  // open: Q
  D_latch d_latch_23 (.EN(PCLK[0]), .D(nor_2_out), .Q(EVAL));  // open: nQ
  D_latch d_latch_24 (.EN(PCLK[0]), .D(d_latch_6_nq), .nQ(E_EV));  // open: Q
  D_latch d_latch_25 (.EN(PCLK[0]), .D(d_latch_7_nq), .nQ(I_OAM2));  // open: Q
  D_latch d_latch_26 (.EN(PCLK[0]), .D(d_latch_8_nq), .nQ(PAR_O));  // open: Q
  D_latch d_latch_27 (.EN(PCLK[0]), .D(d_latch_9_nq), .Q(nVIS));  // open: nQ
  D_latch d_latch_28 (.EN(PCLK[0]), .D(d_latch_10_nq), .Q(nF_NT));  // open: nQ
  D_latch d_latch_29 (.EN(PCLK[0]), .D(d_latch_12_nq), .Q(d_latch_29_q));  // open: nQ
  D_latch d_latch_30 (.EN(PCLK[0]), .D(d_latch_13_nq), .Q(d_latch_30_q));  // open: nQ
  D_latch d_latch_31 (.EN(PCLK[0]), .D(nor_3_out), .Q(d_latch_31_q), .nQ(nFO));
  D_latch d_latch_32 (.EN(PCLK[0]), .D(not_3_out), .Q(d_latch_32_q));  // open: nQ
  not not_3 (not_3_out, s_r_ff_2_q);
  D_latch d_latch_33 (.EN(PCLK[0]), .D(s_r_ff_3_q), .Q(d_latch_33_q));  // open: nQ
  D_latch d_latch_34 (.EN(PCLK[0]), .D(nor_4_out), .Q(d_latch_34_q));  // open: nQ
  D_latch d_latch_35 (.EN(PCLK[0]), .D(d_latch_17_nq), .nQ(RESCL));  // open: Q
  D_Flip_Flop #(.trigger("high")) d_ff_1 (
    .clk(V8), .D(d_ff_2_q), .Q(d_ff_1_q), .Qn(d_ff_1_qn), .reset(RES));  // open: preset, en
  not not_4 (not_4_out, V8);
  nor nor_4 (nor_4_out, s_r_ff_1_q, s_r_ff_8_q);
  and and_3 (and_3_out, s_r_ff_1_q, VPLA_1);
  and and_4 (and_4_out, s_r_ff_1_q, VPLA_0);
  S_R_Flip_Flop #(.trigger("high")) s_r_ff_7 (
    .S(and_1_out), .clk(1'b1), .R(and_2_out), .Q(s_r_ff_7_q));  // open: Qn, preset, reset, en
  nor nor_5 (E_OUT, not_1_out, not_2_out, d_ff_1_q);
  D_Flip_Flop #(.trigger("high")) d_ff_2 (.clk(not_4_out), .D(d_ff_1_qn), .Q(d_ff_2_q));  // open: Qn, preset, en, reset
  D_latch d_latch_36 (.EN(PCLK[1]), .D(Hnn[0]), .Q(H0_prime), .nQ(d_latch_36_nq));
  D_latch d_latch_37 (.EN(PCLK[1]), .D(Hnn[1]), .nQ(nH1_prime));  // open: Q
  D_latch d_latch_38 (.EN(PCLK[1]), .D(Hnn[2]), .nQ(nH2_prime));  // open: Q
  D_latch d_latch_39 (.EN(PCLK[1]), .D(Hnn[3]), .nQ(d_latch_39_nq));  // open: Q
  D_latch d_latch_40 (.EN(PCLK[1]), .D(Hnn[4]), .nQ(d_latch_40_nq));  // open: Q
  D_latch d_latch_41 (.EN(PCLK[1]), .D(Hnn[5]), .nQ(d_latch_41_nq));  // open: Q
  nor nor_6 (CLIP_O, nOBCLIP, d_latch_20_q);
  nor nor_7 (CLIP_B, nBGCLIP, d_latch_21_q);
  nor nor_8 (F_AT, d_latch_11_nq, nor_3_out);
  nor nor_9 (F_TA, d_latch_29_q, d_latch_31_q);
  nor nor_10 (F_TB, d_latch_31_q, d_latch_30_q);
  nor nor_11 (SYNC, d_latch_32_q, d_latch_34_q);
  S_R_Flip_Flop #(.trigger("high")) s_r_ff_8 (
    .S(and_3_out), .clk(1'b1), .R(and_4_out), .Q(s_r_ff_8_q));  // open: Qn, preset, reset, en
  D_latch d_latch_42 (.EN(PCLK[0]), .D(s_r_ff_4_q), .Q(d_latch_42_q));  // open: nQ
  D_latch d_latch_43 (.EN(PCLK[0]), .D(s_r_ff_7_q), .Q(d_latch_43_q));  // open: nQ
  nor nor_12 (nor_12_out, HPLA_23, CFG);
  not not_5 (not_5_out, s_r_ff_1_q);
  nor nor_13 (BURST, SYNC, d_latch_33_q);
  or or_1 (nPICTURE, d_latch_42_q, d_latch_43_q);
  D_latch d_latch_44 (.EN(PCLK[1]), .D(nor_12_out), .Q(d_latch_44_q), .nQ(HC));
  D_latch d_latch_45 (.EN(PCLK[0]), .D(d_latch_36_nq), .nQ(H0_prime_prime));  // open: Q
  D_latch d_latch_46 (.EN(PCLK[0]), .D(nH1_prime), .nQ(H1_prime_prime));  // open: Q
  D_latch d_latch_47 (.EN(PCLK[0]), .D(nH2_prime), .nQ(H2_prime_prime));  // open: Q
  D_latch d_latch_48 (.EN(PCLK[0]), .D(d_latch_39_nq), .nQ(H3_prime_prime));  // open: Q
  D_latch d_latch_49 (.EN(PCLK[0]), .D(d_latch_40_nq), .nQ(H4_prime_prime));  // open: Q
  D_latch d_latch_50 (.EN(PCLK[0]), .D(d_latch_41_nq), .nQ(H5_prime_prime));  // open: Q
  nor nor_14 (SC_CNT, not_5_out, BLACK);
  or or_2 (BLNK, s_r_ff_6_q, BLACK);
  nor nor_15 (VC, d_latch_18_nq, d_latch_44_q);

  assign VIN = HPLA_23;

  // Notes on the sheet:
  //   HPOS control
  //   VPOS control
  //   0
  //   65
  //   0-7, 256-263
  //   0-255
  //   339
  //   63
  //   255
  //   0-63
  //   256-319
  //   0-255
  //   0/1
  //   2/3
  //   4/5
  //   6/7
  //   320-355
  //   0-255
  //   279
  //   304
  //   279
  //   256
  //   323
  //   308
  //   270
  //   328
  //   244
  //   247
  //   241
  //   261
  //   241
  //   240
  //   261
  //   261
  //   340
  //   EVEN/ODD flip/flop
  //   Front porch RS flip/flop
  //   Back porch flip/flop
  //   /FPORCH
  //   BPORCH
  //   BPORCH
  //   /VSET
  //   /HB
  //   VSYNC
  //   /HB
  //   HV COUNTER CONTROL
  //   DELAYED H
  //   BLACK
  //   BLACK
endmodule

module CONTROL_UNIT_PAL (
  input  [1:0] PCLK,
  input  [5:0] Hnn,
  input  nOBCLIP,
  input  nBGCLIP,
  input  HPLA_2,
  input  HPLA_3,
  input  HPLA_4,
  input  HPLA_5,
  input  HPLA_6,
  input  HPLA_7,
  input  HPLA_8,
  input  HPLA_9,
  input  HPLA_10,
  input  HPLA_11,
  input  HPLA_16,
  input  HPLA_13,
  input  HPLA_12,
  input  HPLA_14,
  input  HPLA_15,
  input  HPLA_19,
  input  HPLA_20,
  input  HPLA_0,
  input  HPLA_1,
  input  HPLA_21,
  input  HPLA_22,
  input  HPLA_17,
  input  HPLA_18,
  input  VPLA_1,
  input  VPLA_0,
  input  VPLA_3,
  input  VPLA_2,
  input  VPLA_4,
  input  VPLA_5,
  input  VPLA_6,
  input  VPLA_7,
  input  VPLA_8,
  input  BLACK,
  input  HPLA_23,
  input  VPLA_9,
  output H0_prime_prime,
  output H1_prime_prime,
  output H2_prime_prime,
  output H3_prime_prime,
  output H4_prime_prime,
  output H5_prime_prime,
  output H0_prime,
  output nH1_prime,
  output nH2_prime,
  output S_EV,
  output CLIP_O,
  output CLIP_B,
  output _0_HPOS,
  output EVAL,
  output E_EV,
  output I_OAM2,
  output PAR_O,
  output nVIS,
  output nF_NT,
  output F_AT,
  output F_TA,
  output F_TB,
  output nFO,
  output SC_CNT,
  output SYNC,
  output BURST,
  output nPICTURE,
  output nVSET,
  output VB,
  output BLNK,
  output RESCL,
  output VIN,
  output HC,
  output VC,
  output ZOMG_PAL
);

  wire _5_out, and_1_out, and_2_out, and_3_out, and_4_out, d_latch_1_nq, d_latch_2_q, d_latch_3_nq,
       d_latch_4_nq, d_latch_4_q, d_latch_5_q, d_latch_6_nq, d_latch_6_q, d_latch_7_nq, d_latch_8_nq,
       d_latch_9_nq, d_latch_10_nq, d_latch_11_nq, d_latch_12_nq, d_latch_13_nq, d_latch_14_q, d_latch_15_q,
       d_latch_17_nq, d_latch_19_nq, d_latch_21_q, d_latch_22_q, d_latch_30_q, d_latch_31_q, d_latch_32_q,
       d_latch_33_q, d_latch_34_q, d_latch_35_q, d_latch_37_nq, d_latch_38_nq, d_latch_41_nq, d_latch_42_nq,
       d_latch_43_nq, d_latch_44_q, d_latch_45_q, nor_1_out, nor_2_out, nor_3_out, nor_5_out, not_1_out,
       not_3_out, not_4_out, not_5_out, not_6_out, not_7_out, s_r_ff_1_q, s_r_ff_2_q, s_r_ff_3_q, s_r_ff_4_q,
       s_r_ff_5_q, s_r_ff_6_qn, s_r_ff_7_qn, s_r_ff_8_q, s_r_ff_9_q;

  not not_1 (not_1_out, HPLA_23);
  D_latch d_latch_1 (.EN(PCLK[1]), .D(HPLA_2), .nQ(d_latch_1_nq));  // open: Q
  D_latch d_latch_2 (.EN(PCLK[1]), .D(HPLA_3), .Q(d_latch_2_q));  // open: nQ
  D_latch d_latch_3 (.EN(PCLK[1]), .D(HPLA_4), .nQ(d_latch_3_nq));  // open: Q
  D_latch d_latch_4 (.EN(PCLK[1]), .D(HPLA_5), .Q(d_latch_4_q), .nQ(d_latch_4_nq));
  D_latch d_latch_5 (.EN(PCLK[1]), .D(HPLA_6), .Q(d_latch_5_q));  // open: nQ
  D_latch d_latch_6 (.EN(PCLK[1]), .D(HPLA_7), .Q(d_latch_6_q), .nQ(d_latch_6_nq));
  D_latch d_latch_7 (.EN(PCLK[1]), .D(HPLA_8), .nQ(d_latch_7_nq));  // open: Q
  D_latch d_latch_8 (.EN(PCLK[1]), .D(HPLA_9), .nQ(d_latch_8_nq));  // open: Q
  D_latch d_latch_9 (.EN(PCLK[1]), .D(HPLA_10), .nQ(d_latch_9_nq));  // open: Q
  D_latch d_latch_10 (.EN(PCLK[1]), .D(HPLA_11), .nQ(d_latch_10_nq));  // open: Q
  D_latch d_latch_11 (.EN(PCLK[1]), .D(HPLA_16), .nQ(d_latch_11_nq));  // open: Q
  D_latch d_latch_12 (.EN(PCLK[1]), .D(HPLA_13), .nQ(d_latch_12_nq));  // open: Q
  D_latch d_latch_13 (.EN(PCLK[1]), .D(HPLA_12), .nQ(d_latch_13_nq));  // open: Q
  D_latch d_latch_14 (.EN(PCLK[1]), .D(HPLA_14), .Q(d_latch_14_q));  // open: nQ
  D_latch d_latch_15 (.EN(PCLK[1]), .D(HPLA_15), .Q(d_latch_15_q));  // open: nQ
  D_latch d_latch_16 (.EN(PCLK[1]), .D(VPLA_4), .nQ(nVSET));  // open: Q
  D_latch d_latch_17 (.EN(PCLK[1]), .D(VPLA_8), .nQ(d_latch_17_nq));  // open: Q
  D_latch d_latch_18 (.EN(PCLK[1]), .D(not_1_out), .nQ(HC));  // open: Q
  D_latch d_latch_19 (.EN(PCLK[1]), .D(VPLA_8), .nQ(d_latch_19_nq));  // open: Q
  nor nor_1 (nor_1_out, d_latch_2_q, d_latch_3_nq);
  nor nor_2 (nor_2_out, d_latch_4_q, d_latch_5_q, d_latch_6_q);
  nor nor_3 (nor_3_out, d_latch_14_q, d_latch_15_q);
  S_R_Flip_Flop #(.trigger("high")) s_r_ff_1 (
    .S(HPLA_19), .clk(PCLK[1]), .R(HPLA_20), .Q(s_r_ff_1_q));  // open: Qn, preset, reset, en
  S_R_Flip_Flop #(.trigger("high")) s_r_ff_2 (
    .S(HPLA_0), .clk(PCLK[1]), .R(HPLA_1), .Q(s_r_ff_2_q));  // open: Qn, preset, reset, en
  S_R_Flip_Flop #(.trigger("high")) s_r_ff_3 (
    .S(HPLA_21), .clk(PCLK[1]), .R(HPLA_22), .Q(s_r_ff_3_q));  // open: Qn, preset, reset, en
  S_R_Flip_Flop #(.trigger("high")) s_r_ff_4 (
    .S(HPLA_17), .clk(PCLK[1]), .R(HPLA_18), .Q(s_r_ff_4_q));  // open: Qn, preset, reset, en
  and and_1 (and_1_out, s_r_ff_4_q, VPLA_3);
  and and_2 (and_2_out, s_r_ff_4_q, VPLA_2);
  S_R_Flip_Flop #(.trigger("high")) s_r_ff_5 (
    .S(VPLA_5), .clk(PCLK[1]), .R(VPLA_6), .Q(s_r_ff_5_q));  // open: Qn, preset, reset, en
  not not_2 (VB, s_r_ff_5_q);
  S_R_Flip_Flop #(.trigger("high")) s_r_ff_6 (
    .S(VPLA_6), .clk(PCLK[1]), .R(VPLA_7), .Qn(s_r_ff_6_qn));  // open: Q, preset, reset, en
  S_R_Flip_Flop #(.trigger("high")) s_r_ff_7 (
    .S(VPLA_8), .clk(PCLK[1]), .R(VPLA_9), .Qn(s_r_ff_7_qn));  // open: Q, preset, reset, en
  D_latch d_latch_20 (.EN(PCLK[0]), .D(d_latch_1_nq), .nQ(S_EV));  // open: Q
  D_latch d_latch_21 (.EN(PCLK[0]), .D(nor_1_out), .Q(d_latch_21_q));  // open: nQ
  D_latch d_latch_22 (.EN(PCLK[0]), .D(nor_1_out), .Q(d_latch_22_q));  // open: nQ
  D_latch d_latch_23 (.EN(PCLK[0]), .D(d_latch_4_nq), .nQ(_0_HPOS));  // open: Q
  D_latch d_latch_24 (.D(nor_2_out), .Q(EVAL));  // open: EN, nQ
  D_latch d_latch_25 (.EN(PCLK[0]), .D(d_latch_6_nq), .nQ(E_EV));  // open: Q
  D_latch d_latch_26 (.EN(PCLK[0]), .D(d_latch_7_nq), .nQ(I_OAM2));  // open: Q
  D_latch d_latch_27 (.EN(PCLK[0]), .D(d_latch_8_nq), .nQ(PAR_O));  // open: Q
  D_latch d_latch_28 (.EN(PCLK[0]), .D(d_latch_9_nq), .Q(nVIS));  // open: nQ
  D_latch d_latch_29 (.EN(PCLK[0]), .D(d_latch_10_nq), .Q(nF_NT));  // open: nQ
  D_latch d_latch_30 (.EN(PCLK[0]), .D(d_latch_12_nq), .Q(d_latch_30_q));  // open: nQ
  D_latch d_latch_31 (.EN(PCLK[0]), .D(d_latch_13_nq), .Q(d_latch_31_q));  // open: nQ
  D_latch d_latch_32 (.EN(PCLK[0]), .D(nor_3_out), .Q(d_latch_32_q), .nQ(nFO));
  D_latch d_latch_33 (.EN(PCLK[0]), .D(not_3_out), .Q(d_latch_33_q));  // open: nQ
  not not_3 (not_3_out, s_r_ff_2_q);
  D_latch d_latch_34 (.EN(PCLK[0]), .D(s_r_ff_3_q), .Q(d_latch_34_q));  // open: nQ
  D_latch d_latch_35 (.EN(PCLK[0]), .D(nor_5_out), .Q(d_latch_35_q));  // open: nQ
  and and_3 (and_3_out, s_r_ff_1_q, VPLA_1);
  and and_4 (and_4_out, s_r_ff_1_q, VPLA_0);
  D_latch d_latch_36 (.EN(PCLK[0]), .D(d_latch_17_nq), .nQ(RESCL));  // open: Q
  D_latch d_latch_37 (.EN(PCLK[0]), .D(s_r_ff_7_qn), .nQ(d_latch_37_nq));  // open: Q
  nor nor_4 (SYNC, d_latch_33_q, d_latch_35_q);
  nor nor_5 (nor_5_out, s_r_ff_1_q, s_r_ff_9_q);
  S_R_Flip_Flop #(.trigger("high")) s_r_ff_8 (
    .S(and_1_out), .clk(1'b1), .R(and_2_out), .Q(s_r_ff_8_q));  // open: Qn, preset, reset, en
  D_latch d_latch_38 (.EN(PCLK[1]), .D(Hnn[0]), .Q(H0_prime), .nQ(d_latch_38_nq));
  D_latch d_latch_39 (.EN(PCLK[1]), .D(Hnn[1]), .nQ(nH1_prime));  // open: Q
  D_latch d_latch_40 (.EN(PCLK[1]), .D(Hnn[2]), .nQ(nH2_prime));  // open: Q
  D_latch d_latch_41 (.EN(PCLK[1]), .D(Hnn[3]), .nQ(d_latch_41_nq));  // open: Q
  D_latch d_latch_42 (.EN(PCLK[1]), .D(Hnn[4]), .nQ(d_latch_42_nq));  // open: Q
  D_latch d_latch_43 (.EN(PCLK[1]), .D(Hnn[5]), .nQ(d_latch_43_nq));  // open: Q
  nor nor_6 (CLIP_O, nOBCLIP, d_latch_21_q);
  nor nor_7 (CLIP_B, nBGCLIP, d_latch_22_q);
  nor nor_8 (F_AT, d_latch_11_nq, nor_3_out);
  nor nor_9 (F_TA, d_latch_30_q, d_latch_32_q);
  nor nor_10 (F_TB, d_latch_32_q, d_latch_31_q);
  not not_4 (not_4_out, s_r_ff_1_q);
  S_R_Flip_Flop #(.trigger("high")) s_r_ff_9 (
    .S(and_3_out), .clk(1'b1), .R(and_4_out), .Q(s_r_ff_9_q));  // open: Qn, preset, reset, en
  D_latch d_latch_44 (.EN(PCLK[0]), .D(s_r_ff_4_q), .Q(d_latch_44_q));  // open: nQ
  D_latch d_latch_45 (.EN(PCLK[0]), .D(s_r_ff_8_q), .Q(d_latch_45_q));  // open: nQ
  not not_5 (not_5_out, HC);
  not not_6 (not_6_out, H0_prime);
  nand _5 (_5_out, BLNK, d_latch_37_nq);
  D_latch d_latch_46 (.EN(PCLK[0]), .D(d_latch_38_nq), .nQ(H0_prime_prime));  // open: Q
  D_latch d_latch_47 (.EN(PCLK[0]), .D(nH1_prime), .nQ(H1_prime_prime));  // open: Q
  D_latch d_latch_48 (.EN(PCLK[0]), .D(nH2_prime), .nQ(H2_prime_prime));  // open: Q
  D_latch d_latch_49 (.EN(PCLK[0]), .D(d_latch_41_nq), .nQ(H3_prime_prime));  // open: Q
  D_latch d_latch_50 (.EN(PCLK[0]), .D(d_latch_42_nq), .nQ(H4_prime_prime));  // open: Q
  D_latch d_latch_51 (.EN(PCLK[0]), .D(d_latch_43_nq), .nQ(H5_prime_prime));  // open: Q
  nor nor_11 (SC_CNT, not_4_out, BLACK);
  nor nor_12 (BURST, SYNC, d_latch_34_q);
  or or_1 (nPICTURE, d_latch_44_q, d_latch_45_q);
  nand nand_1 (BLNK, s_r_ff_6_qn, not_7_out);
  not not_7 (not_7_out, BLACK);
  nor _12 (VC, not_5_out, d_latch_19_nq);
  nor _6 (ZOMG_PAL, not_6_out, _5_out, PCLK[1]);

  assign VIN = HPLA_23;

  // Notes on the sheet:
  //   VPOS control
  //   H/V control
  //   HPOS control
  //   65
  //   0-7,256-263
  //   0-255
  //   339
  //   63
  //   255
  //   0-63
  //   256-319
  //   0-255
  //   0/1
  //   2/3
  //   4/5
  //   6/7
  //   320-355
  //   0-255
  //   277
  //   302
  //   277
  //   256
  //   321
  //   306
  //   256
  //   4
  //   269
  //   272
  //   240
  //   1
  //   241
  //   0
  //   240
  //   311
  //   311
  //   340
  //   9
  //   265
  //   Front porch RS flip/flop
  //   Back porch flip/flop
  //   10
  //   7
  //   /FPORCH
  //   BPORCH
  //   BPORCH
  //   /VSET
  //   /HB
  //   3
  //   /HB
  //   VSYNC
  //   DELAYED H
  //   11
  //   4
  //   BLACK
endmodule

// OAM CONTROL
module OAM_CONTROL_PAL (
  input  [1:0] PCLK,
  input  OFETCH,
  input  ZOMG_PAL,
  input  I_OAM2,
  input  H0_prime_prime,
  input  nVIS,
  input  BLNK,
  input  OMFG,
  input  nDBE,
  input  nW3,
  input  PAR_O,
  input  DB0,
  input  DB1,
  input  DB2,
  input  DB3,
  input  DB4,
  input  DB5,
  input  DB6,
  input  DB7,
  input  EVAL,
  input  nH2_prime,
  input  H0_prime,
  input  RESCL,
  input  nR2,
  output nOAM0,
  output nOAM1,
  output nOAM2,
  output nOAM3,
  output nOAM4,
  output nOAM5,
  output nOAM6,
  output nOAM7,
  output nOAM8,
  output SPR_OV,
  output OAMCTR2,
  output DB5_2
);

  wire _6_out, _8_out, _9_out, _10_out, _14_out, _27_out, and_1_out, d_ff_1_qn, d_latch_1_nq, d_latch_2_nq,
       d_latch_3_q, d_latch_4_q, d_latch_5_nq, d_latch_6_q, d_latch_7_q, d_latch_8_q, d_latch_9_q,
       d_latch_10_q, d_latch_11_q, d_latch_12_nq, d_latch_13_nq, d_latch_14_nq, d_latch_15_q,
       multiplexer_1_out, multiplexer_2_out, multiplexer_3_out, multiplexer_4_out, multiplexer_5_out,
       nand_1_out, nand_2_out, nand_3_out, nand_4_out, nor_1_out, nor_2_out, nor_3_out, nor_4_out, nor_5_out,
       nor_6_out, nor_7_out, nor_8_out, nor_9_out, nor_10_out, nor_11_out, nor_12_out, nor_13_out,
       nor_14_out, nor_16_out, nor_17_out, not_1_out, not_2_out, not_3_out, not_4_out, not_5_out, not_6_out,
       not_7_out, not_8_out, not_9_out, not_10_out, not_11_out, not_12_out, not_13_out, not_14_out,
       not_15_out, not_16_out, not_17_out, not_18_out, oam2_counter_1_carry_out, oam2_counter_1_q0,
       oam2_counter_1_q1, oam2_counter_1_q2, oam2_counter_1_q3, oam2_counter_1_q4, oam_counter_1_cout,
       oam_counter_1_out0, oam_counter_1_out1, oam_counter_1_out2, oam_counter_1_out3, oam_counter_1_out4,
       oam_counter_1_out5, oam_counter_1_out6, oam_counter_1_out7, or_1_out, or_2_out;

  nor nor_1 (nor_1_out, I_OAM2, nVIS);
  not not_1 (not_1_out, OMFG);
  nor nor_2 (nor_2_out, nDBE, nW3);
  nand nand_1 (nand_1_out, EVAL, nor_17_out);
  not not_2 (not_2_out, nH2_prime);
  not not_3 (not_3_out, OMFG);
  nor nor_3 (nor_3_out, nR2, nDBE);
  D_latch d_latch_1 (.EN(PCLK[1]), .D(OFETCH), .nQ(d_latch_1_nq));  // open: Q
  D_latch d_latch_2 (.EN(PCLK[1]), .D(BLNK), .nQ(d_latch_2_nq));  // open: Q
  D_latch d_latch_3 (.EN(PCLK[1]), .D(EVAL), .Q(d_latch_3_q));  // open: nQ
  D_latch d_latch_4 (.EN(PCLK[1]), .D(nand_1_out), .Q(d_latch_4_q));  // open: nQ
  and and_1 (and_1_out, PAR_O, not_2_out);
  nor nor_4 (nor_4_out, and_1_out, nor_11_out);
  D_latch d_latch_5 (.EN(PCLK[1]), .D(not_3_out), .nQ(d_latch_5_nq));  // open: Q
  D_latch d_latch_6 (.EN(PCLK[1]), .D(I_OAM2), .Q(d_latch_6_q));  // open: nQ
  not not_4 (not_4_out, nor_3_out);
  nand nand_2 (nand_2_out, nor_1_out, H0_prime_prime);
  or or_1 (or_1_out, H0_prime_prime, nVIS);
  nor nor_5 (nor_5_out, BLNK, not_1_out);
  nor nor_6 (nor_6_out, PCLK[1], d_latch_3_q);
  nor nor_7 (nor_7_out, PCLK[1], d_latch_4_q, nor_4_out);
  nor nor_8 (nor_8_out, d_latch_5_nq, d_latch_6_q);
  nor nor_9 (nor_9_out, PCLK[1], d_latch_1_nq);
  nor nor_10 (nor_10_out, nor_9_out, ZOMG_PAL);
  or or_2 (or_2_out, PCLK[1], d_latch_7_q);
  D_latch d_latch_7 (.EN(PCLK[1]), .D(nand_2_out), .Q(d_latch_7_q));  // open: nQ
  nand nand_3 (nand_3_out, or_1_out, d_latch_2_nq);
  nor nor_11 (nor_11_out, nor_8_out, H0_prime);
  nand nand_4 (nand_4_out, nor_10_out, or_2_out);
  D_latch d_latch_8 (.EN(PCLK[1]), .D(nor_17_out), .Q(d_latch_8_q));  // open: nQ
  D_latch d_latch_9 (.EN(PCLK[1]), .D(OMFG), .Q(d_latch_9_q));  // open: nQ
  nor _8 (_8_out, nor_2_out, _9_out);
  nor _9 (_9_out, _8_out, d_latch_14_nq);
  OAM_COUNTER oam_counter_1 (
    .MODE4(nor_5_out), .STEP(nand_4_out), .LOAD(_10_out), .D0(DB0), .RES(PAR_O), .D1(DB1), .D2(DB2),
    .D3(DB3), .D4(DB4), .D5(DB5), .D6(DB6), .D7(DB7), .out0(oam_counter_1_out0), .out1(oam_counter_1_out1),
    .out2(oam_counter_1_out2), .out3(oam_counter_1_out3), .out4(oam_counter_1_out4),
    .out5(oam_counter_1_out5), .out6(oam_counter_1_out6), .COUT(oam_counter_1_cout), .out7(oam_counter_1_out7));
  OAM2_COUNTER oam2_counter_1 (
    .STEP(nor_7_out), .nPCLK(PCLK[1]), .RES(nor_6_out), .Q0(oam2_counter_1_q0), .Q1(oam2_counter_1_q1),
    .Q2(oam2_counter_1_q2), .Q3(oam2_counter_1_q3), .Q4(oam2_counter_1_q4),
    .CARRY_OUT(oam2_counter_1_carry_out));
  nor _6 (_6_out, nor_2_out, _8_out);
  not not_5 (not_5_out, oam_counter_1_out0);
  not not_6 (not_6_out, oam_counter_1_out1);
  not not_7 (not_7_out, oam_counter_1_out2);
  not not_8 (not_8_out, oam_counter_1_out3);
  not not_9 (not_9_out, oam_counter_1_out4);
  not not_10 (not_10_out, oam_counter_1_out5);
  not not_11 (not_11_out, oam_counter_1_out6);
  not not_12 (not_12_out, oam_counter_1_out7);
  not not_13 (not_13_out, oam2_counter_1_q0);
  not not_14 (not_14_out, oam2_counter_1_q1);
  not not_15 (not_15_out, oam2_counter_1_q2);
  not not_16 (not_16_out, oam2_counter_1_q3);
  not not_17 (not_17_out, oam2_counter_1_q4);
  nor nor_12 (nor_12_out, PCLK[1], d_latch_8_q, d_latch_9_q, H0_prime);
  D_Flip_Flop #(.trigger("low")) d_ff_1 (.clk(PCLK[0]), .D(_6_out), .Qn(d_ff_1_qn));  // open: Q, preset, en, reset
  D_latch d_latch_10 (.EN(PCLK[1]), .D(oam_counter_1_cout), .Q(d_latch_10_q));  // open: nQ
  D_latch d_latch_11 (.EN(PCLK[1]), .D(oam2_counter_1_carry_out), .Q(d_latch_11_q));  // open: nQ
  nor nor_13 (nor_13_out, nor_12_out, nor_14_out);
  nor nor_14 (nor_14_out, nor_13_out, RESCL);
  D_latch d_latch_12 (.EN(PCLK[1]), .D(d_ff_1_qn), .nQ(d_latch_12_nq));  // open: Q
  D_latch d_latch_13 (.EN(PCLK[0]), .D(d_latch_12_nq), .nQ(d_latch_13_nq));  // open: Q
  and _27 (_27_out, nand_4_out, d_latch_10_q);
  and _14 (_14_out, d_latch_11_q, nor_7_out);
  not not_18 (not_18_out, not_4_out);
  D_latch d_latch_14 (.EN(PCLK[1]), .D(d_latch_13_nq), .nQ(d_latch_14_nq));  // open: Q
  Multiplexer #(.enable("false")) multiplexer_1 (
    .in0(not_13_out), .in1(not_8_out), .out(multiplexer_1_out), .sel(nand_3_out));
  Multiplexer #(.enable("false")) multiplexer_2 (
    .in0(not_14_out), .in1(not_9_out), .out(multiplexer_2_out), .sel(nand_3_out));
  Multiplexer #(.enable("false")) multiplexer_3 (
    .in0(not_15_out), .in1(not_10_out), .out(multiplexer_3_out), .sel(nand_3_out));
  Multiplexer #(.enable("false")) multiplexer_4 (
    .in0(not_16_out), .in1(not_11_out), .out(multiplexer_4_out), .sel(nand_3_out));
  Multiplexer #(.enable("false")) multiplexer_5 (
    .in0(not_17_out), .in1(not_12_out), .out(multiplexer_5_out), .sel(nand_3_out));
  nor nor_15 (SPR_OV, I_OAM2, nor_16_out);
  nor nor_16 (nor_16_out, SPR_OV, _27_out, nor_12_out);
  nor nor_17 (nor_17_out, _14_out, OAMCTR2);
  nor nor_18 (OAMCTR2, nor_17_out, nor_6_out);
  D_latch d_latch_15 (.EN(PCLK[0]), .D(d_latch_14_nq), .Q(d_latch_15_q));  // open: nQ
  nor _10 (_10_out, d_latch_15_q, d_latch_13_nq);
  not not_19 (nOAM0, not_5_out);
  not not_20 (nOAM1, not_6_out);
  not not_21 (nOAM2, not_7_out);
  not not_22 (nOAM3, multiplexer_1_out);
  not not_23 (nOAM4, multiplexer_2_out);
  not not_24 (nOAM5, multiplexer_3_out);
  not not_25 (nOAM6, multiplexer_4_out);
  not not_26 (nOAM7, multiplexer_5_out);
  not not_27 (nOAM8, nand_3_out);
  Multiplexer multiplexer_6 (.in0(1'b0), .in1(1'b1), .out(DB5_2), .sel(nor_14_out), .en(not_18_out));

  // Other names for the same wires on the sheet: PCLK_t = PCLK[0]; nPCLK = PCLK[1]

  // Notes on the sheet:
  //   9
  //   10
  //   20
  //   W3'
  //   1
  //   6
  //   4
  //   1
  //   2
  //   OAM CNT2 STEP CONTROL
  //   10
  //   8
  //   21
  //   !!! D-latch PAL
  //   4
  //   3
  //   4
  //   2
  //   /R2'
  //   24
  //   8
  //   7
  //   5
  //   3
  //   !!! NOR PAL
  //   23
  //   OAP
  //   ORES
  //   OSTEP
  //   OAM CNT1 STEP CONTROL
  //   OMSTEP
  //   5
  //   6
  //   FF1
  //   SPRITE OVERFLOW FLAG
  //   TMV
  //   13
  //   FF2
  //   OMV
  //   3
  //   1
  //   PAL W3 ENABLER
  //   9
  //   7
  //   Sprite overflow flag
  //   2
  //   OMV'
  //   TMV'
  //   3
  //   4
  //   1
  //   ASAP
  //   2
  //   MILF
  //   TRI-STATE
endmodule

module CONTROL_REGS_PAL (
  input  RC,
  input  nDBE,
  input  nW0,
  input  DB0,
  input  DB1,
  input  DB2,
  input  DB3,
  input  DB4,
  input  DB5,
  input  DB6,
  input  DB7,
  input  nW1,
  input  [1:0] PCLK,
  input  nVIS,
  input  CLIP_B,
  input  CLIP_O,
  output I1_32,
  output OBSEL,
  output BGSEL,
  output O8_16,
  output nSLAVE,
  output VBL,
  output BW,
  output nBGCLIP,
  output nOBCLIP,
  output CLPB,
  output nCLPO,
  output nTR,
  output nTG,
  output nTB,
  output BLACK
);

  wire d_ff_1_q, d_ff_2_q, d_ff_3_q, d_ff_4_q, d_ff_5_q, d_ff_6_q, d_ff_7_q, d_ff_8_q, d_ff_9_q, d_ff_10_q,
       d_ff_11_q, d_ff_12_q, d_ff_13_q, d_ff_14_q, d_ff_15_q, d_ff_16_q, d_latch_7_nq, d_latch_7_q,
       d_latch_8_nq, d_latch_8_q, d_latch_11_q, d_latch_12_q, d_latch_13_nq, nor_1_out, nor_2_out, nor_3_out,
       nor_5_out, not_1_out, not_2_out, not_4_out, not_7_out;

  D_Flip_Flop #(.trigger("high")) d_ff_1 (.clk(PCLK[1]), .D(nor_3_out), .Q(d_ff_1_q));  // open: Qn, preset, en, reset
  nor nor_1 (nor_1_out, nDBE, nW0);
  nor nor_2 (nor_2_out, nDBE, nW1);
  not not_1 (not_1_out, nor_1_out);
  D_Flip_Flop #(.trigger("high")) d_ff_2 (.clk(nor_1_out), .D(DB2), .Q(d_ff_2_q), .reset(RC));  // open: Qn, preset, en
  D_Flip_Flop #(.trigger("high")) d_ff_3 (.clk(nor_1_out), .D(DB3), .Q(d_ff_3_q), .reset(RC));  // open: Qn, preset, en
  D_Flip_Flop #(.trigger("high")) d_ff_4 (.clk(nor_1_out), .D(DB4), .Q(d_ff_4_q), .reset(RC));  // open: Qn, preset, en
  D_Flip_Flop #(.trigger("high")) d_ff_5 (.clk(nor_1_out), .D(DB5), .Q(d_ff_5_q), .reset(RC));  // open: Qn, preset, en
  D_Flip_Flop #(.trigger("high")) d_ff_6 (.clk(nor_1_out), .D(DB6), .Q(d_ff_6_q), .reset(RC));  // open: Qn, preset, en
  D_Flip_Flop #(.trigger("high")) d_ff_7 (.clk(nor_1_out), .D(DB7), .Q(d_ff_7_q), .reset(RC));  // open: Qn, preset, en
  not not_2 (not_2_out, nor_2_out);
  D_Flip_Flop #(.trigger("high")) d_ff_8 (.clk(nor_2_out), .D(DB0), .Q(d_ff_8_q), .reset(RC));  // open: Qn, preset, en
  D_Flip_Flop #(.trigger("high")) d_ff_9 (.clk(nor_2_out), .D(DB1), .Q(d_ff_9_q), .reset(RC));  // open: Qn, preset, en
  D_Flip_Flop #(.trigger("high")) d_ff_10 (
    .clk(nor_2_out), .D(DB2), .Q(d_ff_10_q), .reset(RC));  // open: Qn, preset, en
  D_Flip_Flop #(.trigger("high")) d_ff_11 (
    .clk(nor_2_out), .D(DB3), .Q(d_ff_11_q), .reset(RC));  // open: Qn, preset, en
  D_Flip_Flop #(.trigger("high")) d_ff_12 (
    .clk(nor_2_out), .D(DB4), .Q(d_ff_12_q), .reset(RC));  // open: Qn, preset, en
  D_Flip_Flop #(.trigger("high")) d_ff_13 (
    .clk(nor_2_out), .D(DB5), .Q(d_ff_13_q), .reset(RC));  // open: Qn, preset, en
  D_Flip_Flop #(.trigger("high")) d_ff_14 (
    .clk(nor_2_out), .D(DB6), .Q(d_ff_14_q), .reset(RC));  // open: Qn, preset, en
  D_Flip_Flop #(.trigger("high")) d_ff_15 (
    .clk(nor_2_out), .D(DB7), .Q(d_ff_15_q), .reset(RC));  // open: Qn, preset, en
  D_Flip_Flop #(.trigger("high")) d_ff_16 (.clk(PCLK[0]), .D(d_ff_1_q), .Q(d_ff_16_q));  // open: Qn, preset, en, reset
  D_latch d_latch_1 (.EN(not_1_out), .D(d_ff_2_q), .nQ(I1_32));  // open: Q
  D_latch d_latch_2 (.EN(not_1_out), .D(d_ff_3_q), .nQ(OBSEL));  // open: Q
  D_latch d_latch_3 (.EN(not_1_out), .D(d_ff_4_q), .nQ(BGSEL));  // open: Q
  D_latch d_latch_4 (.EN(not_1_out), .D(d_ff_5_q), .nQ(O8_16));  // open: Q
  D_latch d_latch_5 (.EN(not_2_out), .D(d_ff_9_q), .Q(nBGCLIP));  // open: nQ
  D_latch d_latch_6 (.EN(not_2_out), .D(d_ff_10_q), .Q(nOBCLIP));  // open: nQ
  D_latch d_latch_7 (.EN(not_2_out), .D(d_ff_11_q), .Q(d_latch_7_q), .nQ(d_latch_7_nq));
  D_latch d_latch_8 (.EN(not_2_out), .D(d_ff_12_q), .Q(d_latch_8_q), .nQ(d_latch_8_nq));
  D_latch d_latch_9 (.EN(not_2_out), .D(d_ff_13_q), .nQ(nTR));  // open: Q
  D_latch d_latch_10 (.EN(not_2_out), .D(d_ff_14_q), .nQ(nTG));  // open: Q
  D_latch d_latch_11 (.EN(PCLK[1]), .D(nVIS), .Q(d_latch_11_q));  // open: nQ
  D_latch d_latch_12 (.EN(PCLK[1]), .D(CLIP_B), .Q(d_latch_12_q));  // open: nQ
  D_latch d_latch_13 (.EN(PCLK[1]), .D(d_ff_16_q), .nQ(d_latch_13_nq));  // open: Q
  nor nor_3 (nor_3_out, d_latch_7_q, d_latch_8_q);
  not not_3 (nTB, d_ff_15_q);
  D_latch d_latch_14 (.EN(PCLK[0]), .D(d_latch_13_nq), .nQ(BLACK));  // open: Q
  not not_4 (not_4_out, d_ff_6_q);
  not not_5 (nSLAVE, not_4_out);
  assign VBL = nor_1_out ? d_ff_7_q : 1'bz;  // Controlled_Buffer controlled_buffer_1
  not not_6 (BW, not_7_out);
  not not_7 (not_7_out, d_ff_8_q);
  nor nor_4 (CLPB, d_latch_11_q, d_latch_7_nq, d_latch_12_q);
  nor nor_5 (nor_5_out, d_latch_11_q, d_latch_8_nq, CLIP_O);
  D_latch d_latch_15 (.EN(PCLK[1]), .D(nor_5_out), .nQ(nCLPO));  // open: Q

  // Notes on the sheet:
  //   PCLK
  //   /PCLK
  //   bits 0 and 1 are in the PPU address generator circuit
  //   !
  //   !
  //   !!! INVERSE LOGIC PAL
  //   !!! INVERSE LOGIC PAL
  //   !
  //   !
  //   !
  //   $2000
  //   $2001
endmodule

module OAM_BUF_CONTROL_RGB (
  input  [1:0] PCLK,
  input  BLNK,
  input  SPR_OV,
  input  nVIS,
  input  OAMCTR2,
  input  H0_prime_prime,
  input  nW4,
  input  nDBE,
  output OB_OAM,
  output nWE,
  output OFETCH
);

  wire _1_out, _3_out, _4_out, d_ff_1_q, d_latch_1_nq, d_latch_2_q, not_1_out, not_2_out;

  not not_1 (not_1_out, H0_prime_prime);
  nor _1 (_1_out, nW4, nDBE);
  nor _7 (OB_OAM, PCLK[1], BLNK);
  nor _4 (_4_out, BLNK, PCLK[0], SPR_OV, nVIS, OAMCTR2, not_1_out);
  D_Flip_Flop d_ff_1 (.clk(PCLK[0]), .D(_1_out), .Q(d_ff_1_q));  // open: Qn, preset, en, reset
  D_latch d_latch_1 (.EN(PCLK[1]), .D(d_ff_1_q), .nQ(d_latch_1_nq));  // open: Q
  D_latch d_latch_2 (.EN(PCLK[0]), .D(d_latch_1_nq), .Q(d_latch_2_q));  // open: nQ
  nor _10 (OFETCH, d_latch_2_q, d_ff_1_q);
  nor _3 (_3_out, _4_out, OFETCH);
  not not_2 (not_2_out, OFETCH);
  assign nWE = not_2_out ? _3_out : 1'bz;  // Controlled_Buffer controlled_buffer_1

  // Notes on the sheet:
  //   5
  //   FF1
  //   TRI-STATE
endmodule

module COLOR_CONTROL_RGB (
  input  [1:0] PCLK,
  input  DB_PAR,
  input  TH_MUX,
  input  nPICTURE,
  input  B_W,
  output nDB_CB,
  output COLOR_EN
);

  wire d_latch_1_q;

  D_latch d_latch_1 (.EN(PCLK[0]), .D(DB_PAR), .Q(d_latch_1_q));  // open: nQ
  nand nand_1 (nDB_CB, d_latch_1_q, TH_MUX);
  nor nor_1 (COLOR_EN, nPICTURE, B_W);

  // Notes on the sheet:
  //   PCLK
endmodule
// PICTURE ADDRESS GEN
module PAR_OLD (
  input  [1:0] PCLK,
  input  OV3,
  input  OV2,
  input  OV1,
  input  OV0,
  input  F_AT,
  input  DB_PAR,
  input  nH1_prime,
  input  SH2,
  input  nH2_prime,
  input  SC_CNT,
  input  RESCL,
  input  E_EV,
  input  l1_32,
  input  TSTEP,
  input  F_TB,
  input  H0,
  input  nF_NT,
  input  BLNK,
  input  O8_16,
  input  OB0,
  input  OB1,
  input  OB2,
  input  OB3,
  input  OB4,
  input  OB5,
  input  OB6,
  input  OB7,
  input  DB0,
  input  DB1,
  input  DB2,
  input  DB3,
  input  DB4,
  input  DB5,
  input  DB6,
  input  DB7,
  input  nW0,
  input  nW5_2,
  input  nW6_1,
  input  nW5_1,
  input  nW6_2,
  input  nDBE,
  input  RC,
  input  PD0,
  input  PD1,
  input  PD2,
  input  PD3,
  input  PD4,
  input  PD5,
  input  PD6,
  input  PD7,
  input  OBSEL,
  input  BGSEL,
  input  PAR_O,
  output THO0,
  output THO1,
  output THO2,
  output THO3,
  output THO4,
  output TVO1,
  output nPA0,
  output nPA1,
  output nPA2,
  output nPA3,
  output nPA4,
  output nPA5,
  output nPA6,
  output nPA7,
  output nPA8,
  output FH0,
  output FH1,
  output nPA9,
  output FH2,
  output nPA10,
  output nPA11,
  output nPA12,
  output nPA13
);

  wire and_1_out, and_2_out, and_3_out, and_4_out, controlled_buffer_1_out, controlled_buffer_2_out,
       controlled_buffer_3_out, controlled_buffer_4_out, controlled_buffer_5_out, controlled_buffer_6_out,
       controlled_buffer_7_out, controlled_buffer_8_out, controlled_buffer_9_out, controlled_buffer_10_out,
       controlled_buffer_11_out, controlled_buffer_12_out, controlled_buffer_13_out,
       controlled_buffer_14_out, controlled_buffer_15_out, controlled_buffer_16_out,
       controlled_buffer_17_out, controlled_buffer_18_out, controlled_buffer_34_out,
       controlled_buffer_35_out, controlled_buffer_36_out, controlled_buffer_37_out,
       controlled_buffer_38_out, controlled_buffer_39_out, controlled_buffer_40_out,
       controlled_buffer_41_out, controlled_buffer_42_out, controlled_buffer_43_out,
       controlled_buffer_54_out, controlled_buffer_55_out, controlled_buffer_56_out, d_ff_4_qn, d_ff_5_q,
       d_ff_6_q, d_ff_7_q, d_ff_8_q, d_ff_9_q, d_ff_10_q, d_ff_11_q, d_ff_12_q, d_ff_13_q, d_ff_14_q,
       d_ff_15_q, d_ff_16_q, d_ff_17_q, d_ff_18_q, d_ff_19_q, d_ff_20_qn, d_latch_1_nq, d_latch_2_nq,
       d_latch_3_nq, d_latch_4_q, d_latch_5_nq, d_latch_6_q, d_latch_7_q, d_latch_8_q, d_latch_9_nq,
       d_latch_10_nq, d_latch_11_nq, d_latch_12_nq, d_latch_13_nq, d_latch_14_nq, d_latch_15_nq,
       d_latch_16_nq, d_latch_17_nq, d_latch_18_nq, d_latch_19_nq, d_latch_20_nq, d_latch_21_nq,
       d_latch_22_nq, d_latch_23_nq, d_latch_24_nq, d_latch_25_nq, d_latch_26_nq, d_latch_27_nq,
       d_latch_28_nq, d_latch_29_nq, d_latch_30_nq, d_latch_31_nq, d_latch_32_nq, d_latch_33_nq,
       d_latch_34_nq, d_latch_35_nq, d_latch_36_nq, d_latch_37_nq, d_latch_38_nq, d_latch_39_nq,
       d_latch_40_nq, d_latch_41_nq, d_latch_42_nq, d_latch_43_nq, d_latch_44_nq, d_latch_45_nq,
       d_latch_46_nq, d_latch_47_nq, d_latch_48_nq, d_latch_49_nq, d_latch_50_nq, d_latch_51_nq,
       d_latch_52_nq, d_latch_53_nq, d_latch_54_nq, d_latch_55_nq, d_latch_56_nq, d_latch_57_nq,
       d_latch_58_nq, d_latch_59_nq, d_latch_60_nq, d_latch_61_nq, d_latch_62_nq, d_latch_63_nq,
       d_latch_64_nq, d_latch_65_nq, d_latch_66_nq, d_latch_67_nq, DBE, multiplexer_1_out, multiplexer_2_out,
       multiplexer_3_out, multiplexer_4_out, multiplexer_5_out, multiplexer_6_out, multiplexer_7_out,
       multiplexer_8_out, multiplexer_9_out, multiplexer_10_out, multiplexer_11_out, multiplexer_12_out,
       multiplexer_13_out, multiplexer_14_out, multiplexer_15_out, nand_1_out, nFVO0, nFVO1, nFVO2,
       nor_6_out, nor_7_out, nor_8_out, nor_11_out, nor_12_out, nor_13_out, nor_14_out, nor_15_out,
       nor_16_out, nor_19_out, nor_20_out, nor_21_out, nor_22_out, nor_23_out, nor_24_out, nor_25_out,
       nor_26_out, nor_27_out, not_1_out, not_3_out, not_4_out, not_5_out, not_6_out, not_7_out, not_8_out,
       not_9_out, not_10_out, not_11_out, not_12_out, not_13_out, not_14_out, not_15_out, not_16_out,
       not_17_out, not_18_out, not_19_out, not_20_out, not_21_out, nW0_prime, nW5_1_prime, nW5_2_prime,
       nW6_1_prime, nW6_2_prime, or_1_out, par_1bit_counter_1_carry_out, par_1bit_counter_1_q,
       par_1bit_counter_2_carry_out, par_1bit_counter_2_q, par_3bit_counter_1_fvz, par_3bit_counter_1_q0,
       par_3bit_counter_1_q1, par_3bit_counter_1_q2, par_5bit_counter_1_nq1, par_5bit_counter_1_txz,
       par_5bit_counter_1_txzb, par_5bit_counter_2_nq1, par_5bit_counter_2_q0, par_5bit_counter_2_q2,
       par_5bit_counter_2_q3, par_5bit_counter_2_q4, par_5bit_counter_2_txz, par_5bit_counter_2_txzb,
       s_r_ff_1_q, THLOAD, THSTEP, TVLOAD, TVSTEP, xnor_1_out, xnor_2_out, xnor_3_out, xnor_4_out;

  and and_1 (and_1_out, F_TB, H0);
  not not_1 (not_1_out, H0);
  nor nor_1 (nW0_prime, nW0, nDBE);
  nor nor_2 (nW5_2_prime, nW5_2, nDBE);
  nor nor_3 (nW6_1_prime, nW6_1, nDBE);
  nor nor_4 (nW5_1_prime, nW5_1, nDBE);
  nor nor_5 (nW6_2_prime, nW6_2, nDBE);
  not not_2 (DBE, nDBE);
  assign controlled_buffer_1_out = nW5_1_prime ? DB0 : 1'bz;  // Controlled_Buffer controlled_buffer_1
  assign controlled_buffer_2_out = nW5_1_prime ? DB1 : 1'bz;  // Controlled_Buffer controlled_buffer_2
  assign controlled_buffer_3_out = nW5_1_prime ? DB2 : 1'bz;  // Controlled_Buffer controlled_buffer_3
  D_latch d_latch_1 (.EN(PCLK[1]), .D(E_EV), .nQ(d_latch_1_nq));  // open: Q
  nor nor_6 (nor_6_out, E_EV, TSTEP);
  nor nor_7 (nor_7_out, TSTEP, and_1_out);
  not not_3 (not_3_out, nor_8_out);
  nor nor_8 (nor_8_out, not_1_out, nF_NT);
  D_Flip_Flop #(.trigger("high")) d_ff_1 (
    .clk(DBE), .D(controlled_buffer_1_out), .Q(FH0), .reset(RC));  // open: Qn, preset, en
  D_Flip_Flop #(.trigger("high")) d_ff_2 (
    .clk(DBE), .D(controlled_buffer_2_out), .Q(FH1), .reset(RC));  // open: Qn, preset, en
  D_Flip_Flop #(.trigger("high")) d_ff_3 (
    .clk(DBE), .D(controlled_buffer_3_out), .Q(FH2), .reset(RC));  // open: Qn, preset, en
  D_latch d_latch_2 (.EN(PCLK[0]), .D(SC_CNT), .nQ(d_latch_2_nq));  // open: Q
  D_latch d_latch_3 (.EN(PCLK[0]), .D(d_latch_1_nq), .nQ(d_latch_3_nq));  // open: Q
  nor nor_9 (TVSTEP, nor_6_out, PCLK[0]);
  nor nor_10 (THSTEP, PCLK[0], nor_7_out);
  D_latch d_latch_4 (.EN(PCLK[1]), .D(not_3_out), .Q(d_latch_4_q));  // open: nQ
  not not_4 (not_4_out, d_latch_2_nq);
  and and_2 (and_2_out, not_4_out, RESCL);
  nor nor_11 (nor_11_out, PCLK[1], d_latch_4_q);
  assign controlled_buffer_4_out = nW5_1_prime ? DB3 : 1'bz;  // Controlled_Buffer controlled_buffer_4
  assign controlled_buffer_5_out = nW5_1_prime ? DB4 : 1'bz;  // Controlled_Buffer controlled_buffer_5
  assign controlled_buffer_6_out = nW5_1_prime ? DB5 : 1'bz;  // Controlled_Buffer controlled_buffer_6
  assign controlled_buffer_7_out = nW5_1_prime ? DB6 : 1'bz;  // Controlled_Buffer controlled_buffer_7
  assign controlled_buffer_8_out = nW5_1_prime ? DB7 : 1'bz;  // Controlled_Buffer controlled_buffer_8
  assign controlled_buffer_9_out = nW5_2_prime ? DB3 : 1'bz;  // Controlled_Buffer controlled_buffer_9
  assign controlled_buffer_10_out = nW5_2_prime ? DB4 : 1'bz;  // Controlled_Buffer controlled_buffer_10
  assign controlled_buffer_11_out = nW5_2_prime ? DB5 : 1'bz;  // Controlled_Buffer controlled_buffer_11
  assign controlled_buffer_12_out = nW5_2_prime ? DB6 : 1'bz;  // Controlled_Buffer controlled_buffer_12
  assign controlled_buffer_13_out = nW5_2_prime ? DB7 : 1'bz;  // Controlled_Buffer controlled_buffer_13
  assign controlled_buffer_14_out = nW0_prime ? DB0 : 1'bz;  // Controlled_Buffer controlled_buffer_14
  assign controlled_buffer_15_out = nW0_prime ? DB1 : 1'bz;  // Controlled_Buffer controlled_buffer_15
  assign controlled_buffer_16_out = nW5_2_prime ? DB0 : 1'bz;  // Controlled_Buffer controlled_buffer_16
  assign controlled_buffer_17_out = nW5_2_prime ? DB1 : 1'bz;  // Controlled_Buffer controlled_buffer_17
  assign controlled_buffer_18_out = nW5_2_prime ? DB2 : 1'bz;  // Controlled_Buffer controlled_buffer_18
  S_R_Flip_Flop s_r_ff_1 (.Q(s_r_ff_1_q), .preset(nW6_2_prime), .reset(and_3_out));  // open: S, clk, R, Qn, en
  and and_3 (and_3_out, PCLK[1], d_latch_8_q);
  assign controlled_buffer_4_out = nW6_2_prime ? DB0 : 1'bz;  // Controlled_Buffer controlled_buffer_19
  assign controlled_buffer_5_out = nW6_2_prime ? DB1 : 1'bz;  // Controlled_Buffer controlled_buffer_20
  assign controlled_buffer_6_out = nW6_2_prime ? DB2 : 1'bz;  // Controlled_Buffer controlled_buffer_21
  assign controlled_buffer_7_out = nW6_2_prime ? DB3 : 1'bz;  // Controlled_Buffer controlled_buffer_22
  assign controlled_buffer_8_out = nW6_2_prime ? DB4 : 1'bz;  // Controlled_Buffer controlled_buffer_23
  and and_4 (and_4_out, l1_32, BLNK);
  assign controlled_buffer_9_out = nW6_2_prime ? DB5 : 1'bz;  // Controlled_Buffer controlled_buffer_24
  assign controlled_buffer_10_out = nW6_2_prime ? DB6 : 1'bz;  // Controlled_Buffer controlled_buffer_25
  assign controlled_buffer_11_out = nW6_2_prime ? DB7 : 1'bz;  // Controlled_Buffer controlled_buffer_26
  assign controlled_buffer_12_out = nW6_1_prime ? DB0 : 1'bz;  // Controlled_Buffer controlled_buffer_27
  assign controlled_buffer_13_out = nW6_1_prime ? DB1 : 1'bz;  // Controlled_Buffer controlled_buffer_28
  assign controlled_buffer_14_out = nW6_1_prime ? DB2 : 1'bz;  // Controlled_Buffer controlled_buffer_29
  assign controlled_buffer_15_out = nW6_1_prime ? DB3 : 1'bz;  // Controlled_Buffer controlled_buffer_30
  assign controlled_buffer_16_out = nW6_1_prime ? DB4 : 1'bz;  // Controlled_Buffer controlled_buffer_31
  assign controlled_buffer_17_out = nW6_1_prime ? DB5 : 1'bz;  // Controlled_Buffer controlled_buffer_32
  assign controlled_buffer_18_out = nW6_1_prime ? 1'b0 : 1'bz;  // Controlled_Buffer controlled_buffer_33
  nor nor_12 (nor_12_out, s_r_ff_1_q, nW6_2_prime);
  nor nor_13 (nor_13_out, par_5bit_counter_1_txzb, and_4_out, par_3bit_counter_1_fvz);
  not not_5 (not_5_out, TVSTEP);
  D_latch d_latch_5 (.EN(PCLK[0]), .D(par_5bit_counter_2_txz), .nQ(d_latch_5_nq));  // open: Q
  D_Flip_Flop #(.trigger("high")) d_ff_4 (.clk(PCLK[1]), .D(nor_12_out), .Qn(d_ff_4_qn));  // open: Q, preset, en, reset
  D_Flip_Flop #(.trigger("high")) d_ff_5 (
    .clk(DBE), .D(controlled_buffer_4_out), .Q(d_ff_5_q), .reset(RC));  // open: Qn, preset, en
  D_Flip_Flop #(.trigger("high")) d_ff_6 (
    .clk(DBE), .D(controlled_buffer_5_out), .Q(d_ff_6_q), .reset(RC));  // open: Qn, preset, en
  D_Flip_Flop #(.trigger("high")) d_ff_7 (
    .clk(DBE), .D(controlled_buffer_6_out), .Q(d_ff_7_q), .reset(RC));  // open: Qn, preset, en
  D_Flip_Flop #(.trigger("high")) d_ff_8 (
    .clk(DBE), .D(controlled_buffer_7_out), .Q(d_ff_8_q), .reset(RC));  // open: Qn, preset, en
  D_Flip_Flop #(.trigger("high")) d_ff_9 (
    .clk(DBE), .D(controlled_buffer_8_out), .Q(d_ff_9_q), .reset(RC));  // open: Qn, preset, en
  not not_6 (not_6_out, nor_13_out);
  D_Flip_Flop #(.trigger("high")) d_ff_10 (
    .clk(DBE), .D(controlled_buffer_9_out), .Q(d_ff_10_q), .reset(RC));  // open: Qn, preset, en
  D_Flip_Flop #(.trigger("high")) d_ff_11 (
    .clk(DBE), .D(controlled_buffer_10_out), .Q(d_ff_11_q), .reset(RC));  // open: Qn, preset, en
  D_Flip_Flop #(.trigger("high")) d_ff_12 (
    .clk(DBE), .D(controlled_buffer_11_out), .Q(d_ff_12_q), .reset(RC));  // open: Qn, preset, en
  D_Flip_Flop #(.trigger("high")) d_ff_13 (
    .clk(DBE), .D(controlled_buffer_12_out), .Q(d_ff_13_q), .reset(RC));  // open: Qn, preset, en
  D_Flip_Flop #(.trigger("high")) d_ff_14 (
    .clk(DBE), .D(controlled_buffer_13_out), .Q(d_ff_14_q), .reset(RC));  // open: Qn, preset, en
  D_latch d_latch_6 (.EN(PCLK[1]), .D(not_5_out), .Q(d_latch_6_q));  // open: nQ
  D_latch d_latch_7 (.EN(PCLK[1]), .D(d_latch_5_nq), .Q(d_latch_7_q));  // open: nQ
  D_Flip_Flop #(.trigger("high")) d_ff_15 (
    .clk(DBE), .D(controlled_buffer_14_out), .Q(d_ff_15_q), .reset(RC));  // open: Qn, preset, en
  D_Flip_Flop #(.trigger("high")) d_ff_16 (
    .clk(DBE), .D(controlled_buffer_15_out), .Q(d_ff_16_q), .reset(RC));  // open: Qn, preset, en
  D_Flip_Flop #(.trigger("high")) d_ff_17 (
    .clk(DBE), .D(controlled_buffer_16_out), .Q(d_ff_17_q), .reset(RC));  // open: Qn, preset, en
  D_Flip_Flop #(.trigger("high")) d_ff_18 (
    .clk(DBE), .D(controlled_buffer_17_out), .Q(d_ff_18_q), .reset(RC));  // open: Qn, preset, en
  D_Flip_Flop #(.trigger("high")) d_ff_19 (
    .clk(DBE), .D(controlled_buffer_18_out), .Q(d_ff_19_q), .reset(RC));  // open: Qn, preset, en
  D_latch d_latch_8 (.EN(PCLK[0]), .D(d_ff_4_qn), .Q(d_latch_8_q));  // open: nQ
  nor nor_14 (nor_14_out, d_latch_6_q, d_latch_7_q);
  nor nor_15 (nor_15_out, and_2_out, d_latch_8_q);
  nor nor_16 (nor_16_out, d_latch_8_q, d_latch_3_nq);
  nand nand_1 (nand_1_out, l1_32, BLNK);
  nor nor_17 (TVLOAD, nor_15_out, PCLK[0]);
  nor nor_18 (THLOAD, PCLK[0], nor_16_out);
  PAR_5BIT_COUNTER par_5bit_counter_1 (
    .IN_NOR7_1(1'b1), .BLNK(BLNK), .STEP(THSTEP), .LOAD(THLOAD), .PCLK(PCLK[0]), .IN0(d_ff_5_q), .RES(1'b0),
    .CARRY_IN(nand_1_out), .IN1(d_ff_6_q), .IN2(d_ff_7_q), .IN3(d_ff_8_q), .IN4(d_ff_9_q),
    .TxZ(par_5bit_counter_1_txz), .TxZB(par_5bit_counter_1_txzb), .CFG(par_5bit_counter_1_nq1), .Q0(THO0),
    .Q1(THO1), .nQ1(par_5bit_counter_1_nq1), .Q2(THO2), .Q3(THO3), .Q4(THO4));
  PAR_5BIT_COUNTER par_5bit_counter_2 (
    .IN_NOR7_1(not_6_out), .BLNK(BLNK), .STEP(TVSTEP), .LOAD(TVLOAD), .PCLK(PCLK[0]), .IN0(d_ff_10_q),
    .RES(nor_14_out), .CARRY_IN(not_6_out), .IN1(d_ff_11_q), .IN2(d_ff_12_q), .IN3(d_ff_13_q),
    .IN4(d_ff_14_q), .TxZ(par_5bit_counter_2_txz), .TxZB(par_5bit_counter_2_txzb), .CFG(TVO1),
    .Q0(par_5bit_counter_2_q0), .Q1(TVO1), .nQ1(par_5bit_counter_2_nq1), .Q2(par_5bit_counter_2_q2),
    .Q3(par_5bit_counter_2_q3), .Q4(par_5bit_counter_2_q4));
  PAR_1BIT_COUNTER par_1bit_counter_1 (
    .STEP(THSTEP), .LOAD(THLOAD), .PCLK(PCLK[0]), .IN(d_ff_15_q), .CARRY_IN(not_8_out), .BLNK(BLNK),
    .Q(par_1bit_counter_1_q), .CARRY_OUT(par_1bit_counter_1_carry_out));
  PAR_1BIT_COUNTER par_1bit_counter_2 (
    .STEP(TVSTEP), .LOAD(TVLOAD), .PCLK(PCLK[0]), .IN(d_ff_16_q), .CARRY_IN(not_9_out), .BLNK(BLNK),
    .Q(par_1bit_counter_2_q), .CARRY_OUT(par_1bit_counter_2_carry_out));
  PAR_3BIT_COUNTER par_3bit_counter_1 (
    .FVZ_IN(nor_21_out), .BLNK(BLNK), .STEP(TVSTEP), .LOAD(TVLOAD), .PCLK(PCLK[0]), .IN0(d_ff_17_q),
    .CARRY_IN(not_10_out), .IN1(d_ff_18_q), .IN2(d_ff_19_q), .FVZ(par_3bit_counter_1_fvz),
    .Q0(par_3bit_counter_1_q0), .nQ0(nFVO0), .Q1(par_3bit_counter_1_q1), .nQ1(nFVO1),
    .Q2(par_3bit_counter_1_q2), .nQ2(nFVO2));
  not not_7 (not_7_out, BLNK);
  nor nor_19 (nor_19_out, par_5bit_counter_1_txz, par_5bit_counter_2_txzb);
  not not_8 (not_8_out, nor_19_out);
  nor nor_20 (nor_20_out, par_5bit_counter_2_txz, par_1bit_counter_1_carry_out);
  not not_9 (not_9_out, nor_20_out);
  not not_10 (not_10_out, nor_21_out);
  nor nor_21 (nor_21_out, par_1bit_counter_2_carry_out, not_7_out);
  nor nor_22 (nor_22_out, nFVO0, not_7_out);
  nor nor_23 (nor_23_out, not_7_out, par_3bit_counter_1_q1);
  not not_11 (not_11_out, nor_23_out);
  assign controlled_buffer_34_out = nor_24_out ? THO0 : 1'bz;  // Controlled_Buffer controlled_buffer_34
  assign controlled_buffer_35_out = nor_24_out ? THO1 : 1'bz;  // Controlled_Buffer controlled_buffer_35
  assign controlled_buffer_36_out = nor_24_out ? THO2 : 1'bz;  // Controlled_Buffer controlled_buffer_36
  assign controlled_buffer_37_out = nor_24_out ? THO3 : 1'bz;  // Controlled_Buffer controlled_buffer_37
  assign controlled_buffer_38_out = nor_24_out ? THO4 : 1'bz;  // Controlled_Buffer controlled_buffer_38
  assign controlled_buffer_39_out = nor_24_out ? par_5bit_counter_2_q0 : 1'bz;  // Controlled_Buffer controlled_buffer_39
  assign controlled_buffer_40_out = nor_24_out ? TVO1 : 1'bz;  // Controlled_Buffer controlled_buffer_40
  assign controlled_buffer_41_out = nor_24_out ? par_5bit_counter_2_q2 : 1'bz;  // Controlled_Buffer controlled_buffer_41
  nor nor_24 (nor_24_out, not_12_out, DB_PAR);
  not not_12 (not_12_out, nor_25_out);
  assign controlled_buffer_42_out = nor_25_out ? par_5bit_counter_2_q3 : 1'bz;  // Controlled_Buffer controlled_buffer_42
  assign controlled_buffer_43_out = nor_25_out ? par_5bit_counter_2_q4 : 1'bz;  // Controlled_Buffer controlled_buffer_43
  or or_1 (or_1_out, nor_25_out, F_AT);
  assign controlled_buffer_34_out = F_AT ? THO2 : 1'bz;  // Controlled_Buffer controlled_buffer_44
  assign controlled_buffer_35_out = F_AT ? THO3 : 1'bz;  // Controlled_Buffer controlled_buffer_45
  assign controlled_buffer_36_out = F_AT ? THO4 : 1'bz;  // Controlled_Buffer controlled_buffer_46
  assign controlled_buffer_37_out = F_AT ? par_5bit_counter_2_q2 : 1'bz;  // Controlled_Buffer controlled_buffer_47
  assign controlled_buffer_38_out = F_AT ? par_5bit_counter_2_q3 : 1'bz;  // Controlled_Buffer controlled_buffer_48
  assign controlled_buffer_39_out = F_AT ? par_5bit_counter_2_q4 : 1'bz;  // Controlled_Buffer controlled_buffer_49
  assign controlled_buffer_40_out = F_AT ? 1'b1 : 1'bz;  // Controlled_Buffer controlled_buffer_50
  assign controlled_buffer_41_out = F_AT ? 1'b1 : 1'bz;  // Controlled_Buffer controlled_buffer_51
  assign controlled_buffer_42_out = F_AT ? 1'b1 : 1'bz;  // Controlled_Buffer controlled_buffer_52
  assign controlled_buffer_43_out = F_AT ? 1'b1 : 1'bz;  // Controlled_Buffer controlled_buffer_53
  nor nor_25 (nor_25_out, nor_27_out, F_AT);
  assign controlled_buffer_54_out = or_1_out ? par_1bit_counter_1_q : 1'bz;  // Controlled_Buffer controlled_buffer_54
  assign controlled_buffer_55_out = or_1_out ? par_1bit_counter_2_q : 1'bz;  // Controlled_Buffer controlled_buffer_55
  assign controlled_buffer_56_out = or_1_out ? nor_22_out : 1'bz;  // Controlled_Buffer controlled_buffer_56
  D_latch d_latch_9 (.EN(or_1_out), .D(not_11_out), .nQ(d_latch_9_nq));  // open: Q
  assign controlled_buffer_34_out = DB_PAR ? DB0 : 1'bz;  // Controlled_Buffer controlled_buffer_57
  assign controlled_buffer_35_out = DB_PAR ? DB1 : 1'bz;  // Controlled_Buffer controlled_buffer_58
  assign controlled_buffer_36_out = DB_PAR ? DB2 : 1'bz;  // Controlled_Buffer controlled_buffer_59
  assign controlled_buffer_37_out = DB_PAR ? DB3 : 1'bz;  // Controlled_Buffer controlled_buffer_60
  assign controlled_buffer_38_out = DB_PAR ? DB4 : 1'bz;  // Controlled_Buffer controlled_buffer_61
  assign controlled_buffer_39_out = DB_PAR ? DB5 : 1'bz;  // Controlled_Buffer controlled_buffer_62
  assign controlled_buffer_40_out = DB_PAR ? DB6 : 1'bz;  // Controlled_Buffer controlled_buffer_63
  assign controlled_buffer_41_out = DB_PAR ? DB7 : 1'bz;  // Controlled_Buffer controlled_buffer_64
  not not_13 (not_13_out, PD0);
  not not_14 (not_14_out, PD1);
  not not_15 (not_15_out, PD2);
  not not_16 (not_16_out, PD3);
  not not_17 (not_17_out, PD4);
  not not_18 (not_18_out, PD5);
  not not_19 (not_19_out, PD6);
  not not_20 (not_20_out, PD7);
  nor nor_26 (nor_26_out, SH2, PCLK[1]);
  D_latch d_latch_10 (.EN(PCLK[1]), .D(OV0), .nQ(d_latch_10_nq));  // open: Q
  D_latch d_latch_11 (.EN(PCLK[1]), .D(OV1), .nQ(d_latch_11_nq));  // open: Q
  D_latch d_latch_12 (.EN(PCLK[1]), .D(OV2), .nQ(d_latch_12_nq));  // open: Q
  D_latch d_latch_13 (.EN(PCLK[1]), .D(OV3), .nQ(d_latch_13_nq));  // open: Q
  D_latch d_latch_14 (.EN(PCLK[1]), .D(not_13_out), .nQ(d_latch_14_nq));  // open: Q
  D_latch d_latch_15 (.EN(PCLK[1]), .D(not_14_out), .nQ(d_latch_15_nq));  // open: Q
  D_latch d_latch_16 (.EN(PCLK[1]), .D(not_15_out), .nQ(d_latch_16_nq));  // open: Q
  D_latch d_latch_17 (.EN(PCLK[1]), .D(not_16_out), .nQ(d_latch_17_nq));  // open: Q
  D_latch d_latch_18 (.EN(PCLK[1]), .D(not_17_out), .nQ(d_latch_18_nq));  // open: Q
  D_latch d_latch_19 (.EN(PCLK[1]), .D(not_18_out), .nQ(d_latch_19_nq));  // open: Q
  D_latch d_latch_20 (.EN(PCLK[1]), .D(not_19_out), .nQ(d_latch_20_nq));  // open: Q
  D_latch d_latch_21 (.EN(PCLK[1]), .D(not_20_out), .nQ(d_latch_21_nq));  // open: Q
  D_Flip_Flop #(.trigger("high")) d_ff_20 (
    .clk(PCLK[0]), .D(OB7), .Qn(d_ff_20_qn), .en(nor_26_out));  // open: Q, preset, reset
  D_latch d_latch_22 (.EN(nor_11_out), .D(d_latch_10_nq), .nQ(d_latch_22_nq));  // open: Q
  D_latch d_latch_23 (.EN(nor_11_out), .D(d_latch_11_nq), .nQ(d_latch_23_nq));  // open: Q
  D_latch d_latch_24 (.EN(nor_11_out), .D(d_latch_12_nq), .nQ(d_latch_24_nq));  // open: Q
  D_latch d_latch_25 (.EN(nor_11_out), .D(d_latch_13_nq), .nQ(d_latch_25_nq));  // open: Q
  D_latch d_latch_26 (.EN(nor_11_out), .D(d_latch_14_nq), .nQ(d_latch_26_nq));  // open: Q
  D_latch d_latch_27 (.EN(nor_11_out), .D(OB0), .nQ(d_latch_27_nq));  // open: Q
  D_latch d_latch_28 (.EN(nor_11_out), .D(d_latch_15_nq), .nQ(d_latch_28_nq));  // open: Q
  D_latch d_latch_29 (.EN(nor_11_out), .D(OB1), .nQ(d_latch_29_nq));  // open: Q
  D_latch d_latch_30 (.EN(nor_11_out), .D(d_latch_16_nq), .nQ(d_latch_30_nq));  // open: Q
  D_latch d_latch_31 (.EN(nor_11_out), .D(OB2), .nQ(d_latch_31_nq));  // open: Q
  D_latch d_latch_32 (.EN(nor_11_out), .D(d_latch_17_nq), .nQ(d_latch_32_nq));  // open: Q
  D_latch d_latch_33 (.EN(nor_11_out), .D(OB3), .nQ(d_latch_33_nq));  // open: Q
  D_latch d_latch_34 (.EN(nor_11_out), .D(d_latch_18_nq), .nQ(d_latch_34_nq));  // open: Q
  D_latch d_latch_35 (.EN(nor_11_out), .D(OB4), .nQ(d_latch_35_nq));  // open: Q
  D_latch d_latch_36 (.EN(nor_11_out), .D(d_latch_19_nq), .nQ(d_latch_36_nq));  // open: Q
  D_latch d_latch_37 (.EN(nor_11_out), .D(OB5), .nQ(d_latch_37_nq));  // open: Q
  D_latch d_latch_38 (.EN(nor_11_out), .D(d_latch_20_nq), .nQ(d_latch_38_nq));  // open: Q
  D_latch d_latch_39 (.EN(nor_11_out), .D(OB6), .nQ(d_latch_39_nq));  // open: Q
  D_latch d_latch_40 (.EN(nor_11_out), .D(d_latch_21_nq), .nQ(d_latch_40_nq));  // open: Q
  D_latch d_latch_41 (.EN(nor_11_out), .D(OB7), .nQ(d_latch_41_nq));  // open: Q
  D_latch d_latch_42 (.EN(nor_11_out), .D(OB0), .nQ(d_latch_42_nq));  // open: Q
  xnor xnor_1 (xnor_1_out, d_ff_20_qn, d_latch_22_nq);
  xnor xnor_2 (xnor_2_out, d_ff_20_qn, d_latch_23_nq);
  xnor xnor_3 (xnor_3_out, d_ff_20_qn, d_latch_24_nq);
  xnor xnor_4 (xnor_4_out, d_ff_20_qn, d_latch_25_nq);
  Multiplexer #(.enable("false")) multiplexer_1 (
    .in0(OBSEL), .in1(d_latch_42_nq), .out(multiplexer_1_out), .sel(O8_16));
  Multiplexer #(.enable("false")) multiplexer_2 (
    .in0(d_latch_27_nq), .in1(xnor_4_out), .out(multiplexer_2_out), .sel(O8_16));
  Multiplexer #(.enable("false")) multiplexer_3 (.in0(nFVO0), .in1(xnor_1_out), .out(multiplexer_3_out), .sel(PAR_O));
  Multiplexer #(.enable("false")) multiplexer_4 (.in0(nFVO1), .in1(xnor_2_out), .out(multiplexer_4_out), .sel(PAR_O));
  Multiplexer #(.enable("false")) multiplexer_5 (.in0(nFVO2), .in1(xnor_3_out), .out(multiplexer_5_out), .sel(PAR_O));
  Multiplexer #(.enable("false")) multiplexer_6 (
    .in0(d_latch_26_nq), .in1(multiplexer_2_out), .out(multiplexer_6_out), .sel(PAR_O));
  Multiplexer #(.enable("false")) multiplexer_7 (
    .in0(d_latch_28_nq), .in1(d_latch_29_nq), .out(multiplexer_7_out), .sel(PAR_O));
  Multiplexer #(.enable("false")) multiplexer_8 (
    .in0(d_latch_30_nq), .in1(d_latch_31_nq), .out(multiplexer_8_out), .sel(PAR_O));
  Multiplexer #(.enable("false")) multiplexer_9 (
    .in0(d_latch_32_nq), .in1(d_latch_33_nq), .out(multiplexer_9_out), .sel(PAR_O));
  Multiplexer #(.enable("false")) multiplexer_10 (
    .in0(d_latch_34_nq), .in1(d_latch_35_nq), .out(multiplexer_10_out), .sel(PAR_O));
  Multiplexer #(.enable("false")) multiplexer_11 (
    .in0(d_latch_36_nq), .in1(d_latch_37_nq), .out(multiplexer_11_out), .sel(PAR_O));
  Multiplexer #(.enable("false")) multiplexer_12 (
    .in0(d_latch_38_nq), .in1(d_latch_39_nq), .out(multiplexer_12_out), .sel(PAR_O));
  Multiplexer #(.enable("false")) multiplexer_13 (
    .in0(d_latch_40_nq), .in1(d_latch_41_nq), .out(multiplexer_13_out), .sel(PAR_O));
  Multiplexer #(.enable("false")) multiplexer_14 (
    .in0(BGSEL), .in1(multiplexer_1_out), .out(multiplexer_14_out), .sel(PAR_O));
  nor nor_27 (nor_27_out, nH2_prime, BLNK);
  D_latch d_latch_43 (.EN(PCLK[1]), .D(multiplexer_3_out), .nQ(d_latch_43_nq));  // open: Q
  D_latch d_latch_44 (.EN(PCLK[1]), .D(multiplexer_4_out), .nQ(d_latch_44_nq));  // open: Q
  D_latch d_latch_45 (.EN(PCLK[1]), .D(multiplexer_5_out), .nQ(d_latch_45_nq));  // open: Q
  not not_21 (not_21_out, nH1_prime);
  D_latch d_latch_46 (.EN(PCLK[1]), .D(multiplexer_6_out), .nQ(d_latch_46_nq));  // open: Q
  D_latch d_latch_47 (.EN(PCLK[1]), .D(multiplexer_7_out), .nQ(d_latch_47_nq));  // open: Q
  D_latch d_latch_48 (.EN(PCLK[1]), .D(multiplexer_8_out), .nQ(d_latch_48_nq));  // open: Q
  D_latch d_latch_49 (.EN(PCLK[1]), .D(multiplexer_9_out), .nQ(d_latch_49_nq));  // open: Q
  D_latch d_latch_50 (.EN(PCLK[1]), .D(multiplexer_10_out), .nQ(d_latch_50_nq));  // open: Q
  D_latch d_latch_51 (.EN(PCLK[1]), .D(multiplexer_11_out), .nQ(d_latch_51_nq));  // open: Q
  D_latch d_latch_52 (.EN(PCLK[1]), .D(multiplexer_12_out), .nQ(d_latch_52_nq));  // open: Q
  D_latch d_latch_53 (.EN(PCLK[1]), .D(multiplexer_13_out), .nQ(d_latch_53_nq));  // open: Q
  D_latch d_latch_54 (.EN(PCLK[1]), .D(multiplexer_14_out), .nQ(d_latch_54_nq));  // open: Q
  assign controlled_buffer_34_out = nor_27_out ? d_latch_43_nq : 1'bz;  // Controlled_Buffer controlled_buffer_65
  assign controlled_buffer_35_out = nor_27_out ? d_latch_44_nq : 1'bz;  // Controlled_Buffer controlled_buffer_66
  assign controlled_buffer_36_out = nor_27_out ? d_latch_45_nq : 1'bz;  // Controlled_Buffer controlled_buffer_67
  assign controlled_buffer_37_out = nor_27_out ? not_21_out : 1'bz;  // Controlled_Buffer controlled_buffer_68
  assign controlled_buffer_38_out = nor_27_out ? d_latch_46_nq : 1'bz;  // Controlled_Buffer controlled_buffer_69
  assign controlled_buffer_39_out = nor_27_out ? d_latch_47_nq : 1'bz;  // Controlled_Buffer controlled_buffer_70
  assign controlled_buffer_40_out = nor_27_out ? d_latch_48_nq : 1'bz;  // Controlled_Buffer controlled_buffer_71
  assign controlled_buffer_41_out = nor_27_out ? d_latch_49_nq : 1'bz;  // Controlled_Buffer controlled_buffer_72
  assign controlled_buffer_42_out = nor_27_out ? d_latch_50_nq : 1'bz;  // Controlled_Buffer controlled_buffer_73
  assign controlled_buffer_43_out = nor_27_out ? d_latch_51_nq : 1'bz;  // Controlled_Buffer controlled_buffer_74
  assign controlled_buffer_54_out = nor_27_out ? d_latch_52_nq : 1'bz;  // Controlled_Buffer controlled_buffer_75
  assign controlled_buffer_55_out = nor_27_out ? d_latch_53_nq : 1'bz;  // Controlled_Buffer controlled_buffer_76
  assign controlled_buffer_56_out = nor_27_out ? d_latch_54_nq : 1'bz;  // Controlled_Buffer controlled_buffer_77
  Multiplexer #(.enable("false")) multiplexer_15 (
    .in0(d_latch_9_nq), .in1(1'b0), .out(multiplexer_15_out), .sel(nor_27_out));
  D_latch d_latch_55 (.EN(1'b1), .D(controlled_buffer_34_out), .nQ(d_latch_55_nq));  // open: Q
  D_latch d_latch_56 (.EN(1'b1), .D(controlled_buffer_35_out), .nQ(d_latch_56_nq));  // open: Q
  D_latch d_latch_57 (.EN(1'b1), .D(controlled_buffer_36_out), .nQ(d_latch_57_nq));  // open: Q
  D_latch d_latch_58 (.EN(1'b1), .D(controlled_buffer_37_out), .nQ(d_latch_58_nq));  // open: Q
  D_latch d_latch_59 (.EN(1'b1), .D(controlled_buffer_38_out), .nQ(d_latch_59_nq));  // open: Q
  D_latch d_latch_60 (.EN(1'b1), .D(controlled_buffer_39_out), .nQ(d_latch_60_nq));  // open: Q
  D_latch d_latch_61 (.EN(1'b1), .D(controlled_buffer_40_out), .nQ(d_latch_61_nq));  // open: Q
  D_latch d_latch_62 (.EN(1'b1), .D(controlled_buffer_41_out), .nQ(d_latch_62_nq));  // open: Q
  D_latch d_latch_63 (.EN(1'b1), .D(controlled_buffer_42_out), .nQ(d_latch_63_nq));  // open: Q
  D_latch d_latch_64 (.EN(1'b1), .D(controlled_buffer_43_out), .nQ(d_latch_64_nq));  // open: Q
  D_latch d_latch_65 (.EN(1'b1), .D(controlled_buffer_54_out), .nQ(d_latch_65_nq));  // open: Q
  D_latch d_latch_66 (.EN(1'b1), .D(controlled_buffer_55_out), .nQ(d_latch_66_nq));  // open: Q
  D_latch d_latch_67 (.EN(1'b1), .D(controlled_buffer_56_out), .nQ(d_latch_67_nq));  // open: Q
  D_latch d_latch_68 (.EN(PCLK[0]), .D(d_latch_55_nq), .Q(nPA0));  // open: nQ
  D_latch d_latch_69 (.EN(PCLK[0]), .D(d_latch_56_nq), .Q(nPA1));  // open: nQ
  D_latch d_latch_70 (.EN(PCLK[0]), .D(d_latch_57_nq), .Q(nPA2));  // open: nQ
  D_latch d_latch_71 (.EN(PCLK[0]), .D(d_latch_58_nq), .Q(nPA3));  // open: nQ
  D_latch d_latch_72 (.EN(PCLK[0]), .D(d_latch_59_nq), .Q(nPA4));  // open: nQ
  D_latch d_latch_73 (.EN(PCLK[0]), .D(d_latch_60_nq), .Q(nPA5));  // open: nQ
  D_latch d_latch_74 (.EN(PCLK[0]), .D(d_latch_61_nq), .Q(nPA6));  // open: nQ
  D_latch d_latch_75 (.EN(PCLK[0]), .D(d_latch_62_nq), .Q(nPA7));  // open: nQ
  D_latch d_latch_76 (.EN(PCLK[0]), .D(d_latch_63_nq), .Q(nPA8));  // open: nQ
  D_latch d_latch_77 (.EN(PCLK[0]), .D(d_latch_64_nq), .Q(nPA9));  // open: nQ
  D_latch d_latch_78 (.EN(PCLK[0]), .D(d_latch_65_nq), .Q(nPA10));  // open: nQ
  D_latch d_latch_79 (.EN(PCLK[0]), .D(d_latch_66_nq), .Q(nPA11));  // open: nQ
  D_latch d_latch_80 (.EN(PCLK[0]), .D(d_latch_67_nq), .Q(nPA12));  // open: nQ
  D_latch d_latch_81 (.EN(PCLK[0]), .D(multiplexer_15_out), .Q(nPA13));  // open: nQ

  // Other names for the same wires on the sheet: PCLK_t = PCLK[0]; nPCLK = PCLK[1]

  // Notes on the sheet:
  //   0
  //   /W5/1'
  //   THZB
  //   FVZ
  //   TVZ
  //   /TVZ''
  //   NTH
  //   NTV
  //   TH0
  //   TH1
  //   TH2
  //   TH3
  //   TH4
  //   TV0
  //   TV1
  //   TV2
  //   TV3
  //   TV4
  //   0/TV
  //   FV0
  //   FV1
  //   FV2
  //   THIN
  //   THZB
  //   TVIN
  //   TVZB
  //   NTHIN
  //   NTVIN
  //   FVIN
  //   THZ
  //   TVZ
  //   NTH0
  //   NTV0
  //   THZ
  //   PAL
  //   PAL
  //   PAH
  //   DB/PAR
  //   F/AT
  //   PARR
  //   O
  //   VDIR
  //   SPRITE V. INVERSION
  //   PARR
endmodule

// EXT IO
module EXT_IO (
  input  [1:0] PCLK,
  input  EXT0_OUT,
  input  EXT0,
  input  EXT1_OUT,
  input  EXT1,
  input  EXT2_OUT,
  input  EXT2,
  input  EXT3_OUT,
  input  EXT3,
  input  nSLAVE,
  output EXT0_2,
  output EXT0_IN,
  output EXT1_2,
  output EXT1_IN,
  output EXT2_2,
  output EXT2_IN,
  output EXT3_2,
  output EXT3_IN
);

  wire d_latch_1_nq, d_latch_2_nq, d_latch_3_nq, d_latch_4_nq, not_1_out, not_2_out, not_3_out, not_4_out;

  D_latch d_latch_1 (.EN(PCLK[1]), .D(EXT0_OUT), .nQ(d_latch_1_nq));  // open: Q
  and and_1 (EXT0_IN, not_1_out, EXT0);
  D_latch d_latch_2 (.EN(PCLK[1]), .D(EXT1_OUT), .nQ(d_latch_2_nq));  // open: Q
  and and_2 (EXT1_IN, not_2_out, EXT1);
  D_latch d_latch_3 (.EN(PCLK[1]), .D(EXT2_OUT), .nQ(d_latch_3_nq));  // open: Q
  and and_3 (EXT2_IN, not_3_out, EXT2);
  D_latch d_latch_4 (.EN(PCLK[1]), .D(EXT3_OUT), .nQ(d_latch_4_nq));  // open: Q
  and and_4 (EXT3_IN, not_4_out, EXT3);
  assign EXT0_2 = nSLAVE ? d_latch_1_nq : 1'bz;  // Controlled_Buffer controlled_buffer_1
  not not_1 (not_1_out, nSLAVE);
  assign EXT1_2 = nSLAVE ? d_latch_2_nq : 1'bz;  // Controlled_Buffer controlled_buffer_2
  not not_2 (not_2_out, nSLAVE);
  assign EXT2_2 = nSLAVE ? d_latch_3_nq : 1'bz;  // Controlled_Buffer controlled_buffer_3
  not not_3 (not_3_out, nSLAVE);
  assign EXT3_2 = nSLAVE ? d_latch_4_nq : 1'bz;  // Controlled_Buffer controlled_buffer_4
  not not_4 (not_4_out, nSLAVE);

  // Notes on the sheet:
  //   /PCLK
endmodule
