// Logisim project CounterStage.circ as structural Verilog: 2 circuits, main circuit main
module main (
  input  CLR,
  input  CLK,
  input  ncarry_in,
  input  RES,
  output out,
  output ncarry_out
);

  wire DLatch_q, multiplexer_1_out, multiplexer_2_out, nor_3_out, not_1_out, not_2_out, not_3_out;

  not not_1 (not_1_out, CLK);
  Multiplexer multiplexer_1 (.in0(not_2_out), .in1(out), .out(multiplexer_1_out), .sel(ncarry_in));  // open: en
  not not_2 (not_2_out, multiplexer_2_out);
  Multiplexer multiplexer_2 (.in0(out), .in1(nor_3_out), .out(multiplexer_2_out), .sel(CLK));  // open: en
  not not_3 (not_3_out, ncarry_in);
  nor nor_1 (out, not_2_out, RES);
  nor nor_2 (ncarry_out, not_2_out, not_3_out);
  nor nor_3 (nor_3_out, DLatch_q, CLR);
  DLatch DLatch (.EN(not_1_out), .D(multiplexer_1_out), .Q(DLatch_q));  // open: NOT_Q

  // Notes on the sheet:
  //   clear manually
  //   global RESET
  //   FF
endmodule

module DLatch (
  input  EN,
  input  D,
  output Q,
  output NOT_Q
);

  D_Flip_Flop #(.trigger("high")) d_ff_1 (.clk(EN), .D(D), .Q(Q), .Qn(NOT_Q));  // open: preset, en, reset
endmodule
